// Digital circuit 74xx_xor.dig as structural Verilog
// XOR build with 7400 and 7404
module _74xx_xor (
  input  A,
  input  B,
  output Y
);

  wire _7400_1_pin3, _7400_1_pin6, _7404_1_pin10, _7404_1_pin12;

  _7404 _7404_1 (
    .pin1(1'b0), .pin3(1'b0), .pin5(1'b0), .pin7(1'b0), .pin9(1'b0), .pin10(_7404_1_pin10), .pin11(B),
    .pin12(_7404_1_pin12), .pin13(A), .pin14(1'b1));  // open: pin2, pin4, pin6, pin8
  _7400 _7400_1 (
    .pin1(A), .pin2(_7404_1_pin10), .pin3(_7400_1_pin3), .pin4(B), .pin5(_7404_1_pin12), .pin6(_7400_1_pin6),
    .pin7(1'b0), .pin8(Y), .pin9(_7400_1_pin6), .pin10(_7400_1_pin3), .pin12(1'b0), .pin13(1'b0), .pin14(1'b1));  // open: pin11
endmodule

/* Test case XOR:
A B Y
0 0 0
0 1 1
1 0 1
1 1 0
*/
