// Digital circuit CrazySmallCPU.dig as structural Verilog
module CrazySmallCPU (
  input  C,
  output [7:0] addr,
  output [7:0] instr,
  output [3:0] A,
  output [3:0] B,
  output [7:0] AB
);

  wire A_pin9, Address_Bottom_p14, Address_Bottom_p15, Address_Bottom_p16, Address_Bottom_p18, ALU_p10,
       ALU_p11, ALU_p12, B_pin9, Control_Top_p12, Control_Top_p13, Control_Top_p14, Control_Top_p24,
       Flags_pin6, MUX_pin1, MUX_pin3, MUX_pin4, MUX_pin6, MUX_pin7, MUX_pin9, MUX_pin12, MUX_pin13,
       not_1_out, OR_pin3, OR_pin6, PChi_pin7, PChi_pin9, RAM_p20;

  // _28c64 Address_Bottom: pin names not known; wires that end beside it: 1'b0, addr[7], addr[6], addr[5], addr[4], addr[3], addr[2], addr[1], addr[0], instr[0], instr[1], 1'b1, 1'b1, Address_Bottom_p14, Address_Bottom_p15, Address_Bottom_p16, 1'b0, Address_Bottom_p18, 1'b0, instr[7]
  // _28c64 Control_Top: pin names not known; wires that end beside it: instr[2], 1'b0, 1'b0, addr[7], addr[6], addr[5], addr[4], addr[3], addr[2], addr[1], addr[0], Control_Top_p12, Control_Top_p13, Control_Top_p14, 1'b0, 1'b1, 1'b1, Address_Bottom_p14, Address_Bottom_p15, Address_Bottom_p16, 1'b0, Address_Bottom_p18, 1'b0, Control_Top_p24
  _74161 PChi (
    .pin1(1'b1), .pin2(C), .pin3(instr[4]), .pin4(instr[5]), .pin5(instr[6]), .pin6(instr[7]),
    .pin7(PChi_pin7), .pin8(1'b0), .pin9(PChi_pin9), .pin10(1'b1), .pin11(addr[7]), .pin12(addr[6]),
    .pin13(addr[5]), .pin14(addr[4]), .pin16(1'b1));  // open: pin15
  _74161 PClow (
    .pin1(1'b1), .pin2(C), .pin3(instr[0]), .pin4(instr[1]), .pin5(instr[2]), .pin6(instr[3]), .pin7(1'b1),
    .pin8(1'b0), .pin9(PChi_pin9), .pin10(1'b1), .pin11(addr[3]), .pin12(addr[2]), .pin13(addr[1]),
    .pin14(addr[0]), .pin15(PChi_pin7), .pin16(1'b1));
  // A623308A RAM: pin names not known; wires that end beside it: 1'b0, 1'b0, instr[7], instr[6], instr[5], instr[4], instr[3], instr[2], instr[1], instr[0], 1'b0, 1'b1, Control_Top_p24, 1'b0, 1'b0, 1'b0, 1'b0, 1'b0, 1'b0, RAM_p20
  _74157 MUX (
    .pin1(MUX_pin1), .pin2(instr[0]), .pin3(MUX_pin3), .pin4(MUX_pin4), .pin5(instr[1]), .pin6(MUX_pin6),
    .pin7(MUX_pin7), .pin8(1'b0), .pin9(MUX_pin9), .pin10(RAM_p20), .pin11(instr[3]), .pin12(MUX_pin12),
    .pin13(MUX_pin13), .pin14(instr[2]), .pin15(1'b0), .pin16(1'b1));
  _74161 u_A (
    .pin1(1'b1), .pin2(C), .pin3(MUX_pin4), .pin4(MUX_pin7), .pin5(MUX_pin12), .pin6(MUX_pin9), .pin7(1'b0),
    .pin8(1'b0), .pin9(A_pin9), .pin10(1'b0), .pin11(A[3]), .pin12(A[2]), .pin13(A[1]), .pin14(A[0]),
    .pin16(1'b1));  // open: pin15
  _74161 u_B (
    .pin1(1'b1), .pin2(C), .pin3(MUX_pin4), .pin4(MUX_pin7), .pin5(MUX_pin12), .pin6(MUX_pin9), .pin7(1'b0),
    .pin8(1'b0), .pin9(B_pin9), .pin10(1'b0), .pin11(AB[3]), .pin12(AB[2]), .pin13(AB[1]), .pin14(AB[0]),
    .pin16(1'b1));  // open: pin15
  // _28c64 ALU: pin names not known; wires that end beside it: MUX_pin1, A[3], A[2], A[1], A[0], AB[3], AB[2], AB[1], AB[0], ALU_p10, ALU_p11, ALU_p12, 1'b0, 1'b1, 1'b1, Control_Top_p12, Control_Top_p13, Address_Bottom_p14, Control_Top_p24, Control_Top_p14, 1'b0, RAM_p20
  not not_1 (not_1_out, OR_pin6);
  _74161 Flags (
    .pin1(1'b1), .pin2(C), .pin3(ALU_p10), .pin4(ALU_p11), .pin5(ALU_p12), .pin6(Flags_pin6), .pin7(1'b0),
    .pin8(1'b0), .pin9(Control_Top_p24), .pin10(1'b0), .pin11(Address_Bottom_p16),
    .pin12(Address_Bottom_p18), .pin13(Address_Bottom_p15), .pin14(Address_Bottom_p14), .pin16(1'b1));  // open: pin15
  _7432 OR (
    .pin1(A_pin9), .pin2(B_pin9), .pin3(OR_pin3), .pin4(OR_pin3), .pin5(C), .pin6(OR_pin6), .pin7(1'b0),
    .pin9(1'b0), .pin10(1'b0), .pin12(1'b0), .pin13(1'b0), .pin14(1'b1));  // open: pin8, pin11
  Terminal #(.termWidth(100)) terminal_1 (.D({A, AB[3:0]}), .C(not_1_out), .en(1'b1));

  assign AB[7:4] = A;
  assign B = AB[3:0];

  // Notes on the sheet:
  //   C: Hz: 2147483647
  //   Warren’s Crazy Small CPU
  //   designed by Warren Toomey
  //   See https://github.com/DoctorWkt/CSCv2 
  //   or https://minnie.tuhs.org/Programs/CrazySmallCPU
  //   contents of Address/Bottom (hex, n*v repeats v):
  //   0,1,5,2,6,3,7,1,4,8,4,8,c,3,7,b,2,6,a,1,5,9,0,9,3,3,a,3,b,3,c,0,a,ff,8,4,c,8,7,3, b,7,6,2,a,
  //   6,5,1,9,5,a,2,8,a,0,c,9,2,3,a,b,d,3,0,6,1,0,4,0,5,ff,3,4,3,2,5,2,2,4,0, 5,ff,1,4,1,0,5,0,ff,
  //   b,1,7,3,0,6,8,9,ff,ff,7,1,7,6,0,6,5f,a,b,ff,c,d,ff,42,0,0,0,0, 0,0,0,0,0,0,0,0,0,0,0,0,0,0,
  //   0,0,0,0,0,0,0,0,0,0,0,0,0,0,0,0,0,0,0,0,0,0,0,0,0,0,0, 0,0,0,0,0,0,0,0,0,0,0,0,0,0,0,0,0,0,
  //   0,0,0,0,0,0,0,0,0,0,0,0,0,0,0,0,0,0,0,0,0,0,0, 0,0,0,0,0,0,0,0,0,0,0,0,0,0,0,0,0,0,0,0,0,0,
  //   0,0,0,0,0,0,0,0,0,0,0,0,0,0,0,0,0,0,0, 0,0,0,0,0,0,0,0,0,0,0,0,0,0,0,0,0,1,5,2,6,3,7,1,4,8,
  //   4,8,c,3,7,b,2,6,a,1,5,9,33,9, 3,3,a,3,b,3,c,0,a,ff,8,4,c,8,7,3,b,7,6,2,a,6,5,1,9,5,a,2,8,a,
  //   0,c,9,2,3,a,b,d,3,0, 6,1,0,4,0,5,ff,3,4,3,2,5,2,2,4,0,5,ff,1,4,1,0,5,0,ff,b,1,7,3,0,6,8,9,ff,
  //   ff,7,1,7, 6,0,6,5f,a,b,ff,c,d,ff,42,0,0,0,0,0,0,0,0,0,0,0,0,0,0,0,0,0,0,0,0,0,0,0,0,0,0,0,0,
  //    0,0,0,0,0,0,0,0,0,0,0,0,0,0,0,0,0,0,0,0,0,0,0,0,0,0,0,0,0,0,0,0,0,0,0,0,0,0,0,0,0, 0,0,0,0,
  //   0,0,0,0,0,0,0,0,0,0,0,0,0,0,0,0,0,0,0,0,0,0,0,0,0,0,0,0,0,0,0,0,0,0,0,0,0, 0,0,0,0,0,0,0,0,
  //   0,0,0,0,0,0,0,0,0,0,0,0,0,0,0,0,0,0,0,0,0,0,0,0,0,0,1,5,2,6,3,7,1, 4,8,4,8,c,3,7,b,2,6,a,1,
  //   5,9,0,9,3,3,a,3,b,3,c,0,a,ff,8,4,c,8,7,3,b,7,6,2,a,6,5,1, 9,5,a,2,8,a,0,c,9,2,3,a,b,d,3,0,6,
  //   1,0,4,0,5,ff,3,4,3,2,5,2,2,4,0,5,ff,1,4,1,0,5,0, ff,b,1,7,3,0,6,8,9,ff,ff,7,1,7,6,0,6,5f,a,
  //   b,ff,c,d,ff,42,0,0,0,0,0,0,0,0,0,0,0,0, 0,0,0,0,0,0,0,0,0,0,0,0,0,0,0,0,0,0,0,0,0,0,0,0,0,0,
  //   0,0,0,0,0,0,0,0,0,0,0,0,0,0,0, 0,0,0,0,0,0,0,0,0,0,0,0,0,0,0,0,0,0,0,0,0,0,0,0,0,0,0,0,0,0,
  //   0,0,0,0,0,0,0,0,0,0,0, 0,0,0,0,0,0,0,0,0,0,0,0,0,0,0,0,0,0,0,0,0,0,0,0,0,0,0,0,0,0,0,0,0,0,
  //   0,0,0,0,0,0,0, 0,0,0,0,0,0,0,0,0,1,5,2,6,3,7,1,4,8,4,8,c,3,7,b,2,6,a,1,5,9,33,9,3,3,a,3,b,3,
  //   c,0, a,ff,8,4,c,8,7,3,b,7,6,2,a,6,5,1,9,5,a,2,8,a,0,c,9,2,3,a,b,d,3,0,6,1,0,4,0,5,ff,3, 4,3,
  //   2,5,2,2,4,0,5,ff,1,4,1,0,5,0,ff,b,1,7,3,0,6,8,9,ff,ff,7,1,7,6,0,6,5f,a,b,ff,c, d,ff,42,0,0,
  //   0,0,0,0,0,0,0,0,0,0,0,0,0,0,0,0,0,0,0,0,0,0,0,0,0,0,0,0,0,0,0,0,0,0,0, 0,0,0,0,0,0,0,0,0,0,
  //   0,0,0,0,0,0,0,0,0,0,0,0,0,0,0,0,0,0,0,0,0,0,0,0,0,0,0,0,0,0,0, 0,0,0,0,0,0,0,0,0,0,0,0,0,0,
  //   0,0,0,0,0,0,0,0,0,0,0,0,0,0,0,0,0,0,0,0,0,0,0,0,0,0,0, 0,0,0,0,0,0,0,0,0,0,0,0,0,0,0,0,0,0,
  //   0,0,0,0,0,0,0,1,5,2,6,3,7,1,4,8,4,8,c,3,7,b,2, 6,a,1,5,9,0,9,3,3,a,3,b,3,c,0,a,ff,8,4,c,8,7,
  //   3,b,7,6,2,a,6,5,1,9,5,a,2,8,a,0,c,9, 2,3,a,b,d,3,0,6,1,0,4,0,5,ff,3,4,3,2,5,2,2,4,0,5,ff,1,
  //   4,1,0,5,0,ff,b,1,7,3,0,6,8, 9,ff,ff,7,1,7,6,0,6,0,a,b,ff,c,d,ff,42,0,0,0,0,0,0,0,0,0,0,0,0,
  //   0,0,0,0,0,0,0,0,0, 0,0,0,0,0,0,0,0,0,0,0,0,0,0,0,0,0,0,0,0,0,0,0,0,0,0,0,0,0,0,0,0,0,0,0,0,
  //   0,0,0,0,0, 0,0,0,0,0,0,0,0,0,0,0,0,0,0,0,0,0,0,0,0,0,0,0,0,0,0,0,0,0,0,0,0,0,0,0,0,0,0,0,0,
  //   0, 0,0,0,0,0,0,0,0,0,0,0,0,0,0,0,0,0,0,0,0,0,0,0,0,0,0,0,0,0,0,0,0,0,0,0,0,0,0,0,0,0, 1,5,2,
  //   6,3,7,1,4,8,4,8,c,3,7,b,2,6,a,1,5,9,33,9,3,3,a,3,b,3,c,0,a,ff,8,4,c,8,7,3,b, 7,6,2,a,6,5,1,
  //   9,5,a,2,8,a,0,c,9,2,3,a,b,d,3,0,6,1,0,4,0,5,ff,3,4,3,2,5,2,2,4,0,5, ff,1,4,1,0,5,0,ff,b,1,7,
  //   3,0,6,8,9,ff,ff,7,1,7,6,0,6,0,a,b,ff,c,d,ff,42,0,0,0,0,0, 0,0,0,0,0,0,0,0,0,0,0,0,0,0,0,0,0,
  //   0,0,0,0,0,0,0,0,0,0,0,0,0,0,0,0,0,0,0,0,0,0,0,0, 0,0,0,0,0,0,0,0,0,0,0,0,0,0,0,0,0,0,0,0,0,
  //   0,0,0,0,0,0,0,0,0,0,0,0,0,0,0,0,0,0,0,0, 0,0,0,0,0,0,0,0,0,0,0,0,0,0,0,0,0,0,0,0,0,0,0,0,0,
  //   0,0,0,0,0,0,0,0,0,0,0,0,0,0,0,0, 0,0,0,0,0,0,0,0,0,0,0,0,0,0,0,0,1,5,2,6,3,7,1,4,8,4,8,c,3,
  //   7,b,2,6,a,1,5,9,0,9,3,3, a,3,b,3,c,0,a,ff,8,4,c,8,7,3,b,7,6,2,a,6,5,1,9,5,a,2,8,a,0,c,9,2,3,
  //   a,b,d,3,0,6,1, 0,4,0,5,ff,3,4,3,2,5,2,2,4,0,5,ff,1,4,1,0,5,0,ff,b,1,7,3,0,6,8,9,ff,ff,7,1,7,
  //   6,0, 6,0,a,b,ff,c,d,ff,42,0,0,0,0,0,0,0,0,0,0,0,0,0,0,0,0,0,0,0,0,0,0,0,0,0,0,0,0,0,0, 0,0,
  //   0,0,0,0,0,0,0,0,0,0,0,0,0,0,0,0,0,0,0,0,0,0,0,0,0,0,0,0,0,0,0,0,0,0,0,0,0,0,0, 0,0,0,0,0,0,
  //   0,0,0,0,0,0,0,0,0,0,0,0,0,0,0,0,0,0,0,0,0,0,0,0,0,0,0,0,0,0,0,0,0,0,0, 0,0,0,0,0,0,0,0,0,0,
  //   0,0,0,0,0,0,0,0,0,0,0,0,0,0,0,0,0,0,0,0,0,0,1,5,2,6,3,7,1,4,8, 4,8,c,3,7,b,2,6,a,1,5,9,33,9,
  //   3,3,a,3,b,3,c,0,a,ff,8,4,c,8,7,3,b,7,6,2,a,6,5,1,9,5, a,2,8,a,0,c,9,2,3,a,b,d,3,0,6,1,0,4,0,
  //   5,ff,3,4,3,2,5,2,2,4,0,5,ff,1,4,1,0,5,0,ff, b,1,7,3,0,6,8,9,ff,ff,7,1,7,6,0,6,0,a,b,ff,c,d,
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  //   contents of Control/Top (hex, n*v repeats v):
  //   a8,7a,7a,7a,7a,7a,7a,a8,7a,7a,e8,d8,38,e8,d8,38,e8,d8,38,e8,d8,38,b8,d8,a8,88,d8, 88,d8,88,
  //   d8,88,98,88,e8,7a,e8,7a,e8,7a,e8,7a,e8,7a,e8,7a,e8,7a,e8,7a,b0,a8,7a,7a, a8,7a,7a,7a,7a,a8,
  //   7a,7a,a8,7a,a8,7a,e8,7a,a8,7a,3f,e8,d8,79,e8,d8,79,e8,7a,a8,7a, 3f,e8,d8,78,e8,d8,78,3f,a8,
  //   d8,78,a8,d8,78,e8,d8,88,3f,e8,98,79,e8,98,79,b0,e8,d8, 88,e8,d8,88,b0,0,0,0,0,0,0,0,0,0,0,0,
  //   0,0,0,0,0,0,0,0,0,0,0,0,0,0,0,0,0,0,0,0,0,0, 0,0,0,0,0,0,0,0,0,0,0,0,0,0,0,0,0,0,0,0,0,0,0,
  //   0,0,0,0,0,0,0,0,0,0,0,0,0,0,0,0,0,0, 0,0,0,0,0,0,0,0,0,0,0,0,0,0,0,0,0,0,0,0,0,0,0,0,0,0,0,
  //   0,0,0,0,0,0,0,0,0,0,0,0,0,0, 0,0,0,0,0,0,0,0,0,0,0,0,0,0,0,0,0,0,0,0,0,0,0,0,0,0,0,0,a8,7a,
  //   7a,7a,7a,7a,7a,a8,7a, 7a,e8,d8,38,e8,d8,38,e8,d8,38,e8,d8,38,b0,d8,a8,88,d8,88,d8,88,d8,88,
  //   98,88,e8,7a, e8,7a,e8,7a,e8,7a,e8,7a,e8,7a,e8,7a,e8,7a,b0,a8,7a,7a,a8,7a,7a,7a,7a,a8,7a,7a,
  //   a8, 7a,a8,7a,e8,7a,a8,7a,3f,e8,d8,79,e8,d8,79,e8,7a,a8,7a,3f,e8,d8,78,e8,d8,78,3f,a8, d8,78,
  //   a8,d8,78,e8,d8,88,3f,e8,98,79,e8,98,79,b0,e8,d8,88,e8,d8,88,b0,0,0,0,0,0,0, 0,0,0,0,0,0,0,0,
  //   0,0,0,0,0,0,0,0,0,0,0,0,0,0,0,0,0,0,0,0,0,0,0,0,0,0,0,0,0,0,0,0,0, 0,0,0,0,0,0,0,0,0,0,0,0,
  //   0,0,0,0,0,0,0,0,0,0,0,0,0,0,0,0,0,0,0,0,0,0,0,0,0,0,0,0,0, 0,0,0,0,0,0,0,0,0,0,0,0,0,0,0,0,
  //   0,0,0,0,0,0,0,0,0,0,0,0,0,0,0,0,0,0,0,0,0,0,0,0,0, 0,0,0,0,0,0,0,0,0,0,0,0,0,0,a8,7a,7a,7a,
  //   7a,7a,7a,a8,7a,7a,e8,d8,38,e8,d8,38,e8,d8, 38,e8,d8,38,b8,d8,a8,88,d8,88,d8,88,d8,88,98,88,
  //   e8,7a,e8,7a,e8,7a,e8,7a,e8,7a,e8, 7a,e8,7a,e8,7a,b0,a8,7a,7a,a8,7a,7a,7a,7a,a8,7a,7a,a8,7a,
  //   a8,7a,e8,7a,a8,7a,3f,e8, d8,79,e8,d8,79,e8,7a,a8,7a,3f,e8,d8,78,e8,d8,78,3f,a8,d8,78,a8,d8,
  //   78,e8,d8,88,3f, e8,98,79,e8,98,79,b0,e8,d8,88,e8,d8,88,b0,0,0,0,0,0,0,0,0,0,0,0,0,0,0,0,0,0,
  //   0,0,0, 0,0,0,0,0,0,0,0,0,0,0,0,0,0,0,0,0,0,0,0,0,0,0,0,0,0,0,0,0,0,0,0,0,0,0,0,0,0,0,0,0, 0,
  //   0,0,0,0,0,0,0,0,0,0,0,0,0,0,0,0,0,0,0,0,0,0,0,0,0,0,0,0,0,0,0,0,0,0,0,0,0,0,0,0, 0,0,0,0,0,
  //   0,0,0,0,0,0,0,0,0,0,0,0,0,0,0,0,0,0,0,0,0,0,0,0,0,0,0,0,0,0,0,0,0,0,0,0, a8,7a,7a,7a,7a,7a,
  //   7a,a8,7a,7a,e8,d8,38,e8,d8,38,e8,d8,38,e8,d8,38,b0,d8,a8,88,d8, 88,d8,88,d8,88,98,88,e8,7a,
  //   e8,7a,e8,7a,e8,7a,e8,7a,e8,7a,e8,7a,e8,7a,b0,a8,7a,7a, a8,7a,7a,7a,7a,a8,7a,7a,a8,7a,a8,7a,
  //   e8,7a,a8,7a,3f,e8,d8,79,e8,d8,79,e8,7a,a8,7a, 3f,e8,d8,78,e8,d8,78,3f,a8,d8,78,a8,d8,78,e8,
  //   d8,88,3f,e8,98,79,e8,98,79,b0,e8,d8, 88,e8,d8,88,b0,0,0,0,0,0,0,0,0,0,0,0,0,0,0,0,0,0,0,0,0,
  //   0,0,0,0,0,0,0,0,0,0,0,0,0, 0,0,0,0,0,0,0,0,0,0,0,0,0,0,0,0,0,0,0,0,0,0,0,0,0,0,0,0,0,0,0,0,
  //   0,0,0,0,0,0,0,0,0, 0,0,0,0,0,0,0,0,0,0,0,0,0,0,0,0,0,0,0,0,0,0,0,0,0,0,0,0,0,0,0,0,0,0,0,0,
  //   0,0,0,0,0, 0,0,0,0,0,0,0,0,0,0,0,0,0,0,0,0,0,0,0,0,0,0,0,0,0,0,0,0,a8,7a,7a,7a,7a,7a,7a,a8,
  //   7a, 7a,e8,d8,38,e8,d8,38,e8,d8,38,e8,d8,38,b8,d8,a8,88,d8,88,d8,88,d8,88,98,88,e8,7a, e8,7a,
  //   e8,7a,e8,7a,e8,7a,e8,7a,e8,7a,e8,7a,b0,a8,7a,7a,a8,7a,7a,7a,7a,a8,7a,7a,a8, 7a,a8,7a,e8,7a,
  //   a8,7a,3f,e8,d8,79,e8,d8,79,e8,7a,a8,7a,3f,e8,d8,78,e8,d8,78,3f,a8, d8,78,a8,d8,78,e8,d8,88,
  //   3f,e8,98,79,e8,98,79,b8,e8,d8,88,e8,d8,88,b0,0,0,0,0,0,0, 0,0,0,0,0,0,0,0,0,0,0,0,0,0,0,0,0,
  //   0,0,0,0,0,0,0,0,0,0,0,0,0,0,0,0,0,0,0,0,0,0,0,0, 0,0,0,0,0,0,0,0,0,0,0,0,0,0,0,0,0,0,0,0,0,
  //   0,0,0,0,0,0,0,0,0,0,0,0,0,0,0,0,0,0,0,0, 0,0,0,0,0,0,0,0,0,0,0,0,0,0,0,0,0,0,0,0,0,0,0,0,0,
  //   0,0,0,0,0,0,0,0,0,0,0,0,0,0,0,0, 0,0,0,0,0,0,0,0,0,0,0,0,0,0,a8,7a,7a,7a,7a,7a,7a,a8,7a,7a,
  //   e8,d8,38,e8,d8,38,e8,d8, 38,e8,d8,38,b0,d8,a8,88,d8,88,d8,88,d8,88,98,88,e8,7a,e8,7a,e8,7a,
  //   e8,7a,e8,7a,e8, 7a,e8,7a,e8,7a,b0,a8,7a,7a,a8,7a,7a,7a,7a,a8,7a,7a,a8,7a,a8,7a,e8,7a,a8,7a,
  //   3f,e8, d8,79,e8,d8,79,e8,7a,a8,7a,3f,e8,d8,78,e8,d8,78,3f,a8,d8,78,a8,d8,78,e8,d8,88,3f, e8,
  //   98,79,e8,98,79,b8,e8,d8,88,e8,d8,88,b0,0,0,0,0,0,0,0,0,0,0,0,0,0,0,0,0,0,0,0,0, 0,0,0,0,0,0,
  //   0,0,0,0,0,0,0,0,0,0,0,0,0,0,0,0,0,0,0,0,0,0,0,0,0,0,0,0,0,0,0,0,0,0,0, 0,0,0,0,0,0,0,0,0,0,
  //   0,0,0,0,0,0,0,0,0,0,0,0,0,0,0,0,0,0,0,0,0,0,0,0,0,0,0,0,0,0,0, 0,0,0,0,0,0,0,0,0,0,0,0,0,0,
  //   0,0,0,0,0,0,0,0,0,0,0,0,0,0,0,0,0,0,0,0,0,0,0,0,0,0,0, a8,7a,7a,7a,7a,7a,7a,a8,7a,7a,e8,d8,
  //   38,e8,d8,38,e8,d8,38,e8,d8,38,b8,d8,a8,88,d8, 88,d8,88,d8,88,98,88,e8,7a,e8,7a,e8,7a,e8,7a,
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  //   contents of ALU (hex, n*v repeats v):
  //   4,10,20,30,40,50,60,70,80,90,4,4,4,4,4,4,10,20,30,40,50,60,70,80,90,5,4,4,4,4,4,4, 20,30,40,
  //   50,60,70,80,90,5,11,4,4,4,4,4,4,30,40,50,60,70,80,90,5,11,21,4,4,4,4,4,4, 40,50,60,70,80,90,
  //   5,11,21,31,4,4,4,4,4,4,50,60,70,80,90,5,11,21,31,41,4,4,4,4,4,4, 60,70,80,90,5,11,21,31,41,
  //   51,4,4,4,4,4,4,70,80,90,5,11,21,31,41,51,61,4,4,4,4,4,4, 80,90,5,11,21,31,41,51,61,71,4,4,4,
  //   4,4,4,90,5,11,21,31,41,51,61,71,81,4,4,4,4,4,4, 4,4,4,4,4,4,4,4,4,4,4,4,4,4,4,4,4,4,4,4,4,4,
  //   4,4,4,4,4,4,4,4,4,4,4,4,4,4,4,4,4,4,4, 4,4,4,4,4,4,4,4,4,4,4,4,4,4,4,4,4,4,4,4,4,4,4,4,4,4,
  //   4,4,4,4,4,4,4,4,4,4,4,4,4,4,4, 4,4,4,4,4,4,4,4,4,4,4,4,4,4,4,91,81,71,61,51,41,31,21,11,4,4,
  //   4,4,4,4,10,4,91,81,71, 61,51,41,31,21,4,4,4,4,4,4,20,10,4,91,81,71,61,51,41,31,4,4,4,4,4,4,
  //   30,20,10,4,91, 81,71,61,51,41,4,4,4,4,4,4,40,30,20,10,4,91,81,71,61,51,4,4,4,4,4,4,50,40,30,
  //   20,10, 4,91,81,71,61,4,4,4,4,4,4,60,50,40,30,20,10,4,91,81,71,4,4,4,4,4,4,70,60,50,40,30, 20,
  //   10,4,91,81,4,4,4,4,4,4,80,70,60,50,40,30,20,10,4,91,4,4,4,4,4,4,90,80,70,60,50, 40,30,20,10,
  //   4,4,4,4,4,4,4,4,4,4,4,4,4,4,4,4,4,4,4,4,4,4,4,4,4,4,4,4,4,4,4,4,4,4,4, 4,4,4,4,4,4,4,4,4,4,
  //   4,4,4,4,4,4,4,4,4,4,4,4,4,4,4,4,4,4,4,4,4,4,4,4,4,4,4,4,4,4,4, 4,4,4,4,4,4,4,4,4,4,4,4,4,4,
  //   4,4,4,4,4,4,4,4,4,4,4,4,4,4,4,4,4,4,4,4,4,4,4,4,4,4,4, 4,4,4,10,4,10,4,10,4,10,4,10,4,10,4,
  //   10,4,10,4,4,20,20,4,4,20,20,4,4,20,20,4,4,20, 20,4,10,20,30,4,10,20,30,4,10,20,30,4,10,20,30,
  //   4,4,4,4,40,40,40,40,4,4,4,4,40,40, 40,40,4,10,4,10,40,50,40,50,4,10,4,10,40,50,40,50,4,4,20,
  //   20,40,40,60,60,4,4,20,20, 40,40,60,60,4,10,20,30,40,50,60,70,4,10,20,30,40,50,60,70,4,4,4,4,
  //   4,4,4,4,88,88,88, 88,88,88,88,88,4,10,4,10,4,10,4,10,88,98,88,98,88,98,88,98,4,4,20,20,4,4,
  //   20,20,88, 88,a8,a8,88,88,a8,a8,4,10,20,30,4,10,20,30,88,98,a8,b8,88,98,a8,b8,4,4,4,4,40,40,
  //    40,40,88,88,88,88,c8,c8,c8,c8,4,10,4,10,40,50,40,50,88,98,88,98,c8,d8,c8,d8,4,4,20, 20,40,
  //   40,60,60,88,88,a8,a8,c8,c8,e8,e8,4,10,20,30,40,50,60,70,88,98,a8,b8,c8,d8,e8, f8,4,10,20,30,
  //   40,50,60,70,88,98,a8,b8,c8,d8,e8,f8,10,10,30,30,50,50,70,70,98,98,b8, b8,d8,d8,f8,f8,20,30,
  //   20,30,60,70,60,70,a8,b8,a8,b8,e8,f8,e8,f8,30,30,30,30,70,70, 70,70,b8,b8,b8,b8,f8,f8,f8,f8,
  //   40,50,60,70,40,50,60,70,c8,d8,e8,f8,c8,d8,e8,f8,50, 50,70,70,50,50,70,70,d8,d8,f8,f8,d8,d8,
  //   f8,f8,60,70,60,70,60,70,60,70,e8,f8,e8,f8, e8,f8,e8,f8,70,70,70,70,70,70,70,70,f8,f8,f8,f8,
  //   f8,f8,f8,f8,88,98,a8,b8,c8,d8,e8, f8,88,98,a8,b8,c8,d8,e8,f8,98,98,b8,b8,d8,d8,f8,f8,98,98,
  //   b8,b8,d8,d8,f8,f8,a8,b8, a8,b8,e8,f8,e8,f8,a8,b8,a8,b8,e8,f8,e8,f8,b8,b8,b8,b8,f8,f8,f8,f8,
  //   b8,b8,b8,b8,f8, f8,f8,f8,c8,d8,e8,f8,c8,d8,e8,f8,c8,d8,e8,f8,c8,d8,e8,f8,d8,d8,f8,f8,d8,d8,
  //   f8,f8, d8,d8,f8,f8,d8,d8,f8,f8,e8,f8,e8,f8,e8,f8,e8,f8,e8,f8,e8,f8,e8,f8,e8,f8,f8,f8,f8, f8,
  //   f8,f8,f8,f8,f8,f8,f8,f8,f8,f8,f8,f8,4,10,20,30,40,50,60,70,88,98,a8,b8,c8,d8,e8, f8,10,4,30,
  //   20,50,40,70,60,98,88,b8,a8,d8,c8,f8,e8,20,30,4,10,60,70,40,50,a8,b8,88, 98,e8,f8,c8,d8,30,20,
  //   10,4,70,60,50,40,b8,a8,98,88,f8,e8,d8,c8,40,50,60,70,4,10,20, 30,c8,d8,e8,f8,88,98,a8,b8,50,
  //   40,70,60,10,4,30,20,d8,c8,f8,e8,98,88,b8,a8,60,70,40, 50,20,30,4,10,e8,f8,c8,d8,a8,b8,88,98,
  //   70,60,50,40,30,20,10,4,f8,e8,d8,c8,b8,a8,98, 88,88,98,a8,b8,c8,d8,e8,f8,6,12,22,32,42,52,62,
  //   72,98,88,b8,a8,d8,c8,f8,e8,12,6,32, 22,52,42,72,62,a8,b8,88,98,e8,f8,c8,d8,22,32,6,12,62,72,
  //   42,52,b8,a8,98,88,f8,e8,d8, c8,32,22,12,6,72,62,52,42,c8,d8,e8,f8,88,98,a8,b8,42,52,62,72,6,
  //   12,22,32,d8,c8,f8, e8,98,88,b8,a8,52,42,72,62,12,6,32,22,e8,f8,c8,d8,a8,b8,88,98,62,72,42,52,
  //   22,32,6, 12,f8,e8,d8,c8,b8,a8,98,88,72,62,52,42,32,22,12,6,10,10,10,10,10,10,10,10,10,10,10,
  //    10,10,10,10,10,20,20,20,20,20,20,20,20,20,20,20,20,20,20,20,20,30,30,30,30,30,30, 30,30,30,
  //   30,30,30,30,30,30,30,40,40,40,40,40,40,40,40,40,40,40,40,40,40,40,40,50, 50,50,50,50,50,50,
  //   50,50,50,50,50,50,50,50,50,60,60,60,60,60,60,60,60,60,60,60,60, 60,60,60,60,70,70,70,70,70,
  //   70,70,70,70,70,70,70,70,70,70,70,8a,8a,8a,8a,8a,8a,8a, 8a,88,88,88,88,88,88,88,88,98,98,98,
  //   98,98,98,98,98,98,98,98,98,98,98,98,98,a8,a8, a8,a8,a8,a8,a8,a8,a8,a8,a8,a8,a8,a8,a8,a8,b8,
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endmodule

/* Test case:
# Clocks the CPU until the last Fibunacci
# number is calculated which is "6765"

C AB
repeat(721) C x
C 0x36
C x
C 0x37
C x
C 0x36
C x
C 0x35
*/
