// Digital circuit counter.dig as structural Verilog
// Three digit BCD counter with seven seg displays.
module counter (
  input  C
);

  wire _7447_1_pin9, _7447_1_pin10, _7447_1_pin11, _7447_1_pin12, _7447_1_pin13, _7447_1_pin14,
       _7447_1_pin15, _7447_2_pin5, _7447_2_pin9, _7447_2_pin10, _7447_2_pin11, _7447_2_pin12, _7447_2_pin13,
       _7447_2_pin14, _7447_2_pin15, _7447_3_pin9, _7447_3_pin10, _7447_3_pin11, _7447_3_pin12,
       _7447_3_pin13, _7447_3_pin14, _7447_3_pin15, _74162_1_pin11, _74162_1_pin12, _74162_1_pin13,
       _74162_1_pin14, _74162_1_pin15, _74162_2_pin11, _74162_2_pin12, _74162_2_pin13, _74162_2_pin14,
       _74162_2_pin15, _74162_3_pin11, _74162_3_pin12, _74162_3_pin13, _74162_3_pin14;

  _74162 _74162_1 (
    .pin1(1'b1), .pin2(C), .pin3(1'b1), .pin4(1'b1), .pin5(1'b1), .pin6(1'b1), .pin7(1'b1), .pin8(1'b0),
    .pin9(1'b1), .pin10(1'b1), .pin11(_74162_1_pin11), .pin12(_74162_1_pin12), .pin13(_74162_1_pin13),
    .pin14(_74162_1_pin14), .pin15(_74162_1_pin15), .pin16(1'b1));
  _74162 _74162_2 (
    .pin1(1'b1), .pin2(C), .pin3(1'b1), .pin4(1'b1), .pin5(1'b1), .pin6(1'b1), .pin7(_74162_1_pin15),
    .pin8(1'b0), .pin9(1'b1), .pin10(1'b1), .pin11(_74162_2_pin11), .pin12(_74162_2_pin12),
    .pin13(_74162_2_pin13), .pin14(_74162_2_pin14), .pin15(_74162_2_pin15), .pin16(1'b1));
  _74162 _74162_3 (
    .pin1(1'b1), .pin2(C), .pin3(1'b1), .pin4(1'b1), .pin5(1'b1), .pin6(1'b1), .pin7(_74162_1_pin15),
    .pin8(1'b0), .pin9(1'b1), .pin10(_74162_2_pin15), .pin11(_74162_3_pin11), .pin12(_74162_3_pin12),
    .pin13(_74162_3_pin13), .pin14(_74162_3_pin14), .pin16(1'b1));  // open: pin15
  _7447 _7447_1 (
    .pin1(_74162_1_pin13), .pin2(_74162_1_pin12), .pin3(1'b1), .pin5(1'b1), .pin6(_74162_1_pin11),
    .pin7(_74162_1_pin14), .pin8(1'b0), .pin9(_7447_1_pin9), .pin10(_7447_1_pin10), .pin11(_7447_1_pin11),
    .pin12(_7447_1_pin12), .pin13(_7447_1_pin13), .pin14(_7447_1_pin14), .pin15(_7447_1_pin15), .pin16(1'b1));  // open: pin4
  _7447 _7447_2 (
    .pin1(_74162_2_pin13), .pin2(_74162_2_pin12), .pin3(1'b1), .pin5(_7447_2_pin5), .pin6(_74162_2_pin11),
    .pin7(_74162_2_pin14), .pin8(1'b0), .pin9(_7447_2_pin9), .pin10(_7447_2_pin10), .pin11(_7447_2_pin11),
    .pin12(_7447_2_pin12), .pin13(_7447_2_pin13), .pin14(_7447_2_pin14), .pin15(_7447_2_pin15), .pin16(1'b1));  // open: pin4
  _7447 _7447_3 (
    .pin1(_74162_3_pin13), .pin2(_74162_3_pin12), .pin3(1'b1), .pin4(_7447_2_pin5), .pin5(1'b0),
    .pin6(_74162_3_pin11), .pin7(_74162_3_pin14), .pin8(1'b0), .pin9(_7447_3_pin9), .pin10(_7447_3_pin10),
    .pin11(_7447_3_pin11), .pin12(_7447_3_pin12), .pin13(_7447_3_pin13), .pin14(_7447_3_pin14),
    .pin15(_7447_3_pin15), .pin16(1'b1));
  Seven_Seg seven_seg_1 (
    .a(_7447_3_pin13), .b(_7447_3_pin12), .c(_7447_3_pin11), .d(_7447_3_pin10), .e(_7447_3_pin9),
    .f(_7447_3_pin15), .g(_7447_3_pin14), .dp(1'b0));
  Seven_Seg seven_seg_2 (
    .a(_7447_2_pin13), .b(_7447_2_pin12), .c(_7447_2_pin11), .d(_7447_2_pin10), .e(_7447_2_pin9),
    .f(_7447_2_pin15), .g(_7447_2_pin14), .dp(1'b0));
  Seven_Seg seven_seg_3 (
    .a(_7447_1_pin13), .b(_7447_1_pin12), .c(_7447_1_pin11), .d(_7447_1_pin10), .e(_7447_1_pin9),
    .f(_7447_1_pin15), .g(_7447_1_pin14), .dp(1'b0));

  // Notes on the sheet:
  //   C: Hz: 2
endmodule
