// Digital circuit hexCounter.dig as structural Verilog
// 12-bit hex counter
module hexCounter (
  input  C,
  output Q0,
  output Q1,
  output Q2,
  output Q3,
  output Q4,
  output Q5,
  output Q6,
  output Q7,
  output Q8,
  output Q9,
  output Q10,
  output Q11
);

  wire _74163_1_pin15, _74163_2_pin15;

  _74163 _74163_1 (
    .pin1(1'b1), .pin2(C), .pin3(1'b1), .pin4(1'b1), .pin5(1'b1), .pin6(1'b1), .pin7(1'b1), .pin8(1'b0),
    .pin9(1'b1), .pin10(1'b1), .pin11(Q3), .pin12(Q2), .pin13(Q1), .pin14(Q0), .pin15(_74163_1_pin15),
    .pin16(1'b1));
  _74163 _74163_2 (
    .pin1(1'b1), .pin2(C), .pin3(1'b1), .pin4(1'b1), .pin5(1'b1), .pin6(1'b1), .pin7(_74163_1_pin15),
    .pin8(1'b0), .pin9(1'b1), .pin10(1'b1), .pin11(Q7), .pin12(Q6), .pin13(Q5), .pin14(Q4),
    .pin15(_74163_2_pin15), .pin16(1'b1));
  _74163 _74163_3 (
    .pin1(1'b1), .pin2(C), .pin3(1'b1), .pin4(1'b1), .pin5(1'b1), .pin6(1'b1), .pin7(_74163_1_pin15),
    .pin8(1'b0), .pin9(1'b1), .pin10(_74163_2_pin15), .pin11(Q11), .pin12(Q10), .pin13(Q9), .pin14(Q8),
    .pin16(1'b1));  // open: pin15

  // Notes on the sheet:
  //   C: Hz: 2
endmodule

/* Test case:
C Q11 Q10 Q9 Q8 Q7 Q6 Q5 Q4 Q3 Q2 Q1 Q0
0  0   0  0  0  0  0  0  0  0  0  0  0
repeat(2<<12) C bits(4,(n+1)>>8) bits(4,(n+1)>>4) bits(4,(n+1))
*/
