// Digital circuit 7451.dig as structural Verilog
// 2-Input/3-Input And-Or invert Gate
module _7451 (
  input  _1A,
  input  _1C,
  input  _1D,
  input  _1F,
  input  _1B,
  input  _1E,
  input  _2A,
  input  _2B,
  input  _2C,
  input  _2D,
  output _1Q,
  output _2Q
);

  wire or_1_out, or_2_out, or_3_out, or_4_out;

  or or_1 (or_1_out, _1A, _1B, _1C);
  or or_2 (or_2_out, _1D, _1E, _1F);
  or or_3 (or_3_out, _2A, _2B);
  or or_4 (or_4_out, _2C, _2D);
  nand nand_1 (_1Q, or_1_out, or_2_out);
  nand nand_2 (_2Q, or_3_out, or_4_out);

  // Notes on the sheet:
  //   _1Q: pin 8
  //   _1A: pin 1
  //   _1C: pin 12
  //   _1D: pin 11
  //   _1F: pin 9
  //   _1B: pin 13
  //   _1E: pin 10
  //   _2Q: pin 6
  //   _2A: pin 2
  //   _2B: pin 3
  //   _2C: pin 4
  //   _2D: pin 5
endmodule
