// Digital circuit 7474.dig as structural Verilog
// Dual D flip-flop
module _7474 (
  input  _1nSD,
  input  _1D,
  input  _1CP,
  input  _1nRD,
  input  _2nSD,
  input  _2D,
  input  _2CP,
  input  _2nRD,
  output _1Q,
  output _1nQ,
  output _2Q,
  output _2nQ
);

  wire nand_1_out, nand_2_out, nand_3_out, nand_4_out, nand_5_out, nand_6_out, nand_7_out, nand_8_out;

  nand nand_1 (nand_1_out, _1nSD, nand_4_out, nand_2_out);
  nand nand_2 (nand_2_out, nand_1_out, _1nRD, _1CP);
  nand nand_3 (nand_3_out, nand_2_out, _1CP, nand_4_out);
  nand nand_4 (nand_4_out, nand_3_out, _1nRD, _1D);
  nand nand_5 (nand_5_out, _2nSD, nand_8_out, nand_6_out);
  nand nand_6 (nand_6_out, nand_5_out, _2nRD, _2CP);
  nand nand_7 (nand_7_out, nand_6_out, _2CP, nand_8_out);
  nand nand_8 (nand_8_out, nand_7_out, _2nRD, _2D);
  nand nand_9 (_1Q, _1nSD, nand_2_out, _1nQ);
  nand nand_10 (_1nQ, _1Q, _1nRD, nand_3_out);
  nand nand_11 (_2Q, _2nSD, nand_6_out, _2nQ);
  nand nand_12 (_2nQ, _2Q, _2nRD, nand_7_out);

  // Notes on the sheet:
  //   _1Q: pin 5
  //   _1nQ: pin 6
  //   _1nSD: pin 4
  //   _1D: pin 2
  //   _1CP: pin 3
  //   _1nRD: pin 1
  //   _2Q: pin 9
  //   _2nQ: pin 8
  //   _2nSD: pin 10
  //   _2D: pin 12
  //   _2CP: pin 11
  //   _2nRD: pin 13
endmodule
