// Digital circuit 7476.dig as structural Verilog
// DUAL J-K FLIP-FLOPS WITH PRESET AND CLEAR
module _7476 (
  input  _1J,
  input  _1CLK,
  input  _1K,
  input  _1nC,
  input  _1nS,
  input  _2J,
  input  _2CLK,
  input  _2K,
  input  _2nC,
  input  _2nS,
  output _1Q,
  output _1nQ,
  output _2Q,
  output _2nQ
);

  wire and_1_out, and_2_out, and_3_out, and_4_out, and_5_out, and_6_out, delay_1_out, delay_2_out, not_1_out,
       not_2_out, not_3_out, not_4_out, not_5_out, not_6_out;

  not not_1 (not_1_out, _1nC);
  not not_2 (not_2_out, _1CLK);
  not not_3 (not_3_out, _1nS);
  not not_4 (not_4_out, _2nC);
  not not_5 (not_5_out, _2CLK);
  not not_6 (not_6_out, _2nS);
  and and_1 (and_1_out, delay_1_out, _1CLK);
  Delay delay_1 (.in(not_2_out), .out(delay_1_out));
  and and_2 (and_2_out, delay_2_out, _2CLK);
  Delay delay_2 (.in(not_5_out), .out(delay_2_out));
  and and_3 (and_3_out, _1Q, _1K, and_1_out);
  and and_4 (and_4_out, and_1_out, _1J, _1nQ);
  and and_5 (and_5_out, _2Q, _2K, and_2_out);
  and and_6 (and_6_out, and_2_out, _2J, _2nQ);
  nor nor_1 (_1Q, not_1_out, and_3_out, _1nQ);
  nor nor_2 (_1nQ, _1Q, and_4_out, not_3_out);
  nor nor_3 (_2Q, not_4_out, and_5_out, _2nQ);
  nor nor_4 (_2nQ, _2Q, and_6_out, not_6_out);

  // Notes on the sheet:
  //   _1J: Set, pin 4
  //   _1Q: pin 15
  //   _1nQ: pin 14
  //   _1CLK: Clock, pin 1
  //   _1K: Kill, pin 16
  //   _1nC: not clear, pin 3
  //   _1nS: not set, pin 2
  //   _2J: Set, pin 9
  //   _2Q: pin 11
  //   _2nQ: pin 10
  //   _2CLK: Clock, pin 6
  //   _2K: Kill, pin 12
  //   _2nC: not clear, pin 8
  //   _2nS: not set, pin 7
endmodule
