// Digital circuit 7474.dig as structural Verilog
// dual D-flip-flop
module _7474 (
  input  _1nSD,
  input  _1D,
  input  _1CP,
  input  _1nRD,
  input  _2nSD,
  input  _2D,
  input  _2CP,
  input  _2nRD,
  output _1Q,
  output _1nQ,
  output _2Q,
  output _2nQ
);

  D_FF_AS d_ff_as_1 (.Set(~_1nSD), .D(_1D), .C(_1CP), .Clr(~_1nRD), .Q(_1Q), .nQ(_1nQ));
  D_FF_AS d_ff_as_2 (.Set(~_2nSD), .D(_2D), .C(_2CP), .Clr(~_2nRD), .Q(_2Q), .nQ(_2nQ));

  // Notes on the sheet:
  //   _1Q: pin 5
  //   _1nQ: pin 6
  //   _1nSD: pin 4
  //   _1D: pin 2
  //   _1CP: pin 3
  //   _1nRD: pin 1
  //   _2Q: pin 9
  //   _2nQ: pin 8
  //   _2nSD: pin 10
  //   _2D: pin 12
  //   _2CP: pin 11
  //   _2nRD: pin 13
endmodule
