// Digital circuit 7476.dig as structural Verilog
// dual J-K flip-flops with preset and clear
module _7476 (
  input  _1J,
  input  _1nCLK,
  input  _1K,
  input  _1nC,
  input  _1nS,
  input  _2J,
  input  _2nCLK,
  input  _2K,
  input  _2nC,
  input  _2nS,
  output _1Q,
  output _1nQ,
  output _2Q,
  output _2nQ
);

  wire not_1_out, not_2_out, not_3_out, not_4_out, not_5_out, not_6_out;

  not not_1 (not_1_out, _1nS);
  not not_2 (not_2_out, _1nCLK);
  not not_3 (not_3_out, _1nC);
  not not_4 (not_4_out, _2nS);
  not not_5 (not_5_out, _2nCLK);
  not not_6 (not_6_out, _2nC);
  JK_FF_AS jk_ff_as_1 (.Set(not_1_out), .J(_1J), .C(not_2_out), .K(_1K), .Clr(not_3_out), .Q(_1Q), .nQ(_1nQ));
  JK_FF_AS jk_ff_as_2 (.Set(not_4_out), .J(_2J), .C(not_5_out), .K(_2K), .Clr(not_6_out), .Q(_2Q), .nQ(_2nQ));

  // Notes on the sheet:
  //   _1J: Set, pin 4
  //   _1Q: pin 15
  //   _1nQ: pin 14
  //   _1nCLK: Clock, pin 1
  //   _1K: Kill, pin 16
  //   _1nC: not clear, pin 3
  //   _1nS: not set, pin 2
  //   _2J: Set, pin 9
  //   _2Q: pin 11
  //   _2nQ: pin 10
  //   _2nCLK: Clock, pin 6
  //   _2K: Kill, pin 12
  //   _2nC: not clear, pin 8
  //   _2nS: not set, pin 7
endmodule
