// Digital circuit traficDiode.dig as structural Verilog
// simple red-yellow-green traffic light with wired and
module traficDiode (
  input  clk
);

  wire _7476_1_pin9, _7476_1_pin10, _7476_1_pin11, _7476_1_pin14, diodebackward_1_out;

  _7476 _7476_1 (
    .pin1(clk), .pin2(1'b1), .pin3(1'b1), .pin4(1'b1), .pin5(1'b1), .pin6(clk), .pin7(1'b1), .pin8(1'b1),
    .pin9(_7476_1_pin9), .pin10(_7476_1_pin10), .pin11(_7476_1_pin11), .pin12(_7476_1_pin9), .pin13(1'b0),
    .pin14(_7476_1_pin14), .pin15(_7476_1_pin9), .pin16(1'b1));
  DiodeBackward diodebackward_1 (.in(_7476_1_pin14), .out(diodebackward_1_out));
  DiodeBackward diodebackward_2 (.in(_7476_1_pin11), .out(diodebackward_1_out));
  LED led_1 (.in(_7476_1_pin10));
  PullUp pullup_1 (.out(diodebackward_1_out));
  LED led_2 (.in(_7476_1_pin9));
  LED led_3 (.in(diodebackward_1_out));
endmodule
