// Digital circuit traficDiodeInv.dig as structural Verilog
// simple red-yellow-green traffic light with wired and
module traficDiodeInv (
  input  clk
);

  wire _7476_1_pin9, _7476_1_pin10, _7476_1_pin11, _7476_1_pin14, diodeforward_1_out;

  _7476 _7476_1 (
    .pin1(clk), .pin2(1'b1), .pin3(1'b1), .pin4(1'b1), .pin5(1'b1), .pin6(clk), .pin7(1'b1), .pin8(1'b1),
    .pin9(_7476_1_pin9), .pin10(_7476_1_pin10), .pin11(_7476_1_pin11), .pin12(_7476_1_pin9), .pin13(1'b0),
    .pin14(_7476_1_pin14), .pin15(_7476_1_pin9), .pin16(1'b1));
  DiodeForward diodeforward_1 (.in(_7476_1_pin9), .out(diodeforward_1_out));
  DiodeForward diodeforward_2 (.in(_7476_1_pin10), .out(diodeforward_1_out));
  LightBulb lightbulb_1 (.A(_7476_1_pin11), .B(1'b1));
  LightBulb lightbulb_2 (.A(_7476_1_pin14), .B(1'b1));
  LightBulb lightbulb_3 (.A(diodeforward_1_out), .B(1'b1));
  PullDown pulldown_1 (.out(diodeforward_1_out));
endmodule
