// Digital circuit traficInv.dig as structural Verilog
// simple red-yellow-green traffic light
module traficInv (
  input  clk
);

  wire _7400_1_pin6, _7476_1_pin9, _7476_1_pin11, _7476_1_pin14;

  _7476 _7476_1 (
    .pin1(clk), .pin2(1'b1), .pin3(1'b1), .pin4(1'b1), .pin5(1'b1), .pin6(clk), .pin7(1'b1), .pin8(1'b1),
    .pin9(_7476_1_pin9), .pin11(_7476_1_pin11), .pin12(_7476_1_pin9), .pin13(1'b0), .pin14(_7476_1_pin14),
    .pin15(_7476_1_pin9), .pin16(1'b1));  // open: pin10
  _7400 _7400_1 (
    .pin1(1'b0), .pin2(1'b0), .pin4(_7476_1_pin14), .pin5(_7476_1_pin11), .pin6(_7400_1_pin6), .pin7(1'b0),
    .pin9(1'b0), .pin10(1'b0), .pin12(1'b0), .pin13(1'b0), .pin14(1'b1));  // open: pin3, pin8, pin11
  LightBulb lightbulb_1 (.A(_7476_1_pin11), .B(1'b1));
  LightBulb lightbulb_2 (.A(_7476_1_pin14), .B(1'b1));
  LightBulb lightbulb_3 (.A(_7400_1_pin6), .B(1'b1));
endmodule
