// Digital circuit Adder8bit.dig as structural Verilog
module Adder8bit (
  input  [3:0] in_1,
  input  [3:0] in_2,
  input  clk,
  output [7:0] out_3,
  output out_5
);

  FullAdderCLA fulladdercla_1 ();
  FullAdderCLA fulladdercla_2 ();
  // Pins of 1 and 4 bits meet at in_1
  // Pins of 1 and 4 bits meet at in_2
  // Pins of 1 and 8 bits meet at out_3
endmodule
