// Digital circuit Ampel_3DFF.dig as structural Verilog
module Ampel_3DFF (
  input  Clock
);

  wire and_1_out, and_2_out, and_3_out, G_q, or_1_out, R_nq, R_q, Y_nq, Y_q;

  and and_1 (and_1_out, R_q, Y_nq);
  and and_2 (and_2_out, Y_q, R_nq);
  and and_3 (and_3_out, Y_q, R_q);
  or or_1 (or_1_out, and_1_out, and_2_out);
  D_FF R (.D(or_1_out), .C(Clock), .Q(R_q), .nQ(R_nq));
  D_FF Y (.D(Y_nq), .C(Clock), .Q(Y_q), .nQ(Y_nq));
  D_FF G (.D(and_3_out), .C(Clock), .Q(G_q));  // open: nQ
  LED Rot (.in(R_q));
  LED Gelb (.in(Y_q));
  LED \Grün  (.in(G_q));
endmodule
