// Digital circuit Ampel_3FF_Save.dig as structural Verilog
module Ampel_3FF_Save (
  input  Clock
);

  wire and_1_out, and_2_out, and_3_out, and_4_out, G_nq, G_q, or_1_out, or_2_out, R_nq, R_q, Y_q;

  and and_1 (and_1_out, G_nq, R_q);
  and and_2 (and_2_out, G_q, R_nq);
  or or_1 (or_1_out, G_nq, Y_q);
  and and_3 (and_3_out, Y_q, G_nq);
  or or_2 (or_2_out, and_1_out, and_2_out);
  and and_4 (and_4_out, Y_q, R_q);
  JK_FF R (.J(or_1_out), .C(Clock), .K(and_3_out), .Q(R_q), .nQ(R_nq));
  JK_FF Y (.J(or_2_out), .C(Clock), .K(1'b1), .Q(Y_q));  // open: nQ
  JK_FF G (.J(and_4_out), .C(Clock), .K(1'b1), .Q(G_q), .nQ(G_nq));
  LED Rot (.in(R_q));
  LED Gelb (.in(Y_q));
  LED \Grün  (.in(G_q));
endmodule
