// Digital circuit Ampel_Einfach.dig as structural Verilog
module Ampel_Einfach (
  input  clk
);

  wire and_1_out, jk_ff_1_nq, jk_ff_1_q, jk_ff_2_nq, jk_ff_2_q;

  JK_FF #(.p("Z_1")) jk_ff_1 (.J(jk_ff_2_q), .C(clk), .K(jk_ff_2_q), .Q(jk_ff_1_q), .nQ(jk_ff_1_nq));
  JK_FF #(.p("Z_0")) jk_ff_2 (.J(1'b1), .C(clk), .K(1'b1), .Q(jk_ff_2_q), .nQ(jk_ff_2_nq));
  and and_1 (and_1_out, jk_ff_1_q, jk_ff_2_nq);
  LED #(.p("Rot")) led_1 (.in(jk_ff_1_nq));
  LED #(.p("Gelb")) led_2 (.in(jk_ff_2_q));
  LED #(.p("Grün")) led_3 (.in(and_1_out));
endmodule
