// Digital circuit Ampel_Feuer.dig as structural Verilog
module Ampel_Feuer (
  input  clk,
  input  in_2
);

  wire and_1_out, and_2_out, and_3_out, jk_ff_1_nq, jk_ff_1_q, jk_ff_2_nq, jk_ff_2_q, not_1_out, or_1_out,
       or_2_out;

  not not_1 (not_1_out, in_2);
  and and_1 (and_1_out, not_1_out, jk_ff_2_q);
  or or_1 (or_1_out, jk_ff_2_q, in_2);
  JK_FF jk_ff_1 (.J(and_1_out), .C(clk), .K(or_1_out), .Q(jk_ff_1_q), .nQ(jk_ff_1_nq));
  JK_FF jk_ff_2 (.J(not_1_out), .C(clk), .K(1'b1), .Q(jk_ff_2_q), .nQ(jk_ff_2_nq));
  or or_2 (or_2_out, jk_ff_1_nq, in_2);
  and and_2 (and_2_out, not_1_out, jk_ff_2_q);
  and and_3 (and_3_out, not_1_out, jk_ff_2_nq);
  LED #(.p("Rot")) led_1 (.in(or_2_out));
  LED #(.p("Gelb")) led_2 (.in(and_2_out));
  LED #(.p("Grün")) led_3 (.in(and_3_out));
endmodule
