// Digital circuit Ampel_Feuer2.dig as structural Verilog
module Ampel_Feuer2 (
  input  clk,
  input  in_2
);

  wire and_1_out, jk_ff_1_nq, jk_ff_1_q, jk_ff_2_nq, jk_ff_2_q, not_1_out, or_1_out;

  or or_1 (or_1_out, jk_ff_1_q, not_1_out);
  not not_1 (not_1_out, in_2);
  JK_FF jk_ff_1 (.J(jk_ff_2_q), .C(clk), .K(jk_ff_2_q), .Q(jk_ff_1_q), .nQ(jk_ff_1_nq));
  JK_FF jk_ff_2 (.J(or_1_out), .C(clk), .K(1'b1), .Q(jk_ff_2_q), .nQ(jk_ff_2_nq));
  and and_1 (and_1_out, jk_ff_1_q, jk_ff_2_nq);
  LED #(.p("Rot")) led_1 (.in(jk_ff_1_nq));
  LED #(.p("Gelb")) led_2 (.in(jk_ff_2_q));
  LED #(.p("Grün")) led_3 (.in(and_1_out));
endmodule
