// Digital circuit Ampel_MSJK.dig as structural Verilog
module Ampel_MSJK (
  input  clk,
  input  in_2
);

  wire and_1_out, jk_trigger_1_p1, jk_trigger_1_p4, jk_trigger_1_p5, jk_trigger_2_p5, not_1_out, or_1_out;

  or or_1 (or_1_out, jk_trigger_1_p4, not_1_out);
  not not_1 (not_1_out, in_2);
  // JK_Trigger jk_trigger_1: pin names not known; wires that end beside it: jk_trigger_1_p1, clk, jk_trigger_1_p1, jk_trigger_1_p4, jk_trigger_1_p5
  // JK_Trigger jk_trigger_2: pin names not known; wires that end beside it: or_1_out, clk, 1'b1, jk_trigger_1_p1, jk_trigger_2_p5
  and and_1 (and_1_out, jk_trigger_1_p4, jk_trigger_2_p5);
  LED #(.p("Rot")) led_1 (.in(jk_trigger_1_p5));
  LED #(.p("Gelb")) led_2 (.in(jk_trigger_1_p1));
  LED #(.p("Grün")) led_3 (.in(and_1_out));
endmodule
