// Digital circuit Ampel_TJK.dig as structural Verilog
module Ampel_TJK (
  input  clk,
  input  in_2
);

  wire and_1_out, ms_jk_1_p1, ms_jk_1_p4, ms_jk_1_p5, ms_jk_2_p5, not_1_out, or_1_out;

  or or_1 (or_1_out, ms_jk_1_p4, not_1_out);
  not not_1 (not_1_out, in_2);
  // MS_JK ms_jk_1: pin names not known; wires that end beside it: ms_jk_1_p1, clk, ms_jk_1_p1, ms_jk_1_p4, ms_jk_1_p5
  // MS_JK ms_jk_2: pin names not known; wires that end beside it: or_1_out, clk, 1'b1, ms_jk_1_p1, ms_jk_2_p5
  and and_1 (and_1_out, ms_jk_1_p4, ms_jk_2_p5);
  LED #(.p("Rot")) led_1 (.in(ms_jk_1_p5));
  LED #(.p("Gelb")) led_2 (.in(ms_jk_1_p1));
  LED #(.p("Grün")) led_3 (.in(and_1_out));
endmodule
