// Digital circuit Count_JK.dig as structural Verilog
module Count_JK (
  input  clk,
  output out_1,
  output out_3,
  output out_4,
  output out_5
);

  wire and_1_out, and_2_out;

  JK_FF Q_0 (.J(1'b1), .C(clk), .K(1'b1), .Q(out_1));  // open: nQ
  JK_FF #(.Default(1)) Q_1 (.J(out_1), .C(clk), .K(out_1), .Q(out_3));  // open: nQ
  and and_1 (and_1_out, out_1, out_3);
  JK_FF #(.Default(1)) Q_2 (.J(and_1_out), .C(clk), .K(and_1_out), .Q(out_4));  // open: nQ
  and and_2 (and_2_out, and_1_out, out_4);
  JK_FF #(.Default(1)) Q_3 (.J(and_2_out), .C(clk), .K(and_2_out), .Q(out_5));  // open: nQ
endmodule
