// Digital circuit FullAdderRC.dig as structural Verilog
module FullAdderRC (
  input  in_1,
  input  in_2,
  input  in_3,
  input  in_5,
  input  in_6,
  input  in_8,
  input  in_9,
  input  in_12,
  input  in_13,
  output out_4,
  output out_7,
  output out_10,
  output out_11,
  output out_14
);

  wire and_1_out, and_2_out, and_3_out, and_4_out, and_5_out, and_6_out, and_7_out, and_8_out, or_2_out,
       or_3_out, or_4_out, xor_1_out, xor_2_out, xor_3_out, xor_4_out;

  and and_1 (and_1_out, in_12, in_13);
  xor xor_1 (xor_1_out, in_12, in_13);
  and and_2 (and_2_out, in_8, in_9);
  xor xor_2 (xor_2_out, in_8, in_9);
  and and_3 (and_3_out, in_5, in_6);
  xor xor_3 (xor_3_out, in_5, in_6);
  and and_4 (and_4_out, in_2, in_3);
  xor xor_4 (xor_4_out, in_2, in_3);
  and and_5 (and_5_out, xor_1_out, or_2_out);
  xor xor_5 (out_14, xor_1_out, or_2_out);
  and and_6 (and_6_out, xor_2_out, or_3_out);
  xor xor_6 (out_10, xor_2_out, or_3_out);
  and and_7 (and_7_out, xor_3_out, or_4_out);
  xor xor_7 (out_7, xor_3_out, or_4_out);
  and and_8 (and_8_out, xor_4_out, in_1);
  xor xor_8 (out_4, xor_4_out, in_1);
  or or_1 (out_11, and_1_out, and_5_out);
  or or_2 (or_2_out, and_2_out, and_6_out);
  or or_3 (or_3_out, and_3_out, and_7_out);
  or or_4 (or_4_out, and_4_out, and_8_out);
endmodule
