// Digital circuit FullAdder_RC_CLA.dig as structural Verilog
module FullAdder_RC_CLA (
  input  in_1,
  input  in_2,
  input  in_3,
  input  in_5,
  input  in_6,
  input  in_8,
  input  in_9,
  input  in_12,
  input  in_13,
  input  in_15,
  input  in_16,
  input  in_17,
  input  in_19,
  input  in_20,
  input  in_23,
  input  in_24,
  input  in_25,
  input  in_26,
  output out_4,
  output out_7,
  output out_10,
  output out_11,
  output out_14,
  output out_18,
  output out_21,
  output out_22,
  output out_27,
  output out_28
);

  wire and_1_out, and_2_out, and_3_out, and_4_out, and_5_out, and_6_out, and_7_out, and_8_out, and_9_out,
       and_10_out, and_11_out, and_12_out, and_15_out, and_16_out, and_18_out, and_19_out, and_20_out,
       and_21_out, and_22_out, or_2_out, or_3_out, or_4_out, or_5_out, or_6_out, or_7_out, or_8_out,
       or_9_out, or_10_out, undriven, undriven_2, undriven_3, xor_1_out, xor_2_out, xor_3_out, xor_4_out,
       xor_9_out, xor_10_out, xor_11_out, xor_12_out;

  and and_1 (and_1_out, in_12, in_13);
  xor xor_1 (xor_1_out, in_12, in_13);
  and and_2 (and_2_out, in_8, in_9);
  xor xor_2 (xor_2_out, in_8, in_9);
  and and_3 (and_3_out, in_5, in_6);
  xor xor_3 (xor_3_out, in_5, in_6);
  and and_4 (and_4_out, in_2, in_3);
  xor xor_4 (xor_4_out, in_2, in_3);
  and and_5 (and_5_out, xor_1_out, or_2_out);
  xor xor_5 (out_14, xor_1_out, or_2_out);
  and and_6 (and_6_out, xor_2_out, or_3_out);
  xor xor_6 (out_10, xor_2_out, or_3_out);
  and and_7 (and_7_out, xor_3_out, or_4_out);
  xor xor_7 (out_7, xor_3_out, or_4_out);
  and and_8 (and_8_out, xor_4_out, in_1);
  xor xor_8 (out_4, xor_4_out, in_1);
  or or_1 (out_11, and_1_out, and_5_out);
  or or_2 (or_2_out, and_2_out, and_6_out);
  or or_3 (or_3_out, and_3_out, and_7_out);
  or or_4 (or_4_out, and_4_out, and_8_out);
  or or_5 (or_5_out, in_25, in_26);
  and and_9 (and_9_out, in_25, in_26);
  or or_6 (or_6_out, in_23, in_24);
  and and_10 (and_10_out, in_23, in_24);
  or or_7 (or_7_out, in_19, in_20);
  and and_11 (and_11_out, in_19, in_20);
  or or_8 (or_8_out, in_15, in_16);
  and and_12 (and_12_out, in_15, in_16);
  // And and_13 has open pins: In_1=in_17, In_2=or_7_out, out=open
  // And and_14 has open pins: In_1=and_12_out, In_2=open, out=open
  and and_15 (and_15_out, and_11_out, or_5_out);
  and and_16 (and_16_out, or_5_out, and_10_out);
  xor xor_9 (xor_9_out, or_5_out, and_9_out);
  // And and_17 has open pins: In_1=in_17, In_2=open, out=open
  and and_18 (and_18_out, or_7_out, and_12_out);
  and and_19 (and_19_out, or_6_out, and_11_out);
  xor xor_10 (xor_10_out, or_6_out, and_10_out);
  and and_20 (and_20_out, in_17, or_7_out);
  and and_21 (and_21_out, or_7_out, and_12_out);
  xor xor_11 (xor_11_out, or_7_out, and_11_out);
  and and_22 (and_22_out, or_8_out, in_17);
  xor xor_12 (xor_12_out, or_8_out, and_12_out);
  or or_9 (or_9_out, and_20_out, and_11_out);
  or or_10 (or_10_out, and_22_out, and_12_out);
  // Or or_11 has open pins: In_1=undriven_2, In_2=and_15_out, out=open
  // Or or_12 has open pins: In_1=undriven, In_2=open, out=open
  xor xor_13 (out_27, xor_9_out, undriven_3);
  xor xor_14 (out_22, xor_10_out, or_9_out);
  xor xor_15 (out_21, xor_11_out, or_10_out);
  xor xor_16 (out_18, xor_12_out, in_17);
endmodule
