// Digital circuit JK-Trigger.dig as structural Verilog
module JK_Trigger (
  input  in_1,
  input  in_4,
  input  in_5,
  output out_2,
  output out_3
);

  wire and_1_out, and_2_out, and_3_out, delay_1_out, not_1_out;

  not not_1 (not_1_out, in_4);
  and and_1 (and_1_out, delay_1_out, in_4);
  Delay delay_1 (.in(not_1_out), .out(delay_1_out));
  and and_2 (and_2_out, out_2, and_1_out);
  // Probe on and_1_out
  and and_3 (and_3_out, and_1_out, out_3);
  nor nor_1 (out_2, and_2_out, out_3);
  nor nor_2 (out_3, out_2, and_3_out);
endmodule
