// Digital circuit T_Counter.dig as structural Verilog
module T_Counter (
  input  clk,
  output out_1,
  output out_2,
  output out_3,
  output out_4,
  output out_6,
  output out_7,
  output out_8
);

  wire not_1_out, not_2_out, not_3_out, not_4_out, not_5_out, not_6_out;

  T_FF t_ff_1 (.T(not_1_out), .Q(out_8));  // open: C, nQ
  not not_1 (not_1_out, out_7);
  T_FF t_ff_2 (.T(not_2_out), .Q(out_7));  // open: C, nQ
  not not_2 (not_2_out, out_6);
  T_FF t_ff_3 (.T(not_3_out), .Q(out_6));  // open: C, nQ
  not not_3 (not_3_out, out_4);
  T_FF t_ff_4 (.T(not_4_out), .Q(out_4));  // open: C, nQ
  not not_4 (not_4_out, out_3);
  T_FF t_ff_5 (.T(not_5_out), .Q(out_3));  // open: C, nQ
  not not_5 (not_5_out, out_2);
  T_FF t_ff_6 (.T(not_6_out), .Q(out_2));  // open: C, nQ
  not not_6 (not_6_out, out_1);
  T_FF t_ff_7 (.T(clk), .Q(out_1));  // open: C, nQ

  // Notes on the sheet:
  //   clk: Hz: 10
endmodule
