// Digital circuit oscillator.dig as structural Verilog
module oscillator (
  output Q,
  output nQ
);

  wire and_1_out, and_2_out, and_3_out, and_4_out, and_5_out, delay_1_out, delay_2_out, nor_1_out, nor_2_out,
       not_1_out, not_2_out, reset_1_out;

  Reset reset_1 (.out(reset_1_out));
  and and_1 (and_1_out, reset_1_out, not_1_out);
  not not_1 (not_1_out, delay_2_out);
  Delay delay_1 (.in(and_1_out), .out(delay_1_out));
  Delay delay_2 (.in(delay_1_out), .out(delay_2_out));
  // Probe C on delay_1_out
  and and_2 (and_2_out, nQ, delay_1_out);
  not not_2 (not_2_out, delay_1_out);
  and and_3 (and_3_out, delay_1_out, Q);
  nor nor_1 (nor_1_out, and_2_out, nor_2_out);
  nor nor_2 (nor_2_out, nor_1_out, and_3_out);
  and and_4 (and_4_out, nor_1_out, not_2_out);
  and and_5 (and_5_out, not_2_out, nor_2_out);
  nor nor_3 (Q, and_4_out, nQ);
  nor nor_4 (nQ, Q, and_5_out);
endmodule
