// Digital circuit CAS_RAS.dig as structural Verilog
module CAS_RAS (
  input  A_0,
  input  A_1,
  input  CS,
  input  RAS,
  input  CAS,
  output Q
);

  wire decoder_1_out_0, decoder_1_out_1, decoder_1_out_2, decoder_1_out_3, decoder_2_out_0, decoder_2_out_1,
       decoder_2_out_2, decoder_2_out_3, fgnfet_1_d, fgnfet_13_d, nfet_1_s, pullup_2_out, pullup_3_out;
  wire [1:0] d_ff_1_q, d_ff_2_q;

  D_FF #(.Bits(2)) d_ff_1 (.D({A_1, A_0}), .C(CAS), .Q(d_ff_1_q));  // open: nQ
  D_FF #(.Bits(2)) d_ff_2 (.D({A_1, A_0}), .C(RAS), .Q(d_ff_2_q));  // open: nQ
  Decoder #(.Selector_Bits(2)) decoder_1 (
    .sel(d_ff_1_q), .out_0(decoder_1_out_0), .out_1(decoder_1_out_1), .out_2(decoder_1_out_2),
    .out_3(decoder_1_out_3));
  Decoder #(.Selector_Bits(2)) decoder_2 (
    .sel(d_ff_2_q), .out_0(decoder_2_out_0), .out_1(decoder_2_out_1), .out_2(decoder_2_out_2),
    .out_3(decoder_2_out_3));
  FGNFET fgnfet_1 (.G(decoder_1_out_0), .D(fgnfet_1_d), .S(1'b0));
  FGNFET fgnfet_2 (.G(decoder_1_out_1), .D(fgnfet_1_d), .S(1'b0));
  FGNFET fgnfet_3 (.G(decoder_1_out_2), .D(fgnfet_1_d), .S(1'b0));
  FGNFET fgnfet_4 (.G(decoder_1_out_3), .D(fgnfet_1_d), .S(1'b0));
  PullUp pullup_1 (.out(fgnfet_1_d));
  NFET nfet_1 (.G(decoder_2_out_0), .D(fgnfet_1_d), .S(nfet_1_s));
  PullUp pullup_2 (.out(pullup_2_out));
  FGNFET fgnfet_5 (.G(decoder_1_out_0), .D(pullup_2_out), .S(1'b0));
  FGNFET fgnfet_6 (.G(decoder_1_out_1), .D(pullup_2_out), .S(1'b0));
  FGNFET #(.Blown("true")) fgnfet_7 (.G(decoder_1_out_2), .D(pullup_2_out), .S(1'b0));
  FGNFET fgnfet_8 (.G(decoder_1_out_3), .D(pullup_2_out), .S(1'b0));
  NFET nfet_2 (.G(decoder_2_out_1), .D(pullup_2_out), .S(nfet_1_s));
  PullUp pullup_3 (.out(pullup_3_out));
  FGNFET fgnfet_9 (.G(decoder_1_out_0), .D(pullup_3_out), .S(1'b0));
  FGNFET #(.Blown("true")) fgnfet_10 (.G(decoder_1_out_1), .D(pullup_3_out), .S(1'b0));
  FGNFET fgnfet_11 (.G(decoder_1_out_2), .D(pullup_3_out), .S(1'b0));
  FGNFET fgnfet_12 (.G(decoder_1_out_3), .D(pullup_3_out), .S(1'b0));
  NFET nfet_3 (.G(decoder_2_out_2), .D(pullup_3_out), .S(nfet_1_s));
  FGNFET fgnfet_13 (.G(decoder_1_out_0), .D(fgnfet_13_d), .S(1'b0));
  FGNFET fgnfet_14 (.G(decoder_1_out_1), .D(fgnfet_13_d), .S(1'b0));
  FGNFET fgnfet_15 (.G(decoder_1_out_2), .D(fgnfet_13_d), .S(1'b0));
  FGNFET fgnfet_16 (.G(decoder_1_out_3), .D(fgnfet_13_d), .S(1'b0));
  NFET nfet_4 (.G(decoder_2_out_3), .D(fgnfet_13_d), .S(nfet_1_s));
  PullUp pullup_4 (.out(fgnfet_13_d));
  assign Q = CS ? nfet_1_s : 1'bz;  // Driver driver_1
endmodule
