// Digital circuit and.dig as structural Verilog
module \and  (
  input  A,
  input  B,
  output Y
);

  wire T1_d, T3_s;

  PFET T1 (.G(A), .S(1'b1), .D(T1_d));
  NFET T3 (.G(A), .D(T1_d), .S(T3_s));
  NFET T4 (.G(B), .D(T3_s), .S(1'b0));
  PFET T2 (.G(B), .S(1'b1), .D(T1_d));
  PFET T5 (.G(T1_d), .S(1'b1), .D(Y));
  NFET T6 (.G(T1_d), .D(Y), .S(1'b0));
endmodule

/* Test case simple:
A B Y
0 0 0 
0 1 0 
1 0 0 
1 1 1 
*/

/* Test case trans:
A B Y
0 0 0 
0 1 0 
1 0 0 
1 1 1 

# switching A
0 0 0 
1 0 0 
0 0 0 
1 0 0 
0 1 0 
1 1 1 
0 1 0 
1 1 1 

# switching B
0 0 0 
0 1 0 
0 0 0 
0 1 0 
1 0 0 
1 1 1 
1 0 0 
1 1 1 

# transitions
0 0 0
0 1 0
0 0 0
1 0 0
0 0 0
1 1 1
0 0 0
0 1 0
1 0 0
0 1 0
1 1 1
0 1 0
1 0 0
1 1 1
1 0 0
*/
