// Digital circuit d-ff.dig as structural Verilog
module d_ff (
  input  D,
  input  C,
  output nQ,
  output Q
);

  wire nfet_2_s, nfet_4_s, nfet_5_s, pfet_1_d, pfet_2_d, pullup_1_out, pullup_2_out;

  PFET pfet_1 (.G(C), .S(1'b1), .D(pfet_1_d));
  NFET nfet_1 (.G(C), .D(pfet_1_d), .S(1'b0));
  PFET pfet_2 (.G(pfet_1_d), .S(1'b1), .D(pfet_2_d));
  PFET pfet_3 (.G(D), .S(pfet_2_d), .D(nQ));
  NFET nfet_2 (.G(D), .D(nQ), .S(nfet_2_s));
  NFET nfet_3 (.G(C), .D(nfet_2_s), .S(1'b0));
  PullUp pullup_1 (.out(pullup_1_out));
  PFET pfet_4 (.G(nQ), .S(pullup_1_out), .D(Q));
  NFET nfet_4 (.G(nQ), .D(Q), .S(nfet_4_s));
  PullDown pulldown_1 (.out(nfet_4_s));
  PullUp pullup_2 (.out(pullup_2_out));
  PFET pfet_5 (.G(Q), .S(pullup_2_out), .D(nQ));
  NFET nfet_5 (.G(Q), .D(nQ), .S(nfet_5_s));
  PullDown pulldown_2 (.out(nfet_5_s));
endmodule

/* Test case:
C D Q ~Q
1 0 0 1
0 0 0 1
0 1 0 1
0 0 0 1
1 1 1 0
0 1 1 0
0 0 1 0
1 0 0 1
0 0 0 1
*/
