// Digital circuit d-sram-ff.dig as structural Verilog
// D flip flop based on a SRAM cell.
module d_sram_ff (
  input  D,
  input  C,
  output Q,
  output nQ
);

  wire nfet_2_s, nfet_3_s, nfet_5_s, nfet_7_s, pfet_1_d, pfet_2_s, pullup_2_out;

  PFET pfet_1 (.G(D), .S(1'b1), .D(pfet_1_d));
  NFET nfet_1 (.G(D), .D(pfet_1_d), .S(1'b0));
  PFET pfet_2 (.G(Q), .S(pfet_2_s), .D(nQ));
  NFET nfet_2 (.G(Q), .D(nQ), .S(nfet_2_s));
  NFET nfet_3 (.G(pfet_1_d), .D(Q), .S(nfet_3_s));
  NFET nfet_4 (.G(C), .D(nfet_3_s), .S(1'b0));
  PullUp pullup_1 (.out(pfet_2_s));
  PullDown pulldown_1 (.out(nfet_2_s));
  NFET nfet_5 (.G(D), .D(nQ), .S(nfet_5_s));
  NFET nfet_6 (.G(C), .D(nfet_5_s), .S(1'b0));
  PullUp pullup_2 (.out(pullup_2_out));
  PFET pfet_3 (.G(nQ), .S(pullup_2_out), .D(Q));
  NFET nfet_7 (.G(nQ), .D(Q), .S(nfet_7_s));
  PullDown pulldown_2 (.out(nfet_7_s));
endmodule

/* Test case:
C D Q ~Q
1 0 0 1
0 0 0 1
0 1 0 1
0 0 0 1
1 1 1 0
0 1 1 0
0 0 1 0
1 0 0 1
0 0 0 1
*/
