// Digital circuit d-tg-ff2.dig as structural Verilog
// The two FETs in the transmission gate are not 
// necessary in this simulation because no body diodes 
// are simulated.
// In order to be compatible with the literature, two FETs 
// are also used in the simulation.
// {{de Die beiden FETs im Transmission Gate sind in dieser 
// Simulation nicht notwendig, da keine Body-Dioden simuliert 
// werden. Um mit der Literatur kompatibel zu sein, werden 
// auch hier zwei FETs in der Simulation verwendet.}}
module d_tg_ff2 (
  input  D,
  input  C,
  output nQ,
  output Q
);

  wire nfet_4_s, pfet_1_d, pfet_4_s;

  PFET pfet_1 (.G(C), .S(1'b1), .D(pfet_1_d));
  NFET nfet_1 (.G(C), .D(pfet_1_d), .S(1'b0));
  PFET pfet_2 (.G(pfet_1_d), .S(Q), .D(D));
  NFET nfet_2 (.G(C), .D(D), .S(Q));
  PFET pfet_3 (.G(Q), .S(1'b1), .D(nQ));
  NFET nfet_3 (.G(Q), .D(nQ), .S(1'b0));
  PFET pfet_4 (.G(nQ), .S(pfet_4_s), .D(Q));
  NFET nfet_4 (.G(nQ), .D(Q), .S(nfet_4_s));
  PullUp pullup_1 (.out(pfet_4_s));
  PullDown pulldown_1 (.out(nfet_4_s));

  // Notes on the sheet:
  //   D: Data In {{de Dateneingang}}
  //   C: Clock In {{de Takteingang}}
endmodule

/* Test case:
C D Q ~Q
1 0 0 1
0 0 0 1
0 1 0 1
0 0 0 1
1 1 1 0
0 1 1 0
0 0 1 0
1 0 0 1
0 0 0 1
*/
