// Digital circuit dec.dig as structural Verilog
module dec (
  input  _0,
  input  _1,
  output a,
  output b,
  output c,
  output d
);

  Decoder #(.Selector_Bits(2)) decoder_1 (.sel({_1, _0}), .out_0(a), .out_1(b), .out_2(c), .out_3(d));
endmodule
