// Digital circuit eprom.dig as structural Verilog
module eprom (
  input  A_0,
  input  A_1,
  input  A_2,
  input  A_3,
  input  CS,
  output Q
);

  wire dec_1_p3, dec_1_p4, dec_1_p5, dec_1_p6, dec_2_p3, dec_2_p4, dec_2_p5, dec_2_p6, fgnfet_1_d,
       fgnfet_13_d, nfet_1_s, pullup_2_out, pullup_3_out;

  // dec dec_1: pin names not known; wires that end beside it: A_0, A_1, dec_1_p3, dec_1_p4, dec_1_p5, dec_1_p6
  // dec dec_2: pin names not known; wires that end beside it: A_2, A_3, dec_2_p3, dec_2_p4, dec_2_p5, dec_2_p6
  FGNFET fgnfet_1 (.G(dec_1_p3), .D(fgnfet_1_d), .S(1'b0));
  FGNFET fgnfet_2 (.G(dec_1_p4), .D(fgnfet_1_d), .S(1'b0));
  FGNFET fgnfet_3 (.G(dec_1_p5), .D(fgnfet_1_d), .S(1'b0));
  FGNFET fgnfet_4 (.G(dec_1_p6), .D(fgnfet_1_d), .S(1'b0));
  PullUp pullup_1 (.out(fgnfet_1_d));
  NFET nfet_1 (.G(dec_2_p3), .D(fgnfet_1_d), .S(nfet_1_s));
  PullUp pullup_2 (.out(pullup_2_out));
  FGNFET fgnfet_5 (.G(dec_1_p3), .D(pullup_2_out), .S(1'b0));
  FGNFET fgnfet_6 (.G(dec_1_p4), .D(pullup_2_out), .S(1'b0));
  FGNFET #(.Blown("true")) fgnfet_7 (.G(dec_1_p5), .D(pullup_2_out), .S(1'b0));
  FGNFET fgnfet_8 (.G(dec_1_p6), .D(pullup_2_out), .S(1'b0));
  NFET nfet_2 (.G(dec_2_p4), .D(pullup_2_out), .S(nfet_1_s));
  PullUp pullup_3 (.out(pullup_3_out));
  FGNFET fgnfet_9 (.G(dec_1_p3), .D(pullup_3_out), .S(1'b0));
  FGNFET #(.Blown("true")) fgnfet_10 (.G(dec_1_p4), .D(pullup_3_out), .S(1'b0));
  FGNFET fgnfet_11 (.G(dec_1_p5), .D(pullup_3_out), .S(1'b0));
  FGNFET fgnfet_12 (.G(dec_1_p6), .D(pullup_3_out), .S(1'b0));
  NFET nfet_3 (.G(dec_2_p5), .D(pullup_3_out), .S(nfet_1_s));
  FGNFET fgnfet_13 (.G(dec_1_p3), .D(fgnfet_13_d), .S(1'b0));
  FGNFET fgnfet_14 (.G(dec_1_p4), .D(fgnfet_13_d), .S(1'b0));
  FGNFET fgnfet_15 (.G(dec_1_p5), .D(fgnfet_13_d), .S(1'b0));
  FGNFET fgnfet_16 (.G(dec_1_p6), .D(fgnfet_13_d), .S(1'b0));
  NFET nfet_4 (.G(dec_2_p6), .D(fgnfet_13_d), .S(nfet_1_s));
  PullUp pullup_4 (.out(fgnfet_13_d));
  assign Q = CS ? nfet_1_s : 1'bz;  // Driver driver_1

  // Notes on the sheet:
  //   CS: default 1
endmodule

/* Test case:
A_0 A_1 A_2 A_3 Q
 0   0   0   0  0
 0   0   0   1  0
 0   0   1   0  0
 0   0   1   1  0
 0   1   0   0  0
 0   1   0   1  0
 0   1   1   0  1
 0   1   1   1  0
 1   0   0   0  0
 1   0   0   1  1
 1   0   1   0  0
 1   0   1   1  0
 1   1   0   0  0
 1   1   0   1  0
 1   1   1   0  0
 1   1   1   1  0
*/
