// Digital circuit inverterCmos.dig as structural Verilog
module inverterCmos (
  input  A,
  output Y
);

  PFET T1 (.G(A), .S(1'b1), .D(Y));
  NFET T2 (.G(A), .D(Y), .S(1'b0));
endmodule

/* Test case:
A Y
0 1
1 0
Z Z
*/
