// Digital circuit nand.dig as structural Verilog
module \nand  (
  input  A,
  input  B,
  output Y
);

  wire T3_s;

  PFET T1 (.G(A), .S(1'b1), .D(Y));
  NFET T3 (.G(A), .D(Y), .S(T3_s));
  NFET T4 (.G(B), .D(T3_s), .S(1'b0));
  PFET T2 (.G(B), .S(1'b1), .D(Y));
endmodule

/* Test case simple:
A B Y
0 0 1 
0 1 1 
1 0 1 
1 1 0
*/

/* Test case trans:
A B Y
0 0 1 
0 1 1 
1 0 1 
1 1 0

 
# transitions
0 0 1
0 1 1
0 0 1
1 0 1
0 0 1
1 1 0
0 0 1
0 1 1
1 0 1
0 1 1
1 1 0
0 1 1
1 0 1
1 1 0
1 0 1
*/
