// Digital circuit nand3.dig as structural Verilog
module nand3 (
  input  A,
  input  C,
  input  B,
  output Y
);

  wire T4_s, T5_s;

  PFET T1 (.G(A), .S(1'b1), .D(Y));
  NFET T4 (.G(A), .D(Y), .S(T4_s));
  NFET T5 (.G(B), .D(T4_s), .S(T5_s));
  NFET T6 (.G(C), .D(T5_s), .S(1'b0));
  PFET T2 (.G(B), .S(1'b1), .D(Y));
  PFET T3 (.G(C), .S(1'b1), .D(Y));
endmodule

/* Test case simple:
A B C Y
0 0 0 1 
0 0 1 1 
0 1 0 1 
0 1 1 1
1 0 0 1 
1 0 1 1 
1 1 0 1 
1 1 1 0
*/

/* Test case trans:
A B C Y
0 0 0 1 
0 0 1 1 
0 1 0 1 
0 1 1 1
1 0 0 1 
1 0 1 1 
1 1 0 1 
1 1 1 0


# transitions
0 0 0 1
0 0 1 1
0 0 0 1
0 1 0 1
0 0 0 1
0 1 1 1
0 0 0 1
1 0 0 1
0 0 0 1
1 0 1 1
0 0 0 1
1 1 0 1
0 0 0 1
1 1 1 0
0 0 0 1
0 0 1 1
0 1 0 1
0 0 1 1
0 1 1 1
0 0 1 1
1 0 0 1
0 0 1 1
1 0 1 1
0 0 1 1
1 1 0 1
0 0 1 1
1 1 1 0
0 0 1 1
0 1 0 1
0 1 1 1
0 1 0 1
1 0 0 1
0 1 0 1
1 0 1 1
0 1 0 1
1 1 0 1
0 1 0 1
1 1 1 0
0 1 0 1
0 1 1 1
1 0 0 1
0 1 1 1
1 0 1 1
0 1 1 1
1 1 0 1
0 1 1 1
1 1 1 0
0 1 1 1
1 0 0 1
1 0 1 1
1 0 0 1
1 1 0 1
1 0 0 1
1 1 1 0
1 0 0 1
1 0 1 1
1 1 0 1
1 0 1 1
1 1 1 0
1 0 1 1
1 1 0 1
1 1 1 0
1 1 0 1
*/
