// Digital circuit nor.dig as structural Verilog
module \nor  (
  input  A,
  input  B,
  output Y
);

  wire T1_d;

  PFET T1 (.G(A), .S(1'b1), .D(T1_d));
  PFET T2 (.G(B), .S(T1_d), .D(Y));
  NFET T4 (.G(B), .D(Y), .S(1'b0));
  NFET T3 (.G(A), .D(Y), .S(1'b0));
endmodule

/* Test case simple:
A B Y
0 0 1 
0 1 0 
1 0 0 
1 1 0 
*/

/* Test case trans:
A B Y
0 0 1 
0 1 0 
1 0 0 
1 1 0 


# transitions
0 0 1
0 1 0
0 0 1
1 0 0
0 0 1
1 1 0
0 0 1
0 1 0
1 0 0
0 1 0
1 1 0
0 1 0
1 0 0
1 1 0
1 0 0
*/
