// Digital circuit nor3.dig as structural Verilog
module nor3 (
  input  A,
  input  C,
  input  B,
  output Y
);

  wire T1_d, T2_d;

  PFET T1 (.G(A), .S(1'b1), .D(T1_d));
  PFET T2 (.G(B), .S(T1_d), .D(T2_d));
  PFET T3 (.G(C), .S(T2_d), .D(Y));
  NFET T4 (.G(A), .D(Y), .S(1'b0));
  NFET T5 (.G(B), .D(Y), .S(1'b0));
  NFET T6 (.G(C), .D(Y), .S(1'b0));
endmodule

/* Test case simple:
A B C Y
0 0 0 1 
0 0 1 0 
0 1 0 0 
0 1 1 0
1 0 0 0 
1 0 1 0 
1 1 0 0 
1 1 1 0
*/

/* Test case trans:
A B C Y
0 0 0 1 
0 0 1 0 
0 1 0 0 
0 1 1 0
1 0 0 0 
1 0 1 0 
1 1 0 0 
1 1 1 0



# transitions
0 0 0 1
0 0 1 0
0 0 0 1
0 1 0 0
0 0 0 1
0 1 1 0
0 0 0 1
1 0 0 0
0 0 0 1
1 0 1 0
0 0 0 1
1 1 0 0
0 0 0 1
1 1 1 0
0 0 0 1
0 0 1 0
0 1 0 0
0 0 1 0
0 1 1 0
0 0 1 0
1 0 0 0
0 0 1 0
1 0 1 0
0 0 1 0
1 1 0 0
0 0 1 0
1 1 1 0
0 0 1 0
0 1 0 0
0 1 1 0
0 1 0 0
1 0 0 0
0 1 0 0
1 0 1 0
0 1 0 0
1 1 0 0
0 1 0 0
1 1 1 0
0 1 0 0
0 1 1 0
1 0 0 0
0 1 1 0
1 0 1 0
0 1 1 0
1 1 0 0
0 1 1 0
1 1 1 0
0 1 1 0
1 0 0 0
1 0 1 0
1 0 0 0
1 1 0 0
1 0 0 0
1 1 1 0
1 0 0 0
1 0 1 0
1 1 0 0
1 0 1 0
1 1 1 0
1 0 1 0
1 1 0 0
1 1 1 0
1 1 0 0
*/
