// Digital circuit openDrainBus.dig as structural Verilog
module openDrainBus (
  input  C,
  input  B,
  input  A,
  output Y
);

  NFET T1 (.G(A), .D(Y), .S(1'b0));
  PullUp pullup_1 (.out(Y));
  NFET T2 (.G(B), .D(Y), .S(1'b0));
  NFET T3 (.G(C), .D(Y), .S(1'b0));

  // Notes on the sheet:
  //   $R$ {{de $R$}}
endmodule

/* Test case:
A B C Y
0 0 0 1
0 0 1 0
0 1 0 0
0 1 1 0
1 0 0 0
1 0 1 0
1 1 0 0
1 1 1 0
*/
