// Digital circuit or.dig as structural Verilog
module \or  (
  input  A,
  input  B,
  output Y
);

  wire T1_d, T2_d;

  PFET T1 (.G(A), .S(1'b1), .D(T1_d));
  PFET T2 (.G(B), .S(T1_d), .D(T2_d));
  NFET T4 (.G(B), .D(T2_d), .S(1'b0));
  NFET T3 (.G(A), .D(T2_d), .S(1'b0));
  PFET T5 (.G(T2_d), .S(1'b1), .D(Y));
  NFET T6 (.G(T2_d), .D(Y), .S(1'b0));
endmodule

/* Test case simple:
A B Y
0 0 0 
0 1 1 
1 0 1 
1 1 1 
*/

/* Test case trans:
A B Y
0 0 0 
0 1 1 
1 0 1 
1 1 1 

# transitions
0 0 0
0 1 1
0 0 0
1 0 1
0 0 0
1 1 1
0 0 0
0 1 1
1 0 1
0 1 1
1 1 1
0 1 1
1 0 1
1 1 1
1 0 1
*/
