// Digital circuit rom.dig as structural Verilog
module rom (
  input  A_0,
  input  A_1,
  input  A_2,
  input  A_3,
  input  CS,
  output Q
);

  wire decoder_1_out_0, decoder_1_out_1, decoder_1_out_2, decoder_1_out_3, decoder_2_out_0, decoder_2_out_1,
       decoder_2_out_2, decoder_2_out_3, nfet_1_d, nfet_5_s, nfet_14_d, pullup_2_out, pullup_3_out;

  Decoder #(.Selector_Bits(2)) decoder_1 (
    .sel({A_1, A_0}), .out_0(decoder_1_out_0), .out_1(decoder_1_out_1), .out_2(decoder_1_out_2),
    .out_3(decoder_1_out_3));
  Decoder #(.Selector_Bits(2)) decoder_2 (
    .sel({A_3, A_2}), .out_0(decoder_2_out_0), .out_1(decoder_2_out_1), .out_2(decoder_2_out_2),
    .out_3(decoder_2_out_3));
  NFET nfet_1 (.G(decoder_1_out_0), .D(nfet_1_d), .S(1'b0));
  NFET nfet_2 (.G(decoder_1_out_1), .D(nfet_1_d), .S(1'b0));
  NFET nfet_3 (.G(decoder_1_out_2), .D(nfet_1_d), .S(1'b0));
  NFET nfet_4 (.G(decoder_1_out_3), .D(nfet_1_d), .S(1'b0));
  PullUp pullup_1 (.out(nfet_1_d));
  NFET nfet_5 (.G(decoder_2_out_0), .D(nfet_1_d), .S(nfet_5_s));
  PullUp pullup_2 (.out(pullup_2_out));
  NFET nfet_6 (.G(decoder_1_out_0), .D(pullup_2_out), .S(1'b0));
  NFET nfet_7 (.G(decoder_1_out_1), .D(pullup_2_out), .S(1'b0));
  NFET nfet_8 (.G(decoder_1_out_3), .D(pullup_2_out), .S(1'b0));
  NFET nfet_9 (.G(decoder_2_out_1), .D(pullup_2_out), .S(nfet_5_s));
  PullUp pullup_3 (.out(pullup_3_out));
  NFET nfet_10 (.G(decoder_1_out_0), .D(pullup_3_out), .S(1'b0));
  NFET nfet_11 (.G(decoder_1_out_2), .D(pullup_3_out), .S(1'b0));
  NFET nfet_12 (.G(decoder_1_out_3), .D(pullup_3_out), .S(1'b0));
  NFET nfet_13 (.G(decoder_2_out_2), .D(pullup_3_out), .S(nfet_5_s));
  NFET nfet_14 (.G(decoder_1_out_0), .D(nfet_14_d), .S(1'b0));
  NFET nfet_15 (.G(decoder_1_out_1), .D(nfet_14_d), .S(1'b0));
  NFET nfet_16 (.G(decoder_1_out_2), .D(nfet_14_d), .S(1'b0));
  NFET nfet_17 (.G(decoder_1_out_3), .D(nfet_14_d), .S(1'b0));
  NFET nfet_18 (.G(decoder_2_out_3), .D(nfet_14_d), .S(nfet_5_s));
  PullUp pullup_4 (.out(nfet_14_d));
  assign Q = CS ? nfet_5_s : 1'bz;  // Driver driver_1
endmodule

/* Test case:
A_0 A_1 A_2 A_3 Q
 0   0   0   0  0
 0   0   0   1  0
 0   0   1   0  0
 0   0   1   1  0
 0   1   0   0  0
 0   1   0   1  0
 0   1   1   0  1
 0   1   1   1  0
 1   0   0   0  0
 1   0   0   1  1
 1   0   1   0  0
 1   0   1   1  0
 1   1   0   0  0
 1   1   0   1  0
 1   1   1   0  0
 1   1   1   1  0
*/
