// Digital circuit tristateOut.dig as structural Verilog
module tristateOut (
  input  nout,
  input  en,
  output Y
);

  wire T1_d, T3_d, T6_s;

  PFET T1 (.G(en), .S(1'b1), .D(T1_d));
  NFET T2 (.G(en), .D(T1_d), .S(1'b0));
  PFET T3 (.G(T1_d), .S(1'b1), .D(T3_d));
  PFET T5 (.G(nout), .S(T3_d), .D(Y));
  NFET T6 (.G(nout), .D(Y), .S(T6_s));
  NFET T4 (.G(en), .D(T6_s), .S(1'b0));
endmodule

/* Test case:
~out en Y
 0  0  z
 1  0  z
 0  1  1
 1  1  0

# switching en
 0  0  z
 0  1  1
 0  0  z
 0  1  1
 1  0  z
 1  1  0
 1  0  z
 1  1  0

# switching out
 0  0  z
 1  0  z
 0  0  z
 1  0  z
 0  1  1
 1  1  0
 0  1  1
 1  1  0

# transitions
0 0 Z
1 0 Z
0 0 Z
0 1 1
0 0 Z
1 1 0
0 0 Z
1 0 Z
0 1 1
1 0 Z
1 1 0
1 0 Z
0 1 1
1 1 0
0 1 1
*/
