// Digital circuit Adder8bit.dig as structural Verilog
// An 8-bit adder made up of two 4-bit CLA adders.
// {{de Ein 8-Bit Addierer, welcher aus zwei 4-Bit 
// CLA-Addierern aufgebaut ist.}}
module Adder8bit (
  input  [7:0] A,
  input  [7:0] B,
  input  C_i_1,
  output [7:0] S,
  output C
);

  FullAdderCLA fulladdercla_1 ();
  FullAdderCLA fulladdercla_2 ();

  // Notes on the sheet:
  //   A: First 8-bit word to be added.
  //   {{de Erstes zu addierendes 8-Bit Wort.}}
  //   B: Second 8-bit word to be added.
  //   {{de Zweites zu addierendes 8-Bit Wort.}}
  //   S: The 8 bit sum.
  //   {{de Die 8-Bit der Summe.}}
  //   C: The carry output.
  //   {{de Übertrag der Addition}}
  //   C_i_1: Carry from the previous adder.
  //   {{de Übertrag aus dem vorhergehenden Addierer.}}
endmodule

/* Test case:
# this test case checks all 2^17 possible additions to be correct
# The for statement repeats the following line 65536 times with the
# variable n going from 0 to 65535. The values to be used for A, B, C and S
# are calculated depending on n.
# Test test result contains all calculated test vectors so you can investigate them.

              C_i-1    A       B            C                      S
loop(A,256)
  loop(B,256)
0 (A) (B) ((A+B)>>8) (A+B)
1 (A) (B) ((A+B+1)>>8) (A+B+1)
  end loop
end loop
*/
