// Digital circuit Bus.dig as structural Verilog
// Simple circuit showing address decoding. The lower three bits 
// of the 5-bit number are output as an address to all ROM components. 
// The upper two bits are used to select one of the four ROM components 
// via the address decoder. The selected ROM then places its data word 
// on the data bus. Through the address decoder, the four ROM 
// components behave like a single four times as large ROM component. 
// All outputs of the ROMs are connected to the same data bus. 
// This is possible because only the output of one of the four ROMs 
// is active. The other outputs are in high-impedance state.
// {{de Einfache Schaltung die eine Adressdecodierung zeigt. 
// Die unteren drei Bit der 5 Bit Zahl werden als Adresse an alle 
// ROM-Bausteine ausgegeben. Die oberen zwei Bits werden 
// verwendet um über den Adressdecoder einen der vier 
// ROM-Bausteine auszuwählen, welcher dann sein Datenwort 
// an den Datenbus legt. Durch den Adressdecoder verhalten 
// sich die vier ROM-Bausteine wie ein einziger viermal so großer 
// ROM-Baustein. Alle Ausgänge der ROMs liegen auf einem 
// Datenbus. Dies ist möglich, da immer nur der Ausgang eines 
// der vier ROMs aktiv ist. Die jeweils anderen Ausgänge sind hochohmig.}}
module Bus (
  input  [4:0] Addr,
  output [7:0] Data
);

  wire decoder_1_out_0, decoder_1_out_1, decoder_1_out_2, decoder_1_out_3;

  Decoder #(.Selector_Bits(2)) decoder_1 (
    .sel(Addr[4:3]), .out_0(decoder_1_out_0), .out_1(decoder_1_out_1), .out_2(decoder_1_out_2),
    .out_3(decoder_1_out_3));
  ROM #(.AddrBits(3), .Bits(8), .Addr_Bits(3)) rom_1 (.A(Addr[2:0]), .sel(decoder_1_out_0), .D(Data));
  ROM #(.AddrBits(3), .Bits(8), .Addr_Bits(3)) rom_2 (.A(Addr[2:0]), .sel(decoder_1_out_1), .D(Data));
  ROM #(.AddrBits(3), .Bits(8), .Addr_Bits(3)) rom_3 (.A(Addr[2:0]), .sel(decoder_1_out_2), .D(Data));
  ROM #(.AddrBits(3), .Bits(8), .Addr_Bits(3)) rom_4 (.A(Addr[2:0]), .sel(decoder_1_out_3), .D(Data));

  // Notes on the sheet:
  //   contents of rom_1 (hex, n*v repeats v):
  //   44,69,65,73,20,69,73,74
  //   contents of rom_2 (hex, n*v repeats v):
  //   20,65,69,6e,20,6c,61,6e
  //   contents of rom_3 (hex, n*v repeats v):
  //   67,65,72,20,54,65,73,74
  //   contents of rom_4 (hex, n*v repeats v):
  //   74,65,78,74,2e,20,20,20
endmodule

/* Test case:
Addr   Data
  0    0x44
  1    0x69
  2    0x65
  3    0x73
  4    0x20
  5    0x69
  6    0x73
  7    0x74

  8    0x20
  9    0x65
 10    0x69
 11    0x6E
 12    0x20
 13    0x6C
 14    0x61
 15    0x6E

 16    0x67
 17    0x65
 18    0x72
 19    0x20
 20    0x54
 21    0x65
 22    0x73
 23    0x74

 24    0x74
 25    0x65
 26    0x78
 27    0x74
 28    0x2E
 29    0x20
 30    0x20
 31    0x20
*/
