// Digital circuit Comp7485.dig as structural Verilog
// Comparator which corresponds to the function of a 74x85. 
// The three inputs with the Compare bits are output directly 
// if the P and Q bits are equal.
// {{de Komparator welcher der Funktion eines
// 74x85 entspricht. Die drei Eingänge mit den
// Vergleichsbits werden direkt wieder ausgegeben,
// wenn die jeweiligen P und Q-Bits übereinstimmen.}}
module Comp7485 (
  input  P_0,
  input  P_1,
  input  P_2,
  input  P_3,
  input  P_lt_Q_i,
  input  P_eq_Q_i,
  input  P_gt_Q_i,
  input  Q_0,
  input  Q_1,
  input  Q_2,
  input  Q_3,
  output P_lt_Q,
  output P_eq_Q,
  output P_gt_Q
);

  wire and_1_out, and_2_out, and_3_out, and_4_out, and_5_out, and_6_out, and_7_out, and_8_out, nand_1_out,
       nand_2_out, nand_3_out, nand_4_out, nand_5_out, nand_6_out, nand_7_out, nand_8_out, nand_9_out,
       nand_10_out, nand_11_out, nand_12_out, nand_13_out, nand_14_out, nand_15_out, nand_16_out, nor_1_out,
       nor_2_out, nor_3_out, nor_4_out;

  nand nand_1 (nand_1_out, P_3, Q_3);
  nand nand_2 (nand_2_out, P_2, Q_2);
  nand nand_3 (nand_3_out, P_1, Q_1);
  nand nand_4 (nand_4_out, P_0, Q_0);
  and and_1 (and_1_out, P_3, nand_1_out);
  and and_2 (and_2_out, nand_1_out, Q_3);
  and and_3 (and_3_out, P_2, nand_2_out);
  and and_4 (and_4_out, nand_2_out, Q_2);
  and and_5 (and_5_out, P_1, nand_3_out);
  and and_6 (and_6_out, nand_3_out, Q_1);
  and and_7 (and_7_out, P_0, nand_4_out);
  and and_8 (and_8_out, nand_4_out, Q_0);
  nor nor_1 (nor_1_out, and_1_out, and_2_out);
  nor nor_2 (nor_2_out, and_3_out, and_4_out);
  nor nor_3 (nor_3_out, and_5_out, and_6_out);
  nor nor_4 (nor_4_out, and_7_out, and_8_out);
  nand nand_5 (nand_5_out, Q_3, nand_1_out);
  nand nand_6 (nand_6_out, Q_2, nand_2_out, nor_1_out);
  nand nand_7 (nand_7_out, Q_1, nand_3_out, nor_1_out, nor_2_out);
  nand nand_8 (nand_8_out, Q_0, nand_4_out, nor_1_out, nor_2_out, nor_3_out);
  nand nand_9 (nand_9_out, nor_1_out, nor_2_out, nor_3_out, nor_4_out, P_lt_Q_i);
  nand nand_10 (nand_10_out, nor_1_out, nor_2_out, nor_3_out, nor_4_out, P_eq_Q_i);
  and and_9 (P_eq_Q, nor_1_out, nor_2_out, P_eq_Q_i, nor_3_out, nor_4_out);
  nand nand_11 (nand_11_out, P_eq_Q_i, nor_4_out, nor_3_out, nor_2_out, nor_1_out);
  nand nand_12 (nand_12_out, P_gt_Q_i, nor_4_out, nor_2_out, nor_3_out, nor_1_out);
  nand nand_13 (nand_13_out, nor_3_out, nor_2_out, nor_1_out, nand_4_out, P_0);
  nand nand_14 (nand_14_out, nor_2_out, nor_1_out, nand_3_out, P_1);
  nand nand_15 (nand_15_out, nor_1_out, nand_2_out, P_2);
  nand nand_16 (nand_16_out, nand_1_out, P_3);
  and and_10 (P_gt_Q, nand_5_out, nand_6_out, nand_7_out, nand_8_out, nand_9_out, nand_10_out);
  and and_11 (P_lt_Q, nand_11_out, nand_12_out, nand_13_out, nand_14_out, nand_15_out, nand_16_out);

  // Notes on the sheet:
  //   P_eq_Q_i: default 1
endmodule

/* Test case:
   P<Q_i P=Q_i P>Q_i  P_3 P_2 P_1 P_0   Q_3 Q_2 Q_1 Q_0  P<Q   P=Q   P>Q
loop(P,16)
  loop(Q,16)
    0    1     0      bits(4,P)         bits(4,Q)        (P<Q) (P=Q) (P>Q)
  end loop
end loop

loop (i,16)
    0    1     0      bits(4,i)         bits(4,i)        0    1     0
    1    0     0      bits(4,i)         bits(4,i)        1    0     0
    0    0     1      bits(4,i)         bits(4,i)        0    0     1
end loop
*/
