// Digital circuit Comp7485Parall.dig as structural Verilog
module Comp7485Parall (
  input  A_0,
  input  A_1,
  input  A_2,
  input  A_3,
  input  B_0,
  input  B_1,
  input  B_2,
  input  B_3,
  input  A_4,
  input  A_5,
  input  A_6,
  input  A_7,
  input  B_4,
  input  B_5,
  input  B_6,
  input  B_7,
  input  A_8,
  input  A_9,
  input  A_10,
  input  A_11,
  input  B_8,
  input  B_9,
  input  B_10,
  input  B_11,
  output P_eq_Q,
  output P_lt_Q,
  output P_gt_Q
);

  wire comp7485_1_p_gt_q, comp7485_1_p_lt_q, comp7485_2_p_gt_q, comp7485_2_p_lt_q, comp7485_3_p_eq_q,
       comp7485_3_p_gt_q, comp7485_3_p_lt_q;

  Comp7485 comp7485_1 (
    .P_0(A_8), .P_1(A_9), .P_2(A_10), .P_3(A_11), .P_lt_Q_i(1'b0), .P_eq_Q_i(1'b1), .P_gt_Q_i(1'b0),
    .Q_0(B_8), .Q_1(B_9), .Q_2(B_10), .Q_3(B_11), .P_lt_Q(comp7485_1_p_lt_q), .P_gt_Q(comp7485_1_p_gt_q));  // open: P_eq_Q
  Comp7485 comp7485_2 (
    .P_0(A_4), .P_1(A_5), .P_2(A_6), .P_3(A_7), .P_lt_Q_i(1'b0), .P_eq_Q_i(1'b1), .P_gt_Q_i(1'b0), .Q_0(B_4),
    .Q_1(B_5), .Q_2(B_6), .Q_3(B_7), .P_lt_Q(comp7485_2_p_lt_q), .P_gt_Q(comp7485_2_p_gt_q));  // open: P_eq_Q
  Comp7485 comp7485_3 (
    .P_0(A_0), .P_1(A_1), .P_2(A_2), .P_3(A_3), .P_lt_Q_i(1'b0), .P_eq_Q_i(1'b1), .P_gt_Q_i(1'b0), .Q_0(B_0),
    .Q_1(B_1), .Q_2(B_2), .Q_3(B_3), .P_lt_Q(comp7485_3_p_lt_q), .P_eq_Q(comp7485_3_p_eq_q),
    .P_gt_Q(comp7485_3_p_gt_q));
  Comp7485 comp7485_4 (
    .P_0(comp7485_2_p_gt_q), .P_1(comp7485_1_p_gt_q), .P_2(1'b0), .P_3(1'b0), .P_lt_Q_i(comp7485_3_p_lt_q),
    .P_eq_Q_i(comp7485_3_p_eq_q), .P_gt_Q_i(comp7485_3_p_gt_q), .Q_0(comp7485_2_p_lt_q),
    .Q_1(comp7485_1_p_lt_q), .Q_2(1'b0), .Q_3(1'b0), .P_lt_Q(P_lt_Q), .P_eq_Q(P_eq_Q), .P_gt_Q(P_gt_Q));

  // Notes on the sheet:
  //   P_eq_Q: Is set to one if P=Q is valid.
  //   {{de Das Bit ist Eins, wenn P=Q gilt.}}
  //   P_lt_Q: Is set to one if P<Q is valid.
  //   {{de Das Bit ist Eins, wenn P<Q gilt.}}
  //   P_gt_Q: Is set to one if P>Q is valid.
  //   {{de Das Bit ist Eins, wenn P>Q gilt.}}
endmodule

/* Test case:
A_11 A_10 A_9 A_8 A_7 A_6 A_5 A_4 A_3 A_2 A_1 A_0   B_11 B_10 B_9 B_8 B_7 B_6 B_5 B_4 B_3 B_2 B_1 B_0  P<Q P=Q P>Q

loop(i,7)
  loop(A,1<<6)
    loop(B,1<<6)

bits(12,A<<i) bits(12,B<<i) (A<B) (A=B) (A>B)

    end loop
  end loop
end loop
*/
