// Digital circuit CompEN.dig as structural Verilog
// Vergleicht zwei Bit miteinander. Besitzt einen 
// zusätzlichen Enable Eingang.
module CompEN (
  input  EN,
  input  P,
  input  Q,
  output P_lt_Q,
  output P_eq_Q,
  output P_gt_Q
);

  wire and_1_out, and_2_out, comp_1_p4;

  and and_1 (and_1_out, P, EN);
  and and_2 (and_2_out, EN, Q);
  // Comp comp_1: pin names not known; wires that end beside it: and_1_out, and_2_out, P_lt_Q, comp_1_p4, P_gt_Q
  and and_3 (P_eq_Q, comp_1_p4, EN);

  // Notes on the sheet:
  //   P_lt_Q: Das Bit ist Eins, wenn P<Q gilt.
  //   P_eq_Q: Das Bit ist Eins, wenn P=Q gilt.
  //   P_gt_Q: Das Bit ist Eins, wenn P>Q gilt.
  //   EN: Enable Eingang. Geht dieser Eingang auf Null, sind 
  //   alle drei Ausgangsbit auch Null. Ist dieser Eingang 
  //   auf EIns, hat der Komparator seine normale 
  //   Funktion.
  //   P: Erstes zu vergleichendes Bit.
  //   Q: Zweites zu vergleichendes Bit.
endmodule

/* Test case:
EN P Q P<Q P=Q P>Q
1  0 0  0   1   0
1  0 1  1   0   0
1  1 0  0   0   1
1  1 1  0   1   0
0  0 0  0   0   0
0  0 1  0   0   0
0  1 0  0   0   0
0  1 1  0   0   0
*/
