// Digital circuit CompRC.dig as structural Verilog
// 4-Bit Vergleicher der nach dem ripple-carry Prinzip
// Aufgebaut ist. Jedoch wird hier das Enable-Bit
// vom höher wertigem Bit an das niederwertige Bit
// herabgereicht wird, also in der umgekehrten 
// Richtung wie das Carry-Bit des ripple-carry 
// Addierers.
module CompRC (
  input  P_3,
  input  P_2,
  input  P_1,
  input  P_0,
  input  Q_3,
  input  Q_2,
  input  Q_1,
  input  Q_0,
  output P_lt_Q,
  output P_eq_Q,
  output P_gt_Q
);

  wire compen_1_p_eq_q, compen_1_p_gt_q, compen_1_p_lt_q, compen_2_p_eq_q, compen_2_p_gt_q, compen_2_p_lt_q,
       compen_3_p_eq_q, compen_3_p_gt_q, compen_3_p_lt_q, compen_4_p_gt_q, compen_4_p_lt_q;

  CompEN compen_1 (
    .EN(1'b1), .P(P_3), .Q(Q_3), .P_lt_Q(compen_1_p_lt_q), .P_eq_Q(compen_1_p_eq_q), .P_gt_Q(compen_1_p_gt_q));
  CompEN compen_2 (
    .EN(compen_1_p_eq_q), .P(P_2), .Q(Q_2), .P_lt_Q(compen_2_p_lt_q), .P_eq_Q(compen_2_p_eq_q),
    .P_gt_Q(compen_2_p_gt_q));
  CompEN compen_3 (
    .EN(compen_2_p_eq_q), .P(P_1), .Q(Q_1), .P_lt_Q(compen_3_p_lt_q), .P_eq_Q(compen_3_p_eq_q),
    .P_gt_Q(compen_3_p_gt_q));
  CompEN compen_4 (
    .EN(compen_3_p_eq_q), .P(P_0), .Q(Q_0), .P_lt_Q(compen_4_p_lt_q), .P_eq_Q(P_eq_Q),
    .P_gt_Q(compen_4_p_gt_q));
  or or_1 (P_lt_Q, compen_1_p_lt_q, compen_2_p_lt_q, compen_3_p_lt_q, compen_4_p_lt_q);
  or or_2 (P_gt_Q, compen_1_p_gt_q, compen_2_p_gt_q, compen_3_p_gt_q, compen_4_p_gt_q);

  // Notes on the sheet:
  //   P_lt_Q: Das Bit ist Eins, wenn P<Q gilt.
  //   P_eq_Q: Das Bit ist Eins, wenn P=Q gilt.
  //   P_gt_Q: Das Bit ist Eins, wenn P>Q gilt.
endmodule

/* Test case:
P_3 P_2 P_1 P_0   Q_3 Q_2 Q_1 Q_0  P<Q P=Q P>Q
0   0   0   0     0   0   0   0     0  1  0
0   0   0   0     0   0   0   1     1  0  0
0   0   0   0     0   0   1   0     1  0  0
0   0   0   0     0   0   1   1     1  0  0
0   0   0   0     0   1   0   0     1  0  0
0   0   0   0     0   1   0   1     1  0  0
0   0   0   0     0   1   1   0     1  0  0
0   0   0   0     0   1   1   1     1  0  0
0   0   0   0     1   0   0   0     1  0  0
0   0   0   0     1   0   0   1     1  0  0
0   0   0   0     1   0   1   0     1  0  0
0   0   0   0     1   0   1   1     1  0  0
0   0   0   0     1   1   0   0     1  0  0
0   0   0   0     1   1   0   1     1  0  0
0   0   0   0     1   1   1   0     1  0  0
0   0   0   0     1   1   1   1     1  0  0
0   0   0   1     0   0   0   0     0  0  1
0   0   0   1     0   0   0   1     0  1  0
0   0   0   1     0   0   1   0     1  0  0
0   0   0   1     0   0   1   1     1  0  0
0   0   0   1     0   1   0   0     1  0  0
0   0   0   1     0   1   0   1     1  0  0
0   0   0   1     0   1   1   0     1  0  0
0   0   0   1     0   1   1   1     1  0  0
0   0   0   1     1   0   0   0     1  0  0
0   0   0   1     1   0   0   1     1  0  0
0   0   0   1     1   0   1   0     1  0  0
0   0   0   1     1   0   1   1     1  0  0
0   0   0   1     1   1   0   0     1  0  0
0   0   0   1     1   1   0   1     1  0  0
0   0   0   1     1   1   1   0     1  0  0
0   0   0   1     1   1   1   1     1  0  0
0   0   1   0     0   0   0   0     0  0  1
0   0   1   0     0   0   0   1     0  0  1
0   0   1   0     0   0   1   0     0  1  0
0   0   1   0     0   0   1   1     1  0  0
0   0   1   0     0   1   0   0     1  0  0
0   0   1   0     0   1   0   1     1  0  0
0   0   1   0     0   1   1   0     1  0  0
0   0   1   0     0   1   1   1     1  0  0
0   0   1   0     1   0   0   0     1  0  0
0   0   1   0     1   0   0   1     1  0  0
0   0   1   0     1   0   1   0     1  0  0
0   0   1   0     1   0   1   1     1  0  0
0   0   1   0     1   1   0   0     1  0  0
0   0   1   0     1   1   0   1     1  0  0
0   0   1   0     1   1   1   0     1  0  0
0   0   1   0     1   1   1   1     1  0  0
0   0   1   1     0   0   0   0     0  0  1
0   0   1   1     0   0   0   1     0  0  1
0   0   1   1     0   0   1   0     0  0  1
0   0   1   1     0   0   1   1     0  1  0
0   0   1   1     0   1   0   0     1  0  0
0   0   1   1     0   1   0   1     1  0  0
0   0   1   1     0   1   1   0     1  0  0
0   0   1   1     0   1   1   1     1  0  0
0   0   1   1     1   0   0   0     1  0  0
0   0   1   1     1   0   0   1     1  0  0
0   0   1   1     1   0   1   0     1  0  0
0   0   1   1     1   0   1   1     1  0  0
0   0   1   1     1   1   0   0     1  0  0
0   0   1   1     1   1   0   1     1  0  0
0   0   1   1     1   1   1   0     1  0  0
0   0   1   1     1   1   1   1     1  0  0
0   1   0   0     0   0   0   0     0  0  1
0   1   0   0     0   0   0   1     0  0  1
0   1   0   0     0   0   1   0     0  0  1
0   1   0   0     0   0   1   1     0  0  1
0   1   0   0     0   1   0   0     0  1  0
0   1   0   0     0   1   0   1     1  0  0
0   1   0   0     0   1   1   0     1  0  0
0   1   0   0     0   1   1   1     1  0  0
0   1   0   0     1   0   0   0     1  0  0
0   1   0   0     1   0   0   1     1  0  0
0   1   0   0     1   0   1   0     1  0  0
0   1   0   0     1   0   1   1     1  0  0
0   1   0   0     1   1   0   0     1  0  0
0   1   0   0     1   1   0   1     1  0  0
0   1   0   0     1   1   1   0     1  0  0
0   1   0   0     1   1   1   1     1  0  0
0   1   0   1     0   0   0   0     0  0  1
0   1   0   1     0   0   0   1     0  0  1
0   1   0   1     0   0   1   0     0  0  1
0   1   0   1     0   0   1   1     0  0  1
0   1   0   1     0   1   0   0     0  0  1
0   1   0   1     0   1   0   1     0  1  0
0   1   0   1     0   1   1   0     1  0  0
0   1   0   1     0   1   1   1     1  0  0
0   1   0   1     1   0   0   0     1  0  0
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*/
