// Digital circuit Dadda-inc.dig as structural Verilog
module Dadda_inc (
  input  [7:0] B,
  input  A_n,
  output P_0,
  output P_1,
  output P_2,
  output P_3,
  output P_4,
  output P_5,
  output P_6,
  output P_7
);

  and and_1 (P_0, B[0], A_n);
  and and_2 (P_1, B[1], A_n);
  and and_3 (P_2, B[2], A_n);
  and and_4 (P_3, B[3], A_n);
  and and_5 (P_4, B[4], A_n);
  and and_6 (P_5, B[5], A_n);
  and and_7 (P_6, B[6], A_n);
  and and_8 (P_7, B[7], A_n);
endmodule
