// Digital circuit DaddaMultiplier.dig as structural Verilog
module DaddaMultiplier (
  input  [7:0] A,
  input  [7:0] B,
  output [15:0] Y
);

  wire dadda_inc_1_p2, dadda_inc_1_p3, dadda_inc_1_p4, dadda_inc_1_p5, dadda_inc_1_p6, dadda_inc_1_p8,
       dadda_inc_1_p10, dadda_inc_1_p11, dadda_inc_1_p12, dadda_inc_2_p1, dadda_inc_2_p2, dadda_inc_2_p3,
       dadda_inc_2_p4, dadda_inc_2_p6, dadda_inc_2_p8, dadda_inc_2_p9, dadda_inc_2_p10, dadda_inc_3_p1,
       dadda_inc_3_p2, dadda_inc_3_p3, dadda_inc_3_p4, dadda_inc_3_p6, dadda_inc_3_p8, dadda_inc_3_p9,
       dadda_inc_3_p10, dadda_inc_4_p1, dadda_inc_4_p2, dadda_inc_4_p3, dadda_inc_4_p4, dadda_inc_4_p6,
       dadda_inc_4_p8, dadda_inc_4_p9, dadda_inc_4_p10, dadda_inc_5_p1, dadda_inc_5_p2, dadda_inc_5_p3,
       dadda_inc_5_p4, dadda_inc_5_p6, dadda_inc_5_p8, dadda_inc_5_p9, dadda_inc_5_p10, dadda_inc_6_p1,
       dadda_inc_6_p2, dadda_inc_6_p3, dadda_inc_6_p4, dadda_inc_6_p6, dadda_inc_6_p8, dadda_inc_6_p9,
       dadda_inc_6_p10, dadda_inc_7_p1, dadda_inc_7_p2, dadda_inc_7_p3, dadda_inc_7_p4, dadda_inc_7_p6,
       dadda_inc_7_p9, dadda_inc_7_p10, dadda_inc_8_p1, dadda_inc_8_p2, dadda_inc_8_p3, fulladder_1_p4,
       fulladder_1_p5, fulladder_2_p4, fulladder_2_p5, fulladder_3_p4, fulladder_3_p5, fulladder_4_p4,
       fulladder_4_p5, fulladder_5_p4, fulladder_5_p5, fulladder_6_p4, fulladder_6_p5, fulladder_7_p4,
       fulladder_7_p5, fulladder_8_p4, fulladder_8_p5, fulladder_9_p4, fulladder_9_p5, fulladder_10_p4,
       fulladder_10_p5, fulladder_11_p4, fulladder_11_p5, fulladder_12_p4, fulladder_12_p5, fulladder_13_p4,
       fulladder_13_p5, fulladder_14_p4, fulladder_14_p5, fulladder_15_p4, fulladder_15_p5, fulladder_16_p4,
       fulladder_16_p5, fulladder_17_p4, fulladder_17_p5, fulladder_18_p4, fulladder_18_p5, fulladder_19_p4,
       fulladder_19_p5, fulladder_20_p4, fulladder_20_p5, fulladder_21_p4, fulladder_21_p5, fulladder_22_p4,
       fulladder_22_p5, fulladder_23_p4, fulladder_23_p5, fulladder_24_p4, fulladder_24_p5, halfadder_1_p3,
       halfadder_1_p4, halfadder_2_p3, halfadder_2_p4, halfadder_3_p3, halfadder_3_p4, halfadder_4_p3,
       halfadder_4_p4, halfadder_5_p3, halfadder_5_p4, halfadder_6_p3, halfadder_6_p4;
  wire [13:0] dadda_inc_8_p4, halfadder_7_p3;

  // Dadda_inc dadda_inc_1: pin names not known; wires that end beside it: halfadder_7_p3[13], dadda_inc_1_p2, dadda_inc_1_p3, dadda_inc_1_p4, dadda_inc_1_p5, dadda_inc_1_p6, A[7], dadda_inc_1_p8, B, dadda_inc_1_p10, dadda_inc_1_p11, dadda_inc_1_p12
  // Dadda_inc dadda_inc_2: pin names not known; wires that end beside it: dadda_inc_2_p1, dadda_inc_2_p2, dadda_inc_2_p3, dadda_inc_2_p4, A[6], dadda_inc_2_p6, B, dadda_inc_2_p8, dadda_inc_2_p9, dadda_inc_2_p10
  // Dadda_inc dadda_inc_3: pin names not known; wires that end beside it: dadda_inc_3_p1, dadda_inc_3_p2, dadda_inc_3_p3, dadda_inc_3_p4, A[5], dadda_inc_3_p6, B, dadda_inc_3_p8, dadda_inc_3_p9, dadda_inc_3_p10
  // Dadda_inc dadda_inc_4: pin names not known; wires that end beside it: dadda_inc_4_p1, dadda_inc_4_p2, dadda_inc_4_p3, dadda_inc_4_p4, A[4], dadda_inc_4_p6, B, dadda_inc_4_p8, dadda_inc_4_p9, dadda_inc_4_p10
  // Dadda_inc dadda_inc_5: pin names not known; wires that end beside it: dadda_inc_5_p1, dadda_inc_5_p2, dadda_inc_5_p3, dadda_inc_5_p4, A[3], dadda_inc_5_p6, B, dadda_inc_5_p8, dadda_inc_5_p9, dadda_inc_5_p10
  // Dadda_inc dadda_inc_6: pin names not known; wires that end beside it: dadda_inc_6_p1, dadda_inc_6_p2, dadda_inc_6_p3, dadda_inc_6_p4, A[2], dadda_inc_6_p6, B, dadda_inc_6_p8, dadda_inc_6_p9, dadda_inc_6_p10
  // Dadda_inc dadda_inc_7: pin names not known; wires that end beside it: dadda_inc_7_p1, dadda_inc_7_p2, dadda_inc_7_p3, dadda_inc_7_p4, A[1], dadda_inc_7_p6, B, halfadder_7_p3[0], dadda_inc_7_p9, dadda_inc_7_p10
  // Dadda_inc dadda_inc_8: pin names not known; wires that end beside it: dadda_inc_8_p1, dadda_inc_8_p2, dadda_inc_8_p3, dadda_inc_8_p4[1], A[0], dadda_inc_8_p4[0], B, Y[0]
  // HalfAdder halfadder_1: pin names not known; wires that end beside it: dadda_inc_6_p2, dadda_inc_5_p3, halfadder_1_p3, halfadder_1_p4
  // FullAdder fulladder_1: pin names not known; wires that end beside it: dadda_inc_6_p1, dadda_inc_5_p2, dadda_inc_4_p3, fulladder_1_p4, fulladder_1_p5
  // HalfAdder halfadder_2: pin names not known; wires that end beside it: dadda_inc_2_p6, dadda_inc_1_p10, halfadder_2_p3, halfadder_2_p4
  // FullAdder fulladder_2: pin names not known; wires that end beside it: dadda_inc_5_p10, dadda_inc_5_p1, dadda_inc_4_p2, fulladder_2_p4, fulladder_2_p5
  // HalfAdder halfadder_3: pin names not known; wires that end beside it: dadda_inc_2_p4, dadda_inc_1_p8, halfadder_3_p3, halfadder_3_p4
  // FullAdder fulladder_3: pin names not known; wires that end beside it: dadda_inc_5_p9, dadda_inc_4_p10, dadda_inc_4_p1, fulladder_3_p4, fulladder_3_p5
  // HalfAdder halfadder_4: pin names not known; wires that end beside it: dadda_inc_5_p6, dadda_inc_4_p8, halfadder_4_p3, halfadder_4_p4
  // FullAdder fulladder_4: pin names not known; wires that end beside it: dadda_inc_8_p1, dadda_inc_7_p2, dadda_inc_6_p3, fulladder_4_p4, fulladder_4_p5
  // HalfAdder halfadder_5: pin names not known; wires that end beside it: dadda_inc_4_p6, dadda_inc_3_p8, halfadder_5_p3, halfadder_5_p4
  // FullAdder fulladder_5: pin names not known; wires that end beside it: dadda_inc_7_p10, dadda_inc_7_p1, halfadder_1_p3, fulladder_5_p4, fulladder_5_p5
  // FullAdder fulladder_6: pin names not known; wires that end beside it: dadda_inc_4_p4, dadda_inc_3_p6, dadda_inc_2_p8, fulladder_6_p4, fulladder_6_p5
  // FullAdder fulladder_7: pin names not known; wires that end beside it: halfadder_1_p4, dadda_inc_7_p9, dadda_inc_6_p10, fulladder_7_p4, fulladder_7_p5
  // FullAdder fulladder_8: pin names not known; wires that end beside it: fulladder_1_p4, dadda_inc_3_p4, halfadder_2_p3, fulladder_8_p4, fulladder_8_p5
  // FullAdder fulladder_9: pin names not known; wires that end beside it: fulladder_1_p5, halfadder_2_p4, dadda_inc_6_p9, fulladder_9_p4, fulladder_9_p5
  // FullAdder fulladder_10: pin names not known; wires that end beside it: fulladder_2_p4, dadda_inc_3_p3, halfadder_3_p3, fulladder_10_p4, fulladder_10_p5
  // FullAdder fulladder_11: pin names not known; wires that end beside it: fulladder_2_p5, halfadder_3_p4, fulladder_3_p4, fulladder_11_p4, fulladder_11_p5
  // FullAdder fulladder_12: pin names not known; wires that end beside it: dadda_inc_3_p2, dadda_inc_2_p3, dadda_inc_1_p6, fulladder_12_p4, fulladder_12_p5
  // FullAdder fulladder_13: pin names not known; wires that end beside it: fulladder_3_p5, dadda_inc_4_p9, dadda_inc_3_p10, fulladder_13_p4, fulladder_13_p5
  // FullAdder fulladder_14: pin names not known; wires that end beside it: dadda_inc_3_p1, dadda_inc_2_p2, dadda_inc_1_p5, fulladder_14_p4, fulladder_14_p5
  // FullAdder fulladder_15: pin names not known; wires that end beside it: dadda_inc_3_p9, dadda_inc_2_p10, dadda_inc_2_p1, fulladder_15_p4, fulladder_15_p5
  // HalfAdder halfadder_6: pin names not known; wires that end beside it: dadda_inc_6_p6, dadda_inc_5_p8, halfadder_6_p3, halfadder_6_p4
  // FullAdder fulladder_16: pin names not known; wires that end beside it: dadda_inc_8_p2, dadda_inc_7_p3, dadda_inc_6_p4, fulladder_16_p4, fulladder_16_p5
  // FullAdder fulladder_17: pin names not known; wires that end beside it: halfadder_4_p4, fulladder_4_p4, dadda_inc_5_p4, fulladder_17_p4, fulladder_17_p5
  // FullAdder fulladder_18: pin names not known; wires that end beside it: fulladder_4_p5, halfadder_5_p4, fulladder_5_p4, fulladder_18_p4, fulladder_18_p5
  // FullAdder fulladder_19: pin names not known; wires that end beside it: fulladder_5_p5, fulladder_6_p5, fulladder_7_p4, fulladder_19_p4, fulladder_19_p5
  // FullAdder fulladder_20: pin names not known; wires that end beside it: fulladder_7_p5, fulladder_8_p5, fulladder_9_p4, fulladder_20_p4, fulladder_20_p5
  // FullAdder fulladder_21: pin names not known; wires that end beside it: fulladder_9_p5, fulladder_10_p5, fulladder_11_p4, fulladder_21_p4, fulladder_21_p5
  // FullAdder fulladder_22: pin names not known; wires that end beside it: fulladder_11_p5, fulladder_12_p5, fulladder_13_p4, fulladder_22_p4, fulladder_22_p5
  // FullAdder fulladder_23: pin names not known; wires that end beside it: fulladder_13_p5, fulladder_14_p5, fulladder_15_p4, fulladder_23_p4, fulladder_23_p5
  // FullAdder fulladder_24: pin names not known; wires that end beside it: fulladder_15_p5, dadda_inc_2_p9, dadda_inc_1_p12, fulladder_24_p4, fulladder_24_p5
  // HalfAdder halfadder_7: pin names not known; wires that end beside it: dadda_inc_7_p6, dadda_inc_6_p8, halfadder_7_p3[1], dadda_inc_8_p4[2]
  // FullAdder fulladder_25: pin names not known; wires that end beside it: dadda_inc_8_p3, dadda_inc_7_p4, halfadder_6_p3, halfadder_7_p3[2], dadda_inc_8_p4[3]
  // FullAdder fulladder_26: pin names not known; wires that end beside it: halfadder_6_p4, fulladder_16_p4, halfadder_4_p3, halfadder_7_p3[3], dadda_inc_8_p4[4]
  // FullAdder fulladder_27: pin names not known; wires that end beside it: fulladder_16_p5, fulladder_17_p4, halfadder_5_p3, halfadder_7_p3[4], dadda_inc_8_p4[5]
  // FullAdder fulladder_28: pin names not known; wires that end beside it: fulladder_17_p5, fulladder_18_p4, fulladder_6_p4, halfadder_7_p3[5], dadda_inc_8_p4[6]
  // FullAdder fulladder_29: pin names not known; wires that end beside it: fulladder_18_p5, fulladder_19_p4, fulladder_8_p4, halfadder_7_p3[6], dadda_inc_8_p4[7]
  // FullAdder fulladder_30: pin names not known; wires that end beside it: fulladder_19_p5, fulladder_20_p4, fulladder_10_p4, halfadder_7_p3[7], dadda_inc_8_p4[8]
  // FullAdder fulladder_31: pin names not known; wires that end beside it: fulladder_20_p5, fulladder_21_p4, fulladder_12_p4, halfadder_7_p3[8], dadda_inc_8_p4[9]
  // FullAdder fulladder_32: pin names not known; wires that end beside it: fulladder_21_p5, fulladder_22_p4, fulladder_14_p4, halfadder_7_p3[9], dadda_inc_8_p4[10]
  // FullAdder fulladder_33: pin names not known; wires that end beside it: fulladder_22_p5, fulladder_23_p4, dadda_inc_1_p4, halfadder_7_p3[10], dadda_inc_8_p4[11]
  // FullAdder fulladder_34: pin names not known; wires that end beside it: fulladder_23_p5, fulladder_24_p4, dadda_inc_1_p3, halfadder_7_p3[11], dadda_inc_8_p4[12]
  // FullAdder fulladder_35: pin names not known; wires that end beside it: fulladder_24_p5, dadda_inc_1_p11, dadda_inc_1_p2, halfadder_7_p3[12], dadda_inc_8_p4[13]
  Add #(.Bits(14)) add_1 (.a(dadda_inc_8_p4), .b(halfadder_7_p3), .c_i(1'b0), .s(Y[14:1]), .c_o(Y[15]));
endmodule

/* Test case:
A B Y
loop (A,256)
loop (B,256)
(A) (B) (A*B)
end loop
end loop
*/
