// Digital circuit Demultiplexer.dig as structural Verilog
module Demultiplexer (
  input  A_1,
  input  A_0,
  input  D,
  output Y_0,
  output Y_1,
  output Y_2,
  output Y_3
);

  wire not_1_out, not_2_out;

  not not_1 (not_1_out, A_1);
  not not_2 (not_2_out, A_0);
  and and_1 (Y_0, not_2_out, not_1_out, D);
  and and_2 (Y_1, A_0, not_1_out, D);
  and and_3 (Y_2, not_2_out, A_1, D);
  and and_4 (Y_3, A_0, A_1, D);
endmodule
