// Digital circuit DemuxCas.dig as structural Verilog
// A 16-bit demultiplexer made up of five 4-bit demultiplexers.
// {{de Ein 16-Bit Demultiplexer der aus fünf 4-Bit 
// Demultiplexern aufgebaut ist.}}
module DemuxCas (
  input  E,
  input  A_0,
  input  A_1,
  input  A_2,
  input  A_3,
  output Y_0,
  output Y_1,
  output Y_2,
  output Y_3,
  output Y_4,
  output Y_5,
  output Y_6,
  output Y_7,
  output Y_8,
  output Y_9,
  output Y_10,
  output Y_11,
  output Y_12,
  output Y_13,
  output Y_14,
  output Y_15
);

  wire demux_1_y_0, demux_1_y_1, demux_1_y_2, demux_1_y_3;

  demux demux_1 (
    .A_0(A_2), .A_1(A_3), .D(E), .Y_0(demux_1_y_0), .Y_1(demux_1_y_1), .Y_2(demux_1_y_2), .Y_3(demux_1_y_3));
  demux demux_2 (.A_0(A_0), .A_1(A_1), .D(demux_1_y_0), .Y_0(Y_0), .Y_1(Y_1), .Y_2(Y_2), .Y_3(Y_3));
  demux demux_3 (.A_0(A_0), .A_1(A_1), .D(demux_1_y_1), .Y_0(Y_4), .Y_1(Y_5), .Y_2(Y_6), .Y_3(Y_7));
  demux demux_4 (.A_0(A_0), .A_1(A_1), .D(demux_1_y_2), .Y_0(Y_8), .Y_1(Y_9), .Y_2(Y_10), .Y_3(Y_11));
  demux demux_5 (.A_0(A_0), .A_1(A_1), .D(demux_1_y_3), .Y_0(Y_12), .Y_1(Y_13), .Y_2(Y_14), .Y_3(Y_15));

  // Notes on the sheet:
  //   E: The input bit which is output to one of the 16 
  //   outputs.
  //   {{de Das Eingangsbit welches auf einen der 16
  //   Ausgänge ausgegeben wird.}}
  //   A_0: select input bit 0
  //   {{de Das 0. Auswahlbit.}}
  //   A_1: select input bit 1
  //   {{de Das 1. Auswahlbit.}}
  //   A_2: select input bit 2
  //   {{de Das 2. Auswahlbit.}}
  //   A_3: select input bit 3
  //   {{de Das 3. Auswahlbit.}}
endmodule

/* Test case:
E A_3 A_2 A_1 A_0  Y_15 Y_14 Y_13 Y_12 Y_11 Y_10 Y_9 Y_8 Y_7 Y_6 Y_5 Y_4 Y_3 Y_2 Y_1 Y_0
repeat(16) 1 bits(4,n) bits(16, 1<<n)
repeat(16) 0 bits(4,n) bits(16, 0)
*/
