// Digital circuit FullAdder.dig as structural Verilog
module FullAdder (
  input  A_i,
  input  B_i,
  input  C_i_1,
  output S_i,
  output C_i
);

  wire and_1_out, and_2_out, xor_1_out;

  and and_1 (and_1_out, A_i, B_i);
  xor xor_1 (xor_1_out, A_i, B_i);
  and and_2 (and_2_out, xor_1_out, C_i_1);
  xor xor_2 (S_i, xor_1_out, C_i_1);
  or or_1 (C_i, and_1_out, and_2_out);

  // Notes on the sheet:
  //   A_i: first bit to add
  //   {{de Erstes zu addierendes Bit.}}
  //   B_i: second bit to add
  //   {{de Zweites zu addierendes Bit.}}
  //   C_i_1: carry in
  //   {{de Übertragsbit der Vorgängerschaltung.}}
  //   S_i: sum {{de Summe}}
  //   C_i: carry bit
  //   {{de Übertragsbit}}
  //   HA 1
  //   HA 2
endmodule

/* Test case:
  A_i B_i C_{i-1} C_i S_i

loop (A,2)
  loop (B,2)
    loop (Ci,2)
 (A) (B) (Ci)   bits(2, A+B+Ci)
    end loop
  end loop
end loop
*/
