// Digital circuit FullAdderCLA.dig as structural Verilog
// Ein Addierer der nach den carry-look-ahead 
// Verfahren implementiert ist.
module FullAdderCLA (
  input  C_i_1,
  input  A_0,
  input  A_1,
  input  A_2,
  input  A_3,
  input  B_0,
  input  B_1,
  input  B_2,
  input  B_3,
  output S_0,
  output S_1,
  output S_2,
  output S_3,
  output C_i
);

  wire and_1_out, and_2_out, and_3_out, and_4_out, and_5_out, and_6_out, and_7_out, and_8_out, and_9_out,
       and_10_out, and_11_out, and_12_out, and_13_out, and_14_out, or_1_out, or_2_out, or_3_out, or_4_out,
       or_5_out, or_6_out, or_8_out, xor_1_out, xor_2_out, xor_3_out, xor_4_out;

  or or_1 (or_1_out, A_3, B_3);
  and and_1 (and_1_out, A_3, B_3);
  or or_2 (or_2_out, A_2, B_2);
  and and_2 (and_2_out, A_2, B_2);
  or or_3 (or_3_out, A_1, B_1);
  and and_3 (and_3_out, A_1, B_1);
  or or_4 (or_4_out, A_0, B_0);
  and and_4 (and_4_out, A_0, B_0);
  and and_5 (and_5_out, C_i_1, or_4_out, or_3_out, or_2_out, or_1_out);
  and and_6 (and_6_out, and_4_out, or_1_out, or_2_out, or_3_out);
  and and_7 (and_7_out, and_3_out, or_2_out, or_1_out);
  and and_8 (and_8_out, or_1_out, and_2_out);
  xor xor_1 (xor_1_out, or_1_out, and_1_out);
  and and_9 (and_9_out, C_i_1, or_4_out, or_3_out, or_2_out);
  and and_10 (and_10_out, or_3_out, or_2_out, and_4_out);
  and and_11 (and_11_out, or_2_out, and_3_out);
  xor xor_2 (xor_2_out, or_2_out, and_2_out);
  and and_12 (and_12_out, C_i_1, or_4_out, or_3_out);
  and and_13 (and_13_out, or_3_out, and_4_out);
  xor xor_3 (xor_3_out, or_3_out, and_3_out);
  and and_14 (and_14_out, or_4_out, C_i_1);
  xor xor_4 (xor_4_out, or_4_out, and_4_out);
  or or_5 (or_5_out, and_12_out, and_13_out, and_3_out);
  or or_6 (or_6_out, and_14_out, and_4_out);
  or or_7 (C_i, and_5_out, and_6_out, and_7_out, and_8_out, and_1_out);
  or or_8 (or_8_out, and_9_out, and_10_out, and_11_out, and_2_out);
  xor xor_5 (S_3, xor_1_out, or_8_out);
  xor xor_6 (S_2, xor_2_out, or_5_out);
  xor xor_7 (S_1, xor_3_out, or_6_out);
  xor xor_8 (S_0, xor_4_out, C_i_1);

  // Notes on the sheet:
  //   C_i_1: Der Übetrag vom Addierer welcher die 
  //   niederwertigeren Bits addiert. Werden die 
  //   niederwertigsten Bits addiert, ist dieser Eingang 
  //   Null.
  //   A_0: Das 0. Bit des ersten zu addierenden Wertes.
  //   A_1: Das 1. Bit des ersten zu addierenden Wertes.
  //   S_0: Das 0. Bit der Summe.
  //   A_2: Das 2. Bit des ersten zu addierenden Wertes.
  //   A_3: Das 3. Bit des ersten zu addierenden Wertes.
  //   S_1: Das 1. Bit der Summe.
  //   S_2: Das 2. Bit der Summe.
  //   B_0: Das 0. Bit des zweiten zu addierenden Wertes.
  //   B_1: Das 1. Bit des zweiten zu addierenden Wertes.
  //   B_2: Das 2. Bit des zweiten zu addierenden Wertes.
  //   B_3: Das 3. Bit des zweiten zu addierenden Wertes.
  //   S_3: Das 3. Bit der Summe.
  //   C_i: Das Übertragsbit, welches an den Adiierer für die
  //   nächst höherwertigen Bits weitergegeben wird.
endmodule

/* Test case:
# complete test of all 512 possible additions
C_i-1 A_3 A_2 A_1 A_0 B_3 B_2 B_1 B_0 C_i S_3 S_2 S_1 S_0
0    0   0   0   0     0   0   0   0     0   0   0   0   0   
0    0   0   0   0     0   0   0   1     0   0   0   0   1   
0    0   0   0   0     0   0   1   0     0   0   0   1   0   
0    0   0   0   0     0   0   1   1     0   0   0   1   1   
0    0   0   0   0     0   1   0   0     0   0   1   0   0   
0    0   0   0   0     0   1   0   1     0   0   1   0   1   
0    0   0   0   0     0   1   1   0     0   0   1   1   0   
0    0   0   0   0     0   1   1   1     0   0   1   1   1   
0    0   0   0   0     1   0   0   0     0   1   0   0   0   
0    0   0   0   0     1   0   0   1     0   1   0   0   1   
0    0   0   0   0     1   0   1   0     0   1   0   1   0   
0    0   0   0   0     1   0   1   1     0   1   0   1   1   
0    0   0   0   0     1   1   0   0     0   1   1   0   0   
0    0   0   0   0     1   1   0   1     0   1   1   0   1   
0    0   0   0   0     1   1   1   0     0   1   1   1   0   
0    0   0   0   0     1   1   1   1     0   1   1   1   1   
0    0   0   0   1     0   0   0   0     0   0   0   0   1   
0    0   0   0   1     0   0   0   1     0   0   0   1   0   
0    0   0   0   1     0   0   1   0     0   0   0   1   1   
0    0   0   0   1     0   0   1   1     0   0   1   0   0   
0    0   0   0   1     0   1   0   0     0   0   1   0   1   
0    0   0   0   1     0   1   0   1     0   0   1   1   0   
0    0   0   0   1     0   1   1   0     0   0   1   1   1   
0    0   0   0   1     0   1   1   1     0   1   0   0   0   
0    0   0   0   1     1   0   0   0     0   1   0   0   1   
0    0   0   0   1     1   0   0   1     0   1   0   1   0   
0    0   0   0   1     1   0   1   0     0   1   0   1   1   
0    0   0   0   1     1   0   1   1     0   1   1   0   0   
0    0   0   0   1     1   1   0   0     0   1   1   0   1   
0    0   0   0   1     1   1   0   1     0   1   1   1   0   
0    0   0   0   1     1   1   1   0     0   1   1   1   1   
0    0   0   0   1     1   1   1   1     1   0   0   0   0   
0    0   0   1   0     0   0   0   0     0   0   0   1   0   
0    0   0   1   0     0   0   0   1     0   0   0   1   1   
0    0   0   1   0     0   0   1   0     0   0   1   0   0   
0    0   0   1   0     0   0   1   1     0   0   1   0   1   
0    0   0   1   0     0   1   0   0     0   0   1   1   0   
0    0   0   1   0     0   1   0   1     0   0   1   1   1   
0    0   0   1   0     0   1   1   0     0   1   0   0   0   
0    0   0   1   0     0   1   1   1     0   1   0   0   1   
0    0   0   1   0     1   0   0   0     0   1   0   1   0   
0    0   0   1   0     1   0   0   1     0   1   0   1   1   
0    0   0   1   0     1   0   1   0     0   1   1   0   0   
0    0   0   1   0     1   0   1   1     0   1   1   0   1   
0    0   0   1   0     1   1   0   0     0   1   1   1   0   
0    0   0   1   0     1   1   0   1     0   1   1   1   1   
0    0   0   1   0     1   1   1   0     1   0   0   0   0   
0    0   0   1   0     1   1   1   1     1   0   0   0   1   
0    0   0   1   1     0   0   0   0     0   0   0   1   1   
0    0   0   1   1     0   0   0   1     0   0   1   0   0   
0    0   0   1   1     0   0   1   0     0   0   1   0   1   
0    0   0   1   1     0   0   1   1     0   0   1   1   0   
0    0   0   1   1     0   1   0   0     0   0   1   1   1   
0    0   0   1   1     0   1   0   1     0   1   0   0   0   
0    0   0   1   1     0   1   1   0     0   1   0   0   1   
0    0   0   1   1     0   1   1   1     0   1   0   1   0   
0    0   0   1   1     1   0   0   0     0   1   0   1   1   
0    0   0   1   1     1   0   0   1     0   1   1   0   0   
0    0   0   1   1     1   0   1   0     0   1   1   0   1   
0    0   0   1   1     1   0   1   1     0   1   1   1   0   
0    0   0   1   1     1   1   0   0     0   1   1   1   1   
0    0   0   1   1     1   1   0   1     1   0   0   0   0   
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*/
