// Digital circuit FullAdderNaive.dig as structural Verilog
// Naive implementation of a full adder.
// {{de Naive Umsetzung eines Volladdierers.}}
module FullAdderNaive (
  input  C_i_1,
  input  A_i,
  input  B_i,
  output S_i,
  output C_i
);

  wire and_1_out, and_2_out, and_3_out, and_4_out, and_5_out, and_6_out, and_7_out, not_1_out, not_2_out,
       not_3_out;

  not not_1 (not_1_out, A_i);
  not not_2 (not_2_out, B_i);
  not not_3 (not_3_out, C_i_1);
  and and_1 (and_1_out, not_1_out, not_2_out, C_i_1);
  and and_2 (and_2_out, not_1_out, B_i, not_3_out);
  and and_3 (and_3_out, A_i, not_2_out, not_3_out);
  and and_4 (and_4_out, A_i, B_i, C_i_1);
  and and_5 (and_5_out, B_i, C_i_1);
  and and_6 (and_6_out, A_i, C_i_1);
  and and_7 (and_7_out, A_i, B_i);
  or or_1 (S_i, and_1_out, and_2_out, and_3_out, and_4_out);
  or or_2 (C_i, and_5_out, and_6_out, and_7_out);
endmodule

/* Test case:
A_i B_i C_{i-1} C_i S_i
 0   0   0     0   0
 0   0   1     0   1
 0   1   0     0   1
 0   1   1     1   0
 1   0   0     0   1
 1   0   1     1   0
 1   1   0     1   0
 1   1   1     1   1
*/
