// Digital circuit FullAdderRC.dig as structural Verilog
// Simplified 4-bit ripple carry adder, consisting of four full adders.
// {{de Vereinfachter 4-Bit Ripple-Carry-Addierer, bestehend
// aus vier Volladdierern.}}
module FullAdderRC (
  input  A_0,
  input  B_0,
  input  A_1,
  input  B_1,
  input  A_2,
  input  B_2,
  input  A_3,
  input  B_3,
  input  C__1,
  output S_0,
  output S_1,
  output S_2,
  output S_3,
  output C_3
);

  wire fulladder_1_p3, fulladder_2_p3, fulladder_3_p3;

  // FullAdder fulladder_1: pin names not known; wires that end beside it: A_3, B_3, fulladder_1_p3, C_3, S_3
  // FullAdder fulladder_2: pin names not known; wires that end beside it: A_2, B_2, fulladder_2_p3, fulladder_1_p3, S_2
  // FullAdder fulladder_3: pin names not known; wires that end beside it: A_1, B_1, fulladder_3_p3, fulladder_2_p3, S_1
  // FullAdder fulladder_4: pin names not known; wires that end beside it: A_0, B_0, C__1, fulladder_3_p3, S_0
endmodule

/* Test case:
# complete test of all 512 possible additions
C_-1 A_3 A_2 A_1 A_0 B_3 B_2 B_1 B_0 C_3 S_3 S_2 S_1 S_0
repeat(256) 0 bits(4,n>>4) bits(4,n) bits(5,(n>>4)+(n&15))
repeat(256) 1 bits(4,n>>4) bits(4,n) bits(5,(n>>4)+(n&15)+1)
*/
