// Digital circuit FullSub.dig as structural Verilog
module FullSub (
  input  A,
  input  B,
  input  BO0,
  input  A_2,
  input  B_2,
  input  BO0_2,
  output S,
  output BO1,
  output S_2,
  output BO1_2
);

  wire halfadder_1_c, halfadder_1_s, halfsub_1_bo, halfsub_1_s, halfsub_2_bo, halfsub_3_bo;

  HalfAdder halfadder_1 (.A(B), .B(BO0), .S(halfadder_1_s), .C(halfadder_1_c));
  HalfSub halfsub_1 (.A(A_2), .B(B_2), .S(halfsub_1_s), .BO(halfsub_1_bo));
  HalfSub halfsub_2 (.A(A), .B(halfadder_1_s), .S(S), .BO(halfsub_2_bo));
  HalfSub halfsub_3 (.A(halfsub_1_s), .B(BO0_2), .S(S_2), .BO(halfsub_3_bo));
  or or_1 (BO1, halfsub_2_bo, halfadder_1_c);
  or or_2 (BO1_2, halfsub_3_bo, halfsub_1_bo);
endmodule
