// Digital circuit FullSub2.dig as structural Verilog
module FullSub2 (
  input  A,
  input  B,
  input  BO_0,
  output S,
  output BO_1
);

  wire halfsub_1_bo, halfsub_1_s, halfsub_2_bo;

  HalfSub halfsub_1 (.A(A), .B(B), .S(halfsub_1_s), .BO(halfsub_1_bo));
  HalfSub halfsub_2 (.A(halfsub_1_s), .B(BO_0), .S(S), .BO(halfsub_2_bo));
  or or_1 (BO_1, halfsub_2_bo, halfsub_1_bo);
endmodule
