// Digital circuit FullSubRC.dig as structural Verilog
module FullSubRC (
  input  A_0,
  input  B_0,
  input  A_1,
  input  B_1,
  input  A_2,
  input  B_2,
  input  A_3,
  input  B_3,
  input  C__1,
  output S_0,
  output S_1,
  output S_2,
  output S_3,
  output C
);

  wire fullsub_1_p5, fullsub_2_p5, fullsub_3_p5;

  // FullSub fullsub_1: pin names not known; wires that end beside it: C__1, A_0, S_0, B_0, fullsub_1_p5
  // FullSub fullsub_2: pin names not known; wires that end beside it: fullsub_1_p5, A_1, S_1, B_1, fullsub_2_p5
  // FullSub fullsub_3: pin names not known; wires that end beside it: fullsub_2_p5, A_2, S_2, B_2, fullsub_3_p5
  // FullSub fullsub_4: pin names not known; wires that end beside it: fullsub_3_p5, A_3, S_3, B_3, C
endmodule

/* Test case:
# complete test of all 512 possible additions
C_{-1} A_3 A_2 A_1 A_0 B_3 B_2 B_1 B_0 C S_3 S_2 S_1 S_0
repeat(256) 0 bits(4,n>>4) bits(4,n) bits(5,(n>>4)-(n&15))
repeat(256) 1 bits(4,n>>4) bits(4,n) bits(5,(n>>4)-(n&15)-1)
*/
