// Digital circuit HalfAdder.dig as structural Verilog
module HalfAdder (
  input  A,
  input  B,
  output S,
  output C
);

  xor xor_1 (S, A, B);
  and and_1 (C, A, B);
endmodule

/* Test case:
A B C S
0 0 0 0
0 1 0 1
1 0 0 1
1 1 1 0
*/
