// Digital circuit LUT.dig as structural Verilog
// A simple look up table. Depending on the position 
// of the four switches, this circuit can emulate any 
// two-input logic function.
// {{de Eine einfache Look Up Table. Je nach Stellung der 
// vier Schalter kann diese Schaltung jede mögliche 
// logische Funktion mit zwei Eingängen nachbilden.}}
module LUT (
  input  A,
  input  B,
  output Y
);

  wire pullup_1_out, pullup_2_out, pullup_3_out, pullup_4_out;

  PullUp pullup_1 (.out(pullup_1_out));
  Switch #(.Closed("true")) S_3 (.A(1'b0), .B(pullup_1_out));
  PullUp pullup_2 (.out(pullup_2_out));
  PullUp pullup_3 (.out(pullup_3_out));
  Switch S_2 (.A(1'b0), .B(pullup_3_out));
  Switch S_1 (.A(1'b0), .B(pullup_2_out));
  PullUp pullup_4 (.out(pullup_4_out));
  Switch #(.Closed("true")) S_0 (.A(1'b0), .B(pullup_4_out));
  mux mux_1 (.A_0(A), .A_1(B), .D_0(pullup_4_out), .D_1(pullup_2_out), .D_2(pullup_3_out), .D_3(pullup_1_out), .Y(Y));

  // Notes on the sheet:
  //   A: first input bit
  //   {{de Erstes Eingangsbit}}
  //   B: second input bit
  //   {{de Zweites Eingangsbit.}}
  //   Y: Output bit of the circuit. The function that is 
  //   output is defined by the four switches.
  //   {{de Ausgangsbit der Schaltung. Die Funktion die
  //   ausgegeben wird, wird über die vier Schalter
  //   definiert.}}
endmodule

/* Test case:
A B Y
0 0 0
0 1 1
1 0 1
1 1 0
*/
