// Digital circuit Multiplexer.dig as structural Verilog
module Multiplexer (
  input  A_0,
  input  A_1,
  input  D_0,
  input  D_1,
  input  D_2,
  input  D_3,
  output Y
);

  wire and_1_out, and_2_out, and_3_out, and_4_out, not_1_out, not_2_out;

  not not_1 (not_1_out, A_1);
  not not_2 (not_2_out, A_0);
  and and_1 (and_1_out, not_2_out, not_1_out, D_0);
  and and_2 (and_2_out, A_0, not_1_out, D_1);
  and and_3 (and_3_out, not_2_out, A_1, D_2);
  and and_4 (and_4_out, A_0, A_1, D_3);
  or or_1 (Y, and_1_out, and_2_out, and_3_out, and_4_out);
endmodule
