// Digital circuit Multiply.dig as structural Verilog
// Einfacher 4-Bit Multiplikator aufgebaut aus drei 4-Bit
// Addierern. Die eigentlichen 1-Bit Multiplikationen 
// werden durch die Und-Gatter implementiert.
module Multiply (
  input  P_0,
  input  P_1,
  input  P_2,
  input  P_3,
  input  Q_0,
  input  Q_1,
  input  Q_2,
  input  Q_3,
  output S_0,
  output S_1,
  output S_2,
  output S_3,
  output S_4,
  output S_5,
  output S_6,
  output S_7
);

  wire and_2_out, and_3_out, and_4_out, and_5_out, and_6_out, and_7_out, and_8_out, and_9_out, and_10_out,
       and_11_out, and_12_out, and_13_out, and_14_out, and_15_out, and_16_out, fulladdercla_1_c_i,
       fulladdercla_1_s_1, fulladdercla_1_s_2, fulladdercla_1_s_3, fulladdercla_2_c_i, fulladdercla_2_s_1,
       fulladdercla_2_s_2, fulladdercla_2_s_3;

  and and_1 (S_0, P_0, Q_0);
  and and_2 (and_2_out, P_0, Q_1);
  and and_3 (and_3_out, P_0, Q_2);
  and and_4 (and_4_out, P_0, Q_3);
  and and_5 (and_5_out, P_1, Q_0);
  and and_6 (and_6_out, P_1, Q_1);
  and and_7 (and_7_out, P_1, Q_2);
  and and_8 (and_8_out, P_1, Q_3);
  and and_9 (and_9_out, P_2, Q_0);
  and and_10 (and_10_out, P_2, Q_1);
  and and_11 (and_11_out, P_2, Q_2);
  and and_12 (and_12_out, P_2, Q_3);
  and and_13 (and_13_out, P_3, Q_0);
  and and_14 (and_14_out, P_3, Q_1);
  and and_15 (and_15_out, P_3, Q_2);
  and and_16 (and_16_out, P_3, Q_3);
  FullAdderCLA fulladdercla_1 (
    .C_i_1(1'b0), .A_0(and_5_out), .A_1(and_9_out), .A_2(and_13_out), .A_3(1'b0), .B_0(and_2_out),
    .B_1(and_6_out), .B_2(and_10_out), .B_3(and_14_out), .S_0(S_1), .S_1(fulladdercla_1_s_1),
    .S_2(fulladdercla_1_s_2), .S_3(fulladdercla_1_s_3), .C_i(fulladdercla_1_c_i));
  FullAdderCLA fulladdercla_2 (
    .C_i_1(1'b0), .A_0(fulladdercla_1_s_1), .A_1(fulladdercla_1_s_2), .A_2(fulladdercla_1_s_3),
    .A_3(fulladdercla_1_c_i), .B_0(and_3_out), .B_1(and_7_out), .B_2(and_11_out), .B_3(and_15_out),
    .S_0(S_2), .S_1(fulladdercla_2_s_1), .S_2(fulladdercla_2_s_2), .S_3(fulladdercla_2_s_3),
    .C_i(fulladdercla_2_c_i));
  FullAdderCLA fulladdercla_3 (
    .C_i_1(1'b0), .A_0(fulladdercla_2_s_1), .A_1(fulladdercla_2_s_2), .A_2(fulladdercla_2_s_3),
    .A_3(fulladdercla_2_c_i), .B_0(and_4_out), .B_1(and_8_out), .B_2(and_12_out), .B_3(and_16_out),
    .S_0(S_3), .S_1(S_4), .S_2(S_5), .S_3(S_6), .C_i(S_7));

  // Notes on the sheet:
  //   P_0: Erste zu multiplizierende 4 Bit Zahl.
  //   Q_0: Zweite zu multiplizierende 4 Bit Zahl.
  //   S_0: Das 8-Bit Ergebnis der Multiplikation
endmodule

/* Test case:
P_3 P_2 P_1 P_0   Q_3 Q_2 Q_1 Q_0   S_7 S_6 S_5 S_4 S_3 S_2 S_1 S_0
0   0   0   0     0   0   0   0     0   0   0   0   0   0   0   0   
0   0   0   0     0   0   0   1     0   0   0   0   0   0   0   0   
0   0   0   0     0   0   1   0     0   0   0   0   0   0   0   0   
0   0   0   0     0   0   1   1     0   0   0   0   0   0   0   0   
0   0   0   0     0   1   0   0     0   0   0   0   0   0   0   0   
0   0   0   0     0   1   0   1     0   0   0   0   0   0   0   0   
0   0   0   0     0   1   1   0     0   0   0   0   0   0   0   0   
0   0   0   0     0   1   1   1     0   0   0   0   0   0   0   0   
0   0   0   0     1   0   0   0     0   0   0   0   0   0   0   0   
0   0   0   0     1   0   0   1     0   0   0   0   0   0   0   0   
0   0   0   0     1   0   1   0     0   0   0   0   0   0   0   0   
0   0   0   0     1   0   1   1     0   0   0   0   0   0   0   0   
0   0   0   0     1   1   0   0     0   0   0   0   0   0   0   0   
0   0   0   0     1   1   0   1     0   0   0   0   0   0   0   0   
0   0   0   0     1   1   1   0     0   0   0   0   0   0   0   0   
0   0   0   0     1   1   1   1     0   0   0   0   0   0   0   0   
0   0   0   1     0   0   0   0     0   0   0   0   0   0   0   0   
0   0   0   1     0   0   0   1     0   0   0   0   0   0   0   1   
0   0   0   1     0   0   1   0     0   0   0   0   0   0   1   0   
0   0   0   1     0   0   1   1     0   0   0   0   0   0   1   1   
0   0   0   1     0   1   0   0     0   0   0   0   0   1   0   0   
0   0   0   1     0   1   0   1     0   0   0   0   0   1   0   1   
0   0   0   1     0   1   1   0     0   0   0   0   0   1   1   0   
0   0   0   1     0   1   1   1     0   0   0   0   0   1   1   1   
0   0   0   1     1   0   0   0     0   0   0   0   1   0   0   0   
0   0   0   1     1   0   0   1     0   0   0   0   1   0   0   1   
0   0   0   1     1   0   1   0     0   0   0   0   1   0   1   0   
0   0   0   1     1   0   1   1     0   0   0   0   1   0   1   1   
0   0   0   1     1   1   0   0     0   0   0   0   1   1   0   0   
0   0   0   1     1   1   0   1     0   0   0   0   1   1   0   1   
0   0   0   1     1   1   1   0     0   0   0   0   1   1   1   0   
0   0   0   1     1   1   1   1     0   0   0   0   1   1   1   1   
0   0   1   0     0   0   0   0     0   0   0   0   0   0   0   0   
0   0   1   0     0   0   0   1     0   0   0   0   0   0   1   0   
0   0   1   0     0   0   1   0     0   0   0   0   0   1   0   0   
0   0   1   0     0   0   1   1     0   0   0   0   0   1   1   0   
0   0   1   0     0   1   0   0     0   0   0   0   1   0   0   0   
0   0   1   0     0   1   0   1     0   0   0   0   1   0   1   0   
0   0   1   0     0   1   1   0     0   0   0   0   1   1   0   0   
0   0   1   0     0   1   1   1     0   0   0   0   1   1   1   0   
0   0   1   0     1   0   0   0     0   0   0   1   0   0   0   0   
0   0   1   0     1   0   0   1     0   0   0   1   0   0   1   0   
0   0   1   0     1   0   1   0     0   0   0   1   0   1   0   0   
0   0   1   0     1   0   1   1     0   0   0   1   0   1   1   0   
0   0   1   0     1   1   0   0     0   0   0   1   1   0   0   0   
0   0   1   0     1   1   0   1     0   0   0   1   1   0   1   0   
0   0   1   0     1   1   1   0     0   0   0   1   1   1   0   0   
0   0   1   0     1   1   1   1     0   0   0   1   1   1   1   0   
0   0   1   1     0   0   0   0     0   0   0   0   0   0   0   0   
0   0   1   1     0   0   0   1     0   0   0   0   0   0   1   1   
0   0   1   1     0   0   1   0     0   0   0   0   0   1   1   0   
0   0   1   1     0   0   1   1     0   0   0   0   1   0   0   1   
0   0   1   1     0   1   0   0     0   0   0   0   1   1   0   0   
0   0   1   1     0   1   0   1     0   0   0   0   1   1   1   1   
0   0   1   1     0   1   1   0     0   0   0   1   0   0   1   0   
0   0   1   1     0   1   1   1     0   0   0   1   0   1   0   1   
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*/
