// Digital circuit Multiply8BitTable.dig as structural Verilog
module Multiply8BitTable (
  input  [7:0] A,
  input  [7:0] B,
  output [15:0] Y
);

  wire [7:0] add_1_s, sub_1_s;
  wire [8:8] add_1_c_o, sub_1_c_o;
  wire [15:0] _9_Bit___16_2_d, _9_Bit___16_d;

  Add #(.Bits(8)) add_1 (.a(A), .b(B), .c_i(1'b0), .s(add_1_s), .c_o(add_1_c_o[8]));
  Sub #(.Bits(8)) sub_1 (.a(A), .b(B), .c_i(1'b0), .s(sub_1_s), .c_o(sub_1_c_o[8]));
  ROM #(.AddrBits(9), .Bits(16)) _9_Bit___16 (.A({add_1_c_o[8], add_1_s}), .sel(1'b1), .D(_9_Bit___16_d));
  ROM #(.AddrBits(9), .Bits(16)) _9_Bit___16_2 (.A({sub_1_c_o[8], sub_1_s}), .sel(1'b1), .D(_9_Bit___16_2_d));
  Sub #(.Bits(16)) sub_2 (.a(_9_Bit___16_d), .b(_9_Bit___16_2_d), .c_i(1'b0), .s(Y));  // open: c_o

  // Notes on the sheet:
  //   A: default 5
  //   B: default 5
  //   (a+b)^2 - (a-b)^2
  //   {{de (a+b)^2 - (a-b)^2}}
  //   ab
  //   {{de ab}}
  //   = a^2+2ab+b^2 - (a^2-2ab+b^2)
  //   = a^2+2ab+b^2 - a^2+2ab-b^2
  //   = 4ab^{ }
  //   = (a+b)^2/4 - (a-b)^2/4
  //   {{de = a^2+2ab+b^2 - (a^2-2ab+b^2)
  //   = a^2+2ab+b^2 - a^2+2ab-b^2
  //   = 4ab^{ }
  //   = (a+b)^2/4 - (a-b)^2/4}}
  //   contents of _9_Bit___16 (hex, n*v repeats v):
  //   0,0,1,2,4,6,9,c,10,14,19,1e,24,2a,31,38,40,48,51,5a,64,6e,79,84,90,9c,a9,b6,c4,d2,
  //   e1,f0,100,110,121,132,144,156,169,17c,190,1a4,1b9,1ce,1e4,1fa,211,228,240,258,271,
  //   28a,2a4,2be,2d9,2f4,310,32c,349,366,384,3a2,3c1,3e0,400,420,441,462,484,4a6,4c9,4ec,
  //   510,534,559,57e,5a4,5ca,5f1,618,640,668,691,6ba,6e4,70e,739,764,790,7bc,7e9,816,844,
  //   872,8a1,8d0,900,930,961,992,9c4,9f6,a29,a5c,a90,ac4,af9,b2e,b64,b9a,bd1,c08,c40,c78,
  //   cb1,cea,d24,d5e,d99,dd4,e10,e4c,e89,ec6,f04,f42,f81,fc0,1000,1040,1081,10c2,1104,
  //   1146,1189,11cc,1210,1254,1299,12de,1324,136a,13b1,13f8,1440,1488,14d1,151a,1564,15ae,
  //   15f9,1644,1690,16dc,1729,1776,17c4,1812,1861,18b0,1900,1950,19a1,19f2,1a44,1a96,1ae9,
  //   1b3c,1b90,1be4,1c39,1c8e,1ce4,1d3a,1d91,1de8,1e40,1e98,1ef1,1f4a,1fa4,1ffe,2059,20b4,
  //   2110,216c,21c9,2226,2284,22e2,2341,23a0,2400,2460,24c1,2522,2584,25e6,2649,26ac,2710,
  //   2774,27d9,283e,28a4,290a,2971,29d8,2a40,2aa8,2b11,2b7a,2be4,2c4e,2cb9,2d24,2d90,2dfc,
  //   2e69,2ed6,2f44,2fb2,3021,3090,3100,3170,31e1,3252,32c4,3336,33a9,341c,3490,3504,3579,
  //   35ee,3664,36da,3751,37c8,3840,38b8,3931,39aa,3a24,3a9e,3b19,3b94,3c10,3c8c,3d09,3d86,
  //   3e04,3e82,3f01,3f80,4000,4080,4101,4182,4204,4286,4309,438c,4410,4494,4519,459e,4624,
  //   46aa,4731,47b8,4840,48c8,4951,49da,4a64,4aee,4b79,4c04,4c90,4d1c,4da9,4e36,4ec4,4f52,
  //   4fe1,5070,5100,5190,5221,52b2,5344,53d6,5469,54fc,5590,5624,56b9,574e,57e4,587a,5911,
  //   59a8,5a40,5ad8,5b71,5c0a,5ca4,5d3e,5dd9,5e74,5f10,5fac,6049,60e6,6184,6222,62c1,6360,
  //   6400,64a0,6541,65e2,6684,6726,67c9,686c,6910,69b4,6a59,6afe,6ba4,6c4a,6cf1,6d98,6e40,
  //   6ee8,6f91,703a,70e4,718e,7239,72e4,7390,743c,74e9,7596,7644,76f2,77a1,7850,7900,79b0,
  //   7a61,7b12,7bc4,7c76,7d29,7ddc,7e90,7f44,7ff9,80ae,8164,821a,82d1,8388,8440,84f8,85b1,
  //   866a,8724,87de,8899,8954,8a10,8acc,8b89,8c46,8d04,8dc2,8e81,8f40,9000,90c0,9181,9242,
  //   9304,93c6,9489,954c,9610,96d4,9799,985e,9924,99ea,9ab1,9b78,9c40,9d08,9dd1,9e9a,9f64,
  //   a02e,a0f9,a1c4,a290,a35c,a429,a4f6,a5c4,a692,a761,a830,a900,a9d0,aaa1,ab72,ac44,ad16,
  //   ade9,aebc,af90,b064,b139,b20e,b2e4,b3ba,b491,b568,b640,b718,b7f1,b8ca,b9a4,ba7e,bb59,
  //   bc34,bd10,bdec,bec9,bfa6,c084,c162,c241,c320,c400,c4e0,c5c1,c6a2,c784,c866,c949,ca2c,
  //   cb10,cbf4,ccd9,cdbe,cea4,cf8a,d071,d158,d240,d328,d411,d4fa,d5e4,d6ce,d7b9,d8a4,d990,
  //   da7c,db69,dc56,dd44,de32,df21,e010,e100,e1f0,e2e1,e3d2,e4c4,e5b6,e6a9,e79c,e890,e984,
  //   ea79,eb6e,ec64,ed5a,ee51,ef48,f040,f138,f231,f32a,f424,f51e,f619,f714,f810,f90c,fa09,
  //   fb06,fc04,fd02,fe01,ff00,1,2,2,3,3,4,4,5,5,6,6,7,7,8,8,9,9,a,a,b,b,c,c,d,d,e,e,f,
  //   f,10,10,11,11,12,12,13,13,14,14,15,15,16,16,17,17,18,18,19,19,1a,1a,1b,1b,1c,1c,1d,
  //   1d,1e,1e,1f,1f,20,20,21,21,22,22,23,23,24,24,25,25,26,26,27,27,28,28,29,29,2a,2a,
  //   2b,2b,2c,2c,2d,2d,2e,2e,2f,2f,30,30,31,31,32,32,33,33,34,34,35,35,36,36,37,37,38,
  //   38,39,39,3a,3a,3b,3b,3c,3c,3d,3d,3e,3e,3f,3f,40,40,41,41,42,42,43,43,44,44,45,45,
  //   46,46,47,47,48,48,49,49,4a,4a,4b,4b,4c,4c,4d,4d,4e,4e,4f,4f,50,50,51,51,52,52,53,
  //   53,54,54,55,55,56,56,57,57,58,58,59,59,5a,5a,5b,5b,5c,5c,5d,5d,5e,5e,5f,5f,60,60,
  //   61,61,62,62,63,63,64,64,65,65,66,66,67,67,68,68,69,69,6a,6a,6b,6b,6c,6c,6d,6d,6e,
  //   6e,6f,6f,70,70,71,71,72,72,73,73,74,74,75,75,76,76,77,77,78,78,79,79,7a,7a,7b,7b,
  //   7c,7c,7d,7d,7e,7e,7f,7f,80,80,81,81,82,82,83,83,84,84,85,85,86,86,87,87,88,88,89,
  //   89,8a,8a,8b,8b,8c,8c,8d,8d,8e,8e,8f,8f,90,90,91,91,92,92,93,93,94,94,95,95,96,96,
  //   97,97,98,98,99,99,9a,9a,9b,9b,9c,9c,9d,9d,9e,9e,9f,9f,a0,a0,a1,a1,a2,a2,a3,a3,a4,
  //   a4,a5,a5,a6,a6,a7,a7,a8,a8,a9,a9,aa,aa,ab,ab,ac,ac,ad,ad,ae,ae,af,af,b0,b0,b1,b1,
  //   b2,b2,b3,b3,b4,b4,b5,b5,b6,b6,b7,b7,b8,b8,b9,b9,ba,ba,bb,bb,bc,bc,bd,bd,be,be,bf,
  //   bf,c0,c0,c1,c1,c2,c2,c3,c3,c4,c4,c5,c5,c6,c6,c7,c7,c8,c8,c9,c9,ca,ca,cb,cb,cc,cc,
  //   cd,cd,ce,ce,cf,cf,d0,d0,d1,d1,d2,d2,d3,d3,d4,d4,d5,d5,d6,d6,d7,d7,d8,d8,d9,d9,da,
  //   da,db,db,dc,dc,dd,dd,de,de,df,df,e0,e0,e1,e1,e2,e2,e3,e3,e4,e4,e5,e5,e6,e6,e7,e7,
  //   e8,e8,e9,e9,ea,ea,eb,eb,ec,ec,ed,ed,ee,ee,ef,ef,f0,f0,f1,f1,f2,f2,f3,f3,f4,f4,f5,
  //   f5,f6,f6,f7,f7,f8,f8,f9,f9,fa,fa,fb,fb,fc,fc,fd,fd,fe,fe,ff,ff,100,100,101,2,3,3,
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  //   contents of _9_Bit___16_2 (hex, n*v repeats v):
  //   0,0,1,2,4,6,9,c,10,14,19,1e,24,2a,31,38,40,48,51,5a,64,6e,79,84,90,9c,a9,b6,c4,d2,
  //   e1,f0,100,110,121,132,144,156,169,17c,190,1a4,1b9,1ce,1e4,1fa,211,228,240,258,271,
  //   28a,2a4,2be,2d9,2f4,310,32c,349,366,384,3a2,3c1,3e0,400,420,441,462,484,4a6,4c9,4ec,
  //   510,534,559,57e,5a4,5ca,5f1,618,640,668,691,6ba,6e4,70e,739,764,790,7bc,7e9,816,844,
  //   872,8a1,8d0,900,930,961,992,9c4,9f6,a29,a5c,a90,ac4,af9,b2e,b64,b9a,bd1,c08,c40,c78,
  //   cb1,cea,d24,d5e,d99,dd4,e10,e4c,e89,ec6,f04,f42,f81,fc0,1000,1040,1081,10c2,1104,
  //   1146,1189,11cc,1210,1254,1299,12de,1324,136a,13b1,13f8,1440,1488,14d1,151a,1564,15ae,
  //   15f9,1644,1690,16dc,1729,1776,17c4,1812,1861,18b0,1900,1950,19a1,19f2,1a44,1a96,1ae9,
  //   1b3c,1b90,1be4,1c39,1c8e,1ce4,1d3a,1d91,1de8,1e40,1e98,1ef1,1f4a,1fa4,1ffe,2059,20b4,
  //   2110,216c,21c9,2226,2284,22e2,2341,23a0,2400,2460,24c1,2522,2584,25e6,2649,26ac,2710,
  //   2774,27d9,283e,28a4,290a,2971,29d8,2a40,2aa8,2b11,2b7a,2be4,2c4e,2cb9,2d24,2d90,2dfc,
  //   2e69,2ed6,2f44,2fb2,3021,3090,3100,3170,31e1,3252,32c4,3336,33a9,341c,3490,3504,3579,
  //   35ee,3664,36da,3751,37c8,3840,38b8,3931,39aa,3a24,3a9e,3b19,3b94,3c10,3c8c,3d09,3d86,
  //   3e04,3e82,3f01,3f80,4000,3f80,3f01,3e82,3e04,3d86,3d09,3c8c,3c10,3b94,3b19,3a9e,3a24,
  //   39aa,3931,38b8,3840,37c8,3751,36da,3664,35ee,3579,3504,3490,341c,33a9,3336,32c4,3252,
  //   31e1,3170,3100,3090,3021,2fb2,2f44,2ed6,2e69,2dfc,2d90,2d24,2cb9,2c4e,2be4,2b7a,2b11,
  //   2aa8,2a40,29d8,2971,290a,28a4,283e,27d9,2774,2710,26ac,2649,25e6,2584,2522,24c1,2460,
  //   2400,23a0,2341,22e2,2284,2226,21c9,216c,2110,20b4,2059,1ffe,1fa4,1f4a,1ef1,1e98,1e40,
  //   1de8,1d91,1d3a,1ce4,1c8e,1c39,1be4,1b90,1b3c,1ae9,1a96,1a44,19f2,19a1,1950,1900,18b0,
  //   1861,1812,17c4,1776,1729,16dc,1690,1644,15f9,15ae,1564,151a,14d1,1488,1440,13f8,13b1,
  //   136a,1324,12de,1299,1254,1210,11cc,1189,1146,1104,10c2,1081,1040,1000,fc0,f81,f42,
  //   f04,ec6,e89,e4c,e10,dd4,d99,d5e,d24,cea,cb1,c78,c40,c08,bd1,b9a,b64,b2e,af9,ac4,a90,
  //   a5c,a29,9f6,9c4,992,961,930,900,8d0,8a1,872,844,816,7e9,7bc,790,764,739,70e,6e4,6ba,
  //   691,668,640,618,5f1,5ca,5a4,57e,559,534,510,4ec,4c9,4a6,484,462,441,420,400,3e0,3c1,
  //   3a2,384,366,349,32c,310,2f4,2d9,2be,2a4,28a,271,258,240,228,211,1fa,1e4,1ce,1b9,1a4,
  //   190,17c,169,156,144,132,121,110,100,f0,e1,d2,c4,b6,a9,9c,90,84,79,6e,64,5a,51,48,
  //   40,38,31,2a,24,1e,19,14,10,c,9,6,4,2,1,0,1,2,2,3,3,4,4,5,5,6,6,7,7,8,8,9,9,a,a,b,
  //   b,c,c,d,d,e,e,f,f,10,10,11,11,12,12,13,13,14,14,15,15,16,16,17,17,18,18,19,19,1a,
  //   1a,1b,1b,1c,1c,1d,1d,1e,1e,1f,1f,20,20,21,21,22,22,23,23,24,24,25,25,26,26,27,27,
  //   28,28,29,29,2a,2a,2b,2b,2c,2c,2d,2d,2e,2e,2f,2f,30,30,31,31,32,32,33,33,34,34,35,
  //   35,36,36,37,37,38,38,39,39,3a,3a,3b,3b,3c,3c,3d,3d,3e,3e,3f,3f,40,40,41,41,42,42,
  //   43,43,44,44,45,45,46,46,47,47,48,48,49,49,4a,4a,4b,4b,4c,4c,4d,4d,4e,4e,4f,4f,50,
  //   50,51,51,52,52,53,53,54,54,55,55,56,56,57,57,58,58,59,59,5a,5a,5b,5b,5c,5c,5d,5d,
  //   5e,5e,5f,5f,60,60,61,61,62,62,63,63,64,64,65,65,66,66,67,67,68,68,69,69,6a,6a,6b,
  //   6b,6c,6c,6d,6d,6e,6e,6f,6f,70,70,71,71,72,72,73,73,74,74,75,75,76,76,77,77,78,78,
  //   79,79,7a,7a,7b,7b,7c,7c,7d,7d,7e,7e,7f,7f,80,80,81,81,82,82,83,83,84,84,85,85,86,
  //   86,87,87,88,88,89,89,8a,8a,8b,8b,8c,8c,8d,8d,8e,8e,8f,8f,90,90,91,91,92,92,93,93,
  //   94,94,95,95,96,96,97,97,98,98,99,99,9a,9a,9b,9b,9c,9c,9d,9d,9e,9e,9f,9f,a0,a0,a1,
  //   a1,a2,a2,a3,a3,a4,a4,a5,a5,a6,a6,a7,a7,a8,a8,a9,a9,aa,aa,ab,ab,ac,ac,ad,ad,ae,ae,
  //   af,af,b0,b0,b1,b1,b2,b2,b3,b3,b4,b4,b5,b5,b6,b6,b7,b7,b8,b8,b9,b9,ba,ba,bb,bb,bc,
  //   bc,bd,bd,be,be,bf,bf,c0,c0,c1,c1,c2,c2,c3,c3,c4,c4,c5,c5,c6,c6,c7,c7,c8,c8,c9,c9,
  //   ca,ca,cb,cb,cc,cc,cd,cd,ce,ce,cf,cf,d0,d0,d1,d1,d2,d2,d3,d3,d4,d4,d5,d5,d6,d6,d7,
  //   d7,d8,d8,d9,d9,da,da,db,db,dc,dc,dd,dd,de,de,df,df,e0,e0,e1,e1,e2,e2,e3,e3,e4,e4,
  //   e5,e5,e6,e6,e7,e7,e8,e8,e9,e9,ea,ea,eb,eb,ec,ec,ed,ed,ee,ee,ef,ef,f0,f0,f1,f1,f2,
  //   f2,f3,f3,f4,f4,f5,f5,f6,f6,f7,f7,f8,f8,f9,f9,fa,fa,fb,fb,fc,fc,fd,fd,fe,fe,ff,ff,
  //   100,100,101,2,3,3,4,4,5,5,6,6,7,7,8,8,9,9,a,a,b,b,c,c,d,d,e,e,f,f,10,10,11,11,12,
  //   12,13,13,14,14,15,15,16,16,17,17,18,18,19,19,1a,1a,1b,1b,1c,1c,1d,1d,1e,1e,1f,1f,
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endmodule

/* Test case:
A B Y

loop (a,256)
  loop (b,256)
(a) (b) (a*b)
  end loop
end loop
*/
