// Digital circuit MultiplyTest.dig as structural Verilog
module MultiplyTest (
  input  [3:0] P,
  input  [3:0] Q
);

  wire [3:0] multiply_1_s_0, multiply_1_s_4;

  Seven_Seg_Hex seven_seg_hex_1 (.dp(Q[0]));  // open: d
  Seven_Seg_Hex seven_seg_hex_2 (.dp(P[0]));  // open: d
  Multiply multiply_1 (
    .P_0(P[0]), .P_1(P[1]), .P_2(P[2]), .P_3(P[3]), .Q_0(Q[0]), .Q_1(Q[1]), .Q_2(Q[2]), .Q_3(Q[3]),
    .S_0(multiply_1_s_0[0]), .S_1(multiply_1_s_0[1]), .S_2(multiply_1_s_0[2]), .S_3(multiply_1_s_0[3]),
    .S_4(multiply_1_s_4[0]), .S_5(multiply_1_s_4[1]), .S_6(multiply_1_s_4[2]), .S_7(multiply_1_s_4[3]));
  Seven_Seg_Hex seven_seg_hex_3 (.dp(multiply_1_s_4[0]));  // open: d
  Seven_Seg_Hex seven_seg_hex_4 (.dp(multiply_1_s_0[0]));  // open: d
  // Pins of 1 and 4 bits meet at P
  // Pins of 1 and 4 bits meet at Q
  // Pins of 1 and 4 bits meet at multiply_1_s_0
  // Pins of 1 and 4 bits meet at multiply_1_s_4
endmodule
