// Digital circuit Xor1.dig as structural Verilog
module Xor1 (
  input  A,
  input  B,
  output Y
);

  wire nand_1_out, or_1_out;

  or or_1 (or_1_out, A, B);
  nand nand_1 (nand_1_out, A, B);
  and and_1 (Y, or_1_out, nand_1_out);
endmodule

/* Test case:
A B Y
0 0 0
0 1 1
1 0 1
1 1 0
*/
