// Digital circuit Xor3.dig as structural Verilog
module Xor3 (
  input  A,
  input  B,
  output Y
);

  wire nand_1_out, nand_2_out, nand_3_out, nand_4_out;

  nand nand_1 (nand_1_out, A, A);
  nand nand_2 (nand_2_out, B, B);
  nand nand_3 (nand_3_out, nand_1_out, B);
  nand nand_4 (nand_4_out, A, nand_2_out);
  nand nand_5 (Y, nand_3_out, nand_4_out);
endmodule

/* Test case:
A B Y
0 0 0
0 1 1
1 0 1
1 1 0
*/
