// Digital circuit demux.dig as structural Verilog
// Ein 4-Bit Demultiplexer. Die zwei Eingangsbits A_0 
// und A_1 legen fest, auf welche der 4 
// Ausgangsleitungen Y_0 bis Y_3  der Eingang D 
// ausgegeben wird.
module demux (
  input  A_0,
  input  A_1,
  input  D,
  output Y_0,
  output Y_1,
  output Y_2,
  output Y_3
);

  wire not_1_out, not_2_out;

  not not_1 (not_1_out, A_1);
  not not_2 (not_2_out, A_0);
  and and_1 (Y_0, not_2_out, not_1_out, D);
  and and_2 (Y_1, A_0, not_1_out, D);
  and and_3 (Y_2, not_2_out, A_1, D);
  and and_4 (Y_3, A_0, A_1, D);

  // Notes on the sheet:
  //   A_0: Das 0. Auswahlbit.
  //   A_1: Das 1. Auswahlbit.
  //   D: Das Datenbit welches auf einen der vier Ausgänge
  //   ausgegeben wird.
  //   Y_0: Das 0. Ausgangsbit.
  //   Y_1: Das 1. Ausgangsbit.
  //   Y_2: Das 2. Ausgangsbit.
  //   Y_3: Das 3. Ausgangsbit.
endmodule

/* Test case:
A_1 A_0 D Y_3 Y_2 Y_1 Y_0
 0   0  0  0   0   0   0
 0   0  1  0   0   0   1
 0   1  0  0   0   0   0
 0   1  1  0   0   1   0
 1   0  0  0   0   0   0
 1   0  1  0   1   0   0
 1   1  0  0   0   0   0
 1   1  1  1   0   0   0
*/
