// Digital circuit errors.dig as structural Verilog
module errors (
  input  in_1,
  input  in_2,
  input  in_3,
  input  [3:0] in_4,
  input  [3:0] in_5,
  output [7:0] out_6,
  output out_7
);

  wire and_1_out, and_2_out;

  and and_1 (and_1_out, in_1, in_2);
  and and_2 (and_2_out, in_3, in_3);
  // And and_3 has open pins: In_1=and_1_out, In_2=and_2_out, out=open
  // Pins of 1 and 4 bits meet at in_4
  // Pins of 1 and 4 bits meet at in_5
  // Pins of 1 and 8 bits meet at {in_5, in_4}

  assign out_6 = {in_5, in_4};
endmodule
