// Digital circuit GrayCounter.dig as structural Verilog
module GrayCounter (
  input  C,
  output [2:0] G
);

  wire and_1_out, Tog_nq, Tog_q;
  wire [1:0] grayfinal_1_p1;

  T_FF #(.withEnable("false")) Tog (.C(C), .Q(Tog_q), .nQ(Tog_nq));
  and and_1 (and_1_out, grayfinal_1_p1[0], Tog_q);
  // GrayFinal #(.generic("inBits:=2; bits:=3; if (isPresent(args)) { bits=args.bits; if (args.bits>3) { setCircuit(\"GrayNode.dig\"); } }")) grayfinal_1: pin names not known; wires that end beside it: grayfinal_1_p1, 1'b1, Tog_q, C, G
  T_FF G_0 (.T(Tog_nq), .C(C), .Q(grayfinal_1_p1[0]));  // open: nQ
  T_FF G_1 (.T(and_1_out), .C(C), .Q(grayfinal_1_p1[1]));  // open: nQ

  // Notes on the sheet:
  //   Generic Gray Code counter. 
  //   Needs the argument "bits" which sets the bit 
  //   width of the counter.
  //   The sub circuit "GrayFinal" is replaced by 
  //   "GrayNode" if necessary.
  //   {{de Generischer Gray-Code Zähler
  //   Benötigt das Argument "bits" welches die 
  //   Bitbreite des Zählers angibt.
  //   Die Teilschaltung "GrayFinal" wird durch 
  //   "GrayNode" ersetzt, wenn die Bitzahl größer 
  //   ist als drei.}}
endmodule

/* Test case:
C G
0 0
loop (n,(1<<3)-1)
C ((n+1) ^ ((n+1)>>1))
end loop
C 0
*/
