// Digital circuit Test.dig as structural Verilog
module Test (
  input  C,
  output [4:0] G_5,
  output [5:0] G_6,
  output [3:0] G_4,
  output [2:0] G_3
);

  // GrayCounter #(.generic("bits := 3;")) graycounter_1: pin names not known; wires that end beside it: C, G_3
  // GrayCounter #(.generic("bits := 4;")) graycounter_2: pin names not known; wires that end beside it: C, G_4
  // GrayCounter #(.generic("bits := 5;")) graycounter_3: pin names not known; wires that end beside it: C, G_5
  // GrayCounter #(.generic("bits := 6;")) graycounter_4: pin names not known; wires that end beside it: C, G_6
endmodule

/* Test case G_3:
C G_3
0 0
loop (n,(1<<3)-1)
C ((n+1) ^ ((n+1)>>1))
end loop
C 0
*/

/* Test case G_4:
C G_4
0 0
loop (n,(1<<4)-1)
C ((n+1) ^ ((n+1)>>1))
end loop
C 0
*/

/* Test case G_5:
C G_5
0 0
loop (n,(1<<5)-1)
C ((n+1) ^ ((n+1)>>1))
end loop
C 0
*/

/* Test case G_6:
C G_6
0 0
loop (n,(1<<6)-1)
C ((n+1) ^ ((n+1)>>1))
end loop
C 0
*/
