// Digital circuit Test.dig as structural Verilog
module Test (
  input  [31:0] D_32_in,
  input  [4:0] sh_32,
  input  [7:0] D_8_in,
  input  [2:0] sh_8,
  output [31:0] D_32,
  output [7:0] D_8
);

  // barrelShifter #(.generic("dataBits := 32;")) _32_bit: pin names not known; wires that end beside it: D_32_in, sh_32, D_32
  // barrelShifter #(.generic("dataBits := 8;")) _8_bit: pin names not known; wires that end beside it: D_8_in, sh_8, D_8

  // Notes on the sheet:
  //   D_32_in: default 1
  //   D_8_in: default 1
endmodule

/* Test case 32 bit:
D^32_in sh^32 D^32
loop(n,32) 
   1     (n)  (1<<n)
end loop

loop(n,32) 
   7     (n)  (7<<n)
end loop
*/

/* Test case 8 bit:
D^8_in sh^8 D^8
loop(n,8) 
   1     (n)  (1<<n)
end loop

loop(n,8) 
   7     (n)  (7<<n)
end loop
*/
