// Digital circuit TestBarrelShifter2.dig as structural Verilog
module TestBarrelShifter2 (
  input  [31:0] D_32_in,
  input  [4:0] sh_32,
  input  [7:0] D_8_in,
  input  [2:0] sh_8,
  input  [7:0] D_8_inR,
  input  [2:0] sh_8_R,
  input  [15:0] D_16_in,
  input  [3:0] sh_16,
  input  [63:0] D_64_in,
  input  [5:0] sh_64,
  output [31:0] D_32,
  output [7:0] D_8,
  output [7:0] D_8_R,
  output [15:0] D_16,
  output [63:0] D_64
);

  // barrelShifter2 #(.generic("dataBits := 64; direction := \"left\";")) _64_bit__left: pin names not known; wires that end beside it: D_64_in, sh_64, D_64
  // barrelShifter2 #(.generic("dataBits := 32; direction := \"left\";")) _32_bit__left: pin names not known; wires that end beside it: D_32_in, sh_32, D_32
  // barrelShifter2 #(.generic("dataBits := 8; direction := \"left\";")) _8_bit__left: pin names not known; wires that end beside it: D_8_in, sh_8, D_8
  // barrelShifter2 #(.generic("dataBits := 8; direction := \"right\";")) _8_bit__right: pin names not known; wires that end beside it: D_8_inR, sh_8_R, D_8_R
  // barrelShifter2 #(.generic("dataBits := 16; direction := \"arith\";")) _16_bit__right__arith: pin names not known; wires that end beside it: D_16_in, sh_16, D_16

  // Notes on the sheet:
  //   D_32_in: default 1
  //   D_8_in: default 1
  //   D_8_inR: default 128
  //   D_16_in: default 32768
  //   D_64_in: default 1
endmodule

/* Test case 64 bit, left:
D^64_in sh^64 D^64
loop(n,64) 
   1     (n)  (1<<n)
end loop

loop(n,64) 
   7     (n)  (7<<n)
end loop
*/

/* Test case 32 bit, left:
D^32_in sh^32 D^32
loop(n,32) 
   1     (n)  (1<<n)
end loop

loop(n,32) 
   7     (n)  (7<<n)
end loop
*/

/* Test case 8 bit, left:
D^8_in sh^8 D^8
loop(n,8) 
   1     (n)  (1<<n)
end loop

loop(n,8) 
   7     (n)  (7<<n)
end loop
*/

/* Test case 8 bit, right:
D^8_inR sh^8_R D^8_R
loop(n,8) 
   128     (n)  (128>>n)
end loop

loop(n,8) 
   192     (n)  (192>>n)
end loop
*/

/* Test case 16 bit, right arith:
D^16_in sh^16 D^16
loop(n,16) 
   (1<<14)     (n)  ((1<<14)>>n)
end loop

loop(n,16) 
   (1<<15)     (n)  (-1<<(15-n))
end loop
*/
