// Digital circuit barrelShifter.dig as structural Verilog
// Barrel-Shifter with selectable bit width.
// {{de Barrel-Shifter mit wählbarer Bitbreite.}}
module barrelShifter (
  input  [15:0] D_in,
  input  [3:0] sh,
  output [15:0] D
);

  shift_inc #(.generic("if (args.direction=\"right\") { export circuit:=\"shift-fixed-right-inc.dig\"; } else { if (args.direction=\"arith\") { export circuit:=\"shift-fixed-arith-right-inc.dig\"; } else { if (args.direction=\"left\") { export circuit:=\"shift-fixed-left-inc.dig\"; } else { panic(\"only \\\"left\\\", \\\"right\\\" or \\\"arith\\\" is allowed as direction, not \\\"\"+args.direction+\"\\\"!\"); } } } shiftBits:=bitsNeededFor(args.dataBit")) shift_inc_1 (
    .D_in(D_in), .sh(sh), .D(D));

  // Notes on the sheet:
  //   A BarrelShifter implemented using recursion.
  //   {{de Ein rekursiv implementierter BarrelShifter.}}
endmodule

/* Test case 4 bits, left:
D_in sh D

  1  0  1
  1  1  2
  1  2  4
  1  3  8
  1  4  1

  2  0  2
  2  1  4
  2  2  8
  2  3  0
  2  4  2
*/

/* Test case 4 bits, right:
D_in sh D

  1  0  1
  2  1  1
  4  2  1
  8  3  1
  1  4  1

  4  0  4
  4  1  2
  4  2  1
  4  3  0
  4  4  4

 15  1  7
*/

/* Code that sets the parameters or builds the circuit:
dataBits := 5;
direction := "left";
*/

/* Test case 4 bits, arith:
D_in sh D

  1  0  1
  2  1  1
  4  2  1
  8  3  15
  1  4  1

  4  0  4
  4  1  2
  4  2  1
  4  3  0
  4  4  4

 15  1  15
*/
