// Digital circuit shift-fixed-arith-right-inc.dig as structural Verilog
module shift_fixed_arith_right_inc (
  input  [7:0] D_in,
  input  en,
  output [7:0] D
);

  wire [7:7] multiplexer_1_out;

  Multiplexer #(.generic("this.Bits=int(args.shift);")) multiplexer_1 (
    .sel(D_in[7]), .in_0(1'b0), .in_1(1'b1), .out(multiplexer_1_out[7]));
  Multiplexer #(.Bits(8), .generic("this.Bits=int(args.dataBits);")) multiplexer_2 (
    .sel(en), .in_0(D_in), .in_1({multiplexer_1_out[7], D_in[7:1]}), .out(D));
endmodule
