// Digital circuit shift-fixed-left-inc.dig as structural Verilog
module shift_fixed_left_inc (
  input  [7:0] D_in,
  input  en,
  output [7:0] D
);

  Multiplexer #(.Bits(8), .generic("this.Bits=int(args.dataBits);")) multiplexer_1 (
    .sel(en), .in_0(D_in), .in_1({D_in[6:0], 1'b0}), .out(D));
endmodule

/* Code that sets the parameters or builds the circuit:
dataBits := 8;
shift := 3;
*/
