// Digital circuit shift-inc.dig as structural Verilog
module shift_inc (
  input  [15:0] D_in,
  input  [3:0] sh,
  output [15:0] D
);

  wire shift_fixed_left_inc_1_p3;

  // shift_fixed_left_inc #(.generic("shift := 1<<(args.shiftBits-1); setCircuit(args.circuit);")) shift_fixed_left_inc_1: pin names not known; wires that end beside it: D_in, sh[3], shift_fixed_left_inc_1_p3
  // shift_inc #(.generic("if (args.shiftBits=2) { export shift := 1; setCircuit(args.circuit); } else { export shiftBits := args.shiftBits-1; }")) shift_inc_1: pin names not known; wires that end beside it: shift_fixed_left_inc_1_p3, sh[2:0], D
endmodule

/* Code that sets the parameters or builds the circuit:
circuit := "shift-fixed-left-inc.dig";
dataBits := 8;
shiftBits := 2;
*/

/* Code that sets the parameters or builds the circuit:
circuit := "shift-fixed-left-inc.dig";
dataBits := 8;
shiftBits := 3;
*/
