// Digital circuit GrayCounter.dig as structural Verilog
module GrayCounter (
  input  C,
  output [2:0] G
);

  wire and_1_out, Tog_nq, Tog_q;
  wire [1:0] grayfinal_inc_1_p1;

  T_FF #(.withEnable("false")) Tog (.C(C), .Q(Tog_q), .nQ(Tog_nq));
  and and_1 (and_1_out, grayfinal_inc_1_p1[0], Tog_q);
  // GrayFinal_inc #(.generic("inBits:=2; if (args.bits>3) { setCircuit(\"GrayNode-inc.dig\"); }")) grayfinal_inc_1: pin names not known; wires that end beside it: grayfinal_inc_1_p1, 1'b1, Tog_q, C, G
  T_FF G_0 (.T(Tog_nq), .C(C), .Q(grayfinal_inc_1_p1[0]));  // open: nQ
  T_FF G_1 (.T(and_1_out), .C(C), .Q(grayfinal_inc_1_p1[1]));  // open: nQ

  // Notes on the sheet:
  //   Generic Gray Code counter. 
  //   Needs the argument "bits" which sets the bit 
  //   width of the counter.
  //   The sub circuit "GrayFinal" is replaced by 
  //   "GrayNode" if necessary.
  //   {{de Generischer Gray-Code Zähler
  //   Benötigt das Argument "bits" welches die 
  //   Bitbreite des Zählers angibt.
  //   Die Teilschaltung "GrayFinal" wird durch 
  //   "GrayNode" ersetzt, wenn die Bitzahl größer 
  //   ist als drei.}}
endmodule

/* Test case 3 bits:
C G
0 0
loop (n,(1<<3)-1)
C ((n+1) ^ ((n+1)>>1))
end loop
C 0
*/

/* Test case 5 bits:
C G
0 0
loop (n,(1<<5)-1)
C ((n+1) ^ ((n+1)>>1))
end loop
C 0
*/

/* Code that sets the parameters or builds the circuit:
bits := 3;
*/

/* Test case 4 bits:
C G
0 0
loop (n,(1<<4)-1)
C ((n+1) ^ ((n+1)>>1))
end loop
C 0
*/
