// Digital circuit GrayFinal-inc.dig as structural Verilog
module GrayFinal_inc (
  input  [1:0] G,
  input  ov,
  input  T,
  input  C,
  output [2:0] G_2,
  output ov_2
);

  wire and_2_out;

  and and_1 (ov_2, ~G[0], ov);  // And
  and and_2 (and_2_out, T, ov_2);
  T_FF #(.generic("this.Label=\"G_\"+args.inBits;")) t_ff_1 (.T(and_2_out), .C(C), .Q(G_2[2]));  // open: nQ

  assign G_2[1:0] = G;

  // Notes on the sheet:
  //   Adds the last bit of the counter to handle 
  //   the overflow correctly.
  //   {{de Ergänzt das letzte Bit des Zählers, um
  //   den Überlauf korrekt umzusetzen.}}
endmodule

/* Code that sets the parameters or builds the circuit:
inBits := 2;
*/
