// Digital circuit GrayNode-inc.dig as structural Verilog
module GrayNode_inc (
  input  [1:0] G,
  input  ov,
  input  T,
  input  C,
  output [3:0] G_2,
  output ov_2
);

  wire and_1_out, and_2_out;
  wire [2:2] grayfinal_inc_1_p1;

  and and_1 (and_1_out, ~G[0], ov);  // And
  and and_2 (and_2_out, G[1], and_1_out, T);
  // GrayFinal_inc #(.generic("export inBits := args.inBits+1; if (args.inBits<args.bits-2) { setCircuit(\"GrayNode-inc.dig\"); }")) grayfinal_inc_1: pin names not known; wires that end beside it: {grayfinal_inc_1_p1[2], G}, and_1_out, T, C, G_2, ov_2
  T_FF #(.generic("this.Label=\"G_\"+args.inBits;")) t_ff_1 (
    .T(and_2_out), .C(C), .Q(grayfinal_inc_1_p1[2]));  // open: nQ

  // Notes on the sheet:
  //   Adds a bit to the counter. The sub circuit 
  //   "GrayFinal" is replaced by "GrayNode" if 
  //   necessary.
  //   {{de Fügt dem Zähler ein Bit hinzu. Die 
  //   Teilschaltung "GrayFinal" wird ersetzt durch 
  //   "GrayNode" wenn die erforderliche Bitzahl 
  //   noch nicht erreicht ist.}}
endmodule

/* Code that sets the parameters or builds the circuit:
bits := 4;
inBits := 2;
*/
