// Digital circuit discrete.dig as structural Verilog
// Implementaion of a single cell of "Conways game of 
// life". This circuit is analyzed to create the truth table
// with 11 inputs and one output. Then the truth table 
// is exported to a hex file, and this hex file is imported
// into a LUT to speedup the cellular automaton.
// {{de Implementierung einer einzelnen Zelle von "Conways game of 
// life". Diese Schaltung wurde analysiert, um eine Wahrheitstabelle mit 11
// Eingängen und einem Ausgang zu erstellen. Diese wurde dann als 
// Hex-Datei exportiert und in eine LUT importiert, um den zellularen 
// Automaten zu beschleunigen.}}
module discrete (
  input  now,
  input  n1,
  input  n2,
  input  n3,
  input  n4,
  input  n5,
  input  n6,
  input  n7,
  input  n8,
  output next
);

  wire and_1_out, and_2_out, comparator_1_eq, comparator_2_eq, not_1_out, or_1_out;
  wire [3:0] bitcount_1_out;

  BitCount #(.Bits(8)) bitcount_1 (.in({n8, n7, n6, n5, n4, n3, n2, n1}), .out(bitcount_1_out));
  Comparator #(.Bits(4)) comparator_1 (.a(4'b0011), .b(bitcount_1_out), .eq(comparator_1_eq));  // open: gt, lt
  Comparator #(.Bits(4)) comparator_2 (.a(4'b0010), .b(bitcount_1_out), .eq(comparator_2_eq));  // open: gt, lt
  or or_1 (or_1_out, comparator_1_eq, comparator_2_eq);
  not not_1 (not_1_out, now);
  and and_1 (and_1_out, not_1_out, comparator_1_eq);
  and and_2 (and_2_out, now, or_1_out);
  or or_2 (next, and_1_out, and_2_out);

  // Notes on the sheet:
  //   now: state of the cell, alive (HIGH) or dead (LOW)
  //   {{de Der aktuelle Zustand der Zelle.}}
  //   next: State of cell in the next generation.
  //   {{de Zustand der Zelle in der nächsten Generation}}
  //   neighbours {{de Nachbarn}}
  //   birth {{de Geburt}}
  //   survive {{de Überleben}}
endmodule
