// Digital circuit genCell.dig as structural Verilog
module genCell (
  input  n1,
  input  n2,
  input  n3,
  input  n4,
  input  n5,
  input  n6,
  input  n7,
  input  n8,
  input  C,
  output O
);

  wire lut_1_next;

  lut lut_1 (.now(O), .n1(n1), .n2(n2), .n3(n3), .n4(n4), .n5(n5), .n6(n6), .n7(n7), .n8(n8), .next(lut_1_next));
  D_FF #(.generic("this.Default=args.default;")) d_ff_1 (.D(lut_1_next), .C(C), .Q(O));  // open: nQ
endmodule

/* Code that sets the parameters or builds the circuit:
default:=1;
*/
