// Digital circuit genAllBitsSet.dig as structural Verilog
module genAllBitsSet (
  input  [1:0] in,
  output out
);

  // And and_1 is placed but not wired
endmodule

/* Code that sets the parameters or builds the circuit:
bits:=5;
*/

/* Code that sets the parameters or builds the circuit:
bits:=4;
*/

/* Code that sets the parameters or builds the circuit:
inputs:=6;
*/

/* Code that sets the parameters or builds the circuit:
if (args.bits<2) {
     panic("needs at least two bits!");
}

y:=args.bits/2;

addWire(4,y,7,0);

o:=0;
for (i:=0;i<args.bits;i++) {
   if ((i=y) & ((args.bits&1)=0)) {
     o=1;
   }

   addWire(-2,i,1,i+o);
}
*/
