// Digital circuit genAllBitsSetTest.dig as structural Verilog
module genAllBitsSetTest (
  input  [3:0] A,
  input  [4:0] B,
  output Y,
  output X
);

  genAllBitsSet #(.generic("bits := 4;")) genallbitsset_1 (.in(A), .out(Y));
  genAllBitsSet #(.generic("bits := 5;")) genallbitsset_2 (.in(B), .out(X));
endmodule

/* Test case:
A B Y X
0 0 0 0
0xf 0xf 1 0
0x1f 0x1f 1 1
*/
