// Digital circuit genAnd.dig as structural Verilog
module genAnd (
);

  // And and_1 is placed but not wired
endmodule

/* Code that sets the parameters or builds the circuit:
inputs:=5;
*/

/* Code that sets the parameters or builds the circuit:
inputs:=8;
*/

/* Code that sets the parameters or builds the circuit:
inputs:=6;
*/

/* Code that sets the parameters or builds the circuit:
y:=args.inputs/2;
out:=addComponent("Out",4,y);
out.Label="Y";
addWire(3,y,4,y);
o:=0;
for (i:=0;i<args.inputs;i++) {
   if ((i=y) & ((args.inputs&1)=0)) {
     o=1;
   }

   in_dx:=-1;
   if ((i&1)=1) in_dx=in_dx-4;

   in:=addComponent("In",in_dx,i+o);
   in.Label="in_"+i;
   addWire(in_dx,i+o,0,i+o);
}
*/
