// Digital circuit genRegTest.dig as structural Verilog
module genRegTest (
  input  C,
  input  [3:0] A,
  input  [1:0] B,
  output [3:0] Y,
  output [1:0] X
);

  // genReg #(.generic("bits := 4;")) genreg_1: pin names not known; wires that end beside it: A, 1'b1, C, Y
  genReg #(.generic("bits := 2;")) genreg_2 (.D(B), .en(1'b1), .C(C), .Q(X));
endmodule

/* Test case:
C A B Y X
0 0 0 0 0
C 1 1 1 1
C 2 2 2 2
C 3 3 3 3
C 5 3 5 3
C 0xf 3 0xf 3
*/
