// Digital circuit col1.dig as structural Verilog
module col1 (
  input  clk
);

  wire [5:0] counter_1_out;
  wire [6:6] graphiccard_1_d;

  Counter #(.Bits(6)) counter_1 (.en(1'b1), .C(clk), .clr(1'b0), .out(counter_1_out));  // open: ovf
  GraphicCard #(.graphicHeight(8), .graphicWidth(8), .Bits(7)) graphiccard_1 (
    .A({1'b0, counter_1_out}), .str(1'b1), .C(clk), .ld(1'b0), .B(1'b0),
    .D({graphiccard_1_d[6], counter_1_out[5], counter_1_out[2], counter_1_out[4:3], counter_1_out[1:0]}));
  // also tied to VCC on the sheet: graphiccard_1_d[6]

  // Notes on the sheet:
  //   clk: Hz: 5000
endmodule
