// Digital circuit col2.dig as structural Verilog
module col2 (
  input  clk
);

  wire [14:0] counter_1_out;
  wire [15:15] graphiccard_1_d;

  Counter #(.Bits(15)) counter_1 (.en(1'b1), .C(clk), .clr(1'b0), .out(counter_1_out));  // open: ovf
  GraphicCard #(.graphicHeight(128), .graphicWidth(256), .Bits(16)) graphiccard_1 (
    .A({1'b0, counter_1_out}), .str(1'b1), .C(clk), .ld(1'b0), .B(1'b0),
    .D({graphiccard_1_d[15], counter_1_out[14:13], counter_1_out[7:5], counter_1_out[12:8], counter_1_out[4:0]}));
  // also tied to VCC on the sheet: graphiccard_1_d[15]

  // Notes on the sheet:
  //   clk: Hz: 5000
endmodule
