// Digital circuit col3.dig as structural Verilog
module col3 (
  input  clk
);

  wire [4:0] counter_1_out;
  wire [5:5] graphiccard_1_d;

  Counter #(.Bits(5)) counter_1 (.en(1'b1), .C(clk), .clr(1'b0), .out(counter_1_out));  // open: ovf
  GraphicCard #(.graphicHeight(4), .graphicWidth(8), .Bits(6)) graphiccard_1 (
    .A({1'b0, counter_1_out}), .str(1'b1), .C(clk), .ld(1'b0), .B(1'b0),
    .D({graphiccard_1_d[5], counter_1_out}));
  // also tied to VCC on the sheet: graphiccard_1_d[5]

  // Notes on the sheet:
  //   clk: Hz: 5000
endmodule
