// Digital circuit calc.dig as structural Verilog
// {{en calculates (a+i*b)^2}}
// {{de berechnet (a+i*b)^2}}
module calc (
  input  [19:0] a,
  input  [19:0] b,
  output [19:0] a_2_b_2,
  output [19:0] _2ab,
  output [19:0] a_2_plus_b_2
);

  wire [19:0] mulfixed_1_p3, mulfixed_2_p3;
  wire [19:19] mulfixed_3_p3;

  // mulFixed mulfixed_1: pin names not known; wires that end beside it: a, a, mulfixed_1_p3
  // mulFixed mulfixed_2: pin names not known; wires that end beside it: b, b, mulfixed_2_p3
  // mulFixed mulfixed_3: pin names not known; wires that end beside it: a, b, {mulfixed_3_p3[19], _2ab[19:1]}
  Sub #(.Bits(20)) sub_1 (.a(mulfixed_1_p3), .b(mulfixed_2_p3), .c_i(1'b0), .s(a_2_b_2));  // open: c_o
  Add #(.Bits(20)) add_1 (.a(mulfixed_1_p3), .b(mulfixed_2_p3), .c_i(1'b0), .s(a_2_plus_b_2));  // open: c_o

  assign _2ab[0] = 1'b0;

  // Notes on the sheet:
  //   a: default 32768
  //   b: default 57344
endmodule
