// Digital circuit coorGen.dig as structural Verilog
// {{de Erzeugt die Koordinaten in der Grafik und die dazu gehörige komplexe Zahl.}}
// {{en Creates the coordinates in the graph and the associated complex number.}}
module coorGen (
  input  en,
  input  clk,
  output [19:0] a,
  output [19:0] b,
  output [8:0] x,
  output [8:0] y,
  output rdy
);

  wire counter_1_ovf;

  Counter #(.Bits(9)) counter_1 (.en(en), .C(clk), .clr(1'b0), .out(x), .ovf(counter_1_ovf));
  Counter #(.Bits(9)) counter_2 (.en(counter_1_ovf), .C(clk), .clr(1'b0), .out(y), .ovf(rdy));
  offset offset_1 (.in(x), .out(a));
  offset offset_2 (.in(y), .out(b));

  // Notes on the sheet:
  //   en: {{en enable}}
  //   {{de enable}}
  //   a: {{en fix point real part}}
  //   {{de Festkomma reller Teil}}
  //   b: {{en fix point imaginary part}}
  //   {{de Festkomma imaginärer Teil}}
  //   x: {{en x-coordinate}}
  //   {{de x-Koordinate}}
  //   y: {{en y-coordinate}}
  //   {{de y-Koordinate}}
  //   rdy: {{en ready}}
  //   {{de fertig}}
endmodule
