// Digital circuit iterate.dig as structural Verilog
// {{de Führt die eigentliche Iteration durch.}}
// {{en Executes the actual iteration.}}
module iterate (
  input  [19:0] a,
  input  [19:0] b,
  input  ld,
  input  clk,
  output div
);

  wire [19:0] a_q, add_1_s, add_2_s, b_q, calc_1__2ab, calc_1_a_2_b_2, calc_1_a_2_plus_b_2,
       multiplexer_1_out, multiplexer_2_out;

  calc calc_1 (.a(a_q), .b(b_q), .a_2_b_2(calc_1_a_2_b_2), ._2ab(calc_1__2ab), .a_2_plus_b_2(calc_1_a_2_plus_b_2));
  Add #(.Bits(20)) add_1 (.a(a), .b(calc_1_a_2_b_2), .c_i(1'b0), .s(add_1_s));  // open: c_o
  Add #(.Bits(20)) add_2 (.a(calc_1__2ab), .b(b), .c_i(1'b0), .s(add_2_s));  // open: c_o
  Comparator #(.Bits(20)) comparator_1 (.a(calc_1_a_2_plus_b_2), .b(20'h10000), .gt(div));  // open: eq, lt
  Multiplexer #(.Bits(20)) multiplexer_1 (.sel(ld), .in_0(add_1_s), .in_1({20{1'b0}}), .out(multiplexer_1_out));
  Multiplexer #(.Bits(20)) multiplexer_2 (.sel(ld), .in_0(add_2_s), .in_1({20{1'b0}}), .out(multiplexer_2_out));
  D_FF #(.Bits(20)) u_a (.D(multiplexer_1_out), .C(clk), .Q(a_q));  // open: nQ
  D_FF #(.Bits(20)) u_b (.D(multiplexer_2_out), .C(clk), .Q(b_q));  // open: nQ
  // Probe a on a_q
  // Probe b on b_q

  // Notes on the sheet:
  //   a: {{en fix point real part}}
  //   {{de Festkomma reller Anteil}}, default 6144
  //   b: {{en fix point imaginary part}}
  //   {{de Festkomma imaginärer Anteil}}, default 2048
  //   div: {{en Number is divergent and does not belong to the mandelbrot set.}}
  //   {{de Zahl ist divergent und gehört damit nicht zur Mandelbrotmenge.}}
  //   ld: {{en new value, initializes flip flops with zero}}
  //   {{de Neuer Wert, initialisiert die Flipflops mit Null.}}
endmodule
