// Digital circuit mandelbrot.dig as structural Verilog
module mandelbrot (
  input  clk
);

  wire coorgen_1_rdy, counter_1_ovf, iterate_1_div, or_1_out;
  wire [5:0] counter_1_out;
  wire [5:5] graphiccard_1_d;
  wire [8:0] coorgen_1_x, coorgen_1_y;
  wire [19:0] coorgen_1_a, coorgen_1_b;

  coorGen coorgen_1 (
    .en(or_1_out), .clk(clk), .a(coorgen_1_a), .b(coorgen_1_b), .x(coorgen_1_x), .y(coorgen_1_y),
    .rdy(coorgen_1_rdy));
  Stop stop_1 (.stop(coorgen_1_rdy));
  Counter #(.Bits(6)) counter_1 (.en(1'b1), .C(clk), .clr(or_1_out), .out(counter_1_out), .ovf(counter_1_ovf));
  iterate iterate_1 (.a(coorgen_1_a), .b(coorgen_1_b), .ld(or_1_out), .clk(clk), .div(iterate_1_div));
  or or_1 (or_1_out, iterate_1_div, counter_1_ovf);
  GraphicCard #(.graphicHeight(512), .graphicWidth(512), .Bits(6)) graphiccard_1 (
    .A({1'b0, coorgen_1_y, coorgen_1_x}), .str(or_1_out), .C(clk), .ld(1'b0), .B(1'b0),
    .D({graphiccard_1_d[5], counter_1_out[5:1]}));
  // also tied to VCC on the sheet: graphiccard_1_d[5]

  // Notes on the sheet:
  //   clk: Hz: 2147483647
  //   {{en Calculates the Mandelbrot set}}
  //   {{de Berechnet die Mandelbrot-Menge}}
endmodule
