// Digital circuit mulFixed.dig as structural Verilog
module mulFixed (
  input  [19:0] a,
  input  [19:0] b,
  output [19:0] p
);

  wire [39:0] mul_1_mul;

  Mul #(.Signed("true"), .Bits(20)) mul_1 (.a(a), .b(b), .mul({mul_1_mul[39:34], p, mul_1_mul[13:0]}));
endmodule
