// Digital circuit offset.dig as structural Verilog
// {{de Erzeugt aus einer Koordinate die zugehörige Festkommazahl.}}
// {{en Generates the corresponding fixed point number from a coordinate.}}
module offset (
  input  [8:0] in,
  output [19:0] out
);

  wire [8:0] sub_1_s;
  wire [16:16] sub_1_c_o;

  Sub #(.Bits(9)) sub_1 (.a(in), .b(9'h100), .c_i(1'b0), .s(sub_1_s), .c_o(sub_1_c_o[16]));
  BitExtender #(.inputBits(17), .outputBits(20)) bitextender_1 (.in({sub_1_c_o[16], sub_1_s, {7{1'b0}}}), .out(out));
endmodule
