// Digital circuit Hazard.dig as structural Verilog
module Hazard (
  input  In,
  output Out
);

  wire delay_1_out, xor_1_out;

  Delay delay_1 (.in(In), .out(delay_1_out));
  xor xor_1 (xor_1_out, delay_1_out, In);
  xor xor_2 (Out, xor_1_out, In);
endmodule
