// Digital circuit BASYS3_lightchase.dig as structural Verilog
module BASYS3_lightchase (
  input  Clock,
  output LED0,
  output LED1,
  output LED2,
  output LED3,
  output LED4,
  output LED5,
  output LED6,
  output LED7,
  output LED8,
  output LED9,
  output LED10,
  output LED11,
  output LED12,
  output LED13,
  output LED14,
  output LED15
);

  wire jk_ff_1_q;
  wire [3:0] add_1_s, d_ff_1_q, multiplexer_1_out;

  Multiplexer #(.Bits(4)) multiplexer_1 (.sel(jk_ff_1_q), .in_0(4'b0001), .in_1(4'b1111), .out(multiplexer_1_out));
  Add #(.Bits(4)) add_1 (.a(d_ff_1_q), .b(multiplexer_1_out), .c_i(1'b0), .s(add_1_s));  // open: c_o
  D_FF #(.Bits(4)) d_ff_1 (.D(add_1_s), .C(Clock), .Q(d_ff_1_q));  // open: nQ
  Decoder #(.Selector_Bits(4)) decoder_1 (
    .sel(d_ff_1_q), .out_0(LED0), .out_1(LED1), .out_2(LED2), .out_3(LED3), .out_4(LED4), .out_5(LED5),
    .out_6(LED6), .out_7(LED7), .out_8(LED8), .out_9(LED9), .out_10(LED10), .out_11(LED11), .out_12(LED12),
    .out_13(LED13), .out_14(LED14), .out_15(LED15));
  JK_FF jk_ff_1 (.J(LED14), .C(Clock), .K(LED1), .Q(jk_ff_1_q));  // open: nQ

  // Notes on the sheet:
  //   LED0: pin U16
  //   LED1: pin E19
  //   LED2: pin U19
  //   LED3: pin V19
  //   LED4: pin W18
  //   LED5: pin U15
  //   LED6: pin U14
  //   LED7: pin V14
  //   LED8: pin V13
  //   LED9: pin V3
  //   LED10: pin W3
  //   LED11: pin U3
  //   LED12: pin P3
  //   LED13: pin N3
  //   LED14: pin P1
  //   LED15: pin L1
  //   Clock: pin W5, Hz: 50
  //   Export this file to VHDL and use Xilinx Vivado to create the bitstream.
  //   Also add the created constraints file to the vivado project to assign
  //   the pins correctly.
  //   {{de Exportieren Sie diese Datei zu VHDL und verwenden Sie Xilinx Vivado, 
  //   um den Bitstream zu erstellen.
  //   Fügen Sie auch die erstellte Constraint-Datei dem Vivado-Projekt hinzu, um 
  //   die Pins korrekt zuzuordnen.}}
  //   Board: BASYS3
endmodule

/* Test case:
Clock LED15 LED14 LED13 LED12 LED11 LED10 LED9 LED8 LED7 LED6 LED5 LED4 LED3 LED2 LED1 LED0
 0  bits(16,1)
repeat(14) C bits(16,1<<n+1)
repeat(15) C bits(16,1<<15-n)
repeat(16) C bits(16,1<<n)
*/
