// Digital circuit 74273.dig as structural Verilog
// 74273 8-bit Register with Clear
module _74273 (
  input  CP,
  input  MR,
  input  D0,
  input  D1,
  input  D2,
  input  D3,
  input  D4,
  input  D5,
  input  D6,
  input  D7,
  input  GND,
  input  VCC,
  output Q0,
  output Q1,
  output Q2,
  output Q3,
  output Q4,
  output Q5,
  output Q6,
  output Q7
);

  wire not_1_out, not_2_out, pulldown_1_out, pulldown_2_out, pulldown_3_out, pulldown_4_out, pulldown_5_out,
       pulldown_6_out, pulldown_7_out, pulldown_8_out;

  not not_1 (not_1_out, CP);
  not not_2 (not_2_out, MR);
  PullDown pulldown_1 (.out(pulldown_1_out));
  D_FF_AS d_ff_as_1 (.Set(pulldown_1_out), .D(D0), .C(not_1_out), .Clr(not_2_out), .Q(Q0));  // open: nQ
  PullDown pulldown_2 (.out(pulldown_2_out));
  D_FF_AS d_ff_as_2 (.Set(pulldown_2_out), .D(D1), .C(not_1_out), .Clr(not_2_out), .Q(Q1));  // open: nQ
  PullDown pulldown_3 (.out(pulldown_3_out));
  D_FF_AS d_ff_as_3 (.Set(pulldown_3_out), .D(D2), .C(not_1_out), .Clr(not_2_out), .Q(Q2));  // open: nQ
  PullDown pulldown_4 (.out(pulldown_4_out));
  D_FF_AS d_ff_as_4 (.Set(pulldown_4_out), .D(D3), .C(not_1_out), .Clr(not_2_out), .Q(Q3));  // open: nQ
  PullDown pulldown_5 (.out(pulldown_5_out));
  D_FF_AS d_ff_as_5 (.Set(pulldown_5_out), .D(D4), .C(not_1_out), .Clr(not_2_out), .Q(Q4));  // open: nQ
  PullDown pulldown_6 (.out(pulldown_6_out));
  D_FF_AS d_ff_as_6 (.Set(pulldown_6_out), .D(D5), .C(not_1_out), .Clr(not_2_out), .Q(Q5));  // open: nQ
  PullDown pulldown_7 (.out(pulldown_7_out));
  D_FF_AS d_ff_as_7 (.Set(pulldown_7_out), .D(D6), .C(not_1_out), .Clr(not_2_out), .Q(Q6));  // open: nQ
  PullDown pulldown_8 (.out(pulldown_8_out));
  D_FF_AS d_ff_as_8 (.Set(pulldown_8_out), .D(D7), .C(not_1_out), .Clr(not_2_out), .Q(Q7));  // open: nQ
  PowerSupply powersupply_1 (.VDD(VCC), .GND(GND));

  // Notes on the sheet:
  //   CP: pin 11
  //   MR: pin 1
  //   D0: pin 3
  //   D1: pin 4
  //   D2: pin 7
  //   D3: pin 8
  //   D4: pin 13
  //   D5: pin 14
  //   D6: pin 17
  //   D7: pin 18
  //   GND: pin 10
  //   VCC: pin 20
  //   Q0: pin 2
  //   Q1: pin 5
  //   Q2: pin 6
  //   Q3: pin 9
  //   Q4: pin 12
  //   Q5: pin 15
  //   Q6: pin 16
  //   Q7: pin 19
endmodule
