// Digital circuit 74147.dig as structural Verilog
// 10-line to 4-line priority encoder
module _74147 (
  input  I9,
  input  I8,
  input  I7,
  input  I6,
  input  I5,
  input  I4,
  input  I3,
  input  I2,
  input  I1,
  input  VCC,
  input  GND,
  output A,
  output B,
  output C,
  output D
);

  wire and_1_out, and_2_out, and_3_out, and_4_out, and_5_out, and_6_out, and_7_out, and_8_out, and_9_out,
       not_1_out, not_2_out, not_3_out, not_4_out, not_5_out, not_6_out;

  not not_1 (not_1_out, I9);
  not not_2 (not_2_out, I8);
  not not_3 (not_3_out, I6);
  not not_4 (not_4_out, I5);
  not not_5 (not_5_out, I4);
  not not_6 (not_6_out, I2);
  and and_1 (and_1_out, I1, I3, I5, I7, I9);
  and and_2 (and_2_out, not_6_out, I3, I5, I7, I9);
  and and_3 (and_3_out, not_5_out, I5, I7, I9);
  and and_4 (and_4_out, not_3_out, I7, I9);
  and and_5 (and_5_out, not_2_out, I9);
  and and_6 (and_6_out, I2, I3, I6, I7);
  and and_7 (and_7_out, not_5_out, I6, I7);
  and and_8 (and_8_out, not_4_out, I6, I7);
  and and_9 (and_9_out, I4, I5, I6, I7);
  and and_10 (D, I8, I9);
  or or_1 (A, and_1_out, and_2_out, and_3_out, and_4_out, and_5_out);
  or or_2 (B, and_6_out, and_7_out, and_8_out, not_2_out, not_1_out);
  or or_3 (C, and_9_out, not_2_out, not_1_out);
  PowerSupply powersupply_1 (.VDD(VCC), .GND(GND));

  // Notes on the sheet:
  //   I9: pin 10
  //   I8: pin 5
  //   I7: pin 4
  //   I6: pin 3
  //   I5: pin 2
  //   I4: pin 1
  //   I3: pin 13
  //   I2: pin 12
  //   I1: pin 11
  //   A: pin 9
  //   B: pin 7
  //   C: pin 6
  //   D: pin 14
  //   VCC: pin 16, default 1
  //   GND: pin 8
endmodule

/* Test case:
I1 I2 I3 I4 I5 I6 I7 I8 I9   D C B A
1  1  1  1  1  1  1  1  1    1 1 1 1
x  x  x  x  x  x  x  x  0    0 1 1 0
x  x  x  x  x  x  x  0  1    0 1 1 1
x  x  x  x  x  x  0  1  1    1 0 0 0
x  x  x  x  x  0  1  1  1    1 0 0 1
x  x  x  x  0  1  1  1  1    1 0 1 0
x  x  x  0  1  1  1  1  1    1 0 1 1
x  x  0  1  1  1  1  1  1    1 1 0 0
x  0  1  1  1  1  1  1  1    1 1 0 1
0  1  1  1  1  1  1  1  1    1 1 1 0
*/
