// Digital circuit 74182.dig as structural Verilog
// look-ahead carry generator
module _74182 (
  input  C_n,
  input  nG0,
  input  nP0,
  input  nG1,
  input  nP1,
  input  nG2,
  input  nP2,
  input  nG3,
  input  nP3,
  input  VCC,
  input  GND,
  output nP,
  output nG,
  output C_n__plus__z,
  output C_n__plus__y,
  output C_n__plus__x
);

  wire and_1_out, and_2_out, and_3_out, and_4_out, and_5_out, and_6_out, and_7_out, and_8_out, and_9_out,
       and_10_out, and_11_out, and_12_out, and_13_out, not_1_out;

  PowerSupply powersupply_1 (.VDD(VCC), .GND(GND));
  not not_1 (not_1_out, C_n);
  or or_1 (nP, nP0, nP1, nP2, nP3);
  and and_1 (and_1_out, nG0, nG1, nG2, nG3);
  and and_2 (and_2_out, nP1, nG3, nG2, nG1);
  and and_3 (and_3_out, nP2, nG3, nG2);
  and and_4 (and_4_out, nP3, nG3);
  and and_5 (and_5_out, nG2, nG1, nG0, not_1_out);
  and and_6 (and_6_out, nP0, nG2, nG1, nG0);
  and and_7 (and_7_out, nP1, nG2, nG1);
  and and_8 (and_8_out, nP2, nG2);
  and and_9 (and_9_out, nG1, nG0, not_1_out);
  and and_10 (and_10_out, nP0, nG1, nG0);
  and and_11 (and_11_out, nP1, nG1);
  and and_12 (and_12_out, nG0, not_1_out);
  and and_13 (and_13_out, nP0, nG0);
  or or_2 (nG, and_1_out, and_2_out, and_3_out, and_4_out);
  nor nor_1 (C_n__plus__z, and_5_out, and_6_out, and_7_out, and_8_out);
  nor nor_2 (C_n__plus__y, and_9_out, and_10_out, and_11_out);
  nor nor_3 (C_n__plus__x, and_12_out, and_13_out);

  // Notes on the sheet:
  //   C_n: pin 13
  //   nG0: pin 3
  //   nP0: pin 4
  //   nG1: pin 1
  //   nP1: pin 2
  //   nG2: pin 14
  //   nP2: pin 15
  //   nG3: pin 5
  //   nP3: pin 6
  //   nP: pin 7
  //   nG: pin 10
  //   C_n__plus__z: pin 9
  //   C_n__plus__y: pin 11
  //   C_n__plus__x: pin 12
  //   VCC: pin 16, default 1
  //   GND: pin 8
endmodule

/* Test case:
C_n ~G0 ~P0 ~G1 ~P1 ~G2 ~P2 ~G3 ~P3 C_n_+_x C_n_+_y C_n_+_z ~G ~P
#
X   1   1   X   X   X   X   X   X   0       X       X       X  X
0   1   X   X   X   X   X   X   X   0       X       X       X  X
X   0   X   X   X   X   X   X   X   1       X       X       X  X
1   X   0   X   X   X   X   X   X   1       X       X       X  X
#
X   X   X   1   1   X   X   X   X   X       0       X       X  X
X   1   1   1   X   X   X   X   X   X       0       X       X  X
0   1   X   1   X   X   X   X   X   X       0       X       X  X
X   X   X   0   X   X   X   X   X   X       1       X       X  X
X   0   X   X   0   X   X   X   X   X       1       X       X  X
1   X   0   X   0   X   X   X   X   X       1       X       X  X
#
X   X   X   X   X   1   1   X   X   X       X       0       X  X
X   X   X   1   1   1   X   X   X   X       X       0       X  X
X   1   1   1   X   1   X   X   X   X       X       0       X  X
0   1   X   1   X   1   X   X   X   X       X       0       X  X
X   X   X   X   X   0   X   X   X   X       X       1       X  X
X   X   X   0   X   X   0   X   X   X       X       1       X  X
X   0   X   X   0   X   0   X   X   X       X       1       X  X
1   X   0   X   0   X   0   X   X   X       X       1       X  X
#
X   X   X   X   X   X   X   1   1   X       X       X       1  X
X   X   X   X   X   1   1   1   X   X       X       X       1  X
X   X   X   1   1   1   X   1   X   X       X       X       1  X
X   1   X   1   X   1   X   1   X   X       X       X       1  X
X   X   X   X   X   X   X   0   X   X       X       X       0  X
X   X   X   X   X   0   X   X   0   X       X       X       0  X
X   X   X   0   X   X   0   X   0   X       X       X       0  X
X   0   X   X   0   X   0   X   0   X       X       X       0  X
#
X   X   1   X   X   X   X   X   X   X       X       X       X  1
X   X   X   X   1   X   X   X   X   X       X       X       X  1
X   X   X   X   X   X   1   X   X   X       X       X       X  1
X   X   X   X   X   X   X   X   1   X       X       X       X  1
X   X   0   X   0   X   0   X   0   X       X       X       X  0
*/
