// Digital circuit 74688.dig as structural Verilog
// 8-bit identity comparator
module _74688 (
  input  P_0,
  input  Q_0,
  input  P_1,
  input  Q_1,
  input  P_2,
  input  Q_2,
  input  P_3,
  input  Q_3,
  input  P_4,
  input  Q_4,
  input  P_5,
  input  Q_5,
  input  P_6,
  input  Q_6,
  input  P_7,
  input  Q_7,
  input  nOE,
  input  VCC,
  input  GND,
  output nEQ
);

  wire nor_1_out, nor_2_out, nor_3_out, xor_1_out, xor_2_out, xor_3_out, xor_4_out, xor_5_out, xor_6_out,
       xor_7_out, xor_8_out;

  xor xor_1 (xor_1_out, P_0, Q_0);
  xor xor_2 (xor_2_out, P_1, Q_1);
  xor xor_3 (xor_3_out, P_2, Q_2);
  xor xor_4 (xor_4_out, P_3, Q_3);
  xor xor_5 (xor_5_out, P_4, Q_4);
  xor xor_6 (xor_6_out, P_5, Q_5);
  xor xor_7 (xor_7_out, P_6, Q_6);
  xor xor_8 (xor_8_out, P_7, Q_7);
  PowerSupply powersupply_1 (.VDD(VCC), .GND(GND));
  nor nor_1 (nor_1_out, xor_1_out, xor_2_out, xor_3_out);
  nor nor_2 (nor_2_out, xor_4_out, xor_5_out, xor_6_out);
  nor nor_3 (nor_3_out, xor_7_out, xor_8_out);
  nand nand_1 (nEQ, ~nOE, nor_1_out, nor_2_out, nor_3_out);  // NAnd

  // Notes on the sheet:
  //   P_0: pin 2
  //   Q_0: pin 3
  //   P_1: pin 4
  //   Q_1: pin 5
  //   P_2: pin 6
  //   Q_2: pin 7
  //   P_3: pin 8
  //   Q_3: pin 9
  //   P_4: pin 11
  //   Q_4: pin 12
  //   P_5: pin 13
  //   Q_5: pin 14
  //   P_6: pin 15
  //   Q_6: pin 16
  //   P_7: pin 17
  //   Q_7: pin 18
  //   nOE: pin 1
  //   nEQ: pin 19
  //   VCC: pin 20, default 1
  //   GND: pin 10
endmodule

/* Test case:
~OE P_7 P_6 P_5 P_4 P_3 P_2 P_1 P_0 Q_7 Q_6 Q_5 Q_4 Q_3 Q_2 Q_1 Q_0 ~EQ
loop(P,16)
loop(Q,16)
0 bits(8,P) bits(8,Q) (~(P=Q))
1 bits(8,P) bits(8,Q) (1)
end loop
end loop
*/
