// Digital circuit 7480.dig as structural Verilog
// Gated Full Adder with Complementary Inputs
// and Complementary Sum Outputs
module _7480 (
  input  A1,
  input  A2,
  input  AC,
  input  A,
  input  B1,
  input  B2,
  input  BC,
  input  B,
  input  Cn,
  input  VCC,
  input  GND,
  output nCn_plus_1,
  output S,
  output nS
);

  wire and_1_out, and_2_out, and_3_out, and_4_out, or_1_out, or_2_out, xor_1_out;

  PowerSupply powersupply_1 (.VDD(VCC), .GND(GND));
  and and_1 (and_1_out, A1, A2);
  and and_2 (and_2_out, B1, B2);
  or or_1 (or_1_out, and_1_out, ~AC, ~A);  // Or
  or or_2 (or_2_out, and_2_out, ~BC, ~B);  // Or
  and and_3 (and_3_out, or_1_out, or_2_out);
  xor xor_1 (xor_1_out, or_1_out, or_2_out);
  and and_4 (and_4_out, xor_1_out, Cn);
  xor xor_2 (S, xor_1_out, Cn);
  nor nor_1 (nCn_plus_1, and_3_out, and_4_out);
  not not_1 (nS, S);

  // Notes on the sheet:
  //   A1: pin 8
  //   A2: pin 9
  //   AC: pin 11
  //   A: pin 10
  //   B1: pin 12
  //   B2: pin 13
  //   BC: pin 2
  //   B: pin 1
  //   Cn: Übertragsbit der Vorgängerschaltung., pin 3
  //   nCn_plus_1: Übertragsbit, pin 4
  //   S: Summe, pin 6
  //   nS: Summe, pin 5
  //   VCC: pin 14, default 1
  //   GND: pin 7
endmodule

/* Test case:
B* A* Cn AC BC ~Cn+1 S ~S
1  1  0  1  1  1     0  1
1  1  0  1  0  1     1  0
1  1  0  0  1  1     1  0
1  1  0  0  0  0     0  1
1  1  1  1  1  1     1  0
1  1  1  1  0  0     0  1
1  1  1  0  1  0     0  1
1  1  1  0  0  0     1  0
*/
