// Digital circuit 7483.dig as structural Verilog
// 4-bit binary full adder
module _7483 (
  input  C0,
  input  B1,
  input  B2,
  input  B3,
  input  B4,
  input  A1,
  input  A2,
  input  A3,
  input  A4,
  input  VCC,
  input  GND,
  output S1,
  output S2,
  output S3,
  output S4,
  output C4
);

  PowerSupply powersupply_1 (.VDD(VCC), .GND(GND));
  Add #(.Bits(4)) add_1 (.a({A4, A3, A2, A1}), .b({B4, B3, B2, B1}), .c_i(C0), .s({S4, S3, S2, S1}), .c_o(C4));

  // Notes on the sheet:
  //   C0: Der Übetrag vom Addierer welcher die 
  //   niederwertigeren Bits addiert. Werden die 
  //   niederwertigsten Bits addiert, ist dieser Eingang 
  //   Null., pin 13
  //   B1: Das 0. Bit des ersten zu addierenden Wertes., pin 11
  //   B2: Das 1. Bit des ersten zu addierenden Wertes., pin 7
  //   S1: Das 0. Bit der Summe., pin 9
  //   B3: Das 2. Bit des ersten zu addierenden Wertes., pin 4
  //   B4: Das 3. Bit des ersten zu addierenden Wertes., pin 16
  //   S2: Das 1. Bit der Summe., pin 6
  //   S3: Das 2. Bit der Summe., pin 2
  //   A1: Das 0. Bit des zweiten zu addierenden Wertes., pin 10
  //   A2: Das 1. Bit des zweiten zu addierenden Wertes., pin 8
  //   A3: Das 2. Bit des zweiten zu addierenden Wertes., pin 3
  //   A4: Das 3. Bit des zweiten zu addierenden Wertes., pin 1
  //   S4: Das 3. Bit der Summe., pin 15
  //   C4: Das Übertragsbit, welches an den Adiierer für die
  //   nächst höherwertigen Bits weitergegeben wird., pin 14
  //   VCC: pin 5, default 1
  //   GND: pin 12
endmodule

/* Test case:
# A complete test of all 512 possible additions
#
# A line that begins with "repeat([i])" is repeated [i] times.
# In this case 256 times. Then the variable n goes from 0 to 255.
# So the values for the inputs are calculated depending on n.
# The function "bits([m],[v])" takes the lowest m bits from the value v.
# The expression "bits(4,n>>4)" takes the lowest 4 bits of the value
# n>>4. Then the resulting bits are used for the inputs A_3 to A_0.
# All created test vectors are shown in the result table.

             C0   A4 A3 A2 A1   B4 B3 B2 B1  C4 S4 S3 S2 S1
repeat(256)  0    bits(4,n>>4)  bits(4,n)    bits(5,(n>>4)+(n&15))
repeat(256)  1    bits(4,n>>4)  bits(4,n)    bits(5,(n>>4)+(n&15)+1)
*/
