// Digital circuit 7409.dig as structural Verilog
// quad 2-input AND gate with open-collector outputs
module _7409 (
  input  _1A,
  input  _1B,
  input  _2A,
  input  _2B,
  input  _3B,
  input  _3A,
  input  _4A,
  input  _4B,
  input  VCC,
  input  GND,
  output _1Y,
  output _2Y,
  output _3Y,
  output _4Y
);

  wire nand_1_out, nand_2_out, nand_3_out, nand_4_out;

  nand nand_1 (nand_1_out, _1A, _1B);
  nand nand_2 (nand_2_out, _2A, _2B);
  nand nand_3 (nand_3_out, _3A, _3B);
  nand nand_4 (nand_4_out, _4A, _4B);
  PowerSupply powersupply_1 (.VDD(VCC), .GND(GND));
  NFET nfet_1 (.G(nand_1_out), .D(_1Y), .S(1'b0));
  NFET nfet_2 (.G(nand_2_out), .D(_2Y), .S(1'b0));
  NFET nfet_3 (.G(nand_3_out), .D(_3Y), .S(1'b0));
  NFET nfet_4 (.G(nand_4_out), .D(_4Y), .S(1'b0));

  // Notes on the sheet:
  //   _1A: pin 1
  //   _1B: pin 2
  //   _1Y: pin 3
  //   _2A: pin 4
  //   _2B: pin 5
  //   _2Y: pin 6
  //   _3B: pin 10
  //   _3A: pin 9
  //   _3Y: pin 8
  //   _4A: pin 12
  //   _4B: pin 13
  //   _4Y: pin 11
  //   VCC: pin 14, default 1
  //   GND: pin 7
endmodule
