// Digital circuit 7428.dig as structural Verilog
module _7428 (
  input  _3A,
  input  _3B,
  input  _4A,
  input  _4B,
  input  _1B,
  input  _1A,
  input  _2B,
  input  _2A,
  input  VCC,
  input  GND,
  output _1Y,
  output _2Y,
  output _3Y,
  output _4Y
);

  PowerSupply powersupply_1 (.VDD(VCC), .GND(GND));
  nor nor_1 (_1Y, _1A, _1B);
  nor nor_2 (_4Y, _4B, _4A);
  nor nor_3 (_2Y, _2A, _2B);
  nor nor_4 (_3Y, _3B, _3A);

  // Notes on the sheet:
  //   _1Y: pin 1
  //   _2Y: pin 4
  //   _3Y: pin 10
  //   _4Y: pin 13
  //   _3A: pin 9
  //   _3B: pin 8
  //   _4A: pin 12
  //   _4B: pin 11
  //   _1B: pin 3
  //   _1A: pin 2
  //   _2B: pin 6
  //   _2A: pin 5
  //   VCC: pin 14, default 1
  //   GND: pin 7
endmodule
