// Digital circuit 7430.dig as structural Verilog
// 8-input NAND gate
module _7430 (
  input  _1A,
  input  _1C,
  input  _1B,
  input  _1D,
  input  _1E,
  input  _1G,
  input  _1F,
  input  _1H,
  input  VCC,
  input  GND,
  output _1Y
);

  nand nand_1 (_1Y, _1A, _1B, _1C, _1D, _1E, _1F, _1G, _1H);
  PowerSupply powersupply_1 (.VDD(VCC), .GND(GND));

  // Notes on the sheet:
  //   _1A: pin 1
  //   _1C: pin 3
  //   _1Y: pin 8
  //   _1B: pin 2
  //   _1D: pin 4
  //   _1E: pin 5
  //   _1G: pin 11
  //   _1F: pin 6
  //   _1H: pin 12
  //   VCC: pin 14, default 1
  //   GND: pin 7
endmodule
