// Digital circuit 7440.dig as structural Verilog
module _7440 (
  input  _1A,
  input  _1B,
  input  NC,
  input  _1C,
  input  _1D,
  input  VCC,
  input  GND,
  input  _2A,
  input  _2B,
  input  _2C,
  input  NC_2,
  input  _2D,
  output _2Y,
  output _1Y
);

  nand nand_1 (_2Y, _2A, _2B, _2C, _2D);
  nand nand_2 (_1Y, _1A, _1B, _1C, _1D);
  PowerSupply powersupply_1 (.VDD(VCC), .GND(GND));

  // Notes on the sheet:
  //   _1A: pin 1
  //   _1B: pin 2
  //   _2Y: pin 8
  //   _1Y: pin 6
  //   NC: pin 3
  //   _1C: pin 4
  //   _1D: pin 5
  //   VCC: pin 14, default 1
  //   GND: pin 7
  //   _2A: pin 9
  //   _2B: pin 10
  //   _2C: pin 12
  //   NC_2: pin 11
  //   _2D: pin 13
endmodule
