// Digital circuit 7454.dig as structural Verilog
// 2-3-2-3-line AND NOR gate
module _7454 (
  input  _1A,
  input  _1B,
  input  _3A,
  input  _3B,
  input  _2A,
  input  _2C,
  input  _2B,
  input  _4A,
  input  _4C,
  input  _4B,
  input  VCC,
  input  GND,
  output Y
);

  wire and_1_out, and_2_out, and_3_out, and_4_out;

  and and_1 (and_1_out, _1A, _1B);
  and and_2 (and_2_out, _2A, _2B, _2C);
  and and_3 (and_3_out, _3A, _3B);
  and and_4 (and_4_out, _4A, _4B, _4C);
  PowerSupply powersupply_1 (.VDD(VCC), .GND(GND));
  nor nor_1 (Y, and_1_out, and_2_out, and_3_out, and_4_out);

  // Notes on the sheet:
  //   Y: pin 6
  //   _1A: pin 1
  //   _1B: pin 2
  //   _3A: pin 13
  //   _3B: pin 12
  //   _2A: pin 3
  //   _2C: pin 5
  //   _2B: pin 4
  //   _4A: pin 9
  //   _4C: pin 11
  //   _4B: pin 10
  //   VCC: pin 14, default 1
  //   GND: pin 7
endmodule
