// Digital circuit 7458.dig as structural Verilog
// dual AND OR gate
module _7458 (
  input  _1A,
  input  _1B,
  input  _1C,
  input  _1D,
  input  _2D,
  input  _2F,
  input  _2E,
  input  _2A,
  input  _2C,
  input  _2B,
  input  VCC,
  input  GND,
  output _1Y,
  output _2Y
);

  wire and_1_out, and_2_out, and_3_out, and_4_out;

  and and_1 (and_1_out, _1A, _1B);
  and and_2 (and_2_out, _1C, _1D);
  and and_3 (and_3_out, _2A, _2B, _2C);
  and and_4 (and_4_out, _2D, _2E, _2F);
  PowerSupply powersupply_1 (.VDD(VCC), .GND(GND));
  or or_1 (_1Y, and_1_out, and_2_out);
  or or_2 (_2Y, and_3_out, and_4_out);

  // Notes on the sheet:
  //   _1Y: pin 6
  //   _1A: pin 2
  //   _1B: pin 3
  //   _1C: pin 4
  //   _1D: pin 5
  //   _2D: pin 11
  //   _2F: pin 9
  //   _2E: pin 10
  //   _2A: pin 1
  //   _2C: pin 12
  //   _2B: pin 13
  //   _2Y: pin 8
  //   VCC: pin 14, default 1
  //   GND: pin 7
endmodule
