// Digital circuit 74161.dig as structural Verilog
// hex synchronous counter, async clear
module _74161 (
  input  nLD,
  input  nCLR,
  input  CLK,
  input  ENT,
  input  ENP,
  input  A,
  input  B,
  input  C,
  input  D,
  input  VCC,
  input  GND,
  output RCO,
  output QA,
  output QB,
  output QC,
  output QD
);

  wire add_1_c_o, and_1_out, not_1_out;
  wire [3:0] add_1_s, multiplexer_1_out, multiplexer_2_out;

  Add #(.Bits(4)) add_1 (.a({QD, QC, QB, QA}), .b(4'b0001), .c_i(1'b0), .s(add_1_s), .c_o(add_1_c_o));
  and and_1 (and_1_out, ENP, ENT);
  PowerSupply powersupply_1 (.VDD(VCC), .GND(GND));
  Multiplexer #(.Bits(4)) multiplexer_1 (
    .sel(and_1_out), .in_0({QD, QC, QB, QA}), .in_1(add_1_s), .out(multiplexer_1_out));
  Multiplexer #(.Bits(4)) multiplexer_2 (
    .sel(nLD), .in_0({D, C, B, A}), .in_1(multiplexer_1_out), .out(multiplexer_2_out));
  D_FF_AS #(.Bits(4)) d_ff_as_1 (
    .Set(1'b0), .D(multiplexer_2_out), .C(CLK), .Clr(not_1_out), .Q({QD, QC, QB, QA}));  // open: nQ
  not not_1 (not_1_out, nCLR);
  and and_2 (RCO, add_1_c_o, ENT);

  // Notes on the sheet:
  //   nLD: pin 9
  //   nCLR: pin 1
  //   CLK: pin 2
  //   RCO: pin 15
  //   ENT: pin 10
  //   ENP: pin 7
  //   A: pin 3
  //   B: pin 4
  //   C: pin 5
  //   D: pin 6
  //   QA: pin 14
  //   QB: pin 13
  //   QC: pin 12
  //   QD: pin 11
  //   VCC: pin 16, default 1
  //   GND: pin 8
endmodule
