// Digital circuit 74162Real.dig as structural Verilog
// presettable synchronous BCD decade
// counter, synchronous reset
module _74162Real (
  input  nMR,
  input  nPE,
  input  D_0,
  input  D_1,
  input  D_2,
  input  D_3,
  input  CET,
  input  CEP,
  input  CP,
  input  VCC,
  input  GND,
  output Q_0,
  output Q_1,
  output Q_2,
  output Q_3,
  output TC
);

  wire and_1_out, and_2_out, and_3_out, and_4_out, and_5_out, and_6_out, and_7_out, and_8_out, and_9_out,
       d_ff_1_nq, d_ff_2_nq, d_ff_3_nq, d_ff_4_nq, nand_1_out, nor_1_out, nor_2_out, nor_3_out, nor_4_out,
       nor_5_out, nor_6_out, nor_7_out, nor_8_out, not_1_out, not_2_out, or_1_out, or_2_out, or_3_out,
       or_4_out, or_5_out, xnor_1_out, xnor_2_out, xnor_3_out;

  PowerSupply powersupply_1 (.VDD(VCC), .GND(GND));
  nand nand_1 (nand_1_out, CET, CEP);
  nor nor_1 (nor_1_out, nPE, not_1_out);
  not not_1 (not_1_out, nMR);
  nor nor_2 (nor_2_out, nor_1_out, not_1_out);
  not not_2 (not_2_out, nand_1_out);
  xnor xnor_1 (xnor_1_out, d_ff_1_nq, not_2_out);
  and and_1 (and_1_out, nor_1_out, D_0);
  or or_1 (or_1_out, and_2_out, and_1_out);
  D_FF d_ff_1 (.D(or_1_out), .C(CP), .Q(Q_0), .nQ(d_ff_1_nq));
  and and_2 (and_2_out, nor_2_out, xnor_1_out);
  nor nor_3 (nor_3_out, Q_3, nand_1_out, d_ff_1_nq);
  and and_3 (and_3_out, nor_1_out, D_1);
  or or_2 (or_2_out, and_4_out, and_3_out);
  D_FF d_ff_2 (.D(or_2_out), .C(CP), .Q(Q_1), .nQ(d_ff_2_nq));
  xnor xnor_2 (xnor_2_out, d_ff_2_nq, nor_3_out);
  and and_4 (and_4_out, nor_2_out, xnor_2_out);
  and and_5 (and_5_out, nor_1_out, D_2);
  nor nor_4 (nor_4_out, d_ff_1_nq, d_ff_2_nq, nand_1_out);
  xnor xnor_3 (xnor_3_out, d_ff_3_nq, nor_4_out);
  and and_6 (and_6_out, nor_2_out, xnor_3_out);
  or or_3 (or_3_out, and_6_out, and_5_out);
  D_FF d_ff_3 (.D(or_3_out), .C(CP), .Q(Q_2), .nQ(d_ff_3_nq));
  and and_7 (and_7_out, nor_1_out, D_3);
  nor nor_5 (nor_5_out, d_ff_1_nq, d_ff_2_nq, d_ff_3_nq, nand_1_out);
  and and_8 (and_8_out, d_ff_4_nq, nor_5_out);
  and and_9 (and_9_out, or_5_out, nor_2_out);
  or or_4 (or_4_out, and_9_out, and_7_out);
  D_FF d_ff_4 (.D(or_4_out), .C(CP), .Q(Q_3), .nQ(d_ff_4_nq));
  nor nor_6 (nor_6_out, nor_8_out, nand_1_out);
  nor nor_7 (nor_7_out, nor_6_out, d_ff_4_nq);
  or or_5 (or_5_out, nor_7_out, and_8_out);
  nor nor_8 (nor_8_out, d_ff_4_nq, Q_0);
  and and_10 (TC, CET, Q_0, d_ff_2_nq, d_ff_3_nq, Q_3);

  // Notes on the sheet:
  //   Q_0: flip-flop outputs, pin 14
  //   Q_1: flip-flop outputs, pin 13
  //   Q_2: flip-flop outputs, pin 12
  //   Q_3: flip-flop outputs, pin 11
  //   nMR: Reset, pin 1
  //   nPE: parallel enable input (active LOW), pin 9
  //   D_0: data inputs, pin 3
  //   D_1: data inputs, pin 4
  //   D_2: data inputs, pin 5
  //   D_3: data inputs, pin 6
  //   TC: terminal count output, pin 15
  //   CET: count enable carry input, pin 10
  //   CEP: count enable input, pin 7
  //   CP: pin 2, Hz: 2
  //   VCC: pin 16, default 1
  //   GND: pin 8
endmodule

/* Test case:
CP ~MR ~PE CET CEP   D_3 D_2 D_1 D_0 Q_3 Q_2 Q_1 Q_0

# load
loop(i,4)
loop(n,16)
C  1   0   bits(2,i) bits(4,n)   bits(4,n)
end loop
end loop

# reset
loop(i,8)
loop(n,16)
C  1   0   0   0     bits(4,n)   bits(4,n)
C  0   bits(3,i)     bits(4,n)   bits(4,0)
end loop
end loop

# count
loop(n,16)
C  1   1   1   1     bits(4,0)   bits(4,(n+1)%10)
end loop

# hold
loop(n,16)
C  1   0   0   0     bits(4,n)   bits(4,n)
C  1   1   0   0     bits(4,n)   bits(4,n)
C  1   1   1   0     bits(4,n)   bits(4,n)
C  1   1   0   1     bits(4,n)   bits(4,n)
end loop
*/
