// Digital circuit 74779-inc.dig as structural Verilog
// flip flop part of 74779
module _74779_inc (
  input  DATA,
  input  LOAD,
  input  nTOGGLE,
  input  CP,
  output Q,
  output nQ
);

  wire and_1_out, and_2_out, and_3_out, not_1_out, not_2_out, or_1_out;

  not not_1 (not_1_out, LOAD);
  not not_2 (not_2_out, nTOGGLE);
  and and_1 (and_1_out, DATA, LOAD);
  and and_2 (and_2_out, not_1_out, nTOGGLE, Q);
  and and_3 (and_3_out, not_1_out, not_2_out, nQ);
  or or_1 (or_1_out, and_1_out, and_2_out, and_3_out);
  D_FF d_ff_1 (.D(or_1_out), .C(CP), .Q(Q), .nQ(nQ));

  // Notes on the sheet:
  //   DATA: pin 1
  //   LOAD: pin 2
  //   Q: pin 4
  //   nQ: pin 3
endmodule
