// Digital circuit 74779.dig as structural Verilog
module _74779 (
  input  CP,
  input  S0,
  input  S1,
  input  nOE,
  input  I_O0,
  input  I_O1,
  input  I_O2,
  input  I_O3,
  input  I_O4,
  input  I_O5,
  input  I_O6,
  input  I_O7,
  input  nCET,
  input  VCC,
  input  GND,
  output nTC
);

  wire _74779___detail_a_1_p3, _74779___detail_a_1_p4, _74779___detail_a_1_p6, _74779___detail_a_2_p3,
       _74779___detail_a_2_p6, _74779___detail_a_3_p3, _74779___detail_a_3_p6, _74779___detail_a_4_p3,
       _74779___detail_a_4_p6, _74779___detail_a_5_p3, _74779___detail_a_5_p6, _74779___detail_a_6_p3,
       _74779___detail_a_6_p6, _74779___detail_a_7_p3, _74779___detail_a_7_p6, _74779___detail_a_8_p3,
       _74779___detail_a_8_p6, and_1_out, and_2_out, and_3_out, and_4_out, and_5_out, and_6_out, and_7_out,
       and_8_out, and_9_out, and_10_out, and_11_out, and_12_out, and_13_out, and_14_out, and_15_out,
       and_16_out, and_17_out, and_18_out, and_19_out, and_20_out, and_21_out, and_22_out, and_23_out,
       and_24_out, and_25_out, and_26_out, and_27_out, and_28_out, and_29_out, and_30_out, and_31_out,
       and_32_out, and_33_out, and_34_out, and_35_out, and_36_out, and_37_out, and_38_out, and_39_out,
       driver_1_out, driver_2_out, driver_3_out, driver_4_out, driver_5_out, driver_6_out, driver_7_out,
       driver_8_out, nor_2_out, nor_3_out, nor_4_out, nor_5_out, nor_6_out, nor_7_out, nor_8_out, not_1_out,
       not_2_out, not_3_out, not_4_out, not_5_out, not_6_out, not_7_out, not_8_out, not_9_out, not_10_out,
       not_11_out, not_12_out, not_13_out, not_14_out, not_15_out;

  not not_1 (not_1_out, S0);
  not not_2 (not_2_out, S1);
  not not_3 (not_3_out, nOE);
  not not_4 (not_4_out, not_2_out);
  not not_5 (not_5_out, not_1_out);
  assign driver_1_out = nOE ? I_O0 : 1'bz;  // Driver driver_1
  assign driver_2_out = nOE ? I_O1 : 1'bz;  // Driver driver_2
  assign driver_3_out = nOE ? I_O2 : 1'bz;  // Driver driver_3
  assign driver_4_out = nOE ? I_O3 : 1'bz;  // Driver driver_4
  assign driver_5_out = nOE ? I_O4 : 1'bz;  // Driver driver_5
  assign driver_6_out = nOE ? I_O5 : 1'bz;  // Driver driver_6
  assign driver_7_out = nOE ? I_O6 : 1'bz;  // Driver driver_7
  assign driver_8_out = nOE ? I_O7 : 1'bz;  // Driver driver_8
  assign I_O0 = not_3_out ? not_7_out : 1'bz;  // Driver driver_9
  assign I_O1 = not_3_out ? not_8_out : 1'bz;  // Driver driver_10
  assign I_O2 = not_3_out ? not_9_out : 1'bz;  // Driver driver_11
  assign I_O3 = not_3_out ? not_10_out : 1'bz;  // Driver driver_12
  assign I_O4 = not_3_out ? not_11_out : 1'bz;  // Driver driver_13
  assign I_O5 = not_3_out ? not_12_out : 1'bz;  // Driver driver_14
  assign I_O6 = not_3_out ? not_13_out : 1'bz;  // Driver driver_15
  assign I_O7 = not_3_out ? not_14_out : 1'bz;  // Driver driver_16
  not not_6 (not_6_out, nCET);
  and and_1 (and_1_out, not_1_out, not_2_out);
  and and_2 (and_2_out, not_4_out, not_1_out);
  and and_3 (and_3_out, not_2_out, not_5_out);
  not not_7 (not_7_out, _74779___detail_a_1_p3);
  not not_8 (not_8_out, _74779___detail_a_2_p3);
  not not_9 (not_9_out, _74779___detail_a_3_p3);
  not not_10 (not_10_out, _74779___detail_a_4_p3);
  not not_11 (not_11_out, _74779___detail_a_5_p3);
  not not_12 (not_12_out, _74779___detail_a_6_p3);
  not not_13 (not_13_out, _74779___detail_a_7_p3);
  not not_14 (not_14_out, _74779___detail_a_8_p3);
  nor nor_1 (nTC, and_23_out, and_5_out);
  and and_4 (and_4_out, _74779___detail_a_3_p3, _74779___detail_a_2_p3, _74779___detail_a_1_p3, and_3_out, not_6_out);
  and and_5 (and_5_out, and_6_out, and_4_out);
  and and_6 (and_6_out, _74779___detail_a_8_p3, _74779___detail_a_7_p3, _74779___detail_a_6_p3, _74779___detail_a_5_p3, _74779___detail_a_4_p3);
  and and_7 (and_7_out, _74779___detail_a_1_p3, and_3_out, not_6_out);
  and and_8 (and_8_out, _74779___detail_a_2_p3, _74779___detail_a_1_p3, and_3_out, not_6_out);
  and and_9 (and_9_out, _74779___detail_a_3_p3, _74779___detail_a_2_p3, _74779___detail_a_1_p3, and_3_out, not_6_out);
  and and_10 (and_10_out, _74779___detail_a_4_p3, _74779___detail_a_3_p3, _74779___detail_a_2_p3);
  and and_11 (and_11_out, _74779___detail_a_1_p3, and_3_out, not_6_out);
  and and_12 (and_12_out, _74779___detail_a_5_p3, _74779___detail_a_4_p3, _74779___detail_a_3_p3);
  and and_13 (and_13_out, _74779___detail_a_2_p3, _74779___detail_a_1_p3, and_3_out, not_6_out);
  and and_14 (and_14_out, _74779___detail_a_6_p3, _74779___detail_a_5_p3, _74779___detail_a_4_p3, _74779___detail_a_3_p3);
  and and_15 (and_15_out, _74779___detail_a_2_p3, _74779___detail_a_1_p3, and_3_out, not_6_out);
  and and_16 (and_16_out, _74779___detail_a_7_p3, _74779___detail_a_6_p3, _74779___detail_a_5_p3, _74779___detail_a_4_p3);
  and and_17 (and_17_out, _74779___detail_a_3_p3, _74779___detail_a_2_p3, _74779___detail_a_1_p3, and_3_out, not_6_out);
  and and_18 (and_18_out, and_10_out, and_11_out);
  and and_19 (and_19_out, and_12_out, and_13_out);
  and and_20 (and_20_out, and_14_out, and_15_out);
  and and_21 (and_21_out, and_16_out, and_17_out);
  and and_22 (and_22_out, _74779___detail_a_3_p6, _74779___detail_a_2_p6, _74779___detail_a_1_p6, and_2_out, not_6_out);
  and and_23 (and_23_out, and_24_out, and_22_out);
  PowerSupply powersupply_1 (.VDD(VCC), .GND(GND));
  and and_24 (and_24_out, _74779___detail_a_8_p6, _74779___detail_a_7_p6, _74779___detail_a_6_p6, _74779___detail_a_5_p6, _74779___detail_a_4_p6);
  and and_25 (and_25_out, not_6_out, _74779___detail_a_1_p6, and_2_out);
  and and_26 (and_26_out, not_6_out, _74779___detail_a_2_p6, _74779___detail_a_1_p6, and_2_out);
  and and_27 (and_27_out, not_6_out, _74779___detail_a_3_p6, _74779___detail_a_2_p6, _74779___detail_a_1_p6, and_2_out);
  and and_28 (and_28_out, not_6_out, _74779___detail_a_4_p6, _74779___detail_a_3_p6);
  and and_29 (and_29_out, _74779___detail_a_2_p6, _74779___detail_a_1_p6, and_2_out);
  and and_30 (and_30_out, not_6_out, _74779___detail_a_5_p6, _74779___detail_a_4_p6);
  and and_31 (and_31_out, _74779___detail_a_3_p6, _74779___detail_a_2_p6, _74779___detail_a_1_p6, and_2_out);
  and and_32 (and_32_out, not_6_out, _74779___detail_a_6_p6, _74779___detail_a_5_p6, _74779___detail_a_4_p6);
  and and_33 (and_33_out, _74779___detail_a_3_p6, _74779___detail_a_2_p6, _74779___detail_a_1_p6, and_2_out);
  and and_34 (and_34_out, not_6_out, _74779___detail_a_7_p6, _74779___detail_a_6_p6, _74779___detail_a_5_p6);
  and and_35 (and_35_out, _74779___detail_a_4_p6, _74779___detail_a_3_p6, _74779___detail_a_2_p6, _74779___detail_a_1_p6, and_2_out);
  and and_36 (and_36_out, and_28_out, and_29_out);
  and and_37 (and_37_out, and_30_out, and_31_out);
  and and_38 (and_38_out, and_32_out, and_33_out);
  and and_39 (and_39_out, and_34_out, and_35_out);
  not not_15 (not_15_out, not_6_out);
  nor nor_2 (nor_2_out, and_25_out, and_7_out);
  nor nor_3 (nor_3_out, and_26_out, and_8_out);
  nor nor_4 (nor_4_out, and_27_out, and_9_out);
  nor nor_5 (nor_5_out, and_36_out, and_18_out);
  nor nor_6 (nor_6_out, and_37_out, and_19_out);
  nor nor_7 (nor_7_out, and_38_out, and_20_out);
  nor nor_8 (nor_8_out, and_39_out, and_21_out);
  // _74779___Detail_A _74779___detail_a_1: pin names not known; wires that end beside it: driver_1_out, and_1_out, _74779___detail_a_1_p3, _74779___detail_a_1_p4, not_15_out, _74779___detail_a_1_p6
  // _74779___Detail_A _74779___detail_a_2: pin names not known; wires that end beside it: driver_2_out, and_1_out, _74779___detail_a_2_p3, _74779___detail_a_1_p4, nor_2_out, _74779___detail_a_2_p6
  // _74779___Detail_A _74779___detail_a_3: pin names not known; wires that end beside it: driver_3_out, and_1_out, _74779___detail_a_3_p3, _74779___detail_a_1_p4, nor_3_out, _74779___detail_a_3_p6
  // _74779___Detail_A _74779___detail_a_4: pin names not known; wires that end beside it: driver_4_out, and_1_out, _74779___detail_a_4_p3, _74779___detail_a_1_p4, nor_4_out, _74779___detail_a_4_p6
  // _74779___Detail_A _74779___detail_a_5: pin names not known; wires that end beside it: driver_5_out, and_1_out, _74779___detail_a_5_p3, _74779___detail_a_1_p4, nor_5_out, _74779___detail_a_5_p6
  // _74779___Detail_A _74779___detail_a_6: pin names not known; wires that end beside it: driver_6_out, and_1_out, _74779___detail_a_6_p3, _74779___detail_a_1_p4, nor_6_out, _74779___detail_a_6_p6
  // _74779___Detail_A _74779___detail_a_7: pin names not known; wires that end beside it: driver_7_out, and_1_out, _74779___detail_a_7_p3, _74779___detail_a_1_p4, nor_7_out, _74779___detail_a_7_p6
  // _74779___Detail_A _74779___detail_a_8: pin names not known; wires that end beside it: driver_8_out, and_1_out, _74779___detail_a_8_p3, _74779___detail_a_1_p4, nor_8_out, _74779___detail_a_8_p6
  not not_16 (_74779___detail_a_1_p4, CP);

  // Notes on the sheet:
  //   CP: pin 15
  //   S0: pin 11
  //   S1: pin 10
  //   nOE: pin 9, default 1
  //   I_O0: pin 16
  //   I_O1: pin 1
  //   I_O2: pin 2
  //   I_O3: pin 3
  //   I_O4: pin 5
  //   I_O5: pin 6
  //   I_O6: pin 7
  //   I_O7: pin 8
  //   nCET: pin 14, default 1
  //   nTC: pin 12
  //   VCC: pin 13, default 1
  //   GND: pin 4
endmodule
