// Digital circuit 7407.dig as structural Verilog
// hex buffer
module _7407 (
  input  _1A,
  input  _2A,
  input  _3A,
  input  _4A,
  input  _5A,
  input  _6A,
  input  VCC,
  input  GND,
  output _1Y,
  output _2Y,
  output _3Y,
  output _4Y,
  output _5Y,
  output _6Y
);

  Delay delay_1 (.in(_1A), .out(_1Y));
  Delay delay_2 (.in(_2A), .out(_2Y));
  Delay delay_3 (.in(_3A), .out(_3Y));
  Delay delay_4 (.in(_4A), .out(_4Y));
  Delay delay_5 (.in(_5A), .out(_5Y));
  Delay delay_6 (.in(_6A), .out(_6Y));
  PowerSupply powersupply_1 (.VDD(VCC), .GND(GND));

  // Notes on the sheet:
  //   _1A: pin 1
  //   _1Y: pin 2
  //   _2A: pin 3
  //   _2Y: pin 4
  //   _3A: pin 5
  //   _3Y: pin 6
  //   _4A: pin 9
  //   _4Y: pin 8
  //   _5A: pin 11
  //   _5Y: pin 10
  //   _6A: pin 13
  //   _6Y: pin 12
  //   VCC: pin 14, default 1
  //   GND: pin 7
endmodule
