// Digital circuit 74107.dig as structural Verilog
// dual J-K flip-flops with clear
module _74107 (
  input  _1J,
  input  _1nCLK,
  input  _1K,
  input  _1nC,
  input  _2J,
  input  _2nCLK,
  input  _2K,
  input  _2nC,
  input  VCC,
  input  GND,
  output _1Q,
  output _1nQ,
  output _2Q,
  output _2nQ
);

  PowerSupply powersupply_1 (.VDD(VCC), .GND(GND));
  JK_FF_AS jk_ff_as_1 (.Set(1'b0), .J(_1J), .C(~_1nCLK), .K(_1K), .Clr(~_1nC), .Q(_1Q), .nQ(_1nQ));
  JK_FF_AS jk_ff_as_2 (.Set(1'b0), .J(_2J), .C(~_2nCLK), .K(_2K), .Clr(~_2nC), .Q(_2Q), .nQ(_2nQ));

  // Notes on the sheet:
  //   _1J: Set, pin 1
  //   _1Q: pin 3
  //   _1nQ: pin 2
  //   _1nCLK: Clock, pin 12
  //   _1K: Kill, pin 4
  //   _1nC: not clear, pin 13
  //   _2J: Set, pin 8
  //   _2Q: pin 5
  //   _2nQ: pin 6
  //   _2nCLK: Clock, pin 9
  //   _2K: Kill, pin 11
  //   _2nC: not clear, pin 10
  //   VCC: pin 14, default 1
  //   GND: pin 7
endmodule
