// Digital circuit 74116.dig as structural Verilog
// dual 4-bit D-type latches
module _74116 (
  input  _1nCLR,
  input  _1nC1,
  input  _1nC2,
  input  _1D1,
  input  _1D2,
  input  _1D3,
  input  _1D4,
  input  _2nCLR,
  input  _2nC1,
  input  _2nC2,
  input  _2D1,
  input  _2D2,
  input  _2D3,
  input  _2D4,
  input  VCC,
  input  GND,
  output _1Q1,
  output _1Q2,
  output _1Q3,
  output _1Q4,
  output _2Q1,
  output _2Q2,
  output _2Q3,
  output _2Q4
);

  wire and_1_out, and_2_out, and_3_out, and_4_out, and_5_out, and_6_out, and_7_out, and_8_out, and_9_out,
       and_10_out, and_11_out, and_12_out, and_17_out, and_18_out, and_19_out, and_20_out, and_21_out,
       and_22_out, and_23_out, and_24_out, and_25_out, and_26_out, and_27_out, and_28_out, not_1_out,
       not_2_out, or_1_out, or_2_out, or_3_out, or_4_out, or_5_out, or_6_out, or_7_out, or_8_out, or_9_out,
       or_10_out, or_11_out, or_12_out, or_13_out, or_14_out, or_15_out, or_16_out, or_17_out, or_18_out;

  or or_1 (or_1_out, _1nC1, _1nC2);
  not not_1 (not_1_out, or_1_out);
  and and_1 (and_1_out, _1Q1, or_1_out);
  and and_2 (and_2_out, _1Q1, _1D1);
  and and_3 (and_3_out, not_1_out, _1D1);
  and and_4 (and_4_out, _1Q2, or_1_out);
  and and_5 (and_5_out, _1Q2, _1D2);
  and and_6 (and_6_out, not_1_out, _1D2);
  and and_7 (and_7_out, _1Q3, or_1_out);
  and and_8 (and_8_out, _1Q3, _1D3);
  and and_9 (and_9_out, not_1_out, _1D3);
  and and_10 (and_10_out, _1Q4, or_1_out);
  and and_11 (and_11_out, _1Q4, _1D4);
  and and_12 (and_12_out, not_1_out, _1D4);
  or or_2 (or_2_out, and_2_out, and_3_out);
  or or_3 (or_3_out, and_5_out, and_6_out);
  or or_4 (or_4_out, and_8_out, and_9_out);
  or or_5 (or_5_out, and_11_out, and_12_out);
  or or_6 (or_6_out, and_1_out, or_2_out);
  or or_7 (or_7_out, and_4_out, or_3_out);
  or or_8 (or_8_out, and_7_out, or_4_out);
  or or_9 (or_9_out, and_10_out, or_5_out);
  and and_13 (_1Q1, _1nCLR, or_6_out);
  and and_14 (_1Q2, _1nCLR, or_7_out);
  and and_15 (_1Q3, _1nCLR, or_8_out);
  and and_16 (_1Q4, _1nCLR, or_9_out);
  PowerSupply powersupply_1 (.VDD(VCC), .GND(GND));
  or or_10 (or_10_out, _2nC1, _2nC2);
  not not_2 (not_2_out, or_10_out);
  and and_17 (and_17_out, _2Q1, or_10_out);
  and and_18 (and_18_out, _2Q1, _2D1);
  and and_19 (and_19_out, not_2_out, _2D1);
  and and_20 (and_20_out, _2Q2, or_10_out);
  and and_21 (and_21_out, _2Q2, _2D2);
  and and_22 (and_22_out, not_2_out, _2D2);
  and and_23 (and_23_out, _2Q3, or_10_out);
  and and_24 (and_24_out, _2Q3, _2D3);
  and and_25 (and_25_out, not_2_out, _2D3);
  and and_26 (and_26_out, _2Q4, or_10_out);
  and and_27 (and_27_out, _2Q4, _2D4);
  and and_28 (and_28_out, not_2_out, _2D4);
  or or_11 (or_11_out, and_18_out, and_19_out);
  or or_12 (or_12_out, and_21_out, and_22_out);
  or or_13 (or_13_out, and_24_out, and_25_out);
  or or_14 (or_14_out, and_27_out, and_28_out);
  or or_15 (or_15_out, and_17_out, or_11_out);
  or or_16 (or_16_out, and_20_out, or_12_out);
  or or_17 (or_17_out, and_23_out, or_13_out);
  or or_18 (or_18_out, and_26_out, or_14_out);
  and and_29 (_2Q1, _2nCLR, or_15_out);
  and and_30 (_2Q2, _2nCLR, or_16_out);
  and and_31 (_2Q3, _2nCLR, or_17_out);
  and and_32 (_2Q4, _2nCLR, or_18_out);

  // Notes on the sheet:
  //   _1nCLR: not clear, pin 1
  //   _1Q1: pin 5
  //   _1nC1: pin 2
  //   _1nC2: pin 3
  //   _1D1: pin 4
  //   _1Q2: pin 7
  //   _1D2: pin 6
  //   _1Q3: pin 9
  //   _1D3: pin 8
  //   _1Q4: pin 11
  //   _1D4: pin 10
  //   _2nCLR: not clear, pin 13
  //   _2Q1: pin 17
  //   _2nC1: pin 14
  //   _2nC2: pin 15
  //   _2D1: pin 16
  //   _2Q2: pin 19
  //   _2D2: pin 18
  //   _2Q3: pin 21
  //   _2D3: pin 20
  //   _2Q4: pin 23
  //   _2D4: pin 22
  //   VCC: pin 24, default 1
  //   GND: pin 12
endmodule
