// Digital circuit 74173.dig as structural Verilog
// quad 3-state D flip-flop with common clock and reset
module _74173 (
  input  D0,
  input  VCC,
  input  GND,
  input  RES,
  input  D1,
  input  D2,
  input  D3,
  input  CLK,
  input  DE1,
  input  DE2,
  input  OE1,
  input  OE2,
  output Q0,
  output Q1,
  output Q2,
  output Q3
);

  wire and_1_out, and_2_out, and_3_out, and_4_out, and_5_out, and_6_out, and_7_out, and_8_out, d_ff_as_1_q,
       d_ff_as_2_q, d_ff_as_3_q, d_ff_as_4_q, nor_1_out, not_1_out, or_1_out, or_2_out, or_3_out, or_4_out,
       or_5_out;

  or or_1 (or_1_out, DE1, DE2);
  nor nor_1 (nor_1_out, OE1, OE2);
  PowerSupply powersupply_1 (.VDD(VCC), .GND(GND));
  not not_1 (not_1_out, or_1_out);
  and and_1 (and_1_out, d_ff_as_1_q, or_1_out);
  and and_2 (and_2_out, D0, not_1_out);
  and and_3 (and_3_out, d_ff_as_2_q, or_1_out);
  and and_4 (and_4_out, D1, not_1_out);
  and and_5 (and_5_out, d_ff_as_3_q, or_1_out);
  and and_6 (and_6_out, D2, not_1_out);
  and and_7 (and_7_out, d_ff_as_4_q, or_1_out);
  and and_8 (and_8_out, D3, not_1_out);
  or or_2 (or_2_out, and_1_out, and_2_out);
  or or_3 (or_3_out, and_3_out, and_4_out);
  or or_4 (or_4_out, and_5_out, and_6_out);
  or or_5 (or_5_out, and_7_out, and_8_out);
  D_FF_AS d_ff_as_1 (.Set(1'b0), .D(or_2_out), .C(CLK), .Clr(RES), .Q(d_ff_as_1_q));  // open: nQ
  D_FF_AS d_ff_as_2 (.Set(1'b0), .D(or_3_out), .C(CLK), .Clr(RES), .Q(d_ff_as_2_q));  // open: nQ
  D_FF_AS d_ff_as_3 (.Set(1'b0), .D(or_4_out), .C(CLK), .Clr(RES), .Q(d_ff_as_3_q));  // open: nQ
  D_FF_AS d_ff_as_4 (.Set(1'b0), .D(or_5_out), .C(CLK), .Clr(RES), .Q(d_ff_as_4_q));  // open: nQ
  assign Q0 = nor_1_out ? d_ff_as_1_q : 1'bz;  // Driver driver_1
  assign Q1 = nor_1_out ? d_ff_as_2_q : 1'bz;  // Driver driver_2
  assign Q2 = nor_1_out ? d_ff_as_3_q : 1'bz;  // Driver driver_3
  assign Q3 = nor_1_out ? d_ff_as_4_q : 1'bz;  // Driver driver_4

  // Notes on the sheet:
  //   D0: pin 14
  //   VCC: pin 16, default 1
  //   GND: pin 8
  //   RES: pin 15, default 1
  //   Q0: pin 3
  //   D1: pin 13
  //   Q1: pin 4
  //   D2: pin 12
  //   Q2: pin 5
  //   D3: pin 11
  //   Q3: pin 6
  //   CLK: pin 7
  //   DE1: pin 9
  //   DE2: pin 10
  //   OE1: pin 1
  //   OE2: pin 2
endmodule

/* Test case:
OE1 OE2 RES CLK DE1 DE2 D0 D1 D2 D3 Q0 Q1 Q2 Q3

 0   0   1   x   x   x  x  x  x  x  0  0  0  0 
 0   0   0   1   x   x  x  x  x  x  0  0  0  0 
 0   0   0   0   x   x  x  x  x  x  0  0  0  0 

#clear ff
 0   0   0   c   0   0  0  0  0  0  0  0  0  0 

 0   0   0   c   1   x  x  x  x  x  0  0  0  0 
 0   0   0   c   x   1  x  x  x  x  0  0  0  0 


loop (n,16)
 0   0   0   c   0   0  bits(4,n)  bits(4,n) 
end loop

#clear ff
 0   0   0   c   0   0  0  0  0  0  0  0  0  0 


 0   1   x   x   x   x  x  x  x  x  z  z  z  z 
 1   0   x   x   x   x  x  x  x  x  z  z  z  z 
 1   1   x   x   x   x  x  x  x  x  z  z  z  z 
*/
