// Digital circuit 74139.dig as structural Verilog
// dual 2-line to 4-line decoder/demultiplexer
module _74139 (
  input  _1A,
  input  _1B,
  input  n1G,
  input  _2A,
  input  _2B,
  input  n2G,
  input  VCC,
  input  GND,
  output n1Y0,
  output n1Y1,
  output n1Y2,
  output n1Y3,
  output n2Y0,
  output n2Y1,
  output n2Y2,
  output n2Y3
);

  wire demultiplexer_1_out_0, demultiplexer_1_out_1, demultiplexer_1_out_2, demultiplexer_1_out_3,
       demultiplexer_2_out_0, demultiplexer_2_out_1, demultiplexer_2_out_2, demultiplexer_2_out_3, not_1_out,
       not_2_out;

  Demultiplexer #(.Selector_Bits(2)) demultiplexer_1 (
    .sel({_1B, _1A}), .in(not_1_out), .out_0(demultiplexer_1_out_0), .out_1(demultiplexer_1_out_1),
    .out_2(demultiplexer_1_out_2), .out_3(demultiplexer_1_out_3));
  not not_1 (not_1_out, n1G);
  Demultiplexer #(.Selector_Bits(2)) demultiplexer_2 (
    .sel({_2B, _2A}), .in(not_2_out), .out_0(demultiplexer_2_out_0), .out_1(demultiplexer_2_out_1),
    .out_2(demultiplexer_2_out_2), .out_3(demultiplexer_2_out_3));
  not not_2 (not_2_out, n2G);
  PowerSupply powersupply_1 (.VDD(VCC), .GND(GND));
  not not_3 (n1Y0, demultiplexer_1_out_0);
  not not_4 (n1Y1, demultiplexer_1_out_1);
  not not_5 (n1Y2, demultiplexer_1_out_2);
  not not_6 (n1Y3, demultiplexer_1_out_3);
  not not_7 (n2Y0, demultiplexer_2_out_0);
  not not_8 (n2Y1, demultiplexer_2_out_1);
  not not_9 (n2Y2, demultiplexer_2_out_2);
  not not_10 (n2Y3, demultiplexer_2_out_3);

  // Notes on the sheet:
  //   _1A: pin 2
  //   _1B: pin 3
  //   n1G: pin 1
  //   n1Y0: pin 4
  //   n1Y1: pin 5
  //   n1Y2: pin 6
  //   n1Y3: pin 7
  //   _2A: pin 14
  //   _2B: pin 13
  //   n2G: pin 15
  //   n2Y0: pin 12
  //   n2Y1: pin 11
  //   n2Y2: pin 10
  //   n2Y3: pin 9
  //   VCC: pin 16, default 1
  //   GND: pin 8
endmodule
