// Digital circuit 74253.dig as structural Verilog
// dual tri state 4-line to 1-line data selectors/multiplexers
module _74253 (
  input  A,
  input  B,
  input  _2G,
  input  _2C0,
  input  _2C1,
  input  _2C2,
  input  _2C3,
  input  _1G,
  input  _1C0,
  input  _1C1,
  input  _1C2,
  input  _1C3,
  input  VCC,
  input  GND,
  output _2Y,
  output _1Y
);

  wire multiplexer_1_out, multiplexer_2_out;

  PowerSupply powersupply_1 (.VDD(VCC), .GND(GND));
  Multiplexer #(.Selector_Bits(2)) multiplexer_1 (
    .sel({B, A}), .in_0(_1C0), .in_1(_1C1), .in_2(_1C2), .in_3(_1C3), .out(multiplexer_1_out));
  Multiplexer #(.Selector_Bits(2)) multiplexer_2 (
    .sel({B, A}), .in_0(_2C0), .in_1(_2C1), .in_2(_2C2), .in_3(_2C3), .out(multiplexer_2_out));
  assign _1Y = ~_1G ? multiplexer_1_out : 1'bz;  // DriverInvSel driverinvsel_1
  assign _2Y = ~_2G ? multiplexer_2_out : 1'bz;  // DriverInvSel driverinvsel_2

  // Notes on the sheet:
  //   A: pin 14
  //   B: pin 2
  //   _2Y: pin 9
  //   _2G: strobe, pin 15
  //   _2C0: pin 10
  //   _2C1: pin 11
  //   _2C2: pin 12
  //   _2C3: pin 13
  //   _1Y: pin 7
  //   _1G: strobe, pin 1
  //   _1C0: pin 6
  //   _1C1: pin 5
  //   _1C2: pin 4
  //   _1C3: pin 3
  //   VCC: pin 16, default 1
  //   GND: pin 8
endmodule
