// Digital circuit 7442.dig as structural Verilog
// 4-line BCD to 10-line decimal decoder
module _7442 (
  input  A,
  input  C,
  input  B,
  input  D,
  input  VCC,
  input  GND,
  output Y0,
  output Y1,
  output Y2,
  output Y3,
  output Y4,
  output Y5,
  output Y6,
  output Y7,
  output Y8,
  output Y9
);

  PowerSupply powersupply_1 (.VDD(VCC), .GND(GND));
  Demultiplexer #(.Selector_Bits(4), .Default(1)) demultiplexer_1 (
    .sel({D, C, B, A}), .in(1'b0), .out_0(Y0), .out_1(Y1), .out_2(Y2), .out_3(Y3), .out_4(Y4), .out_5(Y5),
    .out_6(Y6), .out_7(Y7), .out_8(Y8), .out_9(Y9));  // open: out_10, out_11, out_12, out_13, out_14, out_15

  // Notes on the sheet:
  //   A: pin 15
  //   C: pin 13
  //   B: pin 14
  //   D: pin 12
  //   Y0: pin 1
  //   Y1: pin 2
  //   Y2: pin 3
  //   Y3: pin 4
  //   Y4: pin 5
  //   Y5: pin 6
  //   Y6: pin 7
  //   Y7: pin 9
  //   Y8: pin 10
  //   Y9: pin 11
  //   VCC: pin 16, default 1
  //   GND: pin 8
endmodule
