// Digital circuit 7482.dig as structural Verilog
// 2-bit binary full adder
module _7482 (
  input  C0,
  input  B1,
  input  B2,
  input  A1,
  input  A2,
  input  VCC,
  input  GND,
  output S1,
  output S2,
  output C2
);

  PowerSupply powersupply_1 (.VDD(VCC), .GND(GND));
  Add #(.Bits(2)) add_1 (.a({A2, A1}), .b({B2, B1}), .c_i(C0), .s({S2, S1}), .c_o(C2));

  // Notes on the sheet:
  //   C0: pin 5
  //   B1: pin 3
  //   B2: pin 13
  //   S1: pin 1
  //   S2: pin 12
  //   A1: pin 2
  //   A2: pin 14
  //   C2: pin 10
  //   VCC: pin 4, default 1
  //   GND: pin 11
endmodule

/* Test case:
# A complete test of all 32 possible additions
#

C0   A2 A1   B2 B1  C2 S2 S1
loop(A,4)
  loop(B,4)
0    bits(2,A)     bits(2,B)    bits(3,A+B)
1    bits(2,A)     bits(2,B)    bits(3,A+B+1)
  end loop
end loop
*/
