// Digital circuit 7410.dig as structural Verilog
// triple 3-input NAND gate
module _7410 (
  input  _1A,
  input  _1C,
  input  _2A,
  input  _2C,
  input  _3C,
  input  _3A,
  input  _1B,
  input  _2B,
  input  _3B,
  input  VCC,
  input  GND,
  output _1Y,
  output _2Y,
  output _3Y
);

  nand nand_1 (_1Y, _1A, _1B, _1C);
  nand nand_2 (_2Y, _2A, _2B, _2C);
  nand nand_3 (_3Y, _3A, _3B, _3C);
  PowerSupply powersupply_1 (.VDD(VCC), .GND(GND));

  // Notes on the sheet:
  //   _1A: pin 1
  //   _1C: pin 13
  //   _1Y: pin 12
  //   _2A: pin 3
  //   _2C: pin 5
  //   _2Y: pin 6
  //   _3C: pin 11
  //   _3A: pin 9
  //   _3Y: pin 8
  //   _1B: pin 2
  //   _2B: pin 4
  //   _3B: pin 10
  //   VCC: pin 14, default 1
  //   GND: pin 7
endmodule
