// Digital circuit 744002.dig as structural Verilog
// dual 4-input NOR gate
module _744002 (
  input  _1A,
  input  _1B,
  input  _1C,
  input  _1D,
  input  _2B,
  input  _2A,
  input  _2C,
  input  _2D,
  input  VCC,
  input  GND,
  output _1Y,
  output _2Y
);

  nor nor_1 (_1Y, _1A, _1B, _1C, _1D);
  nor nor_2 (_2Y, _2A, _2B, _2C, _2D);
  PowerSupply powersupply_1 (.VDD(VCC), .GND(GND));

  // Notes on the sheet:
  //   _1A: pin 2
  //   _1B: pin 3
  //   _1Y: pin 1
  //   _1C: pin 4
  //   _1D: pin 5
  //   _2B: pin 10
  //   _2A: pin 9
  //   _2C: pin 11
  //   _2D: pin 12
  //   _2Y: pin 13
  //   VCC: pin 14, default 1
  //   GND: pin 7
endmodule

/* Test case:
1A 1B 1C 1D 1Y 2A 2B 2C 2D 2Y
0  0  0  0  1  X  X  X  X  X
X  X  X  X  X  0  0  0  0  1
1  X  X  X  0  X  X  X  X  X
X  X  X  X  X  1  X  X  X  0
X  1  X  X  0  X  X  X  X  X
X  X  X  X  X  X  1  X  X  0
X  X  1  X  0  X  X  X  X  X
X  X  X  X  X  X  X  1  X  0
X  X  X  1  0  X  X  X  X  X
X  X  X  X  X  X  X  X  1  0
*/
