// Digital circuit 74162.dig as structural Verilog
// Decimal Synchronous Counter
module _74162 (
  input  nLD,
  input  nCLR,
  input  CLK,
  input  ENT,
  input  ENP,
  input  A,
  input  B,
  input  C,
  input  D,
  input  VCC,
  input  GND,
  output RCO,
  output QA,
  output QB,
  output QC,
  output QD
);

  wire and_1_out, comparator_1_eq;
  wire [3:0] add_1_s, multiplexer_1_out, multiplexer_2_out, multiplexer_3_out, multiplexer_4_out;

  Add #(.Bits(4)) add_1 (.a({QD, QC, QB, QA}), .b(4'b0001), .c_i(1'b0), .s(add_1_s));  // open: c_o
  and and_1 (and_1_out, ENP, ENT);
  PowerSupply powersupply_1 (.VDD(VCC), .GND(GND));
  Comparator #(.Bits(4)) comparator_1 (.a({QD, QC, QB, QA}), .b(4'b1001), .eq(comparator_1_eq));  // open: gt, lt
  Multiplexer #(.Bits(4)) multiplexer_1 (
    .sel(comparator_1_eq), .in_0(add_1_s), .in_1(4'b0000), .out(multiplexer_1_out));
  Multiplexer #(.Bits(4)) multiplexer_2 (
    .sel(nLD), .in_0({D, C, B, A}), .in_1(multiplexer_3_out), .out(multiplexer_2_out));
  Multiplexer #(.Bits(4)) multiplexer_3 (
    .sel(and_1_out), .in_0({QD, QC, QB, QA}), .in_1(multiplexer_1_out), .out(multiplexer_3_out));
  Multiplexer #(.Bits(4)) multiplexer_4 (.sel(nCLR), .in_0(4'b0000), .in_1(multiplexer_2_out), .out(multiplexer_4_out));
  and and_2 (RCO, comparator_1_eq, ENT);
  D_FF #(.Bits(4)) Q (.D(multiplexer_4_out), .C(CLK), .Q({QD, QC, QB, QA}));  // open: nQ

  // Notes on the sheet:
  //   nLD: Load counter from inputs A B C D, pin 9
  //   nCLR: Clear counter to zero, pin 1
  //   CLK: pin 2
  //   RCO: Ripple counter overflow, pin 15
  //   ENT: Count Enable Carry In (with ENP), pin 10
  //   ENP: Count Enable (with ENT), pin 7
  //   A: Input low bit, pin 3
  //   QA: Output low bit, pin 14
  //   QB: pin 13
  //   QC: pin 12
  //   QD: Output high bit, pin 11
  //   B: pin 4
  //   C: pin 5
  //   D: Input high bit, pin 6
  //   VCC: pin 16, default 1
  //   GND: pin 8
endmodule

/* Test case:
CLK ~CLR ~LD ENT ENP   D C B A QD QC QB QA

# load
loop(i,4)
loop(n,16)
C  1   0   bits(2,i) bits(4,n)   bits(4,n)
end loop
end loop

# reset
loop(i,8)
loop(n,16)
C  1   0   0   0     bits(4,n)   bits(4,n)
C  0   bits(3,i)     bits(4,n)   bits(4,0)
end loop
end loop

# count
loop(n,16)
C  1   1   1   1     bits(4,0)   bits(4,(n+1)%10)
end loop

# hold
loop(n,16)
C  1   0   0   0     bits(4,n)   bits(4,n)
C  1   1   0   0     bits(4,n)   bits(4,n)
C  1   1   1   0     bits(4,n)   bits(4,n)
C  1   1   0   1     bits(4,n)   bits(4,n)
end loop
*/
