// Digital circuit 74163.dig as structural Verilog
// hex synchronous counter
module _74163 (
  input  nPE,
  input  nSR,
  input  CP,
  input  CET,
  input  CEP,
  input  P0,
  input  P1,
  input  P2,
  input  P3,
  input  VCC,
  input  GND,
  output TC,
  output Q0,
  output Q1,
  output Q2,
  output Q3
);

  wire add_1_c_o, and_1_out;
  wire [3:0] add_1_s, multiplexer_1_out, multiplexer_2_out, multiplexer_3_out;

  PowerSupply powersupply_1 (.VDD(VCC), .GND(GND));
  Add #(.Bits(4)) add_1 (.a({Q3, Q2, Q1, Q0}), .b(4'b0001), .c_i(1'b0), .s(add_1_s), .c_o(add_1_c_o));
  and and_1 (and_1_out, CEP, CET);
  Multiplexer #(.Bits(4)) multiplexer_1 (
    .sel(and_1_out), .in_0({Q3, Q2, Q1, Q0}), .in_1(add_1_s), .out(multiplexer_1_out));
  Multiplexer #(.Bits(4)) multiplexer_2 (
    .sel(nPE), .in_0({P3, P2, P1, P0}), .in_1(multiplexer_1_out), .out(multiplexer_2_out));
  Multiplexer #(.Bits(4)) multiplexer_3 (.sel(nSR), .in_0(4'b0000), .in_1(multiplexer_2_out), .out(multiplexer_3_out));
  and and_2 (TC, add_1_c_o, CET);
  D_FF #(.Bits(4)) Q (.D(multiplexer_3_out), .C(CP), .Q({Q3, Q2, Q1, Q0}));  // open: nQ

  // Notes on the sheet:
  //   nPE: Parallel Enable, pin 9
  //   nSR: Synchronous Reset, pin 1
  //   CP: pin 2
  //   TC: Terminal Count (overflow out), pin 15
  //   CET: Count Enable Trickle (overflow in), pin 10
  //   CEP: Count Enable Parallel, pin 7
  //   P0: pin 3
  //   P1: pin 4
  //   P2: pin 5
  //   P3: pin 6
  //   Q0: pin 14
  //   Q1: pin 13
  //   Q2: pin 12
  //   Q3: pin 11
  //   VCC: pin 16, default 1
  //   GND: pin 8
endmodule

/* Test case:
CP ~SR ~PE CET CEP   P3 P2 P1 P0 Q3 Q2 Q1 Q0

# load
loop(i,4)
loop(n,16)
C  1   0   bits(2,i) bits(4,n)   bits(4,n)
end loop
end loop

# reset
loop(i,8)
loop(n,16)
C  1   0   0   0     bits(4,n)   bits(4,n)
C  0   bits(3,i)     bits(4,n)   bits(4,0)
end loop
end loop

# count
loop(n,16)
C  1   1   1   1     bits(4,0)   bits(4,n+1)
end loop

# hold
loop(n,16)
C  1   0   0   0     bits(4,n)   bits(4,n)
C  1   1   0   0     bits(4,n)   bits(4,n)
C  1   1   1   0     bits(4,n)   bits(4,n)
C  1   1   0   1     bits(4,n)   bits(4,n)
end loop
*/
