// Digital circuit 74190.dig as structural Verilog
// Presettable synchronous 4-bit bcd up/down counter
module _74190 (
  input  D0,
  input  nPL,
  input  nU_D,
  input  CP,
  input  nCE,
  input  D1,
  input  D2,
  input  D3,
  input  VCC,
  input  GND,
  output Q0,
  output Q1,
  output Q2,
  output Q3,
  output TC,
  output nRC
);

  wire and_1_out, and_2_out, and_3_out, and_4_out, and_5_out, and_6_out, and_7_out, and_8_out, and_9_out,
       and_10_out, and_11_out, and_12_out, and_13_out, and_14_out, and_15_out, and_16_out, and_17_out,
       and_18_out, and_19_out, jk_ff_as_1_nq, jk_ff_as_2_nq, jk_ff_as_3_nq, jk_ff_as_4_nq, nand_1_out,
       not_1_out, not_2_out, or_2_out, or_3_out, or_4_out;

  not not_1 (not_1_out, nPL);
  not not_2 (not_2_out, nCE);
  and and_1 (and_1_out, not_2_out, ~nU_D);  // And
  PowerSupply powersupply_1 (.VDD(VCC), .GND(GND));
  and and_2 (and_2_out, nU_D, not_2_out);
  and and_3 (and_3_out, ~nU_D, Q0, Q3);  // And
  and and_4 (and_4_out, nU_D, jk_ff_as_1_nq, jk_ff_as_2_nq, jk_ff_as_3_nq, jk_ff_as_4_nq);
  and and_5 (and_5_out, D0, not_1_out);
  and and_6 (and_6_out, D1, not_1_out);
  and and_7 (and_7_out, and_2_out, jk_ff_as_1_nq, nand_1_out);
  and and_8 (and_8_out, Q0, jk_ff_as_4_nq, and_1_out);
  nand nand_1 (nand_1_out, jk_ff_as_2_nq, jk_ff_as_3_nq, jk_ff_as_4_nq);
  and and_9 (and_9_out, D2, not_1_out);
  and and_10 (and_10_out, nand_1_out, and_2_out, jk_ff_as_1_nq, jk_ff_as_2_nq);
  and and_11 (and_11_out, Q0, Q1, and_1_out);
  and and_12 (and_12_out, D3, not_1_out);
  and and_13 (and_13_out, and_2_out, jk_ff_as_1_nq, jk_ff_as_2_nq, jk_ff_as_3_nq);
  and and_14 (and_14_out, Q0, Q3, and_1_out);
  and and_15 (and_15_out, Q0, Q1, Q2, and_1_out);
  or or_1 (TC, and_3_out, and_4_out);
  and and_16 (and_16_out, ~and_5_out, not_1_out);  // And
  and and_17 (and_17_out, ~and_6_out, not_1_out);  // And
  or or_2 (or_2_out, and_7_out, and_8_out);
  and and_18 (and_18_out, ~and_9_out, not_1_out);  // And
  or or_3 (or_3_out, and_10_out, and_11_out);
  and and_19 (and_19_out, ~and_12_out, not_1_out);  // And
  or or_4 (or_4_out, and_13_out, and_14_out, and_15_out);
  JK_FF_AS jk_ff_as_1 (
    .Set(and_5_out), .J(not_2_out), .C(CP), .K(not_2_out), .Clr(and_16_out), .Q(Q0), .nQ(jk_ff_as_1_nq));
  JK_FF_AS jk_ff_as_2 (
    .Set(and_6_out), .J(or_2_out), .C(CP), .K(or_2_out), .Clr(and_17_out), .Q(Q1), .nQ(jk_ff_as_2_nq));
  JK_FF_AS jk_ff_as_3 (
    .Set(and_9_out), .J(or_3_out), .C(CP), .K(or_3_out), .Clr(and_18_out), .Q(Q2), .nQ(jk_ff_as_3_nq));
  JK_FF_AS jk_ff_as_4 (
    .Set(and_12_out), .J(or_4_out), .C(CP), .K(or_4_out), .Clr(and_19_out), .Q(Q3), .nQ(jk_ff_as_4_nq));
  nand nand_2 (nRC, ~CP, not_2_out, TC);  // NAnd

  // Notes on the sheet:
  //   Q0: pin 3
  //   Q1: pin 2
  //   Q2: pin 6
  //   Q3: pin 7
  //   TC: pin 12
  //   D0: pin 15
  //   nPL: pin 11
  //   nU_D: pin 5
  //   CP: pin 14
  //   nCE: pin 4
  //   nRC: pin 13
  //   D1: pin 1
  //   D2: pin 10
  //   D3: pin 9
  //   VCC: pin 16, default 1
  //   GND: pin 8
  //   1
  //   2
  //   3
  //   4
  //   5
  //   6
  //   7
  //   8
  //   9
  //   10
  //   11
  //   12
  //   13
  //   14
endmodule

/* Test case Count:
~U/D	~CE	~PL	CP	D0	D1	D2	D3	Q0	Q1	Q2	Q3
# Pre-Load & Hold
X	X	0	C	1	1	1	1	1	1	1	1
X	1	1	C	1	1	1	1	1	1	1	1
X	X	0	C	1	0	1	0	1	0	1	0
X	1	1	C	1	0	1	0	1	0	1	0
X	X	0	C	0	1	0	1	0	1	0	1
X	1	1	C	0	1	0	1	0	1	0	1
X	X	0	C	0	0	0	0	0	0	0	0
X	1	1	C	0	0	0	0	0	0	0	0

# Count Up
0	0	1	C	0	0	0	0	1	0	0	0
0	0	1	C	0	0	0	0	0	1	0	0
0	0	1	C	0	0	0	0	1	1	0	0
0	0	1	C	0	0	0	0	0	0	1	0
0	0	1	C	0	0	0	0	1	0	1	0
0	0	1	C	0	0	0	0	0	1	1	0
0	0	1	C	0	0	0	0	1	1	1	0
0	0	1	C	0	0	0	0	0	0	0	1
0	0	1	C	0	0	0	0	1	0	0	1
0	0	1	C	0	0	0	0	0	0	0	0

# Count Down
1	0	1	C	0	0	0	0	1	0	0	1
1	0	1	C	0	0	0	0	0	0	0	1
1	0	1	C	0	0	0	0	1	1	1	0
1	0	1	C	0	0	0	0	0	1	1	0
1	0	1	C	0	0	0	0	1	0	1	0
1	0	1	C	0	0	0	0	0	0	1	0
1	0	1	C	0	0	0	0	1	1	0	0
1	0	1	C	0	0	0	0	0	1	0	0
1	0	1	C	0	0	0	0	1	0	0	0
1	0	1	C	0	0	0	0	0	0	0	0
*/

/* Test case Carry:
~U/D	~CE	~PL	CP	D0	D1	D2	D3	Q0	Q1	Q2	Q3	TC	~RC
1	1	0	C	1	1	1	1	1	1	1	1	X	X
1	1	1	C	1	1	1	1	1	1	1	1	0	1
0	1	1	C	1	1	1	1	1	1	1	1	1	1

1	1	0	C	0	0	0	0	0	0	0	0	X	X
0	1	1	C	0	0	0	0	0	0	0	0	0	1
1	1	1	C	0	0	0	0	0	0	0	0	1	1
*/
