// Digital circuit 744017.dig as structural Verilog
// Johnson decade counter with 10 decoded outputs
module _744017 (
  input  nCP1,
  input  CP0,
  input  MR,
  input  VCC,
  input  GND,
  output Q0,
  output Q1,
  output Q2,
  output Q3,
  output Q4,
  output Q5,
  output Q6,
  output Q7,
  output Q8,
  output Q9,
  output nQ5_9
);

  wire and_1_out, and_2_out, d_ff_as_1_nq, d_ff_as_1_q, d_ff_as_2_nq, d_ff_as_2_q, d_ff_as_3_nq, d_ff_as_3_q,
       d_ff_as_4_nq, d_ff_as_4_q, d_ff_as_5_q, not_1_out, or_1_out;

  PowerSupply powersupply_1 (.VDD(VCC), .GND(GND));
  not not_1 (not_1_out, nCP1);
  and and_1 (and_1_out, not_1_out, CP0);
  nor nor_1 (Q0, d_ff_as_1_q, d_ff_as_5_q);
  nor nor_2 (Q1, d_ff_as_1_nq, d_ff_as_2_q);
  D_FF_AS d_ff_as_1 (.Set(1'b0), .D(nQ5_9), .C(and_1_out), .Clr(MR), .Q(d_ff_as_1_q), .nQ(d_ff_as_1_nq));
  nor nor_3 (Q2, d_ff_as_3_q, d_ff_as_2_nq);
  nor nor_4 (Q3, d_ff_as_3_nq, d_ff_as_4_q);
  or or_1 (or_1_out, d_ff_as_3_q, d_ff_as_1_q);
  D_FF_AS d_ff_as_2 (.Set(1'b0), .D(d_ff_as_1_q), .C(and_1_out), .Clr(MR), .Q(d_ff_as_2_q), .nQ(d_ff_as_2_nq));
  nor nor_5 (Q4, d_ff_as_4_nq, d_ff_as_5_q);
  and and_2 (and_2_out, or_1_out, d_ff_as_2_q);
  nor nor_6 (Q5, nQ5_9, d_ff_as_1_nq);
  D_FF_AS d_ff_as_3 (.Set(1'b0), .D(and_2_out), .C(and_1_out), .Clr(MR), .Q(d_ff_as_3_q), .nQ(d_ff_as_3_nq));
  nor nor_7 (Q6, d_ff_as_2_nq, d_ff_as_1_q);
  D_FF_AS d_ff_as_4 (.Set(1'b0), .D(d_ff_as_3_q), .C(and_1_out), .Clr(MR), .Q(d_ff_as_4_q), .nQ(d_ff_as_4_nq));
  nor nor_8 (Q7, d_ff_as_3_nq, d_ff_as_2_q);
  nor nor_9 (Q8, d_ff_as_3_q, d_ff_as_4_nq);
  D_FF_AS d_ff_as_5 (.Set(1'b0), .D(d_ff_as_4_q), .C(and_1_out), .Clr(MR), .Q(d_ff_as_5_q), .nQ(nQ5_9));
  nor nor_10 (Q9, nQ5_9, d_ff_as_4_q);

  // Notes on the sheet:
  //   nCP1: pin 13
  //   CP0: pin 14
  //   MR: pin 15
  //   Q0: pin 3
  //   Q1: pin 2
  //   Q2: pin 4
  //   Q3: pin 7
  //   Q4: pin 10
  //   Q5: pin 1
  //   Q6: pin 5
  //   Q7: pin 6
  //   Q8: pin 9
  //   Q9: pin 11
  //   nQ5_9: pin 12
  //   VCC: pin 16, default 1
  //   GND: pin 8
endmodule

/* Test case Funktionstest:
MR CP0 ~CP1 Q0 Q1 Q2 Q3 Q4 Q5 Q6 Q7 Q8 Q9 ~{Q5-9}
# master reset should put the counter into a defined state
1  X   X    1  0  0  0  0  0  0  0  0  0  1
# counting should only happen if /CP1 is low and CP0 is pulsed
0  C   1    1  0  0  0  0  0  0  0  0  0  1
0  C   0    0  1  0  0  0  0  0  0  0  0  1
0  C   1    0  1  0  0  0  0  0  0  0  0  1
0  C   0    0  0  1  0  0  0  0  0  0  0  1
0  C   1    0  0  1  0  0  0  0  0  0  0  1
0  C   0    0  0  0  1  0  0  0  0  0  0  1
0  C   0    0  0  0  0  1  0  0  0  0  0  1
0  C   1    0  0  0  0  1  0  0  0  0  0  1
0  C   0    0  0  0  0  0  1  0  0  0  0  0
0  C   1    0  0  0  0  0  1  0  0  0  0  0
0  C   0    0  0  0  0  0  0  1  0  0  0  0
0  C   1    0  0  0  0  0  0  1  0  0  0  0
0  C   0    0  0  0  0  0  0  0  1  0  0  0
0  C   1    0  0  0  0  0  0  0  1  0  0  0
0  C   0    0  0  0  0  0  0  0  0  1  0  0
0  C   1    0  0  0  0  0  0  0  0  1  0  0
0  C   0    0  0  0  0  0  0  0  0  0  1  0
0  C   1    0  0  0  0  0  0  0  0  0  1  0
# the counter should properly wrap to 1
0  C   0    1  0  0  0  0  0  0  0  0  0  1
0  C   1    1  0  0  0  0  0  0  0  0  0  1
0  C   0    0  1  0  0  0  0  0  0  0  0  1
0  C   0    0  0  1  0  0  0  0  0  0  0  1
# testing master reset from some other state
1  X   X    1  0  0  0  0  0  0  0  0  0  1
*/
