// Digital circuit 7490.dig as structural Verilog
// asynchronous two - five - decimal addition counter
module _7490 (
  input  CKB,
  input  R_0_1,
  input  R_0_2,
  input  R_9_1,
  input  R_9_2,
  input  CKA,
  input  VCC,
  input  GND,
  output Q_A,
  output Q_B,
  output Q_C,
  output Q_D
);

  wire and_1_out, jk_ff_as_4_nq, nand_1_out, nand_2_out, nand_3_out, not_1_out;

  PowerSupply powersupply_1 (.VDD(VCC), .GND(GND));
  nand nand_1 (nand_1_out, R_9_1, R_9_2);
  not not_1 (not_1_out, 1'b0);
  nand nand_2 (nand_2_out, R_0_1, R_0_2);
  nand nand_3 (nand_3_out, nand_2_out, nand_1_out);
  JK_FF_AS jk_ff_as_1 (
    .Set(~nand_1_out), .J(not_1_out), .C(~CKA), .K(not_1_out), .Clr(~nand_2_out), .Q(Q_A));  // open: nQ
  JK_FF_AS jk_ff_as_2 (.Set(1'b0), .J(jk_ff_as_4_nq), .C(~CKB), .K(not_1_out), .Clr(nand_3_out), .Q(Q_B));  // open: nQ
  JK_FF_AS jk_ff_as_3 (.Set(1'b0), .J(not_1_out), .C(~Q_B), .K(not_1_out), .Clr(nand_3_out), .Q(Q_C));  // open: nQ
  JK_FF_AS jk_ff_as_4 (
    .Set(~nand_1_out), .J(and_1_out), .C(~CKB), .K(Q_D), .Clr(~nand_2_out), .Q(Q_D), .nQ(jk_ff_as_4_nq));
  and and_1 (and_1_out, Q_B, Q_C);

  // Notes on the sheet:
  //   Q_A: pin 12
  //   Q_B: pin 9
  //   Q_C: pin 8
  //   Q_D: pin 11
  //   CKB: pin 1
  //   R_0_1: pin 2
  //   R_0_2: pin 3
  //   R_9_1: pin 6
  //   R_9_2: pin 7
  //   CKA: pin 14
  //   VCC: pin 5, default 1
  //   GND: pin 10
endmodule

/* Test case basic count:
R_0(1) R_0(2) R_9(1) R_9(2) CKA CKB Q_A Q_B Q_C Q_D

#Clear
1 1 0 0 X X 0 0 0 0

#Count
0 0 0 0 0 0 0 0 0 0
0 0 0 0 1 1 0 0 0 0
0 0 0 0 0 0 1 1 0 0
0 0 0 0 1 1 1 1 0 0
0 0 0 0 0 0 0 0 1 0
0 0 0 0 1 1 0 0 1 0
0 0 0 0 0 0 1 1 1 0
0 0 0 0 1 1 1 1 1 0
0 0 0 0 0 0 0 0 0 1
0 0 0 0 1 1 0 0 0 1
0 0 0 0 0 0 1 0 0 0
0 0 0 0 1 1 1 0 0 0

#Preset 9
0 0 1 1 X X 1 0 0 1
*/

/* Test case 8421BCD-decimal:
R_0(1) R_0(2) R_9(1) R_9(2) CKA CKB Q_D Q_C Q_B Q_A

#Clear
1 1 0 0 X X 0 0 0 0

#Count
0 0 0 0 0 0 0 0 0 0
0 0 0 0 1 0 0 0 0 0
0 0 0 0 0 1 0 0 0 1
0 0 0 0 1 1 0 0 0 1
0 0 0 0 0 0 0 0 1 0
0 0 0 0 1 0 0 0 1 0
0 0 0 0 0 1 0 0 1 1
0 0 0 0 1 1 0 0 1 1
0 0 0 0 0 0 0 1 0 0
0 0 0 0 1 0 0 1 0 0
0 0 0 0 0 1 0 1 0 1
0 0 0 0 1 1 0 1 0 1
0 0 0 0 0 0 0 1 1 0
0 0 0 0 1 0 0 1 1 0
0 0 0 0 0 1 0 1 1 1
0 0 0 0 1 1 0 1 1 1
0 0 0 0 0 0 1 0 0 0
0 0 0 0 1 0 1 0 0 0
0 0 0 0 0 1 1 0 0 1
0 0 0 0 1 1 1 0 0 1
0 0 0 0 0 0 0 0 0 0
0 0 0 0 1 0 0 0 0 0

#Preset 9
0 0 1 1 X X 1 0 0 1
*/

/* Test case 5421BCD-decimal:
R_0(1) R_0(2) R_9(1) R_9(2) CKA CKB Q_A Q_D Q_C Q_B

#Clear
1 1 0 0 X X 0 0 0 0

#Count
0 0 0 0 0 0 0 0 0 0
0 0 0 0 0 1 0 0 0 0
0 0 0 0 0 0 0 0 0 1
0 0 0 0 0 1 0 0 0 1
0 0 0 0 0 0 0 0 1 0
0 0 0 0 0 1 0 0 1 0
0 0 0 0 0 0 0 0 1 1
0 0 0 0 0 1 0 0 1 1
0 0 0 0 1 0 0 1 0 0
0 0 0 0 1 1 0 1 0 0
0 0 0 0 0 0 1 0 0 0
0 0 0 0 0 1 1 0 0 0
0 0 0 0 0 0 1 0 0 1
0 0 0 0 0 1 1 0 0 1
0 0 0 0 0 0 1 0 1 0
0 0 0 0 0 1 1 0 1 0
0 0 0 0 0 0 1 0 1 1
0 0 0 0 0 1 1 0 1 1
0 0 0 0 1 0 1 1 0 0
0 0 0 0 1 1 1 1 0 0
0 0 0 0 0 0 0 0 0 0
0 0 0 0 0 1 0 0 0 0

#Preset 9
0 0 1 1 X X 1 1 0 0
*/

/* Test case novenary:
R_0(1) R_0(2) R_9(1) R_9(2) CKA CKB Q_D Q_C Q_B Q_A

#Clear
1 1 0 0 X X 0 0 0 0

#Count
0 0 0 0 0 0 0 0 0 0
0 0 0 0 1 0 0 0 0 0
0 1 0 0 0 1 0 0 0 1
0 1 0 0 1 1 0 0 0 1
0 0 0 0 0 0 0 0 1 0
0 0 0 0 1 0 0 0 1 0
0 1 0 0 0 1 0 0 1 1
0 1 0 0 1 1 0 0 1 1
0 0 0 0 0 0 0 1 0 0
0 0 0 0 1 0 0 1 0 0
0 1 0 0 0 1 0 1 0 1
0 1 0 0 1 1 0 1 0 1
0 0 0 0 0 0 0 1 1 0
0 0 0 0 1 0 0 1 1 0
0 1 0 0 0 1 0 1 1 1
0 1 0 0 1 1 0 1 1 1
1 0 0 0 0 0 1 0 0 0
1 0 0 0 1 0 1 0 0 0
1 1 0 0 0 0 0 0 0 0
1 1 0 0 1 0 0 0 0 0
0 0 0 0 0 0 0 0 0 0
0 0 0 0 1 0 0 0 0 0

#Preset 9
0 0 1 1 X X 1 0 0 1
*/

/* Test case senary:
R_0(1) R_0(2) R_9(1) R_9(2) CKA CKB Q_D Q_C Q_B Q_A

#Clear
1 1 0 0 X X 0 0 0 0

#Count
0 0 0 0 0 0 0 0 0 0
0 0 0 0 1 0 0 0 0 0
0 0 0 0 0 1 0 0 0 1
0 0 0 0 1 1 0 0 0 1
0 1 0 0 0 0 0 0 1 0
0 1 0 0 1 0 0 0 1 0
0 1 0 0 0 1 0 0 1 1
0 1 0 0 1 1 0 0 1 1
1 0 0 0 0 0 0 1 0 0
1 0 0 0 1 0 0 1 0 0
1 0 0 0 0 1 0 1 0 1
1 0 0 0 1 1 0 1 0 1
1 1 0 0 0 1 0 0 0 0
1 1 0 0 1 1 0 0 0 0
0 0 0 0 0 0 0 0 0 0
0 0 0 0 1 0 0 0 0 0

#Preset 9
0 0 1 1 X X 1 0 0 1
*/
