// Digital circuit 74247.dig as structural Verilog
// BCD to 7-segment decoder, active low, tails on 6 and 9
module _74247 (
  input  A,
  input  B,
  input  C,
  input  D,
  input  nRBI,
  input  nLT,
  input  VCC,
  input  GND,
  input  nBI_nRBO,
  output na,
  output nb,
  output nc,
  output nd,
  output ne,
  output nf,
  output ng
);

  wire and_1_out, and_2_out, and_3_out, and_4_out, and_5_out, and_6_out, and_7_out, and_8_out, and_9_out,
       and_10_out, and_11_out, and_12_out, and_13_out, and_14_out, and_15_out, and_16_out, and_17_out,
       and_18_out, delay_1_out, delay_2_out, nand_1_out, nand_2_out, nand_3_out, nand_4_out, nand_5_out,
       nand_6_out, nand_7_out, not_1_out, not_2_out;

  PowerSupply powersupply_1 (.VDD(VCC), .GND(GND));
  nand nand_1 (nand_1_out, A, delay_1_out);
  nand nand_2 (nand_2_out, B, delay_1_out);
  nand nand_3 (nand_3_out, C, delay_1_out);
  not not_1 (not_1_out, D);
  Delay delay_1 (.in(nLT), .out(delay_1_out));
  and and_1 (and_1_out, delay_1_out, not_2_out, not_1_out, nand_3_out, nand_2_out, nand_1_out);
  not not_2 (not_2_out, nRBI);
  nand nand_4 (nand_4_out, nand_1_out, nBI_nRBO);
  nand nand_5 (nand_5_out, nand_2_out, nBI_nRBO);
  nand nand_6 (nand_6_out, nand_3_out, nBI_nRBO);
  nand nand_7 (nand_7_out, not_1_out, nBI_nRBO);
  PullUp pullup_1 (.out(nBI_nRBO));
  assign nBI_nRBO = and_1_out ? 1'b0 : 1'bz;  // Driver driver_1
  and and_2 (and_2_out, nand_5_out, nand_7_out);
  and and_3 (and_3_out, nand_1_out, nand_2_out, nand_6_out);
  and and_4 (and_4_out, nand_4_out, nand_2_out, nand_3_out, not_1_out);
  and and_5 (and_5_out, nand_5_out, nand_7_out);
  and and_6 (and_6_out, nand_4_out, nand_2_out, nand_6_out);
  and and_7 (and_7_out, nand_1_out, nand_5_out, nand_6_out);
  and and_8 (and_8_out, nand_6_out, nand_7_out);
  and and_9 (and_9_out, nand_1_out, nand_5_out, nand_3_out);
  and and_10 (and_10_out, nand_4_out, nand_2_out, nand_3_out, not_1_out);
  and and_11 (and_11_out, nand_1_out, nand_2_out, nand_6_out);
  and and_12 (and_12_out, nand_4_out, nand_5_out, nand_6_out);
  Delay delay_2 (.in(nand_4_out), .out(delay_2_out));
  and and_13 (and_13_out, nand_2_out, nand_6_out);
  and and_14 (and_14_out, nand_4_out, nand_5_out);
  and and_15 (and_15_out, nand_5_out, nand_3_out);
  and and_16 (and_16_out, nand_4_out, nand_3_out, not_1_out);
  and and_17 (and_17_out, nand_4_out, nand_5_out, nand_6_out);
  and and_18 (and_18_out, nand_2_out, nand_3_out, not_1_out, delay_1_out);
  or or_1 (na, and_2_out, and_3_out, and_4_out);
  or or_2 (nb, and_5_out, and_6_out, and_7_out);
  or or_3 (nc, and_8_out, and_9_out);
  or or_4 (nd, and_10_out, and_11_out, and_12_out);
  or or_5 (ne, delay_2_out, and_13_out);
  or or_6 (nf, and_14_out, and_15_out, and_16_out);
  or or_7 (ng, and_17_out, and_18_out);

  // Notes on the sheet:
  //   A: Bit 0, pin 7
  //   B: Bit 1, pin 1
  //   C: Bit 2, pin 2
  //   D: Bit 3, pin 6
  //   nRBI: ripple blanking input (LOW active), pin 5, default 1
  //   na: pin 13
  //   nb: pin 12
  //   nc: pin 11
  //   nd: pin 10
  //   ne: pin 9
  //   nf: pin 15
  //   ng: pin 14
  //   nLT: lamp test, pin 3, default 1
  //   VCC: pin 16, default 1
  //   GND: pin 8
  //   nBI_nRBO: Blanking Input/Ripple Blank Output, pin 4
endmodule

/* Test case:
~LT ~RBI D C B A ~BI/~RBO  ~a ~b ~c ~d ~e ~f ~g ~BI/~RBO_out
 1    0  0 0 0 0   z        1  1  1  1  1  1  1  0
 1    1  0 0 0 0   z        0  0  0  0  0  0  1  1
 1    0  0 0 0 0   0        1  1  1  1  1  1  1  0
# ~RBI=0 & ~BI=1 is not allowed
#1    0  0 0 0 0   1        0  0  0  0  0  0  1  1
 1    1  0 0 0 0   0        1  1  1  1  1  1  1  0
 1    1  0 0 0 0   1        0  0  0  0  0  0  1  1

 1    x  0 0 0 1   z        1  0  0  1  1  1  1  1
 1    x  0 0 1 0   z        0  0  1  0  0  1  0  1
 1    x  0 0 1 1   z        0  0  0  0  1  1  0  1
 1    x  0 1 0 0   z        1  0  0  1  1  0  0  1
 1    x  0 1 0 1   z        0  1  0  0  1  0  0  1
 1    x  0 1 1 0   z        0  1  0  0  0  0  0  1
 1    x  0 1 1 1   z        0  0  0  1  1  1  1  1
 1    x  1 0 0 0   z        0  0  0  0  0  0  0  1
 1    x  1 0 0 1   z        0  0  0  0  1  0  0  1
 1    x  1 0 1 0   z        1  1  1  0  0  1  0  1
 1    x  1 0 1 1   z        1  1  0  0  1  1  0  1
 1    x  1 1 0 0   z        1  0  1  1  1  0  0  1
 1    x  1 1 0 1   z        0  1  1  0  1  0  0  1
 1    x  1 1 1 0   z        1  1  1  0  0  0  0  1
 1    x  1 1 1 1   z        1  1  1  1  1  1  1  1

#x    x  x x x x   0        1  1  1  1  1  1  1  0
 1    0  0 0 0 0   0        1  1  1  1  1  1  1  0
 0    x  x x x x   z        0  0  0  0  0  0  0  1
 0    x  x x x x   0        1  1  1  1  1  1  1  0
 0    x  x x x x   1        0  0  0  0  0  0  0  1
*/
