// Digital circuit 7447.dig as structural Verilog
// BCD to 7-segment decoder, active low
module _7447 (
  input  A,
  input  B,
  input  C,
  input  D,
  input  nRBI,
  input  nLT,
  input  VCC,
  input  GND,
  output nRBO,
  output na,
  output nb,
  output nc,
  output nd,
  output ne,
  output nf,
  output ng
);

  wire a_t, and_1_out, and_2_out, and_3_out, and_4_out, and_5_out, and_6_out, and_7_out, and_8_out,
       and_9_out, and_10_out, and_11_out, and_12_out, and_13_out, and_14_out, and_15_out, and_16_out,
       and_17_out, and_18_out, and_19_out, and_20_out, and_21_out, and_22_out, and_23_out, and_24_out,
       and_25_out, and_26_out, b_t, c_t, d_t, nor_1_out, not_1_out, not_2_out, not_3_out, not_4_out,
       not_5_out, not_6_out;

  PowerSupply powersupply_1 (.VDD(VCC), .GND(GND));
  nor nor_1 (nor_1_out, A, B, C, D);
  not not_1 (not_1_out, nRBI);
  not not_2 (not_2_out, nLT);
  and and_1 (and_1_out, nor_1_out, not_1_out);
  nand nand_1 (nRBO, nor_1_out, nLT, not_1_out);
  or or_1 (d_t, D, and_1_out);
  or or_2 (c_t, C, and_1_out);
  or or_3 (b_t, B, and_1_out);
  or or_4 (a_t, A, and_1_out);
  not not_3 (not_3_out, d_t);
  not not_4 (not_4_out, c_t);
  not not_5 (not_5_out, b_t);
  not not_6 (not_6_out, a_t);
  and and_2 (and_2_out, d_t, not_5_out, a_t);
  and and_3 (and_3_out, not_3_out, c_t, a_t);
  and and_4 (and_4_out, not_3_out, not_4_out, b_t);
  and and_5 (and_5_out, not_4_out, not_5_out, not_6_out);
  and and_6 (and_6_out, not_3_out, not_4_out);
  and and_7 (and_7_out, not_3_out, b_t, a_t);
  and and_8 (and_8_out, not_4_out, not_5_out);
  and and_9 (and_9_out, not_5_out, not_6_out);
  and and_10 (and_10_out, not_3_out, c_t);
  and and_11 (and_11_out, not_4_out, not_5_out);
  and and_12 (and_12_out, not_4_out, a_t);
  and and_13 (and_13_out, not_4_out, not_6_out);
  and and_14 (and_14_out, not_4_out, b_t);
  and and_15 (and_15_out, c_t, not_5_out, a_t);
  and and_16 (and_16_out, b_t, not_6_out);
  and and_17 (and_17_out, not_4_out, not_6_out);
  and and_18 (and_18_out, b_t, not_6_out);
  and and_19 (and_19_out, d_t, not_5_out);
  and and_20 (and_20_out, c_t, not_5_out);
  and and_21 (and_21_out, c_t, not_6_out);
  and and_22 (and_22_out, not_5_out, not_6_out);
  and and_23 (and_23_out, d_t, not_5_out);
  and and_24 (and_24_out, not_4_out, b_t);
  and and_25 (and_25_out, c_t, not_5_out);
  and and_26 (and_26_out, b_t, not_6_out);
  nor nor_2 (na, and_2_out, and_3_out, not_2_out, and_4_out, and_5_out);
  nor nor_3 (nb, and_6_out, and_7_out, not_2_out, and_8_out, and_9_out);
  nor nor_4 (nc, and_10_out, and_11_out, not_2_out, and_12_out);
  nor nor_5 (nd, and_13_out, and_14_out, not_2_out, and_15_out, and_16_out);
  nor nor_6 (ne, and_17_out, not_2_out, and_18_out);
  nor nor_7 (nf, and_19_out, and_20_out, not_2_out, and_21_out, and_22_out);
  nor nor_8 (ng, and_23_out, and_24_out, not_2_out, and_25_out, and_26_out);

  // Notes on the sheet:
  //   A: pin 7
  //   B: pin 1
  //   C: pin 2
  //   D: pin 6
  //   nRBO: ripple blanking output (LOW active), pin 4
  //   nRBI: ripple blanking input (LOW active), pin 5
  //   na: pin 13
  //   nb: pin 12
  //   nc: pin 11
  //   nd: pin 10
  //   ne: pin 9
  //   nf: pin 15
  //   ng: pin 14
  //   nLT: lamp test, pin 3
  //   VCC: pin 16, default 1
  //   GND: pin 8
endmodule

/* Test case:
~LT ~RBI D C B A ~RBO  ~a ~b ~c ~d ~e ~f ~g 
 1    1  0 0 0 0   1   0 0 0 0 0 0 1

 1    x  0 0 0 1   1   1 0 0 1 1 1 1
 1    x  0 0 1 0   1   0 0 1 0 0 1 0
 1    x  0 0 1 1   1   0 0 0 0 1 1 0
 1    x  0 1 0 0   1   1 0 0 1 1 0 0
 1    x  0 1 0 1   1   0 1 0 0 1 0 0
 1    x  0 1 1 0   1   1 1 0 0 0 0 0
 1    x  0 1 1 1   1   0 0 0 1 1 1 1
 1    x  1 0 0 0   1   0 0 0 0 0 0 0
 1    x  1 0 0 1   1   0 0 0 1 1 0 0
 1    x  1 0 1 0   1   1 1 1 0 0 1 0
 1    x  1 0 1 1   1   1 1 0 0 1 1 0
 1    x  1 1 0 0   1   1 0 1 1 1 0 0
 1    x  1 1 0 1   1   0 1 1 0 1 0 0
 1    x  1 1 1 0   1   1 1 1 0 0 0 0
 1    x  1 1 1 1   1   1 1 1 1 1 1 1

#x    x  x x x x   0   0 0 0 0 0 0 0
 1    0  0 0 0 0   0   1 1 1 1 1 1 1
 0    x  x x x x   1   0 0 0 0 0 0 0
*/
