// Digital circuit 7448.dig as structural Verilog
// BCD to 7-segment decoder, active high
module _7448 (
  input  A,
  input  B,
  input  C,
  input  D,
  input  nRBI,
  input  nLT,
  input  VCC,
  input  GND,
  output nRBO,
  output a_2,
  output b_2,
  output c_2,
  output d_2,
  output e,
  output f,
  output g
);

  wire and_1_out, and_2_out, and_3_out, and_4_out, and_5_out, and_6_out, and_7_out, and_8_out, and_9_out,
       and_10_out, and_11_out, and_12_out, and_13_out, and_14_out, and_15_out, and_16_out, and_17_out,
       and_18_out, and_19_out, and_20_out, and_21_out, and_22_out, and_23_out, and_24_out, and_25_out,
       and_26_out, nor_1_out, not_1_out, not_2_out, not_3_out, not_4_out, not_5_out, not_6_out, or_1_out,
       or_2_out, or_3_out, or_4_out;

  PowerSupply powersupply_1 (.VDD(VCC), .GND(GND));
  nor nor_1 (nor_1_out, A, B, C, D);
  not not_1 (not_1_out, nRBI);
  not not_2 (not_2_out, nLT);
  and and_1 (and_1_out, nor_1_out, not_1_out);
  nand nand_1 (nRBO, nor_1_out, nLT, not_1_out);
  or or_1 (or_1_out, D, and_1_out);
  or or_2 (or_2_out, C, and_1_out);
  or or_3 (or_3_out, B, and_1_out);
  or or_4 (or_4_out, A, and_1_out);
  not not_3 (not_3_out, or_1_out);
  not not_4 (not_4_out, or_2_out);
  not not_5 (not_5_out, or_3_out);
  not not_6 (not_6_out, or_4_out);
  and and_2 (and_2_out, or_1_out, not_5_out, or_4_out);
  and and_3 (and_3_out, not_3_out, or_2_out, or_4_out);
  and and_4 (and_4_out, not_3_out, not_4_out, or_3_out);
  and and_5 (and_5_out, not_4_out, not_5_out, not_6_out);
  and and_6 (and_6_out, not_3_out, not_4_out);
  and and_7 (and_7_out, not_3_out, or_3_out, or_4_out);
  and and_8 (and_8_out, not_4_out, not_5_out);
  and and_9 (and_9_out, not_5_out, not_6_out);
  and and_10 (and_10_out, not_3_out, or_2_out);
  and and_11 (and_11_out, not_4_out, not_5_out);
  and and_12 (and_12_out, not_4_out, or_4_out);
  and and_13 (and_13_out, not_4_out, not_6_out);
  and and_14 (and_14_out, not_4_out, or_3_out);
  and and_15 (and_15_out, or_2_out, not_5_out, or_4_out);
  and and_16 (and_16_out, or_3_out, not_6_out);
  and and_17 (and_17_out, not_4_out, not_6_out);
  and and_18 (and_18_out, or_3_out, not_6_out);
  and and_19 (and_19_out, or_1_out, not_5_out);
  and and_20 (and_20_out, or_2_out, not_5_out);
  and and_21 (and_21_out, or_2_out, not_6_out);
  and and_22 (and_22_out, not_5_out, not_6_out);
  and and_23 (and_23_out, or_1_out, not_5_out);
  and and_24 (and_24_out, not_4_out, or_3_out);
  and and_25 (and_25_out, or_2_out, not_5_out);
  and and_26 (and_26_out, or_3_out, not_6_out);
  or or_5 (a_2, and_2_out, and_3_out, not_2_out, and_4_out, and_5_out);
  or or_6 (b_2, and_6_out, and_7_out, not_2_out, and_8_out, and_9_out);
  or or_7 (c_2, and_10_out, and_11_out, not_2_out, and_12_out);
  or or_8 (d_2, and_13_out, and_14_out, not_2_out, and_15_out, and_16_out);
  or or_9 (e, and_17_out, not_2_out, and_18_out);
  or or_10 (f, and_19_out, and_20_out, not_2_out, and_21_out, and_22_out);
  or or_11 (g, and_23_out, and_24_out, not_2_out, and_25_out, and_26_out);

  // Notes on the sheet:
  //   A: Bit 0, pin 7
  //   B: Bit 1, pin 1
  //   C: Bit 2, pin 2
  //   D: Bit 3, pin 6
  //   nRBO: ripple blanking output (LOW active), pin 4
  //   nRBI: ripple blanking input (LOW active), pin 5
  //   a_2: pin 13
  //   b_2: pin 12
  //   c_2: pin 11
  //   d_2: pin 10
  //   e: pin 9
  //   f: pin 15
  //   g: pin 14
  //   nLT: lamp test, pin 3
  //   VCC: pin 16, default 1
  //   GND: pin 8
endmodule

/* Test case:
~LT ~RBI D C B A ~RBO  a b c d e f g 
 1    1  0 0 0 0   1   1 1 1 1 1 1 0

 1    x  0 0 0 1   1   0 1 1 0 0 0 0
 1    x  0 0 1 0   1   1 1 0 1 1 0 1
 1    x  0 0 1 1   1   1 1 1 1 0 0 1
 1    x  0 1 0 0   1   0 1 1 0 0 1 1
 1    x  0 1 0 1   1   1 0 1 1 0 1 1
 1    x  0 1 1 0   1   0 0 1 1 1 1 1
 1    x  0 1 1 1   1   1 1 1 0 0 0 0
 1    x  1 0 0 0   1   1 1 1 1 1 1 1
 1    x  1 0 0 1   1   1 1 1 0 0 1 1
 1    x  1 0 1 0   1   0 0 0 1 1 0 1
 1    x  1 0 1 1   1   0 0 1 1 0 0 1
 1    x  1 1 0 0   1   0 1 0 0 0 1 1
 1    x  1 1 0 1   1   1 0 0 1 0 1 1
 1    x  1 1 1 0   1   0 0 0 1 1 1 1
 1    x  1 1 1 1   1   0 0 0 0 0 0 0

#x    x  x x x x   0   0 0 0 0 0 0 0
 1    0  0 0 0 0   0   0 0 0 0 0 0 0
 0    x  x x x x   1   1 1 1 1 1 1 1
*/
