// Digital circuit 7417.dig as structural Verilog
// hex buffer, open-collector output, same as 7407
module _7417 (
  input  _1A,
  input  _2A,
  input  _3A,
  input  _4A,
  input  _5A,
  input  _6A,
  input  VCC,
  input  GND,
  output _1Y,
  output _2Y,
  output _3Y,
  output _4Y,
  output _5Y,
  output _6Y
);

  wire not_1_out, not_2_out, not_3_out, not_4_out, not_5_out, not_6_out;

  not not_1 (not_1_out, _1A);
  not not_2 (not_2_out, _2A);
  not not_3 (not_3_out, _3A);
  NFET nfet_1 (.G(not_1_out), .D(_1Y), .S(1'b0));
  NFET nfet_2 (.G(not_2_out), .D(_2Y), .S(1'b0));
  NFET nfet_3 (.G(not_3_out), .D(_3Y), .S(1'b0));
  PowerSupply powersupply_1 (.VDD(VCC), .GND(GND));
  not not_4 (not_4_out, _4A);
  not not_5 (not_5_out, _5A);
  not not_6 (not_6_out, _6A);
  NFET nfet_4 (.G(not_4_out), .D(_4Y), .S(1'b0));
  NFET nfet_5 (.G(not_5_out), .D(_5Y), .S(1'b0));
  NFET nfet_6 (.G(not_6_out), .D(_6Y), .S(1'b0));

  // Notes on the sheet:
  //   _1A: pin 1
  //   _1Y: pin 2
  //   _2A: pin 3
  //   _2Y: pin 4
  //   _3A: pin 5
  //   _3Y: pin 6
  //   _4A: pin 9
  //   _4Y: pin 8
  //   _5A: pin 11
  //   _5Y: pin 10
  //   _6A: pin 13
  //   _6Y: pin 12
  //   VCC: pin 14, default 1
  //   GND: pin 7
endmodule
