// Digital circuit 74244.dig as structural Verilog
// octal 3-state buffer/line driver/line receiver
module _74244 (
  input  _1A1,
  input  _1nG,
  input  _1A2,
  input  _1A3,
  input  _1A4,
  input  _2A1,
  input  _2nG,
  input  _2A2,
  input  _2A3,
  input  _2A4,
  input  VCC,
  input  GND,
  output _1Y1,
  output _1Y2,
  output _1Y3,
  output _1Y4,
  output _2Y1,
  output _2Y2,
  output _2Y3,
  output _2Y4
);

  assign _1Y1 = ~_1nG ? _1A1 : 1'bz;  // DriverInvSel driverinvsel_1
  assign _1Y2 = ~_1nG ? _1A2 : 1'bz;  // DriverInvSel driverinvsel_2
  assign _1Y3 = ~_1nG ? _1A3 : 1'bz;  // DriverInvSel driverinvsel_3
  assign _1Y4 = ~_1nG ? _1A4 : 1'bz;  // DriverInvSel driverinvsel_4
  PowerSupply powersupply_1 (.VDD(VCC), .GND(GND));
  assign _2Y1 = ~_2nG ? _2A1 : 1'bz;  // DriverInvSel driverinvsel_5
  assign _2Y2 = ~_2nG ? _2A2 : 1'bz;  // DriverInvSel driverinvsel_6
  assign _2Y3 = ~_2nG ? _2A3 : 1'bz;  // DriverInvSel driverinvsel_7
  assign _2Y4 = ~_2nG ? _2A4 : 1'bz;  // DriverInvSel driverinvsel_8

  // Notes on the sheet:
  //   _1Y1: pin 18
  //   _1A1: pin 2
  //   _1nG: pin 1
  //   _1Y2: pin 16
  //   _1A2: pin 4
  //   _1Y3: pin 14
  //   _1A3: pin 6
  //   _1Y4: pin 12
  //   _1A4: pin 8
  //   _2Y1: pin 9
  //   _2A1: pin 11
  //   _2nG: pin 19
  //   _2Y2: pin 7
  //   _2A2: pin 13
  //   _2Y3: pin 5
  //   _2A3: pin 15
  //   _2Y4: pin 3
  //   _2A4: pin 17
  //   VCC: pin 20, default 1
  //   GND: pin 10
endmodule
