// Digital circuit 74175.dig as structural Verilog
// quad D-flip-flop
module _74175 (
  input  CLK,
  input  nCL,
  input  D1,
  input  D2,
  input  D3,
  input  D4,
  input  VCC,
  input  GND,
  output Q1,
  output Q2,
  output Q3,
  output Q4,
  output nQ1,
  output nQ2,
  output nQ3,
  output nQ4
);

  D_FF_AS #(.Bits(4)) d_ff_as_1 (
    .Set(1'b0), .D({D4, D3, D2, D1}), .C(CLK), .Clr(~nCL), .Q({Q4, Q3, Q2, Q1}), .nQ({nQ4, nQ3, nQ2, nQ1}));
  PowerSupply powersupply_1 (.VDD(VCC), .GND(GND));

  // Notes on the sheet:
  //   CLK: pin 9
  //   nCL: pin 1
  //   D1: pin 4
  //   D2: pin 5
  //   D3: pin 12
  //   D4: pin 13
  //   Q1: pin 2
  //   Q2: pin 7
  //   Q3: pin 10
  //   Q4: pin 15
  //   VCC: pin 16, default 1
  //   GND: pin 8
  //   nQ1: pin 3
  //   nQ2: pin 6
  //   nQ3: pin 11
  //   nQ4: pin 14
endmodule

/* Test case:
CLK ~CL D4 D3 D2 D1 VCC GND Q4 Q3 Q2 Q1 ~Q4 ~Q3 ~Q2 ~Q1
 x   0  x  x  x  x   1   0  0  0  0  0   1   1   1   1
 c   1  0  0  0  0   1   0  0  0  0  0   1   1   1   1
 c   1  0  0  0  1   1   0  0  0  0  1   1   1   1   0
 c   1  0  0  1  0   1   0  0  0  1  0   1   1   0   1
 c   1  0  0  1  1   1   0  0  0  1  1   1   1   0   0
 c   1  0  1  0  0   1   0  0  1  0  0   1   0   1   1
 c   1  0  1  0  1   1   0  0  1  0  1   1   0   1   0
 c   1  0  1  1  0   1   0  0  1  1  0   1   0   0   1
 c   1  0  1  1  1   1   0  0  1  1  1   1   0   0   0
 c   1  1  0  0  0   1   0  1  0  0  0   0   1   1   1
 c   1  1  0  0  1   1   0  1  0  0  1   0   1   1   0
 c   1  1  0  1  0   1   0  1  0  1  0   0   1   0   1
 c   1  1  0  1  1   1   0  1  0  1  1   0   1   0   0
 c   1  1  1  0  0   1   0  1  1  0  0   0   0   1   1
 c   1  1  1  0  1   1   0  1  1  0  1   0   0   1   0
 c   1  1  1  1  0   1   0  1  1  1  0   0   0   0   1
 c   1  1  1  1  1   1   0  1  1  1  1   0   0   0   0
 c   0  x  x  x  x   1   0  0  0  0  0   1   1   1   1
*/
