// Digital circuit 74374.dig as structural Verilog
// octal positive-edge-triggered flip-flops
module _74374 (
  input  nOC,
  input  CLK,
  input  D0,
  input  D1,
  input  D2,
  input  D3,
  input  D4,
  input  D5,
  input  D6,
  input  D7,
  input  VCC,
  input  GND,
  output Q0,
  output Q1,
  output Q2,
  output Q3,
  output Q4,
  output Q5,
  output Q6,
  output Q7
);

  wire [7:0] d_ff_1_q;

  D_FF #(.Bits(8)) d_ff_1 (.D({D7, D6, D5, D4, D3, D2, D1, D0}), .C(CLK), .Q(d_ff_1_q));  // open: nQ
  assign {Q7, Q6, Q5, Q4, Q3, Q2, Q1, Q0} = ~nOC ? d_ff_1_q : 8'bz;  // DriverInvSel driverinvsel_1
  PowerSupply powersupply_1 (.VDD(VCC), .GND(GND));

  // Notes on the sheet:
  //   Q0: pin 2
  //   Q1: pin 5
  //   Q2: pin 6
  //   Q3: pin 9
  //   nOC: pin 1, default 1
  //   CLK: pin 11
  //   Q4: pin 12
  //   Q5: pin 15
  //   Q6: pin 16
  //   Q7: pin 19
  //   D0: pin 3
  //   D1: pin 4
  //   D2: pin 7
  //   D3: pin 8
  //   D4: pin 13
  //   D5: pin 14
  //   D6: pin 17
  //   D7: pin 18
  //   VCC: pin 20, default 1
  //   GND: pin 10
endmodule
