// Digital circuit 7474.dig as structural Verilog
// dual D-flip-flop
module _7474 (
  input  n1SD,
  input  _1D,
  input  _1CP,
  input  n1RD,
  input  n2SD,
  input  _2D,
  input  _2CP,
  input  n2RD,
  input  VCC,
  input  GND,
  output _1Q,
  output n1Q,
  output _2Q,
  output n2Q
);

  wire and_1_out, and_2_out, d_ff_as_1_nq, d_ff_as_2_nq;

  D_FF_AS d_ff_as_1 (.Set(~n1SD), .D(_1D), .C(_1CP), .Clr(~n1RD), .Q(_1Q), .nQ(d_ff_as_1_nq));
  D_FF_AS d_ff_as_2 (.Set(~n2SD), .D(_2D), .C(_2CP), .Clr(~n2RD), .Q(_2Q), .nQ(d_ff_as_2_nq));
  PowerSupply powersupply_1 (.VDD(VCC), .GND(GND));
  and and_1 (and_1_out, ~n1SD, ~n1RD);  // And
  and and_2 (and_2_out, ~n2SD, ~n2RD);  // And
  or or_1 (n1Q, d_ff_as_1_nq, and_1_out);
  or or_2 (n2Q, d_ff_as_2_nq, and_2_out);

  // Notes on the sheet:
  //   _1Q: pin 5
  //   n1Q: pin 6
  //   n1SD: pin 4
  //   _1D: pin 2
  //   _1CP: pin 3
  //   n1RD: pin 1
  //   _2Q: pin 9
  //   n2Q: pin 8
  //   n2SD: pin 10
  //   _2D: pin 12
  //   _2CP: pin 11
  //   n2RD: pin 13
  //   VCC: pin 14, default 1
  //   GND: pin 7
endmodule

/* Test case #1:
~1SD ~1RD 1CP 1D 1Q ~1Q
0 1 X X 1 0
1 0 X X 0 1
0 0 X X 1 1

1 1 C 1 1 0
1 1 0 X 1 0

1 1 C 0 0 1
1 1 0 X 0 1
*/

/* Test case #2:
~2SD ~2RD 2CP 2D 2Q ~2Q
0 1 X X 1 0
1 0 X X 0 1
0 0 X X 1 1

1 1 C 1 1 0
1 1 0 X 1 0

1 1 C 0 0 1
1 1 0 X 0 1
*/
