// Digital circuit 7440105.dig as structural Verilog
// 4-Bit x 16-Word FIFO Register
module _7440105 (
  input  D0,
  input  D1,
  input  D2,
  input  D3,
  input  SI,
  input  nSO,
  input  noe,
  input  MR,
  input  VCC,
  input  GND,
  output Q0,
  output Q1,
  output Q2,
  output Q3,
  output DOR,
  output DIR
);

  wire and_1_out, and_2_out, and_3_out, and_4_out, and_5_out, and_6_out, and_7_out, and_8_out, and_9_out,
       and_10_out, and_11_out, and_12_out, and_13_out, and_14_out, and_15_out, and_16_out, d_ff_as_1_q,
       d_ff_as_2_q, or_1_out, or_2_out, or_3_out, or_4_out, or_5_out, or_6_out, or_7_out, or_8_out, or_9_out,
       or_10_out, or_11_out, or_12_out, or_13_out, or_14_out, or_15_out, or_16_out, rs_ff_as_1_nq,
       rs_ff_as_1_q, rs_ff_as_2_nq, rs_ff_as_2_q, rs_ff_as_3_nq, rs_ff_as_3_q, rs_ff_as_4_nq, rs_ff_as_4_q,
       rs_ff_as_5_nq, rs_ff_as_5_q, rs_ff_as_6_nq, rs_ff_as_6_q, rs_ff_as_7_nq, rs_ff_as_7_q, rs_ff_as_8_nq,
       rs_ff_as_8_q, rs_ff_as_9_nq, rs_ff_as_9_q, rs_ff_as_10_nq, rs_ff_as_10_q, rs_ff_as_11_nq,
       rs_ff_as_11_q, rs_ff_as_12_nq, rs_ff_as_12_q, rs_ff_as_13_nq, rs_ff_as_13_q, rs_ff_as_14_nq,
       rs_ff_as_14_q, rs_ff_as_15_nq, rs_ff_as_15_q, rs_ff_as_16_nq;
  wire [3:0] d_ff_1_q, d_ff_2_q, d_ff_3_q, d_ff_4_q, d_ff_5_q, d_ff_6_q, d_ff_7_q, d_ff_8_q, d_ff_9_q,
       d_ff_10_q, d_ff_11_q, d_ff_12_q, d_ff_13_q, d_ff_14_q, d_ff_15_q, d_ff_16_q;

  PowerSupply powersupply_1 (.VDD(VCC), .GND(GND));
  D_FF_AS d_ff_as_1 (.Set(1'b0), .D(1'b1), .C(SI), .Clr(d_ff_as_1_q), .Q(d_ff_as_1_q));  // open: nQ
  xor xor_1 (DIR, and_2_out, rs_ff_as_1_nq);
  and and_1 (and_1_out, rs_ff_as_2_nq, rs_ff_as_15_q);
  or or_1 (or_1_out, MR, and_4_out);
  D_FF #(.Bits(4)) d_ff_1 (.D(d_ff_16_q), .C(and_1_out), .Q(d_ff_1_q));  // open: nQ
  and and_2 (and_2_out, rs_ff_as_1_nq, d_ff_as_1_q);
  RS_FF_AS rs_ff_as_1 (.S(and_2_out), .R(or_2_out), .Q(rs_ff_as_1_q), .nQ(rs_ff_as_1_nq));
  or or_2 (or_2_out, MR, and_3_out);
  D_FF #(.Bits(4)) d_ff_2 (.D({D3, D2, D1, D0}), .C(and_2_out), .Q(d_ff_2_q));  // open: nQ
  RS_FF_AS rs_ff_as_2 (.S(and_1_out), .R(or_1_out), .Q(rs_ff_as_2_q), .nQ(rs_ff_as_2_nq));
  // Probe on d_ff_1_q
  // Probe on d_ff_2_q
  and and_3 (and_3_out, rs_ff_as_4_nq, rs_ff_as_1_q);
  or or_3 (or_3_out, MR, and_5_out);
  D_FF #(.Bits(4)) d_ff_3 (.D(d_ff_2_q), .C(and_3_out), .Q(d_ff_3_q));  // open: nQ
  and and_4 (and_4_out, rs_ff_as_3_nq, rs_ff_as_2_q);
  RS_FF_AS rs_ff_as_3 (.S(and_4_out), .R(or_4_out), .Q(rs_ff_as_3_q), .nQ(rs_ff_as_3_nq));
  or or_4 (or_4_out, MR, and_6_out);
  D_FF #(.Bits(4)) d_ff_4 (.D(d_ff_1_q), .C(and_4_out), .Q(d_ff_4_q));  // open: nQ
  RS_FF_AS rs_ff_as_4 (.S(and_3_out), .R(or_3_out), .Q(rs_ff_as_4_q), .nQ(rs_ff_as_4_nq));
  // Probe on d_ff_4_q
  // Probe on d_ff_3_q
  and and_5 (and_5_out, rs_ff_as_6_nq, rs_ff_as_4_q);
  or or_5 (or_5_out, MR, and_8_out);
  D_FF #(.Bits(4)) d_ff_5 (.D(d_ff_3_q), .C(and_5_out), .Q(d_ff_5_q));  // open: nQ
  and and_6 (and_6_out, rs_ff_as_5_nq, rs_ff_as_3_q);
  RS_FF_AS rs_ff_as_5 (.S(and_6_out), .R(or_6_out), .Q(rs_ff_as_5_q), .nQ(rs_ff_as_5_nq));
  or or_6 (or_6_out, MR, and_7_out);
  D_FF #(.Bits(4)) d_ff_6 (.D(d_ff_4_q), .C(and_6_out), .Q(d_ff_6_q));  // open: nQ
  RS_FF_AS rs_ff_as_6 (.S(and_5_out), .R(or_5_out), .Q(rs_ff_as_6_q), .nQ(rs_ff_as_6_nq));
  // Probe on d_ff_5_q
  // Probe on d_ff_6_q
  and and_7 (and_7_out, rs_ff_as_8_nq, rs_ff_as_5_q);
  or or_7 (or_7_out, MR, and_9_out);
  D_FF #(.Bits(4)) d_ff_7 (.D(d_ff_6_q), .C(and_7_out), .Q(d_ff_7_q));  // open: nQ
  and and_8 (and_8_out, rs_ff_as_7_nq, rs_ff_as_6_q);
  RS_FF_AS rs_ff_as_7 (.S(and_8_out), .R(or_8_out), .Q(rs_ff_as_7_q), .nQ(rs_ff_as_7_nq));
  or or_8 (or_8_out, MR, and_10_out);
  D_FF #(.Bits(4)) d_ff_8 (.D(d_ff_5_q), .C(and_8_out), .Q(d_ff_8_q));  // open: nQ
  RS_FF_AS rs_ff_as_8 (.S(and_7_out), .R(or_7_out), .Q(rs_ff_as_8_q), .nQ(rs_ff_as_8_nq));
  // Probe on d_ff_8_q
  // Probe on d_ff_7_q
  and and_9 (and_9_out, rs_ff_as_10_nq, rs_ff_as_8_q);
  or or_9 (or_9_out, MR, and_12_out);
  D_FF #(.Bits(4)) d_ff_9 (.D(d_ff_7_q), .C(and_9_out), .Q(d_ff_9_q));  // open: nQ
  and and_10 (and_10_out, rs_ff_as_9_nq, rs_ff_as_7_q);
  RS_FF_AS rs_ff_as_9 (.S(and_10_out), .R(or_10_out), .Q(rs_ff_as_9_q), .nQ(rs_ff_as_9_nq));
  or or_10 (or_10_out, MR, and_11_out);
  D_FF #(.Bits(4)) d_ff_10 (.D(d_ff_8_q), .C(and_10_out), .Q(d_ff_10_q));  // open: nQ
  RS_FF_AS rs_ff_as_10 (.S(and_9_out), .R(or_9_out), .Q(rs_ff_as_10_q), .nQ(rs_ff_as_10_nq));
  // Probe on d_ff_9_q
  // Probe on d_ff_10_q
  and and_11 (and_11_out, rs_ff_as_12_nq, rs_ff_as_9_q);
  or or_11 (or_11_out, MR, and_13_out);
  D_FF #(.Bits(4)) d_ff_11 (.D(d_ff_10_q), .C(and_11_out), .Q(d_ff_11_q));  // open: nQ
  and and_12 (and_12_out, rs_ff_as_11_nq, rs_ff_as_10_q);
  RS_FF_AS rs_ff_as_11 (.S(and_12_out), .R(or_12_out), .Q(rs_ff_as_11_q), .nQ(rs_ff_as_11_nq));
  or or_12 (or_12_out, MR, and_14_out);
  D_FF #(.Bits(4)) d_ff_12 (.D(d_ff_9_q), .C(and_12_out), .Q(d_ff_12_q));  // open: nQ
  RS_FF_AS rs_ff_as_12 (.S(and_11_out), .R(or_11_out), .Q(rs_ff_as_12_q), .nQ(rs_ff_as_12_nq));
  // Probe on d_ff_12_q
  // Probe on d_ff_11_q
  and and_13 (and_13_out, rs_ff_as_14_nq, rs_ff_as_12_q);
  or or_13 (or_13_out, MR, and_16_out);
  D_FF #(.Bits(4)) d_ff_13 (.D(d_ff_11_q), .C(and_13_out), .Q(d_ff_13_q));  // open: nQ
  and and_14 (and_14_out, rs_ff_as_13_nq, rs_ff_as_11_q);
  RS_FF_AS rs_ff_as_13 (.S(and_14_out), .R(or_14_out), .Q(rs_ff_as_13_q), .nQ(rs_ff_as_13_nq));
  or or_14 (or_14_out, MR, and_15_out);
  D_FF #(.Bits(4)) d_ff_14 (.D(d_ff_12_q), .C(and_14_out), .Q(d_ff_14_q));  // open: nQ
  RS_FF_AS rs_ff_as_14 (.S(and_13_out), .R(or_13_out), .Q(rs_ff_as_14_q), .nQ(rs_ff_as_14_nq));
  // Probe on d_ff_13_q
  // Probe on d_ff_14_q
  and and_15 (and_15_out, rs_ff_as_16_nq, rs_ff_as_13_q);
  or or_15 (or_15_out, MR, d_ff_as_2_q);
  D_FF #(.Bits(4)) d_ff_15 (.D(d_ff_14_q), .C(and_15_out), .Q(d_ff_15_q));  // open: nQ
  and and_16 (and_16_out, rs_ff_as_15_nq, rs_ff_as_14_q);
  RS_FF_AS rs_ff_as_15 (.S(and_16_out), .R(or_16_out), .Q(rs_ff_as_15_q), .nQ(rs_ff_as_15_nq));
  or or_16 (or_16_out, MR, and_1_out);
  D_FF #(.Bits(4)) d_ff_16 (.D(d_ff_13_q), .C(and_16_out), .Q(d_ff_16_q));  // open: nQ
  RS_FF_AS rs_ff_as_16 (.S(and_15_out), .R(or_15_out), .Q(DOR), .nQ(rs_ff_as_16_nq));
  // Probe on d_ff_16_q
  // Probe on d_ff_15_q
  D_FF_AS d_ff_as_2 (.Set(1'b0), .D(1'b1), .C(~nSO), .Clr(d_ff_as_2_q), .Q(d_ff_as_2_q));  // open: nQ
  assign {Q3, Q2, Q1, Q0} = ~noe ? d_ff_15_q : 4'bz;  // DriverInvSel driverinvsel_1

  // Notes on the sheet:
  //   D0: pin 4
  //   Q0: pin 13
  //   Q1: pin 12
  //   D1: pin 5
  //   D2: pin 6
  //   Q2: pin 11
  //   D3: pin 7
  //   SI: pin 3
  //   nSO: pin 15, default 1
  //   noe: pin 1, default 1
  //   MR: pin 9
  //   Q3: pin 10
  //   DOR: pin 14
  //   DIR: pin 2
  //   VCC: pin 16, default 1
  //   GND: pin 8
endmodule

/* Test case:
MR  SI ~SO ~oe  DIR DOR  D3 D2 D1 D0  Q3 Q2 Q1 Q0   VCC GND 
# reset
 1   0  1   1    1   0    0  0  0  0   Z  Z  Z  Z    1   0  
 0   0  1   1    1   0    0  0  0  0   Z  Z  Z  Z    1   0  

# fill 16 bits with value from 0-15
loop(a,16)
let d = (a!=15);
 0   c  1   1   (d)  1    bits(4,a)    Z  Z  Z  Z    1   0  
end loop

 0   0  1   0    0   1    0  0  0  0   0  0  0  0    1   0  
loop(a,15)
let v = (a+1);
 0   0  c   0    1   1      0  0  0  0   bits(4,v)   1   0  
end loop
 0   0  c   0    1   0    0  0  0  0   1  1  1  1    1   0  
*/
