// Digital circuit 74154.dig as structural Verilog
// 4-line to 16-line decoders/demultiplexers
module _74154 (
  input  A,
  input  C,
  input  B,
  input  D,
  input  G1,
  input  G2,
  input  VCC,
  input  GND,
  output Y0,
  output Y1,
  output Y2,
  output Y3,
  output Y4,
  output Y5,
  output Y6,
  output Y7,
  output Y8,
  output Y9,
  output Y10,
  output Y11,
  output Y12,
  output Y13,
  output Y14,
  output Y15
);

  wire or_1_out;
  wire [3:0] delay_1_out;

  PowerSupply powersupply_1 (.VDD(VCC), .GND(GND));
  or or_1 (or_1_out, G1, G2);
  Delay #(.Bits(4)) delay_1 (.in({D, C, B, A}), .out(delay_1_out));
  Demultiplexer #(.Selector_Bits(4), .Default(1)) demultiplexer_1 (
    .sel(delay_1_out), .in(or_1_out), .out_0(Y0), .out_1(Y1), .out_2(Y2), .out_3(Y3), .out_4(Y4), .out_5(Y5),
    .out_6(Y6), .out_7(Y7), .out_8(Y8), .out_9(Y9), .out_10(Y10), .out_11(Y11), .out_12(Y12), .out_13(Y13),
    .out_14(Y14), .out_15(Y15));

  // Notes on the sheet:
  //   A: pin 23
  //   C: pin 21
  //   B: pin 22
  //   D: pin 20
  //   Y0: pin 1
  //   Y1: pin 2
  //   Y2: pin 3
  //   Y3: pin 4
  //   Y4: pin 5
  //   Y5: pin 6
  //   Y6: pin 7
  //   Y7: pin 8
  //   Y8: pin 9
  //   Y9: pin 10
  //   Y10: pin 11
  //   Y11: pin 13
  //   Y12: pin 14
  //   Y13: pin 15
  //   Y14: pin 16
  //   Y15: pin 17
  //   G1: pin 18
  //   G2: pin 19
  //   VCC: pin 24, default 1
  //   GND: pin 12
endmodule
