// Digital circuit 74194.dig as structural Verilog
// 4-Bit Bidirectional Universal Shift Register
module _74194 (
  input  D0,
  input  D1,
  input  D2,
  input  D3,
  input  S0,
  input  S1,
  input  DSL,
  input  DSR,
  input  nMR,
  input  CLK,
  input  VCC,
  input  GND,
  output Q0,
  output Q1,
  output Q2,
  output Q3
);

  wire multiplexer_1_out, multiplexer_2_out, multiplexer_3_out, multiplexer_4_out, nMR_t;

  PowerSupply powersupply_1 (.VDD(VCC), .GND(GND));
  not not_1 (nMR_t, nMR);
  Multiplexer #(.Selector_Bits(2)) multiplexer_1 (
    .sel({S1, S0}), .in_0(Q0), .in_1(DSR), .in_2(Q1), .in_3(D0), .out(multiplexer_1_out));
  D_FF_AS d_ff_as_1 (.Set(1'b0), .D(multiplexer_1_out), .C(CLK), .Clr(nMR_t), .Q(Q0));  // open: nQ
  Multiplexer #(.Selector_Bits(2)) multiplexer_2 (
    .sel({S1, S0}), .in_0(Q1), .in_1(Q0), .in_2(Q2), .in_3(D1), .out(multiplexer_2_out));
  D_FF_AS d_ff_as_2 (.Set(1'b0), .D(multiplexer_2_out), .C(CLK), .Clr(nMR_t), .Q(Q1));  // open: nQ
  Multiplexer #(.Selector_Bits(2)) multiplexer_3 (
    .sel({S1, S0}), .in_0(Q2), .in_1(Q1), .in_2(Q3), .in_3(D2), .out(multiplexer_3_out));
  D_FF_AS d_ff_as_3 (.Set(1'b0), .D(multiplexer_3_out), .C(CLK), .Clr(nMR_t), .Q(Q2));  // open: nQ
  Multiplexer #(.Selector_Bits(2)) multiplexer_4 (
    .sel({S1, S0}), .in_0(Q3), .in_1(Q2), .in_2(DSL), .in_3(D3), .out(multiplexer_4_out));
  D_FF_AS d_ff_as_4 (.Set(1'b0), .D(multiplexer_4_out), .C(CLK), .Clr(nMR_t), .Q(Q3));  // open: nQ

  // Other names for the same wires on the sheet: sel[1:0] = {S1, S0}

  // Notes on the sheet:
  //   D0: pin 3
  //   D1: pin 4
  //   D2: pin 5
  //   Q0: pin 15
  //   D3: pin 6
  //   S0: pin 9, default 1
  //   S1: pin 10, default 1
  //   DSL: pin 7
  //   DSR: pin 2
  //   Q1: pin 14
  //   Q2: pin 13
  //   Q3: pin 12
  //   nMR: pin 1, default 1
  //   CLK: pin 11
  //   VCC: pin 16, default 1
  //   GND: pin 8
  //   "Datasheet Pins" test is taken from the "real" implementation 74194real
endmodule

/* Test case coreidcc:
CLK ~MR S1 S0 DSR D3 D2 D1 D0 DSL Q3 Q2 Q1 Q0
 c   0   x  x  1   1  1  1  1  1   0  0  0  0
 c   1   0  1  1   0  0  0  0  0   0  0  0  1
 c   1   0  1  0   0  0  0  0  1   0  0  1  0
 c   1   0  1  0   0  0  0  0  1   0  1  0  0
 c   1   0  1  0   0  0  0  0  1   1  0  0  0
 c   1   1  1  0   0  0  0  0  1   0  0  0  0
 c   1   1  0  0   0  0  0  0  1   1  0  0  0
 c   1   1  0  1   0  0  0  0  0   0  1  0  0
 c   1   1  0  1   0  0  0  0  0   0  0  1  0
 c   1   1  0  1   0  0  0  0  0   0  0  0  1
 c   1   1  0  1   0  0  0  0  0   0  0  0  0
loop(i,16)
 c   1   1  1  1   bits(4,i)   1   bits(4,i) 
end loop
loop(i,16)
 c   1   0  0  1   bits(4,i)   1   1  1  1  1
end loop
*/

/* Test case Datasheet:
~MR S1 S0 CLK DSL DSR D0 D1 D2 D3 Q0 Q1 Q2 Q3
 0  x  x   x   x   x  x  x  x  x  0  0  0  0 
 1  x  x   0   x   x  x  x  x  x  0  0  0  0
loop (n,16)
 1  1  1   c   x   x  bits(4,n)   bits(4,n)
 1  0  1   c   0   1  bits(4,n)   bits(4,(n>>1)|8)
 1  1  1   c   x   x  bits(4,n)   bits(4,n)
 1  0  1   c   1   1  bits(4,n)   bits(4,(n>>1)|8)

 1  1  1   c   x   x  bits(4,n)   bits(4,n)
 1  0  1   c   0   0  bits(4,n)   bits(4,(n>>1))
 1  1  1   c   x   x  bits(4,n)   bits(4,n)
 1  0  1   c   1   0  bits(4,n)   bits(4,(n>>1))
end loop

loop (n,16)
 1  1  1   c   0   0  bits(4,n)   bits(4,n)
 1  1  0   c   1   0  bits(4,n)   bits(4,(n<<1)|1)
 1  1  1   c   0   0  bits(4,n)   bits(4,n)
 1  1  0   c   1   1  bits(4,n)   bits(4,(n<<1)|1)

 1  1  1   c   0   0  bits(4,n)   bits(4,n)
 1  1  0   c   0   0  bits(4,n)   bits(4,(n<<1))
 1  1  1   c   0   0  bits(4,n)   bits(4,n)
 1  1  0   c   0   1  bits(4,n)   bits(4,(n<<1))
end loop

loop (n,16)
 1  1  1   0   0   0  bits(4,n)   x  x  x  x
 1  1  1   c   0   0  bits(4,n)   bits(4,n)
 1  0  0   x   x   x  x  x  x  x  bits(4,n)
end loop
*/

/* Test case Datasheet Pins:
/1 /10 /9 /11 /7 /2 /3 /4 /5 /6 /15 /14 /13 /12
 0  x  x   x   x   x  x  x  x  x  0  0  0  0 
 1  x  x   0   x   x  x  x  x  x  0  0  0  0
loop (n,16)
 1  1  1   c   x   x  bits(4,n)   bits(4,n)
 1  0  1   c   0   1  bits(4,n)   bits(4,(n>>1)|8)
 1  1  1   c   x   x  bits(4,n)   bits(4,n)
 1  0  1   c   1   1  bits(4,n)   bits(4,(n>>1)|8)

 1  1  1   c   x   x  bits(4,n)   bits(4,n)
 1  0  1   c   0   0  bits(4,n)   bits(4,(n>>1))
 1  1  1   c   x   x  bits(4,n)   bits(4,n)
 1  0  1   c   1   0  bits(4,n)   bits(4,(n>>1))
end loop

loop (n,16)
 1  1  1   c   0   0  bits(4,n)   bits(4,n)
 1  1  0   c   1   0  bits(4,n)   bits(4,(n<<1)|1)
 1  1  1   c   0   0  bits(4,n)   bits(4,n)
 1  1  0   c   1   1  bits(4,n)   bits(4,(n<<1)|1)

 1  1  1   c   0   0  bits(4,n)   bits(4,n)
 1  1  0   c   0   0  bits(4,n)   bits(4,(n<<1))
 1  1  1   c   0   0  bits(4,n)   bits(4,n)
 1  1  0   c   0   1  bits(4,n)   bits(4,(n<<1))
end loop

loop (n,16)
 1  1  1   0   0   0  bits(4,n)   x  x  x  x
 1  1  1   c   0   0  bits(4,n)   bits(4,n)
 1  0  0   x   x   x  x  x  x  x  bits(4,n)
end loop
*/
