// Digital circuit 74194real.dig as structural Verilog
// 4-Bit Bidirectional Universal Shift Register, Databook implementation.
module _74194real (
  input  nCLR,
  input  DSR,
  input  DSL,
  input  CLK,
  input  S0,
  input  S1,
  input  A,
  input  B,
  input  C,
  input  D,
  input  VCC,
  input  GND,
  output Q_C,
  output Q_D,
  output Q_B,
  output Q_A
);

  wire and_1_out, and_2_out, and_3_out, and_4_out, and_5_out, and_6_out, and_7_out, and_8_out, and_9_out,
       and_10_out, and_11_out, and_12_out, and_13_out, nor_1_out, nor_2_out, not_1_out, not_2_out, not_3_out,
       or_1_out, or_2_out, or_3_out, or_4_out;

  not not_1 (not_1_out, S0);
  not not_2 (not_2_out, S1);
  not not_3 (not_3_out, nCLR);
  PowerSupply powersupply_1 (.VDD(VCC), .GND(GND));
  nor nor_1 (nor_1_out, not_1_out, not_2_out);
  and and_1 (and_1_out, not_2_out, not_1_out);
  nor nor_2 (nor_2_out, and_1_out, ~CLK);  // NOr
  and and_2 (and_2_out, not_2_out, DSR);
  and and_3 (and_3_out, A, nor_1_out);
  or or_1 (or_1_out, and_4_out, and_3_out, and_2_out);
  and and_4 (and_4_out, Q_B, not_1_out);
  D_FF_AS d_ff_as_1 (.Set(1'b0), .D(or_1_out), .C(nor_2_out), .Clr(not_3_out), .Q(Q_A));  // open: nQ
  and and_5 (and_5_out, not_2_out, Q_A);
  and and_6 (and_6_out, B, nor_1_out);
  or or_2 (or_2_out, and_7_out, and_6_out, and_5_out);
  D_FF_AS d_ff_as_2 (.Set(1'b0), .D(or_2_out), .C(nor_2_out), .Clr(not_3_out), .Q(Q_B));  // open: nQ
  and and_7 (and_7_out, Q_C, not_1_out);
  and and_8 (and_8_out, not_2_out, Q_B);
  and and_9 (and_9_out, C, nor_1_out);
  or or_3 (or_3_out, and_10_out, and_9_out, and_8_out);
  and and_10 (and_10_out, Q_D, not_1_out);
  D_FF_AS d_ff_as_3 (.Set(1'b0), .D(or_3_out), .C(nor_2_out), .Clr(not_3_out), .Q(Q_C));  // open: nQ
  and and_11 (and_11_out, not_2_out, Q_C);
  and and_12 (and_12_out, D, nor_1_out);
  or or_4 (or_4_out, and_13_out, and_12_out, and_11_out);
  D_FF_AS d_ff_as_4 (.Set(1'b0), .D(or_4_out), .C(nor_2_out), .Clr(not_3_out), .Q(Q_D));  // open: nQ
  and and_13 (and_13_out, DSL, not_1_out);

  // Notes on the sheet:
  //   Q_C: pin 13
  //   Q_D: pin 12
  //   Q_B: pin 14
  //   Q_A: pin 15
  //   nCLR: pin 1
  //   DSR: pin 2
  //   DSL: pin 7
  //   CLK: pin 11
  //   S0: pin 9
  //   S1: pin 10
  //   A: pin 3
  //   B: pin 4
  //   C: pin 5
  //   D: pin 6
  //   VCC: pin 16, default 1
  //   GND: pin 8
  //   Circuit taken from the source given in
  //   https://en.wikipedia.org/wiki/List_of_7400-series_integrated_circuits
  //   which is
  //   https://archive.org/details/bitsavers_tidataBookVol2_45945352/page/n822/
  //   The "Datasheet Pins" test is refering to pin numbers instead of signal names.
endmodule

/* Test case Datasheet Pins:
/1 /10 /9 /11 /7 /2 /3 /4 /5 /6 /15 /14 /13 /12
 0  x  x   x   x   x  x  x  x  x  0  0  0  0 
 1  x  x   0   x   x  x  x  x  x  0  0  0  0
loop (n,16)
 1  1  1   c   x   x  bits(4,n)   bits(4,n)
 1  0  1   c   0   1  bits(4,n)   bits(4,(n>>1)|8)
 1  1  1   c   x   x  bits(4,n)   bits(4,n)
 1  0  1   c   1   1  bits(4,n)   bits(4,(n>>1)|8)

 1  1  1   c   x   x  bits(4,n)   bits(4,n)
 1  0  1   c   0   0  bits(4,n)   bits(4,(n>>1))
 1  1  1   c   x   x  bits(4,n)   bits(4,n)
 1  0  1   c   1   0  bits(4,n)   bits(4,(n>>1))
end loop

loop (n,16)
 1  1  1   c   0   0  bits(4,n)   bits(4,n)
 1  1  0   c   1   0  bits(4,n)   bits(4,(n<<1)|1)
 1  1  1   c   0   0  bits(4,n)   bits(4,n)
 1  1  0   c   1   1  bits(4,n)   bits(4,(n<<1)|1)

 1  1  1   c   0   0  bits(4,n)   bits(4,n)
 1  1  0   c   0   0  bits(4,n)   bits(4,(n<<1))
 1  1  1   c   0   0  bits(4,n)   bits(4,n)
 1  1  0   c   0   1  bits(4,n)   bits(4,(n<<1))
end loop

loop (n,16)
 1  1  1   0   0   0  bits(4,n)   x  x  x  x
 1  1  1   c   0   0  bits(4,n)   bits(4,n)
 1  0  0   x   x   x  x  x  x  x  bits(4,n)
end loop
*/

/* Test case Datasheet:
~CLR S1 S0 CLK DSL DSR A B C D Q_A Q_B Q_C Q_D
 0  x  x   x   x   x  x  x  x  x  0  0  0  0 
 1  x  x   0   x   x  x  x  x  x  0  0  0  0
loop (n,16)
 1  1  1   c   x   x  bits(4,n)   bits(4,n)
 1  0  1   c   0   1  bits(4,n)   bits(4,(n>>1)|8)
 1  1  1   c   x   x  bits(4,n)   bits(4,n)
 1  0  1   c   1   1  bits(4,n)   bits(4,(n>>1)|8)

 1  1  1   c   x   x  bits(4,n)   bits(4,n)
 1  0  1   c   0   0  bits(4,n)   bits(4,(n>>1))
 1  1  1   c   x   x  bits(4,n)   bits(4,n)
 1  0  1   c   1   0  bits(4,n)   bits(4,(n>>1))
end loop

loop (n,16)
 1  1  1   c   0   0  bits(4,n)   bits(4,n)
 1  1  0   c   1   0  bits(4,n)   bits(4,(n<<1)|1)
 1  1  1   c   0   0  bits(4,n)   bits(4,n)
 1  1  0   c   1   1  bits(4,n)   bits(4,(n<<1)|1)

 1  1  1   c   0   0  bits(4,n)   bits(4,n)
 1  1  0   c   0   0  bits(4,n)   bits(4,(n<<1))
 1  1  1   c   0   0  bits(4,n)   bits(4,n)
 1  1  0   c   0   1  bits(4,n)   bits(4,(n<<1))
end loop

loop (n,16)
 1  1  1   0   0   0  bits(4,n)   x  x  x  x
 1  1  1   c   0   0  bits(4,n)   bits(4,n)
 1  0  0   x   x   x  x  x  x  x  bits(4,n)
end loop
*/
