// Digital circuit 74299.dig as structural Verilog
// 8-Input Universal Shift/Storage Register
// with Common Parallel I/O Pins
module _74299 (
  input  DSR,
  input  S0,
  input  S1,
  input  nOE1,
  input  nOE2,
  input  CP,
  input  nMR,
  input  DSL,
  input  VCC,
  input  GND,
  input  I_O0,
  input  I_O1,
  input  I_O2,
  input  I_O3,
  input  I_O4,
  input  I_O5,
  input  I_O6,
  input  I_O7,
  output Q0,
  output Q7
);

  wire and_1_out, and_2_out, and_3_out, and_4_out, and_5_out, and_6_out, and_7_out, and_8_out, and_9_out,
       and_10_out, and_11_out, and_12_out, and_13_out, and_14_out, and_15_out, and_16_out, and_17_out,
       and_18_out, and_19_out, and_20_out, and_21_out, and_22_out, and_23_out, and_24_out, and_25_out,
       and_26_out, and_27_out, and_28_out, and_29_out, and_30_out, and_31_out, and_32_out, and_33_out,
       d_ff_as_2_q, d_ff_as_3_q, d_ff_as_4_q, d_ff_as_5_q, d_ff_as_6_q, d_ff_as_7_q, nand_1_out, not_1_out,
       not_2_out, not_3_out, not_4_out, not_5_out, or_1_out, or_2_out, or_3_out, or_4_out, or_5_out,
       or_6_out, or_7_out, or_8_out;

  not not_1 (not_1_out, nOE1);
  not not_2 (not_2_out, nOE2);
  not not_3 (not_3_out, nMR);
  nand nand_1 (nand_1_out, S1, S0);
  and and_1 (and_1_out, nand_1_out, not_1_out, not_2_out);
  PowerSupply powersupply_1 (.VDD(VCC), .GND(GND));
  not not_4 (not_4_out, S0);
  not not_5 (not_5_out, S1);
  and and_2 (and_2_out, DSR, S0, not_5_out);
  and and_3 (and_3_out, S1, not_4_out, d_ff_as_2_q);
  and and_4 (and_4_out, S1, S0, I_O0);
  and and_5 (and_5_out, not_5_out, not_4_out, Q0);
  and and_6 (and_6_out, Q0, S0, not_5_out);
  and and_7 (and_7_out, S1, not_4_out, d_ff_as_3_q);
  and and_8 (and_8_out, S1, S0, I_O1);
  and and_9 (and_9_out, not_5_out, not_4_out, d_ff_as_2_q);
  and and_10 (and_10_out, d_ff_as_2_q, S0, not_5_out);
  and and_11 (and_11_out, S1, not_4_out, d_ff_as_4_q);
  and and_12 (and_12_out, S1, S0, I_O2);
  and and_13 (and_13_out, not_5_out, not_4_out, d_ff_as_3_q);
  and and_14 (and_14_out, d_ff_as_3_q, S0, not_5_out);
  and and_15 (and_15_out, S1, not_4_out, d_ff_as_5_q);
  and and_16 (and_16_out, S1, S0, I_O3);
  and and_17 (and_17_out, not_5_out, not_4_out, d_ff_as_4_q);
  and and_18 (and_18_out, d_ff_as_4_q, S0, not_5_out);
  and and_19 (and_19_out, S1, not_4_out, d_ff_as_6_q);
  and and_20 (and_20_out, S1, S0, I_O4);
  and and_21 (and_21_out, not_5_out, not_4_out, d_ff_as_5_q);
  and and_22 (and_22_out, d_ff_as_5_q, S0, not_5_out);
  and and_23 (and_23_out, S1, not_4_out, d_ff_as_7_q);
  and and_24 (and_24_out, S1, S0, I_O5);
  and and_25 (and_25_out, not_5_out, not_4_out, d_ff_as_6_q);
  and and_26 (and_26_out, d_ff_as_6_q, S0, not_5_out);
  and and_27 (and_27_out, S1, not_4_out, Q7);
  and and_28 (and_28_out, S1, S0, I_O6);
  and and_29 (and_29_out, not_5_out, not_4_out, d_ff_as_7_q);
  and and_30 (and_30_out, d_ff_as_7_q, S0, not_5_out);
  and and_31 (and_31_out, S1, not_4_out, DSL);
  and and_32 (and_32_out, S1, S0, I_O7);
  and and_33 (and_33_out, not_5_out, not_4_out, Q7);
  or or_1 (or_1_out, and_2_out, and_3_out, and_4_out, and_5_out);
  or or_2 (or_2_out, and_6_out, and_7_out, and_8_out, and_9_out);
  or or_3 (or_3_out, and_10_out, and_11_out, and_12_out, and_13_out);
  or or_4 (or_4_out, and_14_out, and_15_out, and_16_out, and_17_out);
  or or_5 (or_5_out, and_18_out, and_19_out, and_20_out, and_21_out);
  or or_6 (or_6_out, and_22_out, and_23_out, and_24_out, and_25_out);
  or or_7 (or_7_out, and_26_out, and_27_out, and_28_out, and_29_out);
  or or_8 (or_8_out, and_30_out, and_31_out, and_32_out, and_33_out);
  D_FF_AS d_ff_as_1 (.Set(1'b0), .D(or_1_out), .C(CP), .Clr(not_3_out), .Q(Q0));  // open: nQ
  D_FF_AS d_ff_as_2 (.Set(1'b0), .D(or_2_out), .C(CP), .Clr(not_3_out), .Q(d_ff_as_2_q));  // open: nQ
  D_FF_AS d_ff_as_3 (.Set(1'b0), .D(or_3_out), .C(CP), .Clr(not_3_out), .Q(d_ff_as_3_q));  // open: nQ
  D_FF_AS d_ff_as_4 (.Set(1'b0), .D(or_4_out), .C(CP), .Clr(not_3_out), .Q(d_ff_as_4_q));  // open: nQ
  D_FF_AS d_ff_as_5 (.Set(1'b0), .D(or_5_out), .C(CP), .Clr(not_3_out), .Q(d_ff_as_5_q));  // open: nQ
  D_FF_AS d_ff_as_6 (.Set(1'b0), .D(or_6_out), .C(CP), .Clr(not_3_out), .Q(d_ff_as_6_q));  // open: nQ
  D_FF_AS d_ff_as_7 (.Set(1'b0), .D(or_7_out), .C(CP), .Clr(not_3_out), .Q(d_ff_as_7_q));  // open: nQ
  D_FF_AS d_ff_as_8 (.Set(1'b0), .D(or_8_out), .C(CP), .Clr(not_3_out), .Q(Q7));  // open: nQ
  assign I_O0 = and_1_out ? Q0 : 1'bz;  // Driver driver_1
  assign I_O1 = and_1_out ? d_ff_as_2_q : 1'bz;  // Driver driver_2
  assign I_O2 = and_1_out ? d_ff_as_3_q : 1'bz;  // Driver driver_3
  assign I_O3 = and_1_out ? d_ff_as_4_q : 1'bz;  // Driver driver_4
  assign I_O4 = and_1_out ? d_ff_as_5_q : 1'bz;  // Driver driver_5
  assign I_O5 = and_1_out ? d_ff_as_6_q : 1'bz;  // Driver driver_6
  assign I_O6 = and_1_out ? d_ff_as_7_q : 1'bz;  // Driver driver_7
  assign I_O7 = and_1_out ? Q7 : 1'bz;  // Driver driver_8

  // Notes on the sheet:
  //   DSR: pin 11
  //   S0: pin 1
  //   S1: pin 19
  //   nOE1: pin 2, default 1
  //   nOE2: pin 3, default 1
  //   CP: pin 12
  //   Q0: pin 8
  //   nMR: pin 9, default 1
  //   Q7: pin 17
  //   DSL: pin 18
  //   VCC: pin 20, default 1
  //   GND: pin 10
  //   I_O0: pin 7
  //   I_O1: pin 13
  //   I_O2: pin 6
  //   I_O3: pin 14
  //   I_O4: pin 5
  //   I_O5: pin 15
  //   I_O6: pin 4
  //   I_O7: pin 16
endmodule

/* Test case shift:
CP S1 S0 ~OE1 ~OE2 DSL I/O7 I/O6 I/O5 I/O4 I/O3 I/O2 I/O1 I/O0 DSR I/O7_out I/O6_out I/O5_out I/O4_out I/O3_out I/O2_out I/O1_out I/O0_out
# left
c  1  1    1    1   0   0    0    0    0    0    0    0    0    0   0 0 0 0 0 0 0 0
c  1  0    1    1   1   0    0    0    0    0    0    0    0    0   0 0 0 0 0 0 0 0
0  0  0    0    0   1   z    z    z    z    z    z    z    z    0   1 0 0 0 0 0 0 0
c  1  0    0    0   0   z    z    z    z    z    z    z    z    0   0 1 0 0 0 0 0 0
c  1  0    0    0   0   z    z    z    z    z    z    z    z    0   0 0 1 0 0 0 0 0
c  1  0    0    0   0   z    z    z    z    z    z    z    z    0   0 0 0 1 0 0 0 0
c  1  0    0    0   0   z    z    z    z    z    z    z    z    0   0 0 0 0 1 0 0 0
c  1  0    0    0   0   z    z    z    z    z    z    z    z    0   0 0 0 0 0 1 0 0
c  1  0    0    0   0   z    z    z    z    z    z    z    z    0   0 0 0 0 0 0 1 0
c  1  0    0    0   0   z    z    z    z    z    z    z    z    0   0 0 0 0 0 0 0 1
c  1  0    0    0   0   z    z    z    z    z    z    z    z    0   0 0 0 0 0 0 0 0

# right
c  1  1    1    1   0   0    0    0    0    0    0    0    0    0   0 0 0 0 0 0 0 0
c  0  1    1    1   0   0    0    0    0    0    0    0    0    1   0 0 0 0 0 0 0 0
0  0  0    0    0   0   z    z    z    z    z    z    z    z    1   0 0 0 0 0 0 0 1
c  0  1    0    0   0   z    z    z    z    z    z    z    z    0   0 0 0 0 0 0 1 0
c  0  1    0    0   0   z    z    z    z    z    z    z    z    0   0 0 0 0 0 1 0 0
c  0  1    0    0   0   z    z    z    z    z    z    z    z    0   0 0 0 0 1 0 0 0
c  0  1    0    0   0   z    z    z    z    z    z    z    z    0   0 0 0 1 0 0 0 0
c  0  1    0    0   0   z    z    z    z    z    z    z    z    0   0 0 1 0 0 0 0 0
c  0  1    0    0   0   z    z    z    z    z    z    z    z    0   0 1 0 0 0 0 0 0
c  0  1    0    0   0   z    z    z    z    z    z    z    z    0   1 0 0 0 0 0 0 0
c  0  1    0    0   0   z    z    z    z    z    z    z    z    0   0 0 0 0 0 0 0 0
*/

/* Test case load:
CP S1 S0 ~MR ~OE1 ~OE2 DSL I/O7 I/O6 I/O5 I/O4 I/O3 I/O2 I/O1 I/O0 DSR I/O7_out I/O6_out I/O5_out I/O4_out I/O3_out I/O2_out I/O1_out I/O0_out
# load
c  1  1   1    1    1   0   1    1    1    1    1    1    1    1    0   1 1 1 1 1 1 1 1
0  0  0   1    1    1   0   z    z    z    z    z    z    z    z    0   z z z z z z z z
0  0  0   1    0    0   0   z    z    z    z    z    z    z    z    0   1 1 1 1 1 1 1 1

c  1  1   1    1    1   0   0    1    0    1    0    1    0    1    0   0 1 0 1 0 1 0 1
0  0  0   1    1    1   0   z    z    z    z    z    z    z    z    0   z z z z z z z z
0  0  0   1    0    0   0   z    z    z    z    z    z    z    z    0   0 1 0 1 0 1 0 1

c  1  1   1    1    1   0   1    0    1    0    1    0    1    0    0   1 0 1 0 1 0 1 0
0  0  0   1    1    1   0   z    z    z    z    z    z    z    z    0   z z z z z z z z
0  0  0   1    0    0   0   z    z    z    z    z    z    z    z    0   1 0 1 0 1 0 1 0

#clear
c  1  1   1    1    1   0   1    1    1    1    1    1    1    1    0   1 1 1 1 1 1 1 1
0  0  0   1    0    0   0   z    z    z    z    z    z    z    z    0   1 1 1 1 1 1 1 1
0  0  0   0    0    0   0   z    z    z    z    z    z    z    z    0   0 0 0 0 0 0 0 0
*/
