// Digital circuit 27c801.dig as structural Verilog
// 8 Mbit (1Mb x 8) UV EPROM
module _27c801 (
  input  nE,
  input  nG,
  input  VCC,
  input  GND,
  input  I_O0,
  input  I_O1,
  input  I_O2,
  input  I_O3,
  input  I_O4,
  input  I_O5,
  input  I_O6,
  input  I_O7,
  input  A0,
  input  A1,
  input  A2,
  input  A3,
  input  A4,
  input  A5,
  input  A6,
  input  A7,
  input  A8,
  input  A9,
  input  A10,
  input  A11,
  input  A12,
  input  A13,
  input  A14,
  input  A15,
  input  A16,
  input  A17,
  input  A18,
  input  A19
);

  wire nor_1_out;
  wire [7:0] rom_d;

  nor nor_1 (nor_1_out, nE, nG);
  PowerSupply powersupply_1 (.VDD(VCC), .GND(GND));
  ROM #(.AddrBits(20), .Bits(8)) rom (
    .A({A19, A18, A17, A16, A15, A14, A13, A12, A11, A10, A9, A8, A7, A6, A5, A4, A3, A2, A1, A0}),
    .sel(nor_1_out), .D(rom_d));
  BusSplitter #(.Bits(8)) bussplitter_1 (
    .D(rom_d), .OE(nor_1_out), .D0(I_O0), .D1(I_O1), .D2(I_O2), .D3(I_O3), .D4(I_O4), .D5(I_O5), .D6(I_O6),
    .D7(I_O7));

  // Notes on the sheet:
  //   nE: pin 22, default 1
  //   nG: pin 24, default 1
  //   VCC: pin 32, default 1
  //   GND: pin 16
  //   I_O0: pin 13
  //   I_O1: pin 14
  //   I_O2: pin 15
  //   I_O3: pin 17
  //   I_O4: pin 18
  //   I_O5: pin 19
  //   I_O6: pin 20
  //   I_O7: pin 21
  //   A0: pin 12
  //   A1: pin 11
  //   A2: pin 10
  //   A3: pin 9
  //   A4: pin 8
  //   A5: pin 7
  //   A6: pin 6
  //   A7: pin 5
  //   A8: pin 27
  //   A9: pin 26
  //   A10: pin 23
  //   A11: pin 25
  //   A12: pin 4
  //   A13: pin 28
  //   A14: pin 29
  //   A15: pin 3
  //   A16: pin 2
  //   A17: pin 30
  //   A18: pin 31
  //   A19: pin 1
endmodule
