// Digital circuit RAM32Bit.dig as structural Verilog
// A 32-bit memory that allows byte access and can handle non-aligned 
// memory addresses.
// {{de Ein 32-Bit-Speicher, der Bytezugriff ermöglicht und auch mit nicht 
// ausgerichteten Speicheradressen umgehen kann.}}
module RAM32Bit (
  input  [31:0] A,
  input  [31:0] D_in,
  input  we,
  input  [1:0] am,
  input  \signed ,
  input  C,
  output [31:0] D_out
);

  wire and_1_out, or_1_out, str_0, str_1, str_2, str_3;
  wire [7:0] D_0, D_1, D_2, D_3, R0_d, R1_d, R2_d, R3_d;
  wire [15:0] addr_plus_1, multiplexer_1_out, multiplexer_2_out, multiplexer_3_out;
  wire [31:0] outdatagen_inc_1_p7, outdatagen_inc_1_p8, outdatagen_inc_1_p9;

  strDataGen_inc strdatagen_inc_1 (.in(D_in), .sh(A[1:0]), .D_0(D_0), .D_1(D_1), .D_2(D_2), .D_3(D_3));
  Add #(.Bits(16), .generic("this.Bits=int(args.addrBits-2);")) add_1 (
    .a(16'h1), .b(A[17:2]), .c_i(1'b0), .s(addr_plus_1));  // open: c_o
  // strGen_inc strgen_inc_1: pin names not known; wires that end beside it: A[1:0], we, am, str_0, str_1, str_2, str_3
  or or_1 (or_1_out, A[0], A[1]);
  and and_1 (and_1_out, A[0], A[1]);
  Multiplexer #(.Bits(16), .generic("this.Bits=int(args.addrBits-2);")) multiplexer_1 (
    .sel(or_1_out), .in_0(A[17:2]), .in_1(addr_plus_1), .out(multiplexer_1_out));
  Multiplexer #(.Bits(16), .generic("this.Bits=int(args.addrBits-2);")) multiplexer_2 (
    .sel(A[1]), .in_0(A[17:2]), .in_1(addr_plus_1), .out(multiplexer_2_out));
  Multiplexer #(.Bits(16), .generic("this.Bits=int(args.addrBits-2);")) multiplexer_3 (
    .sel(and_1_out), .in_0(A[17:2]), .in_1(addr_plus_1), .out(multiplexer_3_out));
  RAMDualPort #(.AddrBits(16), .Bits(8), .generic("this.AddrBits=int(args.addrBits-2);")) R0 (
    .A(multiplexer_1_out), .Din(D_0), .str(str_0), .C(C), .ld(1'b1), .D(R0_d));
  RAMDualPort #(.AddrBits(16), .Bits(8), .generic("this.AddrBits=int(args.addrBits-2);")) R1 (
    .A(multiplexer_2_out), .Din(D_1), .str(str_1), .C(C), .ld(1'b1), .D(R1_d));
  RAMDualPort #(.AddrBits(16), .Bits(8), .generic("this.AddrBits=int(args.addrBits-2);")) R2 (
    .A(multiplexer_3_out), .Din(D_2), .str(str_2), .C(C), .ld(1'b1), .D(R2_d));
  RAMDualPort #(.AddrBits(16), .Bits(8), .generic("this.AddrBits=int(args.addrBits-2);")) R3 (
    .A(A[17:2]), .Din(D_3), .str(str_3), .C(C), .ld(1'b1), .D(R3_d));
  // outDataGen_inc outdatagen_inc_1: pin names not known; wires that end beside it: R0_d, R1_d, R2_d, R3_d, A[1:0], \signed , outdatagen_inc_1_p7, outdatagen_inc_1_p8, outdatagen_inc_1_p9
  Multiplexer #(.Selector_Bits(2), .Bits(32)) multiplexer_4 (
    .sel(am), .in_0(outdatagen_inc_1_p7), .in_1(outdatagen_inc_1_p8), .in_2(outdatagen_inc_1_p9),
    .in_3({32{1'b0}}), .out(D_out));

  // Other names for the same wires on the sheet: A_0 = A[0]; A_01[1:0] = A[1:0]; A_1 = A[1]; addr[15:0] = A[17:2]

  // Notes on the sheet:
  //   A: The address to use.
  //   {{de Die Adresse}}
  //   D_in: The data to store.
  //   {{de Die zu speichernden Daten}}
  //   D_out: The data output.
  //   {{de Der Datenausgang}}
  //   we: write enable
  //   {{de Schreiben einschalten}}, default 1
  //   am: The addressing mode.
  //   0: word;
  //   1: half word;
  //   2: byte
  //   {{de Der Adressierungsmodus
  //   0: word;
  //   1: half word;
  //   2: byte
  //   }}
  //   signed: if set, half words and bytes preserve sign.
  //   {{de Wenn gesetzt erhällt das Lesen von half words und bytes das Vorzeichen.}}
endmodule

/* Test case read:
A D_in       C am signed D_out

# 32 bit read
4 0x44332211 c  0   0    x
4 0          0  0   0    0x44332211
3 0          0  0   0    0x33221100
2 0          0  0   0    0x22110000
1 0          0  0   0    0x11000000
5 0          0  0   0    0x00443322
6 0          0  0   0    0x00004433
7 0          0  0   0    0x00000044

# 16 bit read unsigned
4 0x83828180 c  0   0    x
4 0          0  1   0    0x8180
3 0          0  1   0    0x8000
2 0          0  1   0    0x0000
5 0          0  1   0    0x8281
6 0          0  1   0    0x8382
7 0          0  1   0    0x0083

# 16 bit read signed
4 0          0  1   1    0xffff8180
3 0          0  1   1    0xffff8000
2 0          0  1   1    0x00000000
5 0          0  1   1    0xffff8281
6 0          0  1   1    0xffff8382
7 0          0  1   1    0x00000083

# 8 bit read
4 0          0  2   0    0x80
3 0          0  2   0    0x00
2 0          0  2   0    0x00
5 0          0  2   0    0x81
6 0          0  2   0    0x82
7 0          0  2   0    0x83

# 8 bit read signed
4 0          0  2   1    0xffffff80
3 0          0  2   1    0x00
2 0          0  2   1    0x00
5 0          0  2   1    0xffffff81
6 0          0  2   1    0xffffff82
7 0          0  2   1    0xffffff83
*/

/* Code that sets the parameters or builds the circuit:
addrBits := 8;
*/

/* Test case write:
A D_in       C am signed D_out

# 32 bit write
0 0          c  0   0    x
4 0          c  0   0    x
1 0x44332211 c  0   0    x
0 0          0  0   0    0x33221100
4 0          0  0   0    0x00000044

0 0          c  0   0    x
4 0          c  0   0    x
2 0x44332211 c  0   0    x
0 0          0  0   0    0x22110000
4 0          0  0   0    0x00004433

0 0          c  0   0    x
4 0          c  0   0    x
3 0x44332211 c  0   0    x
0 0          0  0   0    0x11000000
4 0          0  0   0    0x00443322

# 16 bit write
0 0          c  0   0    x
4 0          c  0   0    x
0 0x2211     c  1   0    x
0 0          0  0   0    0x00002211
1 0x3320     c  1   0    x
0 0          0  0   0    0x00332011
2 0x4430     c  1   0    x
0 0          0  0   0    0x44302011
3 0x5540     c  1   0    x
0 0          0  0   0    0x40302011
4 0          0  0   0    0x00000055

# 0 bit write
0 0          c  0   0    x
4 0          c  0   0    x
0 0x11       c  2   0    x
0 0          0  0   0    0x00000011
1 0x22       c  2   0    x
0 0          0  0   0    0x00002211
2 0x33       c  2   0    x
0 0          0  0   0    0x00332211
3 0x44       c  2   0    x
0 0          0  0   0    0x44332211
*/
