// Digital circuit outDataGen-inc.dig as structural Verilog
// Rotates the output bytes to the right order.
// {{de rotiert die Ausgabebytes in die richtige Reihenfolge.}}
module outDataGen_inc (
  input  [7:0] in_0,
  input  [7:0] in_1,
  input  [7:0] in_2,
  input  [7:0] in_3,
  input  [1:0] sh,
  input  sign,
  output [31:0] D_32,
  output [31:0] D_16,
  output [31:0] D_8
);

  wire [31:0] bitextender_1_out, bitextender_2_out;

  Multiplexer #(.Selector_Bits(2), .Bits(32)) multiplexer_1 (
    .sel(sh), .in_0({in_3, in_2, in_1, in_0}), .in_1({in_0, in_3, in_2, in_1}),
    .in_2({in_1, in_0, in_3, in_2}), .in_3({in_2, in_1, in_0, in_3}), .out(D_32));
  BitExtender #(.inputBits(16), .outputBits(32)) bitextender_1 (.in(D_32[15:0]), .out(bitextender_1_out));
  BitExtender #(.outputBits(32)) bitextender_2 (.in(D_32[7:0]), .out(bitextender_2_out));
  Multiplexer #(.Bits(32)) multiplexer_2 (
    .sel(sign), .in_0({{16{1'b0}}, D_32[15:0]}), .in_1(bitextender_1_out), .out(D_16));
  Multiplexer #(.Bits(32)) multiplexer_3 (
    .sel(sign), .in_0({{24{1'b0}}, D_32[7:0]}), .in_1(bitextender_2_out), .out(D_8));

  // Notes on the sheet:
  //   sign: signed output
endmodule
