// Digital circuit strDataGen-inc.dig as structural Verilog
// Rotates the bytes to match the correct ram components.
// {{de Rotiert die Bytes um die richtigen RAM bausteine zu beschreiben.}}
module strDataGen_inc (
  input  [31:0] in,
  input  [1:0] sh,
  output [7:0] D_0,
  output [7:0] D_1,
  output [7:0] D_2,
  output [7:0] D_3
);

  Multiplexer #(.Selector_Bits(2), .Bits(32)) multiplexer_1 (
    .sel(sh), .in_0(in), .in_1({in[23:0], in[31:24]}), .in_2({in[15:0], in[31:16]}),
    .in_3({in[7:0], in[31:8]}), .out({D_3, D_2, D_1, D_0}));
endmodule
