// Digital circuit strGen-inc.dig as structural Verilog
// Creates the four store enable signals.
// {{de Erzeugt die vier Speicherfreigaben für die RAMs.}}
module strGen_inc (
  input  [1:0] sh,
  input  we,
  input  [1:0] am,
  output str_0,
  output str_1,
  output str_2,
  output str_3
);

  wire [3:0] multiplexer_1_out, multiplexer_2_out;

  Multiplexer #(.Selector_Bits(2), .Bits(4)) multiplexer_1 (
    .sel(am), .in_0(4'b1111), .in_1(4'b0011), .in_2(4'b0001), .in_3(4'b0000), .out(multiplexer_1_out));
  Multiplexer #(.Selector_Bits(2), .Bits(4)) multiplexer_2 (
    .sel(sh), .in_0(multiplexer_1_out), .in_1({multiplexer_1_out[2:0], multiplexer_1_out[3]}),
    .in_2({multiplexer_1_out[1:0], multiplexer_1_out[3:2]}),
    .in_3({multiplexer_1_out[0], multiplexer_1_out[3:1]}), .out(multiplexer_2_out));
  Multiplexer #(.Bits(4)) multiplexer_3 (
    .sel(we), .in_0(4'b0000), .in_1(multiplexer_2_out), .out({str_3, str_2, str_1, str_0}));
endmodule
