// Digital circuit BillieJean.dig as structural Verilog
module BillieJean (
  input  C
);

  wire comparator_1_eq, demultiplexer_1_out_0, demultiplexer_1_out_1, demultiplexer_1_out_2,
       demultiplexer_1_out_3, demultiplexer_1_out_4, demultiplexer_1_out_5, demultiplexer_1_out_6,
       demultiplexer_1_out_7, OnOff, PC;
  wire [6:0] Key, Vol;
  wire [13:0] Event_out;
  wire [16:0] Main_out;
  wire [35:14] rom_1_d;

  Counter #(.Bits(14)) Event (.en(comparator_1_eq), .C(~C), .clr(1'b0), .out(Event_out));  // open: ovf
  Counter #(.Bits(17)) Main (.en(1'b1), .C(~C), .clr(1'b0), .out(Main_out));  // open: ovf
  ROM #(.AddrBits(14), .Bits(36)) rom_1 (
    .A(Event_out), .sel(1'b1), .D({rom_1_d[35:19], PC, OnOff, rom_1_d[16:14], Vol, Key}));
  Comparator #(.Bits(17)) comparator_1 (.a(rom_1_d[35:19]), .b(Main_out), .eq(comparator_1_eq));  // open: gt, lt
  Demultiplexer #(.Selector_Bits(3)) demultiplexer_1 (
    .sel(rom_1_d[16:14]), .in(comparator_1_eq), .out_0(demultiplexer_1_out_0), .out_1(demultiplexer_1_out_1),
    .out_2(demultiplexer_1_out_2), .out_3(demultiplexer_1_out_3), .out_4(demultiplexer_1_out_4),
    .out_5(demultiplexer_1_out_5), .out_6(demultiplexer_1_out_6), .out_7(demultiplexer_1_out_7));
  // MIDI #(.midiProgChange("true"), .midiInstrument("Accordion")) midi_1: pin names not known; wires that end beside it: Key, Vol, OnOff, PC, demultiplexer_1_out_0, C
  // MIDI #(.midiProgChange("true"), .midiInstrument("Accordion"), .midiChannel(3)) midi_2: pin names not known; wires that end beside it: Key, Vol, OnOff, PC, demultiplexer_1_out_2, C
  // MIDI #(.midiProgChange("true"), .midiInstrument("Accordion"), .midiChannel(5)) midi_3: pin names not known; wires that end beside it: Key, Vol, OnOff, PC, demultiplexer_1_out_4, C
  // MIDI #(.midiProgChange("true"), .midiInstrument("Accordion"), .midiChannel(7)) midi_4: pin names not known; wires that end beside it: Key, Vol, OnOff, PC, demultiplexer_1_out_6, C
  // MIDI #(.midiProgChange("true"), .midiInstrument("Accordion"), .midiChannel(2)) midi_5: pin names not known; wires that end beside it: Key, Vol, OnOff, PC, demultiplexer_1_out_1, C
  // MIDI #(.midiProgChange("true"), .midiInstrument("Accordion"), .midiChannel(4)) midi_6: pin names not known; wires that end beside it: Key, Vol, OnOff, PC, demultiplexer_1_out_3, C
  // MIDI #(.midiProgChange("true"), .midiInstrument("Accordion"), .midiChannel(6)) midi_7: pin names not known; wires that end beside it: Key, Vol, OnOff, PC, demultiplexer_1_out_5, C
  // MIDI #(.midiProgChange("true"), .midiInstrument("Accordion"), .midiChannel(10)) midi_8: pin names not known; wires that end beside it: Key, Vol, OnOff, PC, demultiplexer_1_out_7, C

  // Notes on the sheet:
  //   C: Hz: 400
  //   Michael Jackson's
  //   Billie Jean
  //   {{de Michael Jackson's
  //   Billie Jean
  //   }}
  //   contents of rom_1 (hex, n*v repeats v):
  //   fc000,1060035,10e4005,116801b,11ec031,1270007,12f4032,1378023,e8380bc,e8980bc,1003f4a4,
  //   100bdb2a,1061db2a,1069f4a4,1303e2aa,1361e2aa,1603f8a8,160bd8aa,1661d8aa,1669f8a8,
  //   1903e7aa,1961e7aa,1c03f4a4,1c0bd72a,1c61d72a,1c69f4a4,1f03e52a,1f61e52a,2203f8a8,
  //   220bd72a,2261d72a,2269f8a8,2503e7aa,2561e7aa,2803f4a4,280bd52a,2861d52a,2869f4a4,
  //   2b03e2aa,2b61e2aa,2e03f828,2e0bdb2a,2e61db2a,2e69f828,3103e52a,3161e52a,3403f4a4,
  //   340bdcaa,3461dcaa,3469f4a4,3703e2aa,3761e2aa,3a03f8a8,3a0bdcaa,3a61dcaa,3a69f8a8,
  //   3d03e7aa,3d61e7aa,40033a9e,400bbfaa,4013f4a4,401bdb2a,4023df52,4061df52,4069db2a,
  //   4071f4a4,4191bfaa,43013a9e,430bbfa5,4313e2aa,431bdbd2,4361dbd2,4369e2aa,44a1bfa5,
  //   4603bfa8,460bf8a8,4613d8aa,461bdbd2,4661dbd2,4669d8aa,4671f8a8,47b9bfa8,49033a9e,
  //   490bbfaa,4913e7aa,491bd9d2,4961d9d2,4969e7aa,4a99bfaa,4c013a9e,4c0bbfa8,4c13f4a4,
  //   4c1bd72a,4c23dd52,4c61dd52,4c69d72a,4c71f4a4,4dc1bfa8,4f03bfa5,4f0be52a,4f13d7d2,
  //   4f61d7d2,4f69e52a,5099bfa5,5203bfa3,520bf8a8,5213d72a,521bdf52,5261df52,5269d72a,
  //   5271f8a8,53e9bfa3,5503bfa5,550be7aa,5513dd52,5561dd52,5569e7aa,56b1bfa5,58033a9e,
  //   580bbfaa,5813f4a4,581bd52a,5823dc52,5861dc52,5869d52a,5871f4a4,5979bfaa,5b013a9e,
  //   5b0bbfa5,5b13e2aa,5b1bd752,5b61d752,5b69e2aa,5c81bfa5,5e03bfa8,5e0bf828,5e13db2a,
  //   5e1be052,5e61e052,5e69db2a,5e71f828,5fa9bfa8,61033a9e,610bbfaa,6113e52a,611bdad2,
  //   6161dad2,6169e52a,6271bfaa,64013a9e,640bbfa8,6413f4a4,641bdcaa,6423df52,6461df52,
  //   6469dcaa,6471f4a4,65d9bfa8,6703bfa5,670be2aa,6713de52,6761de52,6769e2aa,68b1bfa5,
  //   6a03bfa3,6a0bf8a8,6a13dcaa,6a1be252,6a61e252,6a69dcaa,6a71f8a8,6c09bfa3,6d03bfa5,
  //   6d0be7aa,6d13d952,6d61d952,6d69e7aa,6e99bfa5,70033a9e,700bbfaa,7013f4a4,701bdb2a,
  //   7023e252,7061e252,7069db2a,7071f4a4,7191bfaa,73013a9e,730bbfa5,7313e2aa,731bdd52,
  //   7361dd52,7369e2aa,74a1bfa5,7603bfa8,760bf8a8,7613d8aa,761be152,7661e152,7669d8aa,
  //   7671f8a8,77b9bfa8,79033a9e,790bbfaa,7913e7aa,791bde52,7961de52,7969e7aa,7a99bfaa,
  //   7c013a9e,7c0bbfa8,7c13f4a4,7c1bd72a,7c23dc52,7c61dc52,7c69d72a,7c71f4a4,7dc1bfa8,
  //   7f03bfa5,7f0be52a,7f13de52,7f61de52,7f69e52a,8099bfa5,8203bfa3,820bf8a8,8213d72a,
  //   821be052,8261e052,8269d72a,8271f8a8,83e9bfa3,8503bfa5,850be7aa,8513f245,851be052,
  //   8561e052,8569f245,8571e7aa,86b1bfa5,88033a9e,880bbfaa,8813f4a4,881bd52a,8823f8c5,
  //   882be152,8861e152,8869f8c5,8871d52a,8879f4a4,8979bfaa,8b013a9e,8b0bbfa5,8b13e2aa,
  //   8b1bfac5,8b23e052,8b61e052,8b69fac5,8b71e2aa,8c81bfa5,8e03bfa8,8e0bf828,8e13db2a,
  //   8e1beec5,8e23df52,8e61df52,8e69eec5,8e71db2a,8e79f828,8fa9bfa8,91033a9e,910bbfaa,
  //   9113e52a,911be052,9123e845,9161e052,9169e52a,9181e845,9271bfaa,94013a9e,940bbfa8,
  //   9413f4a4,941bdcaa,9423e052,9461e052,9469dcaa,9471f4a4,95d9bfa8,9703bfa5,970be2aa,
  //   9713e252,9761e252,9769e2aa,98b1bfa5,9a03bfa3,9a0bf8a8,9a13dcaa,9a1bdf52,9a61df52,
  //   9a69dcaa,9a71f8a8,9c09bfa3,9d03bfa5,9d0be7aa,9d13e052,9d61e052,9d69e7aa,9e99bfa5,
  //   a0033a9e,a00bbfaa,a013f4a4,a01bdb2a,a023df52,a061df52,a069db2a,a071f4a4,a191bfaa,
  //   a3013a9e,a30bbfa5,a313e2aa,a31bdbd2,a361dbd2,a369e2aa,a4a1bfa5,a603bfa8,a60bf8a8,
  //   a613d8aa,a61bdbd2,a661dbd2,a669d8aa,a671f8a8,a7b9bfa8,a9033a9e,a90bbfaa,a913e7aa,
  //   a91bd9d2,a961d9d2,a969e7aa,aa99bfaa,ac013a9e,ac0bbfa8,ac13f4a4,ac1bd72a,ac23dd52,
  //   ac61dd52,ac69d72a,ac71f4a4,adc1bfa8,af03bfa5,af0be52a,af13d7d2,af61d7d2,af69e52a,
  //   b099bfa5,b203bfa3,b20bf8a8,b213d72a,b21bdf52,b261df52,b269d72a,b271f8a8,b3e9bfa3,
  //   b503bfa5,b50be7aa,b513dd52,b561dd52,b569e7aa,b6b1bfa5,b8033a9e,b80bbfaa,b813f4a4,
  //   b81bd52a,b823dc52,b861dc52,b869d52a,b871f4a4,b979bfaa,bb013a9e,bb0bbfa5,bb13e2aa,
  //   bb1bd752,bb61d752,bb69e2aa,bc81bfa5,be03bfa8,be0bf828,be13db2a,be1be052,be61e052,
  //   be69db2a,be71f828,bfa9bfa8,c1033a9e,c10bbfaa,c113e52a,c11bdad2,c161dad2,c169e52a,
  //   c271bfaa,c4013a9e,c40bbfa8,c413f4a4,c41bdcaa,c423df52,c461df52,c469dcaa,c471f4a4,
  //   c5d9bfa8,c703bfa5,c70be2aa,c713de52,c761de52,c769e2aa,c8b1bfa5,ca03bfa3,ca0bf8a8,
  //   ca13dcaa,ca1be252,ca61e252,ca69dcaa,ca71f8a8,cc09bfa3,cd03bfa5,cd0be7aa,cd13d952,
  //   cd61d952,cd69e7aa,ce99bfa5,d0033a9e,d00bbfaa,d013f4a4,d01bdb2a,d023e252,d061e252,
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endmodule
