// Digital circuit DebugExample.dig as structural Verilog
module DebugExample (
  input  clk
);

  wire [7:0] counter_1_out;

  Counter #(.Bits(8)) counter_1 (.en(1'b1), .C(clk), .clr(1'b0), .out(counter_1_out));  // open: ovf
  Seven_Seg_Hex seven_seg_hex_1 (.d(counter_1_out[7:4]), .dp(1'b0));
  Seven_Seg_Hex seven_seg_hex_2 (.d(counter_1_out[3:0]), .dp(1'b0));
  Break A (.brk(counter_1_out[2]));
  Break B (.brk(counter_1_out[4]));
endmodule
