// Digital circuit MIDIexample.dig as structural Verilog
module MIDIexample (
  input  [6:0] Vol,
  input  C
);

  wire d_ff_1_nq, d_ff_1_q;
  wire [5:0] counter_1_out;
  wire [6:0] add_1_s;

  D_FF d_ff_1 (.D(d_ff_1_nq), .C(C), .Q(d_ff_1_q), .nQ(d_ff_1_nq));
  Counter #(.Bits(6)) counter_1 (.en(d_ff_1_q), .C(C), .clr(1'b0), .out(counter_1_out));  // open: ovf
  Add #(.Bits(7)) add_1 (.a({1'b0, counter_1_out}), .b(7'b0011110), .c_i(1'b0), .s(add_1_s));  // open: c_o
  // MIDI #(.midiInstrument("Accordion")) midi_1: pin names not known; wires that end beside it: add_1_s, Vol, d_ff_1_nq, 1'b1, C

  // Notes on the sheet:
  //   Vol: default 127
  //   C: Hz: 15
endmodule
