// Digital circuit Telnet.dig as structural Verilog
module Telnet (
  input  clk
);

  wire keyboard_1_av, telnet_1_av, telnet_1_out;
  wire [15:0] keyboard_1_d;

  Keyboard keyboard_1 (.C(clk), .en(keyboard_1_av), .D(keyboard_1_d), .av(keyboard_1_av));
  Telnet #(.port(2323)) telnet_1 (
    .in(keyboard_1_d[7:0]), .C(clk), .wr(keyboard_1_av), .rd(telnet_1_av), .out(telnet_1_out),
    .av(telnet_1_av));
  Terminal terminal_1 (.D(telnet_1_out), .C(clk), .en(telnet_1_av));

  // Notes on the sheet:
  //   clk: Hz: 20
endmodule
