// Digital circuit and.dig as structural Verilog
module \and  (
  input  B,
  input  A,
  output Y
);

  wire nfet_1_s, pullup_1_out;

  PullUp pullup_1 (.out(pullup_1_out));
  NFET nfet_1 (.G(A), .D(pullup_1_out), .S(nfet_1_s));
  NFET nfet_2 (.G(B), .D(nfet_1_s), .S(1'b0));
  PullUp pullup_2 (.out(Y));
  NFET nfet_3 (.G(pullup_1_out), .D(Y), .S(1'b0));
endmodule

/* Test case:
A B Y
0 0 0
0 1 0
1 0 0
1 1 1
*/
