// Digital circuit andNmos.dig as structural Verilog
module andNmos (
  input  B,
  input  A,
  output Y
);

  wire pullup_1_out, T1_s;

  PullUp pullup_1 (.out(pullup_1_out));
  NFET T1 (.G(A), .D(pullup_1_out), .S(T1_s));
  NFET T2 (.G(B), .D(T1_s), .S(1'b0));
  PullUp pullup_2 (.out(Y));
  NFET T3 (.G(pullup_1_out), .D(Y), .S(1'b0));
endmodule

/* Test case:
A B Y
0 0 0
0 1 0
1 0 0
1 1 1
*/
