// Digital circuit inverter.dig as structural Verilog
module inverter (
  input  A,
  output Y
);

  PullUp pullup_1 (.out(Y));
  NFET nfet_1 (.G(A), .D(Y), .S(1'b0));
endmodule

/* Test case:
A Y
0 1
1 0
*/
