// Digital circuit nandNmos.dig as structural Verilog
module nandNmos (
  input  B,
  input  A,
  output Y
);

  wire nfet_1_s;

  PullUp pullup_1 (.out(Y));
  NFET nfet_1 (.G(A), .D(Y), .S(nfet_1_s));
  NFET nfet_2 (.G(B), .D(nfet_1_s), .S(1'b0));
endmodule

/* Test case:
A B Y
0 0 1
0 1 1
1 0 1
1 1 0
*/
