// Digital circuit nor.dig as structural Verilog
module \nor  (
  input  B,
  input  A,
  output Y
);

  PullUp pullup_1 (.out(Y));
  NFET nfet_1 (.G(A), .D(Y), .S(1'b0));
  NFET nfet_2 (.G(B), .D(Y), .S(1'b0));
endmodule

/* Test case:
A B Y
0 0 1
0 1 0
1 0 0
1 1 0
*/
