// Digital circuit xor.dig as structural Verilog
module \xor  (
  input  A,
  input  B,
  output Y
);

  wire nfet_1_d;

  NFET #(.unidirectional("true")) nfet_1 (.G(A), .D(nfet_1_d), .S(B));
  NFET #(.unidirectional("true")) nfet_2 (.G(B), .D(nfet_1_d), .S(A));
  PullUp pullup_1 (.out(nfet_1_d));
  PullUp pullup_2 (.out(Y));
  NFET nfet_3 (.G(nfet_1_d), .D(Y), .S(1'b0));
endmodule

/* Test case simple:
A B Y
0 0 0
0 1 1
1 0 1
1 1 0
*/

/* Test case trans:
A B Y
0 0 0
0 1 1
1 0 1
1 1 0




# transitions
0 0 0
0 1 1
0 0 0
1 0 1
0 0 0
1 1 0
0 0 0
0 1 1
1 0 1
0 1 1
1 1 0
0 1 1
1 0 1
1 1 0
1 0 1
*/
