// Digital circuit PLA.dig as structural Verilog
// Typischer PLA Baustein mit einer UND und einer 
// ODER Matrix.
// Programmiert wird der Baustein
// über die Dioden, die "durchgebrannt" bzw. 
// Programmiert werden können. Zur Vereinfachung 
// können die Dioden mit der Taste [P] programmiert 
// werden.
module PLA (
  input  A,
  input  B,
  input  C,
  input  D,
  output Y_0,
  output Y_1,
  output Y_2,
  output Y_3
);

  wire diodebackward_1_out, diodebackward_3_out, diodebackward_5_out, diodebackward_7_out,
       diodebackward_9_out, diodebackward_11_out, not_1_out, not_2_out, not_3_out, not_4_out;

  not not_1 (not_1_out, A);
  DiodeBackward diodebackward_1 (.in(A), .out(diodebackward_1_out));
  DiodeBackward #(.Blown("true")) diodebackward_2 (.in(not_1_out), .out(diodebackward_1_out));
  DiodeBackward #(.Blown("true")) diodebackward_3 (.in(A), .out(diodebackward_3_out));
  DiodeBackward diodebackward_4 (.in(not_1_out), .out(diodebackward_3_out));
  DiodeBackward #(.Blown("true")) diodebackward_5 (.in(A), .out(diodebackward_5_out));
  DiodeBackward #(.Blown("true")) diodebackward_6 (.in(not_1_out), .out(diodebackward_5_out));
  DiodeBackward diodebackward_7 (.in(A), .out(diodebackward_7_out));
  DiodeBackward #(.Blown("true")) diodebackward_8 (.in(not_1_out), .out(diodebackward_7_out));
  DiodeBackward #(.Blown("true")) diodebackward_9 (.in(A), .out(diodebackward_9_out));
  DiodeBackward #(.Blown("true")) diodebackward_10 (.in(not_1_out), .out(diodebackward_9_out));
  DiodeBackward diodebackward_11 (.in(A), .out(diodebackward_11_out));
  DiodeBackward diodebackward_12 (.in(not_1_out), .out(diodebackward_11_out));
  not not_2 (not_2_out, B);
  DiodeBackward #(.Blown("true")) diodebackward_13 (.in(B), .out(diodebackward_1_out));
  DiodeBackward diodebackward_14 (.in(not_2_out), .out(diodebackward_1_out));
  DiodeBackward diodebackward_15 (.in(B), .out(diodebackward_3_out));
  DiodeBackward #(.Blown("true")) diodebackward_16 (.in(not_2_out), .out(diodebackward_3_out));
  DiodeBackward #(.Blown("true")) diodebackward_17 (.in(B), .out(diodebackward_5_out));
  DiodeBackward #(.Blown("true")) diodebackward_18 (.in(not_2_out), .out(diodebackward_5_out));
  DiodeBackward #(.Blown("true")) diodebackward_19 (.in(B), .out(diodebackward_7_out));
  DiodeBackward #(.Blown("true")) diodebackward_20 (.in(not_2_out), .out(diodebackward_7_out));
  DiodeBackward #(.Blown("true")) diodebackward_21 (.in(B), .out(diodebackward_9_out));
  DiodeBackward #(.Blown("true")) diodebackward_22 (.in(not_2_out), .out(diodebackward_9_out));
  DiodeBackward diodebackward_23 (.in(B), .out(diodebackward_11_out));
  DiodeBackward diodebackward_24 (.in(not_2_out), .out(diodebackward_11_out));
  not not_3 (not_3_out, C);
  DiodeBackward #(.Blown("true")) diodebackward_25 (.in(C), .out(diodebackward_1_out));
  DiodeBackward #(.Blown("true")) diodebackward_26 (.in(not_3_out), .out(diodebackward_1_out));
  DiodeBackward #(.Blown("true")) diodebackward_27 (.in(C), .out(diodebackward_3_out));
  DiodeBackward #(.Blown("true")) diodebackward_28 (.in(not_3_out), .out(diodebackward_3_out));
  DiodeBackward diodebackward_29 (.in(C), .out(diodebackward_5_out));
  DiodeBackward #(.Blown("true")) diodebackward_30 (.in(not_3_out), .out(diodebackward_5_out));
  DiodeBackward #(.Blown("true")) diodebackward_31 (.in(C), .out(diodebackward_7_out));
  DiodeBackward #(.Blown("true")) diodebackward_32 (.in(not_3_out), .out(diodebackward_7_out));
  DiodeBackward diodebackward_33 (.in(C), .out(diodebackward_9_out));
  DiodeBackward #(.Blown("true")) diodebackward_34 (.in(not_3_out), .out(diodebackward_9_out));
  DiodeBackward diodebackward_35 (.in(C), .out(diodebackward_11_out));
  DiodeBackward diodebackward_36 (.in(not_3_out), .out(diodebackward_11_out));
  not not_4 (not_4_out, D);
  DiodeBackward #(.Blown("true")) diodebackward_37 (.in(D), .out(diodebackward_1_out));
  DiodeBackward #(.Blown("true")) diodebackward_38 (.in(not_4_out), .out(diodebackward_1_out));
  DiodeBackward #(.Blown("true")) diodebackward_39 (.in(D), .out(diodebackward_3_out));
  DiodeBackward #(.Blown("true")) diodebackward_40 (.in(not_4_out), .out(diodebackward_3_out));
  DiodeBackward diodebackward_41 (.in(D), .out(diodebackward_5_out));
  DiodeBackward #(.Blown("true")) diodebackward_42 (.in(not_4_out), .out(diodebackward_5_out));
  DiodeBackward #(.Blown("true")) diodebackward_43 (.in(D), .out(diodebackward_7_out));
  DiodeBackward #(.Blown("true")) diodebackward_44 (.in(not_4_out), .out(diodebackward_7_out));
  DiodeBackward #(.Blown("true")) diodebackward_45 (.in(D), .out(diodebackward_9_out));
  DiodeBackward #(.Blown("true")) diodebackward_46 (.in(not_4_out), .out(diodebackward_9_out));
  DiodeBackward diodebackward_47 (.in(D), .out(diodebackward_11_out));
  DiodeBackward diodebackward_48 (.in(not_4_out), .out(diodebackward_11_out));
  PullUp pullup_1 (.out(diodebackward_1_out));
  PullUp pullup_2 (.out(diodebackward_3_out));
  PullUp pullup_3 (.out(diodebackward_5_out));
  PullUp pullup_4 (.out(diodebackward_7_out));
  PullUp pullup_5 (.out(diodebackward_9_out));
  PullUp pullup_6 (.out(diodebackward_11_out));
  // DiodeForeward diodeforeward_1: pin names not known; wires that end beside it: diodebackward_1_out, Y_0
  // DiodeForeward diodeforeward_2: pin names not known; wires that end beside it: diodebackward_3_out, Y_0
  // DiodeForeward #(.Blown("true")) diodeforeward_3: pin names not known; wires that end beside it: diodebackward_5_out, Y_0
  // DiodeForeward #(.Blown("true")) diodeforeward_4: pin names not known; wires that end beside it: diodebackward_7_out, Y_0
  // DiodeForeward #(.Blown("true")) diodeforeward_5: pin names not known; wires that end beside it: diodebackward_9_out, Y_0
  // DiodeForeward diodeforeward_6: pin names not known; wires that end beside it: diodebackward_11_out, Y_0
  PullDown pulldown_1 (.out(Y_0));
  // DiodeForeward #(.Blown("true")) diodeforeward_7: pin names not known; wires that end beside it: diodebackward_1_out, Y_1
  // DiodeForeward #(.Blown("true")) diodeforeward_8: pin names not known; wires that end beside it: diodebackward_3_out, Y_1
  // DiodeForeward diodeforeward_9: pin names not known; wires that end beside it: diodebackward_5_out, Y_1
  // DiodeForeward #(.Blown("true")) diodeforeward_10: pin names not known; wires that end beside it: diodebackward_7_out, Y_1
  // DiodeForeward #(.Blown("true")) diodeforeward_11: pin names not known; wires that end beside it: diodebackward_9_out, Y_1
  // DiodeForeward diodeforeward_12: pin names not known; wires that end beside it: diodebackward_11_out, Y_1
  PullDown pulldown_2 (.out(Y_1));
  // DiodeForeward #(.Blown("true")) diodeforeward_13: pin names not known; wires that end beside it: diodebackward_1_out, Y_2
  // DiodeForeward #(.Blown("true")) diodeforeward_14: pin names not known; wires that end beside it: diodebackward_3_out, Y_2
  // DiodeForeward diodeforeward_15: pin names not known; wires that end beside it: diodebackward_5_out, Y_2
  // DiodeForeward diodeforeward_16: pin names not known; wires that end beside it: diodebackward_7_out, Y_2
  // DiodeForeward #(.Blown("true")) diodeforeward_17: pin names not known; wires that end beside it: diodebackward_9_out, Y_2
  // DiodeForeward diodeforeward_18: pin names not known; wires that end beside it: diodebackward_11_out, Y_2
  PullDown pulldown_3 (.out(Y_2));
  // DiodeForeward #(.Blown("true")) diodeforeward_19: pin names not known; wires that end beside it: diodebackward_1_out, Y_3
  // DiodeForeward #(.Blown("true")) diodeforeward_20: pin names not known; wires that end beside it: diodebackward_3_out, Y_3
  // DiodeForeward #(.Blown("true")) diodeforeward_21: pin names not known; wires that end beside it: diodebackward_5_out, Y_3
  // DiodeForeward diodeforeward_22: pin names not known; wires that end beside it: diodebackward_7_out, Y_3
  // DiodeForeward diodeforeward_23: pin names not known; wires that end beside it: diodebackward_9_out, Y_3
  // DiodeForeward diodeforeward_24: pin names not known; wires that end beside it: diodebackward_11_out, Y_3
  PullDown pulldown_4 (.out(Y_3));

  // Notes on the sheet:
  //   A: Erster frei konfigurierbarer Eingang.
  //   B: Zweiter frei konfigurierbarer Eingang.
  //   C: Dritter frei konfigurierbarer Eingang.
  //   D: Vierter frei konfigurierbarer Eingang.
  //   Y_0: Das 0. Ausgangsbit.
  //   Y_1: Das 1. Ausgangsbit.
  //   Y_2: Das 2. Ausgangsbit.
  //   Y_3: Das 3. Ausgangsbit.
endmodule

/* Test case Y_0=A xor B:
# y_0 = A xor B

A B C D  Y_0
0 0 x x  0 
0 1 x x  1 
1 0 x x  1 
1 1 x x  0 
*/

/* Test case Y_1 = C and D:
# y_1 = C and D

A B C D  Y_1
x x 0 0   0
x x 0 1   0
x x 1 0   0
x x 1 1   1
*/

/* Test case Y_2 = A or (C and D):
# Y_2 = A or (C and D)

A B C D  Y_2
0 x 0 0   0  
0 x 0 1   0  
0 x 1 0   0   
0 x 1 1   1   
1 x 0 0   1  
1 x 0 1   1  
1 x 1 0   1   
1 x 1 1   1   
*/

/* Test case Y_3 = A or C:
# y_3 = A or C

A B C D  Y_3
0 x 0 x   0
0 x 1 x   1
1 x 0 x   1
1 x 1 x   1
*/
