// Digital circuit WiredAnd.dig as structural Verilog
// So-called Wired-AND. An AND gate which is constructed 
// with diodes and a pull-up resistor.
// {{de Sogenanntes Wired-AND. Ein Und-Gatter welches 
// mit Dioden und einem Pull-Up Widerstand 
// aufgebaut ist.}}
module WiredAnd (
  input  A,
  input  B,
  output Y
);

  DiodeBackward diodebackward_1 (.in(A), .out(Y));
  DiodeBackward diodebackward_2 (.in(B), .out(Y));
  PullUp pullup_1 (.out(Y));

  // Notes on the sheet:
  //   A: First input of the AND gate.
  //   {{de Erster Eingang des AND-Gatters.}}
  //   B: Second input of the AND gate.
  //   {{de Zweiter Eingang des AND-Gatters.}}
  //   Y: The output of the AND gate.
  //   {{de Das Ergebnis der Und-Verknüpfung.}}
endmodule

/* Test case:
A B Y
0 0 0
0 1 0
0 Z 0
1 0 0
1 1 1
1 Z 1
Z 0 0
Z 1 1
Z Z 1
*/
