// Digital circuit WiredOr.dig as structural Verilog
// So-called Wired OR. An OR gate which is constructed with 
// diodes and a pull-down resistor.
// {{de Sogenanntes Wired-OR. Ein Oder-Gatter welches 
// mit Dioden und einem Pull-Down Widerstand 
// aufgebaut ist.}}
module WiredOr (
  input  A,
  input  B,
  output Y
);

  DiodeForward diodeforward_1 (.in(A), .out(Y));
  DiodeForward diodeforward_2 (.in(B), .out(Y));
  PullDown pulldown_1 (.out(Y));

  // Notes on the sheet:
  //   A: First input of the OR gate.
  //   {{de Erster Eingang des OR-Gatters.}}
  //   B: Second input of the OR gate.
  //   {{de Zweiter Eingang des OR-Gatters.}}
  //   Y: The output of the OR gate.
  //   {{de Das Ergebnis der OR-Verknüpfung.}}
endmodule

/* Test case:
A B Y
0 0 0
0 1 1
0 Z 0
1 0 1
1 1 1
1 Z 1
Z 0 0
Z 1 1
Z Z 0
*/
