// Digital circuit ALU.dig as structural Verilog
// Arithmetic Logical unit.
// Performs all arithmetic operations.
// Used for arithmetic processor instructions as well as for 
// calculating memory addresses.
// {{de Arithmetisch Logische Einheit. 
// Führt alle arithmetischen Operationen durch. 
// Wird sowohl für arithmetische Prozessorbefehle 
// als auch für die Berechnung der Adressen 
// bei der Speicheradressierung verwendet.}}
module ALU (
  input  [15:0] A,
  input  [15:0] B,
  input  [4:0] Op,
  input  Ci,
  output [15:0] Y,
  output Zero,
  output Neg,
  output Carry
);

  wire add_1_c_o, and_1_out, asr_1_c, lsl_1_co, lsr_1_co, sub_1_c_o;
  wire [15:0] add_1_s, and_2_out, asr_1_do, lsl_1_do, lsr_1_do, neg_1_out, not_1_out, or_1_out, sub_1_s,
       swap_1_do, swapn_1_do, xor_1_out;
  wire [31:0] mul_1_mul;

  and and_1 (and_1_out, Op[4], Ci);
  Add #(.Bits(16)) add_1 (.a(A), .b(B), .c_i(and_1_out), .s(add_1_s), .c_o(add_1_c_o));
  Sub #(.Bits(16)) sub_1 (.a(A), .b(B), .c_i(and_1_out), .s(sub_1_s), .c_o(sub_1_c_o));
  assign and_2_out = A & B;  // And and_2, 16 bits wide
  assign or_1_out = A | B;  // Or or_1, 16 bits wide
  assign xor_1_out = A ^ B;  // XOr xor_1, 16 bits wide
  assign not_1_out = ~A;  // Not not_1, 16 bits wide
  Neg #(.Bits(16)) neg_1 (.in(A), .out(neg_1_out));
  LSL lsl_1 (.Di(A), .Ci(and_1_out), .Do(lsl_1_do), .Co(lsl_1_co));
  LSR lsr_1 (.Di(A), .Ci(and_1_out), .Do(lsr_1_do), .Co(lsr_1_co));
  ASR asr_1 (.Di(A), .C(asr_1_c), .Do(asr_1_do));
  SWAP swap_1 (.Di(A), .Do(swap_1_do));
  SWAPN swapn_1 (.Di(A), .Do(swapn_1_do));
  Mul #(.Bits(16)) mul_1 (.a(A), .b(B), .mul(mul_1_mul));
  Multiplexer #(.Selector_Bits(4)) multiplexer_1 (
    .sel(Op[3:0]), .in_0(1'b0), .in_1(add_1_c_o), .in_2(sub_1_c_o), .in_3(1'b0), .in_4(1'b0), .in_5(1'b0),
    .in_6(1'b0), .in_7(1'b0), .in_8(lsl_1_co), .in_9(lsr_1_co), .in_10(asr_1_c), .in_11(1'b0), .in_12(1'b0),
    .in_13(1'b0), .in_14(1'b0), .in_15(1'b0), .out(Carry));
  Multiplexer #(.Selector_Bits(4), .Bits(16)) multiplexer_2 (
    .sel(Op[3:0]), .in_0(B), .in_1(add_1_s), .in_2(sub_1_s), .in_3(and_2_out), .in_4(or_1_out),
    .in_5(xor_1_out), .in_6(not_1_out), .in_7(neg_1_out), .in_8(lsl_1_do), .in_9(lsr_1_do), .in_10(asr_1_do),
    .in_11(swap_1_do), .in_12(swapn_1_do), .in_13(mul_1_mul[15:0]), .in_14({16{1'b0}}), .in_15({16{1'b0}}),
    .out({Neg, Y[14:0]}));
  Comparator #(.Signed("true"), .Bits(16)) comparator_1 (
    .a({Neg, Y[14:0]}), .b({16{1'b0}}), .eq(Zero));  // open: gt, lt

  assign Y[15] = Neg;

  // Other names for the same wires on the sheet: sel[3:0] = Op[3:0]

  // Notes on the sheet:
  //   A: first operand
  //   {{de Erster Operand}}
  //   B: second operand
  //   {{de Zweiter Operand}}
  //   Op: selected operation
  //   {{de Operationswahl}}
  //   Y: result of the operation
  //   {{de Ergebnis der Operation}}
  //   Zero: Zero-flag. Is high if the relult is zero.
  //   {{de Zero-Flag; Ist High wenn das Ergebnis Null ist.}}
  //   Neg: Is high if the result is negative.
  //   {{de Ist High wenn das Ergebnis negativ ist.}}
  //   Carry: Is high if there has been a carry.
  //   {{de Ist High wenn es einen Übertrag gegeben hat.}}
  //   Ci: carry input
  //   {{de Der Eingang für den Übertrag}}
endmodule
