// Digital circuit LSL.dig as structural Verilog
// Moves the data word to the left to higher bits, so it multiplies 
// by two. The current carry bit is pushed in at the bottom, and 
// the most significant bit is output as a carry bit.
// {{de Schiebt das Datenwort nach Links zu höheren Bits, 
// multipliziert also mit zwei. Dabei wird das aktuelle
// Carry-Bit unten hineingeschoben, und das 
// höchstwertige Bit als Carry-Bit wieder ausgegeben.}}
module LSL (
  input  [15:0] Di,
  input  Ci,
  output [15:0] Do,
  output Co
);


  assign Co = Di[15];
  assign Do = {Di[14:0], Ci};

  // Notes on the sheet:
  //   Di: data input
  //   {{de Dateneingang}}
  //   Ci: carry input
  //   {{de Carry-Eingang}}
  //   Do: data output
  //   {{de Datenausgang}}
  //   Co: carry output
  //   {{de Carry-Ausgang}}
endmodule
