// Digital circuit LSR.dig as structural Verilog
// Shift right. So a division by two.
// The carry bit is inserted at the top. And the least 
// significant bit is output as a new carry bit.
// {{de Rechts schieben. Also eine Division durch Zwei.
// Das Carry-Bit wird dabei oben eingeschoben. Und
// das niederwertigste Bit wird als neues Carry-Bit 
// Ausgegeben.}}
module LSR (
  input  [15:0] Di,
  input  Ci,
  output [15:0] Do,
  output Co
);


  assign Co = Di[0];
  assign Do = {Ci, Di[15:1]};

  // Notes on the sheet:
  //   Di: data input
  //   {{de Dateneingang}}
  //   Ci: carry input
  //   {{de Carry-Eingang}}
  //   Do: data output
  //   {{de Datenausgang}}
  //   Co: carry output
  //   {{de Carry-Ausgang}}
endmodule
