// Digital circuit SWAP.dig as structural Verilog
// Tauscht High-Byte und Low-Byte.
module SWAP (
  input  [15:0] Di,
  output [15:0] Do
);


  assign Do = {Di[7:0], Di[15:8]};

  // Notes on the sheet:
  //   Di: Dateneingang
  //   Do: Datenausgang
endmodule
