// Digital circuit ASR.dig as structural Verilog
// Arithmetisches schieben. Ein vorzeichenrichtige 
// Division durch Zwei. Dabei wird das untere Bit als 
// Carry-Bit ausgegeben, während das oberste Bit 
// unverändert bleibt, um das Vorzeichen zu erhalten.
module ASR (
  input  [15:0] Di,
  output C,
  output [15:0] Do
);


  assign C = Di[0];
  assign Do = {{2{Di[15]}}, Di[14:1]};

  // Notes on the sheet:
  //   Di: Dateneingang
  //   C: Carry-Ausgang
  //   Do: Datenausgang
endmodule
