// Digital circuit Branch.dig as structural Verilog
// Einheit für bedingte Verzweigungen. 
// Je nach Zustand der Flags und des ctrl-Eingangs 
// wird ein bedingter Sprung ausgelößt oder eben 
// nicht.
module Branch (
  input  Z,
  input  N,
  input  C,
  input  [2:0] ctrl,
  output jmp
);

  wire multiplexer_1_out;

  Multiplexer #(.Selector_Bits(2)) multiplexer_1 (
    .sel(ctrl[1:0]), .in_0(1'b0), .in_1(C), .in_2(Z), .in_3(N), .out(multiplexer_1_out));
  xor xor_1 (jmp, multiplexer_1_out, ctrl[2]);

  // Notes on the sheet:
  //   Z: zero
  //   N: negative
  //   C: carry
  //   jmp: Ist dieser Ausgang High, soll ein bedingter relativer Sprung ausgeführt werden.
  //   ctrl: Art des Sprungs wählen
endmodule
