// Digital circuit ClockDiv.dig as structural Verilog
module ClockDiv (
  input  Clock,
  output C_in,
  output S_in,
  output C
);

  wire not_1_out, t_ff_1_nq;

  not not_1 (not_1_out, Clock);
  T_FF t_ff_1 (.T(not_1_out), .Q(S_in), .nQ(t_ff_1_nq));  // open: C
  and and_1 (C_in, Clock, S_in);
  and and_2 (C, t_ff_1_nq, Clock);

  // Notes on the sheet:
  //   Clock: Hz: 500000
endmodule
