// Digital circuit Control.dig as structural Verilog
// Leitwerk für einen einfachen Prozessor.
// Es arbeitet rein kombinatorisch, es handelt sich 
// also um ein einfaches Schaltwerk. 
// Da es vergleichsweise komplex ist (24 
// Ausgangsbits), wird es durch einen 
// entsprechenden ROM-Baustein 
// realisiert, und nicht durch 24 einzelne Schaltnetze.
module Control (
  input  [6:0] Op,
  output stPC,
  output WE,
  output imm,
  output absJmp,
  output [2:0] muxB,
  output srcToD,
  output muxA,
  output ALUToBus,
  output [4:0] ALUop,
  output storeFlags,
  output [2:0] Branch,
  output st,
  output ld,
  output ioW,
  output ioR
);

  wire [5:0] multiplexer_1_out;
  wire [23:20] Logic_d;

  Multiplexer #(.Bits(6)) multiplexer_1 (.sel(Op[6]), .in_0(Op[5:0]), .in_1({6{1'b0}}), .out(multiplexer_1_out));
  ROM #(.Bits(24), .Addr_Bits(6)) Logic (
    .A(multiplexer_1_out), .sel(1'b1),
    .D({Logic_d[23], storeFlags, srcToD, Logic_d[20], ioR, ioW, Branch, ALUop, muxA, stPC, WE, ALUToBus, absJmp, muxB, st, ld}));
  PullDown #(.Bits(24)) pulldown_1 (.out({Logic_d[23], storeFlags, srcToD, Logic_d[20], ioR, ioW, Branch, ALUop, muxA, stPC, WE, ALUToBus, absJmp, muxB, st, ld}));
  Break #(.Cycles(600000)) Break (.brk(Logic_d[20]));

  assign imm = Op[6];

  // Notes on the sheet:
  //   Op: Der Opcode incl. Immediate Bit
  //   stPC: Programm Counter in Register Speichern
  //   WE: Wert am Datenbus in Register speichern
  //   imm: Aktiviert das Speichern der Konstanten
  //   absJmp: absoluten Sprung auslösen
  //   muxB: Selektor für Mux B
  //   srcToD: SourceRegister auf Datenbus legen
  //   muxA: Selector für Mux A
  //   ALUToBus: ALU auf den Datenbus legen
  //   ALUop: Operation der ALU
  //   storeFlags: Wenn gesetzt führt die ALU eine arithmetische Operation aus, so dass die Flags gespeichert werden müssen.
  //   Branch: Art des bedingten Sprunges
  //   st: Ram speichert Daten vom Datenbus
  //   ld: Ram gibt Daten auf den Datenbus
  //   ioW: Es wird auf die IO geschrieben
  //   ioR: Es wird IO gelesen
  //   contents of Logic (hex, n*v repeats v):
  //   63
  //   0
  //   2097280
  //   4195520
  //   4211904
  //   4196544
  //   4212928
  //   4197568
  //   4198592
  //   4199616
  //   196
  //   212
  //   4195524
  //   4195540
  //   4211908
  //   4211924
  //   4196548
  //   4196564
  //   4212932
  //   4212948
  //   4197572
  //   4197588
  //   4198596
  //   4198612
  //   4199620
  //   4199636
  //   4205760
  //   4205764
  //   4205780
  //   4196352
  //   4196356
  //   4196372
  //   4200640
  //   4201664
  //   4217024
  //   4218048
  //   4202688
  //   9408
  //   10432
  //   2098186
  //   1673
  //   2097158
  //   2097182
  //   133
  //   149
  //   2098182
  //   1669
  //   32792
  //   65560
  //   98328
  //   163864
  //   196632
  //   229400
  //   420
  //   32
  //   36
  //   131096
  //   2359300
  //   2359324
  //   2360328
  //   524932
  //   524948
  //   525960
  //   1048576
endmodule
