// Digital circuit Flags.dig as structural Verilog
// Speichert die Prozessorflags
module Flags (
  input  Zi,
  input  Ni,
  input  Ci,
  input  C,
  input  store,
  output Zo,
  output No,
  output Co
);

  wire and_1_out;

  and and_1 (and_1_out, C, store);
  D_FF d_ff_1 (.D(Ci), .C(and_1_out), .Q(Co));  // open: nQ
  D_FF d_ff_2 (.D(Zi), .C(and_1_out), .Q(Zo));  // open: nQ
  D_FF d_ff_3 (.D(Ni), .C(and_1_out), .Q(No));  // open: nQ
endmodule
