// Digital circuit HDLExample.dig as structural Verilog
// Example of a processor that can be exported to VHDL.
// {{de Beispiel für einen Prozessor, der zu VHDL exportiert werden kann.}}
module HDLExample (
  input  Clock,
  input  reset,
  input  U,
  input  D,
  input  R,
  input  L,
  output Y0,
  output Y1,
  output Y2,
  output Y3,
  output Y4,
  output Y5,
  output Y6,
  output Y7,
  output Y8,
  output Y9,
  output Y10,
  output Y11,
  output Y12,
  output Y13,
  output Y14,
  output Y15
);

  wire ioR, processormux_1_iow;
  wire [15:0] adr, gpi_hdl_1_p7, processormux_1_d_out, processormux_1_pc, ROM_d;

  // GPI_HDL gpi_hdl_1: pin names not known; wires that end beside it: adr, ioR, U, L, R, D, gpi_hdl_1_p7, Y15
  ProcessorMux processormux_1 (
    .Instr(ROM_d), .Clock(Clock), .reset(reset), .D_in(gpi_hdl_1_p7), .PC(processormux_1_pc),
    .D_out(processormux_1_d_out), .Addr(adr), .ioR(ioR), .ioW(processormux_1_iow));
  ROM #(.AddrBits(16), .isProgramMemory("true"), .Bits(16), .Addr_Bits(16)) ROM (
    .A(processormux_1_pc), .sel(1'b1), .D(ROM_d));
  // GPO gpo_1: pin names not known; wires that end beside it: Y14, Y13, Y12, Y11, Y10, Y9, Y8, Y7, Y6, Y5, Y4, processormux_1_iow, Y3, Clock, Y2, adr, Y1, processormux_1_d_out, Y0

  // Notes on the sheet:
  //   Clock: pin W5, Hz: 200
  //   Y0: pin U16
  //   Y1: pin E19
  //   Y2: pin U19
  //   Y3: pin V19
  //   Y4: pin W18
  //   Y5: pin U15
  //   Y6: pin U14
  //   Y7: pin V14
  //   Y8: pin V13
  //   Y9: pin V3
  //   Y10: pin W3
  //   Y11: pin U3
  //   Y12: pin P3
  //   Y13: pin N3
  //   Y14: pin P1
  //   Y15: pin L1
  //   reset: pin U18
  //   U: pin T18
  //   D: pin U17
  //   R: pin T17
  //   L: pin W19
  //   Pin numbers are defined to match the BASYS3 FPGA board.
  //   {{de Die Pin-Nummern sind angepasst an ein BASYS3 FPGA Board.}}
  //   contents of ROM (hex, n*v repeats v):
  //   8034,920,4200,3010,2e00,2100,350e,2110,380c,110,1511,3828,110,1518,3838,110,1512,
  //   3804,110,1514,380f,3b02,801b,920,8010,980,a91,8015,3e09,2490,1081,3803,8010,980,a91,
  //   3dde,802a,920,8010,980,8000,991,8015,3e09,2590,1081,3804,8010,980,8000,991,3dce,8038,
  //   920,a91,aa0,8015,3e09,21a0,3806,2490,8000,2091,38c2,aa1,3dc0,2590,2191,38bd,aa0,3dbb,
  //   804c,920,a84,9111,990,8015,3e09,2490,1081,3803,a84,9111,990,3dad
endmodule

/* Test case:
     reset  Clock U D L R Y15 Y14 Y13 Y12 Y11 Y10 Y9 Y8 Y7 Y6 Y5 Y4 Y3 Y2 Y1 Y0
           1    0 0 0 0 0  x   x    x  x   x   x   x  x  x  x  x  x  x  x  x  x
           1    1 0 0 0 0  x   x    x  x   x   x   x  x  x  x  x  x  x  x  x  x
           1    0 0 0 0 0  x   x    x  x   x   x   x  x  x  x  x  x  x  x  x  x
           0    0 0 0 0 0  x   x    x  x   x   x   x  x  x  x  x  x  x  x  x  x

repeat(13) 0    C 0 0 0 0  0   0    0  0   0   0   0  0  0  0  0  0  0  0  0  0

loop(i,15)
repeat(14) 0    C 0 0 0 0  bits(16,1<<i)
end loop

repeat(2)  0    C 0 0 0 0  bits(16,1<<14)

loop(i,15)
repeat(13) 0    C 0 0 0 0  bits(16,1<<(15-i))
end loop
*/
