// Digital circuit GPI-HDL.dig as structural Verilog
// Component for a general purpose input.
// {{de Element für ein allgemeines EIngaberegister.}}
module GPI_HDL (
  input  In0,
  input  In1,
  input  In2,
  input  In3,
  output [15:0] D
);


  assign D = {{12{1'b0}}, In3, In2, In1, In0};

  // Notes on the sheet:
  //   D: Output {{de Ausgabe}}
endmodule
