// Digital circuit GPI.dig as structural Verilog
// Component for a general purpose input.
// {{de Element für ein allgemeines EIngaberegister.}}
module GPI (
  input  [15:0] A,
  input  R,
  input  In0,
  input  In1,
  input  In2,
  input  In3,
  output [15:0] D
);

  wire and_1_out, comparator_1_eq;

  Comparator #(.Bits(16)) comparator_1 (.a(A), .b(16'h14), .eq(comparator_1_eq));  // open: gt, lt
  and and_1 (and_1_out, comparator_1_eq, R);
  assign D = and_1_out ? {{12{1'b0}}, In3, In2, In1, In0} : 16'bz;  // Driver driver_1

  // Notes on the sheet:
  //   A: address bus {{de Addressbus}}
  //   R: Raed Enable {{de Lesefreigabe}}
  //   D: Output {{de Ausgabe}}
endmodule
