// Digital circuit GPI_HDL.dig as structural Verilog
// Simple general input register.
// {{de Element für ein allgemeines Eingaberegister.}}
module GPI_HDL (
  input  [15:0] A,
  input  R,
  input  In0,
  input  In1,
  input  In2,
  input  In3,
  output [15:0] D,
  output sel
);

  wire comparator_1_eq;

  Comparator #(.Bits(16)) comparator_1 (.a(A), .b(16'h14), .eq(comparator_1_eq));  // open: gt, lt
  and and_1 (sel, comparator_1_eq, R);

  assign D = {{12{1'b0}}, In3, In2, In1, In0};

  // Notes on the sheet:
  //   D: Output
  //   {{de Ausgabe}}
  //   A: address bus
  //   {{de Addressbus}}
  //   R: Read Enable
  //   {{de Lesefreigabe}}
endmodule
