// Digital circuit GPI_VHDL.dig as structural Verilog
// Element für ein allgemeines EIngaberegister.
module GPI_VHDL (
  input  In0,
  input  In1,
  input  In2,
  input  In3,
  output [15:0] D
);


  assign D = {{12{1'b0}}, In3, In2, In1, In0};

  // Notes on the sheet:
  //   D: Output
endmodule
