// Digital circuit Graphics.dig as structural Verilog
// Eine einfache "Grafikkarte". 
// Contains a graphics RAM to display the actual graphics. 
// This graphics RAM is configured to display 20x20 pixels. 
// The required 800 bytes of memory are maped to the 
// address 0x8000 in the address space.
// {{de Enthält ein Grafik-RAM um die eigentliche 
// Grafik anzuzeigen. Dieses Grafik-RAM ist auf die 
// Darstellung von 20x20 Pixel konfiguriert. 
// Die erforderlichen 800 Bytes Speicher  werden 
// ab Adresse 0x8000 in den Adressbereich 
// eingeblendet.}}
module Graphics (
  input  [15:0] A,
  input  R,
  input  C,
  input  W,
  output [15:0] D
);

  wire and_1_out, and_2_out, and_3_out, and_4_out, Bank_FF_q, comparator_1_lt, comparator_2_eq,
       comparator_2_gt;
  wire [15:0] sub_1_s;

  Comparator #(.Bits(16)) comparator_1 (.a(A), .b(16'h8320), .lt(comparator_1_lt));  // open: gt, eq
  Comparator #(.Bits(16)) comparator_2 (.a(A), .b(16'h7fff), .gt(comparator_2_gt), .eq(comparator_2_eq));  // open: lt
  and and_1 (and_1_out, comparator_1_lt, comparator_2_gt);
  and and_2 (and_2_out, comparator_2_eq, C, W);
  Sub #(.Bits(16)) sub_1 (.a(A), .b(16'h8000), .c_i(1'b0), .s(sub_1_s));  // open: c_o
  and and_3 (and_3_out, and_1_out, W);
  and and_4 (and_4_out, and_1_out, R);
  D_FF Bank_FF (.D(D[0]), .C(and_2_out), .Q(Bank_FF_q));  // open: nQ
  GraphicCard #(.AddrBits(16), .graphicHeight(20), .graphicWidth(20), .Bits(16), .Addr_Bits(16)) graphiccard_1 (
    .A(sub_1_s[9:0]), .str(and_3_out), .C(C), .ld(and_4_out), .B(Bank_FF_q), .D(D));

  // Notes on the sheet:
  //   A: address {{de Adresse}}
  //   R: Read enable {{de Lesefreigabe}}
  //   D: bidirectional data port
  //   {{de Bidirektionaler Datenanschluss}}
  //   W: Write enable {{de Schreibfreigabe}}
endmodule
