// Digital circuit Keyboard.dig as structural Verilog
module Keyboard (
  input  [15:0] A,
  input  C,
  input  R,
  output [15:0] D,
  output intr
);

  wire and_1_out, comparator_1_eq;

  Comparator #(.Bits(16)) comparator_1 (.a(A), .b(16'h1e), .eq(comparator_1_eq));  // open: gt, lt
  and and_1 (and_1_out, comparator_1_eq, R);
  Keyboard keyboard_1 (.C(C), .en(and_1_out), .D(D), .av(intr));

  // Notes on the sheet:
  //   A: address {{de Adressbus}}
  //   R: Read Enable {{de Lesefreigabe}}
endmodule
