// Digital circuit LedMatrix.dig as structural Verilog
module LedMatrix (
  input  [15:0] D,
  input  [15:0] A,
  input  C,
  input  W
);

  wire and_1_out, and_2_out, comparator_1_eq, comparator_2_eq;
  wire [5:0] register_2_q;
  wire [15:0] register_1_q, register_3_q;
  wire [15:6] register_2_q_2;

  Comparator #(.Bits(16)) comparator_1 (.a(A), .b(16'ha), .eq(comparator_1_eq));  // open: gt, lt
  Comparator #(.Bits(16)) comparator_2 (.a(A), .b(16'hb), .eq(comparator_2_eq));  // open: gt, lt
  and and_1 (and_1_out, comparator_1_eq, W);
  and and_2 (and_2_out, W, comparator_2_eq);
  Register #(.Bits(16)) register_1 (.D(D), .C(C), .en(and_1_out), .Q(register_1_q));
  Register #(.Bits(16)) register_2 (.D(D), .C(C), .en(and_2_out), .Q({register_2_q_2, register_2_q}));
  Register #(.Bits(16)) register_3 (.D(register_1_q), .C(C), .en(and_2_out), .Q(register_3_q));
  LedMatrix #(.ledPersistence("true"), .colAddrBits(6), .rowDataBits(16)) ledmatrix_1 (
    .rows(register_3_q), .column(register_2_q));

  // Notes on the sheet:
  //   D: data bus {{de Datenbus}}
  //   A: address bus {{de Adressbus}}
  //   W: Write Enable {{de Schreibfreigabe}}
endmodule
