// Digital circuit TestIO.dig as structural Verilog
module TestIO (
  input  [15:0] A,
  input  [15:0] D,
  input  w,
  input  r,
  input  C
);

  wire and_1_out, and_2_out, comparator_1_eq;
  wire [15:0] register_q;

  Comparator #(.Bits(16)) comparator_1 (.a(A), .b(16'h1), .eq(comparator_1_eq));  // open: gt, lt
  and and_1 (and_1_out, r, comparator_1_eq);
  and and_2 (and_2_out, comparator_1_eq, w);
  assign D = and_1_out ? register_q : 16'bz;  // Driver driver_1
  Register #(.Bits(16)) register (.D(D), .C(C), .en(and_2_out), .Q(register_q));
endmodule

/* Code that sets the parameters or builds the circuit:
addr:=2;
*/
