// Digital circuit readSelect.dig as structural Verilog
module readSelect (
  input  [15:0] D0,
  input  S0,
  input  [15:0] D1,
  input  S1,
  input  [15:0] D2,
  input  S2,
  input  [15:0] D3,
  input  S3,
  output [15:0] D
);

  wire [1:0] priorityencoder_1_num;

  PriorityEncoder #(.Selector_Bits(2)) priorityencoder_1 (
    .in0(S0), .in1(S1), .in2(S2), .in3(S3), .num(priorityencoder_1_num));  // open: any
  Multiplexer #(.Selector_Bits(2), .Bits(16)) multiplexer_1 (
    .sel(priorityencoder_1_num), .in_0(D0), .in_1(D1), .in_2(D2), .in_3(D3), .out(D));
endmodule
