// Digital circuit ImReg.dig as structural Verilog
// Register zum Speichern von großen Konstanten.
// Es existiert ein 1-Bit Befehl, welcher dieses Register
// beschreibt. Auf diese Weise können 15 Bits 
// gespeichert werden (das 16. Bit aktiviert das 
// Beschreiben dieses Registers und ist daher immer 
// Eins) Um das fehlende 16. Bit zu speichern, steht ein 
// spezielles Bit in jedem Befehlswort zur Verfügung.
module ImReg (
  input  [15:0] inst,
  input  en,
  input  C,
  output [15:0] imm
);

  wire [15:15] register_1_q;

  Register #(.Bits(16)) register_1 (.D(inst), .C(C), .en(en), .Q({register_1_q[15], imm[14:0]}));

  assign imm[15] = inst[8];

  // Notes on the sheet:
  //   inst: Der aktuelle Befehl
  //   imm: Die Konstante aus Registerinhalt und Bit 8
  //   en: Speichern aktivieren
  //   C: Takt
endmodule
