// Digital circuit Interrupt.dig as structural Verilog
// Einfacher Interrupt-Controler.
// Wird ein Interrupt ausgelöst, wird der Controler
// gesperrt: Es können keine weiteren Interrupts
// ausgelöst werden. Am Ende der ISR kann über 
// den IO Port 1 die Return Address abgefragt 
// werden. Diese Abfrage gibt den 
// Interruptcontroller auch wieder frei, so dass 
// erneut Interrupts ausgelöst werden können.
module Interrupt (
  input  [15:0] A,
  input  ioR,
  input  C,
  input  [15:0] Next,
  input  imm,
  input  abs,
  input  rel,
  input  intr,
  output [15:0] D,
  output iEn
);

  wire and_1_out, and_2_out, comparator_1_eq, d_ff_1_q, intLock_nq, not_1_out, not_2_out, not_3_out,
       rising_1_out;
  wire [15:0] intRet_q;

  Rising rising_1 (.Reset(iEn), .Set(intr), .Out(rising_1_out));
  not not_1 (not_1_out, rel);
  not not_2 (not_2_out, imm);
  not not_3 (not_3_out, abs);
  Comparator #(.Bits(16)) comparator_1 (.a(A), .b(16'h1), .eq(comparator_1_eq));  // open: gt, lt
  JK_FF intLock (.J(and_1_out), .C(C), .K(d_ff_1_q), .nQ(intLock_nq));  // open: Q
  and and_1 (and_1_out, intLock_nq, rising_1_out, not_1_out, not_2_out, not_3_out);
  Register #(.Bits(16)) intRet (.D(Next), .C(C), .en(and_1_out), .Q(intRet_q));
  and and_2 (and_2_out, comparator_1_eq, ioR);
  D_FF d_ff_1 (.D(and_2_out), .C(C), .Q(d_ff_1_q));  // open: nQ
  D_FF Sync (.D(and_1_out), .C(C), .Q(iEn));  // open: nQ
  assign D = and_2_out ? intRet_q : 16'bz;  // Driver driver_1

  // Notes on the sheet:
  //   A: Adresse
  //   D: Datenbus
  //   ioR: IO Read
  //   C: Takt
  //   Next: Der nächste Befehl, also die Rücksprungadresse.
  //   iEn: Interrupt-Freigabe für PC
  //   imm: Immediate Register:
  //   Wenn gesetzt, wird Interrupt verhindert.
  //   abs: Absoluter Sprung:
  //   Wenn gesetzt, wird Interrupt verhindert.
  //   rel: relativer Sprung: 
  //   Wenn gesetzt, wird Interrupt verhindert.
  //   intr: Interrupt Anforderung
endmodule
