// Digital circuit Intr.dig as structural Verilog
// Einfacher Interrupt-Controler.
// Wird ein Interrupt ausgelöst, wird der Controler
// gesperrt: Es können keine weiteren Interrupts
// ausgelöst werden. Am Ende der ISR kann über 
// den IO Port 1 die Return Address abgefragt 
// werden. Diese Abfrage gibt den 
// Interruptcontroller auch wieder frei, so dass 
// erneut Interrupts ausgelöst werden können.
module Intr (
  input  [15:0] A,
  input  ioR,
  input  C,
  input  [15:0] Next,
  input  imm,
  input  abs,
  input  rel,
  input  intr,
  output [15:0] D,
  output iEn
);

  wire and_1_out, and_3_out, comparator_1_eq, iLock_nq, not_1_out, not_2_out, not_3_out, not_4_out;
  wire [15:0] register_1_q;

  and and_1 (and_1_out, intr, C);
  not not_1 (not_1_out, rel);
  not not_2 (not_2_out, imm);
  not not_3 (not_3_out, abs);
  Comparator #(.Bits(16)) comparator_1 (.a(A), .b(16'h1), .eq(comparator_1_eq));  // open: gt, lt
  JK_FF iLock (.J(iEn), .C(not_4_out), .K(and_3_out), .nQ(iLock_nq));  // open: Q
  and and_2 (iEn, iLock_nq, and_1_out, not_1_out, not_2_out, not_3_out);
  not not_4 (not_4_out, C);
  Register #(.Bits(16)) register_1 (.D(Next), .C(not_4_out), .en(iEn), .Q(register_1_q));
  and and_3 (and_3_out, comparator_1_eq, ioR);
  assign D = and_3_out ? register_1_q : 16'bz;  // Driver driver_1

  // Notes on the sheet:
  //   A: Adresse
  //   D: Datenbus
  //   ioR: IO Read
  //   C: Takt
  //   Next: Der nächste Befehl, also die Rücksprungadresse.
  //   iEn: Interrupt-Freigabe für PC
  //   imm: Immediate Register:
  //   Wenn gesetzt, wird Interrupt verhindert.
  //   abs: Absoluter Sprung:
  //   Wenn gesetzt, wird Interrupt verhindert.
  //   rel: relativer Sprung: 
  //   Wenn gesetzt, wird Interrupt verhindert.
  //   intr: Interrupt Anforderung
endmodule
