// Digital circuit IntrExample.dig as structural Verilog
// Einfacher Prozessor, der an die MIPS-Architektur 
// angelehnt ist. Es handelt sich um eine Harvard 
// Single-Cycle CPU. Er verfügt über einen Interrupt 
// Controller, der gesteuert durch einen Zähler, alle
// 2048 Zyklen einen Interrupt auslöst, und dabei die
// feste Adresse 0x1000 anspringt.
// An dieser Adresse muss sich die ISR befinden.
module IntrExample (
  input  C
);

  wire counter_1_ovf, gpo_1_p1, gpo_1_p2, gpo_1_p3, gpo_1_p4, gpo_1_p5, gpo_1_p6, gpo_1_p7, gpo_1_p8,
       gpo_1_p9, gpo_1_p10, gpo_1_p11, gpo_1_p12, gpo_1_p14, gpo_1_p16, gpo_1_p18, gpo_1_p20, ioR, ioW;
  wire [15:0] A, D;

  LED led_1 (.in(gpo_1_p2));
  LED led_2 (.in(gpo_1_p1));
  Counter #(.Bits(11)) counter_1 (.en(C), .C(1'b0), .ovf(counter_1_ovf));  // open: clr, out
  LED led_3 (.in(gpo_1_p4));
  LED led_4 (.in(gpo_1_p3));
  LED led_5 (.in(gpo_1_p6));
  LED led_6 (.in(gpo_1_p5));
  ProcessorIntr processorintr_1 (.C(C), .intr(counter_1_ovf), .D(A), .A(D), .ioR(ioR), .ioW(ioW));
  LED led_7 (.in(gpo_1_p8));
  LED led_8 (.in(gpo_1_p7));
  LED led_9 (.in(gpo_1_p10));
  LED led_10 (.in(gpo_1_p9));
  // GPO gpo_1: pin names not known; wires that end beside it: gpo_1_p1, gpo_1_p2, gpo_1_p3, gpo_1_p4, gpo_1_p5, gpo_1_p6, gpo_1_p7, gpo_1_p8, gpo_1_p9, gpo_1_p10, gpo_1_p11, gpo_1_p12, ioW, gpo_1_p14, C, gpo_1_p16, A, gpo_1_p18, D, gpo_1_p20
  LED led_11 (.in(gpo_1_p12));
  LED led_12 (.in(gpo_1_p11));
  Terminal terminal_1 (.D(D), .A(A), .C(C), .W(ioW));
  LED led_13 (.in(gpo_1_p16));
  LED led_14 (.in(gpo_1_p14));
  LED led_15 (.in(gpo_1_p20));
  LED led_16 (.in(gpo_1_p18));

  // Notes on the sheet:
  //   C: Hz: 500000
endmodule
