// Digital circuit LSL.dig as structural Verilog
// Schiebt das Datenwort nach Links zu höheren Bits, 
// multipliziert also mit zwei. Dabei wird das aktuelle
// Carry-Bit unten hineingeschoben, und das 
// höchstwertige Bit als Carry-Bit wieder ausgegeben.
module LSL (
  input  [15:0] Di,
  input  Ci,
  output [15:0] Do,
  output Co
);


  assign Co = Di[15];
  assign Do = {Di[14:0], Ci};

  // Notes on the sheet:
  //   Di: Dateneingang
  //   Ci: Carry-Eingang
  //   Do: Datenausgang
  //   Co: Carry-Ausgang
endmodule
