// Digital circuit Memory.dig as structural Verilog
// Ein Speicher kombiniert aus ROM und RAM.
// Die Adressen 0-0x7FFF werden auf ein ROM 
// abgebildet, die Adressen 0x8000-0xFFFF auf einen
// RAM-Baustein. Somit finden sich ROM und RAM im
// selben Adressraum.
module Memory (
  input  [15:0] A,
  input  C,
  input  str,
  input  ld,
  output [15:0] D
);

  wire and_1_out, and_2_out, and_3_out, not_1_out;

  not not_1 (not_1_out, A[15]);
  and and_1 (and_1_out, not_1_out, ld);
  and and_2 (and_2_out, str, A[15]);
  and and_3 (and_3_out, A[15], ld);
  ROM #(.isProgramMemory("true"), .Bits(16), .Addr_Bits(15)) rom_1 (.A(A[14:0]), .sel(and_1_out), .D(D));
  RAMSinglePort #(.Bits(16), .Addr_Bits(15)) ramsingleport_1 (
    .A(A[14:0]), .str(and_2_out), .C(C), .ld(and_3_out), .D(D));

  // Notes on the sheet:
  //   D: Der bidirektionelle Datenbus
  //   A: Der Adressbus
  //   C: Takt
  //   str: Daten speichern
  //   ld: Speicher lesen
  //   contents of rom_1 (hex, n*v repeats v):
  //   6e0d,48,65,6c,6c,6f,20,57,6f,72,6c,64,a,0,1401,4e10,3c10,5ffc,73f1,1801,6ffa
endmodule
