// Digital circuit PC.dig as structural Verilog
module PC (
  input  [15:0] ALU,
  input  Clock,
  input  abs,
  input  BRK,
  input  rel,
  output [15:0] Next,
  output [15:0] PC
);

  wire not_1_out, not_2_out;
  wire [15:0] Add_ALU_s, multiplexer_1_out, multiplexer_2_out;

  not not_1 (not_1_out, Clock);
  not not_2 (not_2_out, BRK);
  Register #(.Bits(16)) u_PC (.D(multiplexer_2_out), .C(not_1_out), .en(not_2_out), .Q(PC));
  Add #(.Bits(16)) Add_One (.a(PC), .b(16'h1), .c_i(1'b0), .s(Next));  // open: c_o
  Add #(.Bits(16)) Add_ALU (.a(Next), .b(ALU), .c_i(1'b0), .s(Add_ALU_s));  // open: c_o
  Multiplexer #(.Bits(16)) multiplexer_1 (.sel(rel), .in_0(Next), .in_1(Add_ALU_s), .out(multiplexer_1_out));
  Multiplexer #(.Bits(16)) multiplexer_2 (.sel(abs), .in_0(multiplexer_1_out), .in_1(ALU), .out(multiplexer_2_out));
endmodule
