// Digital circuit Processor.dig as structural Verilog
module Processor (
  input  Clock
);

  wire alu_1_carry, alu_1_neg, alu_1_zero, branch_1_jmp, control_1_absjmp, control_1_alutobus, control_1_imm,
       control_1_iow, control_1_ld, control_1_muxa, control_1_srctod, control_1_st, control_1_storeflags,
       control_1_stpc, control_1_we, flags_1_co, flags_1_no, flags_1_zo, gpo_1_p5, gpo_1_p6, gpo_1_p7,
       gpo_1_p8, gpo_1_p9, gpo_1_p10, gpo_1_p11, gpo_1_p12, gpo_1_p13, gpo_1_p14, gpo_1_p15, gpo_1_p16,
       gpo_1_p17, gpo_1_p18, gpo_1_p19, gpo_1_p20;
  wire [2:0] control_1_branch, control_1_muxb;
  wire [4:0] control_1_aluop;
  wire [15:0] alu_1_y, driver_1_out, imreg_1_imm, multiplexer_1_out, multiplexer_2_out, pc_1_next, pc_1_pc,
       register_1_rdest, register_1_rsrc, rom_1_d, signext_1__5d, signext_1__5s, signext_1__9sd;

  ROM #(.showList("true"), .Bits(16), .Addr_Bits(16)) rom_1 (.A(pc_1_pc), .sel(1'b1), .D(rom_1_d));
  PC pc_1 (.ALU(alu_1_y), .C(Clock), .abs(control_1_absjmp), .rel(branch_1_jmp), .Next(pc_1_next), .PC(pc_1_pc));
  assign driver_1_out = control_1_stpc ? pc_1_next : 16'bz;  // Driver driver_1
  Register register_1 (
    .WD(driver_1_out), .C(Clock), .src(rom_1_d[3:0]), .dest(rom_1_d[7:4]), .WE(control_1_we),
    .Rdest(register_1_rdest), .Rsrc(register_1_rsrc));
  ImReg imreg_1 (.inst(rom_1_d), .en(control_1_imm), .C(Clock), .imm(imreg_1_imm));
  assign driver_1_out = control_1_srctod ? register_1_rsrc : 16'bz;  // Driver driver_2
  SignExt signext_1 (.inst(rom_1_d), ._5S(signext_1__5s), ._9SD(signext_1__9sd), ._5D(signext_1__5d));
  Multiplexer #(.Selector_Bits(3), .Bits(16)) multiplexer_1 (
    .sel(control_1_muxb), .in_0(register_1_rsrc), .in_1(imreg_1_imm), .in_2({16{1'b0}}), .in_3(16'hff),
    .in_4(16'hfff), .in_5(signext_1__5s), .in_6(signext_1__9sd), .in_7(signext_1__5d), .out(multiplexer_1_out));
  Control control_1 (
    .Op(rom_1_d[15:9]), .stPC(control_1_stpc), .WE(control_1_we), .imm(control_1_imm),
    .absJmp(control_1_absjmp), .muxB(control_1_muxb), .srcToD(control_1_srctod), .muxA(control_1_muxa),
    .ALUToBus(control_1_alutobus), .ALUop(control_1_aluop), .storeFlags(control_1_storeflags),
    .Branch(control_1_branch), .st(control_1_st), .ld(control_1_ld), .ioW(control_1_iow));  // open: ioR
  Multiplexer #(.Bits(16)) multiplexer_2 (
    .sel(control_1_muxa), .in_0(register_1_rdest), .in_1(register_1_rsrc), .out(multiplexer_2_out));
  ALU alu_1 (
    .A(multiplexer_2_out), .B(multiplexer_1_out), .Op(control_1_aluop), .Ci(flags_1_co), .Y(alu_1_y),
    .Zero(alu_1_zero), .Neg(alu_1_neg), .Carry(alu_1_carry));
  assign driver_1_out = control_1_alutobus ? alu_1_y : 16'bz;  // Driver driver_3
  Flags flags_1 (
    .Zi(alu_1_zero), .Ni(alu_1_neg), .Ci(alu_1_carry), .C(Clock), .store(control_1_storeflags),
    .Zo(flags_1_zo), .No(flags_1_no), .Co(flags_1_co));
  Branch branch_1 (.Z(flags_1_zo), .N(flags_1_no), .C(flags_1_co), .ctrl(control_1_branch), .jmp(branch_1_jmp));
  RAMSinglePort #(.Bits(16), .Addr_Bits(16)) ramsingleport_1 (
    .A(alu_1_y), .str(control_1_st), .C(Clock), .ld(control_1_ld), .D(driver_1_out));
  // GPO gpo_1: pin names not known; wires that end beside it: driver_1_out, Clock, alu_1_y, control_1_iow, gpo_1_p5, gpo_1_p6, gpo_1_p7, gpo_1_p8, gpo_1_p9, gpo_1_p10, gpo_1_p11, gpo_1_p12, gpo_1_p13, gpo_1_p14, gpo_1_p15, gpo_1_p16, gpo_1_p17, gpo_1_p18, gpo_1_p19, gpo_1_p20
  Terminal terminal_1 (.D(alu_1_y), .A(driver_1_out), .C(Clock), .W(control_1_iow));
  LED led_1 (.in(gpo_1_p5));
  LED led_2 (.in(gpo_1_p6));
  LED led_3 (.in(gpo_1_p7));
  LED led_4 (.in(gpo_1_p8));
  LED led_5 (.in(gpo_1_p9));
  LED led_6 (.in(gpo_1_p10));
  LED led_7 (.in(gpo_1_p11));
  LED led_8 (.in(gpo_1_p12));
  LED led_9 (.in(gpo_1_p13));
  LED led_10 (.in(gpo_1_p14));
  LED led_11 (.in(gpo_1_p15));
  LED led_12 (.in(gpo_1_p16));
  LED led_13 (.in(gpo_1_p17));
  LED led_14 (.in(gpo_1_p18));
  LED led_15 (.in(gpo_1_p19));
  LED led_16 (.in(gpo_1_p20));

  // Notes on the sheet:
  //   Clock: Hz: 100
  //   contents of rom_1 (hex, n*v repeats v):
  //   391
  //   5120
  //   21088
  //   21280
  //   32802
  //   20480
  //   32800
  //   4608
  //   21072
  //   21152
  //   21440
  //   32801
  //   20480
  //   32801
  //   4608
  //   21264
  //   32826
  //   4608
  //   32800
  //   20480
  //   32838
  //   4608
  //   21376
  //   32865
  //   4608
  //   21104
  //   21184
  //   21408
  //   32868
  //   4608
  //   21248
  //   32869
  //   4608
  //   20992
  //   21232
  //   21328
  //   21472
  //   32871
  //   4608
  //   21424
  //   32876
  //   4608
  //   21120
  //   21136
  //   21392
  //   32879
  //   4608
  //   21040
  //   32880
  //   4608
  //   21168
  //   32882
  //   4608
  //   21008
  //   21024
  //   21056
  //   21344
  //   21360
  //   32883
  //   4608
  //   21200
  //   21216
  //   21456
  //   32884
  //   4608
  //   21488
  //   5232
  //   4096
  //   5125
  //   15365
  //   24066
  //   33109
  //   27648
  //   15364
  //   25602
  //   33109
  //   27648
  //   15364
  //   25602
  //   33109
  //   27648
  //   5121
  //   8193
  //   24066
  //   33109
  //   27648
  //   5233
  //   5127
  //   5141
  //   1025
  //   15372
  //   24065
  //   28409
  //   5390
  //   5406
  //   1025
  //   32828
  //   14848
  //   24065
  //   28402
  //   5234
  //   5127
  //   5141
  //   2049
  //   15362
  //   24065
  //   28395
  //   32803
  //   4608
  //   32801
  //   4624
  //   2049
  //   15362
  //   24065
  //   28387
  //   31744
  //   5235
  //   5127
  //   5141
  //   5153
  //   16416
  //   1537
  //   15373
  //   24065
  //   28377
  //   5236
  //   5127
  //   5141
  //   5153
  //   16416
  //   2561
  //   15361
  //   24065
  //   28368
  //   5237
  //   65535
  //   4864
  //   17920
  //   65535
  //   15104
  //   24065
  //   28360
  //   65535
  //   4608
  //   17920
  //   49151
  //   14848
  //   24065
  //   28353
  //   5121
  //   17920
  //   23553
  //   28349
  //   17920
  //   25089
  //   28346
  //   5238
  //   37428
  //   4608
  //   18432
  //   46098
  //   14848
  //   24065
  //   28338
  //   37428
  //   4608
  //   18944
  //   41283
  //   14848
  //   24065
  //   28331
  //   5239
  //   15488
  //   24065
  //   28327
  //   5249
  //   32945
  //   26624
  //   32945
  //   4624
  //   5248
  //   14352
  //   24065
  //   28318
  //   5240
  //   15488
  //   24065
  //   28314
  //   32960
  //   4608
  //   5250
  //   27136
  //   28309
  //   5248
  //   5241
  //   5127
  //   13827
  //   15621
  //   24065
  //   28302
  //   5127
  //   32808
  //   13312
  //   33048
  //   14848
  //   24065
  //   28295
  //   5127
  //   5139
  //   12801
  //   15621
  //   24065
  //   28289
  //   5242
  //   5125
  //   21296
  //   6145
  //   21312
  //   22291
  //   15381
  //   24065
  //   28280
  //   22292
  //   15382
  //   24065
  //   28276
  //   5427
  //   20035
  //   15429
  //   24065
  //   28271
  //   6193
  //   20035
  //   15430
  //   24065
  //   28266
  //   5243
  //   5427
  //   5125
  //   19504
  //   6145
  //   6193
  //   19504
  //   22307
  //   15397
  //   24065
  //   28255
  //   22308
  //   15398
  //   24065
  //   28251
  //   5244
  //   5135
  //   21296
  //   5135
  //   32772
  //   23056
  //   15391
  //   24065
  //   28242
  //   5245
  //   5376
  //   5392
  //   32772
  //   22544
  //   22292
  //   15632
  //   24065
  //   28233
  //   5246
  //   15488
  //   24065
  //   28229
  //   5252
  //   65534
  //   4608
  //   6145
  //   26113
  //   28223
  //   6145
  //   24577
  //   28220
  //   5248
  //   5247
  //   5249
  //   5123
  //   10248
  //   24065
  //   28213
  //   5250
  //   5123
  //   10243
  //   25601
  //   28208
  //   5248
  //   5488
  //   5249
  //   5120
  //   11264
  //   24065
  //   28201
  //   5250
  //   5123
  //   11267
  //   25601
  //   28196
  //   5248
  //   5489
  //   5249
  //   5121
  //   12289
  //   24065
  //   28189
  //   5250
  //   5123
  //   12290
  //   25601
  //   28184
  //   5248
  //   15488
  //   24078
  //   5381
  //   8417
  //   33094
  //   4848
  //   19695
  //   28189
  //   520
  //   8417
  //   33100
  //   4848
  //   19695
  //   28191
  //   31744
  //   28671
  //   5127
  //   8417
  //   33108
  //   4848
  //   19695
  //   28175
  //   28671
  //   5120
  //   8417
  //   33115
  //   4848
  //   19695
  //   28168
  //   519
  //   8417
  //   33121
  //   4848
  //   19695
  //   28170
  //   31744
  //   28671
  //   19984
  //   29681
  //   6145
  //   15376
  //   26107
  //   20222
  //   6369
  //   27151
  //   18432
  //   18944
  //   33148
  //   26656
  //   18944
  //   33148
  //   26656
  //   18432
  //   18944
  //   33148
  //   26656
  //   18944
  //   33148
  //   26656
  //   20222
  //   6369
  //   27151
  //   528
  //   10271
  //   15386
  //   25091
  //   32816
  //   5648
  //   28162
  //   32823
  //   5648
  //   29681
  //   27138
  //   16
endmodule
