// Digital circuit ProcessorMux.dig as structural Verilog
// Einfacher Prozessor, der an die MIPS-Architektur 
// angelehnt ist. Es handelt sich um eine Harvard 
// Single-Cycle CPU.
module ProcessorMux (
  input  Clock,
  input  reset,
  input  [15:0] D_in,
  output [15:0] D_out,
  output [15:0] Addr,
  output ioR,
  output ioW
);

  wire abs, ALU2D, alu_vhdl_1_p4, alu_vhdl_1_p6, alu_vhdl_1_p7, alu_vhdl_1_p8, branch_1_jmp, flags_1_no,
       flags_1_zo, imm, ld, muxA, sf, src2D, st, stPC, WE;
  wire [2:0] br, muxB;
  wire [4:0] ALUop;
  wire [15:0] imreg_1_imm, multiplexer_1_out, multiplexer_2_out, multiplexer_3_out, multiplexer_4_out,
       pc_vhdl_1_next, pc_vhdl_1_pc, ramdualport_1_d, register_1_rdest, ROM_d, signext_1__5d, signext_1__5s,
       signext_1__9sd;

  ROM #(.AddrBits(16), .isProgramMemory("true"), .Bits(16), .Addr_Bits(16)) ROM (
    .A(pc_vhdl_1_pc), .sel(1'b1), .D(ROM_d));
  PC_VHDL pc_vhdl_1 (
    .ALU(multiplexer_4_out), .C(Clock), .abs(abs), .reset(reset), .rel(branch_1_jmp), .Next(pc_vhdl_1_next),
    .PC(pc_vhdl_1_pc));
  Multiplexer #(.Bits(16)) multiplexer_1 (
    .sel(stPC), .in_0(multiplexer_4_out), .in_1(pc_vhdl_1_next), .out(multiplexer_1_out));
  Control control_1 (
    .Op(ROM_d[15:9]), .stPC(stPC), .WE(WE), .imm(imm), .absJmp(abs), .muxB(muxB), .srcToD(src2D),
    .muxA(muxA), .ALUToBus(ALU2D), .ALUop(ALUop), .storeFlags(sf), .Branch(br), .st(st), .ld(ld), .ioW(ioW),
    .ioR(ioR));
  Register register_1 (
    .WD(multiplexer_1_out), .C(Clock), .src(ROM_d[3:0]), .dest(ROM_d[7:4]), .WE(WE),
    .Rdest(register_1_rdest), .Rsrc(D_out));
  ImReg imreg_1 (.inst(ROM_d), .en(imm), .C(Clock), .imm(imreg_1_imm));
  SignExt signext_1 (.inst(ROM_d), ._5S(signext_1__5s), ._9SD(signext_1__9sd), ._5D(signext_1__5d));
  Multiplexer #(.Bits(16)) multiplexer_2 (.sel(muxA), .in_0(register_1_rdest), .in_1(D_out), .out(multiplexer_2_out));
  Multiplexer #(.Selector_Bits(3), .Bits(16)) multiplexer_3 (
    .sel(muxB), .in_0(D_out), .in_1(imreg_1_imm), .in_2({16{1'b0}}), .in_3(16'hff), .in_4(16'hfff),
    .in_5(signext_1__5s), .in_6(signext_1__9sd), .in_7(signext_1__5d), .out(multiplexer_3_out));
  Branch branch_1 (.Z(flags_1_zo), .N(flags_1_no), .C(alu_vhdl_1_p4), .ctrl(br), .jmp(branch_1_jmp));
  // ALU_VHDL alu_vhdl_1: pin names not known; wires that end beside it: multiplexer_2_out, multiplexer_3_out, ALUop, alu_vhdl_1_p4, Addr, alu_vhdl_1_p6, alu_vhdl_1_p7, alu_vhdl_1_p8
  Flags flags_1 (
    .Zi(alu_vhdl_1_p6), .Ni(alu_vhdl_1_p7), .Ci(alu_vhdl_1_p8), .C(Clock), .store(sf), .Zo(flags_1_zo),
    .No(flags_1_no), .Co(alu_vhdl_1_p4));
  RAMDualPort #(.AddrBits(10), .Bits(16), .Addr_Bits(10)) ramdualport_1 (
    .A(Addr[9:0]), .Din(D_out), .str(st), .C(Clock), .ld(ld), .D(ramdualport_1_d));
  Multiplexer #(.Selector_Bits(2), .Bits(16)) multiplexer_4 (
    .sel({ioR, ld}), .in_0(Addr), .in_1(ramdualport_1_d), .in_2(D_in), .in_3(D_in), .out(multiplexer_4_out));

  // Other names for the same wires on the sheet: C = Clock; res = reset

  // Notes on the sheet:
  //   Clock: pin W5, Hz: 200
  //   reset: pin U18
  //   contents of ROM (hex, n*v repeats v):
  //   20e1,14f4,4cef,6e0b,20e1,14f8,4cef,6e07,20e1,14fc,4cef,6e0c,8036,1220,6e13,1401,1510,
  //   7350,3e00,2011,65fc,4efe,18e1,6a0f,8000,1300,1510,7350,4000,2011,65fc,4efe,18e1,6a0f,
  //   7800,5610,5200,3c00,5e0e,3c10,640c,210,2811,6422,210,2818,6431,210,2812,6404,210,
  //   2814,640c,6a02,803a,1220,1580,1491,7359,3e90,2081,6402,1580,1491,6fe1,8046,1220,1580,
  //   8000,1390,7359,4090,2081,6403,1580,8000,1390,6fd4,8052,1220,1491,14a0,7359,3ca0,6406,
  //   3e90,8000,3b90,65c9,14a1,6fc7,4090,3c91,65c4,14a0,6fc2,8065,1220,1484,9111,1290,7359,
  //   3e90,2081,6403,1484,9111,1290,6fb5
endmodule
