// Digital circuit ProcessorTest.dig as structural Verilog
module ProcessorTest (
  input  Clk
);

  wire processor_1_ior, processor_1_iow;
  wire [15:0] processor_1_a, processor_1_d;

  Processor processor_1 (
    .Clock(Clk), .A(processor_1_a), .D(processor_1_d), .ioW(processor_1_iow), .ioR(processor_1_ior));
  TestIO #(.generic("addr := 3;")) Reg3 (
    .A(processor_1_a), .D(processor_1_d), .w(processor_1_iow), .r(processor_1_ior), .C(Clk));
  TestIO #(.generic("addr := 32;")) Reg32 (
    .A(processor_1_a), .D(processor_1_d), .w(processor_1_iow), .r(processor_1_ior), .C(Clk));

  // Notes on the sheet:
  //   Clk: Hz: 2147483647
endmodule

/* Test case MOV:
# auto generated, do not modify
Clk R1 R2

init R1=3;
init R2=4;

# mov r2,r1
program(0x121)

C X X

# expects
# R1=3
# R2=3
0 3 3
*/

/* Test case ADD C_in C_out:
# auto generated, do not modify
Clk Carry R1 R2

init Carry=1;
init R1=-1;
init R2=3;

# add r1,r2
program(0x212)

C X X X

# expects
# Carry=1
# R1=2
# R2=3
0 1 2 3
*/

/* Test case ADCI C_out S:
# auto generated, do not modify
Clk Carry R1

init Carry=0;
init R1=-1;

# adci r1,3
program(0xe13)

C X X

# expects
# Carry=1
# R1=2
0 1 2
*/

/* Test case SUBI C_in L:
# auto generated, do not modify
Clk Carry R1

init Carry=1;
init R1=23;

# subi r1,22
program(0x8016,0xf10)

repeat (2) C X X

# expects
# Carry=0
# R1=1
0 0 1
*/

/* Test case SBC C_in:
# auto generated, do not modify
Clk Carry R1 R2

init Carry=1;
init R1=3;
init R2=2;

# sbc r1,r2
program(0x512)

C X X X

# expects
# Carry=0
# R1=0
# R2=2
0 0 0 2
*/

/* Test case NEG:
# auto generated, do not modify
Clk R1

init R1=1;

# neg r1
program(0x1310)

C X

# expects
# R1=65535
0 65535
*/

/* Test case LSL:
# auto generated, do not modify
Clk Carry R1

init R1=8;

# lsl r1
program(0x2410)

C X X

# expects
# Carry=0
# R1=16
0 0 16
*/

/* Test case ROL:
# auto generated, do not modify
Clk Carry R1

init Carry=1;
init R1=8;

# rol r1
program(0x2610)

C X X

# expects
# Carry=0
# R1=17
0 0 17
*/

/* Test case LDS small:
# auto generated, do not modify
Clk R1 R2

memory mem(0)=6;
memory mem(1)=7;

# lds r1,0
# lds r2,1
program(0x3010,0x3021)

repeat (2) C X X

# expects
# R1=6
# R2=7
0 6 7
*/

/* Test case JMP long:
# auto generated, do not modify
Clk R0


# jmp 130
#  ldi r0, 1
# .org 130
# ldi r0,2
program(0x8082,0x3c00,0xa01,0x0,0x0,0x0,0x0,0x0,0x0,0x0,0x0,0x0,0x0,0x0,0x0,0x0,0x0,0x0,0x0,0x0,0x0,0x0,0x0,0x0,0x0,0x0,0x0,0x0,0x0,0x0,0x0,0x0,0x0,0x0,0x0,0x0,0x0,0x0,0x0,0x0,0x0,0x0,0x0,0x0,0x0,0x0,0x0,0x0,0x0,0x0,0x0,0x0,0x0,0x0,0x0,0x0,0x0,0x0,0x0,0x0,0x0,0x0,0x0,0x0,0x0,0x0,0x0,0x0,0x0,0x0,0x0,0x0,0x0,0x0,0x0,0x0,0x0,0x0,0x0,0x0,0x0,0x0,0x0,0x0,0x0,0x0,0x0,0x0,0x0,0x0,0x0,0x0,0x0,0x0,0x0,0x0,0x0,0x0,0x0,0x0,0x0,0x0,0x0,0x0,0x0,0x0,0x0,0x0,0x0,0x0,0x0,0x0,0x0,0x0,0x0,0x0,0x0,0x0,0x0,0x0,0x0,0x0,0x0,0x0,0x0,0x0,0x0,0x0,0x0,0x0,0xa02)

repeat (3) C X

# expects
# R0=2
0 2
*/

/* Test case CPC 220:
# auto generated, do not modify
Clk Carry Zero Neg

init Carry=0;
init R0=2;
init R1=2;

# cpc r0,r1
program(0x1f01)

C X X X

# expects
# Carry=0
# Zero=1
# Neg=0
0 0 1 0
*/

/* Test case CPI 221S:
# auto generated, do not modify
Clk Carry Zero Neg

init Carry=1;
init R0=2;

# cpi r0,2
program(0x2102)

C X X X

# expects
# Carry=0
# Zero=1
# Neg=0
0 0 1 0
*/

/* Test case CPCI 220S:
# auto generated, do not modify
Clk Carry Zero Neg

init Carry=0;
init R0=2;

# cpci r0,2
program(0x2302)

C X X X

# expects
# Carry=0
# Zero=1
# Neg=0
0 0 1 0
*/

/* Test case BRCC jmp:
# auto generated, do not modify
Clk R0

init Carry=0;
init R0=2;

# brcc end
#  ldi r0, 1
# end: nop
program(0x3701,0xa01,0x0)

repeat (3) C X

# expects
# R0=2
0 2
*/

/* Test case OUT short:
# auto generated, do not modify
Clk Reg3

init R1=7;

# out 3,R1
program(0x3f31)

C X

# expects
# Reg3=7
0 7
*/

/* Test case ADD:
# auto generated, do not modify
Clk Carry R1 R2

init Carry=0;
init R1=2;
init R2=3;

# add r1,r2
program(0x212)

C X X X

# expects
# Carry=0
# R1=5
# R2=3
0 0 5 3
*/

/* Test case ADDI C_in C_out S:
# auto generated, do not modify
Clk Carry R1

init Carry=1;
init R1=-1;

# addi r1,3
program(0xc13)

C X X

# expects
# Carry=1
# R1=2
0 1 2
*/

/* Test case ADCI C_out L:
# auto generated, do not modify
Clk Carry R1

init Carry=0;
init R1=-1;

# adci r1,23
program(0x8017,0xd10)

repeat (2) C X X

# expects
# Carry=1
# R1=22
0 1 22
*/

/* Test case SUB C_out:
# auto generated, do not modify
Clk Carry R1 R2

init Carry=0;
init R1=2;
init R2=3;

# sub r1,r2
program(0x412)

C X X X

# expects
# Carry=1
# R1=65535
# R2=3
0 1 65535 3
*/

/* Test case SBCI C_in S:
# auto generated, do not modify
Clk Carry R1

init Carry=1;
init R1=3;

# sbci r1,2
program(0x1212)

C X X

# expects
# Carry=0
# R1=0
0 0 0
*/

/* Test case AND:
# auto generated, do not modify
Clk R1 R2

init R1=2;
init R2=3;

# and r1,r2
program(0x612)

C X X

# expects
# R1=2
# R2=3
0 2 3
*/

/* Test case LSR:
# auto generated, do not modify
Clk Carry R1

init R1=8;

# lsr r1
program(0x2510)

C X X

# expects
# Carry=0
# R1=4
0 0 4
*/

/* Test case SWAP:
# auto generated, do not modify
Clk R1

init R1=4660;

# swap r1
program(0x2910)

C X

# expects
# R1=13330
0 13330
*/

/* Test case LDS large:
# auto generated, do not modify
Clk R1

memory mem(32768)=8;

# lds r1,0x8000
program(0x8000,0x2f11)

repeat (2) C X

# expects
# R1=8
0 8
*/

/* Test case RCALL:
# auto generated, do not modify
Clk R0 RA

init R0=3;

# jmp end
# ldi r0, 1
# func: ldi r0,1
# rret ra
# ldi r0,2
# end: rcall ra,func
program(0x3d04,0xa01,0xa01,0x3b0f,0xa02,0x8002,0x3af0)

repeat (7) C X X

# expects
# R0=1
# RA=7
0 1 7
*/

/* Test case CPC 211:
# auto generated, do not modify
Clk Carry Zero Neg

init Carry=1;
init R0=2;
init R1=1;

# cpc r0,r1
program(0x1f01)

C X X X

# expects
# Carry=0
# Zero=1
# Neg=0
0 0 1 0
*/

/* Test case CPI 221L:
# auto generated, do not modify
Clk Carry Zero Neg

init Carry=1;
init R0=22;

# cpi r0,22
program(0x8016,0x2000)

repeat (2) C X X X

# expects
# Carry=0
# Zero=1
# Neg=0
0 0 1 0
*/

/* Test case CPCI 220L:
# auto generated, do not modify
Clk Carry Zero Neg

init Carry=0;
init R0=22;

# cpci r0,22
program(0x8016,0x2200)

repeat (2) C X X X

# expects
# Carry=0
# Zero=1
# Neg=0
0 0 1 0
*/

/* Test case BRCC skip:
# auto generated, do not modify
Clk R0

init Carry=1;
init R0=2;

# brcc end
#  ldi r0, 1
# end: nop
program(0x3701,0xa01,0x0)

repeat (3) C X

# expects
# R0=1
0 1
*/

/* Test case OUT long:
# auto generated, do not modify
Clk Reg32

init R1=7;

# out 32,R1
program(0x8020,0x3e01)

repeat (2) C X

# expects
# Reg32=7
0 7
*/

/* Test case ADDI S:
# auto generated, do not modify
Clk Carry R1

init Carry=0;
init R1=2;

# addi r1,3
program(0xc13)

C X X

# expects
# Carry=0
# R1=5
0 0 5
*/

/* Test case ADDI C_in C_out L:
# auto generated, do not modify
Clk Carry R1

init Carry=1;
init R1=-1;

# addi r1,23
program(0x8017,0xb10)

repeat (2) C X X

# expects
# Carry=1
# R1=22
0 1 22
*/

/* Test case ADC C_in C_out:
# auto generated, do not modify
Clk Carry R1 R2

init Carry=1;
init R1=-1;
init R2=3;

# adc r1,r2
program(0x312)

C X X X

# expects
# Carry=1
# R1=3
# R2=3
0 1 3 3
*/

/* Test case SUBI C_out S:
# auto generated, do not modify
Clk Carry R1

init Carry=0;
init R1=2;

# subi r1,3
program(0x1013)

C X X

# expects
# Carry=1
# R1=65535
0 1 65535
*/

/* Test case SBCI C_in L:
# auto generated, do not modify
Clk Carry R1

init Carry=1;
init R1=23;

# sbci r1,22
program(0x8016,0x1110)

repeat (2) C X X

# expects
# Carry=0
# R1=0
0 0 0
*/

/* Test case ANDI short:
# auto generated, do not modify
Clk R1

init R1=2;

# andi r1,3
program(0x1513)

C X

# expects
# R1=2
0 2
*/

/* Test case LSR:
# auto generated, do not modify
Clk Carry R1

init R1=65535;

# lsr r1
program(0x2510)

C X X

# expects
# Carry=1
# R1=32767
0 1 32767
*/

/* Test case SWAPN:
# auto generated, do not modify
Clk R1

init R1=4660;

# swapn r1
program(0x2a10)

C X

# expects
# R1=8515
0 8515
*/

/* Test case STS small:
# auto generated, do not modify
Clk R2

init R1=7;

# sts 1,r1
# lds r2,1
program(0x2e11,0x3021)

repeat (2) C X

# expects
# R2=7
0 7
*/

/* Test case CMP 210:
# auto generated, do not modify
Clk Carry Zero Neg

init Carry=0;
init R0=2;
init R1=1;

# cmp r0,r1
program(0x1e01)

C X X X

# expects
# Carry=0
# Zero=0
# Neg=0
0 0 0 0
*/

/* Test case CPC 230:
# auto generated, do not modify
Clk Carry Zero Neg

init Carry=0;
init R0=2;
init R1=3;

# cpc r0,r1
program(0x1f01)

C X X X

# expects
# Carry=1
# Zero=0
# Neg=1
0 1 0 1
*/

/* Test case CPI 230S:
# auto generated, do not modify
Clk Carry Zero Neg

init Carry=0;
init R0=2;

# cpi r0,3
program(0x2103)

C X X X

# expects
# Carry=1
# Zero=0
# Neg=1
0 1 0 1
*/

/* Test case CPCI 211S:
# auto generated, do not modify
Clk Carry Zero Neg

init Carry=1;
init R0=2;

# cpci r0,1
program(0x2301)

C X X X

# expects
# Carry=0
# Zero=1
# Neg=0
0 0 1 0
*/

/* Test case BRMI jmp:
# auto generated, do not modify
Clk R0

init Neg=1;
init R0=2;

# brmi end
#  ldi r0, 1
# end: nop
program(0x3601,0xa01,0x0)

repeat (3) C X

# expects
# R0=2
0 2
*/

/* Test case OUTR:
# auto generated, do not modify
Clk Reg3

init R0=3;
init R1=7;

# outr [R0],R1
program(0x4001)

C X

# expects
# Reg3=7
0 7
*/

/* Test case ADDI L:
# auto generated, do not modify
Clk Carry R1

init Carry=0;
init R1=2;

# addi r1,23
program(0x8017,0xb10)

repeat (2) C X X

# expects
# Carry=0
# R1=25
0 0 25
*/

/* Test case ADC:
# auto generated, do not modify
Clk Carry R1 R2

init Carry=0;
init R1=2;
init R2=3;

# adc r1,r2
program(0x312)

C X X X

# expects
# Carry=0
# R1=5
# R2=3
0 0 5 3
*/

/* Test case ADCI C_in C_out S:
# auto generated, do not modify
Clk Carry R1

init Carry=1;
init R1=-1;

# adci r1,3
program(0xe13)

C X X

# expects
# Carry=1
# R1=3
0 1 3
*/

/* Test case SUBI C_out L:
# auto generated, do not modify
Clk Carry R1

init Carry=0;
init R1=22;

# subi r1,23
program(0x8017,0xf10)

repeat (2) C X X

# expects
# Carry=1
# R1=65535
0 1 65535
*/

/* Test case SBC C_out:
# auto generated, do not modify
Clk Carry R1 R2

init Carry=0;
init R1=2;
init R2=3;

# sbc r1,r2
program(0x512)

C X X X

# expects
# Carry=1
# R1=65535
# R2=3
0 1 65535 3
*/

/* Test case ANDI:
# auto generated, do not modify
Clk R1

init R1=16;

# andi r1,24
program(0x8018,0x1410)

repeat (2) C X

# expects
# R1=16
0 16
*/

/* Test case ASR:
# auto generated, do not modify
Clk Carry R1

init R1=8;

# asr r1
program(0x2810)

C X X

# expects
# Carry=0
# R1=4
0 0 4
*/

/* Test case MUL:
# auto generated, do not modify
Clk R1 R0

init R0=7;
init R1=8;

# mul r0,r1
program(0x1b01)

C X X

# expects
# R1=8
# R0=56
0 8 56
*/

/* Test case STS large:
# auto generated, do not modify
Clk R1

init R1=8;

# sts 0x8000,r1
# lds r2,0x8000
program(0x8000,0x2d11,0x8000,0x2f21)

repeat (4) C X

# expects
# R1=8
0 8
*/

/* Test case CMP 211:
# auto generated, do not modify
Clk Carry Zero Neg

init Carry=1;
init R0=2;
init R1=1;

# cmp r0,r1
program(0x1e01)

C X X X

# expects
# Carry=0
# Zero=0
# Neg=0
0 0 0 0
*/

/* Test case CPC 221:
# auto generated, do not modify
Clk Carry Zero Neg

init Carry=1;
init R0=2;
init R1=2;

# cpc r0,r1
program(0x1f01)

C X X X

# expects
# Carry=1
# Zero=0
# Neg=1
0 1 0 1
*/

/* Test case CPI 230L:
# auto generated, do not modify
Clk Carry Zero Neg

init Carry=0;
init R0=22;

# cpi r0,23
program(0x8017,0x2000)

repeat (2) C X X X

# expects
# Carry=1
# Zero=0
# Neg=1
0 1 0 1
*/

/* Test case CPCI 211L:
# auto generated, do not modify
Clk Carry Zero Neg

init Carry=1;
init R0=22;

# cpci r0,21
program(0x8015,0x2200)

repeat (2) C X X X

# expects
# Carry=0
# Zero=1
# Neg=0
0 0 1 0
*/

/* Test case BRMI skip:
# auto generated, do not modify
Clk R0

init Neg=0;
init R0=2;

# brmi end
#  ldi r0, 1
# end: nop
program(0x3601,0xa01,0x0)

repeat (3) C X

# expects
# R0=1
0 1
*/

/* Test case IN short:
# auto generated, do not modify
Clk R1

init Reg3=7;

# in R1,3
program(0x4213)

C X

# expects
# R1=7
0 7
*/

/* Test case ADD C_in:
# auto generated, do not modify
Clk Carry R1 R2

init Carry=1;
init R1=2;
init R2=3;

# add r1,r2
program(0x212)

C X X X

# expects
# Carry=0
# R1=5
# R2=3
0 0 5 3
*/

/* Test case ADCI S:
# auto generated, do not modify
Clk Carry R1

init Carry=0;
init R1=2;

# adci r1,3
program(0xe13)

C X X

# expects
# Carry=0
# R1=5
0 0 5
*/

/* Test case ADCI C_in C_out L:
# auto generated, do not modify
Clk Carry R1

init Carry=1;
init R1=-1;

# adci r1,23
program(0x8017,0xd10)

repeat (2) C X X

# expects
# Carry=1
# R1=23
0 1 23
*/

/* Test case SUB C_in C_out:
# auto generated, do not modify
Clk Carry R1 R2

init Carry=1;
init R1=2;
init R2=3;

# sub r1,r2
program(0x412)

C X X X

# expects
# Carry=1
# R1=65535
# R2=3
0 1 65535 3
*/

/* Test case SBCI C_out S:
# auto generated, do not modify
Clk Carry R1

init Carry=0;
init R1=2;

# sbci r1,3
program(0x1213)

C X X

# expects
# Carry=1
# R1=65535
0 1 65535
*/

/* Test case OR:
# auto generated, do not modify
Clk R1 R2

init R1=2;
init R2=3;

# or r1,r2
program(0x712)

C X X

# expects
# R1=3
# R2=3
0 3 3
*/

/* Test case ASR:
# auto generated, do not modify
Clk Carry R1

init R1=65535;

# asr r1
program(0x2810)

C X X

# expects
# Carry=1
# R1=65535
0 1 65535
*/

/* Test case MULI short:
# auto generated, do not modify
Clk R0

init R0=7;

# muli r0,3
program(0x1d03)

C X

# expects
# R0=21
0 21
*/

/* Test case LD:
# auto generated, do not modify
Clk R0 R1

memory mem(1)=7;
memory mem(32768)=8;
init R2=1;
init R3=32768;

# ld r0,[r2]
# ld r1,[r3]
program(0x2c02,0x2c13)

repeat (2) C X X

# expects
# R0=7
# R1=8
0 7 8
*/

/* Test case CMP 220:
# auto generated, do not modify
Clk Carry Zero Neg

init Carry=0;
init R0=2;
init R1=2;

# cmp r0,r1
program(0x1e01)

C X X X

# expects
# Carry=0
# Zero=1
# Neg=0
0 0 1 0
*/

/* Test case CPI 210S:
# auto generated, do not modify
Clk Carry Zero Neg

init Carry=0;
init R0=2;

# cpi r0,1
program(0x2101)

C X X X

# expects
# Carry=0
# Zero=0
# Neg=0
0 0 0 0
*/

/* Test case CPI 231S:
# auto generated, do not modify
Clk Carry Zero Neg

init Carry=1;
init R0=2;

# cpi r0,3
program(0x2103)

C X X X

# expects
# Carry=1
# Zero=0
# Neg=1
0 1 0 1
*/

/* Test case CPCI 230S:
# auto generated, do not modify
Clk Carry Zero Neg

init Carry=0;
init R0=2;

# cpci r0,3
program(0x2303)

C X X X

# expects
# Carry=1
# Zero=0
# Neg=1
0 1 0 1
*/

/* Test case BRPL jmp:
# auto generated, do not modify
Clk R0

init Neg=0;
init R0=2;

# brpl end
#  ldi r0, 1
# end: nop
program(0x3901,0xa01,0x0)

repeat (3) C X

# expects
# R0=2
0 2
*/

/* Test case IN long:
# auto generated, do not modify
Clk R1

init Reg32=7;

# in R1,32
program(0x8020,0x4110)

repeat (2) C X

# expects
# R1=7
0 7
*/

/* Test case ADDI C_in S:
# auto generated, do not modify
Clk Carry R1

init Carry=1;
init R1=2;

# addi r1,3
program(0xc13)

C X X

# expects
# Carry=0
# R1=5
0 0 5
*/

/* Test case ADCI L:
# auto generated, do not modify
Clk Carry R1

init Carry=0;
init R1=2;

# adci r1,23
program(0x8017,0xd10)

repeat (2) C X X

# expects
# Carry=0
# R1=25
0 0 25
*/

/* Test case SUB:
# auto generated, do not modify
Clk Carry R1 R2

init Carry=0;
init R1=3;
init R2=2;

# sub r1,r2
program(0x412)

C X X X

# expects
# Carry=0
# R1=1
# R2=2
0 0 1 2
*/

/* Test case SUBI C_in C_out S:
# auto generated, do not modify
Clk Carry R1

init Carry=1;
init R1=2;

# subi r1,3
program(0x1013)

C X X

# expects
# Carry=1
# R1=65535
0 1 65535
*/

/* Test case SBCI C_out L:
# auto generated, do not modify
Clk Carry R1

init Carry=0;
init R1=22;

# sbci r1,23
program(0x8017,0x1110)

repeat (2) C X X

# expects
# Carry=1
# R1=65535
0 1 65535
*/

/* Test case ORI short:
# auto generated, do not modify
Clk R1

init R1=2;

# ori r1,3
program(0x1713)

C X

# expects
# R1=3
0 3
*/

/* Test case ROR:
# auto generated, do not modify
Clk Carry R1

init Carry=0;
init R1=8;

# ror r1
program(0x2710)

C X X

# expects
# Carry=0
# R1=4
0 0 4
*/

/* Test case MULI long:
# auto generated, do not modify
Clk R0

init R0=7;

# muli r0,32
program(0x8020,0x1c00)

repeat (2) C X

# expects
# R0=224
0 224
*/

/* Test case LDD:
# auto generated, do not modify
Clk R0 R1

memory mem(3)=7;
memory mem(32768)=8;
init R2=1;
init R3=32770;

# ldd r0,[r2+2]
# ldd r1,[r3-2]
program(0x8002,0x3202,0xfffe,0x3213)

repeat (4) C X X

# expects
# R0=7
# R1=8
0 7 8
*/

/* Test case CMP 221:
# auto generated, do not modify
Clk Carry Zero Neg

init Carry=1;
init R0=2;
init R1=2;

# cmp r0,r1
program(0x1e01)

C X X X

# expects
# Carry=0
# Zero=1
# Neg=0
0 0 1 0
*/

/* Test case CPI 210L:
# auto generated, do not modify
Clk Carry Zero Neg

init Carry=0;
init R0=22;

# cpi r0,21
program(0x8015,0x2000)

repeat (2) C X X X

# expects
# Carry=0
# Zero=0
# Neg=0
0 0 0 0
*/

/* Test case CPI 231L:
# auto generated, do not modify
Clk Carry Zero Neg

init Carry=1;
init R0=22;

# cpi r0,23
program(0x8017,0x2000)

repeat (2) C X X X

# expects
# Carry=1
# Zero=0
# Neg=1
0 1 0 1
*/

/* Test case CPCI 230L:
# auto generated, do not modify
Clk Carry Zero Neg

init Carry=0;
init R0=22;

# cpci r0,23
program(0x8017,0x2200)

repeat (2) C X X X

# expects
# Carry=1
# Zero=0
# Neg=1
0 1 0 1
*/

/* Test case BRPL skip:
# auto generated, do not modify
Clk R0

init Neg=1;
init R0=2;

# brpl end
#  ldi r0, 1
# end: nop
program(0x3901,0xa01,0x0)

repeat (3) C X

# expects
# R0=1
0 1
*/

/* Test case INR:
# auto generated, do not modify
Clk R1

init R0=3;
init Reg3=7;

# inr R1,[R0]
program(0x4310)

C X

# expects
# R1=7
0 7
*/

/* Test case ADDI C_in L:
# auto generated, do not modify
Clk Carry R1

init Carry=1;
init R1=2;

# addi r1,23
program(0x8017,0xb10)

repeat (2) C X X

# expects
# Carry=0
# R1=25
0 0 25
*/

/* Test case ADC C_in:
# auto generated, do not modify
Clk Carry R1 R2

init Carry=1;
init R1=2;
init R2=3;

# adc r1,r2
program(0x312)

C X X X

# expects
# Carry=0
# R1=6
# R2=3
0 0 6 3
*/

/* Test case SUBI S:
# auto generated, do not modify
Clk Carry R1

init Carry=0;
init R1=3;

# subi r1,2
program(0x1012)

C X X

# expects
# Carry=0
# R1=1
0 0 1
*/

/* Test case SUBI C_in C_out L:
# auto generated, do not modify
Clk Carry R1

init Carry=1;
init R1=22;

# subi r1,23
program(0x8017,0xf10)

repeat (2) C X X

# expects
# Carry=1
# R1=65535
0 1 65535
*/

/* Test case SBC C_in C_out:
# auto generated, do not modify
Clk Carry R1 R2

init Carry=1;
init R1=2;
init R2=3;

# sbc r1,r2
program(0x512)

C X X X

# expects
# Carry=1
# R1=65534
# R2=3
0 1 65534 3
*/

/* Test case ORI:
# auto generated, do not modify
Clk R1

init R1=16;

# ori r1,24
program(0x8018,0x1610)

repeat (2) C X

# expects
# R1=24
0 24
*/

/* Test case ROR:
# auto generated, do not modify
Clk Carry R1

init Carry=0;
init R1=9;

# ror r1
program(0x2710)

C X X

# expects
# Carry=1
# R1=4
0 1 4
*/

/* Test case LDI small:
# auto generated, do not modify
Clk R1


# ldi r1,5
program(0xa15)

C X

# expects
# R1=5
0 5
*/

/* Test case ST:
# auto generated, do not modify
Clk R0

init R1=1;
init R2=7;

# st [r1],r2
# lds r0,1
program(0x2b12,0x3001)

repeat (2) C X

# expects
# R0=7
0 7
*/

/* Test case CMP 230:
# auto generated, do not modify
Clk Carry Zero Neg

init Carry=0;
init R0=2;
init R1=3;

# cmp r0,r1
program(0x1e01)

C X X X

# expects
# Carry=1
# Zero=0
# Neg=1
0 1 0 1
*/

/* Test case CPI 211S:
# auto generated, do not modify
Clk Carry Zero Neg

init Carry=1;
init R0=2;

# cpi r0,1
program(0x2101)

C X X X

# expects
# Carry=0
# Zero=0
# Neg=0
0 0 0 0
*/

/* Test case CPCI 210S:
# auto generated, do not modify
Clk Carry Zero Neg

init Carry=0;
init R0=2;

# cpci r0,1
program(0x2301)

C X X X

# expects
# Carry=0
# Zero=0
# Neg=0
0 0 0 0
*/

/* Test case CPCI 221S:
# auto generated, do not modify
Clk Carry Zero Neg

init Carry=1;
init R0=2;

# cpci r0,2
program(0x2302)

C X X X

# expects
# Carry=1
# Zero=0
# Neg=1
0 1 0 1
*/

/* Test case BREQ jmp:
# auto generated, do not modify
Clk R0

init Zero=1;
init R0=2;

# breq end
#  ldi r0, 1
# end: nop
program(0x3501,0xa01,0x0)

repeat (3) C X

# expects
# R0=2
0 2
*/

/* Test case ADD C_out:
# auto generated, do not modify
Clk Carry R1 R2

init Carry=0;
init R1=-1;
init R2=3;

# add r1,r2
program(0x212)

C X X X

# expects
# Carry=1
# R1=2
# R2=3
0 1 2 3
*/

/* Test case ADCI C_in S:
# auto generated, do not modify
Clk Carry R1

init Carry=1;
init R1=2;

# adci r1,3
program(0xe13)

C X X

# expects
# Carry=0
# R1=6
0 0 6
*/

/* Test case SUBI L:
# auto generated, do not modify
Clk Carry R1

init Carry=0;
init R1=23;

# subi r1,22
program(0x8016,0xf10)

repeat (2) C X X

# expects
# Carry=0
# R1=1
0 0 1
*/

/* Test case SBC:
# auto generated, do not modify
Clk Carry R1 R2

init Carry=0;
init R1=3;
init R2=2;

# sbc r1,r2
program(0x512)

C X X X

# expects
# Carry=0
# R1=1
# R2=2
0 0 1 2
*/

/* Test case SBCI C_in C_out S:
# auto generated, do not modify
Clk Carry R1

init Carry=1;
init R1=2;

# sbci r1,3
program(0x1213)

C X X

# expects
# Carry=1
# R1=65534
0 1 65534
*/

/* Test case EOR:
# auto generated, do not modify
Clk R1 R2

init R1=2;
init R2=3;

# eor r1,r2
program(0x812)

C X X

# expects
# R1=1
# R2=3
0 1 3
*/

/* Test case ROR:
# auto generated, do not modify
Clk Carry R1

init Carry=1;
init R1=8;

# ror r1
program(0x2710)

C X X

# expects
# Carry=0
# R1=32772
0 0 32772
*/

/* Test case LDI small:
# auto generated, do not modify
Clk R1


# ldi r1,15
program(0xa1f)

C X

# expects
# R1=15
0 15
*/

/* Test case STD:
# auto generated, do not modify
Clk R0 R1

init R2=4;
init R3=7;
init R4=8;

# std [r2+2],r3
# std [r2-2],r4
# lds r0,6
# lds r1,2
program(0x8002,0x3123,0xfffe,0x3124,0x3006,0x3012)

repeat (6) C X X

# expects
# R0=7
# R1=8
0 7 8
*/

/* Test case CMP 231:
# auto generated, do not modify
Clk Carry Zero Neg

init Carry=1;
init R0=2;
init R1=3;

# cmp r0,r1
program(0x1e01)

C X X X

# expects
# Carry=1
# Zero=0
# Neg=1
0 1 0 1
*/

/* Test case CPI 211L:
# auto generated, do not modify
Clk Carry Zero Neg

init Carry=1;
init R0=22;

# cpi r0,21
program(0x8015,0x2000)

repeat (2) C X X X

# expects
# Carry=0
# Zero=0
# Neg=0
0 0 0 0
*/

/* Test case CPCI 210L:
# auto generated, do not modify
Clk Carry Zero Neg

init Carry=0;
init R0=22;

# cpci r0,21
program(0x8015,0x2200)

repeat (2) C X X X

# expects
# Carry=0
# Zero=0
# Neg=0
0 0 0 0
*/

/* Test case CPCI 221L:
# auto generated, do not modify
Clk Carry Zero Neg

init Carry=1;
init R0=22;

# cpci r0,22
program(0x8016,0x2200)

repeat (2) C X X X

# expects
# Carry=1
# Zero=0
# Neg=1
0 1 0 1
*/

/* Test case BREQ skip:
# auto generated, do not modify
Clk R0

init Zero=0;
init R0=2;

# breq end
#  ldi r0, 1
# end: nop
program(0x3501,0xa01,0x0)

repeat (3) C X

# expects
# R0=1
0 1
*/

/* Test case ADDI C_out S:
# auto generated, do not modify
Clk Carry R1

init Carry=0;
init R1=-1;

# addi r1,3
program(0xc13)

C X X

# expects
# Carry=1
# R1=2
0 1 2
*/

/* Test case ADCI C_in L:
# auto generated, do not modify
Clk Carry R1

init Carry=1;
init R1=2;

# adci r1,23
program(0x8017,0xd10)

repeat (2) C X X

# expects
# Carry=0
# R1=26
0 0 26
*/

/* Test case SUB C_in:
# auto generated, do not modify
Clk Carry R1 R2

init Carry=1;
init R1=3;
init R2=2;

# sub r1,r2
program(0x412)

C X X X

# expects
# Carry=0
# R1=1
# R2=2
0 0 1 2
*/

/* Test case SBCI S:
# auto generated, do not modify
Clk Carry R1

init Carry=0;
init R1=3;

# sbci r1,2
program(0x1212)

C X X

# expects
# Carry=0
# R1=1
0 0 1
*/

/* Test case SBCI C_in C_out L:
# auto generated, do not modify
Clk Carry R1

init Carry=1;
init R1=22;

# sbci r1,23
program(0x8017,0x1110)

repeat (2) C X X

# expects
# Carry=1
# R1=65534
0 1 65534
*/

/* Test case EORI short:
# auto generated, do not modify
Clk R1

init R1=2;

# eori r1,3
program(0x1913)

C X

# expects
# R1=1
0 1
*/

/* Test case ROL:
# auto generated, do not modify
Clk Carry R1

init Carry=0;
init R1=8;

# rol r1
program(0x2610)

C X X

# expects
# Carry=0
# R1=16
0 0 16
*/

/* Test case LDI large:
# auto generated, do not modify
Clk R1


# ldi r1,16
program(0x8010,0x910)

repeat (2) C X

# expects
# R1=16
0 16
*/

/* Test case JMP short:
# auto generated, do not modify
Clk R0

init R0=2;

# jmp end
#  ldi r0, 1
# end: nop
program(0x3d01,0xa01,0x0)

repeat (3) C X

# expects
# R0=2
0 2
*/

/* Test case CPC 210:
# auto generated, do not modify
Clk Carry Zero Neg

init Carry=0;
init R0=2;
init R1=1;

# cpc r0,r1
program(0x1f01)

C X X X

# expects
# Carry=0
# Zero=0
# Neg=0
0 0 0 0
*/

/* Test case CPI 220S:
# auto generated, do not modify
Clk Carry Zero Neg

init Carry=0;
init R0=2;

# cpi r0,2
program(0x2102)

C X X X

# expects
# Carry=0
# Zero=1
# Neg=0
0 0 1 0
*/

/* Test case CPCI 201S:
# auto generated, do not modify
Clk Carry Zero Neg

init Carry=1;
init R0=2;

# cpci r0,0
program(0x2300)

C X X X

# expects
# Carry=0
# Zero=0
# Neg=0
0 0 0 0
*/

/* Test case BRCS jmp:
# auto generated, do not modify
Clk R0

init Carry=1;
init R0=2;

# brcs end
#  ldi r0, 1
# end: nop
program(0x3401,0xa01,0x0)

repeat (3) C X

# expects
# R0=2
0 2
*/

/* Test case BRNE jmp:
# auto generated, do not modify
Clk R0

init Zero=0;
init R0=2;

# brne end
#  ldi r0, 1
# end: nop
program(0x3801,0xa01,0x0)

repeat (3) C X

# expects
# R0=2
0 2
*/

/* Test case ADDI C_out L:
# auto generated, do not modify
Clk Carry R1

init Carry=0;
init R1=-1;

# addi r1,23
program(0x8017,0xb10)

repeat (2) C X X

# expects
# Carry=1
# R1=22
0 1 22
*/

/* Test case ADC C_out:
# auto generated, do not modify
Clk Carry R1 R2

init Carry=0;
init R1=-1;
init R2=3;

# adc r1,r2
program(0x312)

C X X X

# expects
# Carry=1
# R1=2
# R2=3
0 1 2 3
*/

/* Test case SUBI C_in S:
# auto generated, do not modify
Clk Carry R1

init Carry=1;
init R1=3;

# subi r1,2
program(0x1012)

C X X

# expects
# Carry=0
# R1=1
0 0 1
*/

/* Test case SBCI L:
# auto generated, do not modify
Clk Carry R1

init Carry=0;
init R1=23;

# sbci r1,22
program(0x8016,0x1110)

repeat (2) C X X

# expects
# Carry=0
# R1=1
0 0 1
*/

/* Test case NOT:
# auto generated, do not modify
Clk R1

init R1=0;

# not r1
program(0x1a10)

C X

# expects
# R1=65535
0 65535
*/

/* Test case EORI:
# auto generated, do not modify
Clk R1

init R1=16;

# eori r1,24
program(0x8018,0x1810)

repeat (2) C X

# expects
# R1=8
0 8
*/

/* Test case ROL:
# auto generated, do not modify
Clk Carry R1

init Carry=0;
init R1=32776;

# rol r1
program(0x2610)

C X X

# expects
# Carry=1
# R1=16
0 1 16
*/

/* Test case LDI large:
# auto generated, do not modify
Clk R1


# ldi r1,0x8000
program(0x8000,0x911)

repeat (2) C X

# expects
# R1=32768
0 32768
*/

/* Test case JMP short back:
# auto generated, do not modify
Clk R0

init PC=20;

# ldi r0,1
# .org 10
# code: ldi r0,3
# .org 20
# jmp code
#  ldi r0, 2
program(0xa01,0x0,0x0,0x0,0x0,0x0,0x0,0x0,0x0,0x0,0xa03,0x0,0x0,0x0,0x0,0x0,0x0,0x0,0x0,0x0,0x3df5,0xa02)

repeat (2) C X

# expects
# R0=3
0 3
*/

/* Test case CPC 201:
# auto generated, do not modify
Clk Carry Zero Neg

init Carry=1;
init R0=2;
init R1=0;

# cpc r0,r1
program(0x1f01)

C X X X

# expects
# Carry=0
# Zero=0
# Neg=0
0 0 0 0
*/

/* Test case CPI 220L:
# auto generated, do not modify
Clk Carry Zero Neg

init Carry=0;
init R0=22;

# cpi r0,22
program(0x8016,0x2000)

repeat (2) C X X X

# expects
# Carry=0
# Zero=1
# Neg=0
0 0 1 0
*/

/* Test case CPCI 201L:
# auto generated, do not modify
Clk Carry Zero Neg

init Carry=1;
init R0=22;

# cpci r0,20
program(0x8014,0x2200)

repeat (2) C X X X

# expects
# Carry=0
# Zero=0
# Neg=0
0 0 0 0
*/

/* Test case BRCS skip:
# auto generated, do not modify
Clk R0

init Carry=0;
init R0=2;

# brcs end
#  ldi r0, 1
# end: nop
program(0x3401,0xa01,0x0)

repeat (3) C X

# expects
# R0=1
0 1
*/

/* Test case BRNE skip:
# auto generated, do not modify
Clk R0

init Zero=1;
init R0=2;

# brne end
#  ldi r0, 1
# end: nop
program(0x3801,0xa01,0x0)

repeat (3) C X

# expects
# R0=1
0 1
*/
