// Digital circuit ProcessorTwoCycle.dig as structural Verilog
// Einfacher Prozessor, der an die MIPS-Architektur 
// angelehnt ist. Es handelt sich um eine Harvard 
// Single-Cycle CPU.
module ProcessorTwoCycle (
  input  Clock
);

  wire abs, ALU2D, alu_1_p6, alu_1_p7, alu_1_p8, ALUop, br, branch_1_p3, branch_1_p4, branch_1_p5, C, C_in,
       imm, ioR, ioW, ld, muxA, pc_1_p4, S_in, sf, src2D, st, stPC, WE;
  wire [2:0] muxB;
  wire [15:0] driver_1_out, imreg_1_p4, multiplexer_1_out, multiplexer_2_out, multiplexer_3_out, pc_1_p1,
       pc_1_p5, pc_1_p6, register_1_q, register_2_p6, register_2_p7, signext_1_p2, signext_1_p3, signext_1_p4;

  // PC pc_1: pin names not known; wires that end beside it: pc_1_p1, C, abs, pc_1_p4, pc_1_p5, pc_1_p6
  Register #(.Bits(16)) register_1 (.D(driver_1_out), .C(C_in), .en(1'b1), .Q(register_1_q));
  assign driver_1_out = stPC ? pc_1_p5 : 16'bz;  // Driver driver_1
  // ControlTwoCycle controltwocycle_1: pin names not known; wires that end beside it: ioR, ioW, ld, st, br, sf, ALUop, ALU2D, muxA, src2D, muxB, abs, imm, S_in, WE, register_1_q[15:9], stPC
  // Register register_2: pin names not known; wires that end beside it: driver_1_out, C, register_1_q[3:0], register_1_q[7:4], WE, register_2_p6, register_2_p7
  // ImReg imreg_1: pin names not known; wires that end beside it: register_1_q, imm, C, imreg_1_p4
  // SignExt signext_1: pin names not known; wires that end beside it: register_1_q, signext_1_p2, signext_1_p3, signext_1_p4
  assign driver_1_out = src2D ? register_2_p7 : 16'bz;  // Driver driver_2
  Multiplexer #(.Bits(16)) multiplexer_1 (
    .sel(muxA), .in_0(register_2_p6), .in_1(register_2_p7), .out(multiplexer_1_out));
  Multiplexer #(.Selector_Bits(3), .Bits(16)) multiplexer_2 (
    .sel(muxB), .in_0(register_2_p7), .in_1(imreg_1_p4), .in_2({16{1'b0}}), .in_3(16'hff), .in_4(16'hfff),
    .in_5(signext_1_p2), .in_6(signext_1_p3), .in_7(signext_1_p4), .out(multiplexer_2_out));
  // Branch branch_1: pin names not known; wires that end beside it: pc_1_p4, br, branch_1_p3, branch_1_p4, branch_1_p5
  // ALU alu_1: pin names not known; wires that end beside it: multiplexer_1_out, multiplexer_2_out, ALUop, branch_1_p3, pc_1_p1, alu_1_p6, alu_1_p7, alu_1_p8
  // Flags flags_1: pin names not known; wires that end beside it: branch_1_p3, branch_1_p4, branch_1_p5, sf, C, alu_1_p8, alu_1_p7, alu_1_p6
  // ClockDiv clockdiv_1: pin names not known; wires that end beside it: Clock, C_in, S_in, C
  assign driver_1_out = ALU2D ? pc_1_p1 : 16'bz;  // Driver driver_3
  Multiplexer #(.Bits(16)) multiplexer_3 (.sel(S_in), .in_0(pc_1_p1), .in_1(pc_1_p6), .out(multiplexer_3_out));
  Memory memory_1 (.A(multiplexer_3_out), .C(C), .str(st), .ld(ld), .D(driver_1_out));
  // Graphics graphics_1: pin names not known; wires that end beside it: pc_1_p1, ioR, C, ioW, driver_1_out

  // Notes on the sheet:
  //   Clock: Hz: 500000
endmodule
