// Digital circuit ProcessorVHDL.dig as structural Verilog
// Einfacher Prozessor, der an die MIPS-Architektur 
// angelehnt ist. Es handelt sich um eine Harvard 
// Single-Cycle CPU.
module ProcessorVHDL (
  input  Clock,
  input  reset,
  input  U,
  input  D,
  input  R,
  input  L,
  output Y0,
  output Y1,
  output Y2,
  output Y3,
  output Y4,
  output Y5,
  output Y6,
  output Y7,
  output Y8,
  output Y9,
  output Y10,
  output Y11,
  output Y12,
  output Y13,
  output Y14,
  output Y15
);

  wire abs, ALU2D, alu_vhdl_1_p4, alu_vhdl_1_p6, alu_vhdl_1_p7, alu_vhdl_1_p8, branch_1_jmp, flags_1_no,
       flags_1_zo, imm, ioR, ioW, ld, muxA, sf, src2D, st, stPC, WE;
  wire [2:0] br, muxB;
  wire [4:0] ALUop;
  wire [15:0] alu_vhdl_1_p5, imreg_1_imm, ioData, multiplexer_1_out, multiplexer_2_out, multiplexer_3_out,
       multiplexer_4_out, multiplexer_5_out, pc_vhdl_1_next, pc_vhdl_1_pc, ramdualport_1_d, register_1_rdest,
       register_1_rsrc, ROM_d, signext_1__5d, signext_1__5s, signext_1__9sd;

  ROM #(.AddrBits(16), .isProgramMemory("true"), .Bits(16), .Addr_Bits(16)) ROM (
    .A(pc_vhdl_1_pc), .sel(1'b1), .D(ROM_d));
  PC_VHDL pc_vhdl_1 (
    .ALU(multiplexer_5_out), .C(Clock), .abs(abs), .reset(reset), .rel(branch_1_jmp), .Next(pc_vhdl_1_next),
    .PC(pc_vhdl_1_pc));
  PullDown #(.Bits(16)) pulldown_1 (.out(ROM_d));
  Multiplexer #(.Bits(16)) multiplexer_1 (
    .sel(stPC), .in_0(multiplexer_5_out), .in_1(pc_vhdl_1_next), .out(multiplexer_1_out));
  Control control_1 (
    .Op(ROM_d[15:9]), .stPC(stPC), .WE(WE), .imm(imm), .absJmp(abs), .muxB(muxB), .srcToD(src2D),
    .muxA(muxA), .ALUToBus(ALU2D), .ALUop(ALUop), .storeFlags(sf), .Branch(br), .st(st), .ld(ld), .ioW(ioW),
    .ioR(ioR));
  Register register_1 (
    .WD(multiplexer_1_out), .C(Clock), .src(ROM_d[3:0]), .dest(ROM_d[7:4]), .WE(WE),
    .Rdest(register_1_rdest), .Rsrc(register_1_rsrc));
  ImReg imreg_1 (.inst(ROM_d), .en(imm), .C(Clock), .imm(imreg_1_imm));
  SignExt signext_1 (.inst(ROM_d), ._5S(signext_1__5s), ._9SD(signext_1__9sd), ._5D(signext_1__5d));
  Multiplexer #(.Bits(16)) multiplexer_2 (
    .sel(muxA), .in_0(register_1_rdest), .in_1(register_1_rsrc), .out(multiplexer_2_out));
  Multiplexer #(.Selector_Bits(3), .Bits(16)) multiplexer_3 (
    .sel(muxB), .in_0(register_1_rsrc), .in_1(imreg_1_imm), .in_2({16{1'b0}}), .in_3(16'hff), .in_4(16'hfff),
    .in_5(signext_1__5s), .in_6(signext_1__9sd), .in_7(signext_1__5d), .out(multiplexer_3_out));
  Branch branch_1 (.Z(flags_1_zo), .N(flags_1_no), .C(alu_vhdl_1_p4), .ctrl(br), .jmp(branch_1_jmp));
  // ALU_VHDL alu_vhdl_1: pin names not known; wires that end beside it: multiplexer_2_out, multiplexer_3_out, ALUop, alu_vhdl_1_p4, alu_vhdl_1_p5, alu_vhdl_1_p6, alu_vhdl_1_p7, alu_vhdl_1_p8
  Flags flags_1 (
    .Zi(alu_vhdl_1_p6), .Ni(alu_vhdl_1_p7), .Ci(alu_vhdl_1_p8), .C(Clock), .store(sf), .Zo(flags_1_zo),
    .No(flags_1_no), .Co(alu_vhdl_1_p4));
  // GPI_VHDL gpi_vhdl_1: pin names not known; wires that end beside it: U, L, R, D, ioData
  RAMDualPort #(.AddrBits(10), .Bits(16), .Addr_Bits(10)) ramdualport_1 (
    .A(alu_vhdl_1_p5[9:0]), .Din(register_1_rsrc), .str(st), .C(Clock), .ld(ld), .D(ramdualport_1_d));
  // GPO gpo_1: pin names not known; wires that end beside it: register_1_rsrc, alu_vhdl_1_p5, Clock, ioW, Y0, Y1, Y2, Y3, Y4, Y5, Y6, Y7, Y8, Y9, Y10, Y11, Y12, Y13, Y14, Y15
  Multiplexer #(.Bits(16)) multiplexer_4 (
    .sel(ld), .in_0(alu_vhdl_1_p5), .in_1(ramdualport_1_d), .out(multiplexer_4_out));
  Multiplexer #(.Bits(16)) multiplexer_5 (.sel(ioR), .in_0(multiplexer_4_out), .in_1(ioData), .out(multiplexer_5_out));

  // Other names for the same wires on the sheet: C = Clock; res = reset

  // Notes on the sheet:
  //   Clock: pin W5, Hz: 200
  //   Y0: pin U16
  //   Y1: pin E19
  //   Y2: pin U19
  //   Y3: pin V19
  //   Y4: pin W18
  //   Y5: pin U15
  //   Y6: pin U14
  //   Y7: pin V14
  //   Y8: pin V13
  //   Y9: pin V3
  //   Y10: pin W3
  //   Y11: pin U3
  //   Y12: pin P3
  //   Y13: pin N3
  //   Y14: pin P1
  //   Y15: pin L1
  //   reset: pin U18
  //   U: pin T18
  //   D: pin U17
  //   R: pin T17
  //   L: pin W19
  //   Board: BASYS3
  //   contents of ROM (hex, n*v repeats v):
  //   20e1,14f4,4cef,6e0b,20e1,14f8,4cef,6e07,20e1,14fc,4cef,6e0c,8032,1220,6e13,1401,1510,
  //   7350,3e00,2011,65fc,4efe,18e1,6a0f,8000,1300,1510,7350,4000,2011,65fc,4efe,18e1,6a0f,
  //   7800,3c00,5e0c,210,2811,6422,210,2818,6431,210,2812,6404,210,2814,640c,6a02,8036,
  //   1220,1580,1491,7359,3e90,2081,6402,1580,1491,6fe5,8042,1220,1580,8000,1390,7359,4090,
  //   2081,6403,1580,8000,1390,6fd8,804e,1220,1491,14a0,7359,3ca0,6406,3e90,8000,3b90,65cd,
  //   14a1,6fcb,4090,3c91,65c8,14a0,6fc6,8061,1220,1484,9111,1290,7359,3e90,2081,6403,1484,
  //   9111,1290,6fb9
endmodule

/* Test case:
     reset Clock U D L R Y15 Y14 Y13 Y12 Y11 Y10 Y9 Y8 Y7 Y6 Y5 Y4 Y3 Y2 Y1 Y0
     1         0 0 0 0 0  x   x    x  x   x   x   x  x  x  x  x  x  x  x  x  x
     1         1 0 0 0 0  x   x    x  x   x   x   x  x  x  x  x  x  x  x  x  x
     0         0 0 0 0 0  x   x    x  x   x   x   x  x  x  x  x  x  x  x  x  x

repeat(5) 0    C 0 0 0 0  x   x    x  x   x   x   x  x  x  x  x  x  x  x  x  x
          0    C 0 0 0 0  0   0    0  0   0   0   0  0  0  0  0  0  0  0  0  1

loop(i,15)
repeat(3) 0    C 0 0 0 0  x   x    x  x   x   x   x  x  x  x  x  x  x  x  x  x
          0    C 0 0 0 0  bits(16,1<<(i+1))
end loop

repeat(9) 0    C 0 0 0 0  x   x    x  x   x   x   x  x  x  x  x  x  x  x  x  x

loop(i,16)
repeat(3) 0    C 0 0 0 0  x   x    x  x   x   x   x  x  x  x  x  x  x  x  x  x
          0    C 0 0 0 0  bits(16,1<<i)
end loop

repeat(10) 0   C 0 0 0 0  x   x    x  x   x   x   x  x  x  x  x  x  x  x  x  x

loop(i,15)
repeat(3) 0    C 0 0 0 0  x   x    x  x   x   x   x  x  x  x  x  x  x  x  x  x
          0    C 0 0 0 0  bits(16,1<<(15-i))
end loop
*/
