// Digital circuit Register.dig as structural Verilog
module Register (
  input  [15:0] WD,
  input  C,
  input  [3:0] src,
  input  [3:0] dest,
  input  WE,
  output [15:0] Rdest,
  output [15:0] Rsrc
);

  wire demultiplexer_1_out_0, demultiplexer_1_out_1, demultiplexer_1_out_2, demultiplexer_1_out_3,
       demultiplexer_1_out_4, demultiplexer_1_out_5, demultiplexer_1_out_6, demultiplexer_1_out_7,
       demultiplexer_1_out_8, demultiplexer_1_out_9, demultiplexer_1_out_10, demultiplexer_1_out_11,
       demultiplexer_1_out_12, demultiplexer_1_out_13, demultiplexer_1_out_14, demultiplexer_1_out_15;
  wire [15:0] BP_q, R10_q, R11_q, R12_q, R_0_q, R_1_q, R_2_q, R_3_q, R_4_q, R_5_q, R_6_q, R_7_q, R_8_q,
       R_9_q, RA_q, SP_q;

  Demultiplexer #(.Selector_Bits(4)) demultiplexer_1 (
    .sel(dest), .in(WE), .out_0(demultiplexer_1_out_0), .out_1(demultiplexer_1_out_1),
    .out_2(demultiplexer_1_out_2), .out_3(demultiplexer_1_out_3), .out_4(demultiplexer_1_out_4),
    .out_5(demultiplexer_1_out_5), .out_6(demultiplexer_1_out_6), .out_7(demultiplexer_1_out_7),
    .out_8(demultiplexer_1_out_8), .out_9(demultiplexer_1_out_9), .out_10(demultiplexer_1_out_10),
    .out_11(demultiplexer_1_out_11), .out_12(demultiplexer_1_out_12), .out_13(demultiplexer_1_out_13),
    .out_14(demultiplexer_1_out_14), .out_15(demultiplexer_1_out_15));
  Register #(.Bits(16)) R_0 (.D(WD), .C(C), .en(demultiplexer_1_out_0), .Q(R_0_q));
  Register #(.Bits(16)) R_1 (.D(WD), .C(C), .en(demultiplexer_1_out_1), .Q(R_1_q));
  Register #(.Bits(16)) R_2 (.D(WD), .C(C), .en(demultiplexer_1_out_2), .Q(R_2_q));
  Register #(.Bits(16)) R_3 (.D(WD), .C(C), .en(demultiplexer_1_out_3), .Q(R_3_q));
  Register #(.Bits(16)) R_4 (.D(WD), .C(C), .en(demultiplexer_1_out_4), .Q(R_4_q));
  Register #(.Bits(16)) R_5 (.D(WD), .C(C), .en(demultiplexer_1_out_5), .Q(R_5_q));
  Register #(.Bits(16)) R_6 (.D(WD), .C(C), .en(demultiplexer_1_out_6), .Q(R_6_q));
  Register #(.Bits(16)) R_7 (.D(WD), .C(C), .en(demultiplexer_1_out_7), .Q(R_7_q));
  Register #(.Bits(16)) R_8 (.D(WD), .C(C), .en(demultiplexer_1_out_8), .Q(R_8_q));
  Register #(.Bits(16)) R_9 (.D(WD), .C(C), .en(demultiplexer_1_out_9), .Q(R_9_q));
  Register #(.Bits(16)) R10 (.D(WD), .C(C), .en(demultiplexer_1_out_10), .Q(R10_q));
  Register #(.Bits(16)) R11 (.D(WD), .C(C), .en(demultiplexer_1_out_11), .Q(R11_q));
  Register #(.Bits(16)) R12 (.D(WD), .C(C), .en(demultiplexer_1_out_12), .Q(R12_q));
  Register #(.Bits(16)) BP (.D(WD), .C(C), .en(demultiplexer_1_out_13), .Q(BP_q));
  Register #(.Bits(16)) SP (.D(WD), .C(C), .en(demultiplexer_1_out_14), .Q(SP_q));
  Register #(.Bits(16)) RA (.D(WD), .C(C), .en(demultiplexer_1_out_15), .Q(RA_q));
  Multiplexer #(.Selector_Bits(4), .Bits(16)) multiplexer_1 (
    .sel(dest), .in_0(R_0_q), .in_1(R_1_q), .in_2(R_2_q), .in_3(R_3_q), .in_4(R_4_q), .in_5(R_5_q),
    .in_6(R_6_q), .in_7(R_7_q), .in_8(R_8_q), .in_9(R_9_q), .in_10(R10_q), .in_11(R11_q), .in_12(R12_q),
    .in_13(BP_q), .in_14(SP_q), .in_15(RA_q), .out(Rdest));
  Multiplexer #(.Selector_Bits(4), .Bits(16)) multiplexer_2 (
    .sel(src), .in_0(R_0_q), .in_1(R_1_q), .in_2(R_2_q), .in_3(R_3_q), .in_4(R_4_q), .in_5(R_5_q),
    .in_6(R_6_q), .in_7(R_7_q), .in_8(R_8_q), .in_9(R_9_q), .in_10(R10_q), .in_11(R11_q), .in_12(R12_q),
    .in_13(BP_q), .in_14(SP_q), .in_15(RA_q), .out(Rsrc));
endmodule
