// Digital circuit Rising.dig as structural Verilog
// Ein Baustein zum asynchronen Speichern.
// Sobald der Set Eingang auf 1 geht, wird der 
// Ausgang auf 1 geschaltet. Der Ausgang geht 
// erst wieder auf 0 zurück, wenn Reset auf 1 
// gesetzt wird.
module Rising (
  input  Reset,
  input  Set,
  output Out
);

  wire not_1_out, or_1_out;

  or or_1 (or_1_out, Set, Out);
  and and_1 (Out, or_1_out, not_1_out);
  not not_1 (not_1_out, Reset);

  // Notes on the sheet:
  //   Reset: Setzt den Ausgang zurück auf 0.
  //   Set: Setzt den Ausgang auf 1.
  //   Out: Wechselt auf 1 sobald Set auf 1 wechselt.
endmodule
