// Digital circuit SWAPN.dig as structural Verilog
// Tauscht im High-Byte und im Low-Byte die beiden 
// 4-Bit Nibble.
module SWAPN (
  input  [15:0] Di,
  output [15:0] Do
);


  assign Do = {Di[11:8], Di[15:12], Di[3:0], Di[7:4]};

  // Notes on the sheet:
  //   Di: Dateneingang
  //   Do: Datenausgang
endmodule
