// Digital circuit SignExt.dig as structural Verilog
module SignExt (
  input  [15:0] inst,
  output [15:0] _5S,
  output [15:0] _9SD,
  output [15:0] _5D
);


  assign _5D = {{11{1'b0}}, inst[8:4]};
  assign _5S = {{11{1'b0}}, inst[8], inst[3:0]};
  assign _9SD = {{8{inst[8]}}, inst[7:0]};
endmodule
