// Digital circuit demo.dig as structural Verilog
module demo (
  input  Clk,
  output R0,
  output G0,
  output B0,
  output R1,
  output G1,
  output B1,
  output R2,
  output G2,
  output B2,
  output R3,
  output G3,
  output B3,
  output H_sync,
  output V_sync
);

  wire comparator_1_eq, comparator_2_eq, comparator_3_eq, comparator_4_eq, data_1_pixel, or_1_out, sync_1_oe;
  wire [8:0] sync_1_y;
  wire [9:0] sync_1_x;

  sync sync_1 (.C(Clk), .X(sync_1_x), .Y(sync_1_y), .oe(sync_1_oe), .H_sync(H_sync), .V_sync(V_sync));
  Comparator #(.Bits(10)) comparator_1 (.a(sync_1_x), .b({10{1'b0}}), .eq(comparator_1_eq));  // open: gt, lt
  Comparator #(.Bits(10)) comparator_2 (.a(sync_1_x), .b(10'h27f), .eq(comparator_2_eq));  // open: gt, lt
  Comparator #(.Bits(9)) comparator_3 (.a(sync_1_y), .b({9{1'b0}}), .eq(comparator_3_eq));  // open: gt, lt
  Comparator #(.Bits(9)) comparator_4 (.a(sync_1_y), .b(9'h1df), .eq(comparator_4_eq));  // open: gt, lt
  data data_1 (.X(sync_1_x), .Y(sync_1_y), .Pixel(data_1_pixel));
  or or_1 (or_1_out, comparator_1_eq, comparator_2_eq, comparator_3_eq, comparator_4_eq, data_1_pixel);
  and and_1 (B0, or_1_out, sync_1_oe);

  assign B1 = B0;
  assign B2 = B0;
  assign B3 = B0;
  assign G0 = B0;
  assign G1 = B0;
  assign G2 = B0;
  assign G3 = B0;
  assign R0 = B0;
  assign R1 = B0;
  assign R2 = B0;
  assign R3 = B0;

  // Notes on the sheet:
  //   Clk: pin W5, Hz: 25175000
  //   R0: pin G19
  //   G0: pin J17
  //   B0: pin N18
  //   R1: pin H19
  //   G1: pin H17
  //   B1: pin L18
  //   R2: pin J19
  //   G2: pin G17
  //   B2: pin K18
  //   R3: pin N19
  //   G3: pin D17
  //   B3: pin J18
  //   H_sync: pin P19
  //   V_sync: pin R19
  //   Board: BASYS3
endmodule
