// Digital circuit sync.dig as structural Verilog
// Designed for a 
// 25.175MHz clock.
// Generates 
// 640x480@60Hz
// {{de Ausgelegt für einen 
// 25.175MHz Takt.
// Erzeugt
// 640x480@60Hz}}
module sync (
  input  C,
  output [9:0] X,
  output [8:0] Y,
  output oe,
  output H_sync,
  output V_sync
);

  wire and_1_out, comparator_1_eq, comparator_2_eq, comparator_3_eq, comparator_4_eq, comparator_5_eq,
       comparator_6_eq, comparator_7_eq, comparator_8_eq, jk_ff_2_q, jken_1_p5;
  wire [9:9] v_cnt_out;

  Counter #(.Bits(10)) h_cnt (.en(1'b1), .C(C), .clr(comparator_4_eq), .out(X));  // open: ovf
  Comparator #(.Bits(10)) comparator_1 (.a(X), .b(10'h28f), .eq(comparator_1_eq));  // open: gt, lt
  Comparator #(.Bits(10)) comparator_2 (.a(X), .b(10'h2ef), .eq(comparator_2_eq));  // open: gt, lt
  Comparator #(.Bits(10)) comparator_3 (.a(X), .b(10'h27f), .eq(comparator_3_eq));  // open: gt, lt
  Comparator #(.Bits(10)) comparator_4 (.a(X), .b(10'h31f), .eq(comparator_4_eq));  // open: gt, lt
  and and_1 (and_1_out, comparator_4_eq, comparator_5_eq);
  JK_FF jk_ff_1 (.J(comparator_1_eq), .C(C), .K(comparator_2_eq), .nQ(H_sync));  // open: Q
  JK_FF #(.Default(1)) jk_ff_2 (.J(comparator_4_eq), .C(C), .K(comparator_3_eq), .Q(jk_ff_2_q));  // open: nQ
  Counter #(.Bits(10)) v_cnt (.en(comparator_4_eq), .C(C), .clr(and_1_out), .out({v_cnt_out[9], Y}));  // open: ovf
  Comparator #(.Bits(10)) comparator_5 (.a({v_cnt_out[9], Y}), .b(10'h20c), .eq(comparator_5_eq));  // open: gt, lt
  Comparator #(.Bits(10)) comparator_6 (.a({v_cnt_out[9], Y}), .b(10'h1df), .eq(comparator_6_eq));  // open: gt, lt
  Comparator #(.Bits(10)) comparator_7 (.a({v_cnt_out[9], Y}), .b(10'h1e9), .eq(comparator_7_eq));  // open: gt, lt
  Comparator #(.Bits(10)) comparator_8 (.a({v_cnt_out[9], Y}), .b(10'h1eb), .eq(comparator_8_eq));  // open: gt, lt
  // JKen jken_1: pin names not known; wires that end beside it: comparator_4_eq, comparator_5_eq, C, comparator_6_eq, jken_1_p5
  // JKen jken_2: pin names not known; wires that end beside it: comparator_4_eq, comparator_7_eq, C, comparator_8_eq, V_sync
  and and_2 (oe, jk_ff_2_q, jken_1_p5);

  // Notes on the sheet:
  //   X: The x coordinate of visible pixel.
  //   Is valid only if oe is high.
  //   {{de Die x-Koordinate des sichtbaren Pixels.
  //   Nur gültig, wenn oe auf HIGH gesetzt ist.}}
  //   C: Hz: 20
  //   Y: The y coordinate of visible pixel.
  //   Is valid only if oe is high.
  //   {{de Die y-Koordinate des sichtbaren Pixels.
  //   Nur gültig, wenn oe auf HIGH gesetzt ist.}}
  //   oe: If oe is high the x- and y-coordinates are valid and 
  //   a visible pixel is to output.
  //   {{de Wenn oe HIGH ist, sind x- und y-Koordinate
  //   gültig, und es muss ein Pixel ausgegeben werden.}}
  //   H_sync: The horizontal sync signal. Is low active.
  //   {{de Das horizontale sync-Signal. Ist Active Low}}
  //   V_sync: The vertical sync signal. Is low active.
  //   {{de Das vertikale sync-Signal. Ist Active Low}}
  //   Designed for a 
  //   25.175MHz clock.
  //   Generates 
  //   640x480@60Hz
  //   Designed for a 
  //   25.175MHz clock.
  //   Generates 
  //   640x480@60Hz
  //   {{de Ausgelegt für einen 
  //   25.175MHz Takt.
  //   Erzeugt
  //   640x480@60Hz}}
endmodule

/* Test case H-Sync:
C H-sync oe X

repeat(799) C x x  x

loop (n,3)
loop (p,800)
C  ((p<640+16)|(p>=640+16+96)) (p<640) (p)
end loop
end loop
*/

/* Test case X-Y:
C X Y oe H-sync V-sync

# skip first image
repeat(419999) C x x x x x

# test second image coordiates
loop (i,2)
  loop (y,525)
    loop (x,800)
      C (x) (y) ((x<640)&(y<480)) ((x<640+16)|(x>=640+16+96)) ((y<480+10)|(y>=480+12))
    end loop
  end loop
end loop
*/
