// Digital circuit textMode.dig as structural Verilog
module textMode (
  input  [15:0] D_in,
  input  str,
  input  ld,
  input  [11:0] A,
  input  C,
  input  [9:0] X,
  input  [8:0] Y,
  output [15:0] D,
  output [11:0] Col
);

  wire bitselector_1_out;
  wire [3:0] multiplexer_1_out;
  wire [7:0] Font_d;
  wire [11:4] GraphicRam_d2;
  wire [15:8] GraphicRam_d2_2;

  RAMDualAccess #(.AddrBits(12), .Bits(16)) GraphicRam (
    .str(str), .C(C), .ld(ld), .A1(A), .Din1(D_in), .A2({Y[8:4], X[9:3]}), .D1(D),
    .D2({GraphicRam_d2_2, GraphicRam_d2}));
  ROM #(.AddrBits(12), .Bits(8)) Font (.A({GraphicRam_d2, Y[3:0]}), .sel(1'b1), .D(Font_d));
  BitSelector #(.Selector_Bits(3)) bitselector_1 (.in(Font_d), .sel(X[2:0]), .out(bitselector_1_out));
  Multiplexer #(.Bits(4)) multiplexer_1 (
    .sel(bitselector_1_out), .in_0(GraphicRam_d2_2[11:8]), .in_1(GraphicRam_d2_2[15:12]),
    .out(multiplexer_1_out));
  ROM #(.AddrBits(4), .Bits(12)) Palette (.A(multiplexer_1_out), .sel(1'b1), .D(Col));

  // Notes on the sheet:
  //   contents of Font (hex, n*v repeats v):
  //   0,0,0,0,0,0,0,18,18,0,0,0,0,0,0,0,0,0,7e,81,a5,81,81,bd,99,81,81,7e,0,0,0,0,0,0,7e,
  //   ff,db,ff,ff,c3,e7,ff,ff,7e,0,0,0,0,0,0,0,0,36,7f,7f,7f,7f,3e,1c,8,0,0,0,0,0,0,0,0,
  //   8,1c,3e,7f,3e,1c,8,0,0,0,0,0,0,0,0,18,3c,3c,e7,e7,e7,18,18,3c,0,0,0,0,0,0,0,18,3c,
  //   7e,ff,ff,7e,18,18,3c,0,0,0,0,0,0,0,0,0,0,18,3c,3c,18,0,0,0,0,0,0,ff,ff,ff,ff,ff,ff,
  //   e7,c3,c3,e7,ff,ff,ff,ff,ff,ff,0,0,0,0,0,3c,66,42,42,66,3c,0,0,0,0,0,ff,ff,ff,ff,ff,
  //   c3,99,bd,bd,99,c3,ff,ff,ff,ff,ff,0,0,78,70,58,4c,1e,33,33,33,33,1e,0,0,0,0,0,0,3c,
  //   66,66,66,66,3c,18,7e,18,18,0,0,0,0,0,0,fc,cc,fc,c,c,c,c,e,f,7,0,0,0,0,0,0,fe,c6,fe,
  //   c6,c6,c6,c6,e6,e7,67,3,0,0,0,0,0,0,18,18,db,3c,e7,3c,db,18,18,0,0,0,0,0,1,3,7,f,1f,
  //   7f,1f,f,7,3,1,0,0,0,0,0,40,60,70,78,7c,7f,7c,78,70,60,40,0,0,0,0,0,0,18,3c,7e,18,
  //   18,18,7e,3c,18,0,0,0,0,0,0,0,66,66,66,66,66,66,66,0,66,66,0,0,0,0,0,0,fe,db,db,db,
  //   de,d8,d8,d8,d8,d8,0,0,0,0,0,3e,63,6,1c,36,63,63,36,1c,30,63,3e,0,0,0,0,0,0,0,0,0,
  //   0,0,7f,7f,7f,7f,0,0,0,0,0,0,18,3c,7e,18,18,18,7e,3c,18,7e,0,0,0,0,0,0,18,3c,7e,18,
  //   18,18,18,18,18,18,0,0,0,0,0,0,18,18,18,18,18,18,18,7e,3c,18,0,0,0,0,0,0,0,0,0,18,
  //   30,7f,30,18,0,0,0,0,0,0,0,0,0,0,0,c,6,7f,6,c,0,0,0,0,0,0,0,0,0,0,0,0,3,3,3,7f,0,0,
  //   0,0,0,0,0,0,0,0,0,24,66,ff,66,24,0,0,0,0,0,0,0,0,0,0,8,1c,1c,3e,3e,7f,7f,0,0,0,0,
  //   0,0,0,0,0,7f,7f,3e,3e,1c,1c,8,0,0,0,0,0,0,0,0,0,0,0,0,0,0,0,0,0,0,0,0,0,0,0,18,3c,
  //   3c,3c,18,18,18,0,18,18,0,0,0,0,0,66,66,66,24,0,0,0,0,0,0,0,0,0,0,0,0,0,0,36,36,7f,
  //   36,36,36,7f,36,36,0,0,0,0,18,18,3e,63,43,3,3e,60,60,61,63,3e,18,18,0,0,0,0,0,0,43,
  //   63,30,18,c,6,63,61,0,0,0,0,0,0,1c,36,36,1c,6e,3b,33,33,33,6e,0,0,0,0,0,c,c,c,6,0,
  //   0,0,0,0,0,0,0,0,0,0,0,0,30,18,c,c,c,c,c,c,18,30,0,0,0,0,0,0,c,18,30,30,30,30,30,30,
  //   18,c,0,0,0,0,0,0,0,0,0,66,3c,ff,3c,66,0,0,0,0,0,0,0,0,0,0,0,18,18,7e,18,18,0,0,0,
  //   0,0,0,0,0,0,0,0,0,0,0,0,18,18,18,c,0,0,0,0,0,0,0,0,0,0,7f,0,0,0,0,0,0,0,0,0,0,0,0,
  //   0,0,0,0,0,0,18,18,0,0,0,0,0,0,0,0,40,60,30,18,c,6,3,1,0,0,0,0,0,0,3c,66,c3,c3,db,
  //   db,c3,c3,66,3c,0,0,0,0,0,0,18,1c,1e,18,18,18,18,18,18,7e,0,0,0,0,0,0,3e,63,60,30,
  //   18,c,6,3,63,7f,0,0,0,0,0,0,3e,63,60,60,3c,60,60,60,63,3e,0,0,0,0,0,0,30,38,3c,36,
  //   33,7f,30,30,30,78,0,0,0,0,0,0,7f,3,3,3,3f,60,60,60,63,3e,0,0,0,0,0,0,1c,6,3,3,3f,
  //   63,63,63,63,3e,0,0,0,0,0,0,7f,63,60,60,30,18,c,c,c,c,0,0,0,0,0,0,3e,63,63,63,3e,63,
  //   63,63,63,3e,0,0,0,0,0,0,3e,63,63,63,7e,60,60,60,30,1e,0,0,0,0,0,0,0,0,18,18,0,0,0,
  //   18,18,0,0,0,0,0,0,0,0,0,18,18,0,0,0,18,18,c,0,0,0,0,0,0,0,60,30,18,c,6,c,18,30,60,
  //   0,0,0,0,0,0,0,0,0,7e,0,0,7e,0,0,0,0,0,0,0,0,0,0,6,c,18,30,60,30,18,c,6,0,0,0,0,0,
  //   0,3e,63,63,30,18,18,18,0,18,18,0,0,0,0,0,0,0,3e,63,63,7b,7b,7b,3b,3,3e,0,0,0,0,0,
  //   0,8,1c,36,63,63,7f,63,63,63,63,0,0,0,0,0,0,3f,66,66,66,3e,66,66,66,66,3f,0,0,0,0,
  //   0,0,3c,66,43,3,3,3,3,43,66,3c,0,0,0,0,0,0,1f,36,66,66,66,66,66,66,36,1f,0,0,0,0,0,
  //   0,7f,66,46,16,1e,16,6,46,66,7f,0,0,0,0,0,0,7f,66,46,16,1e,16,6,6,6,f,0,0,0,0,0,0,
  //   3c,66,43,3,3,7b,63,63,66,5c,0,0,0,0,0,0,63,63,63,63,7f,63,63,63,63,63,0,0,0,0,0,0,
  //   3c,18,18,18,18,18,18,18,18,3c,0,0,0,0,0,0,78,30,30,30,30,30,33,33,33,1e,0,0,0,0,0,
  //   0,67,66,66,36,1e,1e,36,66,66,67,0,0,0,0,0,0,f,6,6,6,6,6,6,46,66,7f,0,0,0,0,0,0,c3,
  //   e7,ff,ff,db,c3,c3,c3,c3,c3,0,0,0,0,0,0,63,67,6f,7f,7b,73,63,63,63,63,0,0,0,0,0,0,
  //   3e,63,63,63,63,63,63,63,63,3e,0,0,0,0,0,0,3f,66,66,66,3e,6,6,6,6,f,0,0,0,0,0,0,3e,
  //   63,63,63,63,63,63,6b,7b,3e,30,70,0,0,0,0,3f,66,66,66,3e,36,66,66,66,67,0,0,0,0,0,
  //   0,3e,63,63,6,1c,30,60,63,63,3e,0,0,0,0,0,0,ff,db,99,18,18,18,18,18,18,3c,0,0,0,0,
  //   0,0,63,63,63,63,63,63,63,63,63,3e,0,0,0,0,0,0,c3,c3,c3,c3,c3,c3,c3,66,3c,18,0,0,0,
  //   0,0,0,c3,c3,c3,c3,c3,db,db,ff,66,66,0,0,0,0,0,0,c3,c3,66,3c,18,18,3c,66,c3,c3,0,0,
  //   0,0,0,0,c3,c3,c3,66,3c,18,18,18,18,3c,0,0,0,0,0,0,ff,c3,61,30,18,c,6,83,c3,ff,0,0,
  //   0,0,0,0,3c,c,c,c,c,c,c,c,c,3c,0,0,0,0,0,0,0,1,3,7,e,1c,38,70,60,40,0,0,0,0,0,0,3c,
  //   30,30,30,30,30,30,30,30,3c,0,0,0,0,8,1c,36,63,0,0,0,0,0,0,0,0,0,0,0,0,0,0,0,0,0,0,
  //   0,0,0,0,0,0,0,ff,0,0,c,c,18,0,0,0,0,0,0,0,0,0,0,0,0,0,0,0,0,0,0,1e,30,3e,33,33,33,
  //   6e,0,0,0,0,0,0,7,6,6,1e,36,66,66,66,66,3e,0,0,0,0,0,0,0,0,0,3e,63,3,3,3,63,3e,0,0,
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  //   contents of Palette (hex, n*v repeats v):
  //   0,888,f,f0,f00,ff,ff0,f0f,8,80,800,88,880,808,ccc,fff
endmodule
