// Digital circuit VGAExample.dig as structural Verilog
module VGAExample (
  input  Clock,
  input  rst,
  input  U,
  input  D,
  input  R,
  input  L,
  output Y0,
  output Y1,
  output Y2,
  output Y3,
  output Y4,
  output Y5,
  output Y6,
  output Y7,
  output Y8,
  output Y9,
  output Y10,
  output Y11,
  output Y12,
  output Y13,
  output Y14,
  output Y15,
  output VGA_R0,
  output VGA_G0,
  output VGA_B0,
  output VGA_R1,
  output VGA_G1,
  output VGA_B1,
  output VGA_R2,
  output VGA_G2,
  output VGA_B2,
  output VGA_R3,
  output VGA_G3,
  output VGA_B3,
  output H_sync,
  output V_sync
);

  wire C, d_ff_1_nq, gpi_hdl_1_p7, gpi_hdl_1_p8, ioR, ioW, vga_1_p7, vga_1_p8;
  wire [15:0] A, Dout, processormux_1_pc, readselect_1_p9, ROM_d;

  // VGA vga_1: pin names not known; wires that end beside it: C, Dout, ioW, ioR, A, Clock, vga_1_p7, vga_1_p8, H_sync, V_sync, {VGA_B3, VGA_B2, VGA_B1, VGA_B0, VGA_G3, VGA_G2, VGA_G1, VGA_G0, VGA_R3, VGA_R2, VGA_R1, VGA_R0}
  // GPI_HDL gpi_hdl_1: pin names not known; wires that end beside it: A, ioR, U, L, R, D, gpi_hdl_1_p7, gpi_hdl_1_p8
  VGA vga_2 (
    .R({VGA_R3, VGA_R2, VGA_R1, VGA_R0}), .G({VGA_G3, VGA_G2, VGA_G1, VGA_G0}),
    .B({VGA_B3, VGA_B2, VGA_B1, VGA_B0}), .H(H_sync), .V(V_sync), .C(Clock));
  // readSelect readselect_1: pin names not known; wires that end beside it: gpi_hdl_1_p7, gpi_hdl_1_p8, vga_1_p7, vga_1_p8, {16{1'b0}}, 1'b0, {16{1'b0}}, 1'b0, readselect_1_p9
  D_FF d_ff_1 (.D(d_ff_1_nq), .C(Clock), .Q(C), .nQ(d_ff_1_nq));
  ProcessorMux processormux_1 (
    .Instr(ROM_d), .Clock(C), .reset(rst), .D_in(readselect_1_p9), .PC(processormux_1_pc), .D_out(Dout),
    .Addr(A), .ioR(ioR), .ioW(ioW));
  ROM #(.AddrBits(16), .isProgramMemory("true"), .Bits(16), .Addr_Bits(16)) ROM (
    .A(processormux_1_pc), .sel(1'b1), .D(ROM_d));
  // GPO gpo_1: pin names not known; wires that end beside it: Y15, Y14, Y13, Y12, Y11, Y10, Y9, Y8, Y7, Y6, Y5, Y4, ioW, Y3, C, Y2, A, Y1, Dout, Y0

  // Other names for the same wires on the sheet: PC = Clock

  // Notes on the sheet:
  //   Clock: pin W5, Hz: 25175000
  //   Y0: pin U16
  //   Y1: pin E19
  //   Y2: pin U19
  //   Y3: pin V19
  //   Y4: pin W18
  //   Y5: pin U15
  //   Y6: pin U14
  //   Y7: pin V14
  //   Y8: pin V13
  //   Y9: pin V3
  //   Y10: pin W3
  //   Y11: pin U3
  //   Y12: pin P3
  //   Y13: pin N3
  //   Y14: pin P1
  //   Y15: pin L1
  //   rst: pin U18
  //   U: pin T18
  //   D: pin U17
  //   R: pin T17
  //   L: pin W19
  //   VGA_R0: pin G19
  //   VGA_G0: pin J17
  //   VGA_B0: pin N18
  //   VGA_R1: pin H19
  //   VGA_G1: pin H17
  //   VGA_B1: pin L18
  //   VGA_R2: pin J19
  //   VGA_G2: pin G17
  //   VGA_B2: pin K18
  //   VGA_R3: pin N19
  //   VGA_G3: pin D17
  //   VGA_B3: pin J18
  //   H_sync: pin P19
  //   V_sync: pin R19
  //   Pin numbers are defined to match the BASYS3 FPGA board.
  //   {{de Die Pin-Nummern sind angepasst an ein BASYS3 FPGA Board.}}
  //   contents of ROM (hex, n*v repeats v):
  //   a00,2ec0,8020,900,2e50,8021,900,2eb0,8048,900,2e00,8057,900,2e60,8064,900,2ea0,8065,
  //   900,2e10,806c,900,2e20,2e30,2e90,806f,900,2e40,2e70,8072,900,2e80,8028,900,a1f,a30,
  //   2c23,2120,3505,80b2,3af0,c31,c01,3df8,b0cd,920,a01,a10,80b2,3af0,801d,910,80b2,3af0,
  //   c01,8050,2000,38f5,b0ba,920,a11,a00,80b2,3af0,804f,900,80b2,3af0,c11,801e,2010,38f5,
  //   b0c9,920,a00,a10,80b2,3af0,b0bb,920,804f,900,a10,80b2,3af0,b0c8,920,a00,801d,910,
  //   80b2,3af0,b0bc,920,804f,900,801d,910,80b2,3af0,f000,921,a11,a01,80b2,3af0,c21,c01,
  //   8011,2000,38f9,c11,8011,2010,38f4,4400,a1f,8027,900,a002,920,80a9,3af0,10e1,2be4,
  //   80a2,3af0,2c2e,ce1,80b2,3af0,8014,41a0,30bd,2eda,1ba,15b1,3503,2111,3501,1011,1ba,
  //   15b2,3503,2101,3501,1001,1ba,15b4,3504,804e,2000,3501,c01,1ba,15b8,35da,801c,2010,
  //   35d7,c11,3dd5,ab5,aa0,10a1,38fe,10b1,38fc,3b0f,1a1,29a0,25a0,7a0,8000,ba1,434a,40a2,
  //   3b0f,1a1,29a0,25a0,7a0,8000,ba1,40a2,3b0f
endmodule
