// Digital circuit VHDLExample.dig as structural Verilog
// Einfacher Prozessor, der an die MIPS-Architektur 
// angelehnt ist. Es handelt sich um eine Harvard 
// Single-Cycle CPU.
module VHDLExample (
  input  Clock,
  input  reset,
  input  U,
  input  D,
  input  R,
  input  L,
  output Y0,
  output Y1,
  output Y2,
  output Y3,
  output Y4,
  output Y5,
  output Y6,
  output Y7,
  output Y8,
  output Y9,
  output Y10,
  output Y11,
  output Y12,
  output Y13,
  output Y14,
  output Y15
);

  wire gpi_vhdl_1_p8, processormux_1_p4, processormux_1_p5, processormux_1_p6;

  // GPI_VHDL gpi_vhdl_1: pin names not known; wires that end beside it: U, L, R, D, Y15, Y14, Y13, gpi_vhdl_1_p8, Y12, Y11
  // ProcessorMux processormux_1: pin names not known; wires that end beside it: Clock, reset, gpi_vhdl_1_p8, processormux_1_p4, processormux_1_p5, processormux_1_p6
  // GPO gpo_1: pin names not known; wires that end beside it: Y10, Y9, Y8, Y7, Y6, Y5, Y4, processormux_1_p6, Y3, Clock, Y2, processormux_1_p5, Y1, processormux_1_p4, Y0

  // Notes on the sheet:
  //   Clock: pin W5, Hz: 200
  //   Y0: pin U16
  //   Y1: pin E19
  //   Y2: pin U19
  //   Y3: pin V19
  //   Y4: pin W18
  //   Y5: pin U15
  //   Y6: pin U14
  //   Y7: pin V14
  //   Y8: pin V13
  //   Y9: pin V3
  //   Y10: pin W3
  //   Y11: pin U3
  //   Y12: pin P3
  //   Y13: pin N3
  //   Y14: pin P1
  //   Y15: pin L1
  //   reset: pin U18
  //   U: pin T18
  //   D: pin U17
  //   R: pin T17
  //   L: pin W19
  //   Board: BASYS3
endmodule

/* Test case:
     reset Clock U D L R Y15 Y14 Y13 Y12 Y11 Y10 Y9 Y8 Y7 Y6 Y5 Y4 Y3 Y2 Y1 Y0
     1         0 0 0 0 0  x   x    x  x   x   x   x  x  x  x  x  x  x  x  x  x
     1         1 0 0 0 0  x   x    x  x   x   x   x  x  x  x  x  x  x  x  x  x
     0         0 0 0 0 0  x   x    x  x   x   x   x  x  x  x  x  x  x  x  x  x

repeat(5) 0    C 0 0 0 0  x   x    x  x   x   x   x  x  x  x  x  x  x  x  x  x
          0    C 0 0 0 0  0   0    0  0   0   0   0  0  0  0  0  0  0  0  0  1

loop(i,15)
repeat(3) 0    C 0 0 0 0  x   x    x  x   x   x   x  x  x  x  x  x  x  x  x  x
          0    C 0 0 0 0  bits(16,1<<(i+1))
end loop

repeat(9) 0    C 0 0 0 0  x   x    x  x   x   x   x  x  x  x  x  x  x  x  x  x

loop(i,16)
repeat(3) 0    C 0 0 0 0  x   x    x  x   x   x   x  x  x  x  x  x  x  x  x  x
          0    C 0 0 0 0  bits(16,1<<i)
end loop

repeat(10) 0   C 0 0 0 0  x   x    x  x   x   x   x  x  x  x  x  x  x  x  x  x

loop(i,15)
repeat(3) 0    C 0 0 0 0  x   x    x  x   x   x   x  x  x  x  x  x  x  x  x  x
          0    C 0 0 0 0  bits(16,1<<(15-i))
end loop
*/
