// Digital circuit ClockDiv.dig as structural Verilog
// Clock divider. Here the clock is divided by two, and the 
// memory access signals of the instruction register are generated. 
// A instruction word is alternately read et first and then executed.
// {{de Taktteiler. Hier wird der Takt durch zwei geteilt, und 
// es werden die Signale für den Speicherzugriff des 
// InstructionRegisters erzeugt. Jeweils abwechselnd 
// wird ein Befehlswort gelesen und dieses Befehlswort
// dann ausgeführt.}}
module ClockDiv (
  input  Clock,
  output S_in,
  output C_in,
  output C
);

  wire not_1_out, t_ff_1_nq;

  not not_1 (not_1_out, Clock);
  T_FF #(.withEnable("false")) t_ff_1 (.C(not_1_out), .Q(S_in), .nQ(t_ff_1_nq));
  and and_1 (C_in, Clock, S_in);
  and and_2 (C, t_ff_1_nq, Clock);

  // Notes on the sheet:
  //   S_in: Signal to configure the processor for reading 
  //   the next instruction.
  //   {{de Signal welches den Prozessor für das Lesen 
  //   eines Befehlswortes konfiguriert.}}
  //   C_in: Clock signal to read the next instruction.
  //   {{de Taktsignal für das Lesen eines Befehlswortes}}
  //   C: Clock used to execute an instruction.
  //   {{de Takt der das Ausführen eines Befehlswortes 
  //   steuert.}}
endmodule
