// Digital circuit Control.dig as structural Verilog
// Control unit for a simple processor.
// It works purely combinatorial.
// Since it is relatively complex (24 output bits), it is 
// implemented by a corresponding ROM component, 
// and not by 24 individual combinatorial circuits.
// {{de Leitwerk für einen einfachen Prozessor.
// Es arbeitet rein kombinatorisch, es handelt sich 
// also um ein einfaches Schaltnetz. 
// Da es vergleichsweise komplex ist (24 
// Ausgangsbits), wird es durch einen 
// entsprechenden ROM-Baustein 
// realisiert, und nicht durch 24 einzelne Schaltnetze.}}
module Control (
  input  [7:0] Op,
  output stPC,
  output WE,
  output imm,
  output [1:0] iem,
  output absJmp,
  output [2:0] muxB,
  output src2D,
  output muxA,
  output alu2D,
  output [4:0] aluOp,
  output storeFlags,
  output [2:0] branch,
  output ramSt,
  output ramLd,
  output ioW,
  output ioR,
  output RetI
);

  wire [6:0] multiplexer_1_out;
  wire [24:24] Logic_d;

  Multiplexer #(.Bits(7)) multiplexer_1 (.sel(Op[7]), .in_0(Op[6:0]), .in_1({7{1'b0}}), .out(multiplexer_1_out));
  ROM #(.AddrBits(7), .Bits(26), .Addr_Bits(6)) Logic (
    .A(multiplexer_1_out), .sel(1'b1),
    .D({RetI, Logic_d[24], stPC, ioR, ioW, absJmp, ramSt, ramLd, muxA, branch, iem, alu2D, storeFlags, WE, aluOp, src2D, muxB}));
  Break #(.Cycles(600000)) Break (.brk(Logic_d[24]));

  assign imm = Op[7];

  // Notes on the sheet:
  //   Op: The opcode and the immediate bit.
  //   {{de Der Opcode incl. Immediate Bit}}
  //   stPC: The programm counter is stored in a register.
  //   {{de Programm Counter in Register Speichern}}
  //   WE: The data bus value ist stored in a register.
  //   {{de Wert am Datenbus in Register speichern}}
  //   imm: Enables the storage of a constant value.
  //   {{de Aktiviert das Speichern der Konstanten}}
  //   iem: immediate extend mode
  //   {{de Erweiterungsmodus der Konstanten}}
  //   absJmp: triggers a absolute jump
  //   {{de absoluten Sprung auslösen}}
  //   muxB: selector for mux B
  //   {{de Selektor für Mux B}}
  //   src2D: Put source register to data bus
  //   {{de SourceRegister auf Datenbus legen}}
  //   muxA: selector for mux A
  //   {{de Selector für Mux A}}
  //   alu2D: ALU value is put on the data bus.
  //   {{de ALU auf den Datenbus legen}}
  //   aluOp: the operation of the ALU
  //   {{de Operation der ALU}}
  //   storeFlags: If set, the ALU performs an arithmetic operation so that the 
  //   flags must be stored.
  //   {{de Wenn gesetzt führt die ALU eine arithmetische Operation 
  //   aus, so dass die Flags gespeichert werden müssen.}}
  //   branch: kind of branch
  //   {{de Art des bedingten Sprunges}}
  //   ramSt: The RAM stores the data on the data bus.
  //   {{de Ram speichert Daten vom Datenbus}}
  //   ramLd: The RAM component puts its content to the 
  //   data bus.
  //   {{de Ram gibt Daten auf den Datenbus}}
  //   ioW: write to IO
  //   {{de Es wird auf die IO geschrieben}}
  //   ioR: read from IO
  //   {{de Es wird IO gelesen}}
  //   RetI: Return From Interrupt
  //   {{de Rückkehr aus dem Interrupt}}
  //   contents of Logic (hex, n*v repeats v):
  //   0,208,e10,f10,e20,f20,e30,e40,e50,2a02,a05,2e12,e15,2f12,f15,2e22,e25,2f22,f25,a70,
  //   2e32,e35,2e42,e45,2e52,e55,a60,ed0,2ed2,ed5,420,520,2422,425,2522,525,e80,e90,f80,
  //   f90,ea0,ab0,ac0,8001b,60213,8300a,8000f,42202,40205,8001a,60212,a01,4006,8006,c006,
  //   14006,18006,1c006,902202,100000,102002,10006,20300a,20000f,20001b,422202,420205,420213,
  //   1000000,2100000
endmodule
