// Digital circuit Flags.dig as structural Verilog
// Stores the processor flags.
// Via the store input, the current state of the flags can 
// be stored. The carry flag can then be used for 
// arithmetic function, all flags for a conditional branch.
// {{de Speichert die Prozessor-Flags. 
// Über den store-Eingang, kann der aktuelle Zustand
// der Flags gespeichert werden. Das Carry-Flag kann 
// dann für arithmetische Funktion genutzt werden,
// alle Flags für eine bedingte Verzweigung.}}
module Flags (
  input  Zi,
  input  Ni,
  input  Ci,
  input  C,
  input  store,
  output Zo,
  output No,
  output Co
);

  Register Carry (.D(Ci), .C(C), .en(store), .Q(Co));
  Register Zero (.D(Zi), .C(C), .en(store), .Q(Zo));
  Register Neg (.D(Ni), .C(C), .en(store), .Q(No));

  // Notes on the sheet:
  //   Zi: The zero flag which should be stored.
  //   {{de Das Zero-Flag welches gespeichert werden soll.}}
  //   Zo: Returns the stored zero flag.
  //   {{de Gibt das gespeicherte Zero-Flag aus.}}
  //   Ni: The negative flag which should be stored.
  //   {{de Das Negative-Flag welches gespeichert werden soll.}}
  //   No: Returns the stored negative flag.
  //   {{de Gibt das gespeicherte Negative-Flag aus.}}
  //   Ci: The carry flag which should be stored.
  //   {{de Das Carry-Flag welches gespeichert werden soll.}}
  //   Co: Returns the stored carry flag.
  //   {{de Gibt das gespeicherte Carry-Flag aus.}}
  //   store: The input which activates storing.
  //   It is set to one when performing an arithmetic operation.
  //   {{de Der Eingang welcher das Speichern aktiviert. 
  //   Es wird auf Eins gesetzt, wenn eine arithmetische 
  //   Operation ausgeführt wird.}}
endmodule
