// Digital circuit FlagsRW.dig as structural Verilog
// Stores the processor flags. In contrast to the simple 
// variant, the flags can be read and written via IO operations. 
// The flags can be found at IO address 0.
// {{de Speichert die Prozessorflags. Im Gegensatz zur 
// einfachen Variante können bei diesem Modul
// die Flags per IO Operation gelesen und geschrieben
// werden. Die Flags finden sich an IO Adresse 0.}}
module FlagsRW (
  input  Zi,
  input  Ni,
  input  Ci,
  input  C,
  input  store,
  input  [15:0] A,
  input  IOR,
  input  IOW,
  input  [15:0] Data,
  output nie,
  output Zo,
  output No,
  output Co
);

  wire and_1_out, and_2_out, comparator_1_eq, or_1_out;
  wire [15:0] multiplexer_1_out;
  wire [15:4] register_1_q;

  Comparator #(.Bits(16)) comparator_1 (.a(A), .b({16{1'b0}}), .eq(comparator_1_eq));  // open: gt, lt
  and and_1 (and_1_out, IOW, comparator_1_eq);
  and and_2 (and_2_out, comparator_1_eq, IOR);
  Multiplexer #(.Bits(16)) multiplexer_1 (
    .sel(and_1_out), .in_0({{12{1'b0}}, nie, Ni, Zi, Ci}), .in_1(Data), .out(multiplexer_1_out));
  or or_1 (or_1_out, store, and_1_out);
  Register #(.Bits(16)) register_1 (.D(multiplexer_1_out), .C(C), .en(or_1_out), .Q({register_1_q, nie, No, Zo, Co}));
  assign Data = and_2_out ? {register_1_q, nie, No, Zo, Co} : 16'bz;  // Driver driver_1

  // Notes on the sheet:
  //   Zi: Zero In {{de Zero EIngang}}
  //   Ni: Negative In {{de negative Eingang}}
  //   Zo: Zero Out {{de Zero Ausgang}}
  //   Ci: Carry In {{de Carry EIngang}}
  //   No: Negative Out {{de negative Ausgang}}
  //   store: The input which activates storing.
  //   It is set to one when performing an arithmetic operation.
  //   {{de Der Eingang welcher das Speichern aktiviert. 
  //   Es wird auf Eins gesetzt, wenn eine arithmetische 
  //   Operation ausgeführt wird.}}
  //   A: address {{de Adresse}}
  //   IOR: IO Read {{de Lesen von der IO}}
  //   IOW: IO Write {{de Schreiben auf die IO}}
  //   Co: Carry Out {{de Carry Ausgang}}
endmodule
