// Digital circuit ImReg.dig as structural Verilog
// Register for storing large constants.
// There is a 1-bit command describing this register. 
// In this way, 15 bits can be stored (the 16th bit 
// activates the writing of this register and therefore 
// is always one). To store the missing 16th bit, a special 
// bit is available in each instruction word.
// {{de Register zum Speichern von großen Konstanten.
// Es existiert ein 1-Bit Befehl, welcher dieses Register
// beschreibt. Auf diese Weise können 15 Bits 
// gespeichert werden (das 16. Bit aktiviert das 
// Beschreiben dieses Registers und ist daher immer 
// Eins) Um das fehlende 16. Bit zu speichern, steht ein 
// spezielles Bit in jedem Befehlswort zur Verfügung.}}
module ImReg (
  input  en,
  input  [1:0] iem,
  input  C,
  input  [15:0] inst,
  output [15:0] imm
);

  Register #(.Bits(15)) u_imm (.D(inst[14:0]), .C(C), .en(en), .Q(imm[14:0]));
  Multiplexer #(.Selector_Bits(2)) multiplexer_1 (
    .sel(iem), .in_0(imm[14]), .in_1(1'b0), .in_2(inst[0]), .in_3(inst[4]), .out(imm[15]));

  // Notes on the sheet:
  //   en: enables storage
  //   {{de Speichern aktivieren}}
  //   imm: The constant of register contents and bit 8.
  //   {{de Die Konstante aus Registerinhalt und Bit 8.}}
  //   iem: immediate extend mode (0: sign extend; 1: extend with 0, 2:extend with S0, 3:extend with D0)
  //   {{de Erweiterungsmodus (0: sign extend; 1: extend with 0, 2:extend with S0, 3:extend with D0)}}
  //   inst: the current instruction
  //   {{de Der aktuelle Befehl}}
endmodule
