// Digital circuit PC.dig as structural Verilog
// The program counter.
// Here the current program counter is stored.
// The various inputs can be used to influence how the 
// program counter is modified if a clock signal happens.
// {{de Der Programmzähler. 
// Hier wird der aktuelle Programmzähler gespeichert. 
// Über die verschiedenen Eingänge kann beeinflußt 
// werden, auf welche Weise der Programmzähler mit 
// dem Takt weiter geschaltet wird.}}
module PC (
  input  [15:0] ALU,
  input  C,
  input  abs,
  input  rel,
  output [15:0] Next,
  output [15:0] PC
);

  wire Reset_out;
  wire [15:0] Add_ALU_s, multiplexer_1_out, multiplexer_2_out;

  Reset Reset (.out(Reset_out));
  Register #(.Bits(16), .isProgramCounter("true")) u_PC (.D(multiplexer_2_out), .C(~C), .en(Reset_out), .Q(PC));
  Add #(.Bits(16)) Add_One (.a(PC), .b(16'h1), .c_i(1'b0), .s(Next));  // open: c_o
  Add #(.Bits(16)) Add_ALU (.a(Next), .b(ALU), .c_i(1'b0), .s(Add_ALU_s));  // open: c_o
  Multiplexer #(.Bits(16)) multiplexer_1 (.sel(rel), .in_0(Next), .in_1(Add_ALU_s), .out(multiplexer_1_out));
  Multiplexer #(.Bits(16)) multiplexer_2 (.sel(abs), .in_0(multiplexer_1_out), .in_1(ALU), .out(multiplexer_2_out));

  // Notes on the sheet:
  //   ALU: Current ALU output, this value is used as address in case 
  //   of a in case of a jump or added to the current address.
  //   {{de Aktuelle ALU Ausgabe, dieser Wert wird im Falle 
  //   eines Sprunges als Adresse übernommen oder zur aktuellen Adresse addiert.}}
  //   Next: Address of the next command to be executed. Can be 
  //   used as a return address to implement a call instruction.
  //   {{de Adresse des nächsten auszuführenden Befehls. 
  //   Kann als Rücksprungadresse verwendet werden, um 
  //   einen Call-Befehl zu implementieren.}}
  //   PC: the current program counter
  //   {{de der aktuelle Programmzähler}}
  //   abs: Triggers a absolute jump.
  //   The value of the ALU input is used as the new address.
  //   {{de Absoluten Sprung auslösen. Der Wert des ALU 
  //   Eingangs wird als neue Adresse verwendet.}}
  //   rel: Triggers a relative jump. The value of the ALU 
  //   input is added to the current address.
  //   {{de relativen Spung auslösen. Der Wert des ALU 
  //   Eingangs wird zur aktuellen Adresse addiert.}}
endmodule
