// Digital circuit PC_VHDL.dig as structural Verilog
// Der Programmzähler. 
// Hier wird der aktuelle Programmzähler gespeichert. 
// Über die verschiedenen Eingänge kann beeinflußt 
// werden, auf welche Weise der Programmzähler mit 
// dem Takt weiter geschaltet wird.
module PC_VHDL (
  input  [15:0] ALU,
  input  C,
  input  abs,
  input  reset,
  input  rel,
  output [15:0] Next,
  output [15:0] PC
);

  wire not_1_out;
  wire [15:0] Add_ALU_s, multiplexer_1_out, multiplexer_2_out, multiplexer_3_out;

  Multiplexer #(.Bits(16)) multiplexer_1 (
    .sel(reset), .in_0(multiplexer_3_out), .in_1({16{1'b0}}), .out(multiplexer_1_out));
  not not_1 (not_1_out, C);
  Register #(.Bits(16)) u_PC (.D(multiplexer_1_out), .C(not_1_out), .en(1'b1), .Q(PC));
  Add #(.Bits(16)) Add_One (.a(PC), .b(16'h1), .c_i(1'b0), .s(Next));  // open: c_o
  Add #(.Bits(16)) Add_ALU (.a(Next), .b(ALU), .c_i(1'b0), .s(Add_ALU_s));  // open: c_o
  Multiplexer #(.Bits(16)) multiplexer_2 (.sel(rel), .in_0(Next), .in_1(Add_ALU_s), .out(multiplexer_2_out));
  Multiplexer #(.Bits(16)) multiplexer_3 (.sel(abs), .in_0(multiplexer_2_out), .in_1(ALU), .out(multiplexer_3_out));

  // Notes on the sheet:
  //   ALU: Aktueller ALU-Inhalt
  //   Next: Adresse des nächsten auszuführenden Befehls
  //   PC: Programm Counter
  //   C: Takt
  //   abs: absoluten Sprung auslösen
  //   rel: relativen Spung auslösen
endmodule
