// Digital circuit RS.dig as structural Verilog
// RS Flipflop with set priority
// {{de RS Flipflop bei welchem das Setzen Priorität hat.}}
module RS (
  input  S,
  input  nC,
  input  R,
  output D
);

  wire and_1_out, or_1_out;

  and and_1 (and_1_out, D, ~R);  // And
  or or_1 (or_1_out, and_1_out, S);
  D_FF d_ff (.D(or_1_out), .C(~nC), .Q(D));  // open: nQ

  // Notes on the sheet:
  //   S: Set
  //   {{de Setzen}}
  //   nC: Hz: 2
  //   R: Reset
  //   {{de Zurücksetzen}}
  //   D: Data
  //   {{de Daten}}
endmodule
