// Digital circuit Register.dig as structural Verilog
// This block contains the 16 processor registers.
// {{de In diesem Block befinden sich die 16 
// Prozessorregister.}}
module Register (
  input  [15:0] WD,
  input  C,
  input  [3:0] src,
  input  [3:0] dest,
  input  WE,
  output [15:0] Rdest,
  output [15:0] Rsrc
);

  wire demultiplexer_1_out_0, demultiplexer_1_out_1, demultiplexer_1_out_2, demultiplexer_1_out_3,
       demultiplexer_1_out_4, demultiplexer_1_out_5, demultiplexer_1_out_6, demultiplexer_1_out_7,
       demultiplexer_1_out_8, demultiplexer_1_out_9, demultiplexer_1_out_10, demultiplexer_1_out_11,
       demultiplexer_1_out_12, demultiplexer_1_out_13, demultiplexer_1_out_14, demultiplexer_1_out_15;
  wire [15:0] BP_q, R0_q, R1_q, R2_q, R3_q, R4_q, R5_q, R6_q, R7_q, R8_q, R9_q, R10_q, R11_q, R12_q, RA_q,
       SP_q;

  Demultiplexer #(.Selector_Bits(4)) demultiplexer_1 (
    .sel(dest), .in(WE), .out_0(demultiplexer_1_out_0), .out_1(demultiplexer_1_out_1),
    .out_2(demultiplexer_1_out_2), .out_3(demultiplexer_1_out_3), .out_4(demultiplexer_1_out_4),
    .out_5(demultiplexer_1_out_5), .out_6(demultiplexer_1_out_6), .out_7(demultiplexer_1_out_7),
    .out_8(demultiplexer_1_out_8), .out_9(demultiplexer_1_out_9), .out_10(demultiplexer_1_out_10),
    .out_11(demultiplexer_1_out_11), .out_12(demultiplexer_1_out_12), .out_13(demultiplexer_1_out_13),
    .out_14(demultiplexer_1_out_14), .out_15(demultiplexer_1_out_15));
  Register #(.Bits(16)) R0 (.D(WD), .C(C), .en(demultiplexer_1_out_0), .Q(R0_q));
  Register #(.Bits(16)) R1 (.D(WD), .C(C), .en(demultiplexer_1_out_1), .Q(R1_q));
  Register #(.Bits(16)) R2 (.D(WD), .C(C), .en(demultiplexer_1_out_2), .Q(R2_q));
  Register #(.Bits(16)) R3 (.D(WD), .C(C), .en(demultiplexer_1_out_3), .Q(R3_q));
  Register #(.Bits(16)) R4 (.D(WD), .C(C), .en(demultiplexer_1_out_4), .Q(R4_q));
  Register #(.Bits(16)) R5 (.D(WD), .C(C), .en(demultiplexer_1_out_5), .Q(R5_q));
  Register #(.Bits(16)) R6 (.D(WD), .C(C), .en(demultiplexer_1_out_6), .Q(R6_q));
  Register #(.Bits(16)) R7 (.D(WD), .C(C), .en(demultiplexer_1_out_7), .Q(R7_q));
  Register #(.Bits(16)) R8 (.D(WD), .C(C), .en(demultiplexer_1_out_8), .Q(R8_q));
  Register #(.Bits(16)) R9 (.D(WD), .C(C), .en(demultiplexer_1_out_9), .Q(R9_q));
  Register #(.Bits(16)) R10 (.D(WD), .C(C), .en(demultiplexer_1_out_10), .Q(R10_q));
  Register #(.Bits(16)) R11 (.D(WD), .C(C), .en(demultiplexer_1_out_11), .Q(R11_q));
  Register #(.Bits(16)) R12 (.D(WD), .C(C), .en(demultiplexer_1_out_12), .Q(R12_q));
  Register #(.Bits(16)) BP (.D(WD), .C(C), .en(demultiplexer_1_out_13), .Q(BP_q));
  Register #(.Bits(16)) SP (.D(WD), .C(C), .en(demultiplexer_1_out_14), .Q(SP_q));
  Register #(.Bits(16)) RA (.D(WD), .C(C), .en(demultiplexer_1_out_15), .Q(RA_q));
  Multiplexer #(.Selector_Bits(4), .Bits(16)) multiplexer_1 (
    .sel(dest), .in_0(R0_q), .in_1(R1_q), .in_2(R2_q), .in_3(R3_q), .in_4(R4_q), .in_5(R5_q), .in_6(R6_q),
    .in_7(R7_q), .in_8(R8_q), .in_9(R9_q), .in_10(R10_q), .in_11(R11_q), .in_12(R12_q), .in_13(BP_q),
    .in_14(SP_q), .in_15(RA_q), .out(Rdest));
  Multiplexer #(.Selector_Bits(4), .Bits(16)) multiplexer_2 (
    .sel(src), .in_0(R0_q), .in_1(R1_q), .in_2(R2_q), .in_3(R3_q), .in_4(R4_q), .in_5(R5_q), .in_6(R6_q),
    .in_7(R7_q), .in_8(R8_q), .in_9(R9_q), .in_10(R10_q), .in_11(R11_q), .in_12(R12_q), .in_13(BP_q),
    .in_14(SP_q), .in_15(RA_q), .out(Rsrc));

  // Notes on the sheet:
  //   WD: Data to be stored.
  //   The value applied here is stored when the input WE is set to 1.
  //   {{de Daten die gespeichert werden sollen.
  //   Der hier anliegende Wert wird gespeichert, wenn 
  //   der Eingang WE auf 1 geschaltet wird.}}
  //   src: Number of the source register. 
  //   Defines which register is to be output to Rsrc.
  //   {{de Nummer des Source Registers. Legt fest, welches 
  //   Register an Rsrc ausgegeben werden soll.}}
  //   dest: Number of the destignation register. 
  //   Defines which register is to be output to Rdest. In 
  //   addition, this register will be overwritten if WE is set to 1.
  //   {{de Nummer des Destignation Registers. Legt fest, 
  //   welches Register an Rdest ausgegeben werden soll.
  //   Zudem wird dieses Register beschrieben, wenn
  //   WE auf 1 gesetzt wird.}}
  //   Rdest: Contents of the Destignation Register.
  //   Which register is output is determined by 
  //   the input dest.
  //   {{de  Inhalt des Destignation Registers.
  //   Welches Register ausgegeben wird, wird mittels 
  //   des Eingangs dest festgelegt.}}
  //   Rsrc: Contents of the Source Register.
  //   Which register is output is determined by the input src.
  //   {{de Inhalt des Source Registers. Welches Register
  //   ausgegeben wird, wird mittels des Einganges src
  //   festgelegt.}}
  //   WE: Activate storing. When this input is high, the value at WD is 
  //   stored in the register specified in dest at the next clock signal.
  //   {{de Das Speichern aktivieren. Wenn dieser Eingang auf 
  //   High geht, wird der Wert an WD in dem Register 
  //   gespeichert, welches in dest angegeben ist.}}
endmodule
