// Digital circuit RegisterOpt.dig as structural Verilog
// This block contains the 16 processor registers.
// {{de In diesem Block befinden sich die 16 
// Prozessorregister.}}
module RegisterOpt (
  input  [15:0] WD,
  input  C,
  input  [3:0] src,
  input  [3:0] dest,
  input  WE,
  output [15:0] Rdest,
  output [15:0] Rsrc
);

  RegisterFile #(.AddrBits(4), .Bits(16)) registerfile_1 (
    .Din(WD), .we(WE), .Rw(dest), .C(C), .Ra(dest), .Rb(src), .Da(Rdest), .Db(Rsrc));

  // Notes on the sheet:
  //   WD: Data to be stored.
  //   The value applied here is stored when the input WE is set to 1.
  //   {{de Daten die gespeichert werden sollen.
  //   Der hier anliegende Wert wird gespeichert, wenn 
  //   der Eingang WE auf 1 geschaltet wird.}}
  //   src: Number of the source register. 
  //   Defines which register is to be output to Rsrc.
  //   {{de Nummer des Source Registers. Legt fest, welches 
  //   Register an Rsrc ausgegeben werden soll.}}
  //   dest: Number of the destignation register. 
  //   Defines which register is to be output to Rdest. In 
  //   addition, this register will be overwritten if WE is set to 1.
  //   {{de Nummer des Destignation Registers. Legt fest, 
  //   welches Register an Rdest ausgegeben werden soll.
  //   Zudem wird dieses Register beschrieben, wenn
  //   WE auf 1 gesetzt wird.}}
  //   Rdest: Contents of the Destignation Register.
  //   Which register is output is determined by 
  //   the input dest.
  //   {{de  Inhalt des Destignation Registers.
  //   Welches Register ausgegeben wird, wird mittels 
  //   des Eingangs dest festgelegt.}}
  //   Rsrc: Contents of the Source Register.
  //   Which register is output is determined by the input src.
  //   {{de Inhalt des Source Registers. Welches Register
  //   ausgegeben wird, wird mittels des Einganges src
  //   festgelegt.}}
  //   WE: Activate storing. When this input is high, the value at WD is 
  //   stored in the register specified in dest at the next clock signal.
  //   {{de Das Speichern aktivieren. Wenn dieser Eingang auf 
  //   High geht, wird der Wert an WD in dem Register 
  //   gespeichert, welches in dest angegeben ist.}}
endmodule
