// Digital circuit WDmuxCtrl.dig as structural Verilog
module WDmuxCtrl (
  input  ld,
  input  stPC,
  input  ioR,
  output [1:0] WDm
);

  or or_1 (WDm[0], ld, stPC);
  or or_2 (WDm[1], stPC, ioR);
endmodule
