// Digital circuit Intr.dig as structural Verilog
module Intr (
  input  ioR,
  input  [15:0] A,
  input  C,
  input  [15:0] PC,
  input  intrTrig,
  input  imm,
  output [15:0] D,
  output intr
);

  wire and_2_out, comparator_1_eq, not_1_out;
  wire [15:0] IntrAddr_q;

  not not_1 (not_1_out, imm);
  and and_1 (intr, not_1_out, C, intrTrig);
  Comparator #(.Bits(16)) comparator_1 (.a(A), .b(16'h1), .eq(comparator_1_eq));  // open: gt, lt
  and and_2 (and_2_out, ioR, comparator_1_eq);
  Register #(.Bits(16)) IntrAddr (.D(PC), .C(intr), .en(1'b1), .Q(IntrAddr_q));
  assign D = and_2_out ? IntrAddr_q : 16'bz;  // Driver driver_1
endmodule
