// Digital circuit Keyboard.dig as structural Verilog
// Terminal
module Keyboard (
  input  [15:0] A,
  input  R,
  output [15:0] D
);

  wire and_1_out, comparator_1_eq;

  Comparator #(.Bits(16)) comparator_1 (.a(A), .b(16'h1e), .eq(comparator_1_eq));  // open: gt, lt
  and and_1 (and_1_out, comparator_1_eq, R);
  Keyboard keyboard_1 (.C(and_1_out), .D(D));  // open: en, av

  // Notes on the sheet:
  //   A: Addressbus
  //   R: Read Enable
  //   D: Keycode
endmodule
