// Digital circuit schieben.dig as structural Verilog
module schieben (
  input  in_5,
  input  in_6,
  output out_1,
  output out_2,
  output out_3,
  output out_4
);

  D_FF d_ff_1 (.D(in_5), .C(in_6), .Q(out_1));  // open: nQ
  D_FF d_ff_2 (.D(out_1), .C(in_6), .Q(out_2));  // open: nQ
  D_FF d_ff_3 (.D(out_2), .C(in_6), .Q(out_3));  // open: nQ
  D_FF d_ff_4 (.D(out_3), .C(in_6), .Q(out_4));  // open: nQ
endmodule
