// Digital circuit Counter-D.dig as structural Verilog
module Counter_D (
  input  C
);

  wire and_1_out, and_2_out, and_3_out, and_4_out, and_5_out, and_6_out, and_7_out, and_8_out, and_9_out,
       not_1_out, not_2_out, not_3_out, not_4_out, or_1_out, or_2_out, or_3_out, q_0n, q_1n, q_2n, q_3n;

  not not_1 (not_1_out, q_0n);
  not not_2 (not_2_out, q_1n);
  not not_3 (not_3_out, q_2n);
  not not_4 (not_4_out, q_3n);
  and and_1 (and_1_out, q_0n, q_1n, q_2n, not_4_out);
  and and_2 (and_2_out, not_1_out, q_3n);
  and and_3 (and_3_out, not_2_out, q_3n);
  and and_4 (and_4_out, not_3_out, q_3n);
  and and_5 (and_5_out, q_0n, q_1n, not_3_out);
  and and_6 (and_6_out, not_1_out, q_2n);
  and and_7 (and_7_out, not_2_out, q_2n);
  and and_8 (and_8_out, q_0n, not_2_out);
  and and_9 (and_9_out, not_1_out, q_1n);
  or or_1 (or_1_out, and_1_out, and_2_out, and_3_out, and_4_out);
  or or_2 (or_2_out, and_5_out, and_6_out, and_7_out);
  or or_3 (or_3_out, and_8_out, and_9_out);
  D_FF #(.Default(1)) u_q_3n (.D(or_1_out), .C(C), .Q(q_3n));  // open: nQ
  D_FF #(.Default(1)) u_q_2n (.D(or_2_out), .C(C), .Q(q_2n));  // open: nQ
  D_FF #(.Default(1)) u_q_1n (.D(or_3_out), .C(C), .Q(q_1n));  // open: nQ
  D_FF u_q_0n (.D(not_1_out), .C(C), .Q(q_0n));  // open: nQ
endmodule
