// Digital circuit Counter-JK.dig as structural Verilog
module Counter_JK (
  input  C,
  output Q_0,
  output Q_1,
  output Q_2,
  output Q_3
);

  wire and_1_out, and_2_out;

  JK_FF q_0_n (.J(1'b1), .C(C), .K(1'b1), .Q(Q_0));  // open: nQ
  JK_FF #(.Default(1)) q_1_n (.J(Q_0), .C(C), .K(Q_0), .Q(Q_1));  // open: nQ
  and and_1 (and_1_out, Q_0, Q_1);
  JK_FF #(.Default(1)) q_2_n (.J(and_1_out), .C(C), .K(and_1_out), .Q(Q_2));  // open: nQ
  and and_2 (and_2_out, and_1_out, Q_2);
  JK_FF #(.Default(1)) q_3_n (.J(and_2_out), .C(C), .K(and_2_out), .Q(Q_3));  // open: nQ

  // Notes on the sheet:
  //   Synchronous counter built with JK flip-flops
  //   {{de Synchroner Zähler aufgebaut mit JK-Flipflops}}
endmodule

/* Test case:
           C Q_3 Q_2 Q_1 Q_0
repeat(16) C bits(4,n-1)
*/
