// Digital circuit Counter-T.dig as structural Verilog
module Counter_T (
  input  C,
  output out_1,
  output out_3,
  output out_4,
  output out_5
);

  T_FF #(.withEnable("false")) Q_0 (.C(C), .Q(out_1));  // open: nQ
  T_FF #(.withEnable("false")) Q_1 (.C(~out_1), .Q(out_3));  // open: nQ
  T_FF #(.withEnable("false")) Q_2 (.C(~out_3), .Q(out_4));  // open: nQ
  T_FF #(.withEnable("false")) Q_3 (.C(~out_4), .Q(out_5));  // open: nQ

  // Notes on the sheet:
  //   C: Hz: 2
  //   Asynchronous counter built with T flip-flops
  //   {{de Asynchroner Zähler aufgebaut mit T-Flipflops}}
endmodule
