// Digital circuit Counter_JK.dig as structural Verilog
module Counter_JK (
  input  C,
  output out_1,
  output out_3,
  output out_4,
  output out_5
);

  wire and_1_out, and_2_out;

  JK_FF q_0n (.J(1'b1), .C(C), .K(1'b1), .Q(out_1));  // open: nQ
  JK_FF #(.Default(1)) q_1n (.J(out_1), .C(C), .K(out_1), .Q(out_3));  // open: nQ
  and and_1 (and_1_out, out_1, out_3);
  JK_FF #(.Default(1)) q_2n (.J(and_1_out), .C(C), .K(and_1_out), .Q(out_4));  // open: nQ
  and and_2 (and_2_out, and_1_out, out_4);
  JK_FF #(.Default(1)) q_3n (.J(and_2_out), .C(C), .K(and_2_out), .Q(out_5));  // open: nQ
endmodule
