// Digital circuit D-TransmissionGate.dig as structural Verilog
module D_TransmissionGate (
  input  D,
  input  C,
  output Q,
  output nQ
);

  wire not_2_out;

  assign Q = C ? D : 1'bz;  // Driver driver_1
  assign Q = ~C ? not_2_out : 1'bz;  // DriverInvSel driverinvsel_1
  not not_1 (nQ, Q);
  not not_2 (not_2_out, nQ);
endmodule

/* Test case:
C D Q ~Q
C 1 1  0
0 1 1  0
0 0 1  0
C 0 0  1
0 0 0  1
0 1 0  1
*/
