// Digital circuit Prescaler.dig as structural Verilog
// Simple frequency divider. The divider ratios 
// are 1/2, 1/4, 1/8 and 1/16.
// {{de Einfacher Frequenzteiler. Möglich sind die 
// Teilerverhältnisse 1/2, 1/4, 1/8 und 1/16.}}
module Prescaler (
  input  Clock,
  input  A,
  input  B,
  output Y
);

  wire and_1_out, and_2_out, and_3_out, and_4_out, not_1_out, not_2_out, t_ff_1_q, t_ff_2_q, t_ff_3_q,
       t_ff_4_q;

  not not_1 (not_1_out, A);
  not not_2 (not_2_out, B);
  T_FF #(.withEnable("false")) t_ff_1 (.C(Clock), .Q(t_ff_1_q));  // open: nQ
  T_FF #(.withEnable("false")) t_ff_2 (.C(t_ff_1_q), .Q(t_ff_2_q));  // open: nQ
  and and_1 (and_1_out, t_ff_1_q, not_1_out, not_2_out);
  T_FF #(.withEnable("false")) t_ff_3 (.C(t_ff_2_q), .Q(t_ff_3_q));  // open: nQ
  and and_2 (and_2_out, t_ff_2_q, A, not_2_out);
  T_FF #(.withEnable("false")) t_ff_4 (.C(t_ff_3_q), .Q(t_ff_4_q));  // open: nQ
  and and_3 (and_3_out, t_ff_3_q, not_1_out, B);
  and and_4 (and_4_out, t_ff_4_q, A, B);
  or or_1 (Y, and_4_out, and_3_out, and_2_out, and_1_out);

  // Notes on the sheet:
  //   Clock: Hz: 20
  //   A: First bit of frequency selection
  //   {{de Erstes Bit der Frequenzwahl}}
  //   B: Second bit of frequency selection
  //   {{de zweites Bit der Frequenzwahl}}
  //   Y: Prescaler output
  //   {{de Prescaler Ausgabe}}
endmodule

/* Test case:
           Clock A B Y
repeat(16) C     0 0 (~n&1)
repeat(16) C     1 0 (~(n>>1)&1)
repeat(16) C     0 1 (~(n>>2)&1)
repeat(16) C     1 1 (~(n>>3)&1)
*/
