// Digital circuit RS-C.dig as structural Verilog
// Einfaches NOR RS-Flipflop mit Freigabeeingang.
module RS_C (
  input  S,
  input  C,
  input  R,
  output Q,
  output nQ
);

  wire and_1_out, and_2_out;

  and and_1 (and_1_out, R, C);
  and and_2 (and_2_out, C, S);
  nor nor_1 (Q, and_1_out, nQ);
  nor nor_2 (nQ, Q, and_2_out);

  // Notes on the sheet:
  //   S: Set Eingang
  //   C: Freigabeeingang
  //   Q: Das gespeicherte Bit
  //   nQ: Das inverse des gespeicherten Bits
  //   R: Reset Eingang
endmodule

/* Test case:
R C S Q ~Q
1 C 0 0  1
X 0 X 0  1
0 C 1 1  0
X 0 X 1  0
*/
