// Digital circuit RS-MS-Simp.dig as structural Verilog
// Master Slave RS-Flipflop. 
// Aufgebaut aus zwei einfachen RS-Flipflops und einem 
// Inverter.
module RS_MS_Simp (
  input  R,
  input  C,
  input  S,
  output Q,
  output nQ
);

  wire not_1_out, rs_c_1_p4, rs_c_1_p5;

  // RS_C rs_c_1: pin names not known; wires that end beside it: S, C, R, rs_c_1_p4, rs_c_1_p5
  not not_1 (not_1_out, C);
  // RS_C rs_c_2: pin names not known; wires that end beside it: rs_c_1_p4, not_1_out, rs_c_1_p5, Q, nQ

  // Notes on the sheet:
  //   R: Reset Eingang
  //   C: Clock
  //   Q: Das gespeicherte Bit.
  //   nQ: Das Inverse des gespeicherten Bits.
  //   S: Set Eingang
endmodule

/* Test case:
R C S Q ~Q
1 C 0 0  1
X 0 X 0  1
0 C 1 1  0
X 0 X 1  0
*/
