// Digital circuit RS-T.dig as structural Verilog
module RS_T (
  input  S,
  input  C,
  input  R,
  output Q,
  output nQ
);

  wire and_1_out, and_2_out, and_3_out, not_1_out, not_2_out, not_3_out;

  not not_1 (not_1_out, C);
  not not_2 (not_2_out, not_1_out);
  not not_3 (not_3_out, not_2_out);
  and and_1 (and_1_out, not_3_out, C);
  and and_2 (and_2_out, R, and_1_out);
  and and_3 (and_3_out, and_1_out, S);
  nor nor_1 (Q, and_2_out, nQ);
  nor nor_2 (nQ, Q, and_3_out);
endmodule

/* Test case:
R C S Q ~Q
1 C 0 0  1
X 0 X 0  1
0 C 1 1  0
X 0 X 1  0
*/
