// Digital circuit oscillator.dig as structural Verilog
module oscillator (
  output Q,
  output nQ
);

  wire and_1_out, and_2_out, and_3_out, C, delay_1_out, delay_2_out, not_1_out, reset_1_out;

  Reset reset_1 (.out(reset_1_out));
  xor xor_1 (C, reset_1_out, delay_1_out);
  Delay #(.delayTime(2)) delay_1 (.in(C), .out(delay_1_out));
  not not_1 (not_1_out, C);
  // Probe C on C
  Delay delay_2 (.in(not_1_out), .out(delay_2_out));
  and and_1 (and_1_out, delay_2_out, C);
  and and_2 (and_2_out, Q, and_1_out);
  and and_3 (and_3_out, and_1_out, nQ);
  nor nor_1 (Q, and_2_out, nQ);
  nor nor_2 (nQ, Q, and_3_out);
endmodule
