// Digital circuit cell.dig as structural Verilog
module \cell  (
  input  init,
  input  sel,
  input  C,
  input  n1,
  input  n2,
  input  n3,
  input  n4,
  input  n5,
  input  n6,
  input  n7,
  input  n8,
  output Q
);

  wire descrete_1_p12;

  // descrete descrete_1: pin names not known; wires that end beside it: Q, n1, n2, n3, n4, n5, n6, n7, n8, sel, init, descrete_1_p12
  D_FF d_ff_1 (.D(descrete_1_p12), .C(C), .Q(Q));  // open: nQ

  // Notes on the sheet:
  //   init: The initial value of the cell. Is used if sel is high.
  //   {{de Der Anfangszustand der Zelle.
  //   Wird nur verwendet, wenn sel auf high gesetzt ist.}}
  //   sel: If high, the value given in input init is used as the
  //   next state. Is used to initialize the cell.
  //   {{de Wenn dieser Eingang auf high gesetzt wird,
  //   wird der init-Eingang verwendet um die Zelle zu
  //   initialisieren.}}
endmodule
