// Digital circuit cellExplicit.dig as structural Verilog
module cellExplicit (
  input  ro,
  input  o,
  input  lo,
  input  r,
  input  l,
  input  lu,
  input  u,
  input  ru,
  input  C,
  output Out
);

  wire comparator_1_eq, comparator_2_eq, multiplexer_1_out, or_1_out;
  wire [3:0] bitcount_1_out;

  BitCount #(.Bits(8)) bitcount_1 (.in({ru, u, lu, r, l, lo, o, ro}), .out(bitcount_1_out));
  Comparator #(.Bits(4)) comparator_1 (.a(bitcount_1_out), .b(4'b0011), .eq(comparator_1_eq));  // open: gt, lt
  Comparator #(.Bits(4)) comparator_2 (.a(bitcount_1_out), .b(4'b0010), .eq(comparator_2_eq));  // open: gt, lt
  or or_1 (or_1_out, comparator_1_eq, comparator_2_eq);
  Multiplexer multiplexer_1 (.sel(Out), .in_0(comparator_1_eq), .in_1(or_1_out), .out(multiplexer_1_out));
  D_FF d_ff_1 (.D(multiplexer_1_out), .C(C), .Q(Out));  // open: nQ
endmodule

/* Test case:
C ro o lo l r lu u ru Out
C 1  1 1  0 0 0  0 0  x
C 1  1 1  0 0 0  0 0  1
# if out and two other fields set: survive
0 1  1 0  0 0 0  0 0  1
C 1  1 0  0 0 0  0 0  1
# if out and two other fields set: die
0 1  0 0  0 0 0  0 0  1
C 1  0 0  0 0 0  0 0  0
# set again
0 1  1 1  0 0 0  0 0  0
C 1  1 1  0 0 0  0 0  1
# if out and four other fields set: die
0 1  1 1  1 0 0  0 0  1
C 1  1 1  1 0 0  0 0  0
# if out is clear and two other fields set: stay dead
0 1  1 0  0 0 0  0 0  0
C 1  1 0  0 0 0  0 0  0
# if out is clear and four other fields set: stay dead
0 1  1 1  1 0 0  0 0  0
C 1  1 1  1 0 0  0 0  0
# if out is clear and three other fields set: become alive
0 1  1 1  0 0 0  0 0  0
C 1  1 1  0 0 0  0 0  1
*/
