// Digital circuit cellExplicitSet.dig as structural Verilog
module cellExplicitSet (
  input  ro,
  input  o,
  input  lo,
  input  r,
  input  l,
  input  lu,
  input  u,
  input  ru,
  input  C,
  output Out
);

  wire comparator_1_eq, comparator_2_eq, multiplexer_1_out, or_1_out;
  wire [3:0] bitcount_1_out;

  BitCount #(.Bits(8)) bitcount_1 (.in({ru, u, lu, r, l, lo, o, ro}), .out(bitcount_1_out));
  Comparator #(.Bits(4)) comparator_1 (.a(bitcount_1_out), .b(4'b0011), .eq(comparator_1_eq));  // open: gt, lt
  Comparator #(.Bits(4)) comparator_2 (.a(bitcount_1_out), .b(4'b0010), .eq(comparator_2_eq));  // open: gt, lt
  or or_1 (or_1_out, comparator_1_eq, comparator_2_eq);
  Multiplexer multiplexer_1 (.sel(Out), .in_0(comparator_1_eq), .in_1(or_1_out), .out(multiplexer_1_out));
  D_FF #(.Default(1)) d_ff_1 (.D(multiplexer_1_out), .C(C), .Q(Out));  // open: nQ
endmodule
