// Digital circuit cellSettable.dig as structural Verilog
module cellSettable (
  input  val,
  input  [7:0] ne,
  input  sel,
  input  C,
  output Out
);

  wire comparator_1_eq, comparator_2_eq, multiplexer_1_out, multiplexer_2_out, or_1_out;
  wire [3:0] bitcount_1_out;

  BitCount #(.Bits(8)) bitcount_1 (.in(ne), .out(bitcount_1_out));
  Comparator #(.Bits(4)) comparator_1 (.a(bitcount_1_out), .b(4'b0011), .eq(comparator_1_eq));  // open: gt, lt
  Comparator #(.Bits(4)) comparator_2 (.a(bitcount_1_out), .b(4'b0010), .eq(comparator_2_eq));  // open: gt, lt
  or or_1 (or_1_out, comparator_1_eq, comparator_2_eq);
  Multiplexer multiplexer_1 (.sel(Out), .in_0(comparator_1_eq), .in_1(or_1_out), .out(multiplexer_1_out));
  Multiplexer multiplexer_2 (.sel(sel), .in_0(multiplexer_1_out), .in_1(val), .out(multiplexer_2_out));
  D_FF d_ff_1 (.D(multiplexer_2_out), .C(C), .Q(Out));  // open: nQ
endmodule

/* Test case:
ne C val sel Out
0  C 0   0   0
1  C 0   0   0
3  C 0   0   0
7  C 0   0   1
3  C 0   0   1
1  C 0   0   0
7  C 0   0   1
0xf  C 0   0   0
0  C 1   1   1
7  C 0   1   0
*/
