// Digital circuit descrete.dig as structural Verilog
// Implementaion of a single cell of "Conways game of 
// life". This circuit is analyzed to create the truth table
// with 11 inputs and one output. Then the truth table 
// is exported to a hex file, and this hex file is imported
// into a LUT to speedup the cellular automaton.
module descrete (
  input  n1,
  input  n2,
  input  n3,
  input  n4,
  input  n5,
  input  n6,
  input  n7,
  input  n8,
  input  now,
  input  sel,
  input  init,
  output next
);

  wire and_1_out, and_2_out, comparator_1_eq, comparator_2_eq, not_1_out, or_1_out, or_2_out;
  wire [3:0] bitcount_1_out;

  BitCount #(.Bits(8)) bitcount_1 (.in({n8, n7, n6, n5, n4, n3, n2, n1}), .out(bitcount_1_out));
  Comparator #(.Bits(4)) comparator_1 (.a(4'b0011), .b(bitcount_1_out), .eq(comparator_1_eq));  // open: gt, lt
  Comparator #(.Bits(4)) comparator_2 (.a(4'b0010), .b(bitcount_1_out), .eq(comparator_2_eq));  // open: gt, lt
  or or_1 (or_1_out, comparator_1_eq, comparator_2_eq);
  not not_1 (not_1_out, now);
  and and_1 (and_1_out, not_1_out, comparator_1_eq);
  and and_2 (and_2_out, now, or_1_out);
  or or_2 (or_2_out, and_1_out, and_2_out);
  Multiplexer multiplexer_1 (.sel(sel), .in_0(or_2_out), .in_1(init), .out(next));

  // Notes on the sheet:
  //   n1: neighbour
  //   now: state of the cell, alive (HIGH) or dead (LOW)
  //   next: State of cell in the next generation.
  //   sel: If high, the value given in input init is used as the
  //   next state. Is used to initialize the cell.
  //   init: The initial value of the cell. Is used if sel is high.
  //   neighbours
  //   birth
  //   survive
endmodule
