// Digital circuit multip_D_notWorking.dig as structural Verilog
module multip_D_notWorking (
  input  D,
  input  C,
  output Q
);

  wire and_1_out, and_2_out, and_3_out, and_4_out, and_5_out, and_6_out, nor_1_out, nor_2_out, nor_3_out,
       nor_4_out, nor_6_out, not_1_out, not_2_out, not_3_out;

  and and_1 (and_1_out, not_1_out, C);
  not not_1 (not_1_out, D);
  and and_2 (and_2_out, C, D);
  nor nor_1 (nor_1_out, and_1_out, nor_2_out);
  nor nor_2 (nor_2_out, nor_1_out, and_2_out);
  not not_2 (not_2_out, nor_1_out);
  and and_3 (and_3_out, not_2_out, C);
  and and_4 (and_4_out, C, nor_1_out);
  nor nor_3 (nor_3_out, and_3_out, nor_4_out);
  nor nor_4 (nor_4_out, nor_3_out, and_4_out);
  not not_3 (not_3_out, nor_3_out);
  and and_5 (and_5_out, not_3_out, C);
  and and_6 (and_6_out, C, nor_3_out);
  nor nor_5 (Q, and_5_out, nor_6_out);
  nor nor_6 (nor_6_out, Q, and_6_out);
endmodule
