// Digital circuit multip_D_working.dig as structural Verilog
module multip_D_working (
  input  D,
  input  C,
  output D_2,
  output D_0,
  output D_1,
  output D_3
);

  D_MS d_ms_1 (.D(D), .C(C), .Q(D_0));  // open: nQ
  D_MS d_ms_2 (.D(D_0), .C(C), .Q(D_1));  // open: nQ
  D_MS d_ms_3 (.D(D_1), .C(C), .Q(D_2));  // open: nQ
  D_MS d_ms_4 (.D(D_2), .C(C), .Q(D_3));  // open: nQ
endmodule

/* Test case:
C D D_0 D_1 D_2 D_3
# clear all bits
C 0  0   x   x   x
C 0  0   0   x   x
C 0  0   0   0   x
C 0  0   0   0   0

# fill with one
C 1  1   0   0   0
C 1  1   1   0   0
C 1  1   1   1   0
C 1  1   1   1   1

# fill with zero
C 0  0   1   1   1
C 0  0   0   1   1
C 0  0   0   0   1
C 0  0   0   0   0
*/
