// Digital circuit multip_D_working_T.dig as structural Verilog
module multip_D_working_T (
  input  in_1,
  input  in_3,
  output out_2
);

  wire d_t_1_q, d_t_2_q;

  D_T d_t_1 (.D(in_1), .C(in_3), .Q(d_t_1_q));  // open: nQ
  D_T d_t_2 (.D(d_t_1_q), .C(in_3), .Q(d_t_2_q));  // open: nQ
  D_T d_t_3 (.D(d_t_2_q), .C(in_3), .Q(out_2));  // open: nQ
endmodule
