// Digital circuit ArduinoUno.dig as structural Verilog
module ArduinoUno (
  input  R,
  input  C,
  input  D0_I,
  input  D1_I,
  input  D2_I,
  input  D3_I,
  input  D4_I,
  input  D5_I,
  input  D6_I,
  input  D7_I,
  input  D8_I,
  input  D9_I,
  input  D10_I,
  input  D11_I,
  input  D12_I,
  input  D13_I,
  input  D14_I,
  input  D15_I,
  input  D16_I,
  input  D17_I,
  input  D18_I,
  input  D19_I,
  output [7:0] TxD,
  output TxC,
  output D0_O,
  output D1_O,
  output D2_O,
  output D3_O,
  output D4_O,
  output D5_O,
  output D6_O,
  output D7_O,
  output D8_O,
  output D9_O,
  output D10_O,
  output D11_O,
  output D12_O,
  output D13_O,
  output D14_O,
  output D15_O,
  output D16_O,
  output D17_O,
  output D18_O,
  output D19_O
);

  // Simavr #(.generic("this.simavrFirmwareFilePath = args.firmwareFilePath;")) simavr_1: pin names not known; wires that end beside it: R, C, TxC, TxD, {2'b00, D13_I, D12_I, D11_I, D10_I, D9_I, D8_I}, {1'b1, D19_I, D18_I, D17_I, D16_I, D15_I, D14_I}, {D7_I, D6_I, D5_I, D4_I, D3_I, D2_I, D1_I, D0_I}
  PullDown pulldown_1 (.out(TxC));
  PullDown #(.Bits(8)) pulldown_2 (.out(TxD));

  assign D0_O = D0_I;
  assign D1_O = D1_I;
  assign D2_O = D2_I;
  assign D3_O = D3_I;
  assign D4_O = D4_I;
  assign D5_O = D5_I;
  assign D6_O = D6_I;
  assign D7_O = D7_I;
  assign D8_O = D8_I;
  assign D9_O = D9_I;
  assign D10_O = D10_I;
  assign D11_O = D11_I;
  assign D12_O = D12_I;
  assign D13_O = D13_I;
  assign D14_O = D14_I;
  assign D15_O = D15_I;
  assign D16_O = D16_I;
  assign D17_O = D17_I;
  assign D18_O = D18_I;
  assign D19_O = D19_I;

  // Notes on the sheet:
  //   R: Reset
  //   {{de TODO}}
  //   TxD: TX Data (8-bit)
  //   {{de TODO}}
  //   TxC: TX Clock
  //   {{de TODO}}
  //   D0_I: D0 (not connected to internal UART RX)
  //   {{de TODO}}
  //   D1_I: D1 (not connected to internal UART TX)
  //   {{de TODO}}
  //   D2_I: D2
  //   {{de TODO}}
  //   D3_I: D3
  //   {{de TODO}}
  //   D4_I: D4
  //   {{de TODO}}
  //   D5_I: D5
  //   {{de TODO}}
  //   D6_I: D6
  //   {{de TODO}}
  //   D7_I: D7
  //   {{de TODO}}
  //   D0_O: D0 (not connected to internal UART RX)
  //   {{de TODO}}
  //   D1_O: D1 (not connected to internal UART TX)
  //   {{de TODO}}
  //   D2_O: D2
  //   {{de TODO}}
  //   D3_O: D3
  //   {{de TODO}}
  //   D4_O: D4
  //   {{de TODO}}
  //   D5_O: D5
  //   {{de TODO}}
  //   D6_O: D6
  //   {{de TODO}}
  //   D7_O: D7
  //   {{de TODO}}
  //   D8_I: D8 (ICP1)
  //   {{de TODO}}
  //   D9_I: D9
  //   {{de TODO}}
  //   D10_I: D10 (SPI SS)
  //   {{de TODO}}
  //   D11_I: D11 (SPI MOSI)
  //   {{de TODO}}
  //   D12_I: D12 (SPI MISO)
  //   {{de TODO}}
  //   D13_I: D13 (SPI SCK, on-board LED)
  //   {{de TODO}}
  //   D8_O: D8 (ICP1)
  //   {{de TODO}}
  //   D9_O: D9
  //   {{de TODO}}
  //   D10_O: D10 (SPI SS)
  //   {{de TODO}}
  //   D11_O: D11 (SPI MOSI)
  //   {{de TODO}}
  //   D12_O: D12 (SPI MISO)
  //   {{de TODO}}
  //   D13_O: D13 (SPI SCK, on-board LED)
  //   {{de TODO}}
  //   D14_I: D14/A0
  //   {{de TODO}}
  //   D15_I: D15/A1
  //   {{de TODO}}
  //   D16_I: D16/A2
  //   {{de TODO}}
  //   D17_I: D17/A3
  //   {{de TODO}}
  //   D18_I: D18/A4 (I²C SDA)
  //   {{de TODO}}
  //   D19_I: D19/A5 (I²C SCL)
  //   {{de TODO}}
  //   D14_O: D14/A0
  //   {{de TODO}}
  //   D15_O: D15/A1
  //   {{de TODO}}
  //   D16_O: D16/A2
  //   {{de TODO}}
  //   D17_O: D17/A3
  //   {{de TODO}}
  //   D18_O: D18/A4 (I²C SDA)
  //   {{de TODO}}
  //   D19_O: D19/A5 (I²C SCL)
  //   {{de TODO}}
endmodule

/* Code that sets the parameters or builds the circuit:
firmwareFilePath := "src/test/resources/simavr/test-firmware/firmware.elf";
*/
