// Digital circuit ArduinoUnoExample.dig as structural Verilog
module ArduinoUnoExample (
  input  clk,
  input  in_2,
  input  in_3,
  input  in_4,
  input  in_5,
  input  in_6,
  input  in_7,
  input  in_8,
  input  in_9,
  input  in_10,
  input  in_11,
  input  in_12,
  input  in_13,
  input  in_14,
  input  in_15,
  input  in_16,
  input  in_17,
  input  in_18,
  input  in_19,
  input  in_20,
  input  in_21,
  output out_22,
  output out_23,
  output out_24,
  output out_25,
  output out_26,
  output out_27,
  output out_28,
  output out_29,
  output out_30,
  output out_31,
  output out_32,
  output out_33,
  output out_34,
  output out_35,
  output out_36,
  output out_37,
  output out_38,
  output out_39,
  output out_40,
  output out_41,
  output [7:0] out_42
);

  wire arduinouno_1_txc, comparator_1_eq, reset_1_out, reset_2_out, switchdt_1_p3;

  Reset #(.invertOutput("false")) reset_1 (.out(reset_1_out));
  ArduinoUno #(.generic("firmwareFilePath := \"src/test/resources/simavr/test-firmware/firmware.elf\";")) arduinouno_1 (
    .R(reset_1_out), .C(clk), .D0_I(in_2), .D1_I(in_3), .D2_I(in_4), .D3_I(in_5), .D4_I(in_6), .D5_I(in_7),
    .D6_I(in_8), .D7_I(in_9), .D8_I(in_10), .D9_I(in_11), .D10_I(in_12), .D11_I(in_13), .D12_I(in_14),
    .D13_I(in_15), .D14_I(in_16), .D15_I(in_17), .D16_I(in_18), .D17_I(in_19), .D18_I(in_20), .D19_I(in_21),
    .TxD(out_42), .TxC(arduinouno_1_txc), .D0_O(out_22), .D1_O(out_23), .D2_O(out_24), .D3_O(out_25),
    .D4_O(out_26), .D5_O(out_27), .D6_O(out_28), .D7_O(out_29), .D8_O(out_30), .D9_O(out_31), .D10_O(out_32),
    .D11_O(out_33), .D12_O(out_34), .D13_O(out_35), .D14_O(out_36), .D15_O(out_37), .D16_O(out_38),
    .D17_O(out_39), .D18_O(out_40), .D19_O(out_41));
  Terminal terminal_1 (.D(out_42), .C(arduinouno_1_txc), .en(reset_2_out));
  Reset reset_2 (.out(reset_2_out));
  Comparator #(.Bits(8)) comparator_1 (.a(out_42), .b(8'ha), .eq(comparator_1_eq));  // open: gt, lt
  Break break_1 (.brk(switchdt_1_p3));
  // SwitchDT switchdt_1: pin names not known; wires that end beside it: arduinouno_1_txc, comparator_1_eq, switchdt_1_p3, out_42, arduinouno_1_txc
  PullDown pulldown_1 (.out(switchdt_1_p3));

  // Notes on the sheet:
  //   Break on:
  //   ↑ character
  //   ↓ newline
  //   {{de TODO}}
endmodule
