// Digital circuit arduino_uno_example.dig as structural Verilog
module arduino_uno_example (
  input  clk,
  output out_1,
  output out_2,
  output out_3,
  output out_4,
  output out_5,
  output out_6,
  output out_7,
  output out_8,
  output out_9,
  output out_10,
  output out_11,
  output out_12,
  output out_13,
  output out_14,
  output out_15,
  output out_16,
  output out_17,
  output out_18,
  output out_19,
  output out_20
);

  wire reset_1_out;

  Reset #(.invertOutput("false")) reset_1 (.out(reset_1_out));
  arduino_uno #(.generic("firmwareFilePath := ;")) arduino_uno_1 (
    .R(reset_1_out), .C(clk), .D0(out_1), .D1(out_2), .D2(out_3), .D3(out_4), .D4(out_5), .D5(out_6),
    .D6(out_7), .D7(out_8), .D8(out_9), .D9(out_10), .D10(out_11), .D11(out_12), .D12(out_13), .D13(out_14),
    .D14(out_15), .D15(out_16), .D16(out_17), .D17(out_18), .D18(out_19), .D19(out_20));
endmodule
