// Digital circuit splitter.dig as structural Verilog
module splitter (
  input  [3:0] in_1,
  input  [3:0] in_2,
  input  in_3,
  input  in_4,
  input  [3:0] in_6,
  input  [3:0] in_11,
  input  in_12,
  input  in_13,
  input  in_14,
  input  [3:0] in_19,
  input  [3:0] in_20,
  input  [3:0] in_23,
  input  [3:0] in_24,
  input  [3:0] in_27,
  output [7:0] out_5,
  output [7:0] out_7,
  output out_8,
  output out_9,
  output out_10,
  output [7:0] out_15,
  output out_16,
  output out_17,
  output out_18,
  output [7:0] out_21,
  output out_22,
  output [7:0] out_25,
  output out_26,
  output [7:0] out_28
);

  wire undriven;
  wire [3:0] not_1_out;

  not not_1 (not_1_out[0], in_12);
  not not_2 (out_16, undriven);
  // Pins of 1 and 4 bits meet at in_1
  // Pins of 1 and 4 bits meet at in_2
  // Pins of 1 and 8 bits meet at {in_2, in_1}
  // Pins of 1 and 4 bits meet at in_6
  // Pins of 1 and 8 bits meet at {out_7[7:4], in_6}
  // Pins of 1 and 4 bits meet at in_11
  // Pins of 1 and 4 bits meet at not_1_out
  // Pins of 4 and 8 bits meet at {not_1_out, in_11}
  // Pins of 1 and 8 bits meet at {out_15[7:4], in_11}
  // Pins of 1 and 4 bits meet at in_19
  // Pins of 1 and 4 bits meet at in_20
  // Pins of 1 and 8 bits meet at {in_20, in_19}

  assign out_5 = {in_2, in_1};
  assign out_7[3:0] = in_6;
  assign out_15[3:0] = in_11;
  assign out_21 = {in_20, in_19};
  assign out_25 = {in_24, in_23};
  assign out_28[3:0] = in_27;
endmodule
