// Digital circuit JK-MS.dig as structural Verilog
module JK_MS (
  input  J,
  input  C,
  input  K,
  output Q,
  output nQ
);

  wire and_1_out, and_2_out, and_3_out, and_4_out, nor_1_out, nor_2_out, not_1_out;

  and and_1 (and_1_out, nQ, J, C);
  not not_1 (not_1_out, C);
  and and_2 (and_2_out, C, K, Q);
  nor nor_1 (nor_1_out, and_1_out, nor_2_out);
  nor nor_2 (nor_2_out, nor_1_out, and_2_out);
  and and_3 (and_3_out, nor_1_out, not_1_out);
  and and_4 (and_4_out, not_1_out, nor_2_out);
  nor nor_3 (Q, and_3_out, nQ);
  nor nor_4 (nQ, Q, and_4_out);
endmodule

/* Test case:
J C K Q ~Q
# initial state is unknown
0 C 1 X X
# now its cleared
0 0 0 0 1
# set
1 1 0 0 1
1 0 0 1 0
# reset
0 1 1 1 0
0 0 1 0 1
# toggle
1 1 1 0 1
1 0 1 1 0
1 1 1 1 0
1 0 1 0 1
1 1 1 0 1
1 0 1 1 0
1 1 1 1 0
1 0 1 0 1
*/
