// Digital circuit PLD.dig as structural Verilog
module PLD (
  input  A,
  input  B,
  input  C,
  input  D,
  output Y
);

  wire diodebackward_1_out, diodebackward_3_out, diodebackward_5_out, diodebackward_7_out, not_1_out,
       not_2_out, not_3_out, not_4_out;

  not not_1 (not_1_out, A);
  DiodeBackward diodebackward_1 (.in(A), .out(diodebackward_1_out));
  DiodeBackward #(.Blown("true")) diodebackward_2 (.in(not_1_out), .out(diodebackward_1_out));
  DiodeBackward #(.Blown("true")) diodebackward_3 (.in(A), .out(diodebackward_3_out));
  DiodeBackward diodebackward_4 (.in(not_1_out), .out(diodebackward_3_out));
  DiodeBackward diodebackward_5 (.in(A), .out(diodebackward_5_out));
  DiodeBackward diodebackward_6 (.in(not_1_out), .out(diodebackward_5_out));
  DiodeBackward diodebackward_7 (.in(A), .out(diodebackward_7_out));
  DiodeBackward diodebackward_8 (.in(not_1_out), .out(diodebackward_7_out));
  not not_2 (not_2_out, B);
  DiodeBackward #(.Blown("true")) diodebackward_9 (.in(B), .out(diodebackward_1_out));
  DiodeBackward diodebackward_10 (.in(not_2_out), .out(diodebackward_1_out));
  DiodeBackward diodebackward_11 (.in(B), .out(diodebackward_3_out));
  DiodeBackward #(.Blown("true")) diodebackward_12 (.in(not_2_out), .out(diodebackward_3_out));
  DiodeBackward diodebackward_13 (.in(B), .out(diodebackward_5_out));
  DiodeBackward diodebackward_14 (.in(not_2_out), .out(diodebackward_5_out));
  DiodeBackward diodebackward_15 (.in(B), .out(diodebackward_7_out));
  DiodeBackward diodebackward_16 (.in(not_2_out), .out(diodebackward_7_out));
  not not_3 (not_3_out, C);
  DiodeBackward #(.Blown("true")) diodebackward_17 (.in(C), .out(diodebackward_1_out));
  DiodeBackward #(.Blown("true")) diodebackward_18 (.in(not_3_out), .out(diodebackward_1_out));
  DiodeBackward #(.Blown("true")) diodebackward_19 (.in(C), .out(diodebackward_3_out));
  DiodeBackward #(.Blown("true")) diodebackward_20 (.in(not_3_out), .out(diodebackward_3_out));
  DiodeBackward diodebackward_21 (.in(C), .out(diodebackward_5_out));
  DiodeBackward diodebackward_22 (.in(not_3_out), .out(diodebackward_5_out));
  DiodeBackward diodebackward_23 (.in(C), .out(diodebackward_7_out));
  DiodeBackward diodebackward_24 (.in(not_3_out), .out(diodebackward_7_out));
  not not_4 (not_4_out, D);
  DiodeBackward #(.Blown("true")) diodebackward_25 (.in(D), .out(diodebackward_1_out));
  DiodeBackward #(.Blown("true")) diodebackward_26 (.in(not_4_out), .out(diodebackward_1_out));
  DiodeBackward #(.Blown("true")) diodebackward_27 (.in(D), .out(diodebackward_3_out));
  DiodeBackward #(.Blown("true")) diodebackward_28 (.in(not_4_out), .out(diodebackward_3_out));
  DiodeBackward diodebackward_29 (.in(D), .out(diodebackward_5_out));
  DiodeBackward diodebackward_30 (.in(not_4_out), .out(diodebackward_5_out));
  DiodeBackward diodebackward_31 (.in(D), .out(diodebackward_7_out));
  DiodeBackward diodebackward_32 (.in(not_4_out), .out(diodebackward_7_out));
  PullUp pullup_1 (.out(diodebackward_1_out));
  PullUp pullup_2 (.out(diodebackward_3_out));
  or or_1 (Y, diodebackward_1_out, diodebackward_3_out, diodebackward_5_out, diodebackward_7_out);
  PullUp pullup_3 (.out(diodebackward_5_out));
  PullUp pullup_4 (.out(diodebackward_7_out));
endmodule

/* Test case A xor B:
A B C D Y
0 0 0 0 0
0 1 0 0 1
1 0 0 0 1
1 1 0 0 0
0 0 0 0 0
0 1 0 0 1
1 0 0 0 1
1 1 0 0 0
*/
