// Digital circuit TafficLight3.dig as structural Verilog
module TafficLight3 (
  input  C,
  input  F
);

  wire and_1_out, not_1_out, or_1_out, z_0_nq, z_0_q, z_1_nq, z_1_q;

  not not_1 (not_1_out, F);
  or or_1 (or_1_out, z_1_q, not_1_out);
  JK_FF z_1 (.J(z_0_q), .C(C), .K(z_0_q), .Q(z_1_q), .nQ(z_1_nq));
  JK_FF z_0 (.J(or_1_out), .C(C), .K(1'b1), .Q(z_0_q), .nQ(z_0_nq));
  and and_1 (and_1_out, z_1_q, z_0_nq);
  LED R (.in(z_1_nq));
  LED Y (.in(z_0_q));
  LED G (.in(and_1_out));
endmodule

/* Test case:
C F  R Y G
0 0  1 0 0
C 0  1 1 0
C 0  0 0 1
C 0  0 1 0
C 0  1 0 0
C 0  1 1 0
# Fire signal goes high
C 1  0 0 1
C 1  0 1 0
# TL runs to read and then stops
C 1  1 0 0
C 1  1 0 0
C 1  1 0 0
C 0  1 0 0
# If fire signal goes low TL runs in the normal way
C 0  1 1 0
*/
