// Digital circuit WiredOr.dig as structural Verilog
module WiredOr (
  input  A,
  input  B,
  output Y
);

  // DiodeForeward diodeforeward_1: pin names not known; wires that end beside it: A, Y
  // DiodeForeward diodeforeward_2: pin names not known; wires that end beside it: B, Y
  PullDown pulldown_1 (.out(Y));
endmodule

/* Test case:
A B Y
0 0 0
0 1 1
0 Z 0
1 0 1
1 1 1
1 Z 1
Z 0 0
Z 1 1
Z Z 0
*/
