// Digital circuit BASYS3_lightchase.dig as structural Verilog
module BASYS3_lightchase (
  input  Clk,
  output Y0,
  output Y1,
  output Y2,
  output Y3,
  output Y4,
  output Y5,
  output Y6,
  output Y7,
  output Y8,
  output Y9,
  output Y10,
  output Y11,
  output Y12,
  output Y13,
  output Y14,
  output Y15
);

  wire jk_ff_1_q;
  wire [3:0] add_1_s, d_ff_1_q, multiplexer_1_out;

  Multiplexer #(.Bits(4)) multiplexer_1 (.sel(jk_ff_1_q), .in_0(4'b0001), .in_1(4'b1111), .out(multiplexer_1_out));
  Add #(.Bits(4)) add_1 (.a(d_ff_1_q), .b(multiplexer_1_out), .c_i(1'b0), .s(add_1_s));  // open: c_o
  D_FF #(.Bits(4)) d_ff_1 (.D(add_1_s), .C(Clk), .Q(d_ff_1_q));  // open: nQ
  Decoder #(.Selector_Bits(4)) decoder_1 (
    .sel(d_ff_1_q), .out_0(Y0), .out_1(Y1), .out_2(Y2), .out_3(Y3), .out_4(Y4), .out_5(Y5), .out_6(Y6),
    .out_7(Y7), .out_8(Y8), .out_9(Y9), .out_10(Y10), .out_11(Y11), .out_12(Y12), .out_13(Y13), .out_14(Y14),
    .out_15(Y15));
  JK_FF jk_ff_1 (.J(Y14), .C(Clk), .K(Y1), .Q(jk_ff_1_q));  // open: nQ

  // Notes on the sheet:
  //   Y0: pin U16
  //   Y1: pin E19
  //   Y2: pin U19
  //   Y3: pin V19
  //   Y4: pin W18
  //   Y5: pin U15
  //   Y6: pin U14
  //   Y7: pin V14
  //   Y8: pin V13
  //   Y9: pin V3
  //   Y10: pin W3
  //   Y11: pin U3
  //   Y12: pin P3
  //   Y13: pin N3
  //   Y14: pin P1
  //   Y15: pin L1
  //   Clk: pin W5, Hz: 20
  //   Export this file to VHDL and use Xilinx Vivado to create the bitstream.
  //   Also add the created constrains file to the vivado project to assign 
  //   the pins correctly.
  //   Board: BASYS3
endmodule

/* Test case:
Clk Y15 Y14 Y13 Y12 Y11 Y10 Y9 Y8 Y7 Y6 Y5 Y4 Y3 Y2 Y1 Y0
 0  bits(16,1)
repeat(14) C bits(16,1<<n+1)
repeat(15) C bits(16,1<<15-n)
repeat(16) C bits(16,1<<n)
*/
