// Digital circuit Register.dig as structural Verilog
module Register (
  input  D,
  input  C,
  input  en,
  output Q
);

  wire multiplexer_1_out, xor_1_out, xor_2_out;

  xor xor_1 (xor_1_out, 1'b0, D);
  xor xor_2 (xor_2_out, 1'b0, en);
  Multiplexer #(.generic("this.Bits=orig.Bits;")) multiplexer_1 (
    .sel(xor_2_out), .in_0(Q), .in_1(xor_1_out), .out(multiplexer_1_out));
  D_FF #(.generic("this.Bits=orig.Bits;")) d_ff (.D(multiplexer_1_out), .C(C), .Q(Q));  // open: nQ
endmodule
