// Digital circuit T_FF.dig as structural Verilog
module T_FF (
  input  C,
  output Q,
  output nQ
);

  D_FF #(.generic("this.Default=orig.Default;")) d_ff (.D(nQ), .C(C), .Q(Q), .nQ(nQ));

  // Notes on the sheet:
  //   C: Hz: 2
endmodule
