// Digital circuit T_FF_EN.dig as structural Verilog
module T_FF_EN (
  input  T,
  input  C,
  output Q,
  output nQ
);

  wire and_1_out, and_2_out, or_1_out, xor_1_out;

  xor xor_1 (xor_1_out, 1'b0, T);
  and and_1 (and_1_out, Q, ~xor_1_out);  // And
  and and_2 (and_2_out, xor_1_out, nQ);
  or or_1 (or_1_out, and_1_out, and_2_out);
  D_FF #(.generic("this.Default=orig.Default;")) d_ff (.D(or_1_out), .C(C), .Q(Q), .nQ(nQ));

  // Notes on the sheet:
  //   C: Hz: 2
endmodule
