// Digital circuit CounterSplitter.dig as structural Verilog
module CounterSplitter (
  input  clk,
  output [9:0] out_2
);

  wire counter_1_ovf, counter_2_ovf, not_1_out;
  wire [4:0] counter_1_out, counter_2_out;

  Counter #(.Bits(5)) counter_1 (.en(clk), .C(1'b0), .out(counter_1_out), .ovf(counter_1_ovf));  // open: clr
  Counter #(.Bits(5)) counter_2 (.en(counter_1_ovf), .C(1'b0), .out(counter_2_out), .ovf(counter_2_ovf));  // open: clr
  not not_1 (not_1_out, counter_2_ovf);
  Break break_1 (.brk(counter_2_ovf));
  Register #(.Bits(10)) register_1 (.D({counter_2_out, counter_1_out}), .C(clk), .en(not_1_out), .Q(out_2));
endmodule
