// Digital circuit Diode1Error.dig as structural Verilog
module Diode1Error (
  input  A,
  output Y
);

  wire nfet_1_d;

  NFET nfet_1 (.G(A), .D(nfet_1_d), .S(1'b0));
  PullUp pullup_1 (.out(nfet_1_d));
  PullUp pullup_2 (.out(Y));
  DiodeBackward diodebackward_1 (.in(Y), .out(nfet_1_d));
  DiodeBackward diodebackward_2 (.in(nfet_1_d), .out(Y));
endmodule

/* Test case:
A Y
0 1
1 0
0 1
*/
