// Digital circuit DiodeTest.dig as structural Verilog
module DiodeTest (
  input  A1,
  input  B1,
  input  A2,
  input  B2,
  input  A3,
  input  A4,
  output Y1,
  output Y2,
  output Y3,
  output Y4
);

  Diode diode_1 (.cathode(Y3), .anode(A3));
  Diode diode_2 (.cathode(A3), .anode(Y3));
  Diode diode_3 (.cathode(A4), .anode(Y4));
  Diode diode_4 (.cathode(Y4), .anode(A4));
  Diode diode_5 (.cathode(A1), .anode(Y1));
  Diode diode_6 (.cathode(B1), .anode(Y1));
  PullUp pullup_1 (.out(Y1));
  Diode diode_7 (.cathode(Y2), .anode(A2));
  Diode diode_8 (.cathode(Y2), .anode(B2));
  PullDown pulldown_1 (.out(Y2));
endmodule

/* Test case:
A3 Y3
0 0
1 1
Z Z
*/

/* Test case:
A4 Y4
0 0
1 1
Z Z
*/

/* Test case wired AND:
A1 B1 Y1
0 0 0
0 1 0
0 Z 0
1 0 0
1 1 1
1 Z 1
Z 0 0
Z 1 1
Z Z 1
*/

/* Test case wired OR:
A2 B2 Y2
0 0 0
0 1 1
0 Z 0
1 0 1
1 1 1
1 Z 1
Z 0 0
Z 1 1
Z Z 0
*/
