// Digital circuit Medwedew.dig as structural Verilog
module Medwedew (
  input  C,
  output Q_3,
  output Q_2,
  output Q_1,
  output Q_0
);

  wire and_1_out, and_2_out, and_3_out, and_4_out, and_5_out, and_6_out, and_7_out, and_8_out, and_9_out,
       not_1_out, not_2_out, not_3_out, not_4_out, or_1_out, or_2_out, or_3_out;

  not not_1 (not_1_out, Q_3);
  not not_2 (not_2_out, Q_2);
  not not_3 (not_3_out, Q_1);
  not not_4 (not_4_out, Q_0);
  and and_1 (and_1_out, Q_0, Q_1, Q_2, not_1_out);
  and and_2 (and_2_out, not_4_out, Q_3);
  and and_3 (and_3_out, not_3_out, Q_3);
  and and_4 (and_4_out, not_2_out, Q_3);
  and and_5 (and_5_out, Q_0, Q_1, not_2_out);
  and and_6 (and_6_out, not_4_out, Q_2);
  and and_7 (and_7_out, not_3_out, Q_2);
  and and_8 (and_8_out, Q_0, not_3_out);
  and and_9 (and_9_out, not_4_out, Q_1);
  or or_1 (or_1_out, and_1_out, and_2_out, and_3_out, and_4_out);
  or or_2 (or_2_out, and_5_out, and_6_out, and_7_out);
  or or_3 (or_3_out, and_8_out, and_9_out);
  D_FF Q_3_n (.D(or_1_out), .C(C), .Q(Q_3));  // open: nQ
  D_FF Q_2_n (.D(or_2_out), .C(C), .Q(Q_2));  // open: nQ
  D_FF Q_1_n (.D(or_3_out), .C(C), .Q(Q_1));  // open: nQ
  D_FF Q_0_n (.D(not_4_out), .C(C), .Q(Q_0));  // open: nQ

  // Other names for the same wires on the sheet: Q_0_n = Q_0; Q_1_n = Q_1; Q_2_n = Q_2; Q_3_n = Q_3

  // Notes on the sheet:
  //   C: Hz: 2
  //   Q_3: pin 15
  //   Q_2: pin 16
  //   Q_1: pin 17
  //   Q_0: pin 18
endmodule
