// Digital circuit Names.dig as structural Verilog
module Names (
  input  A_1,
  input  B_2,
  input  C_2,
  input  A,
  output Y
);

  wire and_1_out, and_2_out;

  and and_1 (and_1_out, A_1, B_2);
  and and_2 (and_2_out, C_2, A);
  or or_1 (Y, and_1_out, and_2_out);

  // Notes on the sheet:
  //   Y: pin 1
  //   A_1: pin 2
  //   B_2: pin 3
  //   C_2: pin 4
  //   A: pin 5
endmodule
