// Digital circuit PassThrough.dig as structural Verilog
module PassThrough (
  input  A,
  input  clk,
  output Y,
  output X
);

  D_FF d_ff_1 (.D(A), .C(clk), .Q(Y));  // open: nQ

  assign X = A;

  // Notes on the sheet:
  //   A: pin 3
  //   Y: pin 16
  //   X: pin 15
endmodule
