// Digital circuit analyzeBacktrack.dig as structural Verilog
module analyzeBacktrack (
  input  _1A,
  input  _1B,
  input  _2A,
  input  _2B,
  input  _3A,
  input  _3B,
  input  _4A,
  input  _4B,
  input  _4C,
  output _1Y,
  output _2Y,
  output _3Y,
  output _4Y
);

  xor xor_1 (_1Y, _1A, _1B);
  xnor xnor_1 (_2Y, _2A, _2B);
  or or_1 (_3Y, _3A, _3B);
  and and_1 (_4Y, _4A, _4B, _4C);
endmodule
