// Digital circuit analyzeTestCounterInvIn.dig as structural Verilog
module analyzeTestCounterInvIn (
  input  C
);

  Counter #(.Bits(2)) Q (.en(~1'b0), .C(C), .clr(~1'b1));  // open: out, ovf
endmodule
