// Digital circuit analyzeTestCounterPreset.dig as structural Verilog
module analyzeTestCounterPreset (
  input  C
);

  CounterPreset #(.Bits(2)) counterpreset_1 (
    .en(1'b1), .C(C), .dir(1'b0), .in(2'b00), .ld(1'b0), .clr(1'b0));  // open: out, ovf

  // Notes on the sheet:
  //   C: Hz: 2
endmodule
