// Digital circuit analyzeTestJKFFInvIn.dig as structural Verilog
module analyzeTestJKFFInvIn (
  input  clk
);

  wire Q_0n_nq;

  JK_FF Q_1n (.J(~Q_0n_nq), .C(clk), .K(~Q_0n_nq));  // open: Q, nQ
  JK_FF Q_0n (.J(1'b1), .C(clk), .K(1'b1), .nQ(Q_0n_nq));  // open: Q
endmodule
