// Digital circuit analyzeTestJKFFNested.dig as structural Verilog
module analyzeTestJKFFNested (
  input  clk
);

  wire Q_0n_q;

  jkff Q_1n (.J(Q_0n_q), .C(clk), .K(Q_0n_q));  // open: Q, nQ
  jkff Q_0n (.J(1'b1), .C(clk), .K(1'b1), .Q(Q_0n_q));  // open: nQ
endmodule
