// Digital circuit analyzeTestRegister.dig as structural Verilog
module analyzeTestRegister (
  input  C
);

  wire [1:0] add_1_s, Q_q;

  Add #(.Bits(2)) add_1 (.a(Q_q), .b(2'b01), .c_i(1'b0), .s(add_1_s));  // open: c_o
  Register #(.Bits(2)) Q (.D(add_1_s), .C(C), .en(1'b1), .Q(Q_q));
endmodule
