// Digital circuit analyzeTestTFFEnable.dig as structural Verilog
module analyzeTestTFFEnable (
  input  clk
);

  wire Q_0n_q;

  T_FF Q_1n (.T(Q_0n_q), .C(clk));  // open: Q, nQ
  T_FF Q_0n (.T(1'b1), .C(clk), .Q(Q_0n_q));  // open: nQ
endmodule
