// Digital circuit analyzeTestTFFEnableInvIn.dig as structural Verilog
module analyzeTestTFFEnableInvIn (
  input  clk
);

  wire Q_0n_nq;

  T_FF Q_1n (.T(~Q_0n_nq), .C(clk));  // open: Q, nQ
  T_FF Q_0n (.T(1'b1), .C(clk), .nQ(Q_0n_nq));  // open: Q
endmodule
