// Digital circuit multiBitCounter.dig as structural Verilog
module multiBitCounter (
  input  C,
  output [1:0] Y
);

  wire [1:0] add_1_s, Q_q;

  Add #(.Bits(2)) add_1 (.a(Q_q), .b(2'b01), .c_i(1'b0), .s(add_1_s));  // open: c_o
  D_FF #(.Bits(2)) Q (.D(add_1_s), .C(C), .Q(Q_q), .nQ(Y));
endmodule
