// Digital circuit multiBitInOutXOr.dig as structural Verilog
module multiBitInOutXOr (
  input  [3:0] A,
  input  [3:0] B,
  output [3:0] S
);

  assign S = A ^ B;  // XOr xor_1, 4 bits wide

  // Notes on the sheet:
  //   A: pin 1,2,3,4
  //   B: pin 5,6,7,8
  //   S: pin 9,10,11,12
endmodule
