// Digital circuit testCaseCreation.dig as structural Verilog
module testCaseCreation (
  input  [1:0] b,
  input  [1:0] a,
  input  C_i,
  output C_o,
  output [1:0] S
);

  Add #(.Bits(2)) add_1 (.a(a), .b(b), .c_i(C_i), .s(S), .c_o(C_o));
endmodule
