// Digital circuit uniqueNames3.dig as structural Verilog
module uniqueNames3 (
  input  C
);

  wire and_1_out, and_2_out, not_1_out, not_2_out, or_1_out, Q_0n, Q_1n;

  not not_1 (not_1_out, Q_0n);
  not not_2 (not_2_out, Q_1n);
  and and_1 (and_1_out, Q_0n, not_2_out);
  and and_2 (and_2_out, not_1_out, Q_1n);
  or or_1 (or_1_out, and_1_out, and_2_out);
  D_FF d_ff_1 (.D(or_1_out), .C(C), .Q(Q_1n));  // open: nQ
  D_FF d_ff_2 (.D(not_1_out), .C(C), .Q(Q_0n));  // open: nQ
endmodule
