// Digital circuit uniqueNames4.dig as structural Verilog
module uniqueNames4 (
  input  C,
  output A,
  output B
);

  wire and_1_out, and_2_out, not_1_out, not_2_out, or_1_out;

  not not_1 (not_1_out, A);
  not not_2 (not_2_out, B);
  and and_1 (and_1_out, A, not_2_out);
  and and_2 (and_2_out, not_1_out, B);
  or or_1 (or_1_out, and_1_out, and_2_out);
  D_FF d_ff_1 (.D(or_1_out), .C(C), .Q(B));  // open: nQ
  D_FF d_ff_2 (.D(not_1_out), .C(C), .Q(A));  // open: nQ

  // Other names for the same wires on the sheet: Q_0n = A; Q_1n = B
endmodule
