// Digital circuit analyzeTestJKFF.dig as structural Verilog
module analyzeTestJKFF (
  input  clk
);

  wire Q_0n_q;

  JK_FF Q_1n (.J(Q_0n_q), .C(clk), .K(Q_0n_q));  // open: Q, nQ
  JK_FF Q_0n (.J(1'b1), .C(clk), .K(1'b1), .Q(Q_0n_q));  // open: nQ
endmodule
