// Digital circuit analyzeTestTFF.dig as structural Verilog
module analyzeTestTFF (
  input  clk
);

  wire Q_0n_q;

  JK_FF Q_1n (.J(Q_0n_q), .C(clk), .K(Q_0n_q));  // open: Q, nQ
  T_FF Q_0n (.T(clk), .Q(Q_0n_q));  // open: C, nQ
endmodule
