// Digital circuit autoWire.dig as structural Verilog
module autoWire (
  input  A,
  input  B,
  output Y
);

  // Not not_1 is placed but not wired
  // And and_1 is placed but not wired
  // Not not_2 is placed but not wired
  // Not not_3 is placed but not wired
endmodule

/* Test case:
A B Y
0 0 0
0 1 1
1 0 1
1 1 1
*/
