// Digital circuit Plexer.dig as structural Verilog
module Plexer (
  input  C,
  input  Count,
  output s2,
  output d0,
  output c0,
  output b0,
  output a0,
  output e0,
  output f0,
  output g0,
  output s1,
  output s0
);

  wire C0_p4, C1_p4, dif_1_p3;
  wire [1:0] counter2bit3_1_p2;
  wire [3:0] C0_p3, C1_p3, C2_p3, multiplexer_1_out;

  // dif dif_1: pin names not known; wires that end beside it: Count, C, dif_1_p3
  // counter C0: pin names not known; wires that end beside it: dif_1_p3, C, C0_p3, C0_p4
  // counter C1: pin names not known; wires that end beside it: C0_p4, C, C1_p3, C1_p4
  // counter C2: pin names not known; wires that end beside it: C1_p4, C, C2_p3
  // counter2Bit3 counter2bit3_1: pin names not known; wires that end beside it: C, counter2bit3_1_p2[0], counter2bit3_1_p2[1]
  Multiplexer #(.Selector_Bits(2), .Bits(4)) multiplexer_1 (
    .sel(counter2bit3_1_p2), .in_0(C0_p3), .in_1(C1_p3), .in_2(C2_p3), .in_3(4'b0000), .out(multiplexer_1_out));
  Decoder #(.Selector_Bits(2)) decoder_1 (.sel(counter2bit3_1_p2), .out_0(s0), .out_1(s1), .out_2(s2));  // open: out_3
  // decoder decoder_2: pin names not known; wires that end beside it: multiplexer_1_out[0], multiplexer_1_out[1], multiplexer_1_out[2], multiplexer_1_out[3], d0, c0, b0, a0, e0, f0, g0

  // Notes on the sheet:
  //   C: Hz: 20
  //   s2: Pin 18, pin 18
  //   d0: Pin 14, pin 8
  //   c0: Pin 12, pin 6
  //   b0: Pin 11, pin 5
  //   a0: Pin 9, pin 4
  //   e0: Pin 8, pin 9
  //   f0: Pin 6, pin 11
  //   g0: Pin 5, pin 12
  //   s1: Pin 17, pin 19
  //   s0: Pin 16, pin 20
  //   Count: Pin 26, pin 26
endmodule
