// Digital circuit counter.dig as structural Verilog
module counter (
  input  en,
  input  C,
  output [3:0] Q,
  output ov
);

  wire and_1_out, and_2_out, and_3_out, and_4_out, and_5_out, and_6_out, and_7_out, and_8_out, and_9_out,
       and_10_out, and_11_out, and_12_out, not_1_out, not_2_out, not_3_out, not_4_out, not_5_out, or_1_out,
       or_2_out, or_3_out, or_4_out;

  not not_1 (not_1_out, en);
  not not_2 (not_2_out, Q[0]);
  not not_3 (not_3_out, Q[1]);
  not not_4 (not_4_out, Q[2]);
  not not_5 (not_5_out, Q[3]);
  and and_1 (and_1_out, Q[0], Q[1], Q[2], en);
  and and_2 (and_2_out, not_2_out, Q[3]);
  and and_3 (and_3_out, Q[3], not_1_out);
  and and_4 (and_4_out, Q[0], Q[1], not_4_out, en);
  and and_5 (and_5_out, not_2_out, Q[2]);
  and and_6 (and_6_out, not_3_out, Q[2]);
  and and_7 (and_7_out, Q[2], not_1_out);
  and and_8 (and_8_out, Q[0], not_3_out, not_5_out, en);
  and and_9 (and_9_out, not_2_out, Q[1]);
  and and_10 (and_10_out, Q[1], not_1_out);
  and and_11 (and_11_out, Q[0], not_1_out);
  and and_12 (and_12_out, not_2_out, en);
  and and_13 (ov, Q[0], en, Q[3]);
  or or_1 (or_1_out, and_1_out, and_2_out, and_3_out);
  or or_2 (or_2_out, and_4_out, and_5_out, and_6_out, and_7_out);
  or or_3 (or_3_out, and_8_out, and_9_out, and_10_out);
  or or_4 (or_4_out, and_11_out, and_12_out);
  D_FF Q_3n (.D(or_1_out), .C(C), .Q(Q[3]));  // open: nQ
  D_FF Q_2n (.D(or_2_out), .C(C), .Q(Q[2]));  // open: nQ
  D_FF Q_1n (.D(or_3_out), .C(C), .Q(Q[1]));  // open: nQ
  D_FF Q_0n (.D(or_4_out), .C(C), .Q(Q[0]));  // open: nQ
  // Pins of 1 and 4 bits meet at Q

  // Other names for the same wires on the sheet: Q_0n = Q[0]; Q_1n = Q[1]; Q_2n = Q[2]; Q_3n = Q[3]
endmodule
