// Digital circuit decoder.dig as structural Verilog
module decoder (
  input  D_0,
  input  D_1,
  input  D_2,
  input  D_3,
  output d,
  output c,
  output b,
  output a,
  output e,
  output f,
  output g
);

  wire and_1_out, and_2_out, and_3_out, and_4_out, and_5_out, and_6_out, and_7_out, and_8_out, and_9_out,
       and_10_out, and_11_out, and_12_out, and_13_out, and_14_out, and_15_out, and_16_out, and_17_out,
       and_18_out, and_19_out, and_20_out, and_21_out, and_22_out, and_23_out, and_24_out, and_25_out,
       and_26_out, and_27_out, and_28_out, and_29_out, and_30_out, and_31_out, and_32_out, and_33_out,
       and_34_out, and_35_out, not_1_out, not_2_out, not_3_out, not_4_out;

  not not_1 (not_1_out, D_3);
  not not_2 (not_2_out, D_2);
  not not_3 (not_3_out, D_1);
  not not_4 (not_4_out, D_0);
  and and_1 (and_1_out, not_1_out, D_1);
  and and_2 (and_2_out, not_1_out, D_2, D_0);
  and and_3 (and_3_out, D_3, not_2_out, not_3_out);
  and and_4 (and_4_out, D_3, not_4_out);
  and and_5 (and_5_out, not_2_out, not_4_out);
  and and_6 (and_6_out, D_2, D_1);
  and and_7 (and_7_out, not_1_out, not_3_out, not_4_out);
  and and_8 (and_8_out, not_1_out, D_1, D_0);
  and and_9 (and_9_out, D_3, not_3_out, D_0);
  and and_10 (and_10_out, not_2_out, not_4_out);
  and and_11 (and_11_out, not_2_out, not_3_out);
  and and_12 (and_12_out, not_1_out, D_2);
  and and_13 (and_13_out, D_3, not_2_out);
  and and_14 (and_14_out, not_2_out, D_0);
  and and_15 (and_15_out, not_2_out, not_3_out);
  and and_16 (and_16_out, not_3_out, D_0);
  and and_17 (and_17_out, not_1_out, not_2_out, not_4_out);
  and and_18 (and_18_out, D_3, not_3_out);
  and and_19 (and_19_out, D_2, not_3_out, D_0);
  and and_20 (and_20_out, not_2_out, D_1, D_0);
  and and_21 (and_21_out, D_2, D_1, not_4_out);
  and and_22 (and_22_out, D_3, D_1);
  and and_23 (and_23_out, D_3, D_2);
  and and_24 (and_24_out, not_2_out, not_4_out);
  and and_25 (and_25_out, D_1, not_4_out);
  and and_26 (and_26_out, not_1_out, D_2, not_3_out);
  and and_27 (and_27_out, D_3, not_2_out);
  and and_28 (and_28_out, D_3, D_1);
  and and_29 (and_29_out, D_2, not_4_out);
  and and_30 (and_30_out, not_3_out, not_4_out);
  and and_31 (and_31_out, D_3, not_2_out);
  and and_32 (and_32_out, not_1_out, D_2, not_3_out);
  and and_33 (and_33_out, D_3, D_0);
  and and_34 (and_34_out, not_2_out, D_1);
  and and_35 (and_35_out, D_1, not_4_out);
  or or_1 (b, and_7_out, and_8_out, and_9_out, and_10_out, and_11_out);
  or or_2 (c, and_12_out, and_13_out, and_14_out, and_15_out, and_16_out);
  or or_3 (d, and_17_out, and_18_out, and_19_out, and_20_out, and_21_out);
  or or_4 (e, and_22_out, and_23_out, and_24_out, and_25_out);
  or or_5 (f, and_26_out, and_27_out, and_28_out, and_29_out, and_30_out);
  or or_6 (g, and_31_out, and_32_out, and_33_out, and_34_out, and_35_out);
  or or_7 (a, and_1_out, and_2_out, and_3_out, and_4_out, and_5_out, and_6_out);

  // Notes on the sheet:
  //   D_0: Bit 0 des Dekodereingangs.
  //   D_1: Bit 1 des Dekodereingangs.
  //   D_2: Bit 2 des Dekodereingangs.
  //   D_3: Bit 3 des Dekodereingangs.
endmodule
