// Digital circuit dif.dig as structural Verilog
module dif (
  input  Count,
  input  C,
  output Out
);

  wire p0_q, p1_nq;

  D_FF p0 (.D(Count), .C(C), .Q(p0_q));  // open: nQ
  D_FF p1 (.D(p0_q), .C(C), .nQ(p1_nq));  // open: Q
  and and_1 (Out, p0_q, p1_nq);
endmodule
