// Digital circuit busTest2.dig as structural Verilog
module busTest2 (
  input  [1:0] A0,
  input  [1:0] B11,
  input  [1:0] A1,
  input  [1:0] B10,
  input  [1:0] A2,
  input  [1:0] B9,
  input  [1:0] A3,
  input  [1:0] B8,
  input  [1:0] A4,
  input  [1:0] B7,
  input  [1:0] A5,
  input  [1:0] B6,
  input  [1:0] A6,
  input  [1:0] B5,
  input  [1:0] A7,
  input  [1:0] B4,
  input  [1:0] A8,
  input  [1:0] B3,
  input  [1:0] A9,
  input  [1:0] B2,
  input  [1:0] A10,
  input  [1:0] B1,
  input  [1:0] A11,
  input  [1:0] B0,
  output [1:0] S2,
  output [1:0] S3,
  output [1:0] S4,
  output [1:0] S5,
  output [1:0] S6,
  output [1:0] S7,
  output [1:0] S8,
  output [1:0] S9,
  output [1:0] S10,
  output [1:0] S11,
  output [1:0] S0,
  output [1:0] S1
);

  assign S0 = A0 ^ B0;  // XOr xor_1, 2 bits wide
  assign S1 = A1 ^ B1;  // XOr xor_2, 2 bits wide
  assign S2 = A2 ^ B2;  // XOr xor_3, 2 bits wide
  assign S3 = A3 ^ B3;  // XOr xor_4, 2 bits wide
  assign S4 = A4 ^ B4;  // XOr xor_5, 2 bits wide
  assign S5 = A5 ^ B5;  // XOr xor_6, 2 bits wide
  assign S6 = A6 ^ B6;  // XOr xor_7, 2 bits wide
  assign S7 = A7 ^ B7;  // XOr xor_8, 2 bits wide
  assign S8 = A8 ^ B8;  // XOr xor_9, 2 bits wide
  assign S9 = A9 ^ B9;  // XOr xor_10, 2 bits wide
  assign S10 = A10 ^ B10;  // XOr xor_11, 2 bits wide
  assign S11 = A11 ^ B11;  // XOr xor_12, 2 bits wide
endmodule
