// Digital circuit main.dig as structural Verilog
module main (
  input  in_1,
  input  in_2,
  output out_3
);

  // mid mid_1: pin names not known; wires that end beside it: in_1, in_2, out_3
endmodule
