// Digital circuit main2.dig as structural Verilog
module main2 (
  input  in_1,
  input  in_2,
  output out_3
);

  // mid2 mid2_1: pin names not known; wires that end beside it: in_1, in_2, out_3
endmodule
