// Digital circuit main5.dig as structural Verilog
module main5 (
  input  in_1,
  input  in_3,
  output out_2
);

  // midBit midbit_1: pin names not known; wires that end beside it: in_1, in_3, out_2
endmodule
