// Digital circuit verilog3.dig as structural Verilog
module verilog3 (
  input  [3:0] A,
  input  [3:0] B,
  input  C_i,
  output [3:0] S,
  output C_o
);

  wire verilog3_inc_1_c_o;

  verilog3_inc verilog3_inc_1 (.C_i(C_i), .A(A[1:0]), .B(B[1:0]), .S(S[1:0]), .C_o(verilog3_inc_1_c_o));
  verilog3_inc verilog3_inc_2 (.C_i(verilog3_inc_1_c_o), .A(A[3:2]), .B(B[3:2]), .S(S[3:2]), .C_o(C_o));

  // Notes on the sheet:
  //   A: default 3
  //   B: default 4
  //   C_i: default 4
endmodule

/* Test case:
A B C_i C_o S 

loop(a,16)
loop(b,16)
  (a) (b) 0 ((a+b)>>4) (a+b)
end loop
end loop
*/
