// Digital circuit verilogFile.dig as structural Verilog
module verilogFile (
  input  [3:0] A,
  input  [3:0] B,
  input  C_i,
  output [3:0] S,
  output C_o
);

  add #(.applicationType("IVERILOG"), .CodeFile("/home/hneemann/Dokumente/Java/digital/src/test/resources/dig/external/verilog/verilogFile.v")) u_add (
    .a(A), .b(B), .c_i(C_i), .s(S), .c_o(C_o));

  // Notes on the sheet:
  //   A: default 3
  //   B: default 4
  //   C_i: default 4
endmodule

/* Test case:
A B C_i C_o S 

loop(a,16)
loop(b,16)
  (a) (b) 0 ((a+b)>>4) (a+b)
end loop
end loop
*/
