// Digital circuit failingTest.dig as structural Verilog
module failingTest (
  input  C,
  output Q_3,
  output Q_2,
  output Q_1,
  output Q_0
);

  wire and_1_out, and_2_out, and_3_out, and_4_out, and_5_out, and_6_out, and_7_out, and_8_out, and_9_out,
       not_1_out, not_2_out, not_3_out, not_4_out, or_1_out, or_2_out, or_3_out;

  not not_1 (not_1_out, Q_0);
  not not_2 (not_2_out, Q_1);
  not not_3 (not_3_out, Q_2);
  not not_4 (not_4_out, Q_3);
  and and_1 (and_1_out, Q_0, Q_1, Q_2, not_4_out);
  and and_2 (and_2_out, not_1_out, Q_3);
  and and_3 (and_3_out, not_2_out, Q_3);
  and and_4 (and_4_out, not_3_out, Q_3);
  and and_5 (and_5_out, Q_0, Q_1, not_3_out);
  and and_6 (and_6_out, not_1_out, Q_2);
  and and_7 (and_7_out, not_2_out, Q_2);
  and and_8 (and_8_out, Q_0, not_2_out);
  and and_9 (and_9_out, not_1_out, Q_1);
  or or_1 (or_1_out, and_1_out, and_2_out, and_3_out, and_4_out);
  or or_2 (or_2_out, and_5_out, and_6_out, and_7_out);
  or or_3 (or_3_out, and_8_out, and_9_out);
  D_FF #(.Default(1)) q_3_n (.D(or_1_out), .C(C), .Q(Q_3));  // open: nQ
  D_FF #(.Default(1)) q_2_n (.D(or_2_out), .C(C), .Q(Q_2));  // open: nQ
  D_FF #(.Default(1)) q_1_n (.D(or_3_out), .C(C), .Q(Q_1));  // open: nQ
  D_FF q_0_n (.D(not_1_out), .C(C), .Q(Q_0));  // open: nQ

  // Other names for the same wires on the sheet: q_0n = Q_0; q_1n = Q_1; q_2n = Q_2; q_3n = Q_3
endmodule

/* Test case:
           C Q_3 Q_2 Q_1 Q_0
repeat(16) C bits(4,n-1)
C 1 1 1 0
*/
