// Digital circuit Clock.dig as structural Verilog
module Clock (
  input  Clk,
  input  A,
  output Y0
);

  xor xor_1 (Y0, A, Clk);

  // Notes on the sheet:
  //   Y0: pin U16
  //   Clk: pin W5, Hz: 20
  //   A: pin U17
  //   Board: BASYS3
endmodule
