// Digital circuit Clock3.dig as structural Verilog
module Clock3 (
  input  C,
  output OV
);

  not not_1 (OV, C);

  // Notes on the sheet:
  //   OV: pin U18
  //   C: pin W5, Hz: 100000000
  //   Board: BASYS3
endmodule
