// Digital circuit decoder2.dig as structural Verilog
module decoder2 (
  input  [1:0] Sel,
  output A,
  output B,
  output C,
  output D
);

  Decoder #(.Selector_Bits(2)) decoder_1 (.sel(Sel), .out_0(A), .out_1(B), .out_2(C), .out_3(D));
endmodule
