// Digital circuit demux.dig as structural Verilog
module demux (
  input  S,
  input  D,
  output Y,
  output Z
);

  Demultiplexer demultiplexer_1 (.sel(S), .in(D), .out_0(Y), .out_1(Z));
endmodule

/* Test case:
S D Y Z 

 0 0 0 0
 0 1 1 0
 1 0 0 0
 1 1 0 1
*/
