// Digital circuit demux2.dig as structural Verilog
module demux2 (
  input  S,
  input  [7:0] D,
  output [7:0] Y,
  output [7:0] Z
);

  Demultiplexer #(.Bits(8)) demultiplexer_1 (.sel(S), .in(D), .out_0(Y), .out_1(Z));
endmodule
