// Digital circuit demux3.dig as structural Verilog
module demux3 (
  input  [1:0] S,
  input  [7:0] D,
  output [7:0] Y,
  output [7:0] Z,
  output [7:0] U,
  output [7:0] V
);

  Demultiplexer #(.Selector_Bits(2), .Bits(8)) demultiplexer_1 (
    .sel(S), .in(D), .out_0(Y), .out_1(Z), .out_2(U), .out_3(V));
endmodule
