// Digital circuit demux4.dig as structural Verilog
module demux4 (
  input  _2S,
  input  [1:0] _2D,
  input  _3S,
  input  [2:0] _3D,
  output [1:0] _2Y,
  output [1:0] _2Z,
  output [2:0] _3Y,
  output [2:0] _3Z
);

  Demultiplexer #(.Bits(2)) demultiplexer_1 (.sel(_2S), .in(_2D), .out_0(_2Y), .out_1(_2Z));
  Demultiplexer #(.Bits(3)) demultiplexer_2 (.sel(_3S), .in(_3D), .out_0(_3Y), .out_1(_3Z));
endmodule

/* Test case:
2S 2D 3S 3D 2Y 2Z 3Y 3Z 

 0 0b00 0 0b000 0b00 0b00 0b000 0b000
 0 0b00 0 0b001 0b00 0b00 0b001 0b000
 0 0b00 0 0b010 0b00 0b00 0b010 0b000
 0 0b00 0 0b011 0b00 0b00 0b011 0b000
 0 0b00 0 0b100 0b00 0b00 0b100 0b000
 0 0b00 0 0b101 0b00 0b00 0b101 0b000
 0 0b00 0 0b110 0b00 0b00 0b110 0b000
 0 0b00 0 0b111 0b00 0b00 0b111 0b000
 0 0b00 1 0b000 0b00 0b00 0b000 0b000
 0 0b00 1 0b001 0b00 0b00 0b000 0b001
 0 0b00 1 0b010 0b00 0b00 0b000 0b010
 0 0b00 1 0b011 0b00 0b00 0b000 0b011
 0 0b00 1 0b100 0b00 0b00 0b000 0b100
 0 0b00 1 0b101 0b00 0b00 0b000 0b101
 0 0b00 1 0b110 0b00 0b00 0b000 0b110
 0 0b00 1 0b111 0b00 0b00 0b000 0b111
 0 0b01 0 0b000 0b01 0b00 0b000 0b000
 0 0b01 0 0b001 0b01 0b00 0b001 0b000
 0 0b01 0 0b010 0b01 0b00 0b010 0b000
 0 0b01 0 0b011 0b01 0b00 0b011 0b000
 0 0b01 0 0b100 0b01 0b00 0b100 0b000
 0 0b01 0 0b101 0b01 0b00 0b101 0b000
 0 0b01 0 0b110 0b01 0b00 0b110 0b000
 0 0b01 0 0b111 0b01 0b00 0b111 0b000
 0 0b01 1 0b000 0b01 0b00 0b000 0b000
 0 0b01 1 0b001 0b01 0b00 0b000 0b001
 0 0b01 1 0b010 0b01 0b00 0b000 0b010
 0 0b01 1 0b011 0b01 0b00 0b000 0b011
 0 0b01 1 0b100 0b01 0b00 0b000 0b100
 0 0b01 1 0b101 0b01 0b00 0b000 0b101
 0 0b01 1 0b110 0b01 0b00 0b000 0b110
 0 0b01 1 0b111 0b01 0b00 0b000 0b111
 0 0b10 0 0b000 0b10 0b00 0b000 0b000
 0 0b10 0 0b001 0b10 0b00 0b001 0b000
 0 0b10 0 0b010 0b10 0b00 0b010 0b000
 0 0b10 0 0b011 0b10 0b00 0b011 0b000
 0 0b10 0 0b100 0b10 0b00 0b100 0b000
 0 0b10 0 0b101 0b10 0b00 0b101 0b000
 0 0b10 0 0b110 0b10 0b00 0b110 0b000
 0 0b10 0 0b111 0b10 0b00 0b111 0b000
 0 0b10 1 0b000 0b10 0b00 0b000 0b000
 0 0b10 1 0b001 0b10 0b00 0b000 0b001
 0 0b10 1 0b010 0b10 0b00 0b000 0b010
 0 0b10 1 0b011 0b10 0b00 0b000 0b011
 0 0b10 1 0b100 0b10 0b00 0b000 0b100
 0 0b10 1 0b101 0b10 0b00 0b000 0b101
 0 0b10 1 0b110 0b10 0b00 0b000 0b110
 0 0b10 1 0b111 0b10 0b00 0b000 0b111
 0 0b11 0 0b000 0b11 0b00 0b000 0b000
 0 0b11 0 0b001 0b11 0b00 0b001 0b000
 0 0b11 0 0b010 0b11 0b00 0b010 0b000
 0 0b11 0 0b011 0b11 0b00 0b011 0b000
 0 0b11 0 0b100 0b11 0b00 0b100 0b000
 0 0b11 0 0b101 0b11 0b00 0b101 0b000
 0 0b11 0 0b110 0b11 0b00 0b110 0b000
 0 0b11 0 0b111 0b11 0b00 0b111 0b000
 0 0b11 1 0b000 0b11 0b00 0b000 0b000
 0 0b11 1 0b001 0b11 0b00 0b000 0b001
 0 0b11 1 0b010 0b11 0b00 0b000 0b010
 0 0b11 1 0b011 0b11 0b00 0b000 0b011
 0 0b11 1 0b100 0b11 0b00 0b000 0b100
 0 0b11 1 0b101 0b11 0b00 0b000 0b101
 0 0b11 1 0b110 0b11 0b00 0b000 0b110
 0 0b11 1 0b111 0b11 0b00 0b000 0b111
 1 0b00 0 0b000 0b00 0b00 0b000 0b000
 1 0b00 0 0b001 0b00 0b00 0b001 0b000
 1 0b00 0 0b010 0b00 0b00 0b010 0b000
 1 0b00 0 0b011 0b00 0b00 0b011 0b000
 1 0b00 0 0b100 0b00 0b00 0b100 0b000
 1 0b00 0 0b101 0b00 0b00 0b101 0b000
 1 0b00 0 0b110 0b00 0b00 0b110 0b000
 1 0b00 0 0b111 0b00 0b00 0b111 0b000
 1 0b00 1 0b000 0b00 0b00 0b000 0b000
 1 0b00 1 0b001 0b00 0b00 0b000 0b001
 1 0b00 1 0b010 0b00 0b00 0b000 0b010
 1 0b00 1 0b011 0b00 0b00 0b000 0b011
 1 0b00 1 0b100 0b00 0b00 0b000 0b100
 1 0b00 1 0b101 0b00 0b00 0b000 0b101
 1 0b00 1 0b110 0b00 0b00 0b000 0b110
 1 0b00 1 0b111 0b00 0b00 0b000 0b111
 1 0b01 0 0b000 0b00 0b01 0b000 0b000
 1 0b01 0 0b001 0b00 0b01 0b001 0b000
 1 0b01 0 0b010 0b00 0b01 0b010 0b000
 1 0b01 0 0b011 0b00 0b01 0b011 0b000
 1 0b01 0 0b100 0b00 0b01 0b100 0b000
 1 0b01 0 0b101 0b00 0b01 0b101 0b000
 1 0b01 0 0b110 0b00 0b01 0b110 0b000
 1 0b01 0 0b111 0b00 0b01 0b111 0b000
 1 0b01 1 0b000 0b00 0b01 0b000 0b000
 1 0b01 1 0b001 0b00 0b01 0b000 0b001
 1 0b01 1 0b010 0b00 0b01 0b000 0b010
 1 0b01 1 0b011 0b00 0b01 0b000 0b011
 1 0b01 1 0b100 0b00 0b01 0b000 0b100
 1 0b01 1 0b101 0b00 0b01 0b000 0b101
 1 0b01 1 0b110 0b00 0b01 0b000 0b110
 1 0b01 1 0b111 0b00 0b01 0b000 0b111
 1 0b10 0 0b000 0b00 0b10 0b000 0b000
 1 0b10 0 0b001 0b00 0b10 0b001 0b000
 1 0b10 0 0b010 0b00 0b10 0b010 0b000
 1 0b10 0 0b011 0b00 0b10 0b011 0b000
 1 0b10 0 0b100 0b00 0b10 0b100 0b000
 1 0b10 0 0b101 0b00 0b10 0b101 0b000
 1 0b10 0 0b110 0b00 0b10 0b110 0b000
 1 0b10 0 0b111 0b00 0b10 0b111 0b000
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*/
