// Digital circuit demux5.dig as structural Verilog
module demux5 (
  input  [1:0] S,
  input  [2:0] D,
  output [2:0] Y,
  output [2:0] Z,
  output [2:0] U,
  output [2:0] V
);

  Demultiplexer #(.Selector_Bits(2), .Bits(3), .Default(3)) demultiplexer_1 (
    .sel(S), .in(D), .out_0(Y), .out_1(Z), .out_2(U), .out_3(V));
endmodule

/* Test case:
S D Y Z U V 

 0b00 0b000 0b000 0b011 0b011 0b011
 0b00 0b001 0b001 0b011 0b011 0b011
 0b00 0b010 0b010 0b011 0b011 0b011
 0b00 0b011 0b011 0b011 0b011 0b011
 0b00 0b100 0b100 0b011 0b011 0b011
 0b00 0b101 0b101 0b011 0b011 0b011
 0b00 0b110 0b110 0b011 0b011 0b011
 0b00 0b111 0b111 0b011 0b011 0b011
 0b01 0b000 0b011 0b000 0b011 0b011
 0b01 0b001 0b011 0b001 0b011 0b011
 0b01 0b010 0b011 0b010 0b011 0b011
 0b01 0b011 0b011 0b011 0b011 0b011
 0b01 0b100 0b011 0b100 0b011 0b011
 0b01 0b101 0b011 0b101 0b011 0b011
 0b01 0b110 0b011 0b110 0b011 0b011
 0b01 0b111 0b011 0b111 0b011 0b011
 0b10 0b000 0b011 0b011 0b000 0b011
 0b10 0b001 0b011 0b011 0b001 0b011
 0b10 0b010 0b011 0b011 0b010 0b011
 0b10 0b011 0b011 0b011 0b011 0b011
 0b10 0b100 0b011 0b011 0b100 0b011
 0b10 0b101 0b011 0b011 0b101 0b011
 0b10 0b110 0b011 0b011 0b110 0b011
 0b10 0b111 0b011 0b011 0b111 0b011
 0b11 0b000 0b011 0b011 0b011 0b000
 0b11 0b001 0b011 0b011 0b011 0b001
 0b11 0b010 0b011 0b011 0b011 0b010
 0b11 0b011 0b011 0b011 0b011 0b011
 0b11 0b100 0b011 0b011 0b011 0b100
 0b11 0b101 0b011 0b011 0b011 0b101
 0b11 0b110 0b011 0b011 0b011 0b110
 0b11 0b111 0b011 0b011 0b011 0b111
*/
