// Digital circuit demux6.dig as structural Verilog
module demux6 (
  input  [1:0] S,
  input  D,
  output Y,
  output Z,
  output U,
  output V
);

  Demultiplexer #(.Selector_Bits(2), .Default(3)) demultiplexer_1 (
    .sel(S), .in(D), .out_0(Y), .out_1(Z), .out_2(U), .out_3(V));
endmodule

/* Test case:
S D Y Z U V 

 0b00 0 0 1 1 1
 0b00 1 1 1 1 1
 0b01 0 1 0 1 1
 0b01 1 1 1 1 1
 0b10 0 1 1 0 1
 0b10 1 1 1 1 1
 0b11 0 1 1 1 0
 0b11 1 1 1 1 1
*/
