// Digital circuit dff.dig as structural Verilog
module dff (
  input  D,
  input  C,
  input  [2:0] D3,
  output Q,
  output nQ,
  output [2:0] Q3,
  output [2:0] nQ3
);

  D_FF d_ff_1 (.D(D), .C(C), .Q(Q), .nQ(nQ));
  D_FF #(.Bits(3)) d_ff_2 (.D(D3), .C(C), .Q(Q3), .nQ(nQ3));
endmodule
