// Digital circuit JK-Default.dig as structural Verilog
module JK_Default (
  input  C,
  output Q1,
  output Q2
);

  JK_FF jk_ff_1 (.J(1'b1), .C(C), .K(1'b1), .Q(Q1));  // open: nQ
  JK_FF #(.Default(1)) jk_ff_2 (.J(1'b1), .C(C), .K(1'b1), .Q(Q2));  // open: nQ
endmodule

/* Test case:
C Q1 Q2
0 0  1
C 1  0
C 0  1
C 1  0
*/
