// Digital circuit lightChase.dig as structural Verilog
// Ein Addierer der nach den carry-look-ahead 
// Verfahren implementiert ist.
module lightChase (
  input  Clk,
  input  reset,
  output Y0,
  output Y1,
  output Y2,
  output Y3,
  output Y4,
  output Y5,
  output Y6,
  output Y7
);

  wire jk_ff_1_q;
  wire [2:0] add_1_s, d_ff_1_q, multiplexer_1_out, multiplexer_2_out;

  Multiplexer #(.Bits(3)) multiplexer_1 (.sel(jk_ff_1_q), .in_0(3'b001), .in_1(3'b111), .out(multiplexer_1_out));
  Add #(.Bits(3)) add_1 (.a(d_ff_1_q), .b(multiplexer_1_out), .c_i(1'b0), .s(add_1_s));  // open: c_o
  Multiplexer #(.Bits(3)) multiplexer_2 (.sel(reset), .in_0(add_1_s), .in_1(3'b000), .out(multiplexer_2_out));
  D_FF #(.Bits(3)) d_ff_1 (.D(multiplexer_2_out), .C(Clk), .Q(d_ff_1_q));  // open: nQ
  Decoder #(.Selector_Bits(3)) decoder_1 (
    .sel(d_ff_1_q), .out_0(Y0), .out_1(Y1), .out_2(Y2), .out_3(Y3), .out_4(Y4), .out_5(Y5), .out_6(Y6),
    .out_7(Y7));
  JK_FF jk_ff_1 (.J(Y6), .C(Clk), .K(Y1), .Q(jk_ff_1_q));  // open: nQ

  // Notes on the sheet:
  //   Clk: Hz: 20
endmodule

/* Test case:
          reset Clk Y7 Y6 Y5 Y4 Y3 Y2 Y1 Y0
           1     C  0  0  0  0  0  0  0  1
repeat(7)  0     C  bits(8, 1<<(n+1))
repeat(7)  0     C  bits(8, 1<<(6-n))
repeat(7)  0     C  bits(8, 1<<(n+1))
repeat(7)  0     C  bits(8, 1<<(6-n))
*/
