// Digital circuit clock_mimasv1.dig as structural Verilog
module clock_mimasv1 (
  input  A,
  input  C,
  output X
);

  D_FF d_ff_1 (.D(A), .C(C), .Q(X));  // open: nQ

  // Notes on the sheet:
  //   A: pin P124
  //   C: pin P126, Hz: 1000000
  //   X: pin P119
  //   Board: MimasV1
endmodule
