// Digital circuit comb.dig as structural Verilog
module comb (
  input  A,
  input  B,
  input  C,
  output X,
  output Y,
  output Z,
  output Aident
);

  wire and_1_out, nor_1_out, not_2_out, or_1_out, or_2_out;

  not not_1 (Z, A);
  not not_2 (not_2_out, C);
  or or_1 (or_1_out, A, C);
  or or_2 (or_2_out, Z, C);
  nor nor_1 (nor_1_out, B, C);
  or or_3 (Y, B, not_2_out);
  and and_1 (and_1_out, or_1_out, or_2_out, 1'b1, nor_1_out, Y);
  D_FF d_ff_1 (.D(and_1_out), .C(1'b1), .Q(X));  // open: nQ

  assign Aident = A;
endmodule
