// Digital circuit combBits.dig as structural Verilog
module combBits (
  input  [1:0] A,
  input  [1:0] B,
  input  [1:0] C,
  output [1:0] X,
  output [1:0] Y,
  output [1:0] Z,
  output [1:0] Aident
);

  wire [1:0] and_1_out, nor_1_out, not_2_out, or_1_out, or_2_out;

  assign Z = ~A;  // Not not_1, 2 bits wide
  assign not_2_out = ~C;  // Not not_2, 2 bits wide
  assign or_1_out = A | C;  // Or or_1, 2 bits wide
  assign or_2_out = Z | C;  // Or or_2, 2 bits wide
  assign nor_1_out = ~(B | C);  // NOr nor_1, 2 bits wide
  assign Y = B | not_2_out;  // Or or_3, 2 bits wide
  assign and_1_out = or_1_out & or_2_out & 2'b01 & nor_1_out & Y;  // And and_1, 2 bits wide
  D_FF #(.Bits(2)) d_ff_1 (.D(and_1_out), .C(1'b1), .Q(X));  // open: nQ

  assign Aident = A;
endmodule
