// Digital circuit constMerge.dig as structural Verilog
module constMerge (
  input  A,
  input  B,
  output [1:0] Y,
  output X,
  output [1:0] Z
);

  D_FF d_ff_1 (.D(A), .C(1'b1), .Q(X));  // open: nQ
  D_FF #(.Bits(2)) d_ff_2 (.D(2'b01), .C(B), .Q(Y));  // open: nQ
  Counter #(.Bits(2)) counter_1 (.en(1'b1), .C(1'b1), .clr(1'b0), .out(Z));  // open: ovf
endmodule
