// Digital circuit freqHalf.dig as structural Verilog
module freqHalf (
  input  C,
  output Y
);

  wire d_ff_1_nq;

  D_FF d_ff_1 (.D(d_ff_1_nq), .C(C), .Q(Y), .nQ(d_ff_1_nq));
endmodule

/* Test case:
C Y
C 1
C 0
C 1
C 0
*/
