// Digital circuit inputInvert3.dig as structural Verilog
module inputInvert3 (
  input  D,
  input  C,
  output Y
);

  D_FF d_ff_1 (.D(~D), .C(C), .Q(Y));  // open: nQ
endmodule

/* Test case:
C D Y
0 0 0
1 0 1
0 0 1
1 0 1
0 1 1
1 1 0
*/
