// Digital circuit inputInvert4.dig as structural Verilog
module inputInvert4 (
  input  [1:0] D,
  input  C,
  output [1:0] Y
);

  D_FF #(.Bits(2)) d_ff_1 (.D(~D), .C(C), .Q(Y));  // open: nQ
endmodule

/* Test case:
C D Y
0 0 0
1 0 3
0 0 3
1 0 3
0 1 3
1 1 2
0 0 2
1 0 3
*/
