// Digital circuit inputInvert5.dig as structural Verilog
module inputInvert5 (
  input  D,
  input  C,
  input  Set,
  input  Clr,
  output Q,
  output nQ
);

  D_FF_AS d_ff_as_1 (.Set(~Set), .D(D), .C(C), .Clr(~Clr), .Q(Q), .nQ(nQ));
endmodule

/* Test case:
C D Set Clr Q nQ
C 0  1   1  0  1
C 1  1   1  1  0
C 0  1   1  0  1
0 0  1   1  0  1
0 0  0   1  1  0
0 0  1   1  1  0
0 0  1   0  0  1
0 0  1   1  0  1
*/
