// Digital circuit naming.dig as structural Verilog
module naming (
  input  S0,
  input  S1,
  output S2,
  output S3
);

  wire nor_1_out;

  nor nor_1 (nor_1_out, S0, S1);
  xor xor_1 (S2, S0, nor_1_out);
  xor xor_2 (S3, nor_1_out, S1);
endmodule

/* Test case:
S0 S1 S2 S3
0  0  1  1
0  1  0  1
1  0  1  0
1  1  1  1
*/
