// Digital circuit splitter.dig as structural Verilog
module splitter (
  input  [3:0] A,
  output [1:0] X
);

  assign X = A[1:0] & ~A[3:2];  // And and_1, 2 bits wide
endmodule

/* Test case:
 A  X
 0  0
 1  1
 2  2
 3  3
 4  0
 5  0
 6  2
 7  2
 8  0
 9  1
10  0
11  1
12  0
13  0
14  0
15  0
*/
