// Digital circuit splitter2.dig as structural Verilog
module splitter2 (
  input  [1:0] A,
  input  [1:0] B,
  output X,
  output [2:0] Y
);


  assign X = A[0];
  assign Y = {B, A[1]};
endmodule

/* Test case:
A B X Y

loop(a,4)
loop(b,4)
(a) (b) (a&1) ((a>>1)|(b<<1))
end loop
end loop
*/
