// Digital circuit splitter3.dig as structural Verilog
module splitter3 (
  input  [3:0] A,
  input  [3:0] B,
  output [3:0] S
);

  assign S[1:0] = A[1:0] & B[1:0];  // And and_1, 2 bits wide
  assign S[3:2] = A[3:2] | B[3:2];  // Or or_1, 2 bits wide
endmodule

/* Test case:
A B S
loop(a,16)
loop(b,16)
(a) (b) (((a&b)&3) | ((a|b)&12))
end loop
end loop
*/
