// Digital circuit mux2.dig as structural Verilog
module mux2 (
  input  A,
  input  B,
  input  [1:0] Sel,
  input  C,
  input  D,
  output Y
);

  Multiplexer #(.Selector_Bits(2)) multiplexer_1 (.sel(Sel), .in_0(A), .in_1(B), .in_2(C), .in_3(D), .out(Y));
endmodule
