// Digital circuit mux3.dig as structural Verilog
module mux3 (
  input  [3:0] A,
  input  [3:0] B,
  input  [1:0] Sel,
  input  [3:0] C,
  input  [3:0] D,
  output [3:0] Y
);

  Multiplexer #(.Selector_Bits(2), .Bits(4)) multiplexer_1 (.sel(Sel), .in_0(A), .in_1(B), .in_2(C), .in_3(D), .out(Y));
endmodule
