// Digital circuit readOutput.dig as structural Verilog
// Extrahiert kleine Konstanten aus dem Befehlswort.
// Es können zwei 5-Bit Konstanten (Die 4 Bits eines 
// Registers zusammen mit Bit 8 des Befehlswortes)
// und eine 9-Bit Konstante (Die 8 Bits beider Register
// zusammen mit Bit 8 des Befehlswortes)
module readOutput (
  input  A,
  input  B,
  output Y,
  output Z
);

  and and_1 (Y, A, B);
  not not_1 (Z, Y);

  // Notes on the sheet:
  //   A: Das Befehlswort
  //   B: Das Befehlswort
endmodule
