// Digital circuit splitter.dig as structural Verilog
module splitter (
  input  [3:0] A,
  input  [3:0] B,
  output [2:0] Y,
  output [4:0] Z
);


  assign Y = A[2:0];
  assign Z = {B, A[3]};
endmodule
