// Digital circuit splitter2.dig as structural Verilog
// Extrahiert kleine Konstanten aus dem Befehlswort.
// Es können zwei 5-Bit Konstanten (Die 4 Bits eines 
// Registers zusammen mit Bit 8 des Befehlswortes)
// und eine 9-Bit Konstante (Die 8 Bits beider Register
// zusammen mit Bit 8 des Befehlswortes)
module splitter2 (
  input  [15:0] inst,
  output [15:0] _9SD
);


  assign _9SD = {{8{inst[8]}}, inst[7:0]};

  // Notes on the sheet:
  //   inst: Das Befehlswort
  //   _9SD: Die neun Bit aus Rs,Rd und Bit 8
endmodule
