// Digital circuit splitter3.dig as structural Verilog
// Extrahiert kleine Konstanten aus dem Befehlswort.
// Es können zwei 5-Bit Konstanten (Die 4 Bits eines 
// Registers zusammen mit Bit 8 des Befehlswortes)
// und eine 9-Bit Konstante (Die 8 Bits beider Register
// zusammen mit Bit 8 des Befehlswortes)
module splitter3 (
  input  [3:0] A,
  input  [3:0] B,
  output [7:0] Y,
  output [7:0] Z
);

  assign Z = ~{B, A};  // Not not_1, 8 bits wide

  assign Y = {B, A};

  // Notes on the sheet:
  //   A: Das Befehlswort
  //   B: Das Befehlswort
endmodule
