// Digital circuit xorNeg.dig as structural Verilog
module xorNeg (
  input  A,
  input  B,
  output Y
);

  wire and_1_out, and_2_out;

  and and_1 (and_1_out, ~A, B);  // And
  and and_2 (and_2_out, A, ~B);  // And
  or or_1 (Y, and_1_out, and_2_out);
endmodule
