// Digital circuit xorNegBus.dig as structural Verilog
module xorNegBus (
  input  [1:0] A,
  input  [1:0] B,
  output [1:0] Y
);

  wire [1:0] and_1_out, and_2_out;

  assign and_1_out = ~A & B;  // And and_1, 2 bits wide
  assign and_2_out = A & ~B;  // And and_2, 2 bits wide
  assign Y = and_1_out | and_2_out;  // Or or_1, 2 bits wide
endmodule
