// Digital circuit skipOuter.dig as structural Verilog
module skipOuter (
  input  A,
  input  B,
  output Y
);

  wire skipinner_1_o;

  skipInner skipinner_1 (.i(B), .o(skipinner_1_o));
  and and_1 (Y, A, skipinner_1_o);
endmodule
