// Digital circuit keyboard2.dig as structural Verilog
module keyboard2 (
  input  clk,
  output [15:0] akt
);

  wire keyboard_1_av;

  Keyboard keyboard_1 (.C(clk), .en(keyboard_1_av), .D(akt), .av(keyboard_1_av));
  Terminal terminal_1 (.D(akt), .C(clk), .en(keyboard_1_av));

  // Notes on the sheet:
  //   clk: Hz: 2147483647
endmodule
