// Digital circuit jarLibTest.dig as structural Verilog
module jarLibTest (
  input  A,
  input  B,
  output AND,
  output OR
);

  // MyAnd myand_1: pin names not known; wires that end beside it: A, B, AND
  // MyOr myor_1: pin names not known; wires that end beside it: A, B, OR
endmodule

/* Test case:
A B AND OR
0 0  0  0
0 1  0  1
1 0  0  1
1 1  1  1
*/
