// Digital circuit 01_fastRuntime.dig as structural Verilog
module _01_fastRuntime (
  input  clk
);

  wire counter_1_ovf, driver_1_out;

  Counter #(.Bits(10)) counter_1 (.en(1'b1), .C(clk), .clr(1'b0), .ovf(counter_1_ovf));  // open: out
  assign driver_1_out = counter_1_ovf ? 1'b1 : 1'bz;  // Driver driver_1
  // also tied to GND on the sheet: driver_1_out

  // Notes on the sheet:
  //   clk: Hz: 500000
  //   Shows a runtime error.
  //   The output wire of the 
  //   driver is colored red.
endmodule
