// Digital circuit 02_fastRuntimeEmbed.dig as structural Verilog
module _02_fastRuntimeEmbed (
  input  clk
);

  wire counter_1_ovf;

  Counter #(.Bits(10)) counter_1 (.en(1'b1), .C(clk), .clr(1'b0), .ovf(counter_1_ovf));  // open: out
  short short_1 (.S(counter_1_ovf));

  // Notes on the sheet:
  //   clk: Hz: 500000
  //   Shows a runtime error.
  //   The name "short.dig" is 
  //   given in the error message.
endmodule
