// Digital circuit 04_testExecution.dig as structural Verilog
module _04_testExecution (
  input  A,
  input  B,
  output Y
);

  wire driver_1_out;

  and and_1 (Y, A, B);
  assign driver_1_out = Y ? 1'b1 : 1'bz;  // Driver driver_1
  // also tied to GND on the sheet: driver_1_out

  // Notes on the sheet:
  //   Shows a runtime error
  //   during test execution.
endmodule

/* Test case:
A B Y
0 0 0 
0 1 0 
1 0 0 
1 1 1 
*/
