// Digital circuit 05_runToBreak.dig as structural Verilog
module _05_runToBreak (
  input  clk
);

  wire counter_1_ovf, driver_1_out;
  wire [7:0] counter_1_out;

  Counter #(.Bits(8)) counter_1 (.en(1'b1), .C(clk), .clr(1'b0), .out(counter_1_out), .ovf(counter_1_ovf));
  Break break_1 (.brk(counter_1_ovf));
  assign driver_1_out = counter_1_out[7] ? 1'b1 : 1'bz;  // Driver driver_1
  // also tied to GND on the sheet: driver_1_out

  // Notes on the sheet:
  //   clk: Hz: 500000
  //   Shows a runtime error
  //   during "run to break".
endmodule
