// Digital circuit 06_initPhase.dig as structural Verilog
module _06_initPhase (
  input  A,
  output Y
);

  wire delay_1_out, delay_2_out, driver_1_out, not_1_out;

  not not_1 (not_1_out, A);
  Delay delay_1 (.in(delay_2_out), .out(delay_1_out));
  Delay delay_2 (.in(not_1_out), .out(delay_2_out));
  Delay delay_3 (.in(delay_1_out), .out(Y));
  assign driver_1_out = Y ? 1'b1 : 1'bz;  // Driver driver_1
  // also tied to GND on the sheet: driver_1_out

  // Notes on the sheet:
  //   Shows a runtime error
  //   during init phase.
endmodule
