// Digital circuit 09_analysis.dig as structural Verilog
module _09_analysis (
  input  A,
  input  B,
  input  C,
  output Y
);

  wire not_1_out, not_2_out, or_1_out, or_2_out, or_3_out, or_4_out;

  not not_1 (not_1_out, A);
  not not_2 (not_2_out, C);
  or or_1 (or_1_out, A, C);
  or or_2 (or_2_out, not_1_out, C);
  or or_3 (or_3_out, B, C);
  or or_4 (or_4_out, B, not_2_out);
  and and_1 (Y, or_1_out, or_2_out, or_3_out, or_4_out);
endmodule
