// Digital circuit 15_romDataEditor.dig as structural Verilog
module _15_romDataEditor (
  input  [2:0] A,
  output [2:0] Y
);

  ROM #(.AddrBits(3), .Bits(3)) rom_1 (.A(A), .sel(1'b1), .D(Y));
endmodule

/* Test case:
A Y
0 7
1 6
2 5
3 4
4 3 
5 2
6 1
7 0
*/
