// Digital circuit short.dig as structural Verilog
module short (
  input  S
);

  wire driver_1_out;

  assign driver_1_out = S ? 1'b1 : 1'bz;  // Driver driver_1
  // also tied to GND on the sheet: driver_1_out
endmodule
