// Digital circuit nestedMSFF.dig as structural Verilog
module nestedMSFF (
  input  in_1,
  input  in_2,
  input  in_4,
  output out_3
);

  // MS_JK ms_jk_1: pin names not known; wires that end beside it: in_2, in_1, in_4, out_3
endmodule
