// Digital circuit nestedNestedAnd.dig as structural Verilog
module nestedNestedAnd (
  input  in_1,
  input  in_2,
  output out_3
);

  nestedAnd nestedand_1 (.A(in_1), .B(in_2), .C(out_3));
endmodule
