// Digital circuit netRename.dig as structural Verilog
module netRename (
  input  A,
  output Y,
  output X
);

  not not_1 (X, A);

  assign Y = A;

  // Other names for the same wires on the sheet: n = A
endmodule

/* Test case:
A Y X
0 0 1
1 1 0
*/
