// Digital circuit probeNest.dig as structural Verilog
module probeNest (
  input  A,
  input  B,
  output Y
);

  wire Nest_p3, not_1_out, Probe1_y;

  not not_1 (not_1_out, B);
  pr1 Probe1 (.A(A), .B(B), .Y(Probe1_y));
  // probe Nest: pin names not known; wires that end beside it: A, not_1_out, Nest_p3
  xor xor_1 (Y, Probe1_y, Nest_p3);
endmodule
