// Digital circuit Processor_fibonacci.dig as structural Verilog
module Processor_fibonacci (
  input  Clock
);

  wire abs, ALU2D, alu_1_carry, alu_1_neg, alu_1_zero, branch_1_jmp, flags_1_co, flags_1_no, flags_1_zo,
       gpo_1_p1, gpo_1_p2, gpo_1_p3, gpo_1_p4, gpo_1_p5, gpo_1_p6, gpo_1_p7, gpo_1_p8, gpo_1_p9, gpo_1_p10,
       gpo_1_p11, gpo_1_p12, gpo_1_p14, gpo_1_p16, gpo_1_p18, gpo_1_p20, imm, ioR, ioW, ld, muxA, sf, src2D,
       st, stPC, WE;
  wire [2:0] br, muxB;
  wire [4:0] ALUop;
  wire [15:0] alu_1_y, driver_1_out, imreg_1_imm, multiplexer_1_out, multiplexer_2_out, pc_1_next, pc_1_pc,
       register_1_rdest, register_1_rsrc, rom_1_d, signext_1__5d, signext_1__5s, signext_1__9sd;

  PC pc_1 (.ALU(alu_1_y), .C(Clock), .abs(abs), .rel(branch_1_jmp), .Next(pc_1_next), .PC(pc_1_pc));
  ROM #(.Bits(16), .Addr_Bits(16)) rom_1 (.A(pc_1_pc), .sel(1'b1), .D(rom_1_d));
  assign driver_1_out = stPC ? pc_1_next : 16'bz;  // Driver driver_1
  Control control_1 (
    .Op(rom_1_d[15:9]), .stPC(stPC), .WE(WE), .imm(imm), .absJmp(abs), .muxB(muxB), .srcToD(src2D),
    .muxA(muxA), .ALUToBus(ALU2D), .ALUop(ALUop), .storeFlags(sf), .Branch(br), .st(st), .ld(ld), .ioW(ioW),
    .ioR(ioR));
  Register register_1 (
    .WD(driver_1_out), .C(Clock), .src(rom_1_d[3:0]), .dest(rom_1_d[7:4]), .WE(WE), .Rdest(register_1_rdest),
    .Rsrc(register_1_rsrc));
  ImReg imreg_1 (.inst(rom_1_d), .en(imm), .C(Clock), .imm(imreg_1_imm));
  SignExt signext_1 (.inst(rom_1_d), ._5S(signext_1__5s), ._9SD(signext_1__9sd), ._5D(signext_1__5d));
  assign driver_1_out = src2D ? register_1_rsrc : 16'bz;  // Driver driver_2
  Multiplexer #(.Bits(16)) multiplexer_1 (
    .sel(muxA), .in_0(register_1_rdest), .in_1(register_1_rsrc), .out(multiplexer_1_out));
  Multiplexer #(.Selector_Bits(3), .Bits(16)) multiplexer_2 (
    .sel(muxB), .in_0(register_1_rsrc), .in_1(imreg_1_imm), .in_2({16{1'b0}}), .in_3(16'hff), .in_4(16'hfff),
    .in_5(signext_1__5s), .in_6(signext_1__9sd), .in_7(signext_1__5d), .out(multiplexer_2_out));
  LED led_1 (.in(gpo_1_p1));
  LED led_2 (.in(gpo_1_p3));
  LED led_3 (.in(gpo_1_p2));
  Branch branch_1 (.Z(flags_1_zo), .N(flags_1_no), .C(flags_1_co), .ctrl(br), .jmp(branch_1_jmp));
  LED led_4 (.in(gpo_1_p5));
  LED led_5 (.in(gpo_1_p4));
  ALU alu_1 (
    .A(multiplexer_1_out), .B(multiplexer_2_out), .Op(ALUop), .C(flags_1_co), .Y(alu_1_y), .Zero(alu_1_zero),
    .Neg(alu_1_neg), .Carry(alu_1_carry));
  LED led_6 (.in(gpo_1_p7));
  LED led_7 (.in(gpo_1_p6));
  Flags flags_1 (
    .Zi(alu_1_zero), .Ni(alu_1_neg), .Ci(alu_1_carry), .C(Clock), .store(sf), .Zo(flags_1_zo),
    .No(flags_1_no), .Co(flags_1_co));
  LED led_8 (.in(gpo_1_p9));
  LED led_9 (.in(gpo_1_p8));
  assign driver_1_out = ALU2D ? alu_1_y : 16'bz;  // Driver driver_3
  LED led_10 (.in(gpo_1_p11));
  LED led_11 (.in(gpo_1_p10));
  // GPO gpo_1: pin names not known; wires that end beside it: gpo_1_p1, gpo_1_p2, gpo_1_p3, gpo_1_p4, gpo_1_p5, gpo_1_p6, gpo_1_p7, gpo_1_p8, gpo_1_p9, gpo_1_p10, gpo_1_p11, gpo_1_p12, ioW, gpo_1_p14, Clock, gpo_1_p16, alu_1_y, gpo_1_p18, driver_1_out, gpo_1_p20
  LED led_12 (.in(gpo_1_p14));
  LED led_13 (.in(gpo_1_p12));
  RAMSinglePort #(.Bits(16), .Addr_Bits(16)) ramsingleport_1 (
    .A(alu_1_y), .str(st), .C(Clock), .ld(ld), .D(driver_1_out));
  Terminal terminal_1 (.D(driver_1_out), .A(alu_1_y), .C(Clock), .W(ioW));
  LED led_14 (.in(gpo_1_p18));
  LED led_15 (.in(gpo_1_p16));
  LED led_16 (.in(gpo_1_p20));

  // Other names for the same wires on the sheet: C = Clock

  // Notes on the sheet:
  //   Clock: Hz: 50
  //   contents of rom_1 (hex, n*v repeats v):
  //   46
  //   5135
  //   8417
  //   19680
  //   8417
  //   5367
  //   19695
  //   28163
  //   20992
  //   31744
  //   28662
  //   8417
  //   19693
  //   734
  //   8417
  //   32770
  //   23053
  //   15362
  //   23574
  //   8193
  //   8417
  //   19680
  //   8417
  //   5625
  //   19695
  //   28657
  //   65535
  //   22992
  //   32770
  //   23053
  //   8194
  //   8417
  //   19680
  //   8417
  //   32805
  //   4848
  //   19695
  //   28645
  //   65535
  //   23325
  //   1025
  //   749
  //   20190
  //   6369
  //   20222
  //   6370
  //   27151
  //   16
endmodule
