// Digital circuit Terminal.dig as structural Verilog
// Terminal
module Terminal (
  input  [15:0] A,
  input  [15:0] D,
  input  C,
  input  W
);

  wire and_1_out, comparator_1_eq;

  Comparator #(.Bits(16)) comparator_1 (.a(A), .b(16'h1f), .eq(comparator_1_eq));  // open: gt, lt
  and and_1 (and_1_out, comparator_1_eq, C, W);
  Terminal Terminal (.D(D), .C(and_1_out));  // open: en

  // Notes on the sheet:
  //   A: Addressbus
  //   D: Datenbus
  //   C: Takt
  //   W: Write Enable
endmodule
