// Digital circuit measure.dig as structural Verilog
module measure (
  input  C,
  output Q
);

  JK_FF jk_ff_1 (.J(1'b1), .C(C), .K(1'b1), .Q(Q));  // open: nQ
  ROM #(.isProgramMemory("true")) rom_1 (.A(2'b00), .sel(1'b0));  // open: D
endmodule
