// Digital circuit runToBreak.dig as structural Verilog
module runToBreak (
  input  clk
);

  wire counter_1_ovf;

  Counter #(.Bits(8)) counter_1 (.en(1'b1), .C(clk), .clr(1'b0), .ovf(counter_1_ovf));  // open: out
  Break break_1 (.brk(counter_1_ovf));
endmodule
