// Digital circuit selectOuter.dig as structural Verilog
module selectOuter (
  input  in_1,
  input  in_2,
  output Out
);

  selectInnerLongName selectinnerlongname_1 (.A(in_1), .B(in_2), .Out(Out));
endmodule
