// Digital circuit setStateToTestResult.dig as structural Verilog
module setStateToTestResult (
  input  [7:0] A,
  input  [7:0] B,
  input  C,
  output [7:0] S,
  output O
);

  wire add_1_c_o, comparator_1_eq, comparator_2_eq, nand_1_out;

  Add #(.Bits(8)) add_1 (.a(A), .b(B), .c_i(C), .s(S), .c_o(add_1_c_o));
  Comparator #(.Bits(8)) comparator_1 (.a(A), .b({8{1'b1}}), .eq(comparator_1_eq));  // open: gt, lt
  Comparator #(.Bits(8)) comparator_2 (.a(B), .b({8{1'b1}}), .eq(comparator_2_eq));  // open: gt, lt
  and and_1 (O, add_1_c_o, nand_1_out);
  nand nand_1 (nand_1_out, comparator_1_eq, comparator_2_eq);
endmodule

/* Test case:
A B C O S

loop (a,256)
loop (b,256)
loop (c,2)
let sum=a+b+c;
(a) (b) (c) (sum>>8) (sum)
end loop
end loop
end loop
*/
