// Digital circuit shapes.dig as structural Verilog
module shapes (
  input  in_1,
  input  clk,
  output out_2
);

  wire relay_1_p2, rotencoder_1_p1, rotencoder_1_p2;

  // And and_1 is placed but not wired
  Register register_1 ();  // open: D, C, en, Q
  Add add_1 ();  // open: a, b, c_i, s, c_o
  // NAnd nand_1 is placed but not wired
  ROM rom_1 ();  // open: A, sel, D
  LED led_1 ();  // open: in
  RAMDualPort ramdualport_1 ();  // open: A, Din, str, C, ld, D
  Sub sub_1 ();  // open: a, b, c_i, s, c_o
  // Or or_1 is placed but not wired
  Delay delay_1 ();  // open: in, out
  Mul mul_1 ();  // open: a, b, mul
  // NOr nor_1 is placed but not wired
  Button button_1 ();  // open: out
  // Probe MW on nothing
  Driver driver_1 ();  // open: in, en, out
  RAMSinglePort ramsingleport_1 ();  // open: A, str, C, ld, D
  Seven_Seg seven_seg_1 ();  // open: a, b, c, d, e, f, g, dp
  Driver driver_2 ();  // open: in, en, out
  Counter counter_1 ();  // open: en, C, clr, out, ovf
  Comparator comparator_1 ();  // open: a, b, gt, eq, lt
  // XOr xor_1 is placed but not wired
  Seven_Seg_Hex seven_seg_hex_1 ();  // open: d, dp
  Reset reset_1 ();  // open: out
  Neg neg_1 ();  // open: in, out
  // XNOr xnor_1 is placed but not wired
  Break break_1 ();  // open: brk
  GraphicCard graphiccard_1 ();  // open: A, str, C, ld, B, D
  // Not not_1 is placed but not wired
  RAMSinglePortSel ramsingleportsel_1 ();  // open: A, CS, WE, OE, D
  BitCount bitcount_1 ();  // open: in, out
  LookUpTable lookuptable_1 ();  // open: in0, in1, out
  Terminal terminal_1 ();  // open: D, C, en
  Keyboard keyboard_1 ();  // open: C, en, D, av
  DriverInvSel driverinvsel_1 ();  // open: in, en, out
  Switch switch_1 ();  // open: A, B
  // Relay relay_1: pin names not known; wires that end beside it: 1'b0, relay_1_p2, 1'b1
  DriverInvSel driverinvsel_2 ();  // open: in, en, out
  NFET nfet_1 ();  // open: G, D, S
  FGNFET fgnfet_1 ();  // open: G, D, S
  TransGate transgate_1 ();  // open: A, nA, out1, out2
  // RotEncoder rotencoder_1: pin names not known; wires that end beside it: rotencoder_1_p1, rotencoder_1_p2
  PFET pfet_1 ();  // open: G, S, D
  FGPFET fgpfet_1 ();  // open: G, S, D
  Multiplexer multiplexer_1 ();  // open: sel, in_0, in_1, out
  RS_FF rs_ff_1 ();  // open: S, C, R, Q, nQ
  DiodeForward diodeforward_1 ();  // open: in, out
  Demultiplexer demultiplexer_1 ();  // open: sel, in, out_0, out_1
  JK_FF jk_ff_1 ();  // open: J, C, K, Q, nQ
  DiodeBackward diodebackward_1 ();  // open: in, out
  Decoder decoder_1 ();  // open: sel, out_0, out_1
  PullDown pulldown_1 (.out(rotencoder_1_p2));
  PullUp pullup_1 (.out(rotencoder_1_p1));
  D_FF d_ff_1 ();  // open: D, C, Q, nQ
  T_FF t_ff_1 ();  // open: T, C, Q, nQ
endmodule
