// Digital circuit 74181-74182.dig as structural Verilog
module _74181_74182 (
  input  M,
  input  [3:0] S,
  input  [15:0] A,
  input  [15:0] B,
  input  C,
  output [16:0] F
);

  wire _74181_1_p16, _74181_1_p17, _74181_2_p2, _74181_2_p17, _74181_2_p18, _74181_3_p2, _74181_3_p17,
       _74181_3_p18, _74181_4_p2, _74181_4_p18, _74181_4_p19, _74181_4_p24, not_1_out;

  not not_1 (not_1_out, C);
  // _74181 _74181_1: pin names not known; wires that end beside it: not_1_out, A[0], A[1], A[2], A[3], B[0], B[1], B[2], B[3], S[0], S[1], S[2], S[3], M, 1'b1, _74181_1_p16, _74181_1_p17, F[0], F[1], F[2], F[3]
  // _74181 _74181_2: pin names not known; wires that end beside it: 1'b0, _74181_2_p2, A[4], A[5], A[6], A[7], B[4], B[5], B[6], B[7], S[0], S[1], S[2], S[3], M, 1'b1, _74181_2_p17, _74181_2_p18, F[4], F[5], F[6], F[7]
  // _74181 _74181_3: pin names not known; wires that end beside it: 1'b0, _74181_3_p2, A[8], A[9], A[10], A[11], B[8], B[9], B[10], B[11], S[0], S[1], S[2], S[3], M, 1'b1, _74181_3_p17, _74181_3_p18, F[8], F[9], F[10], F[11]
  // _74181 _74181_4: pin names not known; wires that end beside it: 1'b0, _74181_4_p2, A[12], A[13], A[14], A[15], B[12], B[13], B[14], B[15], S[0], S[1], S[2], S[3], M, 1'b1, 1'b0, _74181_4_p18, _74181_4_p19, F[12], F[13], F[14], F[15], _74181_4_p24
  // _74182 _74182_1: pin names not known; wires that end beside it: not_1_out, _74181_1_p16, _74181_1_p17, _74181_2_p17, _74181_2_p18, _74181_3_p17, _74181_3_p18, _74181_4_p18, _74181_4_p19, 1'b1, 1'b0, _74181_4_p2, _74181_3_p2, _74181_2_p2
  not not_2 (F[16], _74181_4_p24);

  // Notes on the sheet:
  //   S: default 9
  //   16-Bit adder with four 74181 alu's
  //   and a 74182 carry generator
endmodule

/* Test case:
A B S M F

0xffff 1 9 0 0x10000

loop (n,1<<16)
let a = random(1<<16);
let b = random(1<<16);
(a) (b) 9 0 (a+b)
end loop
*/
