// Digital circuit AntiparallelDiodes.dig as structural Verilog
// Test of diodes connected antiparallel.
module AntiparallelDiodes (
  input  A,
  output Y
);

  // DiodeForeward diodeforeward_1: pin names not known; wires that end beside it: A, Y
  DiodeBackward diodebackward_1 (.in(A), .out(Y));

  // Notes on the sheet:
  //   A: Driving input
endmodule

/* Test case:
A Y
0 0
1 1
z z
0 0
z z
1 1
0 0
*/
