// Digital circuit BusSplitterError.dig as structural Verilog
module BusSplitterError (
  input  [7:0] in_1,
  input  in_2,
  input  [7:0] in_3,
  input  in_4,
  input  in_5
);

  wire [7:0] driver_1_out;

  assign driver_1_out = in_2 ? in_1 : 8'bz;  // Driver driver_1
  assign driver_1_out = in_4 ? in_3 : 8'bz;  // Driver driver_2
endmodule
