// Digital circuit maskedRAM.dig as structural Verilog
module maskedRAM (
  input  [7:0] A,
  input  [31:0] Din,
  input  str,
  input  C,
  input  ld,
  input  [3:0] mask,
  output [31:0] D
);

  // RAMDualPortMasked #(.AddrBits(8), .Bits(32)) ramdualportmasked_1: pin names not known; wires that end beside it: A, Din, str, C, ld, mask, D
endmodule

/* Test case:
C A Din        str ld  mask   D

# no write at all, mask is zero
C 0 0xffffffff  1   0  0b0000 x
0 0 0           0   1  0b0000 0

# write bytes

C 0 0xffffffff  1   0  0b0001 x
0 0 0           0   1  0b0000 0xff

C 0 0xffffff00  1   0  0b0010 x
0 0 0           0   1  0b0000 0xffff

C 0 0xffff0000  1   0  0b0100 x
0 0 0           0   1  0b0000 0xffffff

C 0 0xff000000  1   0  0b1000 x
0 0 0           0   1  0b0000 0xffffffff

# write 16 bit words

C 1 0xffff      1   0  0b0011 x
0 1 0           0   1  0b0000  0xffff

C 1 0xffff0000  1   0  0b1100 x
0 1 0           0   1  0b0000 0xffffffff

C 1 0xaaaa00    1   0  0b0110 x
0 1 0           0   1  0b0000 0xffaaaaff

# write 32 bit words

C 2 0xffffffff  1   0  0b1111 x
0 2 0           0   1  0b0000  0xffffffff
*/
