// Digital circuit maskedRAM64.dig as structural Verilog
module maskedRAM64 (
  input  [7:0] A,
  input  [63:0] Din,
  input  str,
  input  C,
  input  ld,
  input  [7:0] mask,
  output [63:0] D
);

  // RAMDualPortMasked #(.AddrBits(8), .Bits(64)) ramdualportmasked_1: pin names not known; wires that end beside it: A, Din, str, C, ld, mask, D
endmodule

/* Test case:
C A Din        str ld  mask   D

# no write at all, mask is zero
C 0 0xffffffffffffffff  1   0  0b00000000 x
0 0 0                   0   1  0b00000000 0

# write bytes

C 0 0xffffffffffffffff  1   0  0b00000001 x
0 0 0                   0   1  0b00000000 0xff

C 0 0xffffffffffffff00  1   0  0b00000010 x
0 0 0                   0   1  0b00000000 0xffff

C 0 0xffffffffffff0000  1   0  0b00000100 x
0 0 0                   0   1  0b00000000 0xffffff

C 0 0xffffffffff000000  1   0  0b00001000 x
0 0 0                   0   1  0b00000000 0xffffffff

C 0 0xffffffff00000000  1   0  0b00010000 x
0 0 0                   0   1  0b00000000 0xffffffffff

C 0 0xffffff0000000000  1   0  0b00100000 x
0 0 0                   0   1  0b00000000 0xffffffffffff

C 0 0xffff000000000000  1   0  0b01000000 x
0 0 0                   0   1  0b00000000 0xffffffffffffff

C 0 0xff00000000000000  1   0  0b10000000 x
0 0 0                   0   1  0b00000000 0xffffffffffffffff

# write 32 bit words

C 1 0xffffffff          1   0  0b00001111 x
0 1 0                   0   1  0b00000000 0xffffffff

C 1 0xaaaaaaaa00000000  1   0  0b11110000 x
0 1 0                   0   1  0b00000000 0xaaaaaaaaffffffff
*/
