// Digital circuit TestCaseInitialState2.dig as structural Verilog
module TestCaseInitialState2 (
  input  C,
  output Q_0,
  output Q_1,
  output Q_2,
  output Q_3,
  output Q_4
);

  T_FF #(.withEnable("false")) t_ff_1 (.C(C), .Q(Q_0));  // open: nQ
  T_FF #(.withEnable("false")) t_ff_2 (.C(~Q_0), .Q(Q_1));  // open: nQ
  T_FF #(.withEnable("false")) t_ff_3 (.C(~Q_1), .Q(Q_2));  // open: nQ
  T_FF #(.withEnable("false")) t_ff_4 (.C(~Q_2), .Q(Q_3));  // open: nQ
  T_FF #(.withEnable("false")) t_ff_5 (.C(~Q_3), .Q(Q_4));  // open: nQ
endmodule

/* Test case:
C Q_4 Q_3 Q_2 Q_1 Q_0

# clock counter to 11111
while(!(Q_4&Q_3&Q_2&Q_1&Q_0))
C x x x x x
end while


# start the test execution
repeat(32) C bits(5,n)
*/
