// Digital circuit TwoTestCases.dig as structural Verilog
module TwoTestCases (
  input  C
);

  wire and_1_out, G_q, not_1_out, R_q, Y_q;

  and and_1 (and_1_out, Y_q, R_q);
  not not_1 (not_1_out, and_1_out);
  JK_FF R (.J(Y_q), .C(C), .K(Y_q), .Q(R_q));  // open: nQ
  JK_FF Y (.J(1'b1), .C(C), .K(1'b1), .Q(Y_q));  // open: nQ
  JK_FF G (.J(and_1_out), .C(C), .K(not_1_out), .Q(G_q));  // open: nQ
  LED R_2 (.in(R_q));
  LED Y_2 (.in(Y_q));
  LED G_2 (.in(G_q));
endmodule

/* Test case Test 1:
C R Y G
0 0 0 0
C 0 1 0
C 1 0 0
C 1 1 0
C 0 0 1
C 0 1 0
C 1 0 0
C 1 1 0
C 0 0 1
C 0 1 0
*/

/* Test case Test 2:
C R Y G
0 0 0 0
C 0 1 0
C 1 0 0
C 1 1 0
C 0 0 1
C 0 1 0
C 1 0 0
C 1 1 0
C 0 0 1
C 0 1 0
*/
