// Digital circuit FullSubRC.dig as structural Verilog
module FullSubRC (
  input  A_0,
  input  A_1,
  input  A_2,
  input  A_3,
  input  B_0,
  input  B_1,
  input  B_2,
  input  B_3,
  input  C__1,
  output S_0,
  output S_1,
  output S_2,
  output S_3,
  output C_3
);

  wire fullsub_2_bo_i, fullsub_3_bo_i, fullsub_4_bo_i;

  FullSub fullsub_1 (.A_i(A_3), .B_i(B_3), .BO_i_1(fullsub_2_bo_i), .BO_i(C_3), .S_i(S_3));
  FullSub fullsub_2 (.A_i(A_2), .B_i(B_2), .BO_i_1(fullsub_3_bo_i), .BO_i(fullsub_2_bo_i), .S_i(S_2));
  FullSub fullsub_3 (.A_i(A_1), .B_i(B_1), .BO_i_1(fullsub_4_bo_i), .BO_i(fullsub_3_bo_i), .S_i(S_1));
  FullSub fullsub_4 (.A_i(A_0), .B_i(B_0), .BO_i_1(C__1), .BO_i(fullsub_4_bo_i), .S_i(S_0));
endmodule

/* Test case:
# complete test of all 512 possible additions
C_-1 A_3 A_2 A_1 A_0 B_3 B_2 B_1 B_0 C_3 S_3 S_2 S_1 S_0
repeat(256) 0 bits(4,n>>4) bits(4,n) bits(5,(n>>4)-(n&15))
repeat(256) 1 bits(4,n>>4) bits(4,n) bits(5,(n>>4)-(n&15)-1)
*/
