// Digital circuit HalfSub.dig as structural Verilog
module HalfSub (
  input  A,
  input  B,
  output S,
  output BO
);

  wire not_1_out;

  not not_1 (not_1_out, A);
  xor xor_1 (S, A, B);
  and and_1 (BO, not_1_out, B);
endmodule

/* Test case:
A B BO S
0 0 0  0
0 1 1  1
1 0 0  1
1 1 0  0
*/
