// Digital circuit barrelShifterTest.dig as structural Verilog
// D flip flop based on a SRAM cell.
module barrelShifterTest (
  input  [5:0] Data,
  input  [2:0] Shift,
  input  Signed,
  output [5:0] UNL,
  output [5:0] URL,
  output [5:0] SRL,
  output [5:0] SNR,
  output [5:0] UNR,
  output [5:0] SNL,
  output [5:0] UAR
);

  wire [3:0] neg_1_out;

  // Probe Data on Data
  Neg #(.Bits(4)) neg_1 (.in({Signed, Shift}), .out(neg_1_out));
  BarrelShifter #(.Bits(6)) U_N_L (.in(Data), .shift(Shift), .out(UNL));
  BarrelShifter #(.datarotate("true"), .Bits(6), .barrelShifterMode("rotate")) U_R_L (
    .in(Data), .shift(Shift), .out(URL));
  BarrelShifter #(.Bits(6), .direction("right")) U_N_R (.in(Data), .shift(Shift), .out(UNR));
  BarrelShifter #(.datarotate("true"), .Bits(6), .barrelShifterMode("arithmetic"), .direction("right")) U_A_R (
    .in(Data), .shift(Shift), .out(UAR));
  BarrelShifter #(.Signed("true"), .Bits(6), .barrelSigned("true")) S_N_L (
    .in(Data), .shift({Signed, Shift}), .out(SNL));
  BarrelShifter #(.Signed("true"), .datarotate("true"), .Bits(6), .barrelShifterMode("rotate"), .barrelSigned("true")) S_R_L (
    .in(Data), .shift({Signed, Shift}), .out(SRL));
  BarrelShifter #(.Signed("true"), .datarotate("true"), .Bits(6), .barrelSigned("true")) S_N_R (
    .in(Data), .shift({Signed, Shift}), .out(SNR));
  // Probe shift on neg_1_out
  // Probe UNL on UNL
  // Probe URL on URL
  // Probe UNR on UNR
  // Probe UAR on UAR
  // Probe SNL on SNL
  // Probe SRL on SRL
  // Probe SNR on SNR

  // Notes on the sheet:
  //   Data: default 17
  //   Shift: default 2
  //   Signed: default 1
endmodule

/* Test case:
Data Shift Signed UNL URL SNL SRL
12    0      0    12  12 12 12
12    1      0    24  24 24 24
12    2      0    48  48 48 48
17    2      0     4   5  4  5
12    3      0    32  33 32 33
12    3      1    32  33  0 24
12    7      1     0  24  6  6
*/
