// Digital circuit subTest.dig as structural Verilog
module subTest (
  input  [3:0] B,
  input  [3:0] A,
  input  C,
  output Y
);

  wire [3:0] sub_1_s;
  wire [4:0] fullsubrc_1_s_0;
  wire [4:4] sub_1_c_o;

  FullSubRC fullsubrc_1 (
    .A_0(A[0]), .A_1(A[1]), .A_2(A[2]), .A_3(A[3]), .B_0(B[0]), .B_1(B[1]), .B_2(B[2]), .B_3(B[3]), .C__1(C),
    .S_0(fullsubrc_1_s_0[0]), .S_1(fullsubrc_1_s_0[1]), .S_2(fullsubrc_1_s_0[2]), .S_3(fullsubrc_1_s_0[3]),
    .C_3(fullsubrc_1_s_0[4]));
  Sub #(.Bits(4)) sub_1 (.a(A), .b(B), .c_i(C), .s(sub_1_s), .c_o(sub_1_c_o[4]));
  Comparator #(.Bits(5)) comparator_1 (.a(fullsubrc_1_s_0), .b({sub_1_c_o[4], sub_1_s}), .eq(Y));  // open: gt, lt
endmodule

/* Test case:
A B C Y

repeat(1<<9) ((n>>4)&0xf) (n & 0xf) (n>>8) 1
*/
