// Digital circuit d_async.dig as structural Verilog
module d_async (
  input  CLK,
  input  D,
  input  S,
  input  C,
  output Q,
  output nQ
);

  D_FF_AS d_ff_as_1 (.Set(S), .D(D), .C(CLK), .Clr(C), .Q(Q), .nQ(nQ));
endmodule

/* Test case:
CLK D S C Q ~Q
 0  0 0 0 0  1
 0  1 0 0 0  1
 C  1 0 0 1  0
 0  0 0 0 1  0
 C  0 0 0 0  1
 0  0 0 1 0  1
 0  0 0 0 0  1
 0  0 1 0 1  0
 0  0 0 0 1  0
*/
