// Digital circuit jk_async.dig as structural Verilog
module jk_async (
  input  CLK,
  input  J,
  input  S,
  input  K,
  input  C,
  output Q,
  output nQ
);

  JK_FF_AS jk_ff_as_1 (.Set(S), .J(J), .C(CLK), .K(K), .Clr(C), .Q(Q), .nQ(nQ));
endmodule

/* Test case:
CLK J K S C Q ~Q
 0  0 0 0 0 0  1
 C  1 0 0 0 1  0
 0  1 0 0 0 1  0
 0  0 0 0 0 1  0
 0  0 1 0 0 1  0
 C  0 1 0 0 0  1
 0  0 0 0 0 0  1
 C  1 0 0 0 1  0
 0  0 0 1 0 1  0
 0  0 0 0 1 0  1
 C  1 1 0 0 1  0
 C  1 1 0 0 0  1
 C  1 1 0 0 1  0
 C  1 1 0 0 0  1
*/
