// Digital circuit cascadeCounter.dig as structural Verilog
module cascadeCounter (
  input  Clk,
  output [8:0] Out
);

  wire counter_1_ovf, counter_2_ovf;

  Counter #(.Bits(3)) counter_1 (.en(1'b1), .C(Clk), .clr(1'b0), .out(Out[2:0]), .ovf(counter_1_ovf));
  Counter #(.Bits(3)) counter_2 (.en(counter_1_ovf), .C(Clk), .clr(1'b0), .out(Out[5:3]), .ovf(counter_2_ovf));
  Counter #(.Bits(3)) counter_3 (.en(counter_2_ovf), .C(Clk), .clr(1'b0), .out(Out[8:6]));  // open: ovf
endmodule

/* Test case:
Clk Out
repeat(1<<9) C ((n+1)&0x1ff)
*/
