// Digital circuit overflow.dig as structural Verilog
module overflow (
  input  Clk,
  input  [63:0] In,
  input  ld,
  output [63:0] Out,
  output ov
);

  CounterPreset #(.Bits(64)) counterpreset_1 (
    .en(1'b1), .C(Clk), .dir(1'b0), .in(In), .ld(ld), .clr(1'b0), .out(Out), .ovf(ov));
endmodule

/* Test case:
Clk ld In                 Out                  ov
c    1 0xfffffffffffffffe 0xfffffffffffffffe   0
0    0 0                  0xfffffffffffffffe   0
c    0 0                  0xffffffffffffffff   1
c    0 0                  0                    0
*/
