// Digital circuit delay.dig as structural Verilog
module delay (
  input  D,
  input  C,
  output O
);

  wire delay_1_out;

  D_FF d_ff_1 (.D(delay_1_out), .C(C), .Q(O));  // open: nQ
  Delay delay_1 (.in(D), .out(delay_1_out));
endmodule

/* Test case:
C D O
C 1 1
C 0 0
*/
