// Digital circuit inner.dig as structural Verilog
module inner (
  input  A,
  input  B,
  input  C,
  output Y
);

  wire not_1_out, or_1_out;

  or or_1 (or_1_out, A, B);
  xor xor_1 (Y, or_1_out, not_1_out);
  not not_1 (not_1_out, C);
endmodule

/* Test case:
A B C Y 

 0 0 0 1
 0 0 1 0
 0 1 0 0
 0 1 1 1
 1 0 0 0
 1 0 1 1
 1 1 0 0
 1 1 1 1
*/
