// Digital circuit outer.dig as structural Verilog
module outer (
  input  [2:0] A,
  input  B,
  input  C,
  output [3:0] Y
);

  inner inner_1 (.A(A), .en(C), .Y(Y));
  // Pins of 1 and 3 bits meet at A
  // Pins of 1 and 4 bits meet at Y
endmodule

/* Test case:
A B C Y 

 0 0 0 1
 0 0 1 0
 0 1 0 0
 0 1 1 1
 1 0 0 0
 1 0 1 1
 1 1 0 0
 1 1 1 1
*/
