// Digital circuit eeprom.dig as structural Verilog
module eeprom (
  input  [7:0] A,
  input  CS,
  input  OE,
  input  WE,
  input  [7:0] D_in,
  output [7:0] D_out
);

  EEPROM #(.AddrBits(8), .Bits(8)) eeprom_1 (.A(A), .CS(CS), .WE(WE), .OE(OE), .D(D_in));

  assign D_out = D_in;

  // Notes on the sheet:
  //   contents of eeprom_1 (hex, n*v repeats v):
  //   0,1,2,3,4,5,6,7,8,9,a,b,c,d,e,f,10,11,12,13,14,15,16,17,18,19,1a,1b,1c,1d
endmodule

/* Test case first:
A   CS OE WE D_in   D_out
0   0  0  0  Z      Z

# write zeros to EEPROM
loop(n,30)
(n) 1  0  0  0      0
(n) 1  0  1  0      0
end loop

# check its cleared
loop(n,30)
(n) 1  1  0  Z      0
end loop


# write data to EEPROM
loop(n,30)
(n) 1  0  0  (n)    (n)
(n) 1  0  1  (n)    (n)
end loop

# read data from EEPROM
loop(n,30)
(n) 1  1  0  Z      (n)
end loop
*/

/* Test case second:
A   CS OE WE D_in   D_out
0   0  0  0  Z      Z

# Data written by the first test case
# is still present in the EEPROM.

# read from EEPROM
loop(n,30)
(n) 1  1  0  Z      (n)
end loop
*/
