// Digital circuit and.dig as structural Verilog
module \and  (
  input  A,
  input  B,
  output Y
);

  wire nfet_1_s, pfet_1_d;

  PFET pfet_1 (.G(A), .S(1'b1), .D(pfet_1_d));
  NFET nfet_1 (.G(A), .D(pfet_1_d), .S(nfet_1_s));
  NFET nfet_2 (.G(B), .D(nfet_1_s), .S(1'b0));
  PFET pfet_2 (.G(pfet_1_d), .S(1'b1), .D(Y));
  PFET pfet_3 (.G(B), .S(1'b1), .D(pfet_1_d));
  NFET nfet_3 (.G(pfet_1_d), .D(Y), .S(1'b0));
endmodule

/* Test case:
A B Y
0 0 0 
0 1 0 
1 0 0 
1 1 1 
1 0 0 
0 1 0 
0 0 0 
1 0 0
1 1 1
*/
