// Digital circuit burn_Error.dig as structural Verilog
module burn_Error (
  input  G,
  output Y
);

  wire delay_1_out;

  Delay delay_1 (.in(G), .out(delay_1_out));
  PullUp pullup_1 (.out(Y));
  NFET nfet_1 (.G(delay_1_out), .D(Y), .S(1'b0));
endmodule

/* Test case Failing:
G Y
1 0
0 1
z 1
*/
