// Digital circuit cmos10TFullAdder.dig as structural Verilog
// 10 Transistor Full Adder
// The drivers represent p-channel fets. Needed to 
// avoid the resistance problem 
// (see https://github.com/hneemann/Digital/issues/30).
module cmos10TFullAdder (
  input  A,
  input  B,
  input  C_i,
  output S,
  output C_o
);

  wire nfet_1_s, pfet_1_d, pfet_3_d;

  PFET #(.unidirectional("true")) pfet_1 (.G(B), .S(A), .D(pfet_1_d));
  NFET #(.unidirectional("true")) nfet_1 (.G(B), .D(pfet_1_d), .S(nfet_1_s));
  NFET #(.unidirectional("true")) nfet_2 (.G(A), .D(nfet_1_s), .S(1'b0));
  PFET #(.unidirectional("true")) pfet_2 (.G(A), .S(B), .D(pfet_1_d));
  PFET #(.unidirectional("true")) pfet_3 (.G(pfet_1_d), .S(1'b1), .D(pfet_3_d));
  NFET #(.unidirectional("true")) nfet_3 (.G(pfet_1_d), .D(pfet_3_d), .S(1'b0));
  PFET #(.unidirectional("true")) pfet_4 (.G(C_i), .S(pfet_1_d), .D(S));
  NFET #(.unidirectional("true")) nfet_4 (.G(C_i), .D(S), .S(pfet_3_d));
  PFET #(.unidirectional("true")) pfet_5 (.G(pfet_3_d), .S(C_i), .D(C_o));
  NFET #(.unidirectional("true")) nfet_5 (.G(pfet_3_d), .D(C_o), .S(A));
endmodule

/* Test case:
 A   B   C_i  C_o  S
 0   0   0     0   0
 0   0   1     0   1
 0   1   0     0   1
 0   1   1     1   0
 1   0   0     0   1
 1   0   1     1   0
 1   1   0     1   0
 1   1   1     1   1



# transitions
0 0 0 0 0
0 0 1 0 1
0 0 0 0 0
0 1 0 0 1
0 0 0 0 0
0 1 1 1 0
0 0 0 0 0
1 0 0 0 1
0 0 0 0 0
1 0 1 1 0
0 0 0 0 0
1 1 0 1 0
0 0 0 0 0
1 1 1 1 1
0 0 0 0 0
0 0 1 0 1
0 1 0 0 1
0 0 1 0 1
0 1 1 1 0
0 0 1 0 1
1 0 0 0 1
0 0 1 0 1
1 0 1 1 0
0 0 1 0 1
1 1 0 1 0
0 0 1 0 1
1 1 1 1 1
0 0 1 0 1
0 1 0 0 1
0 1 1 1 0
0 1 0 0 1
1 0 0 0 1
0 1 0 0 1
1 0 1 1 0
0 1 0 0 1
1 1 0 1 0
0 1 0 0 1
1 1 1 1 1
0 1 0 0 1
0 1 1 1 0
1 0 0 0 1
0 1 1 1 0
1 0 1 1 0
0 1 1 1 0
1 1 0 1 0
0 1 1 1 0
1 1 1 1 1
0 1 1 1 0
1 0 0 0 1
1 0 1 1 0
1 0 0 0 1
1 1 0 1 0
1 0 0 0 1
1 1 1 1 1
1 0 0 0 1
1 0 1 1 0
1 1 0 1 0
1 0 1 1 0
1 1 1 1 1
1 0 1 1 0
1 1 0 1 0
1 1 1 1 1
1 1 0 1 0
*/
