// Digital circuit cmosGDIFullAdder.dig as structural Verilog
// Gate Diffusion Input (GDI) Full Adder
module cmosGDIFullAdder (
  input  A,
  input  B,
  input  C_i,
  output S,
  output C_o
);

  wire pfet_1_d, pfet_2_d, pfet_3_d;

  PFET pfet_1 (.G(A), .S(1'b1), .D(pfet_1_d));
  NFET nfet_1 (.G(A), .D(pfet_1_d), .S(1'b0));
  PFET pfet_2 (.G(B), .S(A), .D(pfet_2_d));
  NFET #(.unidirectional("true")) nfet_2 (.G(B), .D(pfet_2_d), .S(pfet_1_d));
  PFET pfet_3 (.G(pfet_2_d), .S(1'b1), .D(pfet_3_d));
  NFET nfet_3 (.G(pfet_2_d), .D(pfet_3_d), .S(1'b0));
  PFET #(.unidirectional("true")) pfet_4 (.G(C_i), .S(pfet_2_d), .D(S));
  NFET #(.unidirectional("true")) nfet_4 (.G(C_i), .D(S), .S(pfet_3_d));
  NFET nfet_5 (.G(pfet_2_d), .D(C_i), .S(C_o));
  PFET pfet_5 (.G(pfet_2_d), .S(C_o), .D(A));
endmodule

/* Test case:
 A   B   C_i  C_o  S
 0   0   0     0   0
 0   0   1     0   1
 0   1   0     0   1
 0   1   1     1   0
 1   0   0     0   1
 1   0   1     1   0
 1   1   0     1   0
 1   1   1     1   1



# transitions
0 0 0 0 0
0 0 1 0 1
0 0 0 0 0
0 1 0 0 1
0 0 0 0 0
0 1 1 1 0
0 0 0 0 0
1 0 0 0 1
0 0 0 0 0
1 0 1 1 0
0 0 0 0 0
1 1 0 1 0
0 0 0 0 0
1 1 1 1 1
0 0 0 0 0
0 0 1 0 1
0 1 0 0 1
0 0 1 0 1
0 1 1 1 0
0 0 1 0 1
1 0 0 0 1
0 0 1 0 1
1 0 1 1 0
0 0 1 0 1
1 1 0 1 0
0 0 1 0 1
1 1 1 1 1
0 0 1 0 1
0 1 0 0 1
0 1 1 1 0
0 1 0 0 1
1 0 0 0 1
0 1 0 0 1
1 0 1 1 0
0 1 0 0 1
1 1 0 1 0
0 1 0 0 1
1 1 1 1 1
0 1 0 0 1
0 1 1 1 0
1 0 0 0 1
0 1 1 1 0
1 0 1 1 0
0 1 1 1 0
1 1 0 1 0
0 1 1 1 0
1 1 1 1 1
0 1 1 1 0
1 0 0 0 1
1 0 1 1 0
1 0 0 0 1
1 1 0 1 0
1 0 0 0 1
1 1 1 1 1
1 0 0 0 1
1 0 1 1 0
1 1 0 1 0
1 0 1 1 0
1 1 1 1 1
1 0 1 1 0
1 1 0 1 0
1 1 1 1 1
1 1 0 1 0
*/
