// Digital circuit cmosMirrorFullAdder.dig as structural Verilog
// 28T CMOS mirror adder
module cmosMirrorFullAdder (
  input  A,
  input  B,
  input  C_i,
  output C_o,
  output S
);

  wire nfet_1_d, nfet_5_s, nfet_7_d, nfet_11_s, nfet_12_s, pfet_1_d, pfet_2_d, pfet_3_d, pfet_7_d, pfet_8_d,
       pfet_11_d, pfet_12_d;

  NFET nfet_1 (.G(A), .D(nfet_1_d), .S(1'b0));
  PFET pfet_1 (.G(A), .S(1'b1), .D(pfet_1_d));
  PFET pfet_2 (.G(B), .S(pfet_1_d), .D(pfet_2_d));
  PFET pfet_3 (.G(A), .S(pfet_2_d), .D(pfet_3_d));
  NFET nfet_2 (.G(C_i), .D(pfet_3_d), .S(nfet_1_d));
  PFET pfet_4 (.G(B), .S(1'b1), .D(pfet_1_d));
  PFET pfet_5 (.G(C_i), .S(pfet_1_d), .D(pfet_3_d));
  NFET nfet_3 (.G(B), .D(nfet_1_d), .S(1'b0));
  PFET pfet_6 (.G(pfet_3_d), .S(1'b1), .D(C_o));
  NFET nfet_4 (.G(pfet_3_d), .D(C_o), .S(1'b0));
  NFET nfet_5 (.G(A), .D(pfet_3_d), .S(nfet_5_s));
  NFET nfet_6 (.G(B), .D(nfet_5_s), .S(1'b0));
  NFET nfet_7 (.G(C_i), .D(nfet_7_d), .S(1'b0));
  PFET pfet_7 (.G(C_i), .S(1'b1), .D(pfet_7_d));
  PFET pfet_8 (.G(pfet_3_d), .S(pfet_7_d), .D(pfet_8_d));
  NFET nfet_8 (.G(pfet_3_d), .D(pfet_8_d), .S(nfet_7_d));
  NFET nfet_9 (.G(A), .D(nfet_7_d), .S(1'b0));
  PFET pfet_9 (.G(A), .S(1'b1), .D(pfet_7_d));
  NFET nfet_10 (.G(B), .D(nfet_7_d), .S(1'b0));
  PFET pfet_10 (.G(B), .S(1'b1), .D(pfet_7_d));
  PFET pfet_11 (.G(A), .S(pfet_7_d), .D(pfet_11_d));
  PFET pfet_12 (.G(B), .S(pfet_11_d), .D(pfet_12_d));
  PFET pfet_13 (.G(C_i), .S(pfet_12_d), .D(pfet_8_d));
  NFET nfet_11 (.G(A), .D(pfet_8_d), .S(nfet_11_s));
  NFET nfet_12 (.G(B), .D(nfet_11_s), .S(nfet_12_s));
  NFET nfet_13 (.G(C_i), .D(nfet_12_s), .S(1'b0));
  PFET pfet_14 (.G(pfet_8_d), .S(1'b1), .D(S));
  NFET nfet_14 (.G(pfet_8_d), .D(S), .S(1'b0));
endmodule

/* Test case:
 A   B   C_i  C_o  S
 0   0   0     0   0
 0   0   1     0   1
 0   1   0     0   1
 0   1   1     1   0
 1   0   0     0   1
 1   0   1     1   0
 1   1   0     1   0
 1   1   1     1   1




# transitions
0 0 0 0 0
0 0 1 0 1
0 0 0 0 0
0 1 0 0 1
0 0 0 0 0
0 1 1 1 0
0 0 0 0 0
1 0 0 0 1
0 0 0 0 0
1 0 1 1 0
0 0 0 0 0
1 1 0 1 0
0 0 0 0 0
1 1 1 1 1
0 0 0 0 0
0 0 1 0 1
0 1 0 0 1
0 0 1 0 1
0 1 1 1 0
0 0 1 0 1
1 0 0 0 1
0 0 1 0 1
1 0 1 1 0
0 0 1 0 1
1 1 0 1 0
0 0 1 0 1
1 1 1 1 1
0 0 1 0 1
0 1 0 0 1
0 1 1 1 0
0 1 0 0 1
1 0 0 0 1
0 1 0 0 1
1 0 1 1 0
0 1 0 0 1
1 1 0 1 0
0 1 0 0 1
1 1 1 1 1
0 1 0 0 1
0 1 1 1 0
1 0 0 0 1
0 1 1 1 0
1 0 1 1 0
0 1 1 1 0
1 1 0 1 0
0 1 1 1 0
1 1 1 1 1
0 1 1 1 0
1 0 0 0 1
1 0 1 1 0
1 0 0 0 1
1 1 0 1 0
1 0 0 0 1
1 1 1 1 1
1 0 0 0 1
1 0 1 1 0
1 1 0 1 0
1 0 1 1 0
1 1 1 1 1
1 0 1 1 0
1 1 0 1 0
1 1 1 1 1
1 1 0 1 0
*/
