// Digital circuit inverter.dig as structural Verilog
module inverter (
  input  A,
  output Y
);

  PFET pfet_1 (.G(A), .S(1'b1), .D(Y));
  NFET nfet_1 (.G(A), .D(Y), .S(1'b0));
endmodule

/* Test case:
A Y
0 1
1 0
Z Z
*/
