// Digital circuit multiBit.dig as structural Verilog
module multiBit (
  input  A,
  input  [7:0] B,
  input  A1,
  input  [7:0] B1,
  output [7:0] Y,
  output [7:0] Y1
);

  NFET #(.Bits(8)) nfet_1 (.G(A), .D(Y), .S(B));
  PFET #(.Bits(8)) pfet_1 (.G(A1), .S(Y1), .D(B1));
endmodule

/* Test case p-chan:
A1 B1 Y1
0 0 0 
0 7 7 
1 0 z 
1 7 z 
*/

/* Test case n-chan:
A B Y
0 0 z 
0 7 z 
1 0 0 
1 7 7 
*/
