// Digital circuit nand.dig as structural Verilog
module \nand  (
  input  A,
  input  B,
  output Y
);

  wire nfet_1_s;

  PFET pfet_1 (.G(A), .S(1'b1), .D(Y));
  NFET nfet_1 (.G(A), .D(Y), .S(nfet_1_s));
  NFET nfet_2 (.G(B), .D(nfet_1_s), .S(1'b0));
  PFET pfet_2 (.G(B), .S(1'b1), .D(Y));
endmodule

/* Test case:
A B Y
0 0 1 
0 1 1 
1 0 1 
1 1 0 
1 0 1 
0 1 1 
0 0 1 
1 0 1
1 1 0
*/
