// Digital circuit nchan.dig as structural Verilog
module nchan (
  input  D,
  input  S,
  input  G,
  output d_2,
  output s_2
);

  NFET nfet_1 (.G(G), .D(D), .S(S));

  assign d_2 = D;
  assign s_2 = S;
endmodule

/* Test case:
S D G s d
1 z 0 1 z
z 1 0 z 1
1 z z 1 z
z 1 z z 1
1 z 1 1 1
z 1 1 1 1
0 z 1 0 0
z 0 1 0 0



# transitions
1 Z 0 1 Z
Z 1 0 Z 1
1 Z 0 1 Z
1 Z Z 1 Z
1 Z 0 1 Z
Z 1 Z Z 1
1 Z 0 1 Z
1 Z 1 1 1
1 Z 0 1 Z
Z 1 1 1 1
1 Z 0 1 Z
0 Z 1 0 0
1 Z 0 1 Z
Z 0 1 0 0
1 Z 0 1 Z
Z 1 0 Z 1
1 Z Z 1 Z
Z 1 0 Z 1
Z 1 Z Z 1
Z 1 0 Z 1
1 Z 1 1 1
Z 1 0 Z 1
Z 1 1 1 1
Z 1 0 Z 1
0 Z 1 0 0
Z 1 0 Z 1
Z 0 1 0 0
Z 1 0 Z 1
1 Z Z 1 Z
Z 1 Z Z 1
1 Z Z 1 Z
1 Z 1 1 1
1 Z Z 1 Z
Z 1 1 1 1
1 Z Z 1 Z
0 Z 1 0 0
1 Z Z 1 Z
Z 0 1 0 0
1 Z Z 1 Z
Z 1 Z Z 1
1 Z 1 1 1
Z 1 Z Z 1
Z 1 1 1 1
Z 1 Z Z 1
0 Z 1 0 0
Z 1 Z Z 1
Z 0 1 0 0
Z 1 Z Z 1
1 Z 1 1 1
Z 1 1 1 1
1 Z 1 1 1
0 Z 1 0 0
1 Z 1 1 1
Z 0 1 0 0
1 Z 1 1 1
Z 1 1 1 1
0 Z 1 0 0
Z 1 1 1 1
Z 0 1 0 0
Z 1 1 1 1
0 Z 1 0 0
Z 0 1 0 0
0 Z 1 0 0
*/
