// Digital circuit openDrainOut.dig as structural Verilog
module openDrainOut (
  input  A,
  input  B,
  input  C,
  input  D,
  output Y
);

  NFET nfet_1 (.G(A), .D(Y), .S(1'b0));
  NFET nfet_2 (.G(B), .D(Y), .S(1'b0));
  PullUp pullup_1 (.out(Y));
  NFET nfet_3 (.G(C), .D(Y), .S(1'b0));
  NFET nfet_4 (.G(D), .D(Y), .S(1'b0));
endmodule

/* Test case:
A B C D Y
0 0 0 0 1
0 0 0 1 0
0 0 1 0 0
0 0 1 1 0
0 1 0 0 0
0 1 0 1 0
0 1 1 0 0
0 1 1 1 0
1 0 0 0 0
1 0 0 1 0
1 0 1 0 0
1 0 1 1 0
1 1 0 0 0
1 1 0 1 0
1 1 1 0 0
1 1 1 1 0
*/
