// Digital circuit pchan.dig as structural Verilog
module pchan (
  input  S,
  input  D,
  input  G,
  output s_2,
  output d_2
);

  PFET pfet_1 (.G(G), .S(S), .D(D));

  assign d_2 = D;
  assign s_2 = S;
endmodule

/* Test case:
S D G s d
1 z 1 1 z
z 1 1 z 1
1 z z 1 z
z 1 z z 1
1 z 0 1 1
z 1 0 1 1
0 z 0 0 0
z 0 0 0 0


# transitions
1 Z 1 1 Z
Z 1 1 Z 1
1 Z 1 1 Z
1 Z Z 1 Z
1 Z 1 1 Z
Z 1 Z Z 1
1 Z 1 1 Z
1 Z 0 1 1
1 Z 1 1 Z
Z 1 0 1 1
1 Z 1 1 Z
0 Z 0 0 0
1 Z 1 1 Z
Z 0 0 0 0
1 Z 1 1 Z
Z 1 1 Z 1
1 Z Z 1 Z
Z 1 1 Z 1
Z 1 Z Z 1
Z 1 1 Z 1
1 Z 0 1 1
Z 1 1 Z 1
Z 1 0 1 1
Z 1 1 Z 1
0 Z 0 0 0
Z 1 1 Z 1
Z 0 0 0 0
Z 1 1 Z 1
1 Z Z 1 Z
Z 1 Z Z 1
1 Z Z 1 Z
1 Z 0 1 1
1 Z Z 1 Z
Z 1 0 1 1
1 Z Z 1 Z
0 Z 0 0 0
1 Z Z 1 Z
Z 0 0 0 0
1 Z Z 1 Z
Z 1 Z Z 1
1 Z 0 1 1
Z 1 Z Z 1
Z 1 0 1 1
Z 1 Z Z 1
0 Z 0 0 0
Z 1 Z Z 1
Z 0 0 0 0
Z 1 Z Z 1
1 Z 0 1 1
Z 1 0 1 1
1 Z 0 1 1
0 Z 0 0 0
1 Z 0 1 1
Z 0 0 0 0
1 Z 0 1 1
Z 1 0 1 1
0 Z 0 0 0
Z 1 0 1 1
Z 0 0 0 0
Z 1 0 1 1
0 Z 0 0 0
Z 0 0 0 0
0 Z 0 0 0
*/
