// Digital circuit switchTest.dig as structural Verilog
module switchTest (
  input  A,
  output Y
);

  NFET nfet_1 (.G(1'b1), .D(Y), .S(Y));
  NFET nfet_2 (.G(A), .D(Y), .S(1'b0));
  PullUp pullup_1 (.out(Y));
endmodule

/* Test case:
A Y
0 1
1 0
0 1
1 0
0 1
*/
