// Digital circuit tristateout.dig as structural Verilog
module tristateout (
  input  out,
  input  en,
  output Y
);

  wire nfet_2_s, pfet_1_d, pfet_2_d;

  PFET pfet_1 (.G(en), .S(1'b1), .D(pfet_1_d));
  NFET nfet_1 (.G(en), .D(pfet_1_d), .S(1'b0));
  PFET pfet_2 (.G(pfet_1_d), .S(1'b1), .D(pfet_2_d));
  PFET pfet_3 (.G(out), .S(pfet_2_d), .D(Y));
  NFET nfet_2 (.G(out), .D(Y), .S(nfet_2_s));
  NFET nfet_3 (.G(en), .D(nfet_2_s), .S(1'b0));
endmodule

/* Test case:
out en Y
 0  1  1
 1  1  0
 0  0  z
 1  0  z
*/
