// Digital circuit xor.dig as structural Verilog
module \xor  (
  input  A,
  input  B,
  output Y
);

  wire T1_d, T3_s, T5_d, T7_d, T9_s, T11_d, T15_s;

  PFET T5 (.G(A), .S(1'b1), .D(T5_d));
  NFET T6 (.G(A), .D(T5_d), .S(1'b0));
  PFET T1 (.G(B), .S(1'b1), .D(T1_d));
  NFET T3 (.G(B), .D(T1_d), .S(T3_s));
  NFET T4 (.G(T5_d), .D(T3_s), .S(1'b0));
  PFET T11 (.G(B), .S(1'b1), .D(T11_d));
  NFET T12 (.G(B), .D(T11_d), .S(1'b0));
  PFET T2 (.G(T5_d), .S(1'b1), .D(T1_d));
  PFET T7 (.G(A), .S(1'b1), .D(T7_d));
  PFET T8 (.G(T11_d), .S(1'b1), .D(T7_d));
  NFET T9 (.G(A), .D(T7_d), .S(T9_s));
  NFET T10 (.G(T11_d), .D(T9_s), .S(1'b0));
  PFET T13 (.G(T1_d), .S(1'b1), .D(Y));
  PFET T14 (.G(T7_d), .S(1'b1), .D(Y));
  NFET T15 (.G(T1_d), .D(Y), .S(T15_s));
  NFET T16 (.G(T7_d), .D(T15_s), .S(1'b0));
endmodule

/* Test case:
A B Y
0 0 0
0 1 1
1 0 1
1 1 0


# transitions
0 0 0
0 1 1
0 0 0
1 0 1
0 0 0
1 1 0
0 0 0
0 1 1
1 0 1
0 1 1
1 1 0
0 1 1
1 0 1
1 1 0
1 0 1
*/
