// Digital circuit xor2.dig as structural Verilog
module xor2 (
  input  B,
  input  A,
  output Y
);

  wire nfet_1_s;

  PFET #(.unidirectional("true")) pfet_1 (.G(B), .S(A), .D(Y));
  NFET #(.unidirectional("true")) nfet_1 (.G(B), .D(Y), .S(nfet_1_s));
  TransGate transgate_1 (.A(nfet_1_s), .nA(A), .out1(B), .out2(Y));
  PFET pfet_2 (.G(A), .S(1'b1), .D(nfet_1_s));
  NFET nfet_2 (.G(A), .D(nfet_1_s), .S(1'b0));
endmodule

/* Test case:
A B Y
0 0 0
0 1 1
1 0 1
1 1 0



# transitions
0 0 0
0 1 1
0 0 0
1 0 1
0 0 0
1 1 0
0 0 0
0 1 1
1 0 1
0 1 1
1 1 0
0 1 1
1 0 1
1 1 0
1 0 1
*/
