// Digital circuit countSplitter.dig as structural Verilog
module countSplitter (
  input  en,
  input  C,
  output [3:0] d,
  output ov
);

  wire counter_1_ovf;

  Counter #(.Bits(2), .generic("this.Bits=int(args.bits);")) counter_1 (
    .en(en), .C(C), .clr(1'b0), .out(d[1:0]), .ovf(counter_1_ovf));
  Counter #(.Bits(2), .generic("this.Bits=int(args.bits);")) counter_2 (
    .en(counter_1_ovf), .C(C), .clr(1'b0), .out(d[3:2]), .ovf(ov));

  // Notes on the sheet:
  //   C: Hz: 2
endmodule

/* Code that sets the parameters or builds the circuit:
bits := 2;
*/
