// Digital circuit inverterConfig.dig as structural Verilog
module inverterConfig (
  input  D,
  input  C,
  output Q
);

  D_FF #(.generic("this.inverterConfig=newList(\"D\");")) d_ff_1 (.C(C), .Q(Q));  // open: D, nQ
endmodule

/* Test case:
C D Q
c 0 1
c 1 0
*/
