// Digital circuit mainMem.dig as structural Verilog
module mainMem (
  input  [15:0] D,
  input  [7:0] A,
  input  C,
  input  str,
  output [15:0] D_Out
);

  // memNode #(.generic("dataBits := 16; addrBits := 8;")) memnode_1: pin names not known; wires that end beside it: D, A, C, str, D_Out
endmodule

/* Test case:
C  D   A  str  D_Out

# write data
loop(n,1<<8)
C (n+2) (n)  1     x
end loop

# read data
loop(n,1<<8)
0   0   (n)  0   (n+2)
end loop

0   0   (1<<8)  0   (2)
*/
