// Digital circuit mainNest.dig as structural Verilog
module mainNest (
  input  C,
  output [8:0] O
);

  wire nesterror_1_p4, nesterror_2_p4;

  // nestError #(.generic("bits:=2;")) nesterror_1: pin names not known; wires that end beside it: 1'b1, C, O[1:0], nesterror_1_p4
  // nestError #(.generic("bits:=3;")) nesterror_2: pin names not known; wires that end beside it: nesterror_1_p4, C, O[4:2], nesterror_2_p4
  // nestError #(.generic("bits:=4;")) nesterror_3: pin names not known; wires that end beside it: nesterror_2_p4, C, O[8:5]

  // Notes on the sheet:
  //   C: Hz: 5
endmodule

/* Test case:
C O
loop(n,512)
C (n+1)
end loop
*/
