// Digital circuit mainSplitter.dig as structural Verilog
module mainSplitter (
  input  C,
  output [9:0] O
);

  wire countsplitter_1_p4;

  // countSplitter #(.generic("bits:=2;")) countsplitter_1: pin names not known; wires that end beside it: 1'b1, C, O[3:0], countsplitter_1_p4
  // countSplitter #(.generic("bits:=3;")) countsplitter_2: pin names not known; wires that end beside it: countsplitter_1_p4, C, O[9:4]

  // Notes on the sheet:
  //   C: Hz: 5
endmodule

/* Test case:
C O
loop(n,1024)
C (n+1)
end loop
*/
