// Digital circuit memNode.dig as structural Verilog
module memNode (
  input  D_in,
  input  [1:0] A,
  input  C,
  input  str,
  output D_Out
);

  wire and_1_out, and_2_out, memleaf_1_p5, memleaf_2_p5;

  and and_1 (and_1_out, str, ~A[1]);  // And
  and and_2 (and_2_out, str, A[1]);
  // memLeaf #(.generic("if (isPresent(args)) { export dataBits:=args.dataBits; export addrBits:=args.addrBits-1; if (args.addrBits>2) { setCircuit(\"memNode.dig\"); } } else { export dataBits:=int(1); }")) memleaf_1: pin names not known; wires that end beside it: D_in, A[0], C, and_1_out, memleaf_1_p5
  // memLeaf #(.generic("if (isPresent(args)) { export dataBits:=args.dataBits; export addrBits:=args.addrBits-1; if (args.addrBits>2) { setCircuit(\"memNode.dig\"); } } else { export dataBits:=int(1); }")) memleaf_2: pin names not known; wires that end beside it: D_in, A[0], C, and_2_out, memleaf_2_p5
  Multiplexer #(.generic("if (isPresent(args)) { this.Bits=int(args.dataBits); }")) multiplexer_1 (
    .sel(A[1]), .in_0(memleaf_1_p5), .in_1(memleaf_2_p5), .out(D_Out));
endmodule
