// Digital circuit memNode2.dig as structural Verilog
module memNode2 (
  input  D_in,
  input  [3:0] A,
  input  C,
  input  str,
  output D_Out
);

  wire demultiplexer_1_out_0, demultiplexer_1_out_1, demultiplexer_1_out_2, demultiplexer_1_out_3,
       memleaf2_1_p5, memleaf2_2_p5, memleaf2_3_p5, memleaf2_4_p5;

  Demultiplexer #(.Selector_Bits(2)) demultiplexer_1 (
    .sel(A[3:2]), .in(str), .out_0(demultiplexer_1_out_0), .out_1(demultiplexer_1_out_1),
    .out_2(demultiplexer_1_out_2), .out_3(demultiplexer_1_out_3));
  // memLeaf2 #(.generic("if (isPresent(args)) { export dataBits:=args.dataBits; export addrBits:=args.addrBits-2; if (args.addrBits>4) { setCircuit(\"memNode2.dig\"); } } else { export dataBits:=int(1); }")) memleaf2_1: pin names not known; wires that end beside it: D_in, A[1:0], C, demultiplexer_1_out_0, memleaf2_1_p5
  // memLeaf2 #(.generic("if (isPresent(args)) { export dataBits:=args.dataBits; export addrBits:=args.addrBits-2; if (args.addrBits>4) { setCircuit(\"memNode2.dig\"); } } else { export dataBits:=int(1); }")) memleaf2_2: pin names not known; wires that end beside it: D_in, A[1:0], C, demultiplexer_1_out_1, memleaf2_2_p5
  // memLeaf2 #(.generic("if (isPresent(args)) { export dataBits:=args.dataBits; export addrBits:=args.addrBits-2; if (args.addrBits>4) { setCircuit(\"memNode2.dig\"); } } else { export dataBits:=int(1); }")) memleaf2_3: pin names not known; wires that end beside it: D_in, A[1:0], C, demultiplexer_1_out_2, memleaf2_3_p5
  // memLeaf2 #(.generic("if (isPresent(args)) { export dataBits:=args.dataBits; export addrBits:=args.addrBits-2; if (args.addrBits>4) { setCircuit(\"memNode2.dig\"); } } else { export dataBits:=int(1); }")) memleaf2_4: pin names not known; wires that end beside it: D_in, A[1:0], C, demultiplexer_1_out_3, memleaf2_4_p5
  Multiplexer #(.Selector_Bits(2), .generic("if (isPresent(args)) { this.Bits=int(args.dataBits); }")) multiplexer_1 (
    .sel(A[3:2]), .in_0(memleaf2_1_p5), .in_1(memleaf2_2_p5), .in_2(memleaf2_3_p5), .in_3(memleaf2_4_p5),
    .out(D_Out));
endmodule
