// Digital circuit nestError.dig as structural Verilog
module nestError (
  input  en,
  input  C,
  output d,
  output ov
);

  // count #(.generic("bits:=args.bits;")) count_1: pin names not known; wires that end beside it: en, C, d, ov

  // Notes on the sheet:
  //   C: Hz: 5
endmodule
