// Digital circuit highz.dig as structural Verilog
module highz (
  input  I,
  input  en,
  output O
);

  assign O = en ? I : 1'bz;  // Driver driver_1
endmodule

/* Test case High Z:
I en O
1 1  1
0 1  0
1 0  Z
0 0  Z
1 0  X
0 0  X
*/
