// Digital circuit invClock.dig as structural Verilog
module invClock (
  input  C,
  output Y
);

  wire d_ff_1_q;

  D_FF d_ff_1 (.D(~d_ff_1_q), .C(~C), .Q(d_ff_1_q), .nQ(Y));
endmodule

/* Test case:
C Y
0 0
1 0
0 1
1 1
0 0
1 0
*/
