// Digital circuit simpleTest1.dig as structural Verilog
module simpleTest1 (
  input  _2A,
  input  _2B,
  input  _1A,
  input  _1B,
  output _2Y,
  output _1Y
);

  and and_1 (_1Y, ~_1A, _1B);  // And
  buf xor_1 (_2Y, _2B);  // XOr open: In_1
endmodule

/* Test case AND:
1A 1B 1Y
0  0  0
0  1  1
1  0  0
1  1  0
 
*/

/* Test case XOR:
2A 2B 2Y
0  0  1
0  1  0
1  0  0
1  1  1
 
*/
