// Digital circuit simpleTest2.dig as structural Verilog
module simpleTest2 (
  input  C,
  output Q
);

  JK_FF_AS jk_ff_as_1 (.Set(~1'b1), .J(1'b1), .C(C), .K(1'b1), .Clr(~1'b1), .Q(Q));  // open: nQ
endmodule

/* Test case:
C Q
0 0
C 1
C 0
C 1
*/
