// Digital circuit monoflop.dig as structural Verilog
module monoflop (
  input  C,
  input  R,
  input  S,
  output Q,
  output nQ
);

  Monoflop #(.timerDelay(6), .Default(1)) MF (.C(S), .R(R), .Q(Q), .nQ(nQ));

  // Notes on the sheet:
  //   C: Hz: 5
endmodule

/* Test case:
          C S R Q ~Q
repeat(5) C 0 0 1 0
repeat(5) C 0 0 0 1
          C 1 0 1 0
repeat(4) C 0 0 1 0
repeat(5) C 0 0 0 1
          C 1 0 1 0
          C 0 0 1 0
          C 0 1 0 1
*/
