// Digital circuit inner.dig as structural Verilog
module inner (
  input  A,
  input  T,
  input  B,
  output Y
);

  xor xor_1 (Y, A, B);
endmodule

/* Test case:
A B T Y
0 0 0 0
0 1 0 1
1 0 0 1
1 1 0 0
0 0 1 0
0 1 1 1
1 0 1 1
1 1 1 0
*/
