// Digital circuit main.dig as structural Verilog
module main (
  input  A,
  input  B,
  input  T,
  output Y
);

  // inner inner_1: pin names not known; wires that end beside it: A, T, B, Y
endmodule

/* Test case:
A B T Y
0 0 0 0
0 1 0 1
1 0 0 1
1 1 0 0
0 0 1 0
0 1 1 1
1 0 1 1
1 1 1 0
*/
