// Digital circuit main.dig as structural Verilog
module main (
  input  [3:0] A,
  output [3:0] Y
);

  wire not_1_out;

  inner u_A (.A(A[2:0]), .en(not_1_out), .Y(Y));
  not not_1 (not_1_out, A[3]);
  inner B (.A(A[2:0]), .en(A[3]), .Y(Y));

  // Notes on the sheet:
  //   contents of A (hex, n*v repeats v):
  //   /home/sula/Dokumente/Digital/dig/ModelInit/rom_A.hex false
  //   contents of B (hex, n*v repeats v):
  //   rom_B.hex false
endmodule

/* Test case:
A Y 

 0b0000 1
 0b0001 2
 0b0010 3
 0b0011 4
 0b0100 5
 0b0101 6
 0b0110 7
 0b0111 8
 0b1000 9
 0b1001 10
 0b1010 11
 0b1011 12
 0b1100 13
 0b1101 14
 0b1110 15
 0b1111 0
*/
