// Digital circuit simple.dig as structural Verilog
module simple (
  input  [3:0] wr_0,
  input  oe,
  input  [3:0] wr_1,
  output [3:0] rd_0,
  output [3:0] rd_1
);

  wire not_1_out, pincontrol_1_p3;

  // PinControl #(.Bits(4)) pincontrol_1: pin names not known; wires that end beside it: rd_0, oe, pincontrol_1_p3
  not not_1 (not_1_out, oe);
  // PinControl #(.Bits(4)) pincontrol_2: pin names not known; wires that end beside it: wr_0, pincontrol_1_p3, wr_1, rd_1, not_1_out
endmodule

/* Test case:
oe wr_0 rd_0 wr_1 rd_1
1   1     x   x    1
1   2     x   x    2
0   x     1   1    x
0   x     2   2    x
*/
