// Digital circuit uniTest.dig as structural Verilog
module uniTest (
  input  wr,
  input  oe,
  output rd,
  output pin
);

  // PinControl pincontrol_1: pin names not known; wires that end beside it: wr, oe, rd, pin
endmodule

/* Test case:
oe wr rd pin
1  0  0  0
1  1  1  1
*/
