// Digital circuit DiodeBackward.dig as structural Verilog
module DiodeBackward (
  input  A,
  output Y
);

  DiodeBackward diodebackward_1 (.in(A), .out(Y));
  PullUp pullup_1 (.out(Y));
endmodule

/* Test case:
A Y
1 1
0 0
Z 1
*/
