// Digital circuit DiodeForeward.dig as structural Verilog
module DiodeForeward (
  input  A,
  output Y
);

  // DiodeForeward diodeforeward_1: pin names not known; wires that end beside it: A, Y
  PullDown pulldown_1 (.out(Y));
endmodule

/* Test case:
A Y
1 1
0 0
Z 0
*/
