// Digital circuit GAL2v2.dig as structural Verilog
module GAL2v2 (
  input  A,
  input  B,
  input  C,
  output Y_0,
  output Y_1
);

  wire diodebackward_1_out, diodebackward_3_out, diodebackward_5_out, diodebackward_7_out,
       diodebackward_9_out, diodebackward_11_out, diodebackward_13_out, diodebackward_15_out, MC0_q, MC1_q,
       not_1_out, not_2_out, not_3_out, not_4_out, or_1_out, or_2_out, pullup_9_out, pullup_10_out;

  not not_1 (not_1_out, A);
  DiodeBackward #(.Blown("true")) diodebackward_1 (.in(A), .out(diodebackward_1_out));
  DiodeBackward #(.Blown("true")) diodebackward_2 (.in(not_1_out), .out(diodebackward_1_out));
  DiodeBackward diodebackward_3 (.in(A), .out(diodebackward_3_out));
  DiodeBackward diodebackward_4 (.in(not_1_out), .out(diodebackward_3_out));
  DiodeBackward diodebackward_5 (.in(A), .out(diodebackward_5_out));
  DiodeBackward diodebackward_6 (.in(not_1_out), .out(diodebackward_5_out));
  DiodeBackward diodebackward_7 (.in(A), .out(diodebackward_7_out));
  DiodeBackward diodebackward_8 (.in(not_1_out), .out(diodebackward_7_out));
  DiodeBackward #(.Blown("true")) diodebackward_9 (.in(A), .out(diodebackward_9_out));
  DiodeBackward diodebackward_10 (.in(not_1_out), .out(diodebackward_9_out));
  DiodeBackward #(.Blown("true")) diodebackward_11 (.in(A), .out(diodebackward_11_out));
  DiodeBackward diodebackward_12 (.in(not_1_out), .out(diodebackward_11_out));
  DiodeBackward diodebackward_13 (.in(A), .out(diodebackward_13_out));
  DiodeBackward #(.Blown("true")) diodebackward_14 (.in(not_1_out), .out(diodebackward_13_out));
  DiodeBackward diodebackward_15 (.in(A), .out(diodebackward_15_out));
  DiodeBackward #(.Blown("true")) diodebackward_16 (.in(not_1_out), .out(diodebackward_15_out));
  not not_2 (not_2_out, B);
  DiodeBackward #(.Blown("true")) diodebackward_17 (.in(B), .out(diodebackward_1_out));
  DiodeBackward #(.Blown("true")) diodebackward_18 (.in(not_2_out), .out(diodebackward_1_out));
  DiodeBackward diodebackward_19 (.in(B), .out(diodebackward_3_out));
  DiodeBackward diodebackward_20 (.in(not_2_out), .out(diodebackward_3_out));
  DiodeBackward diodebackward_21 (.in(B), .out(diodebackward_5_out));
  DiodeBackward diodebackward_22 (.in(not_2_out), .out(diodebackward_5_out));
  DiodeBackward diodebackward_23 (.in(B), .out(diodebackward_7_out));
  DiodeBackward diodebackward_24 (.in(not_2_out), .out(diodebackward_7_out));
  DiodeBackward #(.Blown("true")) diodebackward_25 (.in(B), .out(diodebackward_9_out));
  DiodeBackward #(.Blown("true")) diodebackward_26 (.in(not_2_out), .out(diodebackward_9_out));
  DiodeBackward #(.Blown("true")) diodebackward_27 (.in(B), .out(diodebackward_11_out));
  DiodeBackward #(.Blown("true")) diodebackward_28 (.in(not_2_out), .out(diodebackward_11_out));
  DiodeBackward #(.Blown("true")) diodebackward_29 (.in(B), .out(diodebackward_13_out));
  DiodeBackward #(.Blown("true")) diodebackward_30 (.in(not_2_out), .out(diodebackward_13_out));
  DiodeBackward #(.Blown("true")) diodebackward_31 (.in(B), .out(diodebackward_15_out));
  DiodeBackward #(.Blown("true")) diodebackward_32 (.in(not_2_out), .out(diodebackward_15_out));
  not not_3 (not_3_out, Y_0);
  DiodeBackward #(.Blown("true")) diodebackward_33 (.in(Y_0), .out(diodebackward_1_out));
  DiodeBackward diodebackward_34 (.in(not_3_out), .out(diodebackward_1_out));
  DiodeBackward diodebackward_35 (.in(Y_0), .out(diodebackward_3_out));
  DiodeBackward diodebackward_36 (.in(not_3_out), .out(diodebackward_3_out));
  DiodeBackward diodebackward_37 (.in(Y_0), .out(diodebackward_5_out));
  DiodeBackward diodebackward_38 (.in(not_3_out), .out(diodebackward_5_out));
  DiodeBackward diodebackward_39 (.in(Y_0), .out(diodebackward_7_out));
  DiodeBackward diodebackward_40 (.in(not_3_out), .out(diodebackward_7_out));
  DiodeBackward diodebackward_41 (.in(Y_0), .out(diodebackward_9_out));
  DiodeBackward #(.Blown("true")) diodebackward_42 (.in(not_3_out), .out(diodebackward_9_out));
  DiodeBackward #(.Blown("true")) diodebackward_43 (.in(Y_0), .out(diodebackward_11_out));
  DiodeBackward diodebackward_44 (.in(not_3_out), .out(diodebackward_11_out));
  DiodeBackward #(.Blown("true")) diodebackward_45 (.in(Y_0), .out(diodebackward_13_out));
  DiodeBackward diodebackward_46 (.in(not_3_out), .out(diodebackward_13_out));
  DiodeBackward diodebackward_47 (.in(Y_0), .out(diodebackward_15_out));
  DiodeBackward #(.Blown("true")) diodebackward_48 (.in(not_3_out), .out(diodebackward_15_out));
  not not_4 (not_4_out, Y_1);
  DiodeBackward #(.Blown("true")) diodebackward_49 (.in(Y_1), .out(diodebackward_1_out));
  DiodeBackward #(.Blown("true")) diodebackward_50 (.in(not_4_out), .out(diodebackward_1_out));
  DiodeBackward diodebackward_51 (.in(Y_1), .out(diodebackward_3_out));
  DiodeBackward diodebackward_52 (.in(not_4_out), .out(diodebackward_3_out));
  DiodeBackward diodebackward_53 (.in(Y_1), .out(diodebackward_5_out));
  DiodeBackward diodebackward_54 (.in(not_4_out), .out(diodebackward_5_out));
  DiodeBackward diodebackward_55 (.in(Y_1), .out(diodebackward_7_out));
  DiodeBackward diodebackward_56 (.in(not_4_out), .out(diodebackward_7_out));
  DiodeBackward #(.Blown("true")) diodebackward_57 (.in(Y_1), .out(diodebackward_9_out));
  DiodeBackward diodebackward_58 (.in(not_4_out), .out(diodebackward_9_out));
  DiodeBackward diodebackward_59 (.in(Y_1), .out(diodebackward_11_out));
  DiodeBackward #(.Blown("true")) diodebackward_60 (.in(not_4_out), .out(diodebackward_11_out));
  DiodeBackward #(.Blown("true")) diodebackward_61 (.in(Y_1), .out(diodebackward_13_out));
  DiodeBackward diodebackward_62 (.in(not_4_out), .out(diodebackward_13_out));
  DiodeBackward diodebackward_63 (.in(Y_1), .out(diodebackward_15_out));
  DiodeBackward #(.Blown("true")) diodebackward_64 (.in(not_4_out), .out(diodebackward_15_out));
  PullUp pullup_1 (.out(diodebackward_1_out));
  PullUp pullup_2 (.out(diodebackward_3_out));
  or or_1 (or_1_out, diodebackward_1_out, diodebackward_3_out, diodebackward_5_out, diodebackward_7_out);
  PullUp pullup_3 (.out(diodebackward_5_out));
  PullUp pullup_4 (.out(diodebackward_7_out));
  PullUp pullup_5 (.out(diodebackward_9_out));
  PullUp pullup_6 (.out(diodebackward_11_out));
  or or_2 (or_2_out, diodebackward_9_out, diodebackward_11_out, diodebackward_13_out, diodebackward_15_out);
  PullUp pullup_7 (.out(diodebackward_13_out));
  PullUp pullup_8 (.out(diodebackward_15_out));
  D_FF MC0 (.D(or_1_out), .C(C), .Q(MC0_q));  // open: nQ
  D_FF MC1 (.D(or_2_out), .C(C), .Q(MC1_q));  // open: nQ
  Multiplexer multiplexer_1 (.sel(pullup_9_out), .in_0(or_1_out), .in_1(MC0_q), .out(Y_0));
  Multiplexer multiplexer_2 (.sel(pullup_10_out), .in_0(or_2_out), .in_1(MC1_q), .out(Y_1));
  PullUp pullup_9 (.out(pullup_9_out));
  DiodeBackward #(.Blown("true")) diodebackward_65 (.in(1'b0), .out(pullup_9_out));
  PullUp pullup_10 (.out(pullup_10_out));
  DiodeBackward #(.Blown("true")) diodebackward_66 (.in(1'b0), .out(pullup_10_out));
endmodule

/* Test case Up-Down Counter:
A B C   Y_1 Y_0
# count up
0 0 C   0   1
0 0 C   1   0
0 0 C   1   1
0 0 C   0   0


# count down
1 0 C   1   1
1 0 C   1   0
1 0 C   0   1
1 0 C   0   0
*/
