// Digital circuit PullDown2.dig as structural Verilog
module PullDown2 (
  input  A,
  output Y
);

  PullDown pulldown_1 (.out(A));
  PullDown pulldown_2 (.out(A));

  assign Y = A;
endmodule

/* Test case:
A Y
1 1
0 0
Z 0
*/
