// Digital circuit PullUp2.dig as structural Verilog
module PullUp2 (
  input  A,
  output Y
);

  PullUp pullup_1 (.out(A));
  PullUp pullup_2 (.out(A));

  assign Y = A;
endmodule

/* Test case:
A Y
1 1
0 0
Z 1
*/
