// Digital circuit PullUpAndDownError.dig as structural Verilog
module PullUpAndDownError (
  input  A,
  output Y
);

  PullUp pullup_1 (.out(A));
  PullDown pulldown_1 (.out(A));

  assign Y = A;
endmodule
