// Digital circuit power3Error.dig as structural Verilog
module power3Error (
);

  wire not_1_out;

  not not_1 (not_1_out, 1'b0);
  PowerSupply powersupply_1 (.VDD(not_1_out), .GND(1'b0));
endmodule
