// Digital circuit prng.dig as structural Verilog
module prng (
  input  C,
  output [7:0] Y
);

  wire jk_ff_1_nq;

  JK_FF jk_ff_1 (.J(1'b1), .C(C), .K(1'b0), .nQ(jk_ff_1_nq));  // open: Q
  PRNG #(.Bits(8)) prng_1 (.S(8'h1), .se(jk_ff_1_nq), .ne(1'b1), .C(C), .R(Y));
endmodule

/* Test case:
C Y
c 0xd8
c 0x92
c 0xf0
c 0xdd
c 0x68
c 0x12
c 0x7e
c 0xe4
c 0xfc
*/
