// Digital circuit programTestData.dig as structural Verilog
module programTestData (
  input  C,
  output [7:0] Out
);

  wire [7:0] counter_1_out;

  Counter #(.Bits(8)) counter_1 (.en(1'b1), .C(C), .clr(1'b0), .out(counter_1_out));  // open: ovf
  ROM #(.AddrBits(8), .isProgramMemory("true"), .Bits(8)) rom_1 (.A(counter_1_out), .sel(1'b1), .D(Out));
endmodule

/* Test case Test 1:
C Out

program(1,2,3,4)

0  1
C  2
C  3
C  4
C  0
*/

/* Test case Test 2:
C Out

program(0x5,0x6,0x7,0x8)

0  5
C  6
C  7
C  8
C  0
*/
