// Digital circuit programTestSignal.dig as structural Verilog
module programTestSignal (
  input  en,
  output [7:0] Out
);

  Register #(.Bits(8)) R (.D({8{1'b0}}), .C(1'b0), .en(en), .Q(Out));
endmodule

/* Test case Test 1:
en Out R

init R=1;

0   1  1
*/

/* Test case Test 2:
en Out R

init R=7;

0   7  7
*/
