// Digital circuit ram.dig as structural Verilog
module ram (
  input  [5:0] A,
  input  [7:0] Din,
  input  WE,
  input  OE,
  input  CS,
  output [7:0] Dout
);

  wire demultiplexer_1_out_0, demultiplexer_1_out_1, demultiplexer_1_out_2, demultiplexer_1_out_3;

  Demultiplexer #(.Selector_Bits(2)) demultiplexer_1 (
    .sel(A[5:4]), .in(CS), .out_0(demultiplexer_1_out_0), .out_1(demultiplexer_1_out_1),
    .out_2(demultiplexer_1_out_2), .out_3(demultiplexer_1_out_3));
  RAMSinglePortSel #(.AddrBits(4), .Bits(8), .Addr_Bits(4)) ramsingleportsel_1 (
    .A(A[3:0]), .CS(demultiplexer_1_out_0), .WE(WE), .OE(OE), .D(Din));
  RAMSinglePortSel #(.AddrBits(4), .Bits(8), .Addr_Bits(4)) ramsingleportsel_2 (
    .A(A[3:0]), .CS(demultiplexer_1_out_1), .WE(WE), .OE(OE), .D(Din));
  RAMSinglePortSel #(.AddrBits(4), .Bits(8), .Addr_Bits(4)) ramsingleportsel_3 (
    .A(A[3:0]), .CS(demultiplexer_1_out_2), .WE(WE), .OE(OE), .D(Din));
  RAMSinglePortSel #(.AddrBits(4), .Bits(8), .Addr_Bits(4)) ramsingleportsel_4 (
    .A(A[3:0]), .CS(demultiplexer_1_out_3), .WE(WE), .OE(OE), .D(Din));

  assign Dout = Din;
endmodule

/* Test case:
CS A WE OE Din Dout

# write some values
 1  0 C 0 7   X
 1 10 C 0 8   X
 1 20 C 0 9   X
 1 30 C 0 10  X
 1 40 C 0 11  X
 1 50 C 0 12  X
 1 60 C 0 13  X

# read some values
 1  0 0 1 Z   7
 1 10 0 1 Z   8   
 1 20 0 1 Z   9   
 1 30 0 1 Z   10  
 1 40 0 1 Z   11  
 1 50 0 1 Z   12  
 1 60 0 1 Z   13  

# read with CS=0 does not work
 0 50 0 0 Z   Z  
 0 60 0 0 Z   Z  

# write with CS=0 does not work
 0  1 C 0 7   X
 0  2 C 0 7   X
 1  1 0 1 Z   0
 1  2 0 1 Z   0   
*/
