// Digital circuit rndReset.dig as structural Verilog
module rndReset (
  input  [7:0] adr,
  input  [7:0] in,
  input  we,
  output [7:0] out
);

  RAMAsync #(.AddrBits(8), .Bits(8)) ramasync_1 (.A(adr), .D(in), .we(we), .Q(out));
endmodule

/* Test case:
we adr in out

loop(a,256)
let d = random(256);
1 (a) (d) (d)
end loop

resetRandom;

loop(a,256)
let d = random(256);
0 (a) (0) (d)
end loop
*/
