// Digital circuit rom-1-inc.dig as structural Verilog
module rom_1_inc (
  input  [2:0] A,
  input  en,
  output [7:0] D
);

  wire demultiplexer_1_out_0, demultiplexer_1_out_1;

  Demultiplexer demultiplexer_1 (.sel(A[2]), .in(en), .out_0(demultiplexer_1_out_0), .out_1(demultiplexer_1_out_1));
  rom_2_inc u_A (.A(A[1:0]), .en(demultiplexer_1_out_0), .D(D));
  rom_2_inc B (.A(A[1:0]), .en(demultiplexer_1_out_1), .D(D));
endmodule
