// Digital circuit rom-2-inc.dig as structural Verilog
module rom_2_inc (
  input  [1:0] A,
  input  en,
  output [7:0] D
);

  ROM #(.Bits(8)) rom (.A(A), .sel(en), .D(D));

  // Notes on the sheet:
  //   contents of rom (hex, n*v repeats v):
  //   1,2,3,4
endmodule
