// Digital circuit rom.dig as structural Verilog
module rom (
  input  [4:0] A,
  output [7:0] D
);

  wire decoder_1_out_0, decoder_1_out_1, decoder_1_out_2, decoder_1_out_3;

  Decoder #(.Selector_Bits(2)) decoder_1 (
    .sel(A[4:3]), .out_0(decoder_1_out_0), .out_1(decoder_1_out_1), .out_2(decoder_1_out_2),
    .out_3(decoder_1_out_3));
  rom_1_inc R0 (.A(A[2:0]), .en(decoder_1_out_0), .D(D));
  rom_1_inc R1 (.A(A[2:0]), .en(decoder_1_out_1), .D(D));
  rom_1_inc R2 (.A(A[2:0]), .en(decoder_1_out_2), .D(D));
  rom_1_inc R3 (.A(A[2:0]), .en(decoder_1_out_3), .D(D));

  // Notes on the sheet:
  //   contents of R3-B (hex, n*v repeats v):
  //   1d,1e,1f,20
  //   contents of R1-B (hex, n*v repeats v):
  //   d,e,f,10
  //   contents of R2-A (hex, n*v repeats v):
  //   11,12,13,14
  //   contents of R2-B (hex, n*v repeats v):
  //   15,16,17,18
  //   contents of R3-A (hex, n*v repeats v):
  //   19,1a,1b,1c
  //   contents of R0-A (hex, n*v repeats v):
  //   1,2,3,4
  //   contents of R0-B (hex, n*v repeats v):
  //   5,6,7,8
  //   contents of R1-A (hex, n*v repeats v):
  //   9,a,b,c
endmodule

/* Test case:
A D

loop(n, 1<<5)
  (n) (n+1)
end loop
*/
