// Digital circuit 4BitAdder.dig as structural Verilog
module _4BitAdder (
  input  [3:0] A,
  input  [3:0] B,
  input  c_i,
  output [4:0] S
);

  wire adder_1_p4, adder_2_p4, adder_3_p4;

  // Adder adder_1: pin names not known; wires that end beside it: A[0], B[0], c_i, adder_1_p4, S[0]
  // Adder adder_2: pin names not known; wires that end beside it: A[1], B[1], adder_1_p4, adder_2_p4, S[1]
  // Adder adder_3: pin names not known; wires that end beside it: A[2], B[2], adder_2_p4, adder_3_p4, S[2]
  // Adder adder_4: pin names not known; wires that end beside it: A[3], B[3], adder_3_p4, S[4], S[3]
endmodule

/* Test case:
A B c_i S
loop (a,16)
loop (b,16)
loop (c,2)
(a) (b) (c) (a+b+c)
end loop
end loop
end loop
*/
