// Digital circuit BusSplitterHighZ.dig as structural Verilog
module BusSplitterHighZ (
  input  [1:0] A,
  input  Aen,
  input  [1:0] B,
  input  Ben,
  output Q0,
  output Q1,
  output Q2,
  output Q3
);

  assign {Q1, Q0} = Aen ? A : 2'bz;  // Driver driver_1
  assign {Q3, Q2} = Ben ? B : 2'bz;  // Driver driver_2
endmodule

/* Test case:
A B Aen Ben Q3 Q2 Q1 Q0

loop (a,4)
loop (b,4)
(a) (b) 1 1 bits(2,b) bits(2,a)
end loop
end loop

loop (a,4)
(a) x 1 0 Z Z bits(2,a)
end loop

loop (b,4)
x (b) 0 1 bits(2,b) z z
end loop
*/
