// Digital circuit BusSplitterHighZ2.dig as structural Verilog
module BusSplitterHighZ2 (
  input  A0,
  input  A1,
  input  B0,
  input  B1,
  output Q0,
  output Q1
);


  assign B0 = A0;
  assign B1 = A1;
  assign Q0 = A0;
  assign Q1 = A1;
endmodule

/* Test case allEqual:
A1 A0 B1 B0 Q1 Q0
0  0  0  0  0  0
0  1  0  1  0  1
1  0  1  0  1  0
1  1  1  1  1  1



# transitions
0 0 0 0 0 0
0 1 0 1 0 1
0 0 0 0 0 0
1 0 1 0 1 0
0 0 0 0 0 0
1 1 1 1 1 1
0 0 0 0 0 0
0 1 0 1 0 1
1 0 1 0 1 0
0 1 0 1 0 1
1 1 1 1 1 1
0 1 0 1 0 1
1 0 1 0 1 0
1 1 1 1 1 1
1 0 1 0 1 0
*/

/* Test case high Z:
A1 A0 B1 B0 Q1 Q0
z  z  0  0  0  0
z  z  0  1  0  1
z  z  1  0  1  0
z  z  1  1  1  1

0  0  z  z  0  0
0  1  z  z  0  1
1  0  z  z  1  0
1  1  z  z  1  1

0  z  z  0  0  0
0  z  z  1  0  1
1  z  z  0  1  0
1  z  z  1  1  1

z  0  0  z  0  0
z  0  1  z  1  0
z  1  0  z  0  1
z  1  1  z  1  1

z  z  z  0  z  0
z  z  z  1  z  1
z  z  0  z  0  z
z  z  1  z  1  z
z  0  z  z  z  0
z  1  z  z  z  1
0  z  z  z  0  z
1  z  z  z  1  z
*/
