// Digital circuit BusSplitterHighZ3.dig as structural Verilog
module BusSplitterHighZ3 (
  input  [1:0] A,
  input  [1:0] B,
  output Q0,
  output [1:0] Q1,
  output Q2,
  output Q10,
  output Q11
);


  assign Q0 = A[0];
  assign Q1 = {B[0], A[1]};
  assign Q2 = B[1];
  assign Q10 = A[1];
  assign Q11 = B[0];
endmodule

/* Test case:
A B   Q0 Q1 Q2

0 0   0  0  0
0 1   0  2  0
0 2   0  0  1
0 3   0  2  1
1 0   1  0  0
1 1   1  2  0
1 2   1  0  1
1 3   1  2  1
2 0   0  1  0
2 1   0  3  0
2 2   0  1  1
2 3   0  3  1
3 0   1  1  0
3 1   1  3  0
3 2   1  1  1
3 3   1  3  1

z 0   z  x  0
0 z   0  x  z
Z z   Z  x  z
*/

/* Test case:
A B   Q10 Q11

z 0   z  0
z 1   z  1

0 z   0  z
2 z   1  z
*/
