// Digital circuit splitter1.dig as structural Verilog
module splitter1 (
  input  [7:0] A,
  output [3:0] X,
  output [5:0] Z,
  output [3:0] Y
);


  assign X = A[7:4];
  assign Y = A[3:0];
  assign Z = A[5:0];
endmodule

/* Test case:
             A  X           Y      Z
repeat(256) (n) ((n>>4)&15) (n&15) (n&63)
*/
