// Digital circuit splitter1Error.dig as structural Verilog
module splitter1Error (
  input  A,
  input  [5:0] B,
  output [3:0] X,
  output [5:0] Z,
  output [3:0] Y,
  output [3:0] U
);


  assign U = B[4:1];
  assign X[2:0] = B[5:3];
  assign Y = {B[2:0], A};
  assign Z = {B[4:0], A};
endmodule
