// Digital circuit splitter2.dig as structural Verilog
module splitter2 (
  input  [3:0] A,
  input  [3:0] B,
  output [3:0] X,
  output [5:0] Z,
  output [3:0] Y,
  output [3:0] U
);


  assign U = {B[1:0], A[3:2]};
  assign X = B;
  assign Y = A;
  assign Z = {B[1:0], A};
endmodule

/* Test case:
            A      B        X           Y      Z      U
repeat(256) (n&15) (n>>4)   ((n>>4)&15) (n&15) (n&63) ((n>>2)&15)
*/
