// Digital circuit splitter2Error.dig as structural Verilog
module splitter2Error (
  input  A,
  input  [8:0] B,
  output [3:0] X,
  output [5:0] Z,
  output [3:0] Y,
  output [3:0] U
);

  // Pins of 8 and 9 bits meet at {B[8:1], A}

  assign B[0] = A;
  assign U = B[5:2];
  assign X = B[7:4];
  assign Y = {B[3:1], A};
  assign Z = {B[5:1], A};
endmodule
