// Digital circuit splitter3.dig as structural Verilog
module splitter3 (
  input  A,
  input  [6:0] B,
  output [3:0] X,
  output [5:0] Z,
  output [3:0] Y,
  output [3:0] U
);


  assign U = B[4:1];
  assign X = B[6:3];
  assign Y = {B[2:0], A};
  assign Z = {B[4:0], A};
endmodule

/* Test case:
            A      B        X           Y      Z      U
repeat(256) (n&1) (n>>1)   ((n>>4)&15) (n&15) (n&63) ((n>>2)&15)
*/
