// Digital circuit splitter3Error.dig as structural Verilog
module splitter3Error (
  input  A,
  input  [6:0] B,
  output [3:0] X,
  output [5:0] Z,
  output [3:0] Y,
  output [3:0] U
);

  // Pins of 6 and 7 bits meet at B

  assign U = B[3:0];
  assign X = B[5:2];
  assign {Y[3:2], Y[0]} = {B[1:0], A};
  assign Z = {B[3:0], Y[1], A};
endmodule
