// Digital circuit splitter4.dig as structural Verilog
module splitter4 (
  input  [3:0] A,
  output X,
  output Z,
  output Y,
  output U
);


  assign U = A[0];
  assign X = A[3];
  assign Y = A[2];
  assign Z = A[1];
endmodule

/* Test case:
             A  X           Y      Z      U
repeat(16)  (n) ((n>>3)&1)  ((n>>2)&1) ((n>>1)&1) (n&1)
*/
