// Digital circuit DmitryVyal1.dig as structural Verilog
module DmitryVyal1 (
  input  A,
  output Y,
  output X
);

  PullUp pullup_1 (.out(X));
  // RelayDT relaydt_1: pin names not known; wires that end beside it: A, X, 1'b0, 1'b0, Y
endmodule

/* Test case:
A X Y
0 1 1
1 0 z
0 1 1
1 0 z
*/
