// Digital circuit DmitryVyal2.dig as structural Verilog
module DmitryVyal2 (
  input  A,
  output Y,
  output X
);

  // RelayDT relaydt_1: pin names not known; wires that end beside it: A, 1'b1, 1'b0, Y, X
  PullDown pulldown_1 (.out(X));
  PullDown pulldown_2 (.out(Y));
endmodule

/* Test case:
A X Y
0 1 0
1 0 1
0 1 0
1 0 1
*/
