// Digital circuit DmitryVyal3.dig as structural Verilog
module DmitryVyal3 (
  input  A,
  output Y
);

  // RelayDT relaydt_1: pin names not known; wires that end beside it: A, Y, 1'b0, 1'b1, 1'b0
  PullDown pulldown_1 (.out(Y));
endmodule

/* Test case:
A Y
0 0
1 1
0 0
1 1
*/
