// Digital circuit DmitryVyal_bug480.dig as structural Verilog
module DmitryVyal_bug480 (
  input  A,
  input  B,
  input  C,
  input  D,
  output Y,
  output X,
  output Z,
  output U
);

  // RelayDT S4: pin names not known; wires that end beside it: 1'b0, 1'b1, Y, 1'b0, D
  // RelayDT S3: pin names not known; wires that end beside it: Y, 1'b1, X, 1'b0, C
  // RelayDT S2: pin names not known; wires that end beside it: X, 1'b1, Z, 1'b0, B
  // RelayDT S1: pin names not known; wires that end beside it: Z, 1'b1, U, 1'b0, A
endmodule

/* Test case comb:
 D C B A Y X Z U 

 0 0 0 0 0 0 0 0
 0 0 0 1 0 0 0 1
 0 0 1 0 0 0 1 1
 0 0 1 1 0 0 1 1
 0 1 0 0 0 1 1 1
 0 1 0 1 0 1 1 1
 0 1 1 0 0 1 1 1
 0 1 1 1 0 1 1 1
 1 0 0 0 1 1 1 1
 1 0 0 1 1 1 1 1
 1 0 1 0 1 1 1 1
 1 0 1 1 1 1 1 1
 1 1 0 0 1 1 1 1
 1 1 0 1 1 1 1 1
 1 1 1 0 1 1 1 1
 1 1 1 1 1 1 1 1
 
*/

/* Test case #480:
 D C B A Y X Z U 

 0 0 0 0 0 0 0 0
 0 0 1 0 0 0 1 1
 0 0 0 0 0 0 0 0
 0 0 0 1 0 0 0 1
 0 0 0 0 0 0 0 0
 0 1 0 0 0 1 1 1
 0 0 0 0 0 0 0 0
 1 0 0 0 1 1 1 1
 0 0 0 0 0 0 0 0
*/
