// Digital circuit FGNFETs.dig as structural Verilog
module FGNFETs (
  input  A_1,
  input  A_2,
  output Y_1,
  output Y_2
);

  FGNFET fgnfet_1 (.G(A_1), .D(Y_1), .S(1'b0));
  PullUp pullup_1 (.out(Y_1));
  PullUp pullup_2 (.out(Y_2));
  FGNFET #(.Blown("true")) fgnfet_2 (.G(A_2), .D(Y_2), .S(1'b0));
endmodule

/* Test case:
A_1 Y_1
 0   1
 1   0 
 z   1 
*/

/* Test case:
A_2 Y_2
 0   1
 1   1 
 z   1 
*/
