// Digital circuit FGPFETs.dig as structural Verilog
module FGPFETs (
  input  A_1,
  input  A_2,
  output Y_1,
  output Y_2
);

  FGPFET fgpfet_1 (.G(A_1), .S(1'b1), .D(Y_1));
  PullDown pulldown_1 (.out(Y_1));
  FGPFET #(.Blown("true")) fgpfet_2 (.G(A_2), .S(1'b1), .D(Y_2));
  PullDown pulldown_2 (.out(Y_2));
endmodule

/* Test case:
A_1 Y_1
 0  1
 1  0
 Z  0
*/

/* Test case:
A_2 Y_2
 0  0
 1  0
 Z  0
*/
