// Digital circuit Heintz_A.dig as structural Verilog
module Heintz_A (
  input  A,
  input  B,
  output Y_1,
  output Y_0
);

  // Relay #(.relayNormallyClosed("true")) relay_1: pin names not known; wires that end beside it: A, 1'b0, 1'b1, Y_0, A, 1'b0
  // Relay relay_2: pin names not known; wires that end beside it: B, 1'b0, Y_0, Y_1
  // Relay relay_3: pin names not known; wires that end beside it: Y_1, Y_0
endmodule

/* Test case:
A B Y_0 Y_1
0 0  1   z
0 1  1   1
1 0  z   z
1 1  z   z

# transitions
0 0 1 Z
0 1 1 1
0 0 1 Z
1 0 Z Z
0 0 1 Z
1 1 Z Z
0 0 1 Z
0 1 1 1
1 0 Z Z
0 1 1 1
1 1 Z Z
0 1 1 1
1 0 Z Z
1 1 Z Z
1 0 Z Z
*/
