// Digital circuit Heintz_A_DT.dig as structural Verilog
module Heintz_A_DT (
  input  A,
  input  B,
  output Y_1,
  output Y_0
);

  wire relaydt_1_p3, relaydt_1_p7, relaydt_1_p10;

  // RelayDT #(.poles(2), .relayNormallyClosed("true")) relaydt_1: pin names not known; wires that end beside it: A, 1'b0, relaydt_1_p3, relaydt_1_p3, Y_0, 1'b1, relaydt_1_p7, Y_1, Y_0, relaydt_1_p10, relaydt_1_p10
  // RelayDT relaydt_2: pin names not known; wires that end beside it: B, 1'b0, Y_0, Y_1, relaydt_1_p7
endmodule

/* Test case:
A B Y_0 Y_1
0 0  1   z
0 1  1   1
1 0  z   z
1 1  z   z

# transitions
0 0 1 Z
0 1 1 1
0 0 1 Z
1 0 Z Z
0 0 1 Z
1 1 Z Z
0 0 1 Z
0 1 1 1
1 0 Z Z
0 1 1 1
1 1 Z Z
0 1 1 1
1 0 Z Z
1 1 Z Z
1 0 Z Z
*/
