// Digital circuit burn.dig as structural Verilog
module burn (
  input  A,
  output Y
);

  // Relay relay_1: pin names not known; wires that end beside it: A, 1'b1, 1'b0

  assign Y = 1'b1;
endmodule

/* Test case Failing:
A Y
1 1
*/
