// Digital circuit burn2.dig as structural Verilog
module burn2 (
  input  A,
  output Y
);

  wire pullup_1_out, relay_1_p3;

  PullUp pullup_1 (.out(pullup_1_out));
  // Relay relay_1: pin names not known; wires that end beside it: A, pullup_1_out, relay_1_p3
  PullDown pulldown_1 (.out(relay_1_p3));

  assign Y = 1'b1;
endmodule

/* Test case Failing:
A Y
1 1
*/
