// Digital circuit const.dig as structural Verilog
module \const  (
  input  A_1,
  input  A_2,
  input  A_3,
  output Y_1,
  output Y_2,
  output Y_3,
  output X_1,
  output X_2,
  output X_3
);

  // RelayDT relaydt_1: pin names not known; wires that end beside it: A_1, 1'b0, 1'b1, X_1, Y_1
  PullDown pulldown_1 (.out(X_1));
  PullDown pulldown_2 (.out(Y_1));
  // RelayDT relaydt_2: pin names not known; wires that end beside it: A_2, 1'b0, Y_2, X_2, 1'b1
  PullDown pulldown_3 (.out(X_2));
  // RelayDT relaydt_3: pin names not known; wires that end beside it: A_3, 1'b0, Y_3, 1'b1, X_3
  PullDown pulldown_4 (.out(Y_2));
  PullDown pulldown_5 (.out(Y_3));
  PullDown pulldown_6 (.out(X_3));

  // Notes on the sheet:
  //   see issue #255
endmodule

/* Test case:
A_1 Y_1 X_1
0  0   0
1  0   1
0  0   0
1  0   1
*/

/* Test case:
A_2 Y_2 X_2
0  0   1
1  0   0
0  0   1
1  0   0
*/

/* Test case:
A_3 Y_3 X_3
0  0   1
1  1   0
0  0   1
1  1   0
*/
