// Digital circuit const2.dig as structural Verilog
module const2 (
  input  A_1,
  input  A_2,
  input  A_3,
  input  A_4,
  input  A_5,
  output Y_1,
  output Y_2,
  output Y_3,
  output X_1,
  output X_2,
  output X_3,
  output Y_4,
  output X_4,
  output Y_5,
  output X_5
);

  // RelayDT relaydt_1: pin names not known; wires that end beside it: A_1, 1'b0, 1'b1, X_1, Y_1
  PullDown pulldown_1 (.out(X_1));
  // RelayDT relaydt_2: pin names not known; wires that end beside it: A_4, 1'b0, 1'b1, X_4, Y_4
  PullDown pulldown_2 (.out(Y_4));
  // RelayDT relaydt_3: pin names not known; wires that end beside it: A_2, 1'b0, Y_2, X_2, 1'b1
  PullDown pulldown_3 (.out(X_2));
  // RelayDT relaydt_4: pin names not known; wires that end beside it: A_3, 1'b0, Y_3, 1'b1, X_3
  // RelayDT relaydt_5: pin names not known; wires that end beside it: A_5, 1'b0, 1'b1, X_5, Y_5
  PullDown pulldown_4 (.out(Y_5));

  // Notes on the sheet:
  //   see issue #255
endmodule

/* Test case 1:
A_1 Y_1 X_1
0  0   0
1  z   1
0  0   0
1  z   1
*/

/* Test case 4:
A_4 Y_4 X_4
0  0   0
1  0   1
0  0   0
1  0   1
*/

/* Test case 2:
A_2 Y_2 X_2
0  z   1
1  0   0
0  z   1
1  0   0
*/

/* Test case 3:
A_3 Y_3 X_3
0  z   1
1  1   z
0  z   1
1  1   z
*/

/* Test case 5:
A_5 Y_5 X_5
0  0   0
1  0   1
0  0   0
1  0   1
*/
