// Digital circuit const3.dig as structural Verilog
module const3 (
  input  A_2,
  input  A_1,
  output Y_2,
  output Y_1
);

  // RelayDT relaydt_1: pin names not known; wires that end beside it: A_1, 1'b0, 1'b1, Y_1, 1'b0
  // RelayDT relaydt_2: pin names not known; wires that end beside it: A_2, 1'b0, 1'b1, Y_2, 1'b0
  PullDown pulldown_1 (.out(Y_2));

  // Notes on the sheet:
  //   see issue #255
endmodule

/* Test case:
A_1 Y_1 
 0   0   
 1   1   
 0   0   
 1   1   
*/

/* Test case:
A_2 Y_2 
 0   0   
 1   1   
 0   0   
 1   1   
*/
