// Digital circuit highZ-DT.dig as structural Verilog
module highZ_DT (
  input  A,
  input  B,
  output Y_1,
  output Y_0
);

  // RelayDT #(.relayNormallyClosed("true")) relaydt_1: pin names not known; wires that end beside it: A, B, Y_1, B, Y_0
endmodule

/* Test case:
A B Y_0 Y_1
0 0  0   z
0 1  z   1
0 z  z   z
1 0  z   0
1 1  1   z
1 z  z   z
z 0  0   z
z 1  1   z
z z  z   z
*/
