// Digital circuit highZ-DT2.dig as structural Verilog
module highZ_DT2 (
  input  A,
  output Y
);

  // RelayDT #(.relayNormallyClosed("true")) relaydt_1: pin names not known; wires that end beside it: A, 1'b0, Y, 1'b1
endmodule

/* Test case:
A Y
0 1
1 Z
0 1
1 Z
*/
