// Digital circuit highZ-DT3.dig as structural Verilog
module highZ_DT3 (
  input  A,
  output Y
);

  // RelayDT #(.relayNormallyClosed("true")) relaydt_1: pin names not known; wires that end beside it: A, 1'b0, 1'b1, Y
endmodule

/* Test case:
A Y
0 Z
1 1
0 Z
1 1
*/
