// Digital circuit highZ-DT4.dig as structural Verilog
module highZ_DT4 (
  input  A,
  output Y
);

  // RelayDT #(.relayNormallyClosed("true")) relaydt_1: pin names not known; wires that end beside it: A, 1'b0, 1'b0, Y
endmodule

/* Test case:
A Y
0 Z
1 0
0 Z
1 0
*/
