// Digital circuit highZ.dig as structural Verilog
module highZ (
  input  A,
  input  B,
  output Y
);

  // Relay relay_1: pin names not known; wires that end beside it: A, B, Y, B
endmodule

/* Test case:
A B Y 
0 0  z
0 1  1
0 z  z
1 0  0
1 1  z
1 z  z
z 0  z
z 1  z
z z  z
*/
