// Digital circuit no_net2.dig as structural Verilog
module no_net2 (
  input  O,
  output Y
);

  // Relay relay_1: pin names not known; wires that end beside it: 1'b1, Y, O, 1'b0
endmodule

/* Test case:
O Y
0 z
1 1
*/
