// Digital circuit relayFullAdder.dig as structural Verilog
module relayFullAdder (
  input  A,
  input  B,
  input  C,
  output Sum,
  output Carry
);

  wire relaydt_1_p3, relaydt_1_p4, relaydt_1_p5, relaydt_2_p3, relaydt_2_p5, relaydt_2_p11, relaydt_2_p16,
       relaydt_3_p3, relaydt_3_p4, relaydt_3_p5, relaydt_4_p2;

  // RelayDT #(.poles(2)) relaydt_1: pin names not known; wires that end beside it: 1'b1, 1'b1, relaydt_1_p3, relaydt_1_p4, relaydt_1_p5
  // RelayDT #(.poles(2)) relaydt_2: pin names not known; wires that end beside it: A, 1'b0, relaydt_2_p3, relaydt_1_p4, relaydt_2_p5, relaydt_2_p3, relaydt_1_p3, relaydt_1_p5, relaydt_2_p5, B, relaydt_2_p11, Carry, 1'b0, relaydt_2_p11, 1'b0, relaydt_2_p16
  // RelayDT #(.poles(2)) relaydt_3: pin names not known; wires that end beside it: 1'b1, 1'b1, relaydt_3_p3, relaydt_3_p4, relaydt_3_p5
  PullDown pulldown_1 (.out(Sum));
  // RelayDT #(.poles(2)) relaydt_4: pin names not known; wires that end beside it: relaydt_3_p4, relaydt_4_p2, relaydt_2_p16, relaydt_3_p3, relaydt_3_p5, relaydt_4_p2, C, Sum, Carry, 1'b0
  PullDown pulldown_2 (.out(Carry));
endmodule

/* Test case:
A B C Sum Carry
loop (C,2)
loop (A,2)
loop (B,2)
let s=A+B+C;
 (A) (B) (C) (s&1) (s>>1)
end loop
end loop
end loop
*/
