// Digital circuit relayFullAdder2.dig as structural Verilog
module relayFullAdder2 (
  input  [3:0] A,
  input  [3:0] B,
  input  C_in,
  output [3:0] S,
  output C_out
);

  wire relaydt_1_p4, relaydt_1_p5, relaydt_1_p6, relaydt_2_p4, relaydt_2_p5, relaydt_2_p6, relaydt_3_p4,
       relaydt_3_p5, relaydt_3_p6, relaydt_4_p3, relaydt_4_p4, relaydt_4_p5, relaydt_5_p3, relaydt_5_p5,
       relaydt_5_p11, relaydt_5_p12, relaydt_5_p16, relaydt_6_p2, relaydt_6_p4, relaydt_6_p10, relaydt_6_p11,
       relaydt_6_p15, relaydt_7_p2, relaydt_7_p4, relaydt_7_p10, relaydt_7_p11, relaydt_7_p15, relaydt_8_p2,
       relaydt_8_p4, relaydt_8_p10, relaydt_8_p15, relaydt_9_p3, relaydt_9_p4, relaydt_9_p5, relaydt_10_p3,
       relaydt_10_p4, relaydt_10_p5, relaydt_11_p3, relaydt_11_p4, relaydt_11_p5, relaydt_12_p3,
       relaydt_12_p4, relaydt_12_p5, relaydt_13_p2, relaydt_14_p2, relaydt_15_p2, relaydt_16_p2;

  // RelayDT #(.poles(2)) relaydt_1: pin names not known; wires that end beside it: 1'b1, 1'b1, A[1], relaydt_1_p4, relaydt_1_p5, relaydt_1_p6
  // RelayDT #(.poles(2)) relaydt_2: pin names not known; wires that end beside it: 1'b1, 1'b1, A[2], relaydt_2_p4, relaydt_2_p5, relaydt_2_p6
  // RelayDT #(.poles(2)) relaydt_3: pin names not known; wires that end beside it: 1'b1, 1'b1, A[3], relaydt_3_p4, relaydt_3_p5, relaydt_3_p6
  // RelayDT #(.poles(2)) relaydt_4: pin names not known; wires that end beside it: 1'b1, 1'b1, relaydt_4_p3, relaydt_4_p4, relaydt_4_p5
  // RelayDT #(.poles(2)) relaydt_5: pin names not known; wires that end beside it: A[0], 1'b0, relaydt_5_p3, relaydt_1_p5, relaydt_5_p5, relaydt_5_p3, relaydt_1_p4, relaydt_1_p6, relaydt_5_p5, B[0], relaydt_5_p11, relaydt_5_p12, 1'b0, relaydt_5_p11, 1'b0, relaydt_5_p16
  // RelayDT #(.poles(2)) relaydt_6: pin names not known; wires that end beside it: 1'b0, relaydt_6_p2, relaydt_2_p5, relaydt_6_p4, relaydt_6_p2, relaydt_2_p4, relaydt_2_p6, relaydt_6_p4, B[1], relaydt_6_p10, relaydt_6_p11, 1'b0, relaydt_6_p10, 1'b0, relaydt_6_p15
  // RelayDT #(.poles(2)) relaydt_7: pin names not known; wires that end beside it: 1'b0, relaydt_7_p2, relaydt_3_p5, relaydt_7_p4, relaydt_7_p2, relaydt_3_p4, relaydt_3_p6, relaydt_7_p4, B[2], relaydt_7_p10, relaydt_7_p11, 1'b0, relaydt_7_p10, 1'b0, relaydt_7_p15
  // RelayDT #(.poles(2)) relaydt_8: pin names not known; wires that end beside it: 1'b0, relaydt_8_p2, relaydt_4_p4, relaydt_8_p4, relaydt_8_p2, relaydt_4_p3, relaydt_4_p5, relaydt_8_p4, B[3], relaydt_8_p10, C_out, 1'b0, relaydt_8_p10, 1'b0, relaydt_8_p15
  // RelayDT #(.poles(2)) relaydt_9: pin names not known; wires that end beside it: 1'b1, 1'b1, relaydt_9_p3, relaydt_9_p4, relaydt_9_p5
  // RelayDT #(.poles(2)) relaydt_10: pin names not known; wires that end beside it: 1'b1, 1'b1, relaydt_10_p3, relaydt_10_p4, relaydt_10_p5
  // RelayDT #(.poles(2)) relaydt_11: pin names not known; wires that end beside it: 1'b1, 1'b1, relaydt_11_p3, relaydt_11_p4, relaydt_11_p5
  // RelayDT #(.poles(2)) relaydt_12: pin names not known; wires that end beside it: 1'b1, 1'b1, relaydt_12_p3, relaydt_12_p4, relaydt_12_p5
  // RelayDT #(.poles(2)) relaydt_13: pin names not known; wires that end beside it: relaydt_9_p4, relaydt_13_p2, relaydt_5_p16, relaydt_9_p3, relaydt_9_p5, relaydt_13_p2, C_in, S[0], relaydt_5_p12, 1'b0
  // RelayDT #(.poles(2)) relaydt_14: pin names not known; wires that end beside it: relaydt_10_p4, relaydt_14_p2, relaydt_6_p15, relaydt_10_p3, relaydt_10_p5, relaydt_14_p2, relaydt_5_p12, S[1], relaydt_6_p11, 1'b0
  // RelayDT #(.poles(2)) relaydt_15: pin names not known; wires that end beside it: relaydt_11_p4, relaydt_15_p2, relaydt_7_p15, relaydt_11_p3, relaydt_11_p5, relaydt_15_p2, relaydt_6_p11, S[2], relaydt_7_p11, 1'b0
  // RelayDT #(.poles(2)) relaydt_16: pin names not known; wires that end beside it: relaydt_12_p4, relaydt_16_p2, relaydt_8_p15, relaydt_12_p3, relaydt_12_p5, relaydt_16_p2, relaydt_7_p11, S[3], C_out, 1'b0
  PullDown #(.Bits(4)) pulldown_1 (.out(S));
  PullDown pulldown_2 (.out(C_out));
endmodule

/* Test case:
A B C_in S C_out
loop (C,2)
loop (A,16)
loop (B,16)
let s=A+B+C;
 (A) (B) (C) (s&15) (s>>4)
end loop
end loop
end loop
*/
