// Digital circuit switch1.dig as structural Verilog
module switch1 (
  input  A,
  input  B,
  input  C,
  output Y
);

  wire relay_1_p4;

  // Relay relay_1: pin names not known; wires that end beside it: A, 1'b1, 1'b0, relay_1_p4
  // Relay relay_2: pin names not known; wires that end beside it: C, relay_1_p4, B, 1'b0, Y, 1'b0
  // Relay relay_3: pin names not known; wires that end beside it: relay_1_p4, Y
endmodule

/* Test case:
A B C Y
0 0 0 Z
0 0 1 Z
0 1 0 Z
0 1 1 Z
1 0 0 Z
1 0 1 1
1 1 0 1
1 1 1 1

# transitions
0 0 0 Z
0 0 1 Z
0 0 0 Z
0 1 0 Z
0 0 0 Z
0 1 1 Z
0 0 0 Z
1 0 0 Z
0 0 0 Z
1 0 1 1
0 0 0 Z
1 1 0 1
0 0 0 Z
1 1 1 1
0 0 0 Z
0 0 1 Z
0 1 0 Z
0 0 1 Z
0 1 1 Z
0 0 1 Z
1 0 0 Z
0 0 1 Z
1 0 1 1
0 0 1 Z
1 1 0 1
0 0 1 Z
1 1 1 1
0 0 1 Z
0 1 0 Z
0 1 1 Z
0 1 0 Z
1 0 0 Z
0 1 0 Z
1 0 1 1
0 1 0 Z
1 1 0 1
0 1 0 Z
1 1 1 1
0 1 0 Z
0 1 1 Z
1 0 0 Z
0 1 1 Z
1 0 1 1
0 1 1 Z
1 1 0 1
0 1 1 Z
1 1 1 1
0 1 1 Z
1 0 0 Z
1 0 1 1
1 0 0 Z
1 1 0 1
1 0 0 Z
1 1 1 1
1 0 0 Z
1 0 1 1
1 1 0 1
1 0 1 1
1 1 1 1
1 0 1 1
1 1 0 1
1 1 1 1
1 1 0 1
*/
