// Digital circuit switch2.dig as structural Verilog
module switch2 (
  input  A,
  input  [7:0] B,
  output [7:0] Y
);

  // Relay #(.Bits(8)) relay_1: pin names not known; wires that end beside it: A, B, 1'b0, Y
endmodule

/* Test case:
A B Y
0 0 z 
0 7 z 
1 0 0 
1 7 7 
*/
