// Digital circuit switchAsInput.dig as structural Verilog
module switchAsInput (
  output Y
);

  wire A_a;

  PullUp pullup_1 (.out(Y));
  Switch #(.switchActsAsInput("true")) A (.A(A_a), .B(Y));
  Switch #(.switchActsAsInput("true")) B (.A(1'b0), .B(A_a));
endmodule

/* Test case:
A B Y
0 0 1
0 1 1
1 0 1
1 1 0
*/
