// Digital circuit switch_xor2.dig as structural Verilog
module switch_xor2 (
  input  A,
  input  B,
  output Y
);

  wire relaydt_1_p2, relaydt_1_p3;

  // RelayDT relaydt_1: pin names not known; wires that end beside it: 1'b1, relaydt_1_p2, relaydt_1_p3, relaydt_1_p2
  // RelayDT relaydt_2: pin names not known; wires that end beside it: A, 1'b0, relaydt_1_p3, B, Y, 1'b0
  PullDown pulldown_1 (.out(Y));
endmodule

/* Test case:
A B Y
0 0 0
0 1 1
1 0 1
1 1 0


# transitions
0 0 0
0 1 1
0 0 0
1 0 1
0 0 0
1 1 0
0 0 0
0 1 1
1 0 1
0 1 1
1 1 0
0 1 1
1 0 1
1 1 0
1 0 1
*/
