// Digital circuit switch_xor3.dig as structural Verilog
module switch_xor3 (
  input  A,
  input  B,
  output Y
);

  wire R1_p2, R1_p3;

  // RelayDT R1: pin names not known; wires that end beside it: 1'b1, R1_p2, R1_p3, R1_p2
  // RelayDT R2: pin names not known; wires that end beside it: A, 1'b0, R1_p3, B, Y, 1'b0
endmodule

/* Test case:
A B Y
0 0 z
0 1 1
1 0 1
1 1 z


# transitions
0 0 z
0 1 1
0 0 z
1 0 1
0 0 z
1 1 z
0 0 z
0 1 1
1 0 1
0 1 1
1 1 z
0 1 1
1 0 1
1 1 z
1 0 1
*/
