// Digital circuit trans2.dig as structural Verilog
module trans2 (
  input  A,
  input  B,
  output Ao,
  output Bo
);

  // trans trans_1: pin names not known; wires that end beside it: A, B, Ao, Bo

  // Notes on the sheet:
  //   Ao: Ist direkt mit A verbunden.
  //   Bo: Ist direkt mit B verbunden.
endmodule

/* Test case:
A B Ao Bo
1 X 1  X
0 X 0  X
X 1 X  1
X 0 X  0
*/
