// Digital circuit trans3.dig as structural Verilog
module trans3 (
  input  A,
  input  B,
  output Ao,
  output Bo
);

  trans2 trans2_1 (.A(A), .B(B), .Ao(Ao), .Bo(Bo));

  // Notes on the sheet:
  //   Ao: Ist direkt mit A verbunden.
  //   Bo: Ist direkt mit B verbunden.
endmodule

/* Test case:
A B Ao Bo
1 X 1  X
0 X 0  X
X 1 X  1
X 0 X  0
*/
