// Digital circuit transtest2.dig as structural Verilog
module transtest2 (
  input  A,
  input  B,
  output Y
);

  // trans2 trans2_1: pin names not known; wires that end beside it: A, B, Y
endmodule

/* Test case:
A B Y
0 0 0
0 1 1
1 0 1
1 1 0
*/
