// Digital circuit transtest3.dig as structural Verilog
module transtest3 (
  input  A,
  input  B,
  output Y
);

  wire trans3_1_ao, trans3_1_bo;

  trans3 trans3_1 (.A(A), .B(B), .Ao(trans3_1_ao), .Bo(trans3_1_bo));
  xor xor_1 (Y, trans3_1_ao, trans3_1_bo);
endmodule

/* Test case:
A B Y
0 0 0
0 1 1
1 0 1
1 1 0
*/
