// Digital circuit BitSelect.dig as structural Verilog
module BitSelect (
  input  [3:0] A,
  input  [1:0] sel,
  output Y
);

  BitSelector #(.Selector_Bits(2)) bitselector_1 (.in(A), .sel(sel), .out(Y));
endmodule

/* Test case:
A sel Y
5  0  1
5  1  0
5  2  1
5  3  0
10  0  0
10  1  1
10  2  0
10  3  1
*/
