// Digital circuit BitSelect2.dig as structural Verilog
module BitSelect2 (
  input  [15:0] A,
  input  [3:0] sel,
  output Y
);

  BitSelector #(.Selector_Bits(4)) bitselector_1 (.in(A), .sel(sel), .out(Y));
endmodule

/* Test case:
A sel Y
loop (n,16)
0      (n)  0
(1<<n) (n)  1
end loop
*/
