// Digital circuit D-Default.dig as structural Verilog
module D_Default (
  input  C,
  output Q1,
  output Q2
);

  D_FF d_ff_1 (.D(1'b1), .C(C), .Q(Q1));  // open: nQ
  D_FF #(.Default(1)) d_ff_2 (.D(1'b1), .C(C), .Q(Q2));  // open: nQ
endmodule

/* Test case:
C Q1 Q2
0 0  1
C 1  1
*/
