// Digital circuit D-DefaultBus.dig as structural Verilog
module D_DefaultBus (
  input  C,
  output [3:0] Q1,
  output [3:0] Q2
);

  D_FF #(.Bits(4), .Default(5)) d_ff_1 (.D(4'b1111), .C(C), .Q(Q1));  // open: nQ
  D_FF #(.Bits(4), .Default(10)) d_ff_2 (.D(4'b1111), .C(C), .Q(Q2));  // open: nQ
endmodule

/* Test case:
C Q1  Q2
0 5   0xA
C 0xf 0xf
*/
