// Digital circuit adder.dig as structural Verilog
module adder (
  input  [3:0] A,
  input  [3:0] B,
  input  C,
  output [3:0] S,
  output Co
);

  Add #(.Bits(4)) add_1 (.a(A), .b(B), .c_i(C), .s(S), .c_o(Co));
endmodule

/* Test case:
               A     B     C  S                     Co
repeat(256) (n&15) (n>>4)  0  (((n&15)+(n>>4))&15) (((n&15)+(n>>4))>>4)
repeat(256) (n&15) (n>>4)  1  (((n&15)+(n>>4)+1)&15) (((n&15)+(n>>4)+1)>>4)
*/
