// Digital circuit TestLeft32.dig as structural Verilog
module TestLeft32 (
  input  [31:0] D_32_in,
  input  [4:0] sh_32,
  output [31:0] D_32
);

  // barrelShifter #(.generic("dataBits := 32; direction := \"left\";")) _32_bit__left: pin names not known; wires that end beside it: D_32_in, sh_32, D_32

  // Notes on the sheet:
  //   D_32_in: default 1
endmodule

/* Test case left32:
D^32_in sh^32 D^32
loop(n,32) 
   1     (n)  (1<<n)
end loop

loop(n,32) 
   7     (n)  (7<<n)
end loop
*/
