// Digital circuit TestLeft8.dig as structural Verilog
module TestLeft8 (
  input  [7:0] D_8_in,
  input  [2:0] sh_8,
  output [7:0] D_8
);

  // barrelShifter #(.generic("dataBits := 8; direction := \"left\";")) _8_bit__left: pin names not known; wires that end beside it: D_8_in, sh_8, D_8

  // Notes on the sheet:
  //   D_8_in: default 1
endmodule

/* Test case left8:
D^8_in sh^8 D^8
loop(n,8) 
   1     (n)  (1<<n)
end loop

loop(n,8) 
   7     (n)  (7<<n)
end loop
*/
