// Digital circuit TestRight8.dig as structural Verilog
module TestRight8 (
  input  [7:0] D_8_inR,
  input  [2:0] sh_8_R,
  output [7:0] D_8_R
);

  // barrelShifter #(.generic("dataBits := 8; direction := \"right\";")) _8_bit__right: pin names not known; wires that end beside it: D_8_inR, sh_8_R, D_8_R

  // Notes on the sheet:
  //   D_8_inR: default 128
endmodule

/* Test case right8:
D^8_inR sh^8_R D^8_R
loop(n,8) 
   128     (n)  (128>>n)
end loop

loop(n,8) 
   192     (n)  (192>>n)
end loop
*/
