// Digital circuit TestRightArith16.dig as structural Verilog
module TestRightArith16 (
  input  [15:0] D_16_in,
  input  [3:0] sh_16,
  output [15:0] D_16
);

  barrelShifter #(.generic("dataBits := 16; direction := \"arith\";")) _16_bit__right__arith (
    .D_in(D_16_in), .sh(sh_16), .D(D_16));

  // Notes on the sheet:
  //   D_16_in: default 32768
endmodule

/* Test case rightArith16:
D^16_in sh^16 D^16
loop(n,16) 
   (1<<14)     (n)  ((1<<14)>>n)
end loop

loop(n,16) 
   (1<<15)     (n)  (-1<<(15-n))
end loop
*/
