// Digital circuit shift-fixed-arith-right-inc.dig as structural Verilog
module shift_fixed_arith_right_inc (
  input  [7:0] D_in,
  input  en,
  output [7:0] D
);

  wire [7:0] bitextender_1_out;

  BitExtender #(.inputBits(7), .outputBits(8), .generic("this.inputBits=int(args.dataBits-args.shift); this.outputBits=int(args.dataBits);")) bitextender_1 (
    .in(D_in[7:1]), .out(bitextender_1_out));
  Multiplexer #(.Bits(8), .generic("this.Bits=int(args.dataBits);")) multiplexer_1 (
    .sel(en), .in_0(D_in), .in_1(bitextender_1_out), .out(D));
endmodule

/* Code that sets the parameters or builds the circuit:
dataBits := 8;
shift := 3;
*/
