// Digital circuit shift-fixed-right-inc.dig as structural Verilog
module shift_fixed_right_inc (
  input  [7:0] D_in,
  input  en,
  output [7:0] D
);

  Multiplexer #(.Bits(8), .generic("this.Bits=int(args.dataBits);")) multiplexer_1 (
    .sel(en), .in_0(D_in), .in_1({1'b0, D_in[7:1]}), .out(D));
endmodule

/* Code that sets the parameters or builds the circuit:
dataBits := 8;
shift := 3;
*/
