// Digital circuit shift-inc.dig as structural Verilog
module shift_inc (
  input  [15:0] D_in,
  input  [3:0] sh,
  output [15:0] D
);

  wire shift_fixed_left_inc_1_p3;

  // shift_fixed_left_inc #(.generic("dataBits:=16; shift:=8; if (isPresent(args)) { dataBits = args.dataBits; shift = 1<<(args.shiftBits-1); if (args.dir=\"right\") { setCircuit(\"shift-fixed-right-inc.dig\"); } else { if (args.dir=\"arith\") { setCircuit(\"shift-fixed-arith-right-inc.dig\"); } else { if (args.dir!=\"left\") { panic(\"only \\\"left\\\", \\\"right\\\" or \\\"arith\\\" is allowed as direction, not \\\"\"+args.dir+\"\\\"!\"); } } } }")) shift_fixed_left_inc_1: pin names not known; wires that end beside it: D_in, sh[3], shift_fixed_left_inc_1_p3
  // shift_inc #(.generic("dataBits:=16; shiftBits:=3; dir:=\"left\"; if (isPresent(args)) { dataBits = args.dataBits; shiftBits = args.shiftBits-1; dir=args.dir; if (args.shiftBits=2) { export shift := 1; if (args.dir=\"right\") { setCircuit(\"shift-fixed-right-inc.dig\"); } else { if (args.dir=\"arith\") { setCircuit(\"shift-fixed-arith-right-inc.dig\"); } else { if (args.dir!=\"left\") { panic(\"only \\\"left\\\", \\\"right\\\" or \\\"arith\\\"")) shift_inc_1: pin names not known; wires that end beside it: shift_fixed_left_inc_1_p3, sh[2:0], D
endmodule
