// Digital circuit bitExtend.dig as structural Verilog
module bitExtend (
  input  [3:0] A,
  output [7:0] Y
);

  BitExtender #(.inputBits(4), .outputBits(8)) bitextender_1 (.in(A), .out(Y));
endmodule

/* Test case:
A   Y
 0  0
 1  1
 2  2
 3  3
 4  4
 5  5
 6  6
 7  7
 8 ((-8)&0xff)
 9 ((-7)&0xff)
10 ((-6)&0xff)
11 ((-5)&0xff)
12 ((-4)&0xff)
13 ((-3)&0xff)
14 ((-2)&0xff)
15 ((-1)&0xff)
*/
