// Digital circuit bitExtend2.dig as structural Verilog
module bitExtend2 (
  input  A,
  output [7:0] Y
);

  BitExtender #(.inputBits(1), .outputBits(8)) bitextender_1 (.in(A), .out(Y));
endmodule

/* Test case:
A   Y
 0  0
 1  0xff
*/
