// Digital circuit bus.dig as structural Verilog
// Einfache Schaltung die eine Adressdecodierung 
// zeigt. Der Zähler erzeugt eine 5-Bit Zahl.
// Die unteren drei Bit werden als Adresse an alle 
// ROM-Bausteine ausgegeben. Die oberen zwei Bits
// werden verwendet um über den Adressdecoder 
// einen der vier ROM-Bausteine auszuwählen, welcher dann
// sein Datenwort an den Datenbus legt. Durch den 
// Adressdecoder verhalten sich die vier ROM-Bausteine wie
// ein einziger viermal so großer ROM-Baustein.
// Alle Ausgänge der ROMs liegen auf einem Datenbus. Dies ist
// möglich, da immer nur der Ausgang eines der vier ROMs aktiv 
// ist. Die jeweils anderen Ausgänge sind hochohmig.
module bus (
  input  Clock,
  output [7:0] Data
);

  wire decoder_1_out_0, decoder_1_out_1;
  wire [3:0] add_1_s, d_ff_1_q;

  Add #(.Bits(4)) add_1 (.a(d_ff_1_q), .b(4'b0001), .c_i(1'b0), .s(add_1_s));  // open: c_o
  D_FF #(.Bits(4)) d_ff_1 (.D(add_1_s), .C(Clock), .Q(d_ff_1_q));  // open: nQ
  Decoder decoder_1 (.sel(d_ff_1_q[3]), .out_0(decoder_1_out_0), .out_1(decoder_1_out_1));
  ROM #(.Bits(8), .Addr_Bits(3)) R1 (.A(d_ff_1_q[2:0]), .sel(decoder_1_out_0), .D(Data));
  ROM #(.Bits(8), .Addr_Bits(3)) R2 (.A(d_ff_1_q[2:0]), .sel(decoder_1_out_1), .D(Data));

  // Notes on the sheet:
  //   Clock: Hz: 2
  //   contents of R1 (hex, n*v repeats v):
  //   5,6,7,8,9,a,b,c
  //   contents of R2 (hex, n*v repeats v):
  //   d,e,f,10,11,12,13,14
endmodule

/* Test case:
Clock Data
  0    5
repeat(15) C (n+6)
repeat(16) C (n+5)
*/
