// Digital circuit comp.dig as structural Verilog
module comp (
  input  [3:0] a,
  input  [3:0] b,
  output eq,
  output gr,
  output le
);

  Comparator #(.Bits(4)) comparator_1 (.a(a), .b(b), .gt(gr), .eq(eq), .lt(le));
endmodule

/* Test case:
a b gr eq le
loop(a, 16)
  loop(b, 16)
(a) (b) (a>b)  (a=b)  (a<b)
  end loop
end loop
*/
