// Digital circuit compSig.dig as structural Verilog
module compSig (
  input  [3:0] a,
  input  [3:0] b,
  output eq,
  output gr,
  output le
);

  Comparator #(.Signed("true"), .Bits(4)) comparator_1 (.a(a), .b(b), .gt(gr), .eq(eq), .lt(le));
endmodule

/* Test case:
a b gr eq le
loop(a, 16)
  loop(b, 16)
(a) (b) (signExt(4,a)>signExt(4,b))  (a=b)  (signExt(4,a)<signExt(4,b))
  end loop
end loop
*/
