// Digital circuit counter.dig as structural Verilog
module counter (
  input  clk,
  input  en,
  input  clr,
  output [3:0] out,
  output ov
);

  Counter #(.Bits(4)) counter_1 (.en(en), .C(clk), .clr(clr), .out(out), .ovf(ov));
endmodule

/* Test case:
clk clr en out ov
 0   1   0  0  0
# not counting if clr is high
 C   1   1  0  0
 C   1   1  0  0

# not counting if en is low
 C   0   0  0  0
 C   0   0  0  0

# normal operation
repeat(14) C   0   1  (n+1)  0

 C   0   1  15  1

# combinatorial ov output
 0   0   0  15  0
 0   0   1  15  1

# overflow
 C   0   1  0  0
 C   0   0  0  0

#sync clr
 C   0   1  1  0
 0   0   0  1  0
 0   1   0  1  0
 C   1   0  0  0
*/
