// Digital circuit counterPre.dig as structural Verilog
module counterPre (
  input  clk,
  input  en,
  input  clr,
  input  dir,
  input  [3:0] in,
  input  ld,
  output [3:0] out,
  output ov
);

  CounterPreset #(.Bits(4)) counterpreset_1 (
    .en(en), .C(clk), .dir(dir), .in(in), .ld(ld), .clr(clr), .out(out), .ovf(ov));
endmodule

/* Test case simple:
clk clr dir in ld  en out ov
 0   1 0 0 0  0  0  0
# not counting if clr is high
 C   1 0 0 0  1  0  0
 C   1 0 0 0  1  0  0

# not counting if en is low
 C   0 0 0 0  0  0  0
 C   0 0 0 0  0  0  0

# normal operation
repeat(14) C   0 0 0 0  1  (n+1)  0

 C   0 0 0 0  1  15  1
 C   0 0 0 0  1  0  0
 C   0 0 0 0  0  0  0

#sync clr
 C   0 0 0 0  1  1  0
 0   0 0 0 0  0  1  0
 0   1 0 0 0  0  1  0
 C   1 0 0 0  0  0  0
*/

/* Test case pre:
#preset
clk clr dir en ld in out ov
 0   0   0  0  0  0   0  0
 c   1   0  1  1  5   0  0
 c   0   0  1  1  5   5  0

 c   0   0  1  1  15 15  1
 0   0   0  1  0  15 15  1
 0   0   0  0  0  15 15  0
 0   0   1  1  0  15 15  0
 0   0   0  1  0  15 15  1
*/

/* Test case dir:
clk clr dir ld in en out ov

# normal operation up
repeat(31) C   0   0 0 0 1  ((n+1)&0xf)  (((n+1)&0xf)=15)

# normal operation down
repeat(32) C   0   1 0 0 1  ((0xe-n)&0xf)  (((0xe-n)&0xf)=0)
*/
