// Digital circuit counterPre2.dig as structural Verilog
module counterPre2 (
  input  clk,
  input  en,
  input  clr,
  input  dir,
  input  [3:0] in,
  input  ld,
  output [3:0] out,
  output ov
);

  CounterPreset #(.maxValue(9), .Bits(4)) counterpreset_1 (
    .en(en), .C(clk), .dir(dir), .in(in), .ld(ld), .clr(clr), .out(out), .ovf(ov));
endmodule

/* Test case dir:
clk clr ld in dir en out ov

# normal operation up
repeat(30) C 0 0 0  0  1  ((n+1)%10)  (((n+1)%10)=9)

# normal operation down
repeat(32) C 0 0 0  1  1  ((39-n)%10)  ((39-n)%10=0)
*/
