// Digital circuit counterPre3.dig as structural Verilog
module counterPre3 (
  input  clk,
  input  en,
  input  dir,
  output [6:0] out
);

  wire counterpreset_1_ovf;

  CounterPreset #(.Bits(4)) counterpreset_1 (
    .en(en), .C(clk), .dir(dir), .in(4'b0000), .ld(1'b0), .clr(1'b0), .out(out[3:0]),
    .ovf(counterpreset_1_ovf));
  CounterPreset #(.Bits(3)) counterpreset_2 (
    .en(counterpreset_1_ovf), .C(clk), .dir(dir), .in(3'b000), .ld(1'b0), .clr(1'b0), .out(out[6:4]));  // open: ovf
endmodule

/* Test case:
clk en dir out

loop (n,128)
 C  1   0  (n+1)
end loop

loop (n,128)
 C  1   1  (127-n)
end loop

 C  1   1  127
*/
