// Digital circuit driver1.dig as structural Verilog
module driver1 (
  input  I,
  input  S,
  output O
);

  assign O = S ? I : 1'bz;  // Driver driver_1
endmodule

/* Test case:
S I O
0 0 Z
0 1 Z
1 0 0
1 1 1
*/
