// Digital circuit driver1inv.dig as structural Verilog
module driver1inv (
  input  I,
  input  S,
  output O
);

  Driver #(.invertDriverOutput("true")) driver_1 (.in(I), .en(S));  // open: out
endmodule

/* Test case:
S I O
0 0 Z
0 1 Z
1 0 1
1 1 0
*/
