// Digital circuit driver2.dig as structural Verilog
module driver2 (
  input  [3:0] I,
  input  S,
  output [3:0] O
);

  assign O = ~S ? I : 4'bz;  // DriverInvSel driverinvsel_1
endmodule

/* Test case:
S I O
1 0 Z
1 1 Z
0 0 0
0 1 1
0 4 4
*/
