// Digital circuit driver2inv.dig as structural Verilog
module driver2inv (
  input  [3:0] I,
  input  S,
  output [3:0] O
);

  DriverInvSel #(.invertDriverOutput("true"), .Bits(4)) driverinvsel_1 (.in(I), .en(S));  // open: out
endmodule

/* Test case:
S I O
1 0 Z
1 1 Z
0 0 0xf
0 1 0xe
0 4 0xb
*/
