// Digital circuit dualPortRam.dig as structural Verilog
module dualPortRam (
  input  str,
  input  C,
  input  ld,
  input  [7:0] _1A,
  input  [7:0] _1Di,
  input  [7:0] _2A,
  output [7:0] _1D,
  output [7:0] _2D
);

  RAMDualAccess #(.AddrBits(8), .Bits(8)) ramdualaccess_1 (
    .str(str), .C(C), .ld(ld), .A1(_1A), .Din1(_1Di), .A2(_2A), .D1(_1D), .D2(_2D));
endmodule

/* Test case:
str C ld 1A  1Di    1D     2A       2D

loop (a, 256)
 1  c  0 (a) (a+10) z      0        x
end loop


loop (a, 256)
 0  0  1 (a) 0      (a+10) (a+10)  (a+20)
end loop
*/
