// Digital circuit Ram32BitTest.dig as structural Verilog
module Ram32BitTest (
  input  [7:0] A,
  input  [31:0] D_in,
  input  we,
  input  [1:0] am,
  input  \signed ,
  input  C,
  output [31:0] D_out
);

  // RAM32Bit #(.generic("addrBits := 8;")) ram32bit_1: pin names not known; wires that end beside it: A, D_in, we, am, \signed , C, D_out
endmodule

/* Test case read:
A we D_in       C am signed D_out

#  32 bit read
0 1  0x0        c  0   0    x
4 1  0x44332211 c  0   0    x
8 1  0x0        c  0   0    x
4 0  0          0  0   0    0x44332211
3 0  0          0  0   0    0x33221100
2 0  0          0  0   0    0x22110000
1 0  0          0  0   0    0x11000000
5 0  0          0  0   0    0x00443322
6 0  0          0  0   0    0x00004433
7 0  0          0  0   0    0x00000044

#   16 bit read unsigned
4 1  0x83828180 c  0   0    x
4 0  0          0  1   0    0x8180
3 0  0          0  1   0    0x8000
2 0  0          0  1   0    0x0000
5 0  0          0  1   0    0x8281
6 0  0          0  1   0    0x8382
7 0  0          0  1   0    0x0083

# 0  16 bit read signed
4 0  0          0  1   1    0xffff8180
3 0  0          0  1   1    0xffff8000
2 0  0          0  1   1    0x00000000
5 0  0          0  1   1    0xffff8281
6 0  0          0  1   1    0xffff8382
7 0  0          0  1   1    0x00000083

# 8 bit read
4 0  0          0  2   0    0x80
3 0  0          0  2   0    0x00
2 0  0          0  2   0    0x00
5 0  0          0  2   0    0x81
6 0  0          0  2   0    0x82
7 0  0          0  2   0    0x83

# 8 bit read signed
4 0  0          0  2   1    0xffffff80
3 0  0          0  2   1    0x00
2 0  0          0  2   1    0x00
5 0  0          0  2   1    0xffffff81
6 0  0          0  2   1    0xffffff82
7 0  0          0  2   1    0xffffff83
*/

/* Test case write:
A we D_in       C am signed D_out

# 32 bit write
0 1  0          c  0   0    x
4 1  0          c  0   0    x
1 1  0x44332211 c  0   0    x
0 0  0          0  0   0    0x33221100
4 0  0          0  0   0    0x00000044

0 1  0          c  0   0    x
4 1  0          c  0   0    x
2 1  0x44332211 c  0   0    x
0 0  0          0  0   0    0x22110000
4 0  0          0  0   0    0x00004433

0 1  0          c  0   0    x
4 1  0          c  0   0    x
3 1  0x44332211 c  0   0    x
0 0  0          0  0   0    0x11000000
4 0  0          0  0   0    0x00443322

# 16 bit write
0 1  0          c  0   0    x
4 1  0          c  0   0    x
0 1  0x2211     c  1   0    x
0 0  0          0  0   0    0x00002211
1 1  0x3320     c  1   0    x
0 0  0          0  0   0    0x00332011
2 1  0x4430     c  1   0    x
0 0  0          0  0   0    0x44302011
3 1  0x5540     c  1   0    x
0 0  0          0  0   0    0x40302011
4 0  0          0  0   0    0x00000055

# 0 bit write
0 1  0          c  0   0    x
4 1  0          c  0   0    x
0 1  0x11       c  2   0    x
0 0  0          0  0   0    0x00000011
1 1  0x22       c  2   0    x
0 0  0          0  0   0    0x00002211
2 1  0x33       c  2   0    x
0 0  0          0  0   0    0x00332211
3 1  0x44       c  2   0    x
0 0  0          0  0   0    0x44332211
*/
