// Digital circuit memLeaf.dig as structural Verilog
module memLeaf (
  input  D_in,
  input  A,
  input  C,
  input  str,
  output D_Out
);

  wire and_1_out, and_2_out, register_1_q, register_2_q;

  and and_1 (and_1_out, str, ~A);  // And
  and and_2 (and_2_out, str, A);
  Register #(.generic("this.Bits=int(args.dataBits);")) register_1 (.D(D_in), .C(C), .en(and_1_out), .Q(register_1_q));
  Register #(.generic("this.Bits=int(args.dataBits);")) register_2 (.D(D_in), .C(C), .en(and_2_out), .Q(register_2_q));
  Multiplexer #(.generic("this.Bits=int(args.dataBits);")) multiplexer_1 (
    .sel(A), .in_0(register_1_q), .in_1(register_2_q), .out(D_Out));
endmodule

/* Code that sets the parameters or builds the circuit:
dataBits := 8;
*/
