// Digital circuit memLeaf2.dig as structural Verilog
module memLeaf2 (
  input  D_in,
  input  [1:0] A,
  input  C,
  input  str,
  output D_Out
);

  wire demultiplexer_1_out_0, demultiplexer_1_out_1, demultiplexer_1_out_2, demultiplexer_1_out_3,
       register_1_q, register_2_q, register_3_q, register_4_q;

  Demultiplexer #(.Selector_Bits(2)) demultiplexer_1 (
    .sel(A), .in(str), .out_0(demultiplexer_1_out_0), .out_1(demultiplexer_1_out_1),
    .out_2(demultiplexer_1_out_2), .out_3(demultiplexer_1_out_3));
  Register #(.generic("this.Bits=int(args.dataBits);")) register_1 (
    .D(D_in), .C(C), .en(demultiplexer_1_out_0), .Q(register_1_q));
  Register #(.generic("this.Bits=int(args.dataBits);")) register_2 (
    .D(D_in), .C(C), .en(demultiplexer_1_out_1), .Q(register_2_q));
  Register #(.generic("this.Bits=int(args.dataBits);")) register_3 (
    .D(D_in), .C(C), .en(demultiplexer_1_out_2), .Q(register_3_q));
  Register #(.generic("this.Bits=int(args.dataBits);")) register_4 (
    .D(D_in), .C(C), .en(demultiplexer_1_out_3), .Q(register_4_q));
  Multiplexer #(.Selector_Bits(2), .generic("this.Bits=int(args.dataBits);")) multiplexer_1 (
    .sel(A), .in_0(register_1_q), .in_1(register_2_q), .in_2(register_3_q), .in_3(register_4_q), .out(D_Out));
endmodule

/* Code that sets the parameters or builds the circuit:
dataBits := 8;
*/
