// Digital circuit genAndTest.dig as structural Verilog
module genAndTest (
  input  A,
  input  B,
  input  C,
  input  D,
  output Y,
  output X
);

  genAnd #(.generic("inputs := 4;")) genand_1 ();
  genAnd #(.generic("inputs := 3;")) genand_2 ();
endmodule

/* Test case:
A B C D Y X 

 0 0 0 0 0 0
 0 0 0 1 0 0
 0 0 1 0 0 0
 0 0 1 1 0 0
 0 1 0 0 0 0
 0 1 0 1 0 0
 0 1 1 0 0 0
 0 1 1 1 0 0
 1 0 0 0 0 0
 1 0 0 1 0 0
 1 0 1 0 0 0
 1 0 1 1 0 0
 1 1 0 0 0 0
 1 1 0 1 0 0
 1 1 1 0 0 1
 1 1 1 1 1 1
*/
