// Digital circuit genReg.dig as structural Verilog
module genReg (
  input  [1:0] D,
  input  en,
  input  C,
  output [1:0] Q
);
endmodule

/* Code that sets the parameters or builds the circuit:
bits:=3;
*/

/* Code that sets the parameters or builds the circuit:
for (i:=0;i<args.bits;i++) {
    y:=i*4;
    addComponent("Register",0,y);
    addWire(0,y,-3,y);
    addWire(0,y+1,-1,y+1);
    addWire(0,y+2,-2,y+2);
    addWire(3,y+1,5,y+1);
}
addWire(-1,-4,-1,args.bits*4-3);
addWire(-2,-2,-2,args.bits*4-2);
*/
