// Digital circuit lut.dig as structural Verilog
module lut (
  input  A_0,
  input  A_1,
  input  A_2,
  output Y
);

  LookUpTable L1 (.in0(A_0), .in1(A_1), .in2(A_2), .out(Y));

  // Notes on the sheet:
  //   contents of L1 (hex, n*v repeats v):
  //   0,0,1,0,1,0,0,1
endmodule

/* Test case:
A_0 A_1 A_2  Y
 0   0   0   0
 0   0   1   1
 0   1   0   1
 0   1   1   0
 1   0   0   0
 1   0   1   0
 1   1   0   0
 1   1   1   1
*/
