// Digital circuit lut2.dig as structural Verilog
module lut2 (
  input  A_0,
  input  A_1,
  input  A_2,
  output [2:0] Y
);

  LookUpTable #(.Bits(3)) L1 (.in0(A_0), .in1(A_1), .in2(A_2), .out(Y));

  // Notes on the sheet:
  //   contents of L1 (hex, n*v repeats v):
  //   0,0,1,0,2,7,0,3
endmodule

/* Test case:
A_0 A_1 A_2  Y
 0   0   0   0
 0   0   1   2
 0   1   0   1
 0   1   1   0
 1   0   0   0
 1   0   1   7
 1   1   0   0
 1   1   1   3
*/
