// Digital circuit lut3.dig as structural Verilog
module lut3 (
  input  A_0,
  input  A_1,
  input  A_2,
  output Y
);

  wire L1_out, L2_out;

  LookUpTable L1 (.in0(A_0), .in1(A_1), .in2(A_2), .out(L1_out));
  LookUpTable L2 (.in0(A_0), .in1(A_1), .in2(A_2), .out(L2_out));
  xor xor_1 (Y, L1_out, L2_out);

  // Notes on the sheet:
  //   contents of L1 (hex, n*v repeats v):
  //   0,0,1,0,1,1,0,1
  //   contents of L2 (hex, n*v repeats v):
  //   0,0,0,1,1,1,0,1
endmodule

/* Test case:
A_0 A_1 A_2  Y
 0   0   0   0
 0   0   1   2
 0   1   0   1
 0   1   1   0
 1   0   0   0
 1   0   1   0
 1   1   0   1
 1   1   1   0
*/
