// Digital circuit multiply.dig as structural Verilog
module multiply (
  input  [3:0] A,
  input  [3:0] B,
  output [7:0] M
);

  Mul #(.Bits(4)) mul_1 (.a(A), .b(B), .mul(M));
endmodule

/* Test case:
               A     B     M
repeat(256) (n&15) (n>>4)  ((n&15)*(n>>4))
*/
