// Digital circuit multiplySigned.dig as structural Verilog
module multiplySigned (
  input  [3:0] A,
  input  [3:0] B,
  output [7:0] M
);

  Mul #(.Signed("true"), .Bits(4)) mul_1 (.a(A), .b(B), .mul(M));
endmodule

/* Test case:
      A   B   M
loop(a,16)
  loop(b,16)
 
     (a-8) (b-8) ((a-8)*(b-8))

  end loop
end loop
*/
