// Digital circuit naming-main.dig as structural Verilog
module naming_main (
  input  A,
  input  B,
  output Y
);

  // naming_inc naming_inc_1: pin names not known; wires that end beside it: A, B, Y
endmodule

/* Test case:
A B Y
0 0 0
0 1 1
1 0 1
1 1 0
*/
