// Digital circuit neg.dig as structural Verilog
module neg (
  input  [3:0] a,
  output [3:0] y
);

  Neg #(.Bits(4)) neg_1 (.in(a), .out(y));
endmodule

/* Test case:
a y

0 0
1 15
2 14
14 2
15 1
8  8
*/
