// Digital circuit not.dig as structural Verilog
module \not  (
  input  A,
  input  B,
  input  C,
  input  D,
  input  E,
  output Y,
  output X,
  output Z,
  output U,
  output V
);

  wire not_2_out, not_3_out, not_4_out, not_5_out, not_7_out, not_8_out, not_9_out, not_11_out, not_13_out,
       not_14_out;

  not not_1 (V, A);
  not not_2 (not_2_out, B);
  not not_3 (not_3_out, C);
  not not_4 (not_4_out, D);
  not not_5 (not_5_out, E);
  not not_6 (U, not_2_out);
  not not_7 (not_7_out, not_3_out);
  not not_8 (not_8_out, not_4_out);
  not not_9 (not_9_out, not_5_out);
  not not_10 (Z, not_7_out);
  not not_11 (not_11_out, not_8_out);
  not not_12 (X, not_11_out);
  not not_13 (not_13_out, not_9_out);
  not not_14 (not_14_out, not_13_out);
  not not_15 (Y, not_14_out);
endmodule

/* Test case:
A B C D E Y X Z U V 

 0 0 0 0 0 1 0 1 0 1
 1 1 1 1 1 0 1 0 1 0
*/
