// Digital circuit priorityEncoder.dig as structural Verilog
module priorityEncoder (
  input  A0,
  input  A1,
  input  A2,
  input  A3,
  input  A4,
  input  A5,
  input  A6,
  input  A7,
  output any,
  output [2:0] num
);

  PriorityEncoder #(.Selector_Bits(3)) priorityencoder_1 (
    .in0(A0), .in1(A1), .in2(A2), .in3(A3), .in4(A4), .in5(A5), .in6(A6), .in7(A7), .num(num), .any(any));
endmodule

/* Test case:
A7 A6 A5 A4 A3 A2 A1 A0 num any
0  0  0  0  0  0  0  0   0   0
0  0  0  0  0  0  0  1   0   1
0  0  0  0  0  0  1  x   1   1
0  0  0  0  0  1  x  x   2   1
0  0  0  0  1  x  x  x   3   1
0  0  0  1  x  x  x  x   4   1
0  0  1  x  x  x  x  x   5   1
0  1  x  x  x  x  x  x   6   1
1  x  x  x  x  x  x  x   7   1
*/
