// Digital circuit pullUp.dig as structural Verilog
module pullUp (
  input  en,
  input  val,
  output YU,
  output YD,
  output Y
);

  assign YU = en ? val : 1'bz;  // Driver driver_1
  assign Y = en ? val : 1'bz;  // Driver driver_2
  assign YD = en ? val : 1'bz;  // Driver driver_3
  PullUp pullup_1 (.out(YU));
  PullDown pulldown_1 (.out(YD));
endmodule

/* Test case:
en val YU Y YD
0   0  1  Z 0
0   1  1  Z 0
1   0  0  0 0
1   1  1  1 1
*/
