// Digital circuit RAMAsync.dig as structural Verilog
module RAMAsync (
  input  [7:0] A,
  input  we,
  input  [7:0] D,
  output [7:0] Q
);

  RAMAsync #(.AddrBits(8), .Bits(8)) ramasync_1 (.A(A), .D(D), .we(we), .Q(Q));
endmodule

/* Test case:
we A D Q
loop(n,256)
1  (n) (n) (n)
end loop
loop(n,256)
0  (n) 0 (n)
end loop
loop(n,256)
0  (n) 0 (n)
end loop
*/
