// Digital circuit blockRAM.dig as structural Verilog
module blockRAM (
  input  [7:0] A,
  input  [31:0] Din,
  input  C,
  input  [3:0] mask,
  output [31:0] D
);

  BlockRAMDualPort #(.AddrBits(8), .Bits(8)) blockramdualport_1 (
    .A(A), .Din(Din[7:0]), .str(mask[0]), .C(C), .D(D[7:0]));
  BlockRAMDualPort #(.AddrBits(8), .Bits(8)) blockramdualport_2 (
    .A(A), .Din(Din[15:8]), .str(mask[1]), .C(C), .D(D[15:8]));
  BlockRAMDualPort #(.AddrBits(8), .Bits(8)) blockramdualport_3 (
    .A(A), .Din(Din[23:16]), .str(mask[2]), .C(C), .D(D[23:16]));
  BlockRAMDualPort #(.AddrBits(8), .Bits(8)) blockramdualport_4 (
    .A(A), .Din(Din[31:24]), .str(mask[3]), .C(C), .D(D[31:24]));
endmodule

/* Test case:
C A Din         mask   D

# no write at all, mask is zero
C 0 0           0b1111 x
C 0 0xffffffff  0b0000 x
C 0 0           0b0000 0

# write bytes

C 0 0xffffffff  0b0001 x
C 0 0           0b0000 0xff

C 0 0xffffff00  0b0010 x
C 0 0           0b0000 0xffff

C 0 0xffff0000  0b0100 x
C 0 0           0b0000 0xffffff

C 0 0xff000000  0b1000 x
C 0 0           0b0000 0xffffffff

# write 16 bit words

C 1 0           0b1111 x
C 1 0xffff      0b0011 x
C 1 0           0b0000  0xffff

C 1 0xffff0000  0b1100 x
C 1 0           0b0000 0xffffffff

C 1 0xaaaa00    0b0110 x
C 1 0           0b0000 0xffaaaaff

# write 32 bit words

C 2 0           0b1111 x
C 2 0xffffffff  0b1111 x
C 2 0           0b0000  0xffffffff

# sync read
C 1 0           0b0000 0xffaaaaff
0 0 0           0b0000 0xffaaaaff
0 2 0           0b0000 0xffaaaaff
C 0 0           0b0000 0xffffffff
C 2 0           0b0000 0xffffffff
*/
