// Digital circuit blockRAM8.dig as structural Verilog
module blockRAM8 (
  input  [7:0] A,
  input  [7:0] Din,
  input  C,
  input  mask,
  output [7:0] D
);

  BlockRAMDualPort #(.AddrBits(8), .Bits(8)) blockramdualport_1 (.A(A), .Din(Din), .str(mask), .C(C), .D(D));
endmodule

/* Test case:
C A Din   mask   D

# no write at all, mask is zero
C 0 0     1      x
C 0 0xff  0      x
C 0 0     0      0

# write byte

C 0 0xff  1      x
C 1 0xf0  1      x

C 2 0     1      x
C 2 0     0      0
0 0 0     0      0
0 1 0     0      0
C 0 0     0      0xff
C 1 0     0      0xf0
*/
