// Digital circuit maskedRAM.dig as structural Verilog
module maskedRAM (
  input  [7:0] A,
  input  [31:0] Din,
  input  C,
  input  [3:0] mask,
  output [31:0] D
);

  // BlockRAMDualPortMasked #(.AddrBits(8), .Bits(32)) blockramdualportmasked_1: pin names not known; wires that end beside it: A, Din, mask, C, D
endmodule

/* Test case:
C A Din         mask   D

# no write at all, mask is zero
C 0 0           0b1111 x
C 0 0xffffffff  0b0000 x
C 0 0           0b0000 0

# write bytes

C 0 0xffffffff  0b0001 x
C 0 0           0b0000 0xff

C 0 0xffffff00  0b0010 x
C 0 0           0b0000 0xffff

C 0 0xffff0000  0b0100 x
C 0 0           0b0000 0xffffff

C 0 0xff000000  0b1000 x
C 0 0           0b0000 0xffffffff

# write 16 bit words

C 1 0           0b1111 x
C 1 0xffff      0b0011 x
C 1 0           0b0000  0xffff

C 1 0xffff0000  0b1100 x
C 1 0           0b0000 0xffffffff

C 1 0xaaaa00    0b0110 x
C 1 0           0b0000 0xffaaaaff

# write 32 bit words

C 2 0           0b1111 x
C 2 0xffffffff  0b1111 x
C 2 0           0b0000  0xffffffff

# sync read
C 1 0           0b0000 0xffaaaaff
0 0 0           0b0000 0xffaaaaff
0 2 0           0b0000 0xffaaaaff
C 0 0           0b0000 0xffffffff
C 2 0           0b0000 0xffffffff
*/
