// Digital circuit maskedRAM64.dig as structural Verilog
module maskedRAM64 (
  input  [7:0] A,
  input  [63:0] Din,
  input  C,
  input  [7:0] mask,
  output [63:0] D
);

  // BlockRAMDualPortMasked #(.AddrBits(8), .Bits(64)) blockramdualportmasked_1: pin names not known; wires that end beside it: A, Din, mask, C, D
endmodule

/* Test case:
C A Din                 mask   D

# no write at all, mask is zero
C 0 0                   0b11111111 x
C 0 0xffffffffffffffff  0b00000000 x
C 0 0                   0b00000000 0

# write bytes

C 0 0xffffffffffffffff  0b00000001 x
C 0 0                   0b00000000 0xff

C 0 0xffffffffffffff00  0b00000010 x
C 0 0                   0b00000000 0xffff

C 0 0xffffffffffff0000  0b00000100 x
C 0 0                   0b00000000 0xffffff

C 0 0xffffffffff000000  0b00001000 x
C 0 0                   0b00000000 0xffffffff

C 0 0xffffffff00000000  0b00010000 x
C 0 0                   0b00000000 0xffffffffff

C 0 0xffffff0000000000  0b00100000 x
C 0 0                   0b00000000 0xffffffffffff

C 0 0xffff000000000000  0b01000000 x
C 0 0                   0b00000000 0xffffffffffffff

C 0 0xff00000000000000  0b10000000 x
C 0 0                   0b00000000 0xffffffffffffffff

# write 32 bit words

C 1 0                   0b11111111 x

C 1 0xffffffff          0b00001111 x
C 1 0                   0b00000000 0xffffffff

C 1 0xaaaaaaaa00000000  0b11110000 x
C 1 0                   0b00000000 0xaaaaaaaaffffffff
*/
