// Digital circuit maskedRAM8.dig as structural Verilog
module maskedRAM8 (
  input  [7:0] A,
  input  [7:0] Din,
  input  C,
  input  mask,
  output [7:0] D
);

  // BlockRAMDualPortMasked #(.AddrBits(8), .Bits(8)) blockramdualportmasked_1: pin names not known; wires that end beside it: A, Din, mask, C, D
endmodule

/* Test case:
C A Din   mask   D

# no write at all, mask is zero
C 0 0     1      x
C 0 0xff  0      x
C 0 0     0      0

# write byte

C 0 0xff  1      x
C 1 0xf0  1      x

C 2 0     1      x
C 2 0     0      0
0 0 0     0      0
0 1 0     0      0
C 0 0     0      0xff
C 1 0     0      0xf0
*/
