// Digital circuit rom2.dig as structural Verilog
module rom2 (
  input  [3:0] A,
  input  en,
  output [7:0] O
);

  ROM #(.AddrBits(4), .Bits(8), .Addr_Bits(4)) ROM (.A(A), .sel(en), .D(O));

  // Notes on the sheet:
  //   contents of ROM (hex, n*v repeats v):
  //   3,1,0,5,7,0,0,0,0,7,0,0,0,ff,0,1
endmodule

/* Test case:
en A O
0  0 Z
0  1 Z
0  2 Z

1  0 3
1  1 1
1  2 0
1  3 5
1  4 7
1  5 0
1  6 0
1  7 0
1  8 0
1  9 7
1 10 0
1 11 0
1 12 0
1 13 255
1 14 0
1 15 1
*/
