// Digital circuit rom3.dig as structural Verilog
module rom3 (
  input  [3:0] A,
  output [7:0] O
);

  ROM #(.AddrBits(4), .Bits(4), .Addr_Bits(4)) ROM1 (.A(A), .sel(1'b1), .D(O[3:0]));
  ROM #(.AddrBits(4), .Bits(4), .Addr_Bits(4)) ROM2 (.A(A), .sel(1'b1), .D(O[7:4]));

  // Notes on the sheet:
  //   contents of ROM1 (hex, n*v repeats v):
  //   3,1,0,5,7,0,0,0,0,7,0,0,0,f,0,1
  //   contents of ROM2 (hex, n*v repeats v):
  //   3,1,0,5,0,0,0,0,0,7,0,0,0,f,0,1
endmodule

/* Test case:
 A O
 0 0x33
 1 0x11
 2 0
 3 0x55
 4 7
 5 0
 6 0
 7 0
 8 0
 9 0x77
10 0
11 0
12 0
13 255
14 0
15 0x11
*/
