// Digital circuit lut.dig as structural Verilog
module lut (
  input  [2:0] A,
  output Y
);

  ROM #(.AddrBits(3), .generic("this.Data=loadHex(args.hexName,1); this.Label=args.hexName;")) rom_1 (
    .A(A), .sel(1'b1), .D(Y));

  // Notes on the sheet:
  //   contents of rom_1 (hex, n*v repeats v):
  //   0,1,1,0,1,0,0,1
endmodule

/* Code that sets the parameters or builds the circuit:
hexName:="lut1.hex";
*/
