// Digital circuit lutTest.dig as structural Verilog
module lutTest (
  input  [2:0] A,
  output Y,
  output X
);

  lut #(.generic("hexName := \"lut1.hex\";")) lut_1 (.A(A), .Y(Y));
  lut #(.generic("hexName := \"lut2.hex\";")) lut_2 (.A(A), .Y(X));
endmodule

/* Test case:
A Y X 

 0b000 0 0
 0b001 1 1
 0b010 1 1
 0b011 0 0
 0b100 1 0
 0b101 1 0
 0b110 1 0
 0b111 1 0
*/
