// Digital circuit subtr.dig as structural Verilog
module subtr (
  input  [3:0] A,
  input  [3:0] B,
  input  C,
  output [3:0] S,
  output Co
);

  Sub #(.Bits(4)) sub_1 (.a(A), .b(B), .c_i(C), .s(S), .c_o(Co));
endmodule

/* Test case:
               A     B     C  S                     Co
repeat(256) (n&15) (n>>4)  0  (((n&15)-(n>>4))&15) ((((n&15)-(n>>4))>>4)&1)
repeat(256) (n&15) (n>>4)  1  (((n&15)-(n>>4)-1)&15) ((((n&15)-(n>>4)-1)>>4)&1)
*/
