// Digital circuit virtualTestSignal.dig as structural Verilog
module virtualTestSignal (
  input  A,
  output [2:0] Y
);

  wire [2:0] notconnected_1_out;

  // NotConnected on notconnected_1_out[0]
  // NotConnected on notconnected_1_out[2]
  assign Y = ~{notconnected_1_out[2], A, notconnected_1_out[0]};  // Not not_1, 3 bits wide
  // Probe P on Y[1]
endmodule

/* Test case:
A P S1 S2 Y

declare S1=(Y>>1)&1;
declare S2=(~(Y>>1))&1;

loop (n,20)
1 0 0 1 x
0 1 1 0 x
end loop
*/
