// Digital circuit w1.dig as structural Verilog
// contains only a pull up
module w1 (
  output w1
);

  PullUp pullup_1 (.out(w1));

  // Notes on the sheet:
  //   w1: connected directly to a pull up
endmodule
