// Digital circuit testProgLoaderSplitErr1.dig as structural Verilog
module testProgLoaderSplitErr1 (
  input  [7:0] in_1,
  input  [7:0] in_2,
  input  in_3,
  input  in_4,
  input  in_5,
  output [7:0] out_6,
  output [7:0] out_7
);

  RAMDualPort #(.AddrBits(8), .isProgramMemory("true"), .Bits(8)) R0 (
    .A(in_1), .Din(in_2), .str(in_3), .C(in_4), .ld(in_5), .D(out_6));
  RAMDualPort #(.AddrBits(8), .isProgramMemory("true"), .Bits(8)) R0_2 (
    .A(in_1), .Din(in_2), .str(in_3), .C(in_4), .ld(in_5), .D(out_7));
endmodule
