// Digital circuit trafficLight.dig as structural Verilog
module trafficLight (
  input  in_1,
  output out_2,
  output out_3,
  output out_4
);

  wire ms_jk_1_p4, ms_jk_2_p5;

  // MS_JK ms_jk_1: pin names not known; wires that end beside it: out_3, in_1, out_3, ms_jk_1_p4, out_2
  // MS_JK ms_jk_2: pin names not known; wires that end beside it: 1'b1, in_1, 1'b1, out_3, ms_jk_2_p5
  and and_1 (out_4, ms_jk_1_p4, ms_jk_2_p5);
endmodule
