// Digital circuit GAL22v10_Pin13.dig as structural Verilog
module GAL22v10_Pin13 (
  input  B,
  input  A,
  input  C,
  output Y
);

  and and_1 (Y, A, B, C);

  // Notes on the sheet:
  //   B: Pin 11
  //   A: Pin 10
  //   C: Pin 13
  //   Y: Pin 23
endmodule
