// Digital circuit GALTest.dig as structural Verilog
module GALTest (
  input  A_1,
  input  A_2,
  input  A_3,
  input  A_4,
  input  A_5,
  input  A_6,
  input  A_7,
  input  A_8,
  output Y_1,
  output Y_2,
  output Y_3,
  output Y_4,
  output Y_5,
  output Y_6,
  output Y_7
);

  and and_1 (Y_1, A_1, A_2);
  and and_2 (Y_2, A_2, A_3);
  and and_3 (Y_3, A_3, A_4);
  and and_4 (Y_4, A_4, A_5);
  and and_5 (Y_5, A_5, A_6);
  and and_6 (Y_6, A_6, A_7);
  and and_7 (Y_7, A_7, A_8);
endmodule
