// Digital circuit ff.dig as structural Verilog
module ff (
  input  CLK,
  output Q
);

  wire d_ff_1_nq;

  D_FF d_ff_1 (.D(d_ff_1_nq), .C(CLK), .Q(Q), .nQ(d_ff_1_nq));

  // Notes on the sheet:
  //   CLK: Hz: 200
endmodule
